// Logisim project PRIZHOK.circ as structural Verilog: 2 circuits, main circuit main
module main (
);

  wire button_1_out;
  wire [31:0] prigalka_1_bus_0;

  Button button_1 (.out(button_1_out));
  prigalka prigalka_1 (.\Кнопка (button_1_out), .bus_0(prigalka_1_bus_0));
  // DotMatrix #(.inputtype("select"), .matrixcols(32), .matrixrows(32)) dotmatrix_1: pin names not known; wires that end beside it: 32'h40, prigalka_1_bus_0
endmodule

module prigalka (
  input  \Кнопка ,
  output [31:0] bus_0
);

  wire _551, _69699, and_1_out, clock_1_out, counter_3_carry, counter_4_carry, d_ff_1_q, d_ff_1_qn, d_ff_2_q,
       d_ff_2_qn, d_ff_3_q, d_ff_3_qn, d_ff_4_q, d_ff_4_qn, d_ff_5_q, d_ff_5_qn, d_ff_6_q, d_ff_6_qn,
       d_ff_7_q, d_ff_7_qn, d_ff_8_q, d_ff_8_qn, d_ff_9_q, d_ff_9_qn, d_ff_10_q, d_ff_10_qn, d_ff_11_qn,
       multiplexer_1_out, not_1_out, or_1_out, transistor_1_out;
  wire [2:0] counter_5_q;
  wire [4:0] counter_6_q;

  Clock clock_1 (.out(clock_1_out));
  D_Flip_Flop d_ff_1 (.clk(clock_1_out), .D(d_ff_1_qn), .Q(d_ff_1_q), .Qn(d_ff_1_qn));  // open: preset, en, reset
  D_Flip_Flop d_ff_2 (.clk(d_ff_1_q), .D(d_ff_2_qn), .Q(d_ff_2_q), .Qn(d_ff_2_qn));  // open: preset, en, reset
  D_Flip_Flop d_ff_3 (.clk(d_ff_2_q), .D(d_ff_3_qn), .Q(d_ff_3_q), .Qn(d_ff_3_qn));  // open: preset, en, reset
  D_Flip_Flop d_ff_4 (.clk(d_ff_3_q), .D(d_ff_4_qn), .Q(d_ff_4_q), .Qn(d_ff_4_qn));  // open: preset, en, reset
  D_Flip_Flop d_ff_5 (.clk(d_ff_4_q), .D(d_ff_5_qn), .Q(d_ff_5_q), .Qn(d_ff_5_qn));  // open: preset, en, reset
  Counter #(.width(2), .max('h3), .ongoal("stay")) counter_1 (
    .clk(d_ff_9_q), .clr(and_1_out));  // open: load, D, count, Q, carry
  D_Flip_Flop d_ff_6 (.clk(d_ff_5_q), .D(d_ff_6_qn), .Q(d_ff_6_q), .Qn(d_ff_6_qn));  // open: preset, en, reset
  Counter #(.width(1), .max('h0), .ongoal("stay")) counter_2 (.clk(d_ff_9_q));  // open: load, D, count, Q, carry, clr
  Counter #(.width(2), .max('h2), .ongoal("stay")) counter_3 (
    .carry(counter_3_carry), .clk(d_ff_9_q), .clr(and_1_out));  // open: load, D, count, Q
  Counter #(.width(1), .max('h1), .ongoal("stay")) counter_4 (
    .carry(counter_4_carry), .clk(d_ff_9_q), .clr(and_1_out));  // open: load, D, count, Q
  D_Flip_Flop d_ff_7 (.clk(d_ff_6_q), .D(d_ff_7_qn), .Q(d_ff_7_q), .Qn(d_ff_7_qn));  // open: preset, en, reset
  Decoder #(.select(5)) decoder_1 (
    .out0(bus_0[31]), .out1(bus_0[30]), .out2(bus_0[29]), .out3(bus_0[28]), .out4(bus_0[27]),
    .out5(bus_0[26]), .out6(bus_0[25]), .out7(bus_0[24]), .out8(bus_0[23]), .out9(bus_0[22]),
    .out10(bus_0[21]), .out11(bus_0[20]), .out12(bus_0[19]), .out13(bus_0[18]), .out14(bus_0[17]),
    .out15(bus_0[16]), .out16(bus_0[15]), .out17(bus_0[14]), .out18(bus_0[13]), .out19(bus_0[12]),
    .out20(bus_0[11]), .out21(bus_0[10]), .out22(bus_0[9]), .out23(bus_0[8]), .out24(bus_0[7]),
    .out25(bus_0[6]), .out26(bus_0[5]), .out27(bus_0[4]), .out28(bus_0[3]), .out29(bus_0[2]),
    .out30(bus_0[1]), .out31(bus_0[0]), .sel(counter_6_q));  // open: en
  D_Flip_Flop d_ff_8 (.clk(d_ff_7_q), .D(d_ff_8_qn), .Q(d_ff_8_q), .Qn(d_ff_8_qn));  // open: preset, en, reset
  D_Flip_Flop d_ff_9 (.clk(d_ff_8_q), .D(d_ff_9_qn), .Q(d_ff_9_q), .Qn(d_ff_9_qn));  // open: preset, en, reset
  D_Flip_Flop d_ff_10 (.clk(d_ff_9_q), .D(d_ff_10_qn), .Q(d_ff_10_q), .Qn(d_ff_10_qn));  // open: preset, en, reset
  Comparator #(.width(5), .mode("unsigned")) comparator_1 (.a(counter_6_q), .b(5'b11110), .gt(_69699));  // open: eq, lt
  nand nand_1 (_551, counter_3_carry, counter_4_carry);
  D_Flip_Flop d_ff_11 (.clk(d_ff_10_q), .D(d_ff_11_qn), .Qn(d_ff_11_qn));  // open: Q, preset, en, reset
  Multiplexer #(.select(3)) multiplexer_1 (
    .in0(d_ff_10_q), .in1(d_ff_9_q), .in2(d_ff_8_q), .in3(d_ff_8_q), .in4(d_ff_7_q), .in5(d_ff_6_q),
    .in6(d_ff_6_q), .in7(d_ff_5_q), .out(multiplexer_1_out), .sel(counter_5_q));  // open: en
  Counter #(.width(3), .max('h7)) counter_5 (
    .Q(counter_5_q), .clk(d_ff_9_q), .clr(or_1_out));  // open: load, D, count, carry
  or or_1 (or_1_out, _69699, _551);
  not not_1 (not_1_out, \Кнопка );
  and and_1 (and_1_out, not_1_out, \Кнопка );
  Transistor transistor_1 (.in(multiplexer_1_out), .out(transistor_1_out), .gate(_551));
  Transistor #(.\type ("n")) transistor_2 (.in(d_ff_7_q), .out(transistor_1_out), .gate(_551));
  Counter #(.width(5), .max('h1f)) counter_6 (
    .load(_551), .Q(counter_6_q), .clk(transistor_1_out));  // open: D, count, carry, clr
endmodule
