// Logisim project big_pipes_2.1.circ as structural Verilog: 15 circuits, main circuit main
module main (
  input  in_1
);

  wire button_1_out, clock_1_out, controlled_buffer_1_out, \вкл ;
  wire [1:0] height_1_signal_down_2, height_2_signal_down_2, height_3_signal_down_2, height_4_signal_down_2,
       height_5_signal_down_2, height_6_signal_down_2, height_7_signal_down_2, height_8_signal_down_2,
       height_9_signal_down_2, height_10_signal_down_2, height_11_signal_down_2, height_12_signal_down_2;
  wire [9:0] height_2_signal, height_2_signal_up_2, height_3_signal, height_3_signal_up_2, height_4_signal,
       height_4_signal_up_2, height_5_signal, height_5_signal_up_2, height_6_signal, height_6_signal_up_2,
       height_7_signal, height_7_signal_up_2, height_8_signal, height_8_signal_up_2, height_9_signal,
       height_9_signal_up_2, height_10_signal, height_10_signal_up_2, height_11_signal,
       height_11_signal_up_2, height_12_signal, height_12_signal_up_2, height_13_signal,
       height_13_signal_up_2, pipes_13_signal_2, pipes_14_signal_2, pipes_15_signal_2, pipes_16_signal_2,
       pipes_17_signal_2, pipes_18_signal_2, pipes_19_signal_2, pipes_20_signal_2, pipes_21_signal_2,
       pipes_22_signal_2, pipes_23_signal_2, pipes_24_signal_2, pipes_25_signal_2, pipes_26_signal_2,
       pipes_27_signal_2, pipes_28_signal_2, pipes_29_signal_2, pipes_30_signal_2, pipes_31_signal_2,
       pipes_32_signal_2, pipes_33_signal_2, pipes_34_signal_2, pipes_35_signal_2, pipes_36_signal_2,
       pipes_37_signal_2, pipes_38_signal_2, pipes_39_signal_2, pipes_40_signal_2, pipes_41_signal_2,
       pipes_42_signal_2, pipes_43_signal_2, pipes_44_signal_2, pipes_45_signal_2, pipes_46_signal_2,
       pipes_47_signal_2, pipes_48_signal_2, pipes_49_signal_2, pipes_50_signal_2, pipes_51_signal_2,
       pipes_52_signal_2, pipes_53_signal_2, pipes_54_signal_2, pipes_55_signal_2, pipes_56_signal_2,
       pipes_57_signal_2, pipes_58_signal_2, pipes_59_signal_2, pipes_60_signal_2, pipes_61_signal_2,
       pipes_62_signal_2, pipes_63_signal_2, pipes_64_signal_2, pipes_65_signal_2, pipes_66_signal_2,
       pipes_67_signal_2, pipes_68_signal_2, pipes_69_signal_2, pipes_70_signal_2, pipes_71_signal_2,
       pipes_72_signal_2, pipes_73_signal_2, pipes_74_signal_2, pipes_75_signal_2, pipes_76_signal_2,
       pipes_77_signal_2, pipes_78_signal_2, pipes_79_signal_2, pipes_80_signal_2, pipes_81_signal_2,
       pipes_82_signal_2, pipes_83_signal_2, pipes_84_signal_2, pipes___bird_1_signal_2,
       pipes___bird_2_signal_2, pipes___bird_3_signal_2, pipes___bird_4_signal_2, pipes___bird_5_signal_2,
       pipes___bird_6_signal_2, pipes___bird_7_signal_2, pipes___bird_8_signal_2, pipes___bird_9_signal_2,
       pipes___bird_10_signal_2, pipes___bird_11_signal_2, pipes___bird_12_signal_2, rand_1_signal, s1, s2,
       s3, s4, s5, s6, s7, s8, s9, s10, s11, s12, s_up;
  wire [17:0] rand_1_rand_pipe;
  wire [31:0] height_2_bird_1, height_2_bird_2, height_2_pipe, height_3_bird_1, height_3_bird_2,
       height_3_pipe, height_4_bird_1, height_4_bird_2, height_4_pipe, height_5_bird_1, height_5_bird_2,
       height_5_pipe, height_6_bird_1, height_6_bird_2, height_6_pipe, height_7_bird_1, height_7_bird_2,
       height_7_pipe, height_8_bird_1, height_8_bird_2, height_8_pipe, height_9_bird_1, height_9_bird_2,
       height_9_pipe, height_10_bird_1, height_10_bird_2, height_10_pipe, height_11_bird_1, height_11_bird_2,
       height_11_pipe, height_12_bird_1, height_12_bird_2, height_12_pipe, height_13_bird_1,
       height_13_bird_2, height_13_pipe, pipes_1_out_5, pipes_1_out_6, pipes_1_out_7, pipes_1_out_8,
       pipes_1_out_9, pipes_1_out_10, pipes_1_out_11, pipes_1_out_12, pipes_1_out_13, pipes_1_out_14,
       pipes_1_out_15, pipes_1_out_16, pipes_1_out_17, pipes_1_out_18, pipes_1_out_19, pipes_1_out_20,
       pipes_1_out_21, pipes_1_out_22, pipes_1_out_23, pipes_1_out_24, pipes_1_out_25, pipes_1_out_26,
       pipes_1_out_27, pipes_1_out_28, pipes_1_out_29, pipes_1_out_30, pipes_1_out_31, pipes_1_out_32,
       pipes_1_out_33, pipes_1_out_34, pipes_1_out_35, pipes_1_out_36, pipes_2_out_5, pipes_2_out_6,
       pipes_2_out_7, pipes_2_out_8, pipes_2_out_9, pipes_2_out_10, pipes_2_out_11, pipes_2_out_12,
       pipes_2_out_13, pipes_2_out_14, pipes_2_out_15, pipes_2_out_16, pipes_2_out_17, pipes_2_out_18,
       pipes_2_out_19, pipes_2_out_20, pipes_2_out_21, pipes_2_out_22, pipes_2_out_23, pipes_2_out_24,
       pipes_2_out_25, pipes_2_out_26, pipes_2_out_27, pipes_2_out_28, pipes_2_out_29, pipes_2_out_30,
       pipes_2_out_31, pipes_2_out_32, pipes_2_out_33, pipes_2_out_34, pipes_2_out_35, pipes_2_out_36,
       pipes_3_out_5, pipes_3_out_6, pipes_3_out_7, pipes_3_out_8, pipes_3_out_9, pipes_3_out_10,
       pipes_3_out_11, pipes_3_out_12, pipes_3_out_13, pipes_3_out_14, pipes_3_out_15, pipes_3_out_16,
       pipes_3_out_17, pipes_3_out_18, pipes_3_out_19, pipes_3_out_20, pipes_3_out_21, pipes_3_out_22,
       pipes_3_out_23, pipes_3_out_24, pipes_3_out_25, pipes_3_out_26, pipes_3_out_27, pipes_3_out_28,
       pipes_3_out_29, pipes_3_out_30, pipes_3_out_31, pipes_3_out_32, pipes_3_out_33, pipes_3_out_34,
       pipes_3_out_35, pipes_3_out_36, pipes_4_out_5, pipes_4_out_6, pipes_4_out_7, pipes_4_out_8,
       pipes_4_out_9, pipes_4_out_10, pipes_4_out_11, pipes_4_out_12, pipes_4_out_13, pipes_4_out_14,
       pipes_4_out_15, pipes_4_out_16, pipes_4_out_17, pipes_4_out_18, pipes_4_out_19, pipes_4_out_20,
       pipes_4_out_21, pipes_4_out_22, pipes_4_out_23, pipes_4_out_24, pipes_4_out_25, pipes_4_out_26,
       pipes_4_out_27, pipes_4_out_28, pipes_4_out_29, pipes_4_out_30, pipes_4_out_31, pipes_4_out_32,
       pipes_4_out_33, pipes_4_out_34, pipes_4_out_35, pipes_4_out_36, pipes_5_out_5, pipes_5_out_6,
       pipes_5_out_7, pipes_5_out_8, pipes_5_out_9, pipes_5_out_10, pipes_5_out_11, pipes_5_out_12,
       pipes_5_out_13, pipes_5_out_14, pipes_5_out_15, pipes_5_out_16, pipes_5_out_17, pipes_5_out_18,
       pipes_5_out_19, pipes_5_out_20, pipes_5_out_21, pipes_5_out_22, pipes_5_out_23, pipes_5_out_24,
       pipes_5_out_25, pipes_5_out_26, pipes_5_out_27, pipes_5_out_28, pipes_5_out_29, pipes_5_out_30,
       pipes_5_out_31, pipes_5_out_32, pipes_5_out_33, pipes_5_out_34, pipes_5_out_35, pipes_5_out_36,
       pipes_6_out_5, pipes_6_out_6, pipes_6_out_7, pipes_6_out_8, pipes_6_out_9, pipes_6_out_10,
       pipes_6_out_11, pipes_6_out_12, pipes_6_out_13, pipes_6_out_14, pipes_6_out_15, pipes_6_out_16,
       pipes_6_out_17, pipes_6_out_18, pipes_6_out_19, pipes_6_out_20, pipes_6_out_21, pipes_6_out_22,
       pipes_6_out_23, pipes_6_out_24, pipes_6_out_25, pipes_6_out_26, pipes_6_out_27, pipes_6_out_28,
       pipes_6_out_29, pipes_6_out_30, pipes_6_out_31, pipes_6_out_32, pipes_6_out_33, pipes_6_out_34,
       pipes_6_out_35, pipes_6_out_36, pipes_7_out_5, pipes_7_out_6, pipes_7_out_7, pipes_7_out_8,
       pipes_7_out_9, pipes_7_out_10, pipes_7_out_11, pipes_7_out_12, pipes_7_out_13, pipes_7_out_14,
       pipes_7_out_15, pipes_7_out_16, pipes_7_out_17, pipes_7_out_18, pipes_7_out_19, pipes_7_out_20,
       pipes_7_out_21, pipes_7_out_22, pipes_7_out_23, pipes_7_out_24, pipes_7_out_25, pipes_7_out_26,
       pipes_7_out_27, pipes_7_out_28, pipes_7_out_29, pipes_7_out_30, pipes_7_out_31, pipes_7_out_32,
       pipes_7_out_33, pipes_7_out_34, pipes_7_out_35, pipes_7_out_36, pipes_8_out_5, pipes_8_out_6,
       pipes_8_out_7, pipes_8_out_8, pipes_8_out_9, pipes_8_out_10, pipes_8_out_11, pipes_8_out_12,
       pipes_8_out_13, pipes_8_out_14, pipes_8_out_15, pipes_8_out_16, pipes_8_out_17, pipes_8_out_18,
       pipes_8_out_19, pipes_8_out_20, pipes_8_out_21, pipes_8_out_22, pipes_8_out_23, pipes_8_out_24,
       pipes_8_out_25, pipes_8_out_26, pipes_8_out_27, pipes_8_out_28, pipes_8_out_29, pipes_8_out_30,
       pipes_8_out_31, pipes_8_out_32, pipes_8_out_33, pipes_8_out_34, pipes_8_out_35, pipes_8_out_36,
       pipes_9_out_5, pipes_9_out_6, pipes_9_out_7, pipes_9_out_8, pipes_9_out_9, pipes_9_out_10,
       pipes_9_out_11, pipes_9_out_12, pipes_9_out_13, pipes_9_out_14, pipes_9_out_15, pipes_9_out_16,
       pipes_9_out_17, pipes_9_out_18, pipes_9_out_19, pipes_9_out_20, pipes_9_out_21, pipes_9_out_22,
       pipes_9_out_23, pipes_9_out_24, pipes_9_out_25, pipes_9_out_26, pipes_9_out_27, pipes_9_out_28,
       pipes_9_out_29, pipes_9_out_30, pipes_9_out_31, pipes_9_out_32, pipes_9_out_33, pipes_9_out_34,
       pipes_9_out_35, pipes_9_out_36, pipes_10_out_5, pipes_10_out_6, pipes_10_out_7, pipes_10_out_8,
       pipes_10_out_9, pipes_10_out_10, pipes_10_out_11, pipes_10_out_12, pipes_10_out_13, pipes_10_out_14,
       pipes_10_out_15, pipes_10_out_16, pipes_10_out_17, pipes_10_out_18, pipes_10_out_19, pipes_10_out_20,
       pipes_10_out_21, pipes_10_out_22, pipes_10_out_23, pipes_10_out_24, pipes_10_out_25, pipes_10_out_26,
       pipes_10_out_27, pipes_10_out_28, pipes_10_out_29, pipes_10_out_30, pipes_10_out_31, pipes_10_out_32,
       pipes_10_out_33, pipes_10_out_34, pipes_10_out_35, pipes_10_out_36, pipes_11_out_5, pipes_11_out_6,
       pipes_11_out_7, pipes_11_out_8, pipes_11_out_9, pipes_11_out_10, pipes_11_out_11, pipes_11_out_12,
       pipes_11_out_13, pipes_11_out_14, pipes_11_out_15, pipes_11_out_16, pipes_11_out_17, pipes_11_out_18,
       pipes_11_out_19, pipes_11_out_20, pipes_11_out_21, pipes_11_out_22, pipes_11_out_23, pipes_11_out_24,
       pipes_11_out_25, pipes_11_out_26, pipes_11_out_27, pipes_11_out_28, pipes_11_out_29, pipes_11_out_30,
       pipes_11_out_31, pipes_11_out_32, pipes_11_out_33, pipes_11_out_34, pipes_11_out_35, pipes_11_out_36,
       pipes_12_out_5, pipes_12_out_6, pipes_12_out_7, pipes_12_out_8, pipes_12_out_9, pipes_12_out_10,
       pipes_12_out_11, pipes_12_out_12, pipes_12_out_13, pipes_12_out_14, pipes_12_out_15, pipes_12_out_16,
       pipes_12_out_17, pipes_12_out_18, pipes_12_out_19, pipes_12_out_20, pipes_12_out_21, pipes_12_out_22,
       pipes_12_out_23, pipes_12_out_24, pipes_12_out_25, pipes_12_out_26, pipes_12_out_27, pipes_12_out_28,
       pipes_12_out_29, pipes_12_out_30, pipes_12_out_31, pipes_12_out_32, pipes_12_out_33, pipes_12_out_34,
       pipes_12_out_35, pipes_12_out_36, pipes_13_bird, pipes_13_bird_1_2, pipes_13_out_5, pipes_13_out_6,
       pipes_13_out_7, pipes_13_out_8, pipes_13_out_9, pipes_13_out_10, pipes_13_out_11, pipes_13_out_12,
       pipes_13_out_13, pipes_13_out_14, pipes_13_out_15, pipes_13_out_16, pipes_13_out_17, pipes_13_out_18,
       pipes_13_out_19, pipes_13_out_20, pipes_13_out_21, pipes_13_out_22, pipes_13_out_23, pipes_13_out_24,
       pipes_13_out_25, pipes_13_out_26, pipes_13_out_27, pipes_13_out_28, pipes_13_out_29, pipes_13_out_30,
       pipes_13_out_31, pipes_13_out_32, pipes_13_out_33, pipes_13_out_34, pipes_13_out_35, pipes_13_out_36,
       pipes_13_pipe_2, pipes_14_bird, pipes_14_bird_1_2, pipes_14_out_5, pipes_14_out_6, pipes_14_out_7,
       pipes_14_out_8, pipes_14_out_9, pipes_14_out_10, pipes_14_out_11, pipes_14_out_12, pipes_14_out_13,
       pipes_14_out_14, pipes_14_out_15, pipes_14_out_16, pipes_14_out_17, pipes_14_out_18, pipes_14_out_19,
       pipes_14_out_20, pipes_14_out_21, pipes_14_out_22, pipes_14_out_23, pipes_14_out_24, pipes_14_out_25,
       pipes_14_out_26, pipes_14_out_27, pipes_14_out_28, pipes_14_out_29, pipes_14_out_30, pipes_14_out_31,
       pipes_14_out_32, pipes_14_out_33, pipes_14_out_34, pipes_14_out_35, pipes_14_out_36, pipes_14_pipe_2,
       pipes_15_bird, pipes_15_bird_1_2, pipes_15_out_5, pipes_15_out_6, pipes_15_out_7, pipes_15_out_8,
       pipes_15_out_9, pipes_15_out_10, pipes_15_out_11, pipes_15_out_12, pipes_15_out_13, pipes_15_out_14,
       pipes_15_out_15, pipes_15_out_16, pipes_15_out_17, pipes_15_out_18, pipes_15_out_19, pipes_15_out_20,
       pipes_15_out_21, pipes_15_out_22, pipes_15_out_23, pipes_15_out_24, pipes_15_out_25, pipes_15_out_26,
       pipes_15_out_27, pipes_15_out_28, pipes_15_out_29, pipes_15_out_30, pipes_15_out_31, pipes_15_out_32,
       pipes_15_out_33, pipes_15_out_34, pipes_15_out_35, pipes_15_out_36, pipes_15_pipe_2, pipes_16_bird,
       pipes_16_bird_1_2, pipes_16_out_5, pipes_16_out_6, pipes_16_out_7, pipes_16_out_8, pipes_16_out_9,
       pipes_16_out_10, pipes_16_out_11, pipes_16_out_12, pipes_16_out_13, pipes_16_out_14, pipes_16_out_15,
       pipes_16_out_16, pipes_16_out_17, pipes_16_out_18, pipes_16_out_19, pipes_16_out_20, pipes_16_out_21,
       pipes_16_out_22, pipes_16_out_23, pipes_16_out_24, pipes_16_out_25, pipes_16_out_26, pipes_16_out_27,
       pipes_16_out_28, pipes_16_out_29, pipes_16_out_30, pipes_16_out_31, pipes_16_out_32, pipes_16_out_33,
       pipes_16_out_34, pipes_16_out_35, pipes_16_out_36, pipes_16_pipe_2, pipes_17_bird, pipes_17_bird_1_2,
       pipes_17_out_5, pipes_17_out_6, pipes_17_out_7, pipes_17_out_8, pipes_17_out_9, pipes_17_out_10,
       pipes_17_out_11, pipes_17_out_12, pipes_17_out_13, pipes_17_out_14, pipes_17_out_15, pipes_17_out_16,
       pipes_17_out_17, pipes_17_out_18, pipes_17_out_19, pipes_17_out_20, pipes_17_out_21, pipes_17_out_22,
       pipes_17_out_23, pipes_17_out_24, pipes_17_out_25, pipes_17_out_26, pipes_17_out_27, pipes_17_out_28,
       pipes_17_out_29, pipes_17_out_30, pipes_17_out_31, pipes_17_out_32, pipes_17_out_33, pipes_17_out_34,
       pipes_17_out_35, pipes_17_out_36, pipes_17_pipe_2, pipes_18_bird, pipes_18_bird_1_2, pipes_18_out_5,
       pipes_18_out_6, pipes_18_out_7, pipes_18_out_8, pipes_18_out_9, pipes_18_out_10, pipes_18_out_11,
       pipes_18_out_12, pipes_18_out_13, pipes_18_out_14, pipes_18_out_15, pipes_18_out_16, pipes_18_out_17,
       pipes_18_out_18, pipes_18_out_19, pipes_18_out_20, pipes_18_out_21, pipes_18_out_22, pipes_18_out_23,
       pipes_18_out_24, pipes_18_out_25, pipes_18_out_26, pipes_18_out_27, pipes_18_out_28, pipes_18_out_29,
       pipes_18_out_30, pipes_18_out_31, pipes_18_out_32, pipes_18_out_33, pipes_18_out_34, pipes_18_out_35,
       pipes_18_out_36, pipes_18_pipe_2, pipes_19_bird, pipes_19_bird_1_2, pipes_19_out_5, pipes_19_out_6,
       pipes_19_out_7, pipes_19_out_8, pipes_19_out_9, pipes_19_out_10, pipes_19_out_11, pipes_19_out_12,
       pipes_19_out_13, pipes_19_out_14, pipes_19_out_15, pipes_19_out_16, pipes_19_out_17, pipes_19_out_18,
       pipes_19_out_19, pipes_19_out_20, pipes_19_out_21, pipes_19_out_22, pipes_19_out_23, pipes_19_out_24,
       pipes_19_out_25, pipes_19_out_26, pipes_19_out_27, pipes_19_out_28, pipes_19_out_29, pipes_19_out_30,
       pipes_19_out_31, pipes_19_out_32, pipes_19_out_33, pipes_19_out_34, pipes_19_out_35, pipes_19_out_36,
       pipes_19_pipe_2, pipes_20_bird, pipes_20_bird_1_2, pipes_20_out_5, pipes_20_out_6, pipes_20_out_7,
       pipes_20_out_8, pipes_20_out_9, pipes_20_out_10, pipes_20_out_11, pipes_20_out_12, pipes_20_out_13,
       pipes_20_out_14, pipes_20_out_15, pipes_20_out_16, pipes_20_out_17, pipes_20_out_18, pipes_20_out_19,
       pipes_20_out_20, pipes_20_out_21, pipes_20_out_22, pipes_20_out_23, pipes_20_out_24, pipes_20_out_25,
       pipes_20_out_26, pipes_20_out_27, pipes_20_out_28, pipes_20_out_29, pipes_20_out_30, pipes_20_out_31,
       pipes_20_out_32, pipes_20_out_33, pipes_20_out_34, pipes_20_out_35, pipes_20_out_36, pipes_20_pipe_2,
       pipes_21_bird, pipes_21_bird_1_2, pipes_21_out_5, pipes_21_out_6, pipes_21_out_7, pipes_21_out_8,
       pipes_21_out_9, pipes_21_out_10, pipes_21_out_11, pipes_21_out_12, pipes_21_out_13, pipes_21_out_14,
       pipes_21_out_15, pipes_21_out_16, pipes_21_out_17, pipes_21_out_18, pipes_21_out_19, pipes_21_out_20,
       pipes_21_out_21, pipes_21_out_22, pipes_21_out_23, pipes_21_out_24, pipes_21_out_25, pipes_21_out_26,
       pipes_21_out_27, pipes_21_out_28, pipes_21_out_29, pipes_21_out_30, pipes_21_out_31, pipes_21_out_32,
       pipes_21_out_33, pipes_21_out_34, pipes_21_out_35, pipes_21_out_36, pipes_21_pipe_2, pipes_22_bird,
       pipes_22_bird_1_2, pipes_22_out_5, pipes_22_out_6, pipes_22_out_7, pipes_22_out_8, pipes_22_out_9,
       pipes_22_out_10, pipes_22_out_11, pipes_22_out_12, pipes_22_out_13, pipes_22_out_14, pipes_22_out_15,
       pipes_22_out_16, pipes_22_out_17, pipes_22_out_18, pipes_22_out_19, pipes_22_out_20, pipes_22_out_21,
       pipes_22_out_22, pipes_22_out_23, pipes_22_out_24, pipes_22_out_25, pipes_22_out_26, pipes_22_out_27,
       pipes_22_out_28, pipes_22_out_29, pipes_22_out_30, pipes_22_out_31, pipes_22_out_32, pipes_22_out_33,
       pipes_22_out_34, pipes_22_out_35, pipes_22_out_36, pipes_22_pipe_2, pipes_23_bird, pipes_23_bird_1_2,
       pipes_23_out_5, pipes_23_out_6, pipes_23_out_7, pipes_23_out_8, pipes_23_out_9, pipes_23_out_10,
       pipes_23_out_11, pipes_23_out_12, pipes_23_out_13, pipes_23_out_14, pipes_23_out_15, pipes_23_out_16,
       pipes_23_out_17, pipes_23_out_18, pipes_23_out_19, pipes_23_out_20, pipes_23_out_21, pipes_23_out_22,
       pipes_23_out_23, pipes_23_out_24, pipes_23_out_25, pipes_23_out_26, pipes_23_out_27, pipes_23_out_28,
       pipes_23_out_29, pipes_23_out_30, pipes_23_out_31, pipes_23_out_32, pipes_23_out_33, pipes_23_out_34,
       pipes_23_out_35, pipes_23_out_36, pipes_23_pipe_2, pipes_24_bird, pipes_24_bird_1_2, pipes_24_out_5,
       pipes_24_out_6, pipes_24_out_7, pipes_24_out_8, pipes_24_out_9, pipes_24_out_10, pipes_24_out_11,
       pipes_24_out_12, pipes_24_out_13, pipes_24_out_14, pipes_24_out_15, pipes_24_out_16, pipes_24_out_17,
       pipes_24_out_18, pipes_24_out_19, pipes_24_out_20, pipes_24_out_21, pipes_24_out_22, pipes_24_out_23,
       pipes_24_out_24, pipes_24_out_25, pipes_24_out_26, pipes_24_out_27, pipes_24_out_28, pipes_24_out_29,
       pipes_24_out_30, pipes_24_out_31, pipes_24_out_32, pipes_24_out_33, pipes_24_out_34, pipes_24_out_35,
       pipes_24_pipe_2, pipes_25_bird, pipes_25_bird_1_2, pipes_25_out_5, pipes_25_out_6, pipes_25_out_7,
       pipes_25_out_8, pipes_25_out_9, pipes_25_out_10, pipes_25_out_11, pipes_25_out_12, pipes_25_out_13,
       pipes_25_out_14, pipes_25_out_15, pipes_25_out_16, pipes_25_out_17, pipes_25_out_18, pipes_25_out_19,
       pipes_25_out_20, pipes_25_out_21, pipes_25_out_22, pipes_25_out_23, pipes_25_out_24, pipes_25_out_25,
       pipes_25_out_26, pipes_25_out_27, pipes_25_out_28, pipes_25_out_29, pipes_25_out_30, pipes_25_out_31,
       pipes_25_out_32, pipes_25_out_33, pipes_25_out_34, pipes_25_out_35, pipes_25_out_36, pipes_25_pipe_2,
       pipes_26_bird, pipes_26_bird_1_2, pipes_26_out_5, pipes_26_out_6, pipes_26_out_7, pipes_26_out_8,
       pipes_26_out_9, pipes_26_out_10, pipes_26_out_11, pipes_26_out_12, pipes_26_out_13, pipes_26_out_14,
       pipes_26_out_15, pipes_26_out_16, pipes_26_out_17, pipes_26_out_18, pipes_26_out_19, pipes_26_out_20,
       pipes_26_out_21, pipes_26_out_22, pipes_26_out_23, pipes_26_out_24, pipes_26_out_25, pipes_26_out_26,
       pipes_26_out_27, pipes_26_out_28, pipes_26_out_29, pipes_26_out_30, pipes_26_out_31, pipes_26_out_32,
       pipes_26_out_33, pipes_26_out_34, pipes_26_out_35, pipes_26_out_36, pipes_26_pipe_2, pipes_27_bird,
       pipes_27_bird_1_2, pipes_27_out_5, pipes_27_out_6, pipes_27_out_7, pipes_27_out_8, pipes_27_out_9,
       pipes_27_out_10, pipes_27_out_11, pipes_27_out_12, pipes_27_out_13, pipes_27_out_14, pipes_27_out_15,
       pipes_27_out_16, pipes_27_out_17, pipes_27_out_18, pipes_27_out_19, pipes_27_out_20, pipes_27_out_21,
       pipes_27_out_22, pipes_27_out_23, pipes_27_out_24, pipes_27_out_25, pipes_27_out_26, pipes_27_out_27,
       pipes_27_out_28, pipes_27_out_29, pipes_27_out_30, pipes_27_out_31, pipes_27_out_32, pipes_27_out_33,
       pipes_27_out_34, pipes_27_out_35, pipes_27_out_36, pipes_27_pipe_2, pipes_28_bird, pipes_28_bird_1_2,
       pipes_28_out_5, pipes_28_out_6, pipes_28_out_7, pipes_28_out_8, pipes_28_out_9, pipes_28_out_10,
       pipes_28_out_11, pipes_28_out_12, pipes_28_out_13, pipes_28_out_14, pipes_28_out_15, pipes_28_out_16,
       pipes_28_out_17, pipes_28_out_18, pipes_28_out_19, pipes_28_out_20, pipes_28_out_21, pipes_28_out_22,
       pipes_28_out_23, pipes_28_out_24, pipes_28_out_25, pipes_28_out_26, pipes_28_out_27, pipes_28_out_28,
       pipes_28_out_29, pipes_28_out_30, pipes_28_out_31, pipes_28_out_32, pipes_28_out_33, pipes_28_out_34,
       pipes_28_out_35, pipes_28_out_36, pipes_28_pipe_2, pipes_29_bird, pipes_29_bird_1_2, pipes_29_out_5,
       pipes_29_out_6, pipes_29_out_7, pipes_29_out_8, pipes_29_out_9, pipes_29_out_10, pipes_29_out_11,
       pipes_29_out_12, pipes_29_out_13, pipes_29_out_14, pipes_29_out_15, pipes_29_out_16, pipes_29_out_17,
       pipes_29_out_18, pipes_29_out_19, pipes_29_out_20, pipes_29_out_21, pipes_29_out_22, pipes_29_out_23,
       pipes_29_out_24, pipes_29_out_25, pipes_29_out_26, pipes_29_out_27, pipes_29_out_28, pipes_29_out_29,
       pipes_29_out_30, pipes_29_out_31, pipes_29_out_32, pipes_29_out_33, pipes_29_out_34, pipes_29_out_35,
       pipes_29_out_36, pipes_29_pipe_2, pipes_30_bird, pipes_30_bird_1_2, pipes_30_out_5, pipes_30_out_6,
       pipes_30_out_7, pipes_30_out_8, pipes_30_out_9, pipes_30_out_10, pipes_30_out_11, pipes_30_out_12,
       pipes_30_out_13, pipes_30_out_14, pipes_30_out_15, pipes_30_out_16, pipes_30_out_17, pipes_30_out_18,
       pipes_30_out_19, pipes_30_out_20, pipes_30_out_21, pipes_30_out_22, pipes_30_out_23, pipes_30_out_24,
       pipes_30_out_25, pipes_30_out_26, pipes_30_out_27, pipes_30_out_28, pipes_30_out_29, pipes_30_out_30,
       pipes_30_out_31, pipes_30_out_32, pipes_30_out_33, pipes_30_out_34, pipes_30_out_35, pipes_30_out_36,
       pipes_30_pipe_2, pipes_31_bird, pipes_31_bird_1_2, pipes_31_out_5, pipes_31_out_6, pipes_31_out_7,
       pipes_31_out_8, pipes_31_out_9, pipes_31_out_10, pipes_31_out_11, pipes_31_out_12, pipes_31_out_13,
       pipes_31_out_14, pipes_31_out_15, pipes_31_out_16, pipes_31_out_17, pipes_31_out_18, pipes_31_out_19,
       pipes_31_out_20, pipes_31_out_21, pipes_31_out_22, pipes_31_out_23, pipes_31_out_24, pipes_31_out_25,
       pipes_31_out_26, pipes_31_out_27, pipes_31_out_28, pipes_31_out_29, pipes_31_out_30, pipes_31_out_31,
       pipes_31_out_32, pipes_31_out_33, pipes_31_out_34, pipes_31_out_35, pipes_31_out_36, pipes_31_pipe_2,
       pipes_32_bird, pipes_32_bird_1_2, pipes_32_out_5, pipes_32_out_6, pipes_32_out_7, pipes_32_out_8,
       pipes_32_out_9, pipes_32_out_10, pipes_32_out_11, pipes_32_out_12, pipes_32_out_13, pipes_32_out_14,
       pipes_32_out_15, pipes_32_out_16, pipes_32_out_17, pipes_32_out_18, pipes_32_out_19, pipes_32_out_20,
       pipes_32_out_21, pipes_32_out_22, pipes_32_out_23, pipes_32_out_24, pipes_32_out_25, pipes_32_out_26,
       pipes_32_out_27, pipes_32_out_28, pipes_32_out_29, pipes_32_out_30, pipes_32_out_31, pipes_32_out_32,
       pipes_32_out_33, pipes_32_out_34, pipes_32_out_35, pipes_32_out_36, pipes_32_pipe_2, pipes_33_bird,
       pipes_33_bird_1_2, pipes_33_out_5, pipes_33_out_6, pipes_33_out_7, pipes_33_out_8, pipes_33_out_9,
       pipes_33_out_10, pipes_33_out_11, pipes_33_out_12, pipes_33_out_13, pipes_33_out_14, pipes_33_out_15,
       pipes_33_out_16, pipes_33_out_17, pipes_33_out_18, pipes_33_out_19, pipes_33_out_20, pipes_33_out_21,
       pipes_33_out_22, pipes_33_out_23, pipes_33_out_24, pipes_33_out_25, pipes_33_out_26, pipes_33_out_27,
       pipes_33_out_28, pipes_33_out_29, pipes_33_out_30, pipes_33_out_31, pipes_33_out_32, pipes_33_out_33,
       pipes_33_out_34, pipes_33_out_35, pipes_33_out_36, pipes_33_pipe_2, pipes_34_bird, pipes_34_bird_1_2,
       pipes_34_out_5, pipes_34_out_6, pipes_34_out_7, pipes_34_out_8, pipes_34_out_9, pipes_34_out_10,
       pipes_34_out_11, pipes_34_out_12, pipes_34_out_13, pipes_34_out_14, pipes_34_out_15, pipes_34_out_16,
       pipes_34_out_17, pipes_34_out_18, pipes_34_out_19, pipes_34_out_20, pipes_34_out_21, pipes_34_out_22,
       pipes_34_out_23, pipes_34_out_24, pipes_34_out_25, pipes_34_out_26, pipes_34_out_27, pipes_34_out_28,
       pipes_34_out_29, pipes_34_out_30, pipes_34_out_31, pipes_34_out_32, pipes_34_out_33, pipes_34_out_34,
       pipes_34_out_35, pipes_34_out_36, pipes_34_pipe_2, pipes_35_bird, pipes_35_bird_1_2, pipes_35_out_5,
       pipes_35_out_6, pipes_35_out_7, pipes_35_out_8, pipes_35_out_9, pipes_35_out_10, pipes_35_out_11,
       pipes_35_out_12, pipes_35_out_13, pipes_35_out_14, pipes_35_out_15, pipes_35_out_16, pipes_35_out_17,
       pipes_35_out_18, pipes_35_out_19, pipes_35_out_20, pipes_35_out_21, pipes_35_out_22, pipes_35_out_23,
       pipes_35_out_24, pipes_35_out_25, pipes_35_out_26, pipes_35_out_27, pipes_35_out_28, pipes_35_out_29,
       pipes_35_out_30, pipes_35_out_31, pipes_35_out_32, pipes_35_out_33, pipes_35_out_34, pipes_35_out_35,
       pipes_35_out_36, pipes_35_pipe_2, pipes_36_bird, pipes_36_bird_1_2, pipes_36_out_5, pipes_36_out_6,
       pipes_36_out_7, pipes_36_out_8, pipes_36_out_9, pipes_36_out_10, pipes_36_out_11, pipes_36_out_12,
       pipes_36_out_13, pipes_36_out_14, pipes_36_out_15, pipes_36_out_16, pipes_36_out_17, pipes_36_out_18,
       pipes_36_out_19, pipes_36_out_20, pipes_36_out_21, pipes_36_out_22, pipes_36_out_23, pipes_36_out_24,
       pipes_36_out_25, pipes_36_out_26, pipes_36_out_27, pipes_36_out_28, pipes_36_out_29, pipes_36_out_30,
       pipes_36_out_31, pipes_36_out_32, pipes_36_out_33, pipes_36_out_34, pipes_36_out_35, pipes_36_out_36,
       pipes_36_pipe_2, pipes_37_bird, pipes_37_bird_1_2, pipes_37_out_5, pipes_37_out_6, pipes_37_out_7,
       pipes_37_out_8, pipes_37_out_9, pipes_37_out_10, pipes_37_out_11, pipes_37_out_12, pipes_37_out_13,
       pipes_37_out_14, pipes_37_out_15, pipes_37_out_16, pipes_37_out_17, pipes_37_out_18, pipes_37_out_19,
       pipes_37_out_20, pipes_37_out_21, pipes_37_out_22, pipes_37_out_23, pipes_37_out_24, pipes_37_out_25,
       pipes_37_out_26, pipes_37_out_27, pipes_37_out_28, pipes_37_out_29, pipes_37_out_30, pipes_37_out_31,
       pipes_37_out_32, pipes_37_out_33, pipes_37_out_34, pipes_37_out_35, pipes_37_out_36, pipes_37_pipe_2,
       pipes_38_bird, pipes_38_bird_1_2, pipes_38_out_5, pipes_38_out_6, pipes_38_out_7, pipes_38_out_8,
       pipes_38_out_9, pipes_38_out_10, pipes_38_out_11, pipes_38_out_12, pipes_38_out_13, pipes_38_out_14,
       pipes_38_out_15, pipes_38_out_16, pipes_38_out_17, pipes_38_out_18, pipes_38_out_19, pipes_38_out_20,
       pipes_38_out_21, pipes_38_out_22, pipes_38_out_23, pipes_38_out_24, pipes_38_out_25, pipes_38_out_26,
       pipes_38_out_27, pipes_38_out_28, pipes_38_out_29, pipes_38_out_30, pipes_38_out_31, pipes_38_out_32,
       pipes_38_out_33, pipes_38_out_34, pipes_38_out_35, pipes_38_out_36, pipes_38_pipe_2, pipes_39_bird,
       pipes_39_bird_1_2, pipes_39_out_5, pipes_39_out_6, pipes_39_out_7, pipes_39_out_8, pipes_39_out_9,
       pipes_39_out_10, pipes_39_out_11, pipes_39_out_12, pipes_39_out_13, pipes_39_out_14, pipes_39_out_15,
       pipes_39_out_16, pipes_39_out_17, pipes_39_out_18, pipes_39_out_19, pipes_39_out_20, pipes_39_out_21,
       pipes_39_out_22, pipes_39_out_23, pipes_39_out_24, pipes_39_out_25, pipes_39_out_26, pipes_39_out_27,
       pipes_39_out_28, pipes_39_out_29, pipes_39_out_30, pipes_39_out_31, pipes_39_out_32, pipes_39_out_33,
       pipes_39_out_34, pipes_39_out_35, pipes_39_out_36, pipes_39_pipe_2, pipes_40_bird, pipes_40_bird_1_2,
       pipes_40_out_5, pipes_40_out_6, pipes_40_out_7, pipes_40_out_8, pipes_40_out_9, pipes_40_out_10,
       pipes_40_out_11, pipes_40_out_12, pipes_40_out_13, pipes_40_out_14, pipes_40_out_15, pipes_40_out_16,
       pipes_40_out_17, pipes_40_out_18, pipes_40_out_19, pipes_40_out_20, pipes_40_out_21, pipes_40_out_22,
       pipes_40_out_23, pipes_40_out_24, pipes_40_out_25, pipes_40_out_26, pipes_40_out_27, pipes_40_out_28,
       pipes_40_out_29, pipes_40_out_30, pipes_40_out_31, pipes_40_out_32, pipes_40_out_33, pipes_40_out_34,
       pipes_40_out_35, pipes_40_out_36, pipes_40_pipe_2, pipes_41_bird, pipes_41_bird_1_2, pipes_41_out_5,
       pipes_41_out_6, pipes_41_out_7, pipes_41_out_8, pipes_41_out_9, pipes_41_out_10, pipes_41_out_11,
       pipes_41_out_12, pipes_41_out_13, pipes_41_out_14, pipes_41_out_15, pipes_41_out_16, pipes_41_out_17,
       pipes_41_out_18, pipes_41_out_19, pipes_41_out_20, pipes_41_out_21, pipes_41_out_22, pipes_41_out_23,
       pipes_41_out_24, pipes_41_out_25, pipes_41_out_26, pipes_41_out_27, pipes_41_out_28, pipes_41_out_29,
       pipes_41_out_30, pipes_41_out_31, pipes_41_out_32, pipes_41_out_33, pipes_41_out_34, pipes_41_out_35,
       pipes_41_out_36, pipes_41_pipe_2, pipes_42_bird, pipes_42_bird_1_2, pipes_42_out_5, pipes_42_out_6,
       pipes_42_out_7, pipes_42_out_8, pipes_42_out_9, pipes_42_out_10, pipes_42_out_11, pipes_42_out_12,
       pipes_42_out_13, pipes_42_out_14, pipes_42_out_15, pipes_42_out_16, pipes_42_out_17, pipes_42_out_18,
       pipes_42_out_19, pipes_42_out_20, pipes_42_out_21, pipes_42_out_22, pipes_42_out_23, pipes_42_out_24,
       pipes_42_out_25, pipes_42_out_26, pipes_42_out_27, pipes_42_out_28, pipes_42_out_29, pipes_42_out_30,
       pipes_42_out_31, pipes_42_out_32, pipes_42_out_33, pipes_42_out_34, pipes_42_out_35, pipes_42_out_36,
       pipes_42_pipe_2, pipes_43_bird, pipes_43_bird_1_2, pipes_43_out_5, pipes_43_out_6, pipes_43_out_7,
       pipes_43_out_8, pipes_43_out_9, pipes_43_out_10, pipes_43_out_11, pipes_43_out_12, pipes_43_out_13,
       pipes_43_out_14, pipes_43_out_15, pipes_43_out_16, pipes_43_out_17, pipes_43_out_18, pipes_43_out_19,
       pipes_43_out_20, pipes_43_out_21, pipes_43_out_22, pipes_43_out_23, pipes_43_out_24, pipes_43_out_25,
       pipes_43_out_26, pipes_43_out_27, pipes_43_out_28, pipes_43_out_29, pipes_43_out_30, pipes_43_out_31,
       pipes_43_out_32, pipes_43_out_33, pipes_43_out_34, pipes_43_out_35, pipes_43_out_36, pipes_43_pipe_2,
       pipes_44_bird, pipes_44_bird_1_2, pipes_44_out_5, pipes_44_out_6, pipes_44_out_7, pipes_44_out_8,
       pipes_44_out_9, pipes_44_out_10, pipes_44_out_11, pipes_44_out_12, pipes_44_out_13, pipes_44_out_14,
       pipes_44_out_15, pipes_44_out_16, pipes_44_out_17, pipes_44_out_18, pipes_44_out_19, pipes_44_out_20,
       pipes_44_out_21, pipes_44_out_22, pipes_44_out_23, pipes_44_out_24, pipes_44_out_25, pipes_44_out_26,
       pipes_44_out_27, pipes_44_out_28, pipes_44_out_29, pipes_44_out_30, pipes_44_out_31, pipes_44_out_32,
       pipes_44_out_33, pipes_44_out_34, pipes_44_out_35, pipes_44_out_36, pipes_44_pipe_2, pipes_45_bird,
       pipes_45_bird_1_2, pipes_45_out_5, pipes_45_out_6, pipes_45_out_7, pipes_45_out_8, pipes_45_out_9,
       pipes_45_out_10, pipes_45_out_11, pipes_45_out_12, pipes_45_out_13, pipes_45_out_14, pipes_45_out_15,
       pipes_45_out_16, pipes_45_out_17, pipes_45_out_18, pipes_45_out_19, pipes_45_out_20, pipes_45_out_21,
       pipes_45_out_22, pipes_45_out_23, pipes_45_out_24, pipes_45_out_25, pipes_45_out_26, pipes_45_out_27,
       pipes_45_out_28, pipes_45_out_29, pipes_45_out_30, pipes_45_out_31, pipes_45_out_32, pipes_45_out_33,
       pipes_45_out_34, pipes_45_out_35, pipes_45_out_36, pipes_45_pipe_2, pipes_46_bird, pipes_46_bird_1_2,
       pipes_46_out_5, pipes_46_out_6, pipes_46_out_7, pipes_46_out_8, pipes_46_out_9, pipes_46_out_10,
       pipes_46_out_11, pipes_46_out_12, pipes_46_out_13, pipes_46_out_14, pipes_46_out_15, pipes_46_out_16,
       pipes_46_out_17, pipes_46_out_18, pipes_46_out_19, pipes_46_out_20, pipes_46_out_21, pipes_46_out_22,
       pipes_46_out_23, pipes_46_out_24, pipes_46_out_25, pipes_46_out_26, pipes_46_out_27, pipes_46_out_28,
       pipes_46_out_29, pipes_46_out_30, pipes_46_out_31, pipes_46_out_32, pipes_46_out_33, pipes_46_out_34,
       pipes_46_out_35, pipes_46_out_36, pipes_46_pipe_2, pipes_47_bird, pipes_47_bird_1_2, pipes_47_out_5,
       pipes_47_out_6, pipes_47_out_7, pipes_47_out_8, pipes_47_out_9, pipes_47_out_10, pipes_47_out_11,
       pipes_47_out_12, pipes_47_out_13, pipes_47_out_14, pipes_47_out_15, pipes_47_out_16, pipes_47_out_17,
       pipes_47_out_18, pipes_47_out_19, pipes_47_out_20, pipes_47_out_21, pipes_47_out_22, pipes_47_out_23,
       pipes_47_out_24, pipes_47_out_25, pipes_47_out_26, pipes_47_out_27, pipes_47_out_28, pipes_47_out_29,
       pipes_47_out_30, pipes_47_out_31, pipes_47_out_32, pipes_47_out_33, pipes_47_out_34, pipes_47_out_35,
       pipes_47_out_36, pipes_47_pipe_2, pipes_48_bird, pipes_48_bird_1_2, pipes_48_out_5, pipes_48_out_6,
       pipes_48_out_7, pipes_48_out_8, pipes_48_out_9, pipes_48_out_10, pipes_48_out_11, pipes_48_out_12,
       pipes_48_out_13, pipes_48_out_14, pipes_48_out_15, pipes_48_out_16, pipes_48_out_17, pipes_48_out_18,
       pipes_48_out_19, pipes_48_out_20, pipes_48_out_21, pipes_48_out_22, pipes_48_out_23, pipes_48_out_24,
       pipes_48_out_25, pipes_48_out_26, pipes_48_out_27, pipes_48_out_28, pipes_48_out_29, pipes_48_out_30,
       pipes_48_out_31, pipes_48_out_32, pipes_48_out_33, pipes_48_out_34, pipes_48_out_35, pipes_48_out_36,
       pipes_48_pipe_2, pipes_49_bird, pipes_49_bird_1_2, pipes_49_out_5, pipes_49_out_6, pipes_49_out_7,
       pipes_49_out_8, pipes_49_out_9, pipes_49_out_10, pipes_49_out_11, pipes_49_out_12, pipes_49_out_13,
       pipes_49_out_14, pipes_49_out_15, pipes_49_out_16, pipes_49_out_17, pipes_49_out_18, pipes_49_out_19,
       pipes_49_out_20, pipes_49_out_21, pipes_49_out_22, pipes_49_out_23, pipes_49_out_24, pipes_49_out_25,
       pipes_49_out_26, pipes_49_out_27, pipes_49_out_28, pipes_49_out_29, pipes_49_out_30, pipes_49_out_31,
       pipes_49_out_32, pipes_49_out_33, pipes_49_out_34, pipes_49_out_35, pipes_49_out_36, pipes_49_pipe_2,
       pipes_50_bird, pipes_50_bird_1_2, pipes_50_out_5, pipes_50_out_6, pipes_50_out_7, pipes_50_out_8,
       pipes_50_out_9, pipes_50_out_10, pipes_50_out_11, pipes_50_out_12, pipes_50_out_13, pipes_50_out_14,
       pipes_50_out_15, pipes_50_out_16, pipes_50_out_17, pipes_50_out_18, pipes_50_out_19, pipes_50_out_20,
       pipes_50_out_21, pipes_50_out_22, pipes_50_out_23, pipes_50_out_24, pipes_50_out_25, pipes_50_out_26,
       pipes_50_out_27, pipes_50_out_28, pipes_50_out_29, pipes_50_out_30, pipes_50_out_31, pipes_50_out_32,
       pipes_50_out_33, pipes_50_out_34, pipes_50_out_35, pipes_50_out_36, pipes_50_pipe_2, pipes_51_bird,
       pipes_51_bird_1_2, pipes_51_out_5, pipes_51_out_6, pipes_51_out_7, pipes_51_out_8, pipes_51_out_9,
       pipes_51_out_10, pipes_51_out_11, pipes_51_out_12, pipes_51_out_13, pipes_51_out_14, pipes_51_out_15,
       pipes_51_out_16, pipes_51_out_17, pipes_51_out_18, pipes_51_out_19, pipes_51_out_20, pipes_51_out_21,
       pipes_51_out_22, pipes_51_out_23, pipes_51_out_24, pipes_51_out_25, pipes_51_out_26, pipes_51_out_27,
       pipes_51_out_28, pipes_51_out_29, pipes_51_out_30, pipes_51_out_31, pipes_51_out_32, pipes_51_out_33,
       pipes_51_out_34, pipes_51_out_35, pipes_51_out_36, pipes_51_pipe_2, pipes_52_bird, pipes_52_bird_1_2,
       pipes_52_out_5, pipes_52_out_6, pipes_52_out_7, pipes_52_out_8, pipes_52_out_9, pipes_52_out_10,
       pipes_52_out_11, pipes_52_out_12, pipes_52_out_13, pipes_52_out_14, pipes_52_out_15, pipes_52_out_16,
       pipes_52_out_17, pipes_52_out_18, pipes_52_out_19, pipes_52_out_20, pipes_52_out_21, pipes_52_out_22,
       pipes_52_out_23, pipes_52_out_24, pipes_52_out_25, pipes_52_out_26, pipes_52_out_27, pipes_52_out_28,
       pipes_52_out_29, pipes_52_out_30, pipes_52_out_31, pipes_52_out_32, pipes_52_out_33, pipes_52_out_34,
       pipes_52_out_35, pipes_52_out_36, pipes_52_pipe_2, pipes_53_bird, pipes_53_bird_1_2, pipes_53_out_5,
       pipes_53_out_6, pipes_53_out_7, pipes_53_out_8, pipes_53_out_9, pipes_53_out_10, pipes_53_out_11,
       pipes_53_out_12, pipes_53_out_13, pipes_53_out_14, pipes_53_out_15, pipes_53_out_16, pipes_53_out_17,
       pipes_53_out_18, pipes_53_out_19, pipes_53_out_20, pipes_53_out_21, pipes_53_out_22, pipes_53_out_23,
       pipes_53_out_24, pipes_53_out_25, pipes_53_out_26, pipes_53_out_27, pipes_53_out_28, pipes_53_out_29,
       pipes_53_out_30, pipes_53_out_31, pipes_53_out_32, pipes_53_out_33, pipes_53_out_34, pipes_53_out_35,
       pipes_53_out_36, pipes_53_pipe_2, pipes_54_bird, pipes_54_bird_1_2, pipes_54_out_5, pipes_54_out_6,
       pipes_54_out_7, pipes_54_out_8, pipes_54_out_9, pipes_54_out_10, pipes_54_out_11, pipes_54_out_12,
       pipes_54_out_13, pipes_54_out_14, pipes_54_out_15, pipes_54_out_16, pipes_54_out_17, pipes_54_out_18,
       pipes_54_out_19, pipes_54_out_20, pipes_54_out_21, pipes_54_out_22, pipes_54_out_23, pipes_54_out_24,
       pipes_54_out_25, pipes_54_out_26, pipes_54_out_27, pipes_54_out_28, pipes_54_out_29, pipes_54_out_30,
       pipes_54_out_31, pipes_54_out_32, pipes_54_out_33, pipes_54_out_34, pipes_54_out_35, pipes_54_out_36,
       pipes_54_pipe_2, pipes_55_bird, pipes_55_bird_1_2, pipes_55_out_5, pipes_55_out_6, pipes_55_out_7,
       pipes_55_out_8, pipes_55_out_9, pipes_55_out_10, pipes_55_out_11, pipes_55_out_12, pipes_55_out_13,
       pipes_55_out_14, pipes_55_out_15, pipes_55_out_16, pipes_55_out_17, pipes_55_out_18, pipes_55_out_19,
       pipes_55_out_20, pipes_55_out_21, pipes_55_out_22, pipes_55_out_23, pipes_55_out_24, pipes_55_out_25,
       pipes_55_out_26, pipes_55_out_27, pipes_55_out_28, pipes_55_out_29, pipes_55_out_30, pipes_55_out_31,
       pipes_55_out_32, pipes_55_out_33, pipes_55_out_34, pipes_55_out_35, pipes_55_out_36, pipes_55_pipe_2,
       pipes_56_bird, pipes_56_bird_1_2, pipes_56_out_5, pipes_56_out_6, pipes_56_out_7, pipes_56_out_8,
       pipes_56_out_9, pipes_56_out_10, pipes_56_out_11, pipes_56_out_12, pipes_56_out_13, pipes_56_out_14,
       pipes_56_out_15, pipes_56_out_16, pipes_56_out_17, pipes_56_out_18, pipes_56_out_19, pipes_56_out_20,
       pipes_56_out_21, pipes_56_out_22, pipes_56_out_23, pipes_56_out_24, pipes_56_out_25, pipes_56_out_26,
       pipes_56_out_27, pipes_56_out_28, pipes_56_out_29, pipes_56_out_30, pipes_56_out_31, pipes_56_out_32,
       pipes_56_out_33, pipes_56_out_34, pipes_56_out_35, pipes_56_out_36, pipes_56_pipe_2, pipes_57_bird,
       pipes_57_bird_1_2, pipes_57_out_5, pipes_57_out_6, pipes_57_out_7, pipes_57_out_8, pipes_57_out_9,
       pipes_57_out_10, pipes_57_out_11, pipes_57_out_12, pipes_57_out_13, pipes_57_out_14, pipes_57_out_15,
       pipes_57_out_16, pipes_57_out_17, pipes_57_out_18, pipes_57_out_19, pipes_57_out_20, pipes_57_out_21,
       pipes_57_out_22, pipes_57_out_23, pipes_57_out_24, pipes_57_out_25, pipes_57_out_26, pipes_57_out_27,
       pipes_57_out_28, pipes_57_out_29, pipes_57_out_30, pipes_57_out_31, pipes_57_out_32, pipes_57_out_33,
       pipes_57_out_34, pipes_57_out_35, pipes_57_out_36, pipes_57_pipe_2, pipes_58_bird, pipes_58_bird_1_2,
       pipes_58_out_5, pipes_58_out_6, pipes_58_out_7, pipes_58_out_8, pipes_58_out_9, pipes_58_out_10,
       pipes_58_out_11, pipes_58_out_12, pipes_58_out_13, pipes_58_out_14, pipes_58_out_15, pipes_58_out_16,
       pipes_58_out_17, pipes_58_out_18, pipes_58_out_19, pipes_58_out_20, pipes_58_out_21, pipes_58_out_22,
       pipes_58_out_23, pipes_58_out_24, pipes_58_out_25, pipes_58_out_26, pipes_58_out_27, pipes_58_out_28,
       pipes_58_out_29, pipes_58_out_30, pipes_58_out_31, pipes_58_out_32, pipes_58_out_33, pipes_58_out_34,
       pipes_58_out_35, pipes_58_out_36, pipes_58_pipe_2, pipes_59_bird, pipes_59_bird_1_2, pipes_59_out_5,
       pipes_59_out_6, pipes_59_out_7, pipes_59_out_8, pipes_59_out_9, pipes_59_out_10, pipes_59_out_11,
       pipes_59_out_12, pipes_59_out_13, pipes_59_out_14, pipes_59_out_15, pipes_59_out_16, pipes_59_out_17,
       pipes_59_out_18, pipes_59_out_19, pipes_59_out_20, pipes_59_out_21, pipes_59_out_22, pipes_59_out_23,
       pipes_59_out_24, pipes_59_out_25, pipes_59_out_26, pipes_59_out_27, pipes_59_out_28, pipes_59_out_29,
       pipes_59_out_30, pipes_59_out_31, pipes_59_out_32, pipes_59_out_33, pipes_59_out_34, pipes_59_out_35,
       pipes_59_out_36, pipes_59_pipe_2, pipes_60_bird, pipes_60_bird_1_2, pipes_60_out_5, pipes_60_out_6,
       pipes_60_out_7, pipes_60_out_8, pipes_60_out_9, pipes_60_out_10, pipes_60_out_11, pipes_60_out_12,
       pipes_60_out_13, pipes_60_out_14, pipes_60_out_15, pipes_60_out_16, pipes_60_out_17, pipes_60_out_18,
       pipes_60_out_19, pipes_60_out_20, pipes_60_out_21, pipes_60_out_22, pipes_60_out_23, pipes_60_out_24,
       pipes_60_out_25, pipes_60_out_26, pipes_60_out_27, pipes_60_out_28, pipes_60_out_29, pipes_60_out_30,
       pipes_60_out_31, pipes_60_out_32, pipes_60_out_33, pipes_60_out_34, pipes_60_out_35, pipes_60_out_36,
       pipes_60_pipe_2, pipes_61_bird, pipes_61_bird_1_2, pipes_61_out_5, pipes_61_out_6, pipes_61_out_7,
       pipes_61_out_8, pipes_61_out_9, pipes_61_out_10, pipes_61_out_11, pipes_61_out_12, pipes_61_out_13,
       pipes_61_out_14, pipes_61_out_15, pipes_61_out_16, pipes_61_out_17, pipes_61_out_18, pipes_61_out_19,
       pipes_61_out_20, pipes_61_out_21, pipes_61_out_22, pipes_61_out_23, pipes_61_out_24, pipes_61_out_25,
       pipes_61_out_26, pipes_61_out_27, pipes_61_out_28, pipes_61_out_29, pipes_61_out_30, pipes_61_out_31,
       pipes_61_out_32, pipes_61_out_33, pipes_61_out_34, pipes_61_out_35, pipes_61_out_36, pipes_61_pipe_2,
       pipes_62_bird, pipes_62_bird_1_2, pipes_62_out_5, pipes_62_out_6, pipes_62_out_7, pipes_62_out_8,
       pipes_62_out_9, pipes_62_out_10, pipes_62_out_11, pipes_62_out_12, pipes_62_out_13, pipes_62_out_14,
       pipes_62_out_15, pipes_62_out_16, pipes_62_out_17, pipes_62_out_18, pipes_62_out_19, pipes_62_out_20,
       pipes_62_out_21, pipes_62_out_22, pipes_62_out_23, pipes_62_out_24, pipes_62_out_25, pipes_62_out_26,
       pipes_62_out_27, pipes_62_out_28, pipes_62_out_29, pipes_62_out_30, pipes_62_out_31, pipes_62_out_32,
       pipes_62_out_33, pipes_62_out_34, pipes_62_out_35, pipes_62_out_36, pipes_62_pipe_2, pipes_63_bird,
       pipes_63_bird_1_2, pipes_63_out_5, pipes_63_out_6, pipes_63_out_7, pipes_63_out_8, pipes_63_out_9,
       pipes_63_out_10, pipes_63_out_11, pipes_63_out_12, pipes_63_out_13, pipes_63_out_14, pipes_63_out_15,
       pipes_63_out_16, pipes_63_out_17, pipes_63_out_18, pipes_63_out_19, pipes_63_out_20, pipes_63_out_21,
       pipes_63_out_22, pipes_63_out_23, pipes_63_out_24, pipes_63_out_25, pipes_63_out_26, pipes_63_out_27,
       pipes_63_out_28, pipes_63_out_29, pipes_63_out_30, pipes_63_out_31, pipes_63_out_32, pipes_63_out_33,
       pipes_63_out_34, pipes_63_out_35, pipes_63_out_36, pipes_63_pipe_2, pipes_64_bird, pipes_64_bird_1_2,
       pipes_64_out_5, pipes_64_out_6, pipes_64_out_7, pipes_64_out_8, pipes_64_out_9, pipes_64_out_10,
       pipes_64_out_11, pipes_64_out_12, pipes_64_out_13, pipes_64_out_14, pipes_64_out_15, pipes_64_out_16,
       pipes_64_out_17, pipes_64_out_18, pipes_64_out_19, pipes_64_out_20, pipes_64_out_21, pipes_64_out_22,
       pipes_64_out_23, pipes_64_out_24, pipes_64_out_25, pipes_64_out_26, pipes_64_out_27, pipes_64_out_28,
       pipes_64_out_29, pipes_64_out_30, pipes_64_out_31, pipes_64_out_32, pipes_64_out_33, pipes_64_out_34,
       pipes_64_out_35, pipes_64_out_36, pipes_64_pipe_2, pipes_65_bird, pipes_65_bird_1_2, pipes_65_out_5,
       pipes_65_out_6, pipes_65_out_7, pipes_65_out_8, pipes_65_out_9, pipes_65_out_10, pipes_65_out_11,
       pipes_65_out_12, pipes_65_out_13, pipes_65_out_14, pipes_65_out_15, pipes_65_out_16, pipes_65_out_17,
       pipes_65_out_18, pipes_65_out_19, pipes_65_out_20, pipes_65_out_21, pipes_65_out_22, pipes_65_out_23,
       pipes_65_out_24, pipes_65_out_25, pipes_65_out_26, pipes_65_out_27, pipes_65_out_28, pipes_65_out_29,
       pipes_65_out_30, pipes_65_out_31, pipes_65_out_32, pipes_65_out_33, pipes_65_out_34, pipes_65_out_35,
       pipes_65_out_36, pipes_65_pipe_2, pipes_66_bird, pipes_66_bird_1_2, pipes_66_out_5, pipes_66_out_6,
       pipes_66_out_7, pipes_66_out_8, pipes_66_out_9, pipes_66_out_10, pipes_66_out_11, pipes_66_out_12,
       pipes_66_out_13, pipes_66_out_14, pipes_66_out_15, pipes_66_out_16, pipes_66_out_17, pipes_66_out_18,
       pipes_66_out_19, pipes_66_out_20, pipes_66_out_21, pipes_66_out_22, pipes_66_out_23, pipes_66_out_24,
       pipes_66_out_25, pipes_66_out_26, pipes_66_out_27, pipes_66_out_28, pipes_66_out_29, pipes_66_out_30,
       pipes_66_out_31, pipes_66_out_32, pipes_66_out_33, pipes_66_out_34, pipes_66_out_35, pipes_66_out_36,
       pipes_66_pipe_2, pipes_67_bird, pipes_67_bird_1_2, pipes_67_out_5, pipes_67_out_6, pipes_67_out_7,
       pipes_67_out_8, pipes_67_out_9, pipes_67_out_10, pipes_67_out_11, pipes_67_out_12, pipes_67_out_13,
       pipes_67_out_14, pipes_67_out_15, pipes_67_out_16, pipes_67_out_17, pipes_67_out_18, pipes_67_out_19,
       pipes_67_out_20, pipes_67_out_21, pipes_67_out_22, pipes_67_out_23, pipes_67_out_24, pipes_67_out_25,
       pipes_67_out_26, pipes_67_out_27, pipes_67_out_28, pipes_67_out_29, pipes_67_out_30, pipes_67_out_31,
       pipes_67_out_32, pipes_67_out_33, pipes_67_out_34, pipes_67_out_35, pipes_67_out_36, pipes_67_pipe_2,
       pipes_68_bird, pipes_68_bird_1_2, pipes_68_out_5, pipes_68_out_6, pipes_68_out_7, pipes_68_out_8,
       pipes_68_out_9, pipes_68_out_10, pipes_68_out_11, pipes_68_out_12, pipes_68_out_13, pipes_68_out_14,
       pipes_68_out_15, pipes_68_out_16, pipes_68_out_17, pipes_68_out_18, pipes_68_out_19, pipes_68_out_20,
       pipes_68_out_21, pipes_68_out_22, pipes_68_out_23, pipes_68_out_24, pipes_68_out_25, pipes_68_out_26,
       pipes_68_out_27, pipes_68_out_28, pipes_68_out_29, pipes_68_out_30, pipes_68_out_31, pipes_68_out_32,
       pipes_68_out_33, pipes_68_out_34, pipes_68_out_35, pipes_68_out_36, pipes_68_pipe_2, pipes_69_bird,
       pipes_69_bird_1_2, pipes_69_out_5, pipes_69_out_6, pipes_69_out_7, pipes_69_out_8, pipes_69_out_9,
       pipes_69_out_10, pipes_69_out_11, pipes_69_out_12, pipes_69_out_13, pipes_69_out_14, pipes_69_out_15,
       pipes_69_out_16, pipes_69_out_17, pipes_69_out_18, pipes_69_out_19, pipes_69_out_20, pipes_69_out_21,
       pipes_69_out_22, pipes_69_out_23, pipes_69_out_24, pipes_69_out_25, pipes_69_out_26, pipes_69_out_27,
       pipes_69_out_28, pipes_69_out_29, pipes_69_out_30, pipes_69_out_31, pipes_69_out_32, pipes_69_out_33,
       pipes_69_out_34, pipes_69_out_35, pipes_69_out_36, pipes_69_pipe_2, pipes_70_bird, pipes_70_bird_1_2,
       pipes_70_out_5, pipes_70_out_6, pipes_70_out_7, pipes_70_out_8, pipes_70_out_9, pipes_70_out_10,
       pipes_70_out_11, pipes_70_out_12, pipes_70_out_13, pipes_70_out_14, pipes_70_out_15, pipes_70_out_16,
       pipes_70_out_17, pipes_70_out_18, pipes_70_out_19, pipes_70_out_20, pipes_70_out_21, pipes_70_out_22,
       pipes_70_out_23, pipes_70_out_24, pipes_70_out_25, pipes_70_out_26, pipes_70_out_27, pipes_70_out_28,
       pipes_70_out_29, pipes_70_out_30, pipes_70_out_31, pipes_70_out_32, pipes_70_out_33, pipes_70_out_34,
       pipes_70_out_35, pipes_70_out_36, pipes_70_pipe_2, pipes_71_bird, pipes_71_bird_1_2, pipes_71_out_5,
       pipes_71_out_6, pipes_71_out_7, pipes_71_out_8, pipes_71_out_9, pipes_71_out_10, pipes_71_out_11,
       pipes_71_out_12, pipes_71_out_13, pipes_71_out_14, pipes_71_out_15, pipes_71_out_16, pipes_71_out_17,
       pipes_71_out_18, pipes_71_out_19, pipes_71_out_20, pipes_71_out_21, pipes_71_out_22, pipes_71_out_23,
       pipes_71_out_24, pipes_71_out_25, pipes_71_out_26, pipes_71_out_27, pipes_71_out_28, pipes_71_out_29,
       pipes_71_out_30, pipes_71_out_31, pipes_71_out_32, pipes_71_out_33, pipes_71_out_34, pipes_71_out_35,
       pipes_71_out_36, pipes_71_pipe_2, pipes_72_bird, pipes_72_bird_1_2, pipes_72_out_5, pipes_72_out_6,
       pipes_72_out_7, pipes_72_out_8, pipes_72_out_9, pipes_72_out_10, pipes_72_out_11, pipes_72_out_12,
       pipes_72_out_13, pipes_72_out_14, pipes_72_out_15, pipes_72_out_16, pipes_72_out_17, pipes_72_out_18,
       pipes_72_out_19, pipes_72_out_20, pipes_72_out_21, pipes_72_out_22, pipes_72_out_23, pipes_72_out_24,
       pipes_72_out_25, pipes_72_out_26, pipes_72_out_27, pipes_72_out_28, pipes_72_out_29, pipes_72_out_30,
       pipes_72_out_31, pipes_72_out_32, pipes_72_out_33, pipes_72_out_34, pipes_72_out_35, pipes_72_out_36,
       pipes_72_pipe_2, pipes_73_bird, pipes_73_bird_1_2, pipes_73_out_5, pipes_73_out_6, pipes_73_out_7,
       pipes_73_out_8, pipes_73_out_9, pipes_73_out_10, pipes_73_out_11, pipes_73_out_12, pipes_73_out_13,
       pipes_73_out_14, pipes_73_out_15, pipes_73_out_16, pipes_73_out_17, pipes_73_out_18, pipes_73_out_19,
       pipes_73_out_20, pipes_73_out_21, pipes_73_out_22, pipes_73_out_23, pipes_73_out_24, pipes_73_out_25,
       pipes_73_out_26, pipes_73_out_27, pipes_73_out_28, pipes_73_out_29, pipes_73_out_30, pipes_73_out_31,
       pipes_73_out_32, pipes_73_out_33, pipes_73_out_34, pipes_73_out_35, pipes_73_out_36, pipes_73_pipe_2,
       pipes_74_bird, pipes_74_bird_1_2, pipes_74_out_5, pipes_74_out_6, pipes_74_out_7, pipes_74_out_8,
       pipes_74_out_9, pipes_74_out_10, pipes_74_out_11, pipes_74_out_12, pipes_74_out_13, pipes_74_out_14,
       pipes_74_out_15, pipes_74_out_16, pipes_74_out_17, pipes_74_out_18, pipes_74_out_19, pipes_74_out_20,
       pipes_74_out_21, pipes_74_out_22, pipes_74_out_23, pipes_74_out_24, pipes_74_out_25, pipes_74_out_26,
       pipes_74_out_27, pipes_74_out_28, pipes_74_out_29, pipes_74_out_30, pipes_74_out_31, pipes_74_out_32,
       pipes_74_out_33, pipes_74_out_34, pipes_74_out_35, pipes_74_out_36, pipes_74_pipe_2, pipes_75_bird,
       pipes_75_bird_1_2, pipes_75_out_5, pipes_75_out_6, pipes_75_out_7, pipes_75_out_8, pipes_75_out_9,
       pipes_75_out_10, pipes_75_out_11, pipes_75_out_12, pipes_75_out_13, pipes_75_out_14, pipes_75_out_15,
       pipes_75_out_16, pipes_75_out_17, pipes_75_out_18, pipes_75_out_19, pipes_75_out_20, pipes_75_out_21,
       pipes_75_out_22, pipes_75_out_23, pipes_75_out_24, pipes_75_out_25, pipes_75_out_26, pipes_75_out_27,
       pipes_75_out_28, pipes_75_out_29, pipes_75_out_30, pipes_75_out_31, pipes_75_out_32, pipes_75_out_33,
       pipes_75_out_34, pipes_75_out_35, pipes_75_out_36, pipes_75_pipe_2, pipes_76_bird, pipes_76_bird_1_2,
       pipes_76_out_5, pipes_76_out_6, pipes_76_out_7, pipes_76_out_8, pipes_76_out_9, pipes_76_out_10,
       pipes_76_out_11, pipes_76_out_12, pipes_76_out_13, pipes_76_out_14, pipes_76_out_15, pipes_76_out_16,
       pipes_76_out_17, pipes_76_out_18, pipes_76_out_19, pipes_76_out_20, pipes_76_out_21, pipes_76_out_22,
       pipes_76_out_23, pipes_76_out_24, pipes_76_out_25, pipes_76_out_26, pipes_76_out_27, pipes_76_out_28,
       pipes_76_out_29, pipes_76_out_30, pipes_76_out_31, pipes_76_out_32, pipes_76_out_33, pipes_76_out_34,
       pipes_76_out_35, pipes_76_out_36, pipes_76_pipe_2, pipes_77_bird, pipes_77_bird_1_2, pipes_77_out_5,
       pipes_77_out_6, pipes_77_out_7, pipes_77_out_8, pipes_77_out_9, pipes_77_out_10, pipes_77_out_11,
       pipes_77_out_12, pipes_77_out_13, pipes_77_out_14, pipes_77_out_15, pipes_77_out_16, pipes_77_out_17,
       pipes_77_out_18, pipes_77_out_19, pipes_77_out_20, pipes_77_out_21, pipes_77_out_22, pipes_77_out_23,
       pipes_77_out_24, pipes_77_out_25, pipes_77_out_26, pipes_77_out_27, pipes_77_out_28, pipes_77_out_29,
       pipes_77_out_30, pipes_77_out_31, pipes_77_out_32, pipes_77_out_33, pipes_77_out_34, pipes_77_out_35,
       pipes_77_out_36, pipes_77_pipe_2, pipes_78_bird, pipes_78_bird_1_2, pipes_78_out_5, pipes_78_out_6,
       pipes_78_out_7, pipes_78_out_8, pipes_78_out_9, pipes_78_out_10, pipes_78_out_11, pipes_78_out_12,
       pipes_78_out_13, pipes_78_out_14, pipes_78_out_15, pipes_78_out_16, pipes_78_out_17, pipes_78_out_18,
       pipes_78_out_19, pipes_78_out_20, pipes_78_out_21, pipes_78_out_22, pipes_78_out_23, pipes_78_out_24,
       pipes_78_out_25, pipes_78_out_26, pipes_78_out_27, pipes_78_out_28, pipes_78_out_29, pipes_78_out_30,
       pipes_78_out_31, pipes_78_out_32, pipes_78_out_33, pipes_78_out_34, pipes_78_out_35, pipes_78_out_36,
       pipes_78_pipe_2, pipes_79_bird, pipes_79_bird_1_2, pipes_79_out_5, pipes_79_out_6, pipes_79_out_7,
       pipes_79_out_8, pipes_79_out_9, pipes_79_out_10, pipes_79_out_11, pipes_79_out_12, pipes_79_out_13,
       pipes_79_out_14, pipes_79_out_15, pipes_79_out_16, pipes_79_out_17, pipes_79_out_18, pipes_79_out_19,
       pipes_79_out_20, pipes_79_out_21, pipes_79_out_22, pipes_79_out_23, pipes_79_out_24, pipes_79_out_25,
       pipes_79_out_26, pipes_79_out_27, pipes_79_out_28, pipes_79_out_29, pipes_79_out_30, pipes_79_out_31,
       pipes_79_out_32, pipes_79_out_33, pipes_79_out_34, pipes_79_out_35, pipes_79_out_36, pipes_79_pipe_2,
       pipes_80_bird, pipes_80_bird_1_2, pipes_80_out_5, pipes_80_out_6, pipes_80_out_7, pipes_80_out_8,
       pipes_80_out_9, pipes_80_out_10, pipes_80_out_11, pipes_80_out_12, pipes_80_out_13, pipes_80_out_14,
       pipes_80_out_15, pipes_80_out_16, pipes_80_out_17, pipes_80_out_18, pipes_80_out_19, pipes_80_out_20,
       pipes_80_out_21, pipes_80_out_22, pipes_80_out_23, pipes_80_out_24, pipes_80_out_25, pipes_80_out_26,
       pipes_80_out_27, pipes_80_out_28, pipes_80_out_29, pipes_80_out_30, pipes_80_out_31, pipes_80_out_32,
       pipes_80_out_33, pipes_80_out_34, pipes_80_out_35, pipes_80_out_36, pipes_80_pipe_2, pipes_81_bird,
       pipes_81_bird_1_2, pipes_81_out_5, pipes_81_out_6, pipes_81_out_7, pipes_81_out_8, pipes_81_out_9,
       pipes_81_out_10, pipes_81_out_11, pipes_81_out_12, pipes_81_out_13, pipes_81_out_14, pipes_81_out_15,
       pipes_81_out_16, pipes_81_out_17, pipes_81_out_18, pipes_81_out_19, pipes_81_out_20, pipes_81_out_21,
       pipes_81_out_22, pipes_81_out_23, pipes_81_out_24, pipes_81_out_25, pipes_81_out_26, pipes_81_out_27,
       pipes_81_out_28, pipes_81_out_29, pipes_81_out_30, pipes_81_out_31, pipes_81_out_32, pipes_81_out_33,
       pipes_81_out_34, pipes_81_out_35, pipes_81_out_36, pipes_81_pipe_2, pipes_82_bird, pipes_82_bird_1_2,
       pipes_82_out_5, pipes_82_out_6, pipes_82_out_7, pipes_82_out_8, pipes_82_out_9, pipes_82_out_10,
       pipes_82_out_11, pipes_82_out_12, pipes_82_out_13, pipes_82_out_14, pipes_82_out_15, pipes_82_out_16,
       pipes_82_out_17, pipes_82_out_18, pipes_82_out_19, pipes_82_out_20, pipes_82_out_21, pipes_82_out_22,
       pipes_82_out_23, pipes_82_out_24, pipes_82_out_25, pipes_82_out_26, pipes_82_out_27, pipes_82_out_28,
       pipes_82_out_29, pipes_82_out_30, pipes_82_out_31, pipes_82_out_32, pipes_82_out_33, pipes_82_out_34,
       pipes_82_out_35, pipes_82_out_36, pipes_82_pipe_2, pipes_83_bird, pipes_83_bird_1_2, pipes_83_out_5,
       pipes_83_out_6, pipes_83_out_7, pipes_83_out_8, pipes_83_out_9, pipes_83_out_10, pipes_83_out_11,
       pipes_83_out_12, pipes_83_out_13, pipes_83_out_14, pipes_83_out_15, pipes_83_out_16, pipes_83_out_17,
       pipes_83_out_18, pipes_83_out_19, pipes_83_out_20, pipes_83_out_21, pipes_83_out_22, pipes_83_out_23,
       pipes_83_out_24, pipes_83_out_25, pipes_83_out_26, pipes_83_out_27, pipes_83_out_28, pipes_83_out_29,
       pipes_83_out_30, pipes_83_out_31, pipes_83_out_32, pipes_83_out_33, pipes_83_out_34, pipes_83_out_35,
       pipes_83_out_36, pipes_83_pipe_2, pipes_84_bird, pipes_84_bird_1_2, pipes_84_out_5, pipes_84_out_6,
       pipes_84_out_7, pipes_84_out_8, pipes_84_out_9, pipes_84_out_10, pipes_84_out_11, pipes_84_out_12,
       pipes_84_out_13, pipes_84_out_14, pipes_84_out_15, pipes_84_out_16, pipes_84_out_17, pipes_84_out_18,
       pipes_84_out_19, pipes_84_out_20, pipes_84_out_21, pipes_84_out_22, pipes_84_out_23, pipes_84_out_24,
       pipes_84_out_25, pipes_84_out_26, pipes_84_out_27, pipes_84_out_28, pipes_84_out_29, pipes_84_out_30,
       pipes_84_out_31, pipes_84_out_32, pipes_84_out_33, pipes_84_out_34, pipes_84_out_35, pipes_84_out_36,
       pipes_84_pipe_2, pipes___bird_1_bird_1_2, pipes___bird_1_bird_2_2, pipes___bird_1_out_5,
       pipes___bird_1_out_6, pipes___bird_1_out_7, pipes___bird_1_out_8, pipes___bird_1_out_9,
       pipes___bird_1_out_10, pipes___bird_1_out_11, pipes___bird_1_out_12, pipes___bird_1_out_13,
       pipes___bird_1_out_14, pipes___bird_1_out_15, pipes___bird_1_out_16, pipes___bird_1_out_17,
       pipes___bird_1_out_18, pipes___bird_1_out_19, pipes___bird_1_out_20, pipes___bird_1_out_21,
       pipes___bird_1_out_22, pipes___bird_1_out_23, pipes___bird_1_out_24, pipes___bird_1_out_25,
       pipes___bird_1_out_26, pipes___bird_1_out_27, pipes___bird_1_out_28, pipes___bird_1_out_29,
       pipes___bird_1_out_30, pipes___bird_1_out_31, pipes___bird_1_out_32, pipes___bird_1_out_33,
       pipes___bird_1_out_34, pipes___bird_1_out_35, pipes___bird_1_out_36, pipes___bird_1_pipe_2,
       pipes___bird_2_bird_1_2, pipes___bird_2_bird_2_2, pipes___bird_2_out_5, pipes___bird_2_out_6,
       pipes___bird_2_out_7, pipes___bird_2_out_8, pipes___bird_2_out_9, pipes___bird_2_out_10,
       pipes___bird_2_out_11, pipes___bird_2_out_12, pipes___bird_2_out_13, pipes___bird_2_out_14,
       pipes___bird_2_out_15, pipes___bird_2_out_16, pipes___bird_2_out_17, pipes___bird_2_out_18,
       pipes___bird_2_out_19, pipes___bird_2_out_20, pipes___bird_2_out_21, pipes___bird_2_out_22,
       pipes___bird_2_out_23, pipes___bird_2_out_24, pipes___bird_2_out_25, pipes___bird_2_out_26,
       pipes___bird_2_out_27, pipes___bird_2_out_28, pipes___bird_2_out_29, pipes___bird_2_out_30,
       pipes___bird_2_out_31, pipes___bird_2_out_32, pipes___bird_2_out_33, pipes___bird_2_out_34,
       pipes___bird_2_out_35, pipes___bird_2_out_36, pipes___bird_2_pipe_2, pipes___bird_3_bird_1_2,
       pipes___bird_3_bird_2_2, pipes___bird_3_out_5, pipes___bird_3_out_6, pipes___bird_3_out_7,
       pipes___bird_3_out_8, pipes___bird_3_out_9, pipes___bird_3_out_10, pipes___bird_3_out_11,
       pipes___bird_3_out_12, pipes___bird_3_out_13, pipes___bird_3_out_14, pipes___bird_3_out_15,
       pipes___bird_3_out_16, pipes___bird_3_out_17, pipes___bird_3_out_18, pipes___bird_3_out_19,
       pipes___bird_3_out_20, pipes___bird_3_out_21, pipes___bird_3_out_22, pipes___bird_3_out_23,
       pipes___bird_3_out_24, pipes___bird_3_out_25, pipes___bird_3_out_26, pipes___bird_3_out_27,
       pipes___bird_3_out_28, pipes___bird_3_out_29, pipes___bird_3_out_30, pipes___bird_3_out_31,
       pipes___bird_3_out_32, pipes___bird_3_out_33, pipes___bird_3_out_34, pipes___bird_3_out_35,
       pipes___bird_3_out_36, pipes___bird_3_pipe_2, pipes___bird_4_bird_1_2, pipes___bird_4_bird_2_2,
       pipes___bird_4_out_5, pipes___bird_4_out_6, pipes___bird_4_out_7, pipes___bird_4_out_8,
       pipes___bird_4_out_9, pipes___bird_4_out_10, pipes___bird_4_out_11, pipes___bird_4_out_12,
       pipes___bird_4_out_13, pipes___bird_4_out_14, pipes___bird_4_out_15, pipes___bird_4_out_16,
       pipes___bird_4_out_17, pipes___bird_4_out_18, pipes___bird_4_out_19, pipes___bird_4_out_20,
       pipes___bird_4_out_21, pipes___bird_4_out_22, pipes___bird_4_out_23, pipes___bird_4_out_24,
       pipes___bird_4_out_25, pipes___bird_4_out_26, pipes___bird_4_out_27, pipes___bird_4_out_28,
       pipes___bird_4_out_29, pipes___bird_4_out_30, pipes___bird_4_out_31, pipes___bird_4_out_32,
       pipes___bird_4_out_33, pipes___bird_4_out_34, pipes___bird_4_out_35, pipes___bird_4_out_36,
       pipes___bird_4_pipe_2, pipes___bird_5_bird_1_2, pipes___bird_5_bird_2_2, pipes___bird_5_out_5,
       pipes___bird_5_out_6, pipes___bird_5_out_7, pipes___bird_5_out_8, pipes___bird_5_out_9,
       pipes___bird_5_out_10, pipes___bird_5_out_11, pipes___bird_5_out_12, pipes___bird_5_out_13,
       pipes___bird_5_out_14, pipes___bird_5_out_15, pipes___bird_5_out_16, pipes___bird_5_out_17,
       pipes___bird_5_out_18, pipes___bird_5_out_19, pipes___bird_5_out_20, pipes___bird_5_out_21,
       pipes___bird_5_out_22, pipes___bird_5_out_23, pipes___bird_5_out_24, pipes___bird_5_out_25,
       pipes___bird_5_out_26, pipes___bird_5_out_27, pipes___bird_5_out_28, pipes___bird_5_out_29,
       pipes___bird_5_out_30, pipes___bird_5_out_31, pipes___bird_5_out_32, pipes___bird_5_out_33,
       pipes___bird_5_out_34, pipes___bird_5_out_35, pipes___bird_5_out_36, pipes___bird_5_pipe_2,
       pipes___bird_6_bird_1_2, pipes___bird_6_bird_2_2, pipes___bird_6_out_5, pipes___bird_6_out_6,
       pipes___bird_6_out_7, pipes___bird_6_out_8, pipes___bird_6_out_9, pipes___bird_6_out_10,
       pipes___bird_6_out_11, pipes___bird_6_out_12, pipes___bird_6_out_13, pipes___bird_6_out_14,
       pipes___bird_6_out_15, pipes___bird_6_out_16, pipes___bird_6_out_17, pipes___bird_6_out_18,
       pipes___bird_6_out_19, pipes___bird_6_out_20, pipes___bird_6_out_21, pipes___bird_6_out_22,
       pipes___bird_6_out_23, pipes___bird_6_out_24, pipes___bird_6_out_25, pipes___bird_6_out_26,
       pipes___bird_6_out_27, pipes___bird_6_out_28, pipes___bird_6_out_29, pipes___bird_6_out_30,
       pipes___bird_6_out_31, pipes___bird_6_out_32, pipes___bird_6_out_33, pipes___bird_6_out_34,
       pipes___bird_6_out_35, pipes___bird_6_out_36, pipes___bird_6_pipe_2, pipes___bird_7_bird_1_2,
       pipes___bird_7_bird_2_2, pipes___bird_7_out_5, pipes___bird_7_out_6, pipes___bird_7_out_7,
       pipes___bird_7_out_8, pipes___bird_7_out_9, pipes___bird_7_out_10, pipes___bird_7_out_11,
       pipes___bird_7_out_12, pipes___bird_7_out_13, pipes___bird_7_out_14, pipes___bird_7_out_15,
       pipes___bird_7_out_16, pipes___bird_7_out_17, pipes___bird_7_out_18, pipes___bird_7_out_19,
       pipes___bird_7_out_20, pipes___bird_7_out_21, pipes___bird_7_out_22, pipes___bird_7_out_23,
       pipes___bird_7_out_24, pipes___bird_7_out_25, pipes___bird_7_out_26, pipes___bird_7_out_27,
       pipes___bird_7_out_28, pipes___bird_7_out_29, pipes___bird_7_out_30, pipes___bird_7_out_31,
       pipes___bird_7_out_32, pipes___bird_7_out_33, pipes___bird_7_out_34, pipes___bird_7_out_35,
       pipes___bird_7_out_36, pipes___bird_7_pipe_2, pipes___bird_8_bird_1_2, pipes___bird_8_bird_2_2,
       pipes___bird_8_out_5, pipes___bird_8_out_6, pipes___bird_8_out_7, pipes___bird_8_out_8,
       pipes___bird_8_out_9, pipes___bird_8_out_10, pipes___bird_8_out_11, pipes___bird_8_out_12,
       pipes___bird_8_out_13, pipes___bird_8_out_14, pipes___bird_8_out_15, pipes___bird_8_out_16,
       pipes___bird_8_out_17, pipes___bird_8_out_18, pipes___bird_8_out_19, pipes___bird_8_out_20,
       pipes___bird_8_out_21, pipes___bird_8_out_22, pipes___bird_8_out_23, pipes___bird_8_out_24,
       pipes___bird_8_out_25, pipes___bird_8_out_26, pipes___bird_8_out_27, pipes___bird_8_out_28,
       pipes___bird_8_out_29, pipes___bird_8_out_30, pipes___bird_8_out_31, pipes___bird_8_out_32,
       pipes___bird_8_out_33, pipes___bird_8_out_34, pipes___bird_8_out_35, pipes___bird_8_out_36,
       pipes___bird_8_pipe_2, pipes___bird_9_bird_1_2, pipes___bird_9_bird_2_2, pipes___bird_9_out_5,
       pipes___bird_9_out_6, pipes___bird_9_out_7, pipes___bird_9_out_8, pipes___bird_9_out_9,
       pipes___bird_9_out_10, pipes___bird_9_out_11, pipes___bird_9_out_12, pipes___bird_9_out_13,
       pipes___bird_9_out_14, pipes___bird_9_out_15, pipes___bird_9_out_16, pipes___bird_9_out_17,
       pipes___bird_9_out_18, pipes___bird_9_out_19, pipes___bird_9_out_20, pipes___bird_9_out_21,
       pipes___bird_9_out_22, pipes___bird_9_out_23, pipes___bird_9_out_24, pipes___bird_9_out_25,
       pipes___bird_9_out_26, pipes___bird_9_out_27, pipes___bird_9_out_28, pipes___bird_9_out_29,
       pipes___bird_9_out_30, pipes___bird_9_out_31, pipes___bird_9_out_32, pipes___bird_9_out_33,
       pipes___bird_9_out_34, pipes___bird_9_out_35, pipes___bird_9_out_36, pipes___bird_9_pipe_2,
       pipes___bird_10_bird_1_2, pipes___bird_10_bird_2_2, pipes___bird_10_out_5, pipes___bird_10_out_6,
       pipes___bird_10_out_7, pipes___bird_10_out_8, pipes___bird_10_out_9, pipes___bird_10_out_10,
       pipes___bird_10_out_11, pipes___bird_10_out_12, pipes___bird_10_out_13, pipes___bird_10_out_14,
       pipes___bird_10_out_15, pipes___bird_10_out_16, pipes___bird_10_out_17, pipes___bird_10_out_18,
       pipes___bird_10_out_19, pipes___bird_10_out_20, pipes___bird_10_out_21, pipes___bird_10_out_22,
       pipes___bird_10_out_23, pipes___bird_10_out_24, pipes___bird_10_out_25, pipes___bird_10_out_26,
       pipes___bird_10_out_27, pipes___bird_10_out_28, pipes___bird_10_out_29, pipes___bird_10_out_30,
       pipes___bird_10_out_31, pipes___bird_10_out_32, pipes___bird_10_out_33, pipes___bird_10_out_34,
       pipes___bird_10_out_35, pipes___bird_10_out_36, pipes___bird_10_pipe_2, pipes___bird_11_bird_1_2,
       pipes___bird_11_bird_2_2, pipes___bird_11_out_5, pipes___bird_11_out_6, pipes___bird_11_out_7,
       pipes___bird_11_out_8, pipes___bird_11_out_9, pipes___bird_11_out_10, pipes___bird_11_out_11,
       pipes___bird_11_out_12, pipes___bird_11_out_13, pipes___bird_11_out_14, pipes___bird_11_out_15,
       pipes___bird_11_out_16, pipes___bird_11_out_17, pipes___bird_11_out_18, pipes___bird_11_out_19,
       pipes___bird_11_out_20, pipes___bird_11_out_21, pipes___bird_11_out_22, pipes___bird_11_out_23,
       pipes___bird_11_out_24, pipes___bird_11_out_25, pipes___bird_11_out_26, pipes___bird_11_out_27,
       pipes___bird_11_out_28, pipes___bird_11_out_29, pipes___bird_11_out_30, pipes___bird_11_out_31,
       pipes___bird_11_out_32, pipes___bird_11_out_33, pipes___bird_11_out_34, pipes___bird_11_out_35,
       pipes___bird_11_out_36, pipes___bird_11_pipe_2, pipes___bird_12_bird_1_2, pipes___bird_12_bird_2_2,
       pipes___bird_12_out_5, pipes___bird_12_out_6, pipes___bird_12_out_7, pipes___bird_12_out_8,
       pipes___bird_12_out_9, pipes___bird_12_out_10, pipes___bird_12_out_11, pipes___bird_12_out_12,
       pipes___bird_12_out_13, pipes___bird_12_out_14, pipes___bird_12_out_15, pipes___bird_12_out_16,
       pipes___bird_12_out_17, pipes___bird_12_out_18, pipes___bird_12_out_19, pipes___bird_12_out_20,
       pipes___bird_12_out_21, pipes___bird_12_out_22, pipes___bird_12_out_23, pipes___bird_12_out_24,
       pipes___bird_12_out_25, pipes___bird_12_out_26, pipes___bird_12_out_27, pipes___bird_12_out_28,
       pipes___bird_12_out_29, pipes___bird_12_out_30, pipes___bird_12_out_31, pipes___bird_12_out_32,
       pipes___bird_12_out_33, pipes___bird_12_out_34, pipes___bird_12_out_35, pipes___bird_12_out_36,
       pipes___bird_12_pipe_2, plus_1, \индикаторы_1_out_3 , \индикаторы_1_out_4 , \индикаторы_1_out_5 ,
       \индикаторы_1_out_6 , \индикаторы_1_out_7 , \индикаторы_1_out_8 , \индикаторы_1_out_9 ,
       \индикаторы_1_out_10 , \индикаторы_1_out_11 , \индикаторы_1_out_12 , \индикаторы_1_out_13 ,
       \индикаторы_1_out_14 , \индикаторы_1_out_15 , \индикаторы_1_out_16 , \индикаторы_1_out_17 ,
       \индикаторы_1_out_18 , \индикаторы_1_out_19 , \индикаторы_1_out_20 , \индикаторы_1_out_21 ,
       \индикаторы_1_out_22 , \индикаторы_1_out_23 , \индикаторы_1_out_24 , \индикаторы_1_out_25 ,
       \индикаторы_1_out_26 , \индикаторы_1_out_27 , \индикаторы_1_out_28 , \индикаторы_1_out_29 ,
       \индикаторы_1_out_30 , \индикаторы_1_out_31 , \индикаторы_1_out_32 , \индикаторы_1_out_33 ,
       \индикаторы_1_out_34 , \индикаторы_1_out_35 , \индикаторы_1_out_36 , \индикаторы_1_out_37 ,
       \индикаторы_1_out_38 , \индикаторы_1_out_39 , \индикаторы_1_out_40 , \индикаторы_1_out_41 ,
       \индикаторы_1_out_42 , \индикаторы_1_out_43 , \индикаторы_1_out_44 , \индикаторы_1_out_45 ,
       \индикаторы_1_out_46 , \индикаторы_1_out_47 , \индикаторы_1_out_48 , \индикаторы_1_out_49 ,
       \индикаторы_1_out_50 , \индикаторы_1_out_51 , \индикаторы_1_out_52 , \индикаторы_1_out_53 ,
       \индикаторы_1_out_54 , \индикаторы_1_out_55 , \индикаторы_1_out_56 , \индикаторы_1_out_57 ,
       \индикаторы_1_out_58 , \индикаторы_1_out_59 , \индикаторы_1_out_60 , \индикаторы_1_out_61 ,
       \индикаторы_1_out_62 , \индикаторы_1_out_63 , \индикаторы_1_out_64 , \индикаторы_1_out_65 ,
       \индикаторы_1_out_66 , \индикаторы_1_out_67 , \индикаторы_1_out_68 , \индикаторы_1_out_69 ,
       \индикаторы_1_out_70 , \индикаторы_1_out_71 , \индикаторы_1_out_72 , \индикаторы_1_out_73 ,
       \индикаторы_1_out_74 , \индикаторы_1_out_75 , \индикаторы_1_out_76 , \индикаторы_1_out_77 ,
       \индикаторы_1_out_78 , \индикаторы_1_out_79 , \индикаторы_1_out_80 , \индикаторы_1_out_81 ,
       \индикаторы_1_out_82 , \индикаторы_1_out_83 , \индикаторы_1_out_84 , \индикаторы_1_out_85 ,
       \индикаторы_1_out_86 , \индикаторы_1_out_87 , \индикаторы_1_out_88 , \индикаторы_1_out_89 ,
       \индикаторы_1_out_90 , \индикаторы_1_out_91 , \индикаторы_1_out_92 , \индикаторы_1_out_93 ,
       \индикаторы_1_out_94 , \индикаторы_1_out_95 , \индикаторы_1_out_96 , \индикаторы_1_out_97 ,
       \индикаторы_1_out_98 , \индикаторы_1_out_99 , \индикаторы_1_out_100 , \индикаторы_1_out_101 ,
       \индикаторы_1_out_102 , \индикаторы_1_out_103 , \индикаторы_1_out_104 , \индикаторы_1_out_105 ,
       \индикаторы_1_out_106 , \индикаторы_1_out_107 , \индикаторы_1_out_108 , \индикаторы_1_out_109 ,
       \индикаторы_1_out_110 , \индикаторы_1_out_111 , \индикаторы_1_out_112 , \индикаторы_1_out_113 ,
       \индикаторы_1_out_114 , \индикаторы_1_out_115 , \индикаторы_1_out_116 , \индикаторы_1_out_117 ,
       \индикаторы_1_out_118 , \индикаторы_1_out_119 , \индикаторы_1_out_120 , \индикаторы_1_out_121 ,
       \индикаторы_1_out_122 ;

  DotMatrix #(.matrixcols(32), .matrixrows(32)) dotmatrix_1 (
    .col0(pipes_1_out_5), .col1(pipes_1_out_6), .col2(pipes_1_out_7), .col3(pipes_1_out_8),
    .col4(pipes_1_out_9), .col5(pipes_1_out_10), .col6(pipes_1_out_11), .col7(pipes_1_out_12),
    .col8(pipes_1_out_13), .col9(pipes_1_out_14), .col10(pipes_1_out_15), .col11(pipes_1_out_16),
    .col12(pipes_1_out_17), .col13(pipes_1_out_18), .col14(pipes_1_out_19), .col15(pipes_1_out_20),
    .col16(pipes_1_out_21), .col17(pipes_1_out_22), .col18(pipes_1_out_23), .col19(pipes_1_out_24),
    .col20(pipes_1_out_25), .col21(pipes_1_out_26), .col22(pipes_1_out_27), .col23(pipes_1_out_28),
    .col24(pipes_1_out_29), .col25(pipes_1_out_30), .col26(pipes_1_out_31), .col27(pipes_1_out_32),
    .col28(pipes_1_out_33), .col29(pipes_1_out_34), .col30(pipes_1_out_35), .col31(pipes_1_out_36));
  pipes pipes_1 (
    .out_5(pipes_1_out_5), .out_6(pipes_1_out_6), .out_7(pipes_1_out_7), .out_8(pipes_1_out_8),
    .out_9(pipes_1_out_9), .out_10(pipes_1_out_10), .out_11(pipes_1_out_11), .out_12(pipes_1_out_12),
    .out_13(pipes_1_out_13), .out_14(pipes_1_out_14), .out_15(pipes_1_out_15), .out_16(pipes_1_out_16),
    .out_17(pipes_1_out_17), .out_18(pipes_1_out_18), .out_19(pipes_1_out_19), .out_20(pipes_1_out_20),
    .out_21(pipes_1_out_21), .out_22(pipes_1_out_22), .out_23(pipes_1_out_23), .out_24(pipes_1_out_24),
    .out_25(pipes_1_out_25), .out_26(pipes_1_out_26), .out_27(pipes_1_out_27), .out_28(pipes_1_out_28),
    .out_29(pipes_1_out_29), .out_30(pipes_1_out_30), .out_31(pipes_1_out_31), .out_32(pipes_1_out_32),
    .out_33(pipes_1_out_33), .out_34(pipes_1_out_34), .out_35(pipes_1_out_35), .out_36(pipes_1_out_36),
    .pipe(pipes_13_pipe_2), .signal(pipes_13_signal_2), .signal_2(s12), .bird_1(pipes_13_bird_1_2),
    .bird_2(pipes_13_bird));  // open: pipe_2, bird_1_2, bird
  DotMatrix #(.matrixcols(32), .matrixrows(32)) dotmatrix_2 (
    .col0(pipes_2_out_5), .col1(pipes_2_out_6), .col2(pipes_2_out_7), .col3(pipes_2_out_8),
    .col4(pipes_2_out_9), .col5(pipes_2_out_10), .col6(pipes_2_out_11), .col7(pipes_2_out_12),
    .col8(pipes_2_out_13), .col9(pipes_2_out_14), .col10(pipes_2_out_15), .col11(pipes_2_out_16),
    .col12(pipes_2_out_17), .col13(pipes_2_out_18), .col14(pipes_2_out_19), .col15(pipes_2_out_20),
    .col16(pipes_2_out_21), .col17(pipes_2_out_22), .col18(pipes_2_out_23), .col19(pipes_2_out_24),
    .col20(pipes_2_out_25), .col21(pipes_2_out_26), .col22(pipes_2_out_27), .col23(pipes_2_out_28),
    .col24(pipes_2_out_29), .col25(pipes_2_out_30), .col26(pipes_2_out_31), .col27(pipes_2_out_32),
    .col28(pipes_2_out_33), .col29(pipes_2_out_34), .col30(pipes_2_out_35), .col31(pipes_2_out_36));
  pipes pipes_2 (
    .out_5(pipes_2_out_5), .out_6(pipes_2_out_6), .out_7(pipes_2_out_7), .out_8(pipes_2_out_8),
    .out_9(pipes_2_out_9), .out_10(pipes_2_out_10), .out_11(pipes_2_out_11), .out_12(pipes_2_out_12),
    .out_13(pipes_2_out_13), .out_14(pipes_2_out_14), .out_15(pipes_2_out_15), .out_16(pipes_2_out_16),
    .out_17(pipes_2_out_17), .out_18(pipes_2_out_18), .out_19(pipes_2_out_19), .out_20(pipes_2_out_20),
    .out_21(pipes_2_out_21), .out_22(pipes_2_out_22), .out_23(pipes_2_out_23), .out_24(pipes_2_out_24),
    .out_25(pipes_2_out_25), .out_26(pipes_2_out_26), .out_27(pipes_2_out_27), .out_28(pipes_2_out_28),
    .out_29(pipes_2_out_29), .out_30(pipes_2_out_30), .out_31(pipes_2_out_31), .out_32(pipes_2_out_32),
    .out_33(pipes_2_out_33), .out_34(pipes_2_out_34), .out_35(pipes_2_out_35), .out_36(pipes_2_out_36),
    .pipe(pipes_14_pipe_2), .signal(pipes_14_signal_2), .signal_2(s11), .bird_1(pipes_14_bird_1_2),
    .bird_2(pipes_14_bird));  // open: pipe_2, bird_1_2, bird
  pipes pipes_3 (
    .out_5(pipes_3_out_5), .out_6(pipes_3_out_6), .out_7(pipes_3_out_7), .out_8(pipes_3_out_8),
    .out_9(pipes_3_out_9), .out_10(pipes_3_out_10), .out_11(pipes_3_out_11), .out_12(pipes_3_out_12),
    .out_13(pipes_3_out_13), .out_14(pipes_3_out_14), .out_15(pipes_3_out_15), .out_16(pipes_3_out_16),
    .out_17(pipes_3_out_17), .out_18(pipes_3_out_18), .out_19(pipes_3_out_19), .out_20(pipes_3_out_20),
    .out_21(pipes_3_out_21), .out_22(pipes_3_out_22), .out_23(pipes_3_out_23), .out_24(pipes_3_out_24),
    .out_25(pipes_3_out_25), .out_26(pipes_3_out_26), .out_27(pipes_3_out_27), .out_28(pipes_3_out_28),
    .out_29(pipes_3_out_29), .out_30(pipes_3_out_30), .out_31(pipes_3_out_31), .out_32(pipes_3_out_32),
    .out_33(pipes_3_out_33), .out_34(pipes_3_out_34), .out_35(pipes_3_out_35), .out_36(pipes_3_out_36),
    .pipe(pipes_15_pipe_2), .signal(pipes_15_signal_2), .signal_2(s10), .bird_1(pipes_15_bird_1_2),
    .bird_2(pipes_15_bird));  // open: pipe_2, bird_1_2, bird
  DotMatrix #(.matrixcols(32), .matrixrows(32)) dotmatrix_3 (
    .col0(pipes_3_out_5), .col1(pipes_3_out_6), .col2(pipes_3_out_7), .col3(pipes_3_out_8),
    .col4(pipes_3_out_9), .col5(pipes_3_out_10), .col6(pipes_3_out_11), .col7(pipes_3_out_12),
    .col8(pipes_3_out_13), .col9(pipes_3_out_14), .col10(pipes_3_out_15), .col11(pipes_3_out_16),
    .col12(pipes_3_out_17), .col13(pipes_3_out_18), .col14(pipes_3_out_19), .col15(pipes_3_out_20),
    .col16(pipes_3_out_21), .col17(pipes_3_out_22), .col18(pipes_3_out_23), .col19(pipes_3_out_24),
    .col20(pipes_3_out_25), .col21(pipes_3_out_26), .col22(pipes_3_out_27), .col23(pipes_3_out_28),
    .col24(pipes_3_out_29), .col25(pipes_3_out_30), .col26(pipes_3_out_31), .col27(pipes_3_out_32),
    .col28(pipes_3_out_33), .col29(pipes_3_out_34), .col30(pipes_3_out_35), .col31(pipes_3_out_36));
  pipes pipes_4 (
    .out_5(pipes_4_out_5), .out_6(pipes_4_out_6), .out_7(pipes_4_out_7), .out_8(pipes_4_out_8),
    .out_9(pipes_4_out_9), .out_10(pipes_4_out_10), .out_11(pipes_4_out_11), .out_12(pipes_4_out_12),
    .out_13(pipes_4_out_13), .out_14(pipes_4_out_14), .out_15(pipes_4_out_15), .out_16(pipes_4_out_16),
    .out_17(pipes_4_out_17), .out_18(pipes_4_out_18), .out_19(pipes_4_out_19), .out_20(pipes_4_out_20),
    .out_21(pipes_4_out_21), .out_22(pipes_4_out_22), .out_23(pipes_4_out_23), .out_24(pipes_4_out_24),
    .out_25(pipes_4_out_25), .out_26(pipes_4_out_26), .out_27(pipes_4_out_27), .out_28(pipes_4_out_28),
    .out_29(pipes_4_out_29), .out_30(pipes_4_out_30), .out_31(pipes_4_out_31), .out_32(pipes_4_out_32),
    .out_33(pipes_4_out_33), .out_34(pipes_4_out_34), .out_35(pipes_4_out_35), .out_36(pipes_4_out_36),
    .pipe(pipes_16_pipe_2), .signal(pipes_16_signal_2), .signal_2(s9), .bird_1(pipes_16_bird_1_2),
    .bird_2(pipes_16_bird));  // open: pipe_2, bird_1_2, bird
  DotMatrix #(.matrixcols(32), .matrixrows(32)) dotmatrix_4 (
    .col0(pipes_4_out_5), .col1(pipes_4_out_6), .col2(pipes_4_out_7), .col3(pipes_4_out_8),
    .col4(pipes_4_out_9), .col5(pipes_4_out_10), .col6(pipes_4_out_11), .col7(pipes_4_out_12),
    .col8(pipes_4_out_13), .col9(pipes_4_out_14), .col10(pipes_4_out_15), .col11(pipes_4_out_16),
    .col12(pipes_4_out_17), .col13(pipes_4_out_18), .col14(pipes_4_out_19), .col15(pipes_4_out_20),
    .col16(pipes_4_out_21), .col17(pipes_4_out_22), .col18(pipes_4_out_23), .col19(pipes_4_out_24),
    .col20(pipes_4_out_25), .col21(pipes_4_out_26), .col22(pipes_4_out_27), .col23(pipes_4_out_28),
    .col24(pipes_4_out_29), .col25(pipes_4_out_30), .col26(pipes_4_out_31), .col27(pipes_4_out_32),
    .col28(pipes_4_out_33), .col29(pipes_4_out_34), .col30(pipes_4_out_35), .col31(pipes_4_out_36));
  pipes pipes_5 (
    .out_5(pipes_5_out_5), .out_6(pipes_5_out_6), .out_7(pipes_5_out_7), .out_8(pipes_5_out_8),
    .out_9(pipes_5_out_9), .out_10(pipes_5_out_10), .out_11(pipes_5_out_11), .out_12(pipes_5_out_12),
    .out_13(pipes_5_out_13), .out_14(pipes_5_out_14), .out_15(pipes_5_out_15), .out_16(pipes_5_out_16),
    .out_17(pipes_5_out_17), .out_18(pipes_5_out_18), .out_19(pipes_5_out_19), .out_20(pipes_5_out_20),
    .out_21(pipes_5_out_21), .out_22(pipes_5_out_22), .out_23(pipes_5_out_23), .out_24(pipes_5_out_24),
    .out_25(pipes_5_out_25), .out_26(pipes_5_out_26), .out_27(pipes_5_out_27), .out_28(pipes_5_out_28),
    .out_29(pipes_5_out_29), .out_30(pipes_5_out_30), .out_31(pipes_5_out_31), .out_32(pipes_5_out_32),
    .out_33(pipes_5_out_33), .out_34(pipes_5_out_34), .out_35(pipes_5_out_35), .out_36(pipes_5_out_36),
    .pipe(pipes_17_pipe_2), .signal(pipes_17_signal_2), .signal_2(s8), .bird_1(pipes_17_bird_1_2),
    .bird_2(pipes_17_bird));  // open: pipe_2, bird_1_2, bird
  DotMatrix #(.matrixcols(32), .matrixrows(32)) dotmatrix_5 (
    .col0(pipes_5_out_5), .col1(pipes_5_out_6), .col2(pipes_5_out_7), .col3(pipes_5_out_8),
    .col4(pipes_5_out_9), .col5(pipes_5_out_10), .col6(pipes_5_out_11), .col7(pipes_5_out_12),
    .col8(pipes_5_out_13), .col9(pipes_5_out_14), .col10(pipes_5_out_15), .col11(pipes_5_out_16),
    .col12(pipes_5_out_17), .col13(pipes_5_out_18), .col14(pipes_5_out_19), .col15(pipes_5_out_20),
    .col16(pipes_5_out_21), .col17(pipes_5_out_22), .col18(pipes_5_out_23), .col19(pipes_5_out_24),
    .col20(pipes_5_out_25), .col21(pipes_5_out_26), .col22(pipes_5_out_27), .col23(pipes_5_out_28),
    .col24(pipes_5_out_29), .col25(pipes_5_out_30), .col26(pipes_5_out_31), .col27(pipes_5_out_32),
    .col28(pipes_5_out_33), .col29(pipes_5_out_34), .col30(pipes_5_out_35), .col31(pipes_5_out_36));
  pipes pipes_6 (
    .out_5(pipes_6_out_5), .out_6(pipes_6_out_6), .out_7(pipes_6_out_7), .out_8(pipes_6_out_8),
    .out_9(pipes_6_out_9), .out_10(pipes_6_out_10), .out_11(pipes_6_out_11), .out_12(pipes_6_out_12),
    .out_13(pipes_6_out_13), .out_14(pipes_6_out_14), .out_15(pipes_6_out_15), .out_16(pipes_6_out_16),
    .out_17(pipes_6_out_17), .out_18(pipes_6_out_18), .out_19(pipes_6_out_19), .out_20(pipes_6_out_20),
    .out_21(pipes_6_out_21), .out_22(pipes_6_out_22), .out_23(pipes_6_out_23), .out_24(pipes_6_out_24),
    .out_25(pipes_6_out_25), .out_26(pipes_6_out_26), .out_27(pipes_6_out_27), .out_28(pipes_6_out_28),
    .out_29(pipes_6_out_29), .out_30(pipes_6_out_30), .out_31(pipes_6_out_31), .out_32(pipes_6_out_32),
    .out_33(pipes_6_out_33), .out_34(pipes_6_out_34), .out_35(pipes_6_out_35), .out_36(pipes_6_out_36),
    .pipe(pipes_18_pipe_2), .signal(pipes_18_signal_2), .signal_2(s7), .bird_1(pipes_18_bird_1_2),
    .bird_2(pipes_18_bird));  // open: pipe_2, bird_1_2, bird
  DotMatrix #(.matrixcols(32), .matrixrows(32)) dotmatrix_6 (
    .col0(pipes_6_out_5), .col1(pipes_6_out_6), .col2(pipes_6_out_7), .col3(pipes_6_out_8),
    .col4(pipes_6_out_9), .col5(pipes_6_out_10), .col6(pipes_6_out_11), .col7(pipes_6_out_12),
    .col8(pipes_6_out_13), .col9(pipes_6_out_14), .col10(pipes_6_out_15), .col11(pipes_6_out_16),
    .col12(pipes_6_out_17), .col13(pipes_6_out_18), .col14(pipes_6_out_19), .col15(pipes_6_out_20),
    .col16(pipes_6_out_21), .col17(pipes_6_out_22), .col18(pipes_6_out_23), .col19(pipes_6_out_24),
    .col20(pipes_6_out_25), .col21(pipes_6_out_26), .col22(pipes_6_out_27), .col23(pipes_6_out_28),
    .col24(pipes_6_out_29), .col25(pipes_6_out_30), .col26(pipes_6_out_31), .col27(pipes_6_out_32),
    .col28(pipes_6_out_33), .col29(pipes_6_out_34), .col30(pipes_6_out_35), .col31(pipes_6_out_36));
  pipes pipes_7 (
    .out_5(pipes_7_out_5), .out_6(pipes_7_out_6), .out_7(pipes_7_out_7), .out_8(pipes_7_out_8),
    .out_9(pipes_7_out_9), .out_10(pipes_7_out_10), .out_11(pipes_7_out_11), .out_12(pipes_7_out_12),
    .out_13(pipes_7_out_13), .out_14(pipes_7_out_14), .out_15(pipes_7_out_15), .out_16(pipes_7_out_16),
    .out_17(pipes_7_out_17), .out_18(pipes_7_out_18), .out_19(pipes_7_out_19), .out_20(pipes_7_out_20),
    .out_21(pipes_7_out_21), .out_22(pipes_7_out_22), .out_23(pipes_7_out_23), .out_24(pipes_7_out_24),
    .out_25(pipes_7_out_25), .out_26(pipes_7_out_26), .out_27(pipes_7_out_27), .out_28(pipes_7_out_28),
    .out_29(pipes_7_out_29), .out_30(pipes_7_out_30), .out_31(pipes_7_out_31), .out_32(pipes_7_out_32),
    .out_33(pipes_7_out_33), .out_34(pipes_7_out_34), .out_35(pipes_7_out_35), .out_36(pipes_7_out_36),
    .pipe(pipes_19_pipe_2), .signal(pipes_19_signal_2), .signal_2(s6), .bird_1(pipes_19_bird_1_2),
    .bird_2(pipes_19_bird));  // open: pipe_2, bird_1_2, bird
  DotMatrix #(.matrixcols(32), .matrixrows(32)) dotmatrix_7 (
    .col0(pipes_7_out_5), .col1(pipes_7_out_6), .col2(pipes_7_out_7), .col3(pipes_7_out_8),
    .col4(pipes_7_out_9), .col5(pipes_7_out_10), .col6(pipes_7_out_11), .col7(pipes_7_out_12),
    .col8(pipes_7_out_13), .col9(pipes_7_out_14), .col10(pipes_7_out_15), .col11(pipes_7_out_16),
    .col12(pipes_7_out_17), .col13(pipes_7_out_18), .col14(pipes_7_out_19), .col15(pipes_7_out_20),
    .col16(pipes_7_out_21), .col17(pipes_7_out_22), .col18(pipes_7_out_23), .col19(pipes_7_out_24),
    .col20(pipes_7_out_25), .col21(pipes_7_out_26), .col22(pipes_7_out_27), .col23(pipes_7_out_28),
    .col24(pipes_7_out_29), .col25(pipes_7_out_30), .col26(pipes_7_out_31), .col27(pipes_7_out_32),
    .col28(pipes_7_out_33), .col29(pipes_7_out_34), .col30(pipes_7_out_35), .col31(pipes_7_out_36));
  pipes pipes_8 (
    .out_5(pipes_8_out_5), .out_6(pipes_8_out_6), .out_7(pipes_8_out_7), .out_8(pipes_8_out_8),
    .out_9(pipes_8_out_9), .out_10(pipes_8_out_10), .out_11(pipes_8_out_11), .out_12(pipes_8_out_12),
    .out_13(pipes_8_out_13), .out_14(pipes_8_out_14), .out_15(pipes_8_out_15), .out_16(pipes_8_out_16),
    .out_17(pipes_8_out_17), .out_18(pipes_8_out_18), .out_19(pipes_8_out_19), .out_20(pipes_8_out_20),
    .out_21(pipes_8_out_21), .out_22(pipes_8_out_22), .out_23(pipes_8_out_23), .out_24(pipes_8_out_24),
    .out_25(pipes_8_out_25), .out_26(pipes_8_out_26), .out_27(pipes_8_out_27), .out_28(pipes_8_out_28),
    .out_29(pipes_8_out_29), .out_30(pipes_8_out_30), .out_31(pipes_8_out_31), .out_32(pipes_8_out_32),
    .out_33(pipes_8_out_33), .out_34(pipes_8_out_34), .out_35(pipes_8_out_35), .out_36(pipes_8_out_36),
    .pipe(pipes_20_pipe_2), .signal(pipes_20_signal_2), .signal_2(s5), .bird_1(pipes_20_bird_1_2),
    .bird_2(pipes_20_bird));  // open: pipe_2, bird_1_2, bird
  DotMatrix #(.matrixcols(32), .matrixrows(32)) dotmatrix_8 (
    .col0(pipes_8_out_5), .col1(pipes_8_out_6), .col2(pipes_8_out_7), .col3(pipes_8_out_8),
    .col4(pipes_8_out_9), .col5(pipes_8_out_10), .col6(pipes_8_out_11), .col7(pipes_8_out_12),
    .col8(pipes_8_out_13), .col9(pipes_8_out_14), .col10(pipes_8_out_15), .col11(pipes_8_out_16),
    .col12(pipes_8_out_17), .col13(pipes_8_out_18), .col14(pipes_8_out_19), .col15(pipes_8_out_20),
    .col16(pipes_8_out_21), .col17(pipes_8_out_22), .col18(pipes_8_out_23), .col19(pipes_8_out_24),
    .col20(pipes_8_out_25), .col21(pipes_8_out_26), .col22(pipes_8_out_27), .col23(pipes_8_out_28),
    .col24(pipes_8_out_29), .col25(pipes_8_out_30), .col26(pipes_8_out_31), .col27(pipes_8_out_32),
    .col28(pipes_8_out_33), .col29(pipes_8_out_34), .col30(pipes_8_out_35), .col31(pipes_8_out_36));
  DotMatrix #(.matrixcols(32), .matrixrows(32)) dotmatrix_9 (
    .col0(pipes_9_out_5), .col1(pipes_9_out_6), .col2(pipes_9_out_7), .col3(pipes_9_out_8),
    .col4(pipes_9_out_9), .col5(pipes_9_out_10), .col6(pipes_9_out_11), .col7(pipes_9_out_12),
    .col8(pipes_9_out_13), .col9(pipes_9_out_14), .col10(pipes_9_out_15), .col11(pipes_9_out_16),
    .col12(pipes_9_out_17), .col13(pipes_9_out_18), .col14(pipes_9_out_19), .col15(pipes_9_out_20),
    .col16(pipes_9_out_21), .col17(pipes_9_out_22), .col18(pipes_9_out_23), .col19(pipes_9_out_24),
    .col20(pipes_9_out_25), .col21(pipes_9_out_26), .col22(pipes_9_out_27), .col23(pipes_9_out_28),
    .col24(pipes_9_out_29), .col25(pipes_9_out_30), .col26(pipes_9_out_31), .col27(pipes_9_out_32),
    .col28(pipes_9_out_33), .col29(pipes_9_out_34), .col30(pipes_9_out_35), .col31(pipes_9_out_36));
  pipes pipes_9 (
    .out_5(pipes_9_out_5), .out_6(pipes_9_out_6), .out_7(pipes_9_out_7), .out_8(pipes_9_out_8),
    .out_9(pipes_9_out_9), .out_10(pipes_9_out_10), .out_11(pipes_9_out_11), .out_12(pipes_9_out_12),
    .out_13(pipes_9_out_13), .out_14(pipes_9_out_14), .out_15(pipes_9_out_15), .out_16(pipes_9_out_16),
    .out_17(pipes_9_out_17), .out_18(pipes_9_out_18), .out_19(pipes_9_out_19), .out_20(pipes_9_out_20),
    .out_21(pipes_9_out_21), .out_22(pipes_9_out_22), .out_23(pipes_9_out_23), .out_24(pipes_9_out_24),
    .out_25(pipes_9_out_25), .out_26(pipes_9_out_26), .out_27(pipes_9_out_27), .out_28(pipes_9_out_28),
    .out_29(pipes_9_out_29), .out_30(pipes_9_out_30), .out_31(pipes_9_out_31), .out_32(pipes_9_out_32),
    .out_33(pipes_9_out_33), .out_34(pipes_9_out_34), .out_35(pipes_9_out_35), .out_36(pipes_9_out_36),
    .pipe(pipes_21_pipe_2), .signal(pipes_21_signal_2), .signal_2(s4), .bird_1(pipes_21_bird_1_2),
    .bird_2(pipes_21_bird));  // open: pipe_2, bird_1_2, bird
  pipes pipes_10 (
    .out_5(pipes_10_out_5), .out_6(pipes_10_out_6), .out_7(pipes_10_out_7), .out_8(pipes_10_out_8),
    .out_9(pipes_10_out_9), .out_10(pipes_10_out_10), .out_11(pipes_10_out_11), .out_12(pipes_10_out_12),
    .out_13(pipes_10_out_13), .out_14(pipes_10_out_14), .out_15(pipes_10_out_15), .out_16(pipes_10_out_16),
    .out_17(pipes_10_out_17), .out_18(pipes_10_out_18), .out_19(pipes_10_out_19), .out_20(pipes_10_out_20),
    .out_21(pipes_10_out_21), .out_22(pipes_10_out_22), .out_23(pipes_10_out_23), .out_24(pipes_10_out_24),
    .out_25(pipes_10_out_25), .out_26(pipes_10_out_26), .out_27(pipes_10_out_27), .out_28(pipes_10_out_28),
    .out_29(pipes_10_out_29), .out_30(pipes_10_out_30), .out_31(pipes_10_out_31), .out_32(pipes_10_out_32),
    .out_33(pipes_10_out_33), .out_34(pipes_10_out_34), .out_35(pipes_10_out_35), .out_36(pipes_10_out_36),
    .pipe(pipes_22_pipe_2), .signal(pipes_22_signal_2), .signal_2(s3), .bird_1(pipes_22_bird_1_2),
    .bird_2(pipes_22_bird));  // open: pipe_2, bird_1_2, bird
  DotMatrix #(.matrixcols(32), .matrixrows(32)) dotmatrix_10 (
    .col0(pipes_10_out_5), .col1(pipes_10_out_6), .col2(pipes_10_out_7), .col3(pipes_10_out_8),
    .col4(pipes_10_out_9), .col5(pipes_10_out_10), .col6(pipes_10_out_11), .col7(pipes_10_out_12),
    .col8(pipes_10_out_13), .col9(pipes_10_out_14), .col10(pipes_10_out_15), .col11(pipes_10_out_16),
    .col12(pipes_10_out_17), .col13(pipes_10_out_18), .col14(pipes_10_out_19), .col15(pipes_10_out_20),
    .col16(pipes_10_out_21), .col17(pipes_10_out_22), .col18(pipes_10_out_23), .col19(pipes_10_out_24),
    .col20(pipes_10_out_25), .col21(pipes_10_out_26), .col22(pipes_10_out_27), .col23(pipes_10_out_28),
    .col24(pipes_10_out_29), .col25(pipes_10_out_30), .col26(pipes_10_out_31), .col27(pipes_10_out_32),
    .col28(pipes_10_out_33), .col29(pipes_10_out_34), .col30(pipes_10_out_35), .col31(pipes_10_out_36));
  DotMatrix #(.matrixcols(32), .matrixrows(32)) dotmatrix_11 (
    .col0(pipes_11_out_5), .col1(pipes_11_out_6), .col2(pipes_11_out_7), .col3(pipes_11_out_8),
    .col4(pipes_11_out_9), .col5(pipes_11_out_10), .col6(pipes_11_out_11), .col7(pipes_11_out_12),
    .col8(pipes_11_out_13), .col9(pipes_11_out_14), .col10(pipes_11_out_15), .col11(pipes_11_out_16),
    .col12(pipes_11_out_17), .col13(pipes_11_out_18), .col14(pipes_11_out_19), .col15(pipes_11_out_20),
    .col16(pipes_11_out_21), .col17(pipes_11_out_22), .col18(pipes_11_out_23), .col19(pipes_11_out_24),
    .col20(pipes_11_out_25), .col21(pipes_11_out_26), .col22(pipes_11_out_27), .col23(pipes_11_out_28),
    .col24(pipes_11_out_29), .col25(pipes_11_out_30), .col26(pipes_11_out_31), .col27(pipes_11_out_32),
    .col28(pipes_11_out_33), .col29(pipes_11_out_34), .col30(pipes_11_out_35), .col31(pipes_11_out_36));
  pipes pipes_11 (
    .out_5(pipes_11_out_5), .out_6(pipes_11_out_6), .out_7(pipes_11_out_7), .out_8(pipes_11_out_8),
    .out_9(pipes_11_out_9), .out_10(pipes_11_out_10), .out_11(pipes_11_out_11), .out_12(pipes_11_out_12),
    .out_13(pipes_11_out_13), .out_14(pipes_11_out_14), .out_15(pipes_11_out_15), .out_16(pipes_11_out_16),
    .out_17(pipes_11_out_17), .out_18(pipes_11_out_18), .out_19(pipes_11_out_19), .out_20(pipes_11_out_20),
    .out_21(pipes_11_out_21), .out_22(pipes_11_out_22), .out_23(pipes_11_out_23), .out_24(pipes_11_out_24),
    .out_25(pipes_11_out_25), .out_26(pipes_11_out_26), .out_27(pipes_11_out_27), .out_28(pipes_11_out_28),
    .out_29(pipes_11_out_29), .out_30(pipes_11_out_30), .out_31(pipes_11_out_31), .out_32(pipes_11_out_32),
    .out_33(pipes_11_out_33), .out_34(pipes_11_out_34), .out_35(pipes_11_out_35), .out_36(pipes_11_out_36),
    .pipe(pipes_23_pipe_2), .signal(pipes_23_signal_2), .signal_2(s2), .bird_1(pipes_23_bird_1_2),
    .bird_2(pipes_23_bird));  // open: pipe_2, bird_1_2, bird
  pipes pipes_12 (
    .out_5(pipes_12_out_5), .out_6(pipes_12_out_6), .out_7(pipes_12_out_7), .out_8(pipes_12_out_8),
    .out_9(pipes_12_out_9), .out_10(pipes_12_out_10), .out_11(pipes_12_out_11), .out_12(pipes_12_out_12),
    .out_13(pipes_12_out_13), .out_14(pipes_12_out_14), .out_15(pipes_12_out_15), .out_16(pipes_12_out_16),
    .out_17(pipes_12_out_17), .out_18(pipes_12_out_18), .out_19(pipes_12_out_19), .out_20(pipes_12_out_20),
    .out_21(pipes_12_out_21), .out_22(pipes_12_out_22), .out_23(pipes_12_out_23), .out_24(pipes_12_out_24),
    .out_25(pipes_12_out_25), .out_26(pipes_12_out_26), .out_27(pipes_12_out_27), .out_28(pipes_12_out_28),
    .out_29(pipes_12_out_29), .out_30(pipes_12_out_30), .out_31(pipes_12_out_31), .out_32(pipes_12_out_32),
    .out_33(pipes_12_out_33), .out_34(pipes_12_out_34), .out_35(pipes_12_out_35), .out_36(pipes_12_out_36),
    .pipe(pipes_24_pipe_2), .signal(pipes_24_signal_2), .signal_2(s1), .bird_1(pipes_24_bird_1_2),
    .bird_2(pipes_24_bird));  // open: pipe_2, bird_1_2, bird
  DotMatrix #(.matrixcols(32), .matrixrows(32)) dotmatrix_12 (
    .col0(pipes_12_out_5), .col1(pipes_12_out_6), .col2(pipes_12_out_7), .col3(pipes_12_out_8),
    .col4(pipes_12_out_9), .col5(pipes_12_out_10), .col6(pipes_12_out_11), .col7(pipes_12_out_12),
    .col8(pipes_12_out_13), .col9(pipes_12_out_14), .col10(pipes_12_out_15), .col11(pipes_12_out_16),
    .col12(pipes_12_out_17), .col13(pipes_12_out_18), .col14(pipes_12_out_19), .col15(pipes_12_out_20),
    .col16(pipes_12_out_21), .col17(pipes_12_out_22), .col18(pipes_12_out_23), .col19(pipes_12_out_24),
    .col20(pipes_12_out_25), .col21(pipes_12_out_26), .col22(pipes_12_out_27), .col23(pipes_12_out_28),
    .col24(pipes_12_out_29), .col25(pipes_12_out_30), .col26(pipes_12_out_31), .col27(pipes_12_out_32),
    .col28(pipes_12_out_33), .col29(pipes_12_out_34), .col30(pipes_12_out_35), .col31(pipes_12_out_36));
  DotMatrix #(.matrixcols(32), .matrixrows(32)) dotmatrix_13 (
    .col0({32{1'b1}}), .col1({32{1'b1}}), .col2({32{1'b1}}), .col3({32{1'b1}}), .col4({32{1'b1}}),
    .col5({32{1'b1}}), .col6({32{1'b1}}), .col7({32{1'b1}}), .col8({32{1'b1}}), .col9({32{1'b1}}),
    .col10({32{1'b1}}), .col11({32{1'b1}}), .col12({32{1'b1}}), .col13({32{1'b1}}), .col14({32{1'b1}}),
    .col15({32{1'b1}}), .col16({32{1'b1}}), .col17({32{1'b1}}), .col18({32{1'b1}}), .col19({32{1'b1}}),
    .col20({32{1'b1}}), .col21({32{1'b1}}), .col22({32{1'b1}}), .col23({32{1'b1}}), .col24({32{1'b1}}),
    .col25({32{1'b1}}), .col26({32{1'b1}}), .col27({32{1'b1}}), .col28({32{1'b1}}), .col29({32{1'b1}}),
    .col30({32{1'b1}}), .col31({32{1'b1}}));
  DotMatrix #(.matrixcols(32), .matrixrows(32)) dotmatrix_14 (
    .col0({32{1'b1}}), .col1({32{1'b1}}), .col2({32{1'b1}}), .col3({32{1'b1}}), .col4({32{1'b1}}),
    .col5({32{1'b1}}), .col6({32{1'b1}}), .col7({32{1'b1}}), .col8({32{1'b1}}), .col9({32{1'b1}}),
    .col10({32{1'b1}}), .col11({32{1'b1}}), .col12({32{1'b1}}), .col13({32{1'b1}}), .col14({32{1'b1}}),
    .col15({32{1'b1}}), .col16({32{1'b1}}), .col17({32{1'b1}}), .col18({32{1'b1}}), .col19({32{1'b1}}),
    .col20({32{1'b1}}), .col21({32{1'b1}}), .col22({32{1'b1}}), .col23({32{1'b1}}), .col24({32{1'b1}}),
    .col25({32{1'b1}}), .col26({32{1'b1}}), .col27({32{1'b1}}), .col28({32{1'b1}}), .col29({32{1'b1}}),
    .col30({32{1'b1}}), .col31({32{1'b1}}));
  pipes pipes_13 (
    .out_5(pipes_13_out_5), .out_6(pipes_13_out_6), .out_7(pipes_13_out_7), .out_8(pipes_13_out_8),
    .out_9(pipes_13_out_9), .out_10(pipes_13_out_10), .out_11(pipes_13_out_11), .out_12(pipes_13_out_12),
    .out_13(pipes_13_out_13), .out_14(pipes_13_out_14), .out_15(pipes_13_out_15), .out_16(pipes_13_out_16),
    .out_17(pipes_13_out_17), .out_18(pipes_13_out_18), .out_19(pipes_13_out_19), .out_20(pipes_13_out_20),
    .out_21(pipes_13_out_21), .out_22(pipes_13_out_22), .out_23(pipes_13_out_23), .out_24(pipes_13_out_24),
    .out_25(pipes_13_out_25), .out_26(pipes_13_out_26), .out_27(pipes_13_out_27), .out_28(pipes_13_out_28),
    .out_29(pipes_13_out_29), .out_30(pipes_13_out_30), .out_31(pipes_13_out_31), .out_32(pipes_13_out_32),
    .out_33(pipes_13_out_33), .out_34(pipes_13_out_34), .out_35(pipes_13_out_35), .out_36(pipes_13_out_36),
    .pipe(pipes___bird_1_pipe_2), .pipe_2(pipes_13_pipe_2), .signal(pipes___bird_1_signal_2),
    .signal_2(pipes_13_signal_2), .bird_1(pipes___bird_1_bird_1_2), .bird_1_2(pipes_13_bird_1_2),
    .bird_2(pipes___bird_1_bird_2_2), .bird(pipes_13_bird));
  DotMatrix #(.matrixcols(32), .matrixrows(32)) dotmatrix_15 (
    .col0(pipes_13_out_5), .col1(pipes_13_out_6), .col2(pipes_13_out_7), .col3(pipes_13_out_8),
    .col4(pipes_13_out_9), .col5(pipes_13_out_10), .col6(pipes_13_out_11), .col7(pipes_13_out_12),
    .col8(pipes_13_out_13), .col9(pipes_13_out_14), .col10(pipes_13_out_15), .col11(pipes_13_out_16),
    .col12(pipes_13_out_17), .col13(pipes_13_out_18), .col14(pipes_13_out_19), .col15(pipes_13_out_20),
    .col16(pipes_13_out_21), .col17(pipes_13_out_22), .col18(pipes_13_out_23), .col19(pipes_13_out_24),
    .col20(pipes_13_out_25), .col21(pipes_13_out_26), .col22(pipes_13_out_27), .col23(pipes_13_out_28),
    .col24(pipes_13_out_29), .col25(pipes_13_out_30), .col26(pipes_13_out_31), .col27(pipes_13_out_32),
    .col28(pipes_13_out_33), .col29(pipes_13_out_34), .col30(pipes_13_out_35), .col31(pipes_13_out_36));
  DotMatrix #(.matrixcols(32), .matrixrows(32)) dotmatrix_16 (
    .col0(pipes_14_out_5), .col1(pipes_14_out_6), .col2(pipes_14_out_7), .col3(pipes_14_out_8),
    .col4(pipes_14_out_9), .col5(pipes_14_out_10), .col6(pipes_14_out_11), .col7(pipes_14_out_12),
    .col8(pipes_14_out_13), .col9(pipes_14_out_14), .col10(pipes_14_out_15), .col11(pipes_14_out_16),
    .col12(pipes_14_out_17), .col13(pipes_14_out_18), .col14(pipes_14_out_19), .col15(pipes_14_out_20),
    .col16(pipes_14_out_21), .col17(pipes_14_out_22), .col18(pipes_14_out_23), .col19(pipes_14_out_24),
    .col20(pipes_14_out_25), .col21(pipes_14_out_26), .col22(pipes_14_out_27), .col23(pipes_14_out_28),
    .col24(pipes_14_out_29), .col25(pipes_14_out_30), .col26(pipes_14_out_31), .col27(pipes_14_out_32),
    .col28(pipes_14_out_33), .col29(pipes_14_out_34), .col30(pipes_14_out_35), .col31(pipes_14_out_36));
  pipes pipes_14 (
    .out_5(pipes_14_out_5), .out_6(pipes_14_out_6), .out_7(pipes_14_out_7), .out_8(pipes_14_out_8),
    .out_9(pipes_14_out_9), .out_10(pipes_14_out_10), .out_11(pipes_14_out_11), .out_12(pipes_14_out_12),
    .out_13(pipes_14_out_13), .out_14(pipes_14_out_14), .out_15(pipes_14_out_15), .out_16(pipes_14_out_16),
    .out_17(pipes_14_out_17), .out_18(pipes_14_out_18), .out_19(pipes_14_out_19), .out_20(pipes_14_out_20),
    .out_21(pipes_14_out_21), .out_22(pipes_14_out_22), .out_23(pipes_14_out_23), .out_24(pipes_14_out_24),
    .out_25(pipes_14_out_25), .out_26(pipes_14_out_26), .out_27(pipes_14_out_27), .out_28(pipes_14_out_28),
    .out_29(pipes_14_out_29), .out_30(pipes_14_out_30), .out_31(pipes_14_out_31), .out_32(pipes_14_out_32),
    .out_33(pipes_14_out_33), .out_34(pipes_14_out_34), .out_35(pipes_14_out_35), .out_36(pipes_14_out_36),
    .pipe(pipes___bird_2_pipe_2), .pipe_2(pipes_14_pipe_2), .signal(pipes___bird_2_signal_2),
    .signal_2(pipes_14_signal_2), .bird_1(pipes___bird_2_bird_1_2), .bird_1_2(pipes_14_bird_1_2),
    .bird_2(pipes___bird_2_bird_2_2), .bird(pipes_14_bird));
  pipes pipes_15 (
    .out_5(pipes_15_out_5), .out_6(pipes_15_out_6), .out_7(pipes_15_out_7), .out_8(pipes_15_out_8),
    .out_9(pipes_15_out_9), .out_10(pipes_15_out_10), .out_11(pipes_15_out_11), .out_12(pipes_15_out_12),
    .out_13(pipes_15_out_13), .out_14(pipes_15_out_14), .out_15(pipes_15_out_15), .out_16(pipes_15_out_16),
    .out_17(pipes_15_out_17), .out_18(pipes_15_out_18), .out_19(pipes_15_out_19), .out_20(pipes_15_out_20),
    .out_21(pipes_15_out_21), .out_22(pipes_15_out_22), .out_23(pipes_15_out_23), .out_24(pipes_15_out_24),
    .out_25(pipes_15_out_25), .out_26(pipes_15_out_26), .out_27(pipes_15_out_27), .out_28(pipes_15_out_28),
    .out_29(pipes_15_out_29), .out_30(pipes_15_out_30), .out_31(pipes_15_out_31), .out_32(pipes_15_out_32),
    .out_33(pipes_15_out_33), .out_34(pipes_15_out_34), .out_35(pipes_15_out_35), .out_36(pipes_15_out_36),
    .pipe(pipes___bird_3_pipe_2), .pipe_2(pipes_15_pipe_2), .signal(pipes___bird_3_signal_2),
    .signal_2(pipes_15_signal_2), .bird_1(pipes___bird_3_bird_1_2), .bird_1_2(pipes_15_bird_1_2),
    .bird_2(pipes___bird_3_bird_2_2), .bird(pipes_15_bird));
  DotMatrix #(.matrixcols(32), .matrixrows(32)) dotmatrix_17 (
    .col0(pipes_15_out_5), .col1(pipes_15_out_6), .col2(pipes_15_out_7), .col3(pipes_15_out_8),
    .col4(pipes_15_out_9), .col5(pipes_15_out_10), .col6(pipes_15_out_11), .col7(pipes_15_out_12),
    .col8(pipes_15_out_13), .col9(pipes_15_out_14), .col10(pipes_15_out_15), .col11(pipes_15_out_16),
    .col12(pipes_15_out_17), .col13(pipes_15_out_18), .col14(pipes_15_out_19), .col15(pipes_15_out_20),
    .col16(pipes_15_out_21), .col17(pipes_15_out_22), .col18(pipes_15_out_23), .col19(pipes_15_out_24),
    .col20(pipes_15_out_25), .col21(pipes_15_out_26), .col22(pipes_15_out_27), .col23(pipes_15_out_28),
    .col24(pipes_15_out_29), .col25(pipes_15_out_30), .col26(pipes_15_out_31), .col27(pipes_15_out_32),
    .col28(pipes_15_out_33), .col29(pipes_15_out_34), .col30(pipes_15_out_35), .col31(pipes_15_out_36));
  pipes pipes_16 (
    .out_5(pipes_16_out_5), .out_6(pipes_16_out_6), .out_7(pipes_16_out_7), .out_8(pipes_16_out_8),
    .out_9(pipes_16_out_9), .out_10(pipes_16_out_10), .out_11(pipes_16_out_11), .out_12(pipes_16_out_12),
    .out_13(pipes_16_out_13), .out_14(pipes_16_out_14), .out_15(pipes_16_out_15), .out_16(pipes_16_out_16),
    .out_17(pipes_16_out_17), .out_18(pipes_16_out_18), .out_19(pipes_16_out_19), .out_20(pipes_16_out_20),
    .out_21(pipes_16_out_21), .out_22(pipes_16_out_22), .out_23(pipes_16_out_23), .out_24(pipes_16_out_24),
    .out_25(pipes_16_out_25), .out_26(pipes_16_out_26), .out_27(pipes_16_out_27), .out_28(pipes_16_out_28),
    .out_29(pipes_16_out_29), .out_30(pipes_16_out_30), .out_31(pipes_16_out_31), .out_32(pipes_16_out_32),
    .out_33(pipes_16_out_33), .out_34(pipes_16_out_34), .out_35(pipes_16_out_35), .out_36(pipes_16_out_36),
    .pipe(pipes___bird_4_pipe_2), .pipe_2(pipes_16_pipe_2), .signal(pipes___bird_4_signal_2),
    .signal_2(pipes_16_signal_2), .bird_1(pipes___bird_4_bird_1_2), .bird_1_2(pipes_16_bird_1_2),
    .bird_2(pipes___bird_4_bird_2_2), .bird(pipes_16_bird));
  DotMatrix #(.matrixcols(32), .matrixrows(32)) dotmatrix_18 (
    .col0(pipes_16_out_5), .col1(pipes_16_out_6), .col2(pipes_16_out_7), .col3(pipes_16_out_8),
    .col4(pipes_16_out_9), .col5(pipes_16_out_10), .col6(pipes_16_out_11), .col7(pipes_16_out_12),
    .col8(pipes_16_out_13), .col9(pipes_16_out_14), .col10(pipes_16_out_15), .col11(pipes_16_out_16),
    .col12(pipes_16_out_17), .col13(pipes_16_out_18), .col14(pipes_16_out_19), .col15(pipes_16_out_20),
    .col16(pipes_16_out_21), .col17(pipes_16_out_22), .col18(pipes_16_out_23), .col19(pipes_16_out_24),
    .col20(pipes_16_out_25), .col21(pipes_16_out_26), .col22(pipes_16_out_27), .col23(pipes_16_out_28),
    .col24(pipes_16_out_29), .col25(pipes_16_out_30), .col26(pipes_16_out_31), .col27(pipes_16_out_32),
    .col28(pipes_16_out_33), .col29(pipes_16_out_34), .col30(pipes_16_out_35), .col31(pipes_16_out_36));
  DotMatrix #(.matrixcols(32), .matrixrows(32)) dotmatrix_19 (
    .col0(pipes_17_out_5), .col1(pipes_17_out_6), .col2(pipes_17_out_7), .col3(pipes_17_out_8),
    .col4(pipes_17_out_9), .col5(pipes_17_out_10), .col6(pipes_17_out_11), .col7(pipes_17_out_12),
    .col8(pipes_17_out_13), .col9(pipes_17_out_14), .col10(pipes_17_out_15), .col11(pipes_17_out_16),
    .col12(pipes_17_out_17), .col13(pipes_17_out_18), .col14(pipes_17_out_19), .col15(pipes_17_out_20),
    .col16(pipes_17_out_21), .col17(pipes_17_out_22), .col18(pipes_17_out_23), .col19(pipes_17_out_24),
    .col20(pipes_17_out_25), .col21(pipes_17_out_26), .col22(pipes_17_out_27), .col23(pipes_17_out_28),
    .col24(pipes_17_out_29), .col25(pipes_17_out_30), .col26(pipes_17_out_31), .col27(pipes_17_out_32),
    .col28(pipes_17_out_33), .col29(pipes_17_out_34), .col30(pipes_17_out_35), .col31(pipes_17_out_36));
  pipes pipes_17 (
    .out_5(pipes_17_out_5), .out_6(pipes_17_out_6), .out_7(pipes_17_out_7), .out_8(pipes_17_out_8),
    .out_9(pipes_17_out_9), .out_10(pipes_17_out_10), .out_11(pipes_17_out_11), .out_12(pipes_17_out_12),
    .out_13(pipes_17_out_13), .out_14(pipes_17_out_14), .out_15(pipes_17_out_15), .out_16(pipes_17_out_16),
    .out_17(pipes_17_out_17), .out_18(pipes_17_out_18), .out_19(pipes_17_out_19), .out_20(pipes_17_out_20),
    .out_21(pipes_17_out_21), .out_22(pipes_17_out_22), .out_23(pipes_17_out_23), .out_24(pipes_17_out_24),
    .out_25(pipes_17_out_25), .out_26(pipes_17_out_26), .out_27(pipes_17_out_27), .out_28(pipes_17_out_28),
    .out_29(pipes_17_out_29), .out_30(pipes_17_out_30), .out_31(pipes_17_out_31), .out_32(pipes_17_out_32),
    .out_33(pipes_17_out_33), .out_34(pipes_17_out_34), .out_35(pipes_17_out_35), .out_36(pipes_17_out_36),
    .pipe(pipes___bird_5_pipe_2), .pipe_2(pipes_17_pipe_2), .signal(pipes___bird_5_signal_2),
    .signal_2(pipes_17_signal_2), .bird_1(pipes___bird_5_bird_1_2), .bird_1_2(pipes_17_bird_1_2),
    .bird_2(pipes___bird_5_bird_2_2), .bird(pipes_17_bird));
  DotMatrix #(.matrixcols(32), .matrixrows(32)) dotmatrix_20 (
    .col0(pipes_18_out_5), .col1(pipes_18_out_6), .col2(pipes_18_out_7), .col3(pipes_18_out_8),
    .col4(pipes_18_out_9), .col5(pipes_18_out_10), .col6(pipes_18_out_11), .col7(pipes_18_out_12),
    .col8(pipes_18_out_13), .col9(pipes_18_out_14), .col10(pipes_18_out_15), .col11(pipes_18_out_16),
    .col12(pipes_18_out_17), .col13(pipes_18_out_18), .col14(pipes_18_out_19), .col15(pipes_18_out_20),
    .col16(pipes_18_out_21), .col17(pipes_18_out_22), .col18(pipes_18_out_23), .col19(pipes_18_out_24),
    .col20(pipes_18_out_25), .col21(pipes_18_out_26), .col22(pipes_18_out_27), .col23(pipes_18_out_28),
    .col24(pipes_18_out_29), .col25(pipes_18_out_30), .col26(pipes_18_out_31), .col27(pipes_18_out_32),
    .col28(pipes_18_out_33), .col29(pipes_18_out_34), .col30(pipes_18_out_35), .col31(pipes_18_out_36));
  pipes pipes_18 (
    .out_5(pipes_18_out_5), .out_6(pipes_18_out_6), .out_7(pipes_18_out_7), .out_8(pipes_18_out_8),
    .out_9(pipes_18_out_9), .out_10(pipes_18_out_10), .out_11(pipes_18_out_11), .out_12(pipes_18_out_12),
    .out_13(pipes_18_out_13), .out_14(pipes_18_out_14), .out_15(pipes_18_out_15), .out_16(pipes_18_out_16),
    .out_17(pipes_18_out_17), .out_18(pipes_18_out_18), .out_19(pipes_18_out_19), .out_20(pipes_18_out_20),
    .out_21(pipes_18_out_21), .out_22(pipes_18_out_22), .out_23(pipes_18_out_23), .out_24(pipes_18_out_24),
    .out_25(pipes_18_out_25), .out_26(pipes_18_out_26), .out_27(pipes_18_out_27), .out_28(pipes_18_out_28),
    .out_29(pipes_18_out_29), .out_30(pipes_18_out_30), .out_31(pipes_18_out_31), .out_32(pipes_18_out_32),
    .out_33(pipes_18_out_33), .out_34(pipes_18_out_34), .out_35(pipes_18_out_35), .out_36(pipes_18_out_36),
    .pipe(pipes___bird_6_pipe_2), .pipe_2(pipes_18_pipe_2), .signal(pipes___bird_6_signal_2),
    .signal_2(pipes_18_signal_2), .bird_1(pipes___bird_6_bird_1_2), .bird_1_2(pipes_18_bird_1_2),
    .bird_2(pipes___bird_6_bird_2_2), .bird(pipes_18_bird));
  pipes pipes_19 (
    .out_5(pipes_19_out_5), .out_6(pipes_19_out_6), .out_7(pipes_19_out_7), .out_8(pipes_19_out_8),
    .out_9(pipes_19_out_9), .out_10(pipes_19_out_10), .out_11(pipes_19_out_11), .out_12(pipes_19_out_12),
    .out_13(pipes_19_out_13), .out_14(pipes_19_out_14), .out_15(pipes_19_out_15), .out_16(pipes_19_out_16),
    .out_17(pipes_19_out_17), .out_18(pipes_19_out_18), .out_19(pipes_19_out_19), .out_20(pipes_19_out_20),
    .out_21(pipes_19_out_21), .out_22(pipes_19_out_22), .out_23(pipes_19_out_23), .out_24(pipes_19_out_24),
    .out_25(pipes_19_out_25), .out_26(pipes_19_out_26), .out_27(pipes_19_out_27), .out_28(pipes_19_out_28),
    .out_29(pipes_19_out_29), .out_30(pipes_19_out_30), .out_31(pipes_19_out_31), .out_32(pipes_19_out_32),
    .out_33(pipes_19_out_33), .out_34(pipes_19_out_34), .out_35(pipes_19_out_35), .out_36(pipes_19_out_36),
    .pipe(pipes___bird_7_pipe_2), .pipe_2(pipes_19_pipe_2), .signal(pipes___bird_7_signal_2),
    .signal_2(pipes_19_signal_2), .bird_1(pipes___bird_7_bird_1_2), .bird_1_2(pipes_19_bird_1_2),
    .bird_2(pipes___bird_7_bird_2_2), .bird(pipes_19_bird));
  DotMatrix #(.matrixcols(32), .matrixrows(32)) dotmatrix_21 (
    .col0(pipes_19_out_5), .col1(pipes_19_out_6), .col2(pipes_19_out_7), .col3(pipes_19_out_8),
    .col4(pipes_19_out_9), .col5(pipes_19_out_10), .col6(pipes_19_out_11), .col7(pipes_19_out_12),
    .col8(pipes_19_out_13), .col9(pipes_19_out_14), .col10(pipes_19_out_15), .col11(pipes_19_out_16),
    .col12(pipes_19_out_17), .col13(pipes_19_out_18), .col14(pipes_19_out_19), .col15(pipes_19_out_20),
    .col16(pipes_19_out_21), .col17(pipes_19_out_22), .col18(pipes_19_out_23), .col19(pipes_19_out_24),
    .col20(pipes_19_out_25), .col21(pipes_19_out_26), .col22(pipes_19_out_27), .col23(pipes_19_out_28),
    .col24(pipes_19_out_29), .col25(pipes_19_out_30), .col26(pipes_19_out_31), .col27(pipes_19_out_32),
    .col28(pipes_19_out_33), .col29(pipes_19_out_34), .col30(pipes_19_out_35), .col31(pipes_19_out_36));
  DotMatrix #(.matrixcols(32), .matrixrows(32)) dotmatrix_22 (
    .col0(pipes_20_out_5), .col1(pipes_20_out_6), .col2(pipes_20_out_7), .col3(pipes_20_out_8),
    .col4(pipes_20_out_9), .col5(pipes_20_out_10), .col6(pipes_20_out_11), .col7(pipes_20_out_12),
    .col8(pipes_20_out_13), .col9(pipes_20_out_14), .col10(pipes_20_out_15), .col11(pipes_20_out_16),
    .col12(pipes_20_out_17), .col13(pipes_20_out_18), .col14(pipes_20_out_19), .col15(pipes_20_out_20),
    .col16(pipes_20_out_21), .col17(pipes_20_out_22), .col18(pipes_20_out_23), .col19(pipes_20_out_24),
    .col20(pipes_20_out_25), .col21(pipes_20_out_26), .col22(pipes_20_out_27), .col23(pipes_20_out_28),
    .col24(pipes_20_out_29), .col25(pipes_20_out_30), .col26(pipes_20_out_31), .col27(pipes_20_out_32),
    .col28(pipes_20_out_33), .col29(pipes_20_out_34), .col30(pipes_20_out_35), .col31(pipes_20_out_36));
  pipes pipes_20 (
    .out_5(pipes_20_out_5), .out_6(pipes_20_out_6), .out_7(pipes_20_out_7), .out_8(pipes_20_out_8),
    .out_9(pipes_20_out_9), .out_10(pipes_20_out_10), .out_11(pipes_20_out_11), .out_12(pipes_20_out_12),
    .out_13(pipes_20_out_13), .out_14(pipes_20_out_14), .out_15(pipes_20_out_15), .out_16(pipes_20_out_16),
    .out_17(pipes_20_out_17), .out_18(pipes_20_out_18), .out_19(pipes_20_out_19), .out_20(pipes_20_out_20),
    .out_21(pipes_20_out_21), .out_22(pipes_20_out_22), .out_23(pipes_20_out_23), .out_24(pipes_20_out_24),
    .out_25(pipes_20_out_25), .out_26(pipes_20_out_26), .out_27(pipes_20_out_27), .out_28(pipes_20_out_28),
    .out_29(pipes_20_out_29), .out_30(pipes_20_out_30), .out_31(pipes_20_out_31), .out_32(pipes_20_out_32),
    .out_33(pipes_20_out_33), .out_34(pipes_20_out_34), .out_35(pipes_20_out_35), .out_36(pipes_20_out_36),
    .pipe(pipes___bird_8_pipe_2), .pipe_2(pipes_20_pipe_2), .signal(pipes___bird_8_signal_2),
    .signal_2(pipes_20_signal_2), .bird_1(pipes___bird_8_bird_1_2), .bird_1_2(pipes_20_bird_1_2),
    .bird_2(pipes___bird_8_bird_2_2), .bird(pipes_20_bird));
  pipes pipes_21 (
    .out_5(pipes_21_out_5), .out_6(pipes_21_out_6), .out_7(pipes_21_out_7), .out_8(pipes_21_out_8),
    .out_9(pipes_21_out_9), .out_10(pipes_21_out_10), .out_11(pipes_21_out_11), .out_12(pipes_21_out_12),
    .out_13(pipes_21_out_13), .out_14(pipes_21_out_14), .out_15(pipes_21_out_15), .out_16(pipes_21_out_16),
    .out_17(pipes_21_out_17), .out_18(pipes_21_out_18), .out_19(pipes_21_out_19), .out_20(pipes_21_out_20),
    .out_21(pipes_21_out_21), .out_22(pipes_21_out_22), .out_23(pipes_21_out_23), .out_24(pipes_21_out_24),
    .out_25(pipes_21_out_25), .out_26(pipes_21_out_26), .out_27(pipes_21_out_27), .out_28(pipes_21_out_28),
    .out_29(pipes_21_out_29), .out_30(pipes_21_out_30), .out_31(pipes_21_out_31), .out_32(pipes_21_out_32),
    .out_33(pipes_21_out_33), .out_34(pipes_21_out_34), .out_35(pipes_21_out_35), .out_36(pipes_21_out_36),
    .pipe(pipes___bird_9_pipe_2), .pipe_2(pipes_21_pipe_2), .signal(pipes___bird_9_signal_2),
    .signal_2(pipes_21_signal_2), .bird_1(pipes___bird_9_bird_1_2), .bird_1_2(pipes_21_bird_1_2),
    .bird_2(pipes___bird_9_bird_2_2), .bird(pipes_21_bird));
  DotMatrix #(.matrixcols(32), .matrixrows(32)) dotmatrix_23 (
    .col0(pipes_21_out_5), .col1(pipes_21_out_6), .col2(pipes_21_out_7), .col3(pipes_21_out_8),
    .col4(pipes_21_out_9), .col5(pipes_21_out_10), .col6(pipes_21_out_11), .col7(pipes_21_out_12),
    .col8(pipes_21_out_13), .col9(pipes_21_out_14), .col10(pipes_21_out_15), .col11(pipes_21_out_16),
    .col12(pipes_21_out_17), .col13(pipes_21_out_18), .col14(pipes_21_out_19), .col15(pipes_21_out_20),
    .col16(pipes_21_out_21), .col17(pipes_21_out_22), .col18(pipes_21_out_23), .col19(pipes_21_out_24),
    .col20(pipes_21_out_25), .col21(pipes_21_out_26), .col22(pipes_21_out_27), .col23(pipes_21_out_28),
    .col24(pipes_21_out_29), .col25(pipes_21_out_30), .col26(pipes_21_out_31), .col27(pipes_21_out_32),
    .col28(pipes_21_out_33), .col29(pipes_21_out_34), .col30(pipes_21_out_35), .col31(pipes_21_out_36));
  DotMatrix #(.matrixcols(32), .matrixrows(32)) dotmatrix_24 (
    .col0(pipes_22_out_5), .col1(pipes_22_out_6), .col2(pipes_22_out_7), .col3(pipes_22_out_8),
    .col4(pipes_22_out_9), .col5(pipes_22_out_10), .col6(pipes_22_out_11), .col7(pipes_22_out_12),
    .col8(pipes_22_out_13), .col9(pipes_22_out_14), .col10(pipes_22_out_15), .col11(pipes_22_out_16),
    .col12(pipes_22_out_17), .col13(pipes_22_out_18), .col14(pipes_22_out_19), .col15(pipes_22_out_20),
    .col16(pipes_22_out_21), .col17(pipes_22_out_22), .col18(pipes_22_out_23), .col19(pipes_22_out_24),
    .col20(pipes_22_out_25), .col21(pipes_22_out_26), .col22(pipes_22_out_27), .col23(pipes_22_out_28),
    .col24(pipes_22_out_29), .col25(pipes_22_out_30), .col26(pipes_22_out_31), .col27(pipes_22_out_32),
    .col28(pipes_22_out_33), .col29(pipes_22_out_34), .col30(pipes_22_out_35), .col31(pipes_22_out_36));
  pipes pipes_22 (
    .out_5(pipes_22_out_5), .out_6(pipes_22_out_6), .out_7(pipes_22_out_7), .out_8(pipes_22_out_8),
    .out_9(pipes_22_out_9), .out_10(pipes_22_out_10), .out_11(pipes_22_out_11), .out_12(pipes_22_out_12),
    .out_13(pipes_22_out_13), .out_14(pipes_22_out_14), .out_15(pipes_22_out_15), .out_16(pipes_22_out_16),
    .out_17(pipes_22_out_17), .out_18(pipes_22_out_18), .out_19(pipes_22_out_19), .out_20(pipes_22_out_20),
    .out_21(pipes_22_out_21), .out_22(pipes_22_out_22), .out_23(pipes_22_out_23), .out_24(pipes_22_out_24),
    .out_25(pipes_22_out_25), .out_26(pipes_22_out_26), .out_27(pipes_22_out_27), .out_28(pipes_22_out_28),
    .out_29(pipes_22_out_29), .out_30(pipes_22_out_30), .out_31(pipes_22_out_31), .out_32(pipes_22_out_32),
    .out_33(pipes_22_out_33), .out_34(pipes_22_out_34), .out_35(pipes_22_out_35), .out_36(pipes_22_out_36),
    .pipe(pipes___bird_10_pipe_2), .pipe_2(pipes_22_pipe_2), .signal(pipes___bird_10_signal_2),
    .signal_2(pipes_22_signal_2), .bird_1(pipes___bird_10_bird_1_2), .bird_1_2(pipes_22_bird_1_2),
    .bird_2(pipes___bird_10_bird_2_2), .bird(pipes_22_bird));
  pipes pipes_23 (
    .out_5(pipes_23_out_5), .out_6(pipes_23_out_6), .out_7(pipes_23_out_7), .out_8(pipes_23_out_8),
    .out_9(pipes_23_out_9), .out_10(pipes_23_out_10), .out_11(pipes_23_out_11), .out_12(pipes_23_out_12),
    .out_13(pipes_23_out_13), .out_14(pipes_23_out_14), .out_15(pipes_23_out_15), .out_16(pipes_23_out_16),
    .out_17(pipes_23_out_17), .out_18(pipes_23_out_18), .out_19(pipes_23_out_19), .out_20(pipes_23_out_20),
    .out_21(pipes_23_out_21), .out_22(pipes_23_out_22), .out_23(pipes_23_out_23), .out_24(pipes_23_out_24),
    .out_25(pipes_23_out_25), .out_26(pipes_23_out_26), .out_27(pipes_23_out_27), .out_28(pipes_23_out_28),
    .out_29(pipes_23_out_29), .out_30(pipes_23_out_30), .out_31(pipes_23_out_31), .out_32(pipes_23_out_32),
    .out_33(pipes_23_out_33), .out_34(pipes_23_out_34), .out_35(pipes_23_out_35), .out_36(pipes_23_out_36),
    .pipe(pipes___bird_11_pipe_2), .pipe_2(pipes_23_pipe_2), .signal(pipes___bird_11_signal_2),
    .signal_2(pipes_23_signal_2), .bird_1(pipes___bird_11_bird_1_2), .bird_1_2(pipes_23_bird_1_2),
    .bird_2(pipes___bird_11_bird_2_2), .bird(pipes_23_bird));
  DotMatrix #(.matrixcols(32), .matrixrows(32)) dotmatrix_25 (
    .col0(pipes_23_out_5), .col1(pipes_23_out_6), .col2(pipes_23_out_7), .col3(pipes_23_out_8),
    .col4(pipes_23_out_9), .col5(pipes_23_out_10), .col6(pipes_23_out_11), .col7(pipes_23_out_12),
    .col8(pipes_23_out_13), .col9(pipes_23_out_14), .col10(pipes_23_out_15), .col11(pipes_23_out_16),
    .col12(pipes_23_out_17), .col13(pipes_23_out_18), .col14(pipes_23_out_19), .col15(pipes_23_out_20),
    .col16(pipes_23_out_21), .col17(pipes_23_out_22), .col18(pipes_23_out_23), .col19(pipes_23_out_24),
    .col20(pipes_23_out_25), .col21(pipes_23_out_26), .col22(pipes_23_out_27), .col23(pipes_23_out_28),
    .col24(pipes_23_out_29), .col25(pipes_23_out_30), .col26(pipes_23_out_31), .col27(pipes_23_out_32),
    .col28(pipes_23_out_33), .col29(pipes_23_out_34), .col30(pipes_23_out_35), .col31(pipes_23_out_36));
  DotMatrix #(.matrixcols(32), .matrixrows(32)) dotmatrix_26 (
    .col0(pipes_24_out_5), .col1(pipes_24_out_6), .col2(pipes_24_out_7), .col3(pipes_24_out_8),
    .col4(pipes_24_out_9), .col5(pipes_24_out_10), .col6(pipes_24_out_11), .col7(pipes_24_out_12),
    .col8(pipes_24_out_13), .col9(pipes_24_out_14), .col10(pipes_24_out_15), .col11(pipes_24_out_16),
    .col12(pipes_24_out_17), .col13(pipes_24_out_18), .col14(pipes_24_out_19), .col15(pipes_24_out_20),
    .col16(pipes_24_out_21), .col17(pipes_24_out_22), .col18(pipes_24_out_23), .col19(pipes_24_out_24),
    .col20(pipes_24_out_25), .col21(pipes_24_out_26), .col22(pipes_24_out_27), .col23(pipes_24_out_28),
    .col24(pipes_24_out_29), .col25(pipes_24_out_30), .col26(pipes_24_out_31), .col27(pipes_24_out_32),
    .col28(pipes_24_out_33), .col29(pipes_24_out_34), .col30(pipes_24_out_35), .col31(plus_1));
  pipes pipes_24 (
    .out_5(pipes_24_out_5), .out_6(pipes_24_out_6), .out_7(pipes_24_out_7), .out_8(pipes_24_out_8),
    .out_9(pipes_24_out_9), .out_10(pipes_24_out_10), .out_11(pipes_24_out_11), .out_12(pipes_24_out_12),
    .out_13(pipes_24_out_13), .out_14(pipes_24_out_14), .out_15(pipes_24_out_15), .out_16(pipes_24_out_16),
    .out_17(pipes_24_out_17), .out_18(pipes_24_out_18), .out_19(pipes_24_out_19), .out_20(pipes_24_out_20),
    .out_21(pipes_24_out_21), .out_22(pipes_24_out_22), .out_23(pipes_24_out_23), .out_24(pipes_24_out_24),
    .out_25(pipes_24_out_25), .out_26(pipes_24_out_26), .out_27(pipes_24_out_27), .out_28(pipes_24_out_28),
    .out_29(pipes_24_out_29), .out_30(pipes_24_out_30), .out_31(pipes_24_out_31), .out_32(pipes_24_out_32),
    .out_33(pipes_24_out_33), .out_34(pipes_24_out_34), .out_35(pipes_24_out_35), .out_36(plus_1),
    .pipe(pipes___bird_12_pipe_2), .pipe_2(pipes_24_pipe_2), .signal(pipes___bird_12_signal_2),
    .signal_2(pipes_24_signal_2), .bird_1(pipes___bird_12_bird_1_2), .bird_1_2(pipes_24_bird_1_2),
    .bird_2(pipes___bird_12_bird_2_2), .bird(pipes_24_bird));
  DotMatrix #(.matrixcols(32), .matrixrows(32)) dotmatrix_27 (
    .col0({32{1'b1}}), .col1({32{1'b1}}), .col2({32{1'b1}}), .col3({32{1'b1}}), .col4({32{1'b1}}),
    .col5({32{1'b1}}), .col6({32{1'b1}}), .col7({32{1'b1}}), .col8({32{1'b1}}), .col9({32{1'b1}}),
    .col10({32{1'b1}}), .col11({32{1'b1}}), .col12({32{1'b1}}), .col13({32{1'b1}}), .col14({32{1'b1}}),
    .col15({32{1'b1}}), .col16({32{1'b1}}), .col17({32{1'b1}}), .col18({32{1'b1}}), .col19({32{1'b1}}),
    .col20({32{1'b1}}), .col21({32{1'b1}}), .col22({32{1'b1}}), .col23({32{1'b1}}), .col24({32{1'b1}}),
    .col25({32{1'b1}}), .col26({32{1'b1}}), .col27({32{1'b1}}), .col28({32{1'b1}}), .col29({32{1'b1}}),
    .col30({32{1'b1}}), .col31({32{1'b1}}));
  DotMatrix #(.matrixcols(32), .matrixrows(32)) dotmatrix_28 (
    .col0({32{1'b1}}), .col1({32{1'b1}}), .col2({32{1'b1}}), .col3({32{1'b1}}), .col4({32{1'b1}}),
    .col5({32{1'b1}}), .col6({32{1'b1}}), .col7({32{1'b1}}), .col8({32{1'b1}}), .col9({32{1'b1}}),
    .col10({32{1'b1}}), .col11({32{1'b1}}), .col12({32{1'b1}}), .col13({32{1'b1}}), .col14({32{1'b1}}),
    .col15({32{1'b1}}), .col16({32{1'b1}}), .col17({32{1'b1}}), .col18({32{1'b1}}), .col19({32{1'b1}}),
    .col20({32{1'b1}}), .col21({32{1'b1}}), .col22({32{1'b1}}), .col23({32{1'b1}}), .col24({32{1'b1}}),
    .col25({32{1'b1}}), .col26({32{1'b1}}), .col27({32{1'b1}}), .col28({32{1'b1}}), .col29({32{1'b1}}),
    .col30({32{1'b1}}), .col31({32{1'b1}}));
  DotMatrix #(.matrixcols(32), .matrixrows(32)) dotmatrix_29 (
    .col0(pipes___bird_1_out_5), .col1(pipes___bird_1_out_6), .col2(pipes___bird_1_out_7),
    .col3(pipes___bird_1_out_8), .col4(pipes___bird_1_out_9), .col5(pipes___bird_1_out_10),
    .col6(pipes___bird_1_out_11), .col7(pipes___bird_1_out_12), .col8(pipes___bird_1_out_13),
    .col9(pipes___bird_1_out_14), .col10(pipes___bird_1_out_15), .col11(pipes___bird_1_out_16),
    .col12(pipes___bird_1_out_17), .col13(pipes___bird_1_out_18), .col14(pipes___bird_1_out_19),
    .col15(pipes___bird_1_out_20), .col16(pipes___bird_1_out_21), .col17(pipes___bird_1_out_22),
    .col18(pipes___bird_1_out_23), .col19(pipes___bird_1_out_24), .col20(pipes___bird_1_out_25),
    .col21(pipes___bird_1_out_26), .col22(pipes___bird_1_out_27), .col23(pipes___bird_1_out_28),
    .col24(pipes___bird_1_out_29), .col25(pipes___bird_1_out_30), .col26(pipes___bird_1_out_31),
    .col27(pipes___bird_1_out_32), .col28(pipes___bird_1_out_33), .col29(pipes___bird_1_out_34),
    .col30(pipes___bird_1_out_35), .col31(pipes___bird_1_out_36));
  DotMatrix #(.matrixcols(32), .matrixrows(32)) dotmatrix_30 (
    .col0(pipes___bird_2_out_5), .col1(pipes___bird_2_out_6), .col2(pipes___bird_2_out_7),
    .col3(pipes___bird_2_out_8), .col4(pipes___bird_2_out_9), .col5(pipes___bird_2_out_10),
    .col6(pipes___bird_2_out_11), .col7(pipes___bird_2_out_12), .col8(pipes___bird_2_out_13),
    .col9(pipes___bird_2_out_14), .col10(pipes___bird_2_out_15), .col11(pipes___bird_2_out_16),
    .col12(pipes___bird_2_out_17), .col13(pipes___bird_2_out_18), .col14(pipes___bird_2_out_19),
    .col15(pipes___bird_2_out_20), .col16(pipes___bird_2_out_21), .col17(pipes___bird_2_out_22),
    .col18(pipes___bird_2_out_23), .col19(pipes___bird_2_out_24), .col20(pipes___bird_2_out_25),
    .col21(pipes___bird_2_out_26), .col22(pipes___bird_2_out_27), .col23(pipes___bird_2_out_28),
    .col24(pipes___bird_2_out_29), .col25(pipes___bird_2_out_30), .col26(pipes___bird_2_out_31),
    .col27(pipes___bird_2_out_32), .col28(pipes___bird_2_out_33), .col29(pipes___bird_2_out_34),
    .col30(pipes___bird_2_out_35), .col31(pipes___bird_2_out_36));
  DotMatrix #(.matrixcols(32), .matrixrows(32)) dotmatrix_31 (
    .col0(pipes___bird_3_out_5), .col1(pipes___bird_3_out_6), .col2(pipes___bird_3_out_7),
    .col3(pipes___bird_3_out_8), .col4(pipes___bird_3_out_9), .col5(pipes___bird_3_out_10),
    .col6(pipes___bird_3_out_11), .col7(pipes___bird_3_out_12), .col8(pipes___bird_3_out_13),
    .col9(pipes___bird_3_out_14), .col10(pipes___bird_3_out_15), .col11(pipes___bird_3_out_16),
    .col12(pipes___bird_3_out_17), .col13(pipes___bird_3_out_18), .col14(pipes___bird_3_out_19),
    .col15(pipes___bird_3_out_20), .col16(pipes___bird_3_out_21), .col17(pipes___bird_3_out_22),
    .col18(pipes___bird_3_out_23), .col19(pipes___bird_3_out_24), .col20(pipes___bird_3_out_25),
    .col21(pipes___bird_3_out_26), .col22(pipes___bird_3_out_27), .col23(pipes___bird_3_out_28),
    .col24(pipes___bird_3_out_29), .col25(pipes___bird_3_out_30), .col26(pipes___bird_3_out_31),
    .col27(pipes___bird_3_out_32), .col28(pipes___bird_3_out_33), .col29(pipes___bird_3_out_34),
    .col30(pipes___bird_3_out_35), .col31(pipes___bird_3_out_36));
  DotMatrix #(.matrixcols(32), .matrixrows(32)) dotmatrix_32 (
    .col0(pipes___bird_4_out_5), .col1(pipes___bird_4_out_6), .col2(pipes___bird_4_out_7),
    .col3(pipes___bird_4_out_8), .col4(pipes___bird_4_out_9), .col5(pipes___bird_4_out_10),
    .col6(pipes___bird_4_out_11), .col7(pipes___bird_4_out_12), .col8(pipes___bird_4_out_13),
    .col9(pipes___bird_4_out_14), .col10(pipes___bird_4_out_15), .col11(pipes___bird_4_out_16),
    .col12(pipes___bird_4_out_17), .col13(pipes___bird_4_out_18), .col14(pipes___bird_4_out_19),
    .col15(pipes___bird_4_out_20), .col16(pipes___bird_4_out_21), .col17(pipes___bird_4_out_22),
    .col18(pipes___bird_4_out_23), .col19(pipes___bird_4_out_24), .col20(pipes___bird_4_out_25),
    .col21(pipes___bird_4_out_26), .col22(pipes___bird_4_out_27), .col23(pipes___bird_4_out_28),
    .col24(pipes___bird_4_out_29), .col25(pipes___bird_4_out_30), .col26(pipes___bird_4_out_31),
    .col27(pipes___bird_4_out_32), .col28(pipes___bird_4_out_33), .col29(pipes___bird_4_out_34),
    .col30(pipes___bird_4_out_35), .col31(pipes___bird_4_out_36));
  DotMatrix #(.matrixcols(32), .matrixrows(32)) dotmatrix_33 (
    .col0(pipes___bird_5_out_5), .col1(pipes___bird_5_out_6), .col2(pipes___bird_5_out_7),
    .col3(pipes___bird_5_out_8), .col4(pipes___bird_5_out_9), .col5(pipes___bird_5_out_10),
    .col6(pipes___bird_5_out_11), .col7(pipes___bird_5_out_12), .col8(pipes___bird_5_out_13),
    .col9(pipes___bird_5_out_14), .col10(pipes___bird_5_out_15), .col11(pipes___bird_5_out_16),
    .col12(pipes___bird_5_out_17), .col13(pipes___bird_5_out_18), .col14(pipes___bird_5_out_19),
    .col15(pipes___bird_5_out_20), .col16(pipes___bird_5_out_21), .col17(pipes___bird_5_out_22),
    .col18(pipes___bird_5_out_23), .col19(pipes___bird_5_out_24), .col20(pipes___bird_5_out_25),
    .col21(pipes___bird_5_out_26), .col22(pipes___bird_5_out_27), .col23(pipes___bird_5_out_28),
    .col24(pipes___bird_5_out_29), .col25(pipes___bird_5_out_30), .col26(pipes___bird_5_out_31),
    .col27(pipes___bird_5_out_32), .col28(pipes___bird_5_out_33), .col29(pipes___bird_5_out_34),
    .col30(pipes___bird_5_out_35), .col31(pipes___bird_5_out_36));
  DotMatrix #(.matrixcols(32), .matrixrows(32)) dotmatrix_34 (
    .col0(pipes___bird_6_out_5), .col1(pipes___bird_6_out_6), .col2(pipes___bird_6_out_7),
    .col3(pipes___bird_6_out_8), .col4(pipes___bird_6_out_9), .col5(pipes___bird_6_out_10),
    .col6(pipes___bird_6_out_11), .col7(pipes___bird_6_out_12), .col8(pipes___bird_6_out_13),
    .col9(pipes___bird_6_out_14), .col10(pipes___bird_6_out_15), .col11(pipes___bird_6_out_16),
    .col12(pipes___bird_6_out_17), .col13(pipes___bird_6_out_18), .col14(pipes___bird_6_out_19),
    .col15(pipes___bird_6_out_20), .col16(pipes___bird_6_out_21), .col17(pipes___bird_6_out_22),
    .col18(pipes___bird_6_out_23), .col19(pipes___bird_6_out_24), .col20(pipes___bird_6_out_25),
    .col21(pipes___bird_6_out_26), .col22(pipes___bird_6_out_27), .col23(pipes___bird_6_out_28),
    .col24(pipes___bird_6_out_29), .col25(pipes___bird_6_out_30), .col26(pipes___bird_6_out_31),
    .col27(pipes___bird_6_out_32), .col28(pipes___bird_6_out_33), .col29(pipes___bird_6_out_34),
    .col30(pipes___bird_6_out_35), .col31(pipes___bird_6_out_36));
  DotMatrix #(.matrixcols(32), .matrixrows(32)) dotmatrix_35 (
    .col0(pipes___bird_7_out_5), .col1(pipes___bird_7_out_6), .col2(pipes___bird_7_out_7),
    .col3(pipes___bird_7_out_8), .col4(pipes___bird_7_out_9), .col5(pipes___bird_7_out_10),
    .col6(pipes___bird_7_out_11), .col7(pipes___bird_7_out_12), .col8(pipes___bird_7_out_13),
    .col9(pipes___bird_7_out_14), .col10(pipes___bird_7_out_15), .col11(pipes___bird_7_out_16),
    .col12(pipes___bird_7_out_17), .col13(pipes___bird_7_out_18), .col14(pipes___bird_7_out_19),
    .col15(pipes___bird_7_out_20), .col16(pipes___bird_7_out_21), .col17(pipes___bird_7_out_22),
    .col18(pipes___bird_7_out_23), .col19(pipes___bird_7_out_24), .col20(pipes___bird_7_out_25),
    .col21(pipes___bird_7_out_26), .col22(pipes___bird_7_out_27), .col23(pipes___bird_7_out_28),
    .col24(pipes___bird_7_out_29), .col25(pipes___bird_7_out_30), .col26(pipes___bird_7_out_31),
    .col27(pipes___bird_7_out_32), .col28(pipes___bird_7_out_33), .col29(pipes___bird_7_out_34),
    .col30(pipes___bird_7_out_35), .col31(pipes___bird_7_out_36));
  DotMatrix #(.matrixcols(32), .matrixrows(32)) dotmatrix_36 (
    .col0(pipes___bird_8_out_5), .col1(pipes___bird_8_out_6), .col2(pipes___bird_8_out_7),
    .col3(pipes___bird_8_out_8), .col4(pipes___bird_8_out_9), .col5(pipes___bird_8_out_10),
    .col6(pipes___bird_8_out_11), .col7(pipes___bird_8_out_12), .col8(pipes___bird_8_out_13),
    .col9(pipes___bird_8_out_14), .col10(pipes___bird_8_out_15), .col11(pipes___bird_8_out_16),
    .col12(pipes___bird_8_out_17), .col13(pipes___bird_8_out_18), .col14(pipes___bird_8_out_19),
    .col15(pipes___bird_8_out_20), .col16(pipes___bird_8_out_21), .col17(pipes___bird_8_out_22),
    .col18(pipes___bird_8_out_23), .col19(pipes___bird_8_out_24), .col20(pipes___bird_8_out_25),
    .col21(pipes___bird_8_out_26), .col22(pipes___bird_8_out_27), .col23(pipes___bird_8_out_28),
    .col24(pipes___bird_8_out_29), .col25(pipes___bird_8_out_30), .col26(pipes___bird_8_out_31),
    .col27(pipes___bird_8_out_32), .col28(pipes___bird_8_out_33), .col29(pipes___bird_8_out_34),
    .col30(pipes___bird_8_out_35), .col31(pipes___bird_8_out_36));
  DotMatrix #(.matrixcols(32), .matrixrows(32)) dotmatrix_37 (
    .col0(pipes___bird_9_out_5), .col1(pipes___bird_9_out_6), .col2(pipes___bird_9_out_7),
    .col3(pipes___bird_9_out_8), .col4(pipes___bird_9_out_9), .col5(pipes___bird_9_out_10),
    .col6(pipes___bird_9_out_11), .col7(pipes___bird_9_out_12), .col8(pipes___bird_9_out_13),
    .col9(pipes___bird_9_out_14), .col10(pipes___bird_9_out_15), .col11(pipes___bird_9_out_16),
    .col12(pipes___bird_9_out_17), .col13(pipes___bird_9_out_18), .col14(pipes___bird_9_out_19),
    .col15(pipes___bird_9_out_20), .col16(pipes___bird_9_out_21), .col17(pipes___bird_9_out_22),
    .col18(pipes___bird_9_out_23), .col19(pipes___bird_9_out_24), .col20(pipes___bird_9_out_25),
    .col21(pipes___bird_9_out_26), .col22(pipes___bird_9_out_27), .col23(pipes___bird_9_out_28),
    .col24(pipes___bird_9_out_29), .col25(pipes___bird_9_out_30), .col26(pipes___bird_9_out_31),
    .col27(pipes___bird_9_out_32), .col28(pipes___bird_9_out_33), .col29(pipes___bird_9_out_34),
    .col30(pipes___bird_9_out_35), .col31(pipes___bird_9_out_36));
  DotMatrix #(.matrixcols(32), .matrixrows(32)) dotmatrix_38 (
    .col0(pipes___bird_10_out_5), .col1(pipes___bird_10_out_6), .col2(pipes___bird_10_out_7),
    .col3(pipes___bird_10_out_8), .col4(pipes___bird_10_out_9), .col5(pipes___bird_10_out_10),
    .col6(pipes___bird_10_out_11), .col7(pipes___bird_10_out_12), .col8(pipes___bird_10_out_13),
    .col9(pipes___bird_10_out_14), .col10(pipes___bird_10_out_15), .col11(pipes___bird_10_out_16),
    .col12(pipes___bird_10_out_17), .col13(pipes___bird_10_out_18), .col14(pipes___bird_10_out_19),
    .col15(pipes___bird_10_out_20), .col16(pipes___bird_10_out_21), .col17(pipes___bird_10_out_22),
    .col18(pipes___bird_10_out_23), .col19(pipes___bird_10_out_24), .col20(pipes___bird_10_out_25),
    .col21(pipes___bird_10_out_26), .col22(pipes___bird_10_out_27), .col23(pipes___bird_10_out_28),
    .col24(pipes___bird_10_out_29), .col25(pipes___bird_10_out_30), .col26(pipes___bird_10_out_31),
    .col27(pipes___bird_10_out_32), .col28(pipes___bird_10_out_33), .col29(pipes___bird_10_out_34),
    .col30(pipes___bird_10_out_35), .col31(pipes___bird_10_out_36));
  DotMatrix #(.matrixcols(32), .matrixrows(32)) dotmatrix_39 (
    .col0(pipes___bird_11_out_5), .col1(pipes___bird_11_out_6), .col2(pipes___bird_11_out_7),
    .col3(pipes___bird_11_out_8), .col4(pipes___bird_11_out_9), .col5(pipes___bird_11_out_10),
    .col6(pipes___bird_11_out_11), .col7(pipes___bird_11_out_12), .col8(pipes___bird_11_out_13),
    .col9(pipes___bird_11_out_14), .col10(pipes___bird_11_out_15), .col11(pipes___bird_11_out_16),
    .col12(pipes___bird_11_out_17), .col13(pipes___bird_11_out_18), .col14(pipes___bird_11_out_19),
    .col15(pipes___bird_11_out_20), .col16(pipes___bird_11_out_21), .col17(pipes___bird_11_out_22),
    .col18(pipes___bird_11_out_23), .col19(pipes___bird_11_out_24), .col20(pipes___bird_11_out_25),
    .col21(pipes___bird_11_out_26), .col22(pipes___bird_11_out_27), .col23(pipes___bird_11_out_28),
    .col24(pipes___bird_11_out_29), .col25(pipes___bird_11_out_30), .col26(pipes___bird_11_out_31),
    .col27(pipes___bird_11_out_32), .col28(pipes___bird_11_out_33), .col29(pipes___bird_11_out_34),
    .col30(pipes___bird_11_out_35), .col31(pipes___bird_11_out_36));
  DotMatrix #(.matrixcols(32), .matrixrows(32)) dotmatrix_40 (
    .col0(pipes___bird_12_out_5), .col1(pipes___bird_12_out_6), .col2(pipes___bird_12_out_7),
    .col3(pipes___bird_12_out_8), .col4(pipes___bird_12_out_9), .col5(pipes___bird_12_out_10),
    .col6(pipes___bird_12_out_11), .col7(pipes___bird_12_out_12), .col8(pipes___bird_12_out_13),
    .col9(pipes___bird_12_out_14), .col10(pipes___bird_12_out_15), .col11(pipes___bird_12_out_16),
    .col12(pipes___bird_12_out_17), .col13(pipes___bird_12_out_18), .col14(pipes___bird_12_out_19),
    .col15(pipes___bird_12_out_20), .col16(pipes___bird_12_out_21), .col17(pipes___bird_12_out_22),
    .col18(pipes___bird_12_out_23), .col19(pipes___bird_12_out_24), .col20(pipes___bird_12_out_25),
    .col21(pipes___bird_12_out_26), .col22(pipes___bird_12_out_27), .col23(pipes___bird_12_out_28),
    .col24(pipes___bird_12_out_29), .col25(pipes___bird_12_out_30), .col26(pipes___bird_12_out_31),
    .col27(pipes___bird_12_out_32), .col28(pipes___bird_12_out_33), .col29(pipes___bird_12_out_34),
    .col30(pipes___bird_12_out_35), .col31(pipes___bird_12_out_36));
  DotMatrix #(.matrixcols(32), .matrixrows(32)) dotmatrix_41 (
    .col0({32{1'b1}}), .col1({32{1'b1}}), .col2({32{1'b1}}), .col3({32{1'b1}}), .col4({32{1'b1}}),
    .col5({32{1'b1}}), .col6({32{1'b1}}), .col7({32{1'b1}}), .col8({32{1'b1}}), .col9({32{1'b1}}),
    .col10({32{1'b1}}), .col11({32{1'b1}}), .col12({32{1'b1}}), .col13({32{1'b1}}), .col14({32{1'b1}}),
    .col15({32{1'b1}}), .col16({32{1'b1}}), .col17({32{1'b1}}), .col18({32{1'b1}}), .col19({32{1'b1}}),
    .col20({32{1'b1}}), .col21({32{1'b1}}), .col22({32{1'b1}}), .col23({32{1'b1}}), .col24({32{1'b1}}),
    .col25({32{1'b1}}), .col26({32{1'b1}}), .col27({32{1'b1}}), .col28({32{1'b1}}), .col29({32{1'b1}}),
    .col30({32{1'b1}}), .col31({32{1'b1}}));
  DotMatrix #(.matrixcols(32), .matrixrows(32)) dotmatrix_42 (
    .col0({32{1'b1}}), .col1({32{1'b1}}), .col2({32{1'b1}}), .col3({32{1'b1}}), .col4({32{1'b1}}),
    .col5({32{1'b1}}), .col6({32{1'b1}}), .col7({32{1'b1}}), .col8({32{1'b1}}), .col9({32{1'b1}}),
    .col10({32{1'b1}}), .col11({32{1'b1}}), .col12({32{1'b1}}), .col13({32{1'b1}}), .col14({32{1'b1}}),
    .col15({32{1'b1}}), .col16({32{1'b1}}), .col17({32{1'b1}}), .col18({32{1'b1}}), .col19({32{1'b1}}),
    .col20({32{1'b1}}), .col21({32{1'b1}}), .col22({32{1'b1}}), .col23({32{1'b1}}), .col24({32{1'b1}}),
    .col25({32{1'b1}}), .col26({32{1'b1}}), .col27({32{1'b1}}), .col28({32{1'b1}}), .col29({32{1'b1}}),
    .col30({32{1'b1}}), .col31({32{1'b1}}));
  pipes pipes_25 (
    .out_5(pipes_25_out_5), .out_6(pipes_25_out_6), .out_7(pipes_25_out_7), .out_8(pipes_25_out_8),
    .out_9(pipes_25_out_9), .out_10(pipes_25_out_10), .out_11(pipes_25_out_11), .out_12(pipes_25_out_12),
    .out_13(pipes_25_out_13), .out_14(pipes_25_out_14), .out_15(pipes_25_out_15), .out_16(pipes_25_out_16),
    .out_17(pipes_25_out_17), .out_18(pipes_25_out_18), .out_19(pipes_25_out_19), .out_20(pipes_25_out_20),
    .out_21(pipes_25_out_21), .out_22(pipes_25_out_22), .out_23(pipes_25_out_23), .out_24(pipes_25_out_24),
    .out_25(pipes_25_out_25), .out_26(pipes_25_out_26), .out_27(pipes_25_out_27), .out_28(pipes_25_out_28),
    .out_29(pipes_25_out_29), .out_30(pipes_25_out_30), .out_31(pipes_25_out_31), .out_32(pipes_25_out_32),
    .out_33(pipes_25_out_33), .out_34(pipes_25_out_34), .out_35(pipes_25_out_35), .out_36(pipes_25_out_36),
    .pipe(pipes_37_pipe_2), .pipe_2(pipes_25_pipe_2), .signal(pipes_37_signal_2),
    .signal_2(pipes_25_signal_2), .bird_1(pipes_37_bird_1_2), .bird_1_2(pipes_25_bird_1_2),
    .bird_2(pipes_37_bird), .bird(pipes_25_bird));
  DotMatrix #(.matrixcols(32), .matrixrows(32)) dotmatrix_43 (
    .col0(pipes_25_out_5), .col1(pipes_25_out_6), .col2(pipes_25_out_7), .col3(pipes_25_out_8),
    .col4(pipes_25_out_9), .col5(pipes_25_out_10), .col6(pipes_25_out_11), .col7(pipes_25_out_12),
    .col8(pipes_25_out_13), .col9(pipes_25_out_14), .col10(pipes_25_out_15), .col11(pipes_25_out_16),
    .col12(pipes_25_out_17), .col13(pipes_25_out_18), .col14(pipes_25_out_19), .col15(pipes_25_out_20),
    .col16(pipes_25_out_21), .col17(pipes_25_out_22), .col18(pipes_25_out_23), .col19(pipes_25_out_24),
    .col20(pipes_25_out_25), .col21(pipes_25_out_26), .col22(pipes_25_out_27), .col23(pipes_25_out_28),
    .col24(pipes_25_out_29), .col25(pipes_25_out_30), .col26(pipes_25_out_31), .col27(pipes_25_out_32),
    .col28(pipes_25_out_33), .col29(pipes_25_out_34), .col30(pipes_25_out_35), .col31(pipes_25_out_36));
  pipes___bird pipes___bird_1 (
    .pipe_2(pipes___bird_1_pipe_2), .signal(pipes_25_signal_2), .bird_1(pipes_25_bird_1_2),
    .pipe(pipes_25_pipe_2), .signal_2(pipes___bird_1_signal_2), .bird_1_2(pipes___bird_1_bird_1_2),
    .out_5(pipes___bird_1_out_5), .out_6(pipes___bird_1_out_6), .out_7(pipes___bird_1_out_7),
    .out_8(pipes___bird_1_out_8), .out_9(pipes___bird_1_out_9), .out_10(pipes___bird_1_out_10),
    .out_11(pipes___bird_1_out_11), .out_12(pipes___bird_1_out_12), .out_13(pipes___bird_1_out_13),
    .out_14(pipes___bird_1_out_14), .out_15(pipes___bird_1_out_15), .out_16(pipes___bird_1_out_16),
    .out_17(pipes___bird_1_out_17), .out_18(pipes___bird_1_out_18), .out_19(pipes___bird_1_out_19),
    .out_20(pipes___bird_1_out_20), .out_21(pipes___bird_1_out_21), .out_22(pipes___bird_1_out_22),
    .out_23(pipes___bird_1_out_23), .out_24(pipes___bird_1_out_24), .out_25(pipes___bird_1_out_25),
    .out_26(pipes___bird_1_out_26), .out_27(pipes___bird_1_out_27), .out_28(pipes___bird_1_out_28),
    .out_29(pipes___bird_1_out_29), .out_30(pipes___bird_1_out_30), .out_31(pipes___bird_1_out_31),
    .out_32(pipes___bird_1_out_32), .out_33(pipes___bird_1_out_33), .out_34(pipes___bird_1_out_34),
    .out_35(pipes___bird_1_out_35), .out_36(pipes___bird_1_out_36), .bird_2(pipes_25_bird),
    .bird_2_2(pipes___bird_1_bird_2_2));
  DotMatrix #(.matrixcols(32), .matrixrows(32)) dotmatrix_44 (
    .col0(pipes_26_out_5), .col1(pipes_26_out_6), .col2(pipes_26_out_7), .col3(pipes_26_out_8),
    .col4(pipes_26_out_9), .col5(pipes_26_out_10), .col6(pipes_26_out_11), .col7(pipes_26_out_12),
    .col8(pipes_26_out_13), .col9(pipes_26_out_14), .col10(pipes_26_out_15), .col11(pipes_26_out_16),
    .col12(pipes_26_out_17), .col13(pipes_26_out_18), .col14(pipes_26_out_19), .col15(pipes_26_out_20),
    .col16(pipes_26_out_21), .col17(pipes_26_out_22), .col18(pipes_26_out_23), .col19(pipes_26_out_24),
    .col20(pipes_26_out_25), .col21(pipes_26_out_26), .col22(pipes_26_out_27), .col23(pipes_26_out_28),
    .col24(pipes_26_out_29), .col25(pipes_26_out_30), .col26(pipes_26_out_31), .col27(pipes_26_out_32),
    .col28(pipes_26_out_33), .col29(pipes_26_out_34), .col30(pipes_26_out_35), .col31(pipes_26_out_36));
  pipes pipes_26 (
    .out_5(pipes_26_out_5), .out_6(pipes_26_out_6), .out_7(pipes_26_out_7), .out_8(pipes_26_out_8),
    .out_9(pipes_26_out_9), .out_10(pipes_26_out_10), .out_11(pipes_26_out_11), .out_12(pipes_26_out_12),
    .out_13(pipes_26_out_13), .out_14(pipes_26_out_14), .out_15(pipes_26_out_15), .out_16(pipes_26_out_16),
    .out_17(pipes_26_out_17), .out_18(pipes_26_out_18), .out_19(pipes_26_out_19), .out_20(pipes_26_out_20),
    .out_21(pipes_26_out_21), .out_22(pipes_26_out_22), .out_23(pipes_26_out_23), .out_24(pipes_26_out_24),
    .out_25(pipes_26_out_25), .out_26(pipes_26_out_26), .out_27(pipes_26_out_27), .out_28(pipes_26_out_28),
    .out_29(pipes_26_out_29), .out_30(pipes_26_out_30), .out_31(pipes_26_out_31), .out_32(pipes_26_out_32),
    .out_33(pipes_26_out_33), .out_34(pipes_26_out_34), .out_35(pipes_26_out_35), .out_36(pipes_26_out_36),
    .pipe(pipes_38_pipe_2), .pipe_2(pipes_26_pipe_2), .signal(pipes_38_signal_2),
    .signal_2(pipes_26_signal_2), .bird_1(pipes_38_bird_1_2), .bird_1_2(pipes_26_bird_1_2),
    .bird_2(pipes_38_bird), .bird(pipes_26_bird));
  pipes___bird pipes___bird_2 (
    .pipe_2(pipes___bird_2_pipe_2), .signal(pipes_26_signal_2), .bird_1(pipes_26_bird_1_2),
    .pipe(pipes_26_pipe_2), .signal_2(pipes___bird_2_signal_2), .bird_1_2(pipes___bird_2_bird_1_2),
    .out_5(pipes___bird_2_out_5), .out_6(pipes___bird_2_out_6), .out_7(pipes___bird_2_out_7),
    .out_8(pipes___bird_2_out_8), .out_9(pipes___bird_2_out_9), .out_10(pipes___bird_2_out_10),
    .out_11(pipes___bird_2_out_11), .out_12(pipes___bird_2_out_12), .out_13(pipes___bird_2_out_13),
    .out_14(pipes___bird_2_out_14), .out_15(pipes___bird_2_out_15), .out_16(pipes___bird_2_out_16),
    .out_17(pipes___bird_2_out_17), .out_18(pipes___bird_2_out_18), .out_19(pipes___bird_2_out_19),
    .out_20(pipes___bird_2_out_20), .out_21(pipes___bird_2_out_21), .out_22(pipes___bird_2_out_22),
    .out_23(pipes___bird_2_out_23), .out_24(pipes___bird_2_out_24), .out_25(pipes___bird_2_out_25),
    .out_26(pipes___bird_2_out_26), .out_27(pipes___bird_2_out_27), .out_28(pipes___bird_2_out_28),
    .out_29(pipes___bird_2_out_29), .out_30(pipes___bird_2_out_30), .out_31(pipes___bird_2_out_31),
    .out_32(pipes___bird_2_out_32), .out_33(pipes___bird_2_out_33), .out_34(pipes___bird_2_out_34),
    .out_35(pipes___bird_2_out_35), .out_36(pipes___bird_2_out_36), .bird_2(pipes_26_bird),
    .bird_2_2(pipes___bird_2_bird_2_2));
  pipes pipes_27 (
    .out_5(pipes_27_out_5), .out_6(pipes_27_out_6), .out_7(pipes_27_out_7), .out_8(pipes_27_out_8),
    .out_9(pipes_27_out_9), .out_10(pipes_27_out_10), .out_11(pipes_27_out_11), .out_12(pipes_27_out_12),
    .out_13(pipes_27_out_13), .out_14(pipes_27_out_14), .out_15(pipes_27_out_15), .out_16(pipes_27_out_16),
    .out_17(pipes_27_out_17), .out_18(pipes_27_out_18), .out_19(pipes_27_out_19), .out_20(pipes_27_out_20),
    .out_21(pipes_27_out_21), .out_22(pipes_27_out_22), .out_23(pipes_27_out_23), .out_24(pipes_27_out_24),
    .out_25(pipes_27_out_25), .out_26(pipes_27_out_26), .out_27(pipes_27_out_27), .out_28(pipes_27_out_28),
    .out_29(pipes_27_out_29), .out_30(pipes_27_out_30), .out_31(pipes_27_out_31), .out_32(pipes_27_out_32),
    .out_33(pipes_27_out_33), .out_34(pipes_27_out_34), .out_35(pipes_27_out_35), .out_36(pipes_27_out_36),
    .pipe(pipes_39_pipe_2), .pipe_2(pipes_27_pipe_2), .signal(pipes_39_signal_2),
    .signal_2(pipes_27_signal_2), .bird_1(pipes_39_bird_1_2), .bird_1_2(pipes_27_bird_1_2),
    .bird_2(pipes_39_bird), .bird(pipes_27_bird));
  DotMatrix #(.matrixcols(32), .matrixrows(32)) dotmatrix_45 (
    .col0(pipes_27_out_5), .col1(pipes_27_out_6), .col2(pipes_27_out_7), .col3(pipes_27_out_8),
    .col4(pipes_27_out_9), .col5(pipes_27_out_10), .col6(pipes_27_out_11), .col7(pipes_27_out_12),
    .col8(pipes_27_out_13), .col9(pipes_27_out_14), .col10(pipes_27_out_15), .col11(pipes_27_out_16),
    .col12(pipes_27_out_17), .col13(pipes_27_out_18), .col14(pipes_27_out_19), .col15(pipes_27_out_20),
    .col16(pipes_27_out_21), .col17(pipes_27_out_22), .col18(pipes_27_out_23), .col19(pipes_27_out_24),
    .col20(pipes_27_out_25), .col21(pipes_27_out_26), .col22(pipes_27_out_27), .col23(pipes_27_out_28),
    .col24(pipes_27_out_29), .col25(pipes_27_out_30), .col26(pipes_27_out_31), .col27(pipes_27_out_32),
    .col28(pipes_27_out_33), .col29(pipes_27_out_34), .col30(pipes_27_out_35), .col31(pipes_27_out_36));
  pipes___bird pipes___bird_3 (
    .pipe_2(pipes___bird_3_pipe_2), .signal(pipes_27_signal_2), .bird_1(pipes_27_bird_1_2),
    .pipe(pipes_27_pipe_2), .signal_2(pipes___bird_3_signal_2), .bird_1_2(pipes___bird_3_bird_1_2),
    .out_5(pipes___bird_3_out_5), .out_6(pipes___bird_3_out_6), .out_7(pipes___bird_3_out_7),
    .out_8(pipes___bird_3_out_8), .out_9(pipes___bird_3_out_9), .out_10(pipes___bird_3_out_10),
    .out_11(pipes___bird_3_out_11), .out_12(pipes___bird_3_out_12), .out_13(pipes___bird_3_out_13),
    .out_14(pipes___bird_3_out_14), .out_15(pipes___bird_3_out_15), .out_16(pipes___bird_3_out_16),
    .out_17(pipes___bird_3_out_17), .out_18(pipes___bird_3_out_18), .out_19(pipes___bird_3_out_19),
    .out_20(pipes___bird_3_out_20), .out_21(pipes___bird_3_out_21), .out_22(pipes___bird_3_out_22),
    .out_23(pipes___bird_3_out_23), .out_24(pipes___bird_3_out_24), .out_25(pipes___bird_3_out_25),
    .out_26(pipes___bird_3_out_26), .out_27(pipes___bird_3_out_27), .out_28(pipes___bird_3_out_28),
    .out_29(pipes___bird_3_out_29), .out_30(pipes___bird_3_out_30), .out_31(pipes___bird_3_out_31),
    .out_32(pipes___bird_3_out_32), .out_33(pipes___bird_3_out_33), .out_34(pipes___bird_3_out_34),
    .out_35(pipes___bird_3_out_35), .out_36(pipes___bird_3_out_36), .bird_2(pipes_27_bird),
    .bird_2_2(pipes___bird_3_bird_2_2));
  pipes pipes_28 (
    .out_5(pipes_28_out_5), .out_6(pipes_28_out_6), .out_7(pipes_28_out_7), .out_8(pipes_28_out_8),
    .out_9(pipes_28_out_9), .out_10(pipes_28_out_10), .out_11(pipes_28_out_11), .out_12(pipes_28_out_12),
    .out_13(pipes_28_out_13), .out_14(pipes_28_out_14), .out_15(pipes_28_out_15), .out_16(pipes_28_out_16),
    .out_17(pipes_28_out_17), .out_18(pipes_28_out_18), .out_19(pipes_28_out_19), .out_20(pipes_28_out_20),
    .out_21(pipes_28_out_21), .out_22(pipes_28_out_22), .out_23(pipes_28_out_23), .out_24(pipes_28_out_24),
    .out_25(pipes_28_out_25), .out_26(pipes_28_out_26), .out_27(pipes_28_out_27), .out_28(pipes_28_out_28),
    .out_29(pipes_28_out_29), .out_30(pipes_28_out_30), .out_31(pipes_28_out_31), .out_32(pipes_28_out_32),
    .out_33(pipes_28_out_33), .out_34(pipes_28_out_34), .out_35(pipes_28_out_35), .out_36(pipes_28_out_36),
    .pipe(pipes_40_pipe_2), .pipe_2(pipes_28_pipe_2), .signal(pipes_40_signal_2),
    .signal_2(pipes_28_signal_2), .bird_1(pipes_40_bird_1_2), .bird_1_2(pipes_28_bird_1_2),
    .bird_2(pipes_40_bird), .bird(pipes_28_bird));
  DotMatrix #(.matrixcols(32), .matrixrows(32)) dotmatrix_46 (
    .col0(pipes_28_out_5), .col1(pipes_28_out_6), .col2(pipes_28_out_7), .col3(pipes_28_out_8),
    .col4(pipes_28_out_9), .col5(pipes_28_out_10), .col6(pipes_28_out_11), .col7(pipes_28_out_12),
    .col8(pipes_28_out_13), .col9(pipes_28_out_14), .col10(pipes_28_out_15), .col11(pipes_28_out_16),
    .col12(pipes_28_out_17), .col13(pipes_28_out_18), .col14(pipes_28_out_19), .col15(pipes_28_out_20),
    .col16(pipes_28_out_21), .col17(pipes_28_out_22), .col18(pipes_28_out_23), .col19(pipes_28_out_24),
    .col20(pipes_28_out_25), .col21(pipes_28_out_26), .col22(pipes_28_out_27), .col23(pipes_28_out_28),
    .col24(pipes_28_out_29), .col25(pipes_28_out_30), .col26(pipes_28_out_31), .col27(pipes_28_out_32),
    .col28(pipes_28_out_33), .col29(pipes_28_out_34), .col30(pipes_28_out_35), .col31(pipes_28_out_36));
  pipes___bird pipes___bird_4 (
    .pipe_2(pipes___bird_4_pipe_2), .signal(pipes_28_signal_2), .bird_1(pipes_28_bird_1_2),
    .pipe(pipes_28_pipe_2), .signal_2(pipes___bird_4_signal_2), .bird_1_2(pipes___bird_4_bird_1_2),
    .out_5(pipes___bird_4_out_5), .out_6(pipes___bird_4_out_6), .out_7(pipes___bird_4_out_7),
    .out_8(pipes___bird_4_out_8), .out_9(pipes___bird_4_out_9), .out_10(pipes___bird_4_out_10),
    .out_11(pipes___bird_4_out_11), .out_12(pipes___bird_4_out_12), .out_13(pipes___bird_4_out_13),
    .out_14(pipes___bird_4_out_14), .out_15(pipes___bird_4_out_15), .out_16(pipes___bird_4_out_16),
    .out_17(pipes___bird_4_out_17), .out_18(pipes___bird_4_out_18), .out_19(pipes___bird_4_out_19),
    .out_20(pipes___bird_4_out_20), .out_21(pipes___bird_4_out_21), .out_22(pipes___bird_4_out_22),
    .out_23(pipes___bird_4_out_23), .out_24(pipes___bird_4_out_24), .out_25(pipes___bird_4_out_25),
    .out_26(pipes___bird_4_out_26), .out_27(pipes___bird_4_out_27), .out_28(pipes___bird_4_out_28),
    .out_29(pipes___bird_4_out_29), .out_30(pipes___bird_4_out_30), .out_31(pipes___bird_4_out_31),
    .out_32(pipes___bird_4_out_32), .out_33(pipes___bird_4_out_33), .out_34(pipes___bird_4_out_34),
    .out_35(pipes___bird_4_out_35), .out_36(pipes___bird_4_out_36), .bird_2(pipes_28_bird),
    .bird_2_2(pipes___bird_4_bird_2_2));
  pipes pipes_29 (
    .out_5(pipes_29_out_5), .out_6(pipes_29_out_6), .out_7(pipes_29_out_7), .out_8(pipes_29_out_8),
    .out_9(pipes_29_out_9), .out_10(pipes_29_out_10), .out_11(pipes_29_out_11), .out_12(pipes_29_out_12),
    .out_13(pipes_29_out_13), .out_14(pipes_29_out_14), .out_15(pipes_29_out_15), .out_16(pipes_29_out_16),
    .out_17(pipes_29_out_17), .out_18(pipes_29_out_18), .out_19(pipes_29_out_19), .out_20(pipes_29_out_20),
    .out_21(pipes_29_out_21), .out_22(pipes_29_out_22), .out_23(pipes_29_out_23), .out_24(pipes_29_out_24),
    .out_25(pipes_29_out_25), .out_26(pipes_29_out_26), .out_27(pipes_29_out_27), .out_28(pipes_29_out_28),
    .out_29(pipes_29_out_29), .out_30(pipes_29_out_30), .out_31(pipes_29_out_31), .out_32(pipes_29_out_32),
    .out_33(pipes_29_out_33), .out_34(pipes_29_out_34), .out_35(pipes_29_out_35), .out_36(pipes_29_out_36),
    .pipe(pipes_41_pipe_2), .pipe_2(pipes_29_pipe_2), .signal(pipes_41_signal_2),
    .signal_2(pipes_29_signal_2), .bird_1(pipes_41_bird_1_2), .bird_1_2(pipes_29_bird_1_2),
    .bird_2(pipes_41_bird), .bird(pipes_29_bird));
  DotMatrix #(.matrixcols(32), .matrixrows(32)) dotmatrix_47 (
    .col0(pipes_29_out_5), .col1(pipes_29_out_6), .col2(pipes_29_out_7), .col3(pipes_29_out_8),
    .col4(pipes_29_out_9), .col5(pipes_29_out_10), .col6(pipes_29_out_11), .col7(pipes_29_out_12),
    .col8(pipes_29_out_13), .col9(pipes_29_out_14), .col10(pipes_29_out_15), .col11(pipes_29_out_16),
    .col12(pipes_29_out_17), .col13(pipes_29_out_18), .col14(pipes_29_out_19), .col15(pipes_29_out_20),
    .col16(pipes_29_out_21), .col17(pipes_29_out_22), .col18(pipes_29_out_23), .col19(pipes_29_out_24),
    .col20(pipes_29_out_25), .col21(pipes_29_out_26), .col22(pipes_29_out_27), .col23(pipes_29_out_28),
    .col24(pipes_29_out_29), .col25(pipes_29_out_30), .col26(pipes_29_out_31), .col27(pipes_29_out_32),
    .col28(pipes_29_out_33), .col29(pipes_29_out_34), .col30(pipes_29_out_35), .col31(pipes_29_out_36));
  pipes___bird pipes___bird_5 (
    .pipe_2(pipes___bird_5_pipe_2), .signal(pipes_29_signal_2), .bird_1(pipes_29_bird_1_2),
    .pipe(pipes_29_pipe_2), .signal_2(pipes___bird_5_signal_2), .bird_1_2(pipes___bird_5_bird_1_2),
    .out_5(pipes___bird_5_out_5), .out_6(pipes___bird_5_out_6), .out_7(pipes___bird_5_out_7),
    .out_8(pipes___bird_5_out_8), .out_9(pipes___bird_5_out_9), .out_10(pipes___bird_5_out_10),
    .out_11(pipes___bird_5_out_11), .out_12(pipes___bird_5_out_12), .out_13(pipes___bird_5_out_13),
    .out_14(pipes___bird_5_out_14), .out_15(pipes___bird_5_out_15), .out_16(pipes___bird_5_out_16),
    .out_17(pipes___bird_5_out_17), .out_18(pipes___bird_5_out_18), .out_19(pipes___bird_5_out_19),
    .out_20(pipes___bird_5_out_20), .out_21(pipes___bird_5_out_21), .out_22(pipes___bird_5_out_22),
    .out_23(pipes___bird_5_out_23), .out_24(pipes___bird_5_out_24), .out_25(pipes___bird_5_out_25),
    .out_26(pipes___bird_5_out_26), .out_27(pipes___bird_5_out_27), .out_28(pipes___bird_5_out_28),
    .out_29(pipes___bird_5_out_29), .out_30(pipes___bird_5_out_30), .out_31(pipes___bird_5_out_31),
    .out_32(pipes___bird_5_out_32), .out_33(pipes___bird_5_out_33), .out_34(pipes___bird_5_out_34),
    .out_35(pipes___bird_5_out_35), .out_36(pipes___bird_5_out_36), .bird_2(pipes_29_bird),
    .bird_2_2(pipes___bird_5_bird_2_2));
  DotMatrix #(.matrixcols(32), .matrixrows(32)) dotmatrix_48 (
    .col0(pipes_30_out_5), .col1(pipes_30_out_6), .col2(pipes_30_out_7), .col3(pipes_30_out_8),
    .col4(pipes_30_out_9), .col5(pipes_30_out_10), .col6(pipes_30_out_11), .col7(pipes_30_out_12),
    .col8(pipes_30_out_13), .col9(pipes_30_out_14), .col10(pipes_30_out_15), .col11(pipes_30_out_16),
    .col12(pipes_30_out_17), .col13(pipes_30_out_18), .col14(pipes_30_out_19), .col15(pipes_30_out_20),
    .col16(pipes_30_out_21), .col17(pipes_30_out_22), .col18(pipes_30_out_23), .col19(pipes_30_out_24),
    .col20(pipes_30_out_25), .col21(pipes_30_out_26), .col22(pipes_30_out_27), .col23(pipes_30_out_28),
    .col24(pipes_30_out_29), .col25(pipes_30_out_30), .col26(pipes_30_out_31), .col27(pipes_30_out_32),
    .col28(pipes_30_out_33), .col29(pipes_30_out_34), .col30(pipes_30_out_35), .col31(pipes_30_out_36));
  pipes pipes_30 (
    .out_5(pipes_30_out_5), .out_6(pipes_30_out_6), .out_7(pipes_30_out_7), .out_8(pipes_30_out_8),
    .out_9(pipes_30_out_9), .out_10(pipes_30_out_10), .out_11(pipes_30_out_11), .out_12(pipes_30_out_12),
    .out_13(pipes_30_out_13), .out_14(pipes_30_out_14), .out_15(pipes_30_out_15), .out_16(pipes_30_out_16),
    .out_17(pipes_30_out_17), .out_18(pipes_30_out_18), .out_19(pipes_30_out_19), .out_20(pipes_30_out_20),
    .out_21(pipes_30_out_21), .out_22(pipes_30_out_22), .out_23(pipes_30_out_23), .out_24(pipes_30_out_24),
    .out_25(pipes_30_out_25), .out_26(pipes_30_out_26), .out_27(pipes_30_out_27), .out_28(pipes_30_out_28),
    .out_29(pipes_30_out_29), .out_30(pipes_30_out_30), .out_31(pipes_30_out_31), .out_32(pipes_30_out_32),
    .out_33(pipes_30_out_33), .out_34(pipes_30_out_34), .out_35(pipes_30_out_35), .out_36(pipes_30_out_36),
    .pipe(pipes_42_pipe_2), .pipe_2(pipes_30_pipe_2), .signal(pipes_42_signal_2),
    .signal_2(pipes_30_signal_2), .bird_1(pipes_42_bird_1_2), .bird_1_2(pipes_30_bird_1_2),
    .bird_2(pipes_42_bird), .bird(pipes_30_bird));
  pipes___bird pipes___bird_6 (
    .pipe_2(pipes___bird_6_pipe_2), .signal(pipes_30_signal_2), .bird_1(pipes_30_bird_1_2),
    .pipe(pipes_30_pipe_2), .signal_2(pipes___bird_6_signal_2), .bird_1_2(pipes___bird_6_bird_1_2),
    .out_5(pipes___bird_6_out_5), .out_6(pipes___bird_6_out_6), .out_7(pipes___bird_6_out_7),
    .out_8(pipes___bird_6_out_8), .out_9(pipes___bird_6_out_9), .out_10(pipes___bird_6_out_10),
    .out_11(pipes___bird_6_out_11), .out_12(pipes___bird_6_out_12), .out_13(pipes___bird_6_out_13),
    .out_14(pipes___bird_6_out_14), .out_15(pipes___bird_6_out_15), .out_16(pipes___bird_6_out_16),
    .out_17(pipes___bird_6_out_17), .out_18(pipes___bird_6_out_18), .out_19(pipes___bird_6_out_19),
    .out_20(pipes___bird_6_out_20), .out_21(pipes___bird_6_out_21), .out_22(pipes___bird_6_out_22),
    .out_23(pipes___bird_6_out_23), .out_24(pipes___bird_6_out_24), .out_25(pipes___bird_6_out_25),
    .out_26(pipes___bird_6_out_26), .out_27(pipes___bird_6_out_27), .out_28(pipes___bird_6_out_28),
    .out_29(pipes___bird_6_out_29), .out_30(pipes___bird_6_out_30), .out_31(pipes___bird_6_out_31),
    .out_32(pipes___bird_6_out_32), .out_33(pipes___bird_6_out_33), .out_34(pipes___bird_6_out_34),
    .out_35(pipes___bird_6_out_35), .out_36(pipes___bird_6_out_36), .bird_2(pipes_30_bird),
    .bird_2_2(pipes___bird_6_bird_2_2));
  DotMatrix #(.matrixcols(32), .matrixrows(32)) dotmatrix_49 (
    .col0(pipes_31_out_5), .col1(pipes_31_out_6), .col2(pipes_31_out_7), .col3(pipes_31_out_8),
    .col4(pipes_31_out_9), .col5(pipes_31_out_10), .col6(pipes_31_out_11), .col7(pipes_31_out_12),
    .col8(pipes_31_out_13), .col9(pipes_31_out_14), .col10(pipes_31_out_15), .col11(pipes_31_out_16),
    .col12(pipes_31_out_17), .col13(pipes_31_out_18), .col14(pipes_31_out_19), .col15(pipes_31_out_20),
    .col16(pipes_31_out_21), .col17(pipes_31_out_22), .col18(pipes_31_out_23), .col19(pipes_31_out_24),
    .col20(pipes_31_out_25), .col21(pipes_31_out_26), .col22(pipes_31_out_27), .col23(pipes_31_out_28),
    .col24(pipes_31_out_29), .col25(pipes_31_out_30), .col26(pipes_31_out_31), .col27(pipes_31_out_32),
    .col28(pipes_31_out_33), .col29(pipes_31_out_34), .col30(pipes_31_out_35), .col31(pipes_31_out_36));
  pipes pipes_31 (
    .out_5(pipes_31_out_5), .out_6(pipes_31_out_6), .out_7(pipes_31_out_7), .out_8(pipes_31_out_8),
    .out_9(pipes_31_out_9), .out_10(pipes_31_out_10), .out_11(pipes_31_out_11), .out_12(pipes_31_out_12),
    .out_13(pipes_31_out_13), .out_14(pipes_31_out_14), .out_15(pipes_31_out_15), .out_16(pipes_31_out_16),
    .out_17(pipes_31_out_17), .out_18(pipes_31_out_18), .out_19(pipes_31_out_19), .out_20(pipes_31_out_20),
    .out_21(pipes_31_out_21), .out_22(pipes_31_out_22), .out_23(pipes_31_out_23), .out_24(pipes_31_out_24),
    .out_25(pipes_31_out_25), .out_26(pipes_31_out_26), .out_27(pipes_31_out_27), .out_28(pipes_31_out_28),
    .out_29(pipes_31_out_29), .out_30(pipes_31_out_30), .out_31(pipes_31_out_31), .out_32(pipes_31_out_32),
    .out_33(pipes_31_out_33), .out_34(pipes_31_out_34), .out_35(pipes_31_out_35), .out_36(pipes_31_out_36),
    .pipe(pipes_43_pipe_2), .pipe_2(pipes_31_pipe_2), .signal(pipes_43_signal_2),
    .signal_2(pipes_31_signal_2), .bird_1(pipes_43_bird_1_2), .bird_1_2(pipes_31_bird_1_2),
    .bird_2(pipes_43_bird), .bird(pipes_31_bird));
  pipes___bird pipes___bird_7 (
    .pipe_2(pipes___bird_7_pipe_2), .signal(pipes_31_signal_2), .bird_1(pipes_31_bird_1_2),
    .pipe(pipes_31_pipe_2), .signal_2(pipes___bird_7_signal_2), .bird_1_2(pipes___bird_7_bird_1_2),
    .out_5(pipes___bird_7_out_5), .out_6(pipes___bird_7_out_6), .out_7(pipes___bird_7_out_7),
    .out_8(pipes___bird_7_out_8), .out_9(pipes___bird_7_out_9), .out_10(pipes___bird_7_out_10),
    .out_11(pipes___bird_7_out_11), .out_12(pipes___bird_7_out_12), .out_13(pipes___bird_7_out_13),
    .out_14(pipes___bird_7_out_14), .out_15(pipes___bird_7_out_15), .out_16(pipes___bird_7_out_16),
    .out_17(pipes___bird_7_out_17), .out_18(pipes___bird_7_out_18), .out_19(pipes___bird_7_out_19),
    .out_20(pipes___bird_7_out_20), .out_21(pipes___bird_7_out_21), .out_22(pipes___bird_7_out_22),
    .out_23(pipes___bird_7_out_23), .out_24(pipes___bird_7_out_24), .out_25(pipes___bird_7_out_25),
    .out_26(pipes___bird_7_out_26), .out_27(pipes___bird_7_out_27), .out_28(pipes___bird_7_out_28),
    .out_29(pipes___bird_7_out_29), .out_30(pipes___bird_7_out_30), .out_31(pipes___bird_7_out_31),
    .out_32(pipes___bird_7_out_32), .out_33(pipes___bird_7_out_33), .out_34(pipes___bird_7_out_34),
    .out_35(pipes___bird_7_out_35), .out_36(pipes___bird_7_out_36), .bird_2(pipes_31_bird),
    .bird_2_2(pipes___bird_7_bird_2_2));
  DotMatrix #(.matrixcols(32), .matrixrows(32)) dotmatrix_50 (
    .col0(pipes_32_out_5), .col1(pipes_32_out_6), .col2(pipes_32_out_7), .col3(pipes_32_out_8),
    .col4(pipes_32_out_9), .col5(pipes_32_out_10), .col6(pipes_32_out_11), .col7(pipes_32_out_12),
    .col8(pipes_32_out_13), .col9(pipes_32_out_14), .col10(pipes_32_out_15), .col11(pipes_32_out_16),
    .col12(pipes_32_out_17), .col13(pipes_32_out_18), .col14(pipes_32_out_19), .col15(pipes_32_out_20),
    .col16(pipes_32_out_21), .col17(pipes_32_out_22), .col18(pipes_32_out_23), .col19(pipes_32_out_24),
    .col20(pipes_32_out_25), .col21(pipes_32_out_26), .col22(pipes_32_out_27), .col23(pipes_32_out_28),
    .col24(pipes_32_out_29), .col25(pipes_32_out_30), .col26(pipes_32_out_31), .col27(pipes_32_out_32),
    .col28(pipes_32_out_33), .col29(pipes_32_out_34), .col30(pipes_32_out_35), .col31(pipes_32_out_36));
  pipes pipes_32 (
    .out_5(pipes_32_out_5), .out_6(pipes_32_out_6), .out_7(pipes_32_out_7), .out_8(pipes_32_out_8),
    .out_9(pipes_32_out_9), .out_10(pipes_32_out_10), .out_11(pipes_32_out_11), .out_12(pipes_32_out_12),
    .out_13(pipes_32_out_13), .out_14(pipes_32_out_14), .out_15(pipes_32_out_15), .out_16(pipes_32_out_16),
    .out_17(pipes_32_out_17), .out_18(pipes_32_out_18), .out_19(pipes_32_out_19), .out_20(pipes_32_out_20),
    .out_21(pipes_32_out_21), .out_22(pipes_32_out_22), .out_23(pipes_32_out_23), .out_24(pipes_32_out_24),
    .out_25(pipes_32_out_25), .out_26(pipes_32_out_26), .out_27(pipes_32_out_27), .out_28(pipes_32_out_28),
    .out_29(pipes_32_out_29), .out_30(pipes_32_out_30), .out_31(pipes_32_out_31), .out_32(pipes_32_out_32),
    .out_33(pipes_32_out_33), .out_34(pipes_32_out_34), .out_35(pipes_32_out_35), .out_36(pipes_32_out_36),
    .pipe(pipes_44_pipe_2), .pipe_2(pipes_32_pipe_2), .signal(pipes_44_signal_2),
    .signal_2(pipes_32_signal_2), .bird_1(pipes_44_bird_1_2), .bird_1_2(pipes_32_bird_1_2),
    .bird_2(pipes_44_bird), .bird(pipes_32_bird));
  pipes___bird pipes___bird_8 (
    .pipe_2(pipes___bird_8_pipe_2), .signal(pipes_32_signal_2), .bird_1(pipes_32_bird_1_2),
    .pipe(pipes_32_pipe_2), .signal_2(pipes___bird_8_signal_2), .bird_1_2(pipes___bird_8_bird_1_2),
    .out_5(pipes___bird_8_out_5), .out_6(pipes___bird_8_out_6), .out_7(pipes___bird_8_out_7),
    .out_8(pipes___bird_8_out_8), .out_9(pipes___bird_8_out_9), .out_10(pipes___bird_8_out_10),
    .out_11(pipes___bird_8_out_11), .out_12(pipes___bird_8_out_12), .out_13(pipes___bird_8_out_13),
    .out_14(pipes___bird_8_out_14), .out_15(pipes___bird_8_out_15), .out_16(pipes___bird_8_out_16),
    .out_17(pipes___bird_8_out_17), .out_18(pipes___bird_8_out_18), .out_19(pipes___bird_8_out_19),
    .out_20(pipes___bird_8_out_20), .out_21(pipes___bird_8_out_21), .out_22(pipes___bird_8_out_22),
    .out_23(pipes___bird_8_out_23), .out_24(pipes___bird_8_out_24), .out_25(pipes___bird_8_out_25),
    .out_26(pipes___bird_8_out_26), .out_27(pipes___bird_8_out_27), .out_28(pipes___bird_8_out_28),
    .out_29(pipes___bird_8_out_29), .out_30(pipes___bird_8_out_30), .out_31(pipes___bird_8_out_31),
    .out_32(pipes___bird_8_out_32), .out_33(pipes___bird_8_out_33), .out_34(pipes___bird_8_out_34),
    .out_35(pipes___bird_8_out_35), .out_36(pipes___bird_8_out_36), .bird_2(pipes_32_bird),
    .bird_2_2(pipes___bird_8_bird_2_2));
  pipes pipes_33 (
    .out_5(pipes_33_out_5), .out_6(pipes_33_out_6), .out_7(pipes_33_out_7), .out_8(pipes_33_out_8),
    .out_9(pipes_33_out_9), .out_10(pipes_33_out_10), .out_11(pipes_33_out_11), .out_12(pipes_33_out_12),
    .out_13(pipes_33_out_13), .out_14(pipes_33_out_14), .out_15(pipes_33_out_15), .out_16(pipes_33_out_16),
    .out_17(pipes_33_out_17), .out_18(pipes_33_out_18), .out_19(pipes_33_out_19), .out_20(pipes_33_out_20),
    .out_21(pipes_33_out_21), .out_22(pipes_33_out_22), .out_23(pipes_33_out_23), .out_24(pipes_33_out_24),
    .out_25(pipes_33_out_25), .out_26(pipes_33_out_26), .out_27(pipes_33_out_27), .out_28(pipes_33_out_28),
    .out_29(pipes_33_out_29), .out_30(pipes_33_out_30), .out_31(pipes_33_out_31), .out_32(pipes_33_out_32),
    .out_33(pipes_33_out_33), .out_34(pipes_33_out_34), .out_35(pipes_33_out_35), .out_36(pipes_33_out_36),
    .pipe(pipes_45_pipe_2), .pipe_2(pipes_33_pipe_2), .signal(pipes_45_signal_2),
    .signal_2(pipes_33_signal_2), .bird_1(pipes_45_bird_1_2), .bird_1_2(pipes_33_bird_1_2),
    .bird_2(pipes_45_bird), .bird(pipes_33_bird));
  DotMatrix #(.matrixcols(32), .matrixrows(32)) dotmatrix_51 (
    .col0(pipes_33_out_5), .col1(pipes_33_out_6), .col2(pipes_33_out_7), .col3(pipes_33_out_8),
    .col4(pipes_33_out_9), .col5(pipes_33_out_10), .col6(pipes_33_out_11), .col7(pipes_33_out_12),
    .col8(pipes_33_out_13), .col9(pipes_33_out_14), .col10(pipes_33_out_15), .col11(pipes_33_out_16),
    .col12(pipes_33_out_17), .col13(pipes_33_out_18), .col14(pipes_33_out_19), .col15(pipes_33_out_20),
    .col16(pipes_33_out_21), .col17(pipes_33_out_22), .col18(pipes_33_out_23), .col19(pipes_33_out_24),
    .col20(pipes_33_out_25), .col21(pipes_33_out_26), .col22(pipes_33_out_27), .col23(pipes_33_out_28),
    .col24(pipes_33_out_29), .col25(pipes_33_out_30), .col26(pipes_33_out_31), .col27(pipes_33_out_32),
    .col28(pipes_33_out_33), .col29(pipes_33_out_34), .col30(pipes_33_out_35), .col31(pipes_33_out_36));
  pipes___bird pipes___bird_9 (
    .pipe_2(pipes___bird_9_pipe_2), .signal(pipes_33_signal_2), .bird_1(pipes_33_bird_1_2),
    .pipe(pipes_33_pipe_2), .signal_2(pipes___bird_9_signal_2), .bird_1_2(pipes___bird_9_bird_1_2),
    .out_5(pipes___bird_9_out_5), .out_6(pipes___bird_9_out_6), .out_7(pipes___bird_9_out_7),
    .out_8(pipes___bird_9_out_8), .out_9(pipes___bird_9_out_9), .out_10(pipes___bird_9_out_10),
    .out_11(pipes___bird_9_out_11), .out_12(pipes___bird_9_out_12), .out_13(pipes___bird_9_out_13),
    .out_14(pipes___bird_9_out_14), .out_15(pipes___bird_9_out_15), .out_16(pipes___bird_9_out_16),
    .out_17(pipes___bird_9_out_17), .out_18(pipes___bird_9_out_18), .out_19(pipes___bird_9_out_19),
    .out_20(pipes___bird_9_out_20), .out_21(pipes___bird_9_out_21), .out_22(pipes___bird_9_out_22),
    .out_23(pipes___bird_9_out_23), .out_24(pipes___bird_9_out_24), .out_25(pipes___bird_9_out_25),
    .out_26(pipes___bird_9_out_26), .out_27(pipes___bird_9_out_27), .out_28(pipes___bird_9_out_28),
    .out_29(pipes___bird_9_out_29), .out_30(pipes___bird_9_out_30), .out_31(pipes___bird_9_out_31),
    .out_32(pipes___bird_9_out_32), .out_33(pipes___bird_9_out_33), .out_34(pipes___bird_9_out_34),
    .out_35(pipes___bird_9_out_35), .out_36(pipes___bird_9_out_36), .bird_2(pipes_33_bird),
    .bird_2_2(pipes___bird_9_bird_2_2));
  pipes pipes_34 (
    .out_5(pipes_34_out_5), .out_6(pipes_34_out_6), .out_7(pipes_34_out_7), .out_8(pipes_34_out_8),
    .out_9(pipes_34_out_9), .out_10(pipes_34_out_10), .out_11(pipes_34_out_11), .out_12(pipes_34_out_12),
    .out_13(pipes_34_out_13), .out_14(pipes_34_out_14), .out_15(pipes_34_out_15), .out_16(pipes_34_out_16),
    .out_17(pipes_34_out_17), .out_18(pipes_34_out_18), .out_19(pipes_34_out_19), .out_20(pipes_34_out_20),
    .out_21(pipes_34_out_21), .out_22(pipes_34_out_22), .out_23(pipes_34_out_23), .out_24(pipes_34_out_24),
    .out_25(pipes_34_out_25), .out_26(pipes_34_out_26), .out_27(pipes_34_out_27), .out_28(pipes_34_out_28),
    .out_29(pipes_34_out_29), .out_30(pipes_34_out_30), .out_31(pipes_34_out_31), .out_32(pipes_34_out_32),
    .out_33(pipes_34_out_33), .out_34(pipes_34_out_34), .out_35(pipes_34_out_35), .out_36(pipes_34_out_36),
    .pipe(pipes_46_pipe_2), .pipe_2(pipes_34_pipe_2), .signal(pipes_46_signal_2),
    .signal_2(pipes_34_signal_2), .bird_1(pipes_46_bird_1_2), .bird_1_2(pipes_34_bird_1_2),
    .bird_2(pipes_46_bird), .bird(pipes_34_bird));
  DotMatrix #(.matrixcols(32), .matrixrows(32)) dotmatrix_52 (
    .col0(pipes_34_out_5), .col1(pipes_34_out_6), .col2(pipes_34_out_7), .col3(pipes_34_out_8),
    .col4(pipes_34_out_9), .col5(pipes_34_out_10), .col6(pipes_34_out_11), .col7(pipes_34_out_12),
    .col8(pipes_34_out_13), .col9(pipes_34_out_14), .col10(pipes_34_out_15), .col11(pipes_34_out_16),
    .col12(pipes_34_out_17), .col13(pipes_34_out_18), .col14(pipes_34_out_19), .col15(pipes_34_out_20),
    .col16(pipes_34_out_21), .col17(pipes_34_out_22), .col18(pipes_34_out_23), .col19(pipes_34_out_24),
    .col20(pipes_34_out_25), .col21(pipes_34_out_26), .col22(pipes_34_out_27), .col23(pipes_34_out_28),
    .col24(pipes_34_out_29), .col25(pipes_34_out_30), .col26(pipes_34_out_31), .col27(pipes_34_out_32),
    .col28(pipes_34_out_33), .col29(pipes_34_out_34), .col30(pipes_34_out_35), .col31(pipes_34_out_36));
  pipes___bird pipes___bird_10 (
    .pipe_2(pipes___bird_10_pipe_2), .signal(pipes_34_signal_2), .bird_1(pipes_34_bird_1_2),
    .pipe(pipes_34_pipe_2), .signal_2(pipes___bird_10_signal_2), .bird_1_2(pipes___bird_10_bird_1_2),
    .out_5(pipes___bird_10_out_5), .out_6(pipes___bird_10_out_6), .out_7(pipes___bird_10_out_7),
    .out_8(pipes___bird_10_out_8), .out_9(pipes___bird_10_out_9), .out_10(pipes___bird_10_out_10),
    .out_11(pipes___bird_10_out_11), .out_12(pipes___bird_10_out_12), .out_13(pipes___bird_10_out_13),
    .out_14(pipes___bird_10_out_14), .out_15(pipes___bird_10_out_15), .out_16(pipes___bird_10_out_16),
    .out_17(pipes___bird_10_out_17), .out_18(pipes___bird_10_out_18), .out_19(pipes___bird_10_out_19),
    .out_20(pipes___bird_10_out_20), .out_21(pipes___bird_10_out_21), .out_22(pipes___bird_10_out_22),
    .out_23(pipes___bird_10_out_23), .out_24(pipes___bird_10_out_24), .out_25(pipes___bird_10_out_25),
    .out_26(pipes___bird_10_out_26), .out_27(pipes___bird_10_out_27), .out_28(pipes___bird_10_out_28),
    .out_29(pipes___bird_10_out_29), .out_30(pipes___bird_10_out_30), .out_31(pipes___bird_10_out_31),
    .out_32(pipes___bird_10_out_32), .out_33(pipes___bird_10_out_33), .out_34(pipes___bird_10_out_34),
    .out_35(pipes___bird_10_out_35), .out_36(pipes___bird_10_out_36), .bird_2(pipes_34_bird),
    .bird_2_2(pipes___bird_10_bird_2_2));
  DotMatrix #(.matrixcols(32), .matrixrows(32)) dotmatrix_53 (
    .col0(pipes_35_out_5), .col1(pipes_35_out_6), .col2(pipes_35_out_7), .col3(pipes_35_out_8),
    .col4(pipes_35_out_9), .col5(pipes_35_out_10), .col6(pipes_35_out_11), .col7(pipes_35_out_12),
    .col8(pipes_35_out_13), .col9(pipes_35_out_14), .col10(pipes_35_out_15), .col11(pipes_35_out_16),
    .col12(pipes_35_out_17), .col13(pipes_35_out_18), .col14(pipes_35_out_19), .col15(pipes_35_out_20),
    .col16(pipes_35_out_21), .col17(pipes_35_out_22), .col18(pipes_35_out_23), .col19(pipes_35_out_24),
    .col20(pipes_35_out_25), .col21(pipes_35_out_26), .col22(pipes_35_out_27), .col23(pipes_35_out_28),
    .col24(pipes_35_out_29), .col25(pipes_35_out_30), .col26(pipes_35_out_31), .col27(pipes_35_out_32),
    .col28(pipes_35_out_33), .col29(pipes_35_out_34), .col30(pipes_35_out_35), .col31(pipes_35_out_36));
  pipes pipes_35 (
    .out_5(pipes_35_out_5), .out_6(pipes_35_out_6), .out_7(pipes_35_out_7), .out_8(pipes_35_out_8),
    .out_9(pipes_35_out_9), .out_10(pipes_35_out_10), .out_11(pipes_35_out_11), .out_12(pipes_35_out_12),
    .out_13(pipes_35_out_13), .out_14(pipes_35_out_14), .out_15(pipes_35_out_15), .out_16(pipes_35_out_16),
    .out_17(pipes_35_out_17), .out_18(pipes_35_out_18), .out_19(pipes_35_out_19), .out_20(pipes_35_out_20),
    .out_21(pipes_35_out_21), .out_22(pipes_35_out_22), .out_23(pipes_35_out_23), .out_24(pipes_35_out_24),
    .out_25(pipes_35_out_25), .out_26(pipes_35_out_26), .out_27(pipes_35_out_27), .out_28(pipes_35_out_28),
    .out_29(pipes_35_out_29), .out_30(pipes_35_out_30), .out_31(pipes_35_out_31), .out_32(pipes_35_out_32),
    .out_33(pipes_35_out_33), .out_34(pipes_35_out_34), .out_35(pipes_35_out_35), .out_36(pipes_35_out_36),
    .pipe(pipes_47_pipe_2), .pipe_2(pipes_35_pipe_2), .signal(pipes_47_signal_2),
    .signal_2(pipes_35_signal_2), .bird_1(pipes_47_bird_1_2), .bird_1_2(pipes_35_bird_1_2),
    .bird_2(pipes_47_bird), .bird(pipes_35_bird));
  pipes___bird pipes___bird_11 (
    .pipe_2(pipes___bird_11_pipe_2), .signal(pipes_35_signal_2), .bird_1(pipes_35_bird_1_2),
    .pipe(pipes_35_pipe_2), .signal_2(pipes___bird_11_signal_2), .bird_1_2(pipes___bird_11_bird_1_2),
    .out_5(pipes___bird_11_out_5), .out_6(pipes___bird_11_out_6), .out_7(pipes___bird_11_out_7),
    .out_8(pipes___bird_11_out_8), .out_9(pipes___bird_11_out_9), .out_10(pipes___bird_11_out_10),
    .out_11(pipes___bird_11_out_11), .out_12(pipes___bird_11_out_12), .out_13(pipes___bird_11_out_13),
    .out_14(pipes___bird_11_out_14), .out_15(pipes___bird_11_out_15), .out_16(pipes___bird_11_out_16),
    .out_17(pipes___bird_11_out_17), .out_18(pipes___bird_11_out_18), .out_19(pipes___bird_11_out_19),
    .out_20(pipes___bird_11_out_20), .out_21(pipes___bird_11_out_21), .out_22(pipes___bird_11_out_22),
    .out_23(pipes___bird_11_out_23), .out_24(pipes___bird_11_out_24), .out_25(pipes___bird_11_out_25),
    .out_26(pipes___bird_11_out_26), .out_27(pipes___bird_11_out_27), .out_28(pipes___bird_11_out_28),
    .out_29(pipes___bird_11_out_29), .out_30(pipes___bird_11_out_30), .out_31(pipes___bird_11_out_31),
    .out_32(pipes___bird_11_out_32), .out_33(pipes___bird_11_out_33), .out_34(pipes___bird_11_out_34),
    .out_35(pipes___bird_11_out_35), .out_36(pipes___bird_11_out_36), .bird_2(pipes_35_bird),
    .bird_2_2(pipes___bird_11_bird_2_2));
  pipes pipes_36 (
    .out_5(pipes_36_out_5), .out_6(pipes_36_out_6), .out_7(pipes_36_out_7), .out_8(pipes_36_out_8),
    .out_9(pipes_36_out_9), .out_10(pipes_36_out_10), .out_11(pipes_36_out_11), .out_12(pipes_36_out_12),
    .out_13(pipes_36_out_13), .out_14(pipes_36_out_14), .out_15(pipes_36_out_15), .out_16(pipes_36_out_16),
    .out_17(pipes_36_out_17), .out_18(pipes_36_out_18), .out_19(pipes_36_out_19), .out_20(pipes_36_out_20),
    .out_21(pipes_36_out_21), .out_22(pipes_36_out_22), .out_23(pipes_36_out_23), .out_24(pipes_36_out_24),
    .out_25(pipes_36_out_25), .out_26(pipes_36_out_26), .out_27(pipes_36_out_27), .out_28(pipes_36_out_28),
    .out_29(pipes_36_out_29), .out_30(pipes_36_out_30), .out_31(pipes_36_out_31), .out_32(pipes_36_out_32),
    .out_33(pipes_36_out_33), .out_34(pipes_36_out_34), .out_35(pipes_36_out_35), .out_36(pipes_36_out_36),
    .pipe(pipes_48_pipe_2), .pipe_2(pipes_36_pipe_2), .signal(pipes_48_signal_2),
    .signal_2(pipes_36_signal_2), .bird_1(pipes_48_bird_1_2), .bird_1_2(pipes_36_bird_1_2),
    .bird_2(pipes_48_bird), .bird(pipes_36_bird));
  DotMatrix #(.matrixcols(32), .matrixrows(32)) dotmatrix_54 (
    .col0(pipes_36_out_5), .col1(pipes_36_out_6), .col2(pipes_36_out_7), .col3(pipes_36_out_8),
    .col4(pipes_36_out_9), .col5(pipes_36_out_10), .col6(pipes_36_out_11), .col7(pipes_36_out_12),
    .col8(pipes_36_out_13), .col9(pipes_36_out_14), .col10(pipes_36_out_15), .col11(pipes_36_out_16),
    .col12(pipes_36_out_17), .col13(pipes_36_out_18), .col14(pipes_36_out_19), .col15(pipes_36_out_20),
    .col16(pipes_36_out_21), .col17(pipes_36_out_22), .col18(pipes_36_out_23), .col19(pipes_36_out_24),
    .col20(pipes_36_out_25), .col21(pipes_36_out_26), .col22(pipes_36_out_27), .col23(pipes_36_out_28),
    .col24(pipes_36_out_29), .col25(pipes_36_out_30), .col26(pipes_36_out_31), .col27(pipes_36_out_32),
    .col28(pipes_36_out_33), .col29(pipes_36_out_34), .col30(pipes_36_out_35), .col31(pipes_36_out_36));
  pipes___bird pipes___bird_12 (
    .pipe_2(pipes___bird_12_pipe_2), .signal(pipes_36_signal_2), .bird_1(pipes_36_bird_1_2),
    .pipe(pipes_36_pipe_2), .signal_2(pipes___bird_12_signal_2), .bird_1_2(pipes___bird_12_bird_1_2),
    .out_5(pipes___bird_12_out_5), .out_6(pipes___bird_12_out_6), .out_7(pipes___bird_12_out_7),
    .out_8(pipes___bird_12_out_8), .out_9(pipes___bird_12_out_9), .out_10(pipes___bird_12_out_10),
    .out_11(pipes___bird_12_out_11), .out_12(pipes___bird_12_out_12), .out_13(pipes___bird_12_out_13),
    .out_14(pipes___bird_12_out_14), .out_15(pipes___bird_12_out_15), .out_16(pipes___bird_12_out_16),
    .out_17(pipes___bird_12_out_17), .out_18(pipes___bird_12_out_18), .out_19(pipes___bird_12_out_19),
    .out_20(pipes___bird_12_out_20), .out_21(pipes___bird_12_out_21), .out_22(pipes___bird_12_out_22),
    .out_23(pipes___bird_12_out_23), .out_24(pipes___bird_12_out_24), .out_25(pipes___bird_12_out_25),
    .out_26(pipes___bird_12_out_26), .out_27(pipes___bird_12_out_27), .out_28(pipes___bird_12_out_28),
    .out_29(pipes___bird_12_out_29), .out_30(pipes___bird_12_out_30), .out_31(pipes___bird_12_out_31),
    .out_32(pipes___bird_12_out_32), .out_33(pipes___bird_12_out_33), .out_34(pipes___bird_12_out_34),
    .out_35(pipes___bird_12_out_35), .out_36(pipes___bird_12_out_36), .bird_2(pipes_36_bird),
    .bird_2_2(pipes___bird_12_bird_2_2));
  DotMatrix #(.matrixcols(32), .matrixrows(32)) dotmatrix_55 (
    .col0({32{1'b1}}), .col1({32{1'b1}}), .col2({32{1'b1}}), .col3({32{1'b1}}), .col4({32{1'b1}}),
    .col5({32{1'b1}}), .col6({32{1'b1}}), .col7({32{1'b1}}), .col8({32{1'b1}}), .col9({32{1'b1}}),
    .col10({32{1'b1}}), .col11({32{1'b1}}), .col12({32{1'b1}}), .col13({32{1'b1}}), .col14({32{1'b1}}),
    .col15({32{1'b1}}), .col16({32{1'b1}}), .col17({32{1'b1}}), .col18({32{1'b1}}), .col19({32{1'b1}}),
    .col20({32{1'b1}}), .col21({32{1'b1}}), .col22({32{1'b1}}), .col23({32{1'b1}}), .col24({32{1'b1}}),
    .col25({32{1'b1}}), .col26({32{1'b1}}), .col27({32{1'b1}}), .col28({32{1'b1}}), .col29({32{1'b1}}),
    .col30({32{1'b1}}), .col31({32{1'b1}}));
  DotMatrix #(.matrixcols(32), .matrixrows(32)) dotmatrix_56 (
    .col0({32{1'b1}}), .col1({32{1'b1}}), .col2({32{1'b1}}), .col3({32{1'b1}}), .col4({32{1'b1}}),
    .col5({32{1'b1}}), .col6({32{1'b1}}), .col7({32{1'b1}}), .col8({32{1'b1}}), .col9({32{1'b1}}),
    .col10({32{1'b1}}), .col11({32{1'b1}}), .col12({32{1'b1}}), .col13({32{1'b1}}), .col14({32{1'b1}}),
    .col15({32{1'b1}}), .col16({32{1'b1}}), .col17({32{1'b1}}), .col18({32{1'b1}}), .col19({32{1'b1}}),
    .col20({32{1'b1}}), .col21({32{1'b1}}), .col22({32{1'b1}}), .col23({32{1'b1}}), .col24({32{1'b1}}),
    .col25({32{1'b1}}), .col26({32{1'b1}}), .col27({32{1'b1}}), .col28({32{1'b1}}), .col29({32{1'b1}}),
    .col30({32{1'b1}}), .col31({32{1'b1}}));
  pipes pipes_37 (
    .out_5(pipes_37_out_5), .out_6(pipes_37_out_6), .out_7(pipes_37_out_7), .out_8(pipes_37_out_8),
    .out_9(pipes_37_out_9), .out_10(pipes_37_out_10), .out_11(pipes_37_out_11), .out_12(pipes_37_out_12),
    .out_13(pipes_37_out_13), .out_14(pipes_37_out_14), .out_15(pipes_37_out_15), .out_16(pipes_37_out_16),
    .out_17(pipes_37_out_17), .out_18(pipes_37_out_18), .out_19(pipes_37_out_19), .out_20(pipes_37_out_20),
    .out_21(pipes_37_out_21), .out_22(pipes_37_out_22), .out_23(pipes_37_out_23), .out_24(pipes_37_out_24),
    .out_25(pipes_37_out_25), .out_26(pipes_37_out_26), .out_27(pipes_37_out_27), .out_28(pipes_37_out_28),
    .out_29(pipes_37_out_29), .out_30(pipes_37_out_30), .out_31(pipes_37_out_31), .out_32(pipes_37_out_32),
    .out_33(pipes_37_out_33), .out_34(pipes_37_out_34), .out_35(pipes_37_out_35), .out_36(pipes_37_out_36),
    .pipe(pipes_49_pipe_2), .pipe_2(pipes_37_pipe_2), .signal(pipes_49_signal_2),
    .signal_2(pipes_37_signal_2), .bird_1(pipes_49_bird_1_2), .bird_1_2(pipes_37_bird_1_2),
    .bird_2(pipes_49_bird), .bird(pipes_37_bird));
  DotMatrix #(.matrixcols(32), .matrixrows(32)) dotmatrix_57 (
    .col0(pipes_37_out_5), .col1(pipes_37_out_6), .col2(pipes_37_out_7), .col3(pipes_37_out_8),
    .col4(pipes_37_out_9), .col5(pipes_37_out_10), .col6(pipes_37_out_11), .col7(pipes_37_out_12),
    .col8(pipes_37_out_13), .col9(pipes_37_out_14), .col10(pipes_37_out_15), .col11(pipes_37_out_16),
    .col12(pipes_37_out_17), .col13(pipes_37_out_18), .col14(pipes_37_out_19), .col15(pipes_37_out_20),
    .col16(pipes_37_out_21), .col17(pipes_37_out_22), .col18(pipes_37_out_23), .col19(pipes_37_out_24),
    .col20(pipes_37_out_25), .col21(pipes_37_out_26), .col22(pipes_37_out_27), .col23(pipes_37_out_28),
    .col24(pipes_37_out_29), .col25(pipes_37_out_30), .col26(pipes_37_out_31), .col27(pipes_37_out_32),
    .col28(pipes_37_out_33), .col29(pipes_37_out_34), .col30(pipes_37_out_35), .col31(pipes_37_out_36));
  DotMatrix #(.matrixcols(32), .matrixrows(32)) dotmatrix_58 (
    .col0(pipes_38_out_5), .col1(pipes_38_out_6), .col2(pipes_38_out_7), .col3(pipes_38_out_8),
    .col4(pipes_38_out_9), .col5(pipes_38_out_10), .col6(pipes_38_out_11), .col7(pipes_38_out_12),
    .col8(pipes_38_out_13), .col9(pipes_38_out_14), .col10(pipes_38_out_15), .col11(pipes_38_out_16),
    .col12(pipes_38_out_17), .col13(pipes_38_out_18), .col14(pipes_38_out_19), .col15(pipes_38_out_20),
    .col16(pipes_38_out_21), .col17(pipes_38_out_22), .col18(pipes_38_out_23), .col19(pipes_38_out_24),
    .col20(pipes_38_out_25), .col21(pipes_38_out_26), .col22(pipes_38_out_27), .col23(pipes_38_out_28),
    .col24(pipes_38_out_29), .col25(pipes_38_out_30), .col26(pipes_38_out_31), .col27(pipes_38_out_32),
    .col28(pipes_38_out_33), .col29(pipes_38_out_34), .col30(pipes_38_out_35), .col31(pipes_38_out_36));
  pipes pipes_38 (
    .out_5(pipes_38_out_5), .out_6(pipes_38_out_6), .out_7(pipes_38_out_7), .out_8(pipes_38_out_8),
    .out_9(pipes_38_out_9), .out_10(pipes_38_out_10), .out_11(pipes_38_out_11), .out_12(pipes_38_out_12),
    .out_13(pipes_38_out_13), .out_14(pipes_38_out_14), .out_15(pipes_38_out_15), .out_16(pipes_38_out_16),
    .out_17(pipes_38_out_17), .out_18(pipes_38_out_18), .out_19(pipes_38_out_19), .out_20(pipes_38_out_20),
    .out_21(pipes_38_out_21), .out_22(pipes_38_out_22), .out_23(pipes_38_out_23), .out_24(pipes_38_out_24),
    .out_25(pipes_38_out_25), .out_26(pipes_38_out_26), .out_27(pipes_38_out_27), .out_28(pipes_38_out_28),
    .out_29(pipes_38_out_29), .out_30(pipes_38_out_30), .out_31(pipes_38_out_31), .out_32(pipes_38_out_32),
    .out_33(pipes_38_out_33), .out_34(pipes_38_out_34), .out_35(pipes_38_out_35), .out_36(pipes_38_out_36),
    .pipe(pipes_50_pipe_2), .pipe_2(pipes_38_pipe_2), .signal(pipes_50_signal_2),
    .signal_2(pipes_38_signal_2), .bird_1(pipes_50_bird_1_2), .bird_1_2(pipes_38_bird_1_2),
    .bird_2(pipes_50_bird), .bird(pipes_38_bird));
  DotMatrix #(.matrixcols(32), .matrixrows(32)) dotmatrix_59 (
    .col0(pipes_39_out_5), .col1(pipes_39_out_6), .col2(pipes_39_out_7), .col3(pipes_39_out_8),
    .col4(pipes_39_out_9), .col5(pipes_39_out_10), .col6(pipes_39_out_11), .col7(pipes_39_out_12),
    .col8(pipes_39_out_13), .col9(pipes_39_out_14), .col10(pipes_39_out_15), .col11(pipes_39_out_16),
    .col12(pipes_39_out_17), .col13(pipes_39_out_18), .col14(pipes_39_out_19), .col15(pipes_39_out_20),
    .col16(pipes_39_out_21), .col17(pipes_39_out_22), .col18(pipes_39_out_23), .col19(pipes_39_out_24),
    .col20(pipes_39_out_25), .col21(pipes_39_out_26), .col22(pipes_39_out_27), .col23(pipes_39_out_28),
    .col24(pipes_39_out_29), .col25(pipes_39_out_30), .col26(pipes_39_out_31), .col27(pipes_39_out_32),
    .col28(pipes_39_out_33), .col29(pipes_39_out_34), .col30(pipes_39_out_35), .col31(pipes_39_out_36));
  pipes pipes_39 (
    .out_5(pipes_39_out_5), .out_6(pipes_39_out_6), .out_7(pipes_39_out_7), .out_8(pipes_39_out_8),
    .out_9(pipes_39_out_9), .out_10(pipes_39_out_10), .out_11(pipes_39_out_11), .out_12(pipes_39_out_12),
    .out_13(pipes_39_out_13), .out_14(pipes_39_out_14), .out_15(pipes_39_out_15), .out_16(pipes_39_out_16),
    .out_17(pipes_39_out_17), .out_18(pipes_39_out_18), .out_19(pipes_39_out_19), .out_20(pipes_39_out_20),
    .out_21(pipes_39_out_21), .out_22(pipes_39_out_22), .out_23(pipes_39_out_23), .out_24(pipes_39_out_24),
    .out_25(pipes_39_out_25), .out_26(pipes_39_out_26), .out_27(pipes_39_out_27), .out_28(pipes_39_out_28),
    .out_29(pipes_39_out_29), .out_30(pipes_39_out_30), .out_31(pipes_39_out_31), .out_32(pipes_39_out_32),
    .out_33(pipes_39_out_33), .out_34(pipes_39_out_34), .out_35(pipes_39_out_35), .out_36(pipes_39_out_36),
    .pipe(pipes_51_pipe_2), .pipe_2(pipes_39_pipe_2), .signal(pipes_51_signal_2),
    .signal_2(pipes_39_signal_2), .bird_1(pipes_51_bird_1_2), .bird_1_2(pipes_39_bird_1_2),
    .bird_2(pipes_51_bird), .bird(pipes_39_bird));
  DotMatrix #(.matrixcols(32), .matrixrows(32)) dotmatrix_60 (
    .col0(pipes_40_out_5), .col1(pipes_40_out_6), .col2(pipes_40_out_7), .col3(pipes_40_out_8),
    .col4(pipes_40_out_9), .col5(pipes_40_out_10), .col6(pipes_40_out_11), .col7(pipes_40_out_12),
    .col8(pipes_40_out_13), .col9(pipes_40_out_14), .col10(pipes_40_out_15), .col11(pipes_40_out_16),
    .col12(pipes_40_out_17), .col13(pipes_40_out_18), .col14(pipes_40_out_19), .col15(pipes_40_out_20),
    .col16(pipes_40_out_21), .col17(pipes_40_out_22), .col18(pipes_40_out_23), .col19(pipes_40_out_24),
    .col20(pipes_40_out_25), .col21(pipes_40_out_26), .col22(pipes_40_out_27), .col23(pipes_40_out_28),
    .col24(pipes_40_out_29), .col25(pipes_40_out_30), .col26(pipes_40_out_31), .col27(pipes_40_out_32),
    .col28(pipes_40_out_33), .col29(pipes_40_out_34), .col30(pipes_40_out_35), .col31(pipes_40_out_36));
  pipes pipes_40 (
    .out_5(pipes_40_out_5), .out_6(pipes_40_out_6), .out_7(pipes_40_out_7), .out_8(pipes_40_out_8),
    .out_9(pipes_40_out_9), .out_10(pipes_40_out_10), .out_11(pipes_40_out_11), .out_12(pipes_40_out_12),
    .out_13(pipes_40_out_13), .out_14(pipes_40_out_14), .out_15(pipes_40_out_15), .out_16(pipes_40_out_16),
    .out_17(pipes_40_out_17), .out_18(pipes_40_out_18), .out_19(pipes_40_out_19), .out_20(pipes_40_out_20),
    .out_21(pipes_40_out_21), .out_22(pipes_40_out_22), .out_23(pipes_40_out_23), .out_24(pipes_40_out_24),
    .out_25(pipes_40_out_25), .out_26(pipes_40_out_26), .out_27(pipes_40_out_27), .out_28(pipes_40_out_28),
    .out_29(pipes_40_out_29), .out_30(pipes_40_out_30), .out_31(pipes_40_out_31), .out_32(pipes_40_out_32),
    .out_33(pipes_40_out_33), .out_34(pipes_40_out_34), .out_35(pipes_40_out_35), .out_36(pipes_40_out_36),
    .pipe(pipes_52_pipe_2), .pipe_2(pipes_40_pipe_2), .signal(pipes_52_signal_2),
    .signal_2(pipes_40_signal_2), .bird_1(pipes_52_bird_1_2), .bird_1_2(pipes_40_bird_1_2),
    .bird_2(pipes_52_bird), .bird(pipes_40_bird));
  pipes pipes_41 (
    .out_5(pipes_41_out_5), .out_6(pipes_41_out_6), .out_7(pipes_41_out_7), .out_8(pipes_41_out_8),
    .out_9(pipes_41_out_9), .out_10(pipes_41_out_10), .out_11(pipes_41_out_11), .out_12(pipes_41_out_12),
    .out_13(pipes_41_out_13), .out_14(pipes_41_out_14), .out_15(pipes_41_out_15), .out_16(pipes_41_out_16),
    .out_17(pipes_41_out_17), .out_18(pipes_41_out_18), .out_19(pipes_41_out_19), .out_20(pipes_41_out_20),
    .out_21(pipes_41_out_21), .out_22(pipes_41_out_22), .out_23(pipes_41_out_23), .out_24(pipes_41_out_24),
    .out_25(pipes_41_out_25), .out_26(pipes_41_out_26), .out_27(pipes_41_out_27), .out_28(pipes_41_out_28),
    .out_29(pipes_41_out_29), .out_30(pipes_41_out_30), .out_31(pipes_41_out_31), .out_32(pipes_41_out_32),
    .out_33(pipes_41_out_33), .out_34(pipes_41_out_34), .out_35(pipes_41_out_35), .out_36(pipes_41_out_36),
    .pipe(pipes_53_pipe_2), .pipe_2(pipes_41_pipe_2), .signal(pipes_53_signal_2),
    .signal_2(pipes_41_signal_2), .bird_1(pipes_53_bird_1_2), .bird_1_2(pipes_41_bird_1_2),
    .bird_2(pipes_53_bird), .bird(pipes_41_bird));
  DotMatrix #(.matrixcols(32), .matrixrows(32)) dotmatrix_61 (
    .col0(pipes_41_out_5), .col1(pipes_41_out_6), .col2(pipes_41_out_7), .col3(pipes_41_out_8),
    .col4(pipes_41_out_9), .col5(pipes_41_out_10), .col6(pipes_41_out_11), .col7(pipes_41_out_12),
    .col8(pipes_41_out_13), .col9(pipes_41_out_14), .col10(pipes_41_out_15), .col11(pipes_41_out_16),
    .col12(pipes_41_out_17), .col13(pipes_41_out_18), .col14(pipes_41_out_19), .col15(pipes_41_out_20),
    .col16(pipes_41_out_21), .col17(pipes_41_out_22), .col18(pipes_41_out_23), .col19(pipes_41_out_24),
    .col20(pipes_41_out_25), .col21(pipes_41_out_26), .col22(pipes_41_out_27), .col23(pipes_41_out_28),
    .col24(pipes_41_out_29), .col25(pipes_41_out_30), .col26(pipes_41_out_31), .col27(pipes_41_out_32),
    .col28(pipes_41_out_33), .col29(pipes_41_out_34), .col30(pipes_41_out_35), .col31(pipes_41_out_36));
  pipes pipes_42 (
    .out_5(pipes_42_out_5), .out_6(pipes_42_out_6), .out_7(pipes_42_out_7), .out_8(pipes_42_out_8),
    .out_9(pipes_42_out_9), .out_10(pipes_42_out_10), .out_11(pipes_42_out_11), .out_12(pipes_42_out_12),
    .out_13(pipes_42_out_13), .out_14(pipes_42_out_14), .out_15(pipes_42_out_15), .out_16(pipes_42_out_16),
    .out_17(pipes_42_out_17), .out_18(pipes_42_out_18), .out_19(pipes_42_out_19), .out_20(pipes_42_out_20),
    .out_21(pipes_42_out_21), .out_22(pipes_42_out_22), .out_23(pipes_42_out_23), .out_24(pipes_42_out_24),
    .out_25(pipes_42_out_25), .out_26(pipes_42_out_26), .out_27(pipes_42_out_27), .out_28(pipes_42_out_28),
    .out_29(pipes_42_out_29), .out_30(pipes_42_out_30), .out_31(pipes_42_out_31), .out_32(pipes_42_out_32),
    .out_33(pipes_42_out_33), .out_34(pipes_42_out_34), .out_35(pipes_42_out_35), .out_36(pipes_42_out_36),
    .pipe(pipes_54_pipe_2), .pipe_2(pipes_42_pipe_2), .signal(pipes_54_signal_2),
    .signal_2(pipes_42_signal_2), .bird_1(pipes_54_bird_1_2), .bird_1_2(pipes_42_bird_1_2),
    .bird_2(pipes_54_bird), .bird(pipes_42_bird));
  DotMatrix #(.matrixcols(32), .matrixrows(32)) dotmatrix_62 (
    .col0(pipes_42_out_5), .col1(pipes_42_out_6), .col2(pipes_42_out_7), .col3(pipes_42_out_8),
    .col4(pipes_42_out_9), .col5(pipes_42_out_10), .col6(pipes_42_out_11), .col7(pipes_42_out_12),
    .col8(pipes_42_out_13), .col9(pipes_42_out_14), .col10(pipes_42_out_15), .col11(pipes_42_out_16),
    .col12(pipes_42_out_17), .col13(pipes_42_out_18), .col14(pipes_42_out_19), .col15(pipes_42_out_20),
    .col16(pipes_42_out_21), .col17(pipes_42_out_22), .col18(pipes_42_out_23), .col19(pipes_42_out_24),
    .col20(pipes_42_out_25), .col21(pipes_42_out_26), .col22(pipes_42_out_27), .col23(pipes_42_out_28),
    .col24(pipes_42_out_29), .col25(pipes_42_out_30), .col26(pipes_42_out_31), .col27(pipes_42_out_32),
    .col28(pipes_42_out_33), .col29(pipes_42_out_34), .col30(pipes_42_out_35), .col31(pipes_42_out_36));
  pipes pipes_43 (
    .out_5(pipes_43_out_5), .out_6(pipes_43_out_6), .out_7(pipes_43_out_7), .out_8(pipes_43_out_8),
    .out_9(pipes_43_out_9), .out_10(pipes_43_out_10), .out_11(pipes_43_out_11), .out_12(pipes_43_out_12),
    .out_13(pipes_43_out_13), .out_14(pipes_43_out_14), .out_15(pipes_43_out_15), .out_16(pipes_43_out_16),
    .out_17(pipes_43_out_17), .out_18(pipes_43_out_18), .out_19(pipes_43_out_19), .out_20(pipes_43_out_20),
    .out_21(pipes_43_out_21), .out_22(pipes_43_out_22), .out_23(pipes_43_out_23), .out_24(pipes_43_out_24),
    .out_25(pipes_43_out_25), .out_26(pipes_43_out_26), .out_27(pipes_43_out_27), .out_28(pipes_43_out_28),
    .out_29(pipes_43_out_29), .out_30(pipes_43_out_30), .out_31(pipes_43_out_31), .out_32(pipes_43_out_32),
    .out_33(pipes_43_out_33), .out_34(pipes_43_out_34), .out_35(pipes_43_out_35), .out_36(pipes_43_out_36),
    .pipe(pipes_55_pipe_2), .pipe_2(pipes_43_pipe_2), .signal(pipes_55_signal_2),
    .signal_2(pipes_43_signal_2), .bird_1(pipes_55_bird_1_2), .bird_1_2(pipes_43_bird_1_2),
    .bird_2(pipes_55_bird), .bird(pipes_43_bird));
  DotMatrix #(.matrixcols(32), .matrixrows(32)) dotmatrix_63 (
    .col0(pipes_43_out_5), .col1(pipes_43_out_6), .col2(pipes_43_out_7), .col3(pipes_43_out_8),
    .col4(pipes_43_out_9), .col5(pipes_43_out_10), .col6(pipes_43_out_11), .col7(pipes_43_out_12),
    .col8(pipes_43_out_13), .col9(pipes_43_out_14), .col10(pipes_43_out_15), .col11(pipes_43_out_16),
    .col12(pipes_43_out_17), .col13(pipes_43_out_18), .col14(pipes_43_out_19), .col15(pipes_43_out_20),
    .col16(pipes_43_out_21), .col17(pipes_43_out_22), .col18(pipes_43_out_23), .col19(pipes_43_out_24),
    .col20(pipes_43_out_25), .col21(pipes_43_out_26), .col22(pipes_43_out_27), .col23(pipes_43_out_28),
    .col24(pipes_43_out_29), .col25(pipes_43_out_30), .col26(pipes_43_out_31), .col27(pipes_43_out_32),
    .col28(pipes_43_out_33), .col29(pipes_43_out_34), .col30(pipes_43_out_35), .col31(pipes_43_out_36));
  pipes pipes_44 (
    .out_5(pipes_44_out_5), .out_6(pipes_44_out_6), .out_7(pipes_44_out_7), .out_8(pipes_44_out_8),
    .out_9(pipes_44_out_9), .out_10(pipes_44_out_10), .out_11(pipes_44_out_11), .out_12(pipes_44_out_12),
    .out_13(pipes_44_out_13), .out_14(pipes_44_out_14), .out_15(pipes_44_out_15), .out_16(pipes_44_out_16),
    .out_17(pipes_44_out_17), .out_18(pipes_44_out_18), .out_19(pipes_44_out_19), .out_20(pipes_44_out_20),
    .out_21(pipes_44_out_21), .out_22(pipes_44_out_22), .out_23(pipes_44_out_23), .out_24(pipes_44_out_24),
    .out_25(pipes_44_out_25), .out_26(pipes_44_out_26), .out_27(pipes_44_out_27), .out_28(pipes_44_out_28),
    .out_29(pipes_44_out_29), .out_30(pipes_44_out_30), .out_31(pipes_44_out_31), .out_32(pipes_44_out_32),
    .out_33(pipes_44_out_33), .out_34(pipes_44_out_34), .out_35(pipes_44_out_35), .out_36(pipes_44_out_36),
    .pipe(pipes_56_pipe_2), .pipe_2(pipes_44_pipe_2), .signal(pipes_56_signal_2),
    .signal_2(pipes_44_signal_2), .bird_1(pipes_56_bird_1_2), .bird_1_2(pipes_44_bird_1_2),
    .bird_2(pipes_56_bird), .bird(pipes_44_bird));
  DotMatrix #(.matrixcols(32), .matrixrows(32)) dotmatrix_64 (
    .col0(pipes_44_out_5), .col1(pipes_44_out_6), .col2(pipes_44_out_7), .col3(pipes_44_out_8),
    .col4(pipes_44_out_9), .col5(pipes_44_out_10), .col6(pipes_44_out_11), .col7(pipes_44_out_12),
    .col8(pipes_44_out_13), .col9(pipes_44_out_14), .col10(pipes_44_out_15), .col11(pipes_44_out_16),
    .col12(pipes_44_out_17), .col13(pipes_44_out_18), .col14(pipes_44_out_19), .col15(pipes_44_out_20),
    .col16(pipes_44_out_21), .col17(pipes_44_out_22), .col18(pipes_44_out_23), .col19(pipes_44_out_24),
    .col20(pipes_44_out_25), .col21(pipes_44_out_26), .col22(pipes_44_out_27), .col23(pipes_44_out_28),
    .col24(pipes_44_out_29), .col25(pipes_44_out_30), .col26(pipes_44_out_31), .col27(pipes_44_out_32),
    .col28(pipes_44_out_33), .col29(pipes_44_out_34), .col30(pipes_44_out_35), .col31(pipes_44_out_36));
  DotMatrix #(.matrixcols(32), .matrixrows(32)) dotmatrix_65 (
    .col0(pipes_45_out_5), .col1(pipes_45_out_6), .col2(pipes_45_out_7), .col3(pipes_45_out_8),
    .col4(pipes_45_out_9), .col5(pipes_45_out_10), .col6(pipes_45_out_11), .col7(pipes_45_out_12),
    .col8(pipes_45_out_13), .col9(pipes_45_out_14), .col10(pipes_45_out_15), .col11(pipes_45_out_16),
    .col12(pipes_45_out_17), .col13(pipes_45_out_18), .col14(pipes_45_out_19), .col15(pipes_45_out_20),
    .col16(pipes_45_out_21), .col17(pipes_45_out_22), .col18(pipes_45_out_23), .col19(pipes_45_out_24),
    .col20(pipes_45_out_25), .col21(pipes_45_out_26), .col22(pipes_45_out_27), .col23(pipes_45_out_28),
    .col24(pipes_45_out_29), .col25(pipes_45_out_30), .col26(pipes_45_out_31), .col27(pipes_45_out_32),
    .col28(pipes_45_out_33), .col29(pipes_45_out_34), .col30(pipes_45_out_35), .col31(pipes_45_out_36));
  pipes pipes_45 (
    .out_5(pipes_45_out_5), .out_6(pipes_45_out_6), .out_7(pipes_45_out_7), .out_8(pipes_45_out_8),
    .out_9(pipes_45_out_9), .out_10(pipes_45_out_10), .out_11(pipes_45_out_11), .out_12(pipes_45_out_12),
    .out_13(pipes_45_out_13), .out_14(pipes_45_out_14), .out_15(pipes_45_out_15), .out_16(pipes_45_out_16),
    .out_17(pipes_45_out_17), .out_18(pipes_45_out_18), .out_19(pipes_45_out_19), .out_20(pipes_45_out_20),
    .out_21(pipes_45_out_21), .out_22(pipes_45_out_22), .out_23(pipes_45_out_23), .out_24(pipes_45_out_24),
    .out_25(pipes_45_out_25), .out_26(pipes_45_out_26), .out_27(pipes_45_out_27), .out_28(pipes_45_out_28),
    .out_29(pipes_45_out_29), .out_30(pipes_45_out_30), .out_31(pipes_45_out_31), .out_32(pipes_45_out_32),
    .out_33(pipes_45_out_33), .out_34(pipes_45_out_34), .out_35(pipes_45_out_35), .out_36(pipes_45_out_36),
    .pipe(pipes_57_pipe_2), .pipe_2(pipes_45_pipe_2), .signal(pipes_57_signal_2),
    .signal_2(pipes_45_signal_2), .bird_1(pipes_57_bird_1_2), .bird_1_2(pipes_45_bird_1_2),
    .bird_2(pipes_57_bird), .bird(pipes_45_bird));
  pipes pipes_46 (
    .out_5(pipes_46_out_5), .out_6(pipes_46_out_6), .out_7(pipes_46_out_7), .out_8(pipes_46_out_8),
    .out_9(pipes_46_out_9), .out_10(pipes_46_out_10), .out_11(pipes_46_out_11), .out_12(pipes_46_out_12),
    .out_13(pipes_46_out_13), .out_14(pipes_46_out_14), .out_15(pipes_46_out_15), .out_16(pipes_46_out_16),
    .out_17(pipes_46_out_17), .out_18(pipes_46_out_18), .out_19(pipes_46_out_19), .out_20(pipes_46_out_20),
    .out_21(pipes_46_out_21), .out_22(pipes_46_out_22), .out_23(pipes_46_out_23), .out_24(pipes_46_out_24),
    .out_25(pipes_46_out_25), .out_26(pipes_46_out_26), .out_27(pipes_46_out_27), .out_28(pipes_46_out_28),
    .out_29(pipes_46_out_29), .out_30(pipes_46_out_30), .out_31(pipes_46_out_31), .out_32(pipes_46_out_32),
    .out_33(pipes_46_out_33), .out_34(pipes_46_out_34), .out_35(pipes_46_out_35), .out_36(pipes_46_out_36),
    .pipe(pipes_58_pipe_2), .pipe_2(pipes_46_pipe_2), .signal(pipes_58_signal_2),
    .signal_2(pipes_46_signal_2), .bird_1(pipes_58_bird_1_2), .bird_1_2(pipes_46_bird_1_2),
    .bird_2(pipes_58_bird), .bird(pipes_46_bird));
  DotMatrix #(.matrixcols(32), .matrixrows(32)) dotmatrix_66 (
    .col0(pipes_46_out_5), .col1(pipes_46_out_6), .col2(pipes_46_out_7), .col3(pipes_46_out_8),
    .col4(pipes_46_out_9), .col5(pipes_46_out_10), .col6(pipes_46_out_11), .col7(pipes_46_out_12),
    .col8(pipes_46_out_13), .col9(pipes_46_out_14), .col10(pipes_46_out_15), .col11(pipes_46_out_16),
    .col12(pipes_46_out_17), .col13(pipes_46_out_18), .col14(pipes_46_out_19), .col15(pipes_46_out_20),
    .col16(pipes_46_out_21), .col17(pipes_46_out_22), .col18(pipes_46_out_23), .col19(pipes_46_out_24),
    .col20(pipes_46_out_25), .col21(pipes_46_out_26), .col22(pipes_46_out_27), .col23(pipes_46_out_28),
    .col24(pipes_46_out_29), .col25(pipes_46_out_30), .col26(pipes_46_out_31), .col27(pipes_46_out_32),
    .col28(pipes_46_out_33), .col29(pipes_46_out_34), .col30(pipes_46_out_35), .col31(pipes_46_out_36));
  pipes pipes_47 (
    .out_5(pipes_47_out_5), .out_6(pipes_47_out_6), .out_7(pipes_47_out_7), .out_8(pipes_47_out_8),
    .out_9(pipes_47_out_9), .out_10(pipes_47_out_10), .out_11(pipes_47_out_11), .out_12(pipes_47_out_12),
    .out_13(pipes_47_out_13), .out_14(pipes_47_out_14), .out_15(pipes_47_out_15), .out_16(pipes_47_out_16),
    .out_17(pipes_47_out_17), .out_18(pipes_47_out_18), .out_19(pipes_47_out_19), .out_20(pipes_47_out_20),
    .out_21(pipes_47_out_21), .out_22(pipes_47_out_22), .out_23(pipes_47_out_23), .out_24(pipes_47_out_24),
    .out_25(pipes_47_out_25), .out_26(pipes_47_out_26), .out_27(pipes_47_out_27), .out_28(pipes_47_out_28),
    .out_29(pipes_47_out_29), .out_30(pipes_47_out_30), .out_31(pipes_47_out_31), .out_32(pipes_47_out_32),
    .out_33(pipes_47_out_33), .out_34(pipes_47_out_34), .out_35(pipes_47_out_35), .out_36(pipes_47_out_36),
    .pipe(pipes_59_pipe_2), .pipe_2(pipes_47_pipe_2), .signal(pipes_59_signal_2),
    .signal_2(pipes_47_signal_2), .bird_1(pipes_59_bird_1_2), .bird_1_2(pipes_47_bird_1_2),
    .bird_2(pipes_59_bird), .bird(pipes_47_bird));
  DotMatrix #(.matrixcols(32), .matrixrows(32)) dotmatrix_67 (
    .col0(pipes_47_out_5), .col1(pipes_47_out_6), .col2(pipes_47_out_7), .col3(pipes_47_out_8),
    .col4(pipes_47_out_9), .col5(pipes_47_out_10), .col6(pipes_47_out_11), .col7(pipes_47_out_12),
    .col8(pipes_47_out_13), .col9(pipes_47_out_14), .col10(pipes_47_out_15), .col11(pipes_47_out_16),
    .col12(pipes_47_out_17), .col13(pipes_47_out_18), .col14(pipes_47_out_19), .col15(pipes_47_out_20),
    .col16(pipes_47_out_21), .col17(pipes_47_out_22), .col18(pipes_47_out_23), .col19(pipes_47_out_24),
    .col20(pipes_47_out_25), .col21(pipes_47_out_26), .col22(pipes_47_out_27), .col23(pipes_47_out_28),
    .col24(pipes_47_out_29), .col25(pipes_47_out_30), .col26(pipes_47_out_31), .col27(pipes_47_out_32),
    .col28(pipes_47_out_33), .col29(pipes_47_out_34), .col30(pipes_47_out_35), .col31(pipes_47_out_36));
  DotMatrix #(.matrixcols(32), .matrixrows(32)) dotmatrix_68 (
    .col0(pipes_48_out_5), .col1(pipes_48_out_6), .col2(pipes_48_out_7), .col3(pipes_48_out_8),
    .col4(pipes_48_out_9), .col5(pipes_48_out_10), .col6(pipes_48_out_11), .col7(pipes_48_out_12),
    .col8(pipes_48_out_13), .col9(pipes_48_out_14), .col10(pipes_48_out_15), .col11(pipes_48_out_16),
    .col12(pipes_48_out_17), .col13(pipes_48_out_18), .col14(pipes_48_out_19), .col15(pipes_48_out_20),
    .col16(pipes_48_out_21), .col17(pipes_48_out_22), .col18(pipes_48_out_23), .col19(pipes_48_out_24),
    .col20(pipes_48_out_25), .col21(pipes_48_out_26), .col22(pipes_48_out_27), .col23(pipes_48_out_28),
    .col24(pipes_48_out_29), .col25(pipes_48_out_30), .col26(pipes_48_out_31), .col27(pipes_48_out_32),
    .col28(pipes_48_out_33), .col29(pipes_48_out_34), .col30(pipes_48_out_35), .col31(pipes_48_out_36));
  pipes pipes_48 (
    .out_5(pipes_48_out_5), .out_6(pipes_48_out_6), .out_7(pipes_48_out_7), .out_8(pipes_48_out_8),
    .out_9(pipes_48_out_9), .out_10(pipes_48_out_10), .out_11(pipes_48_out_11), .out_12(pipes_48_out_12),
    .out_13(pipes_48_out_13), .out_14(pipes_48_out_14), .out_15(pipes_48_out_15), .out_16(pipes_48_out_16),
    .out_17(pipes_48_out_17), .out_18(pipes_48_out_18), .out_19(pipes_48_out_19), .out_20(pipes_48_out_20),
    .out_21(pipes_48_out_21), .out_22(pipes_48_out_22), .out_23(pipes_48_out_23), .out_24(pipes_48_out_24),
    .out_25(pipes_48_out_25), .out_26(pipes_48_out_26), .out_27(pipes_48_out_27), .out_28(pipes_48_out_28),
    .out_29(pipes_48_out_29), .out_30(pipes_48_out_30), .out_31(pipes_48_out_31), .out_32(pipes_48_out_32),
    .out_33(pipes_48_out_33), .out_34(pipes_48_out_34), .out_35(pipes_48_out_35), .out_36(pipes_48_out_36),
    .pipe(pipes_60_pipe_2), .pipe_2(pipes_48_pipe_2), .signal(pipes_60_signal_2),
    .signal_2(pipes_48_signal_2), .bird_1(pipes_60_bird_1_2), .bird_1_2(pipes_48_bird_1_2),
    .bird_2(pipes_60_bird), .bird(pipes_48_bird));
  DotMatrix #(.matrixcols(32), .matrixrows(32)) dotmatrix_69 (
    .col0({32{1'b1}}), .col1({32{1'b1}}), .col2({32{1'b1}}), .col3({32{1'b1}}), .col4({32{1'b1}}),
    .col5({32{1'b1}}), .col6({32{1'b1}}), .col7({32{1'b1}}), .col8({32{1'b1}}), .col9({32{1'b1}}),
    .col10({32{1'b1}}), .col11({32{1'b1}}), .col12({32{1'b1}}), .col13({32{1'b1}}), .col14({32{1'b1}}),
    .col15({32{1'b1}}), .col16({32{1'b1}}), .col17({32{1'b1}}), .col18({32{1'b1}}), .col19({32{1'b1}}),
    .col20({32{1'b1}}), .col21({32{1'b1}}), .col22({32{1'b1}}), .col23({32{1'b1}}), .col24({32{1'b1}}),
    .col25({32{1'b1}}), .col26({32{1'b1}}), .col27({32{1'b1}}), .col28({32{1'b1}}), .col29({32{1'b1}}),
    .col30({32{1'b1}}), .col31({32{1'b1}}));
  DotMatrix #(.matrixcols(32), .matrixrows(32)) dotmatrix_70 (
    .col0({32{1'b1}}), .col1({32{1'b1}}), .col2({32{1'b1}}), .col3({32{1'b1}}), .col4({32{1'b1}}),
    .col5({32{1'b1}}), .col6({32{1'b1}}), .col7({32{1'b1}}), .col8({32{1'b1}}), .col9({32{1'b1}}),
    .col10({32{1'b1}}), .col11({32{1'b1}}), .col12({32{1'b1}}), .col13({32{1'b1}}), .col14({32{1'b1}}),
    .col15({32{1'b1}}), .col16({32{1'b1}}), .col17({32{1'b1}}), .col18({32{1'b1}}), .col19({32{1'b1}}),
    .col20({32{1'b1}}), .col21({32{1'b1}}), .col22({32{1'b1}}), .col23({32{1'b1}}), .col24({32{1'b1}}),
    .col25({32{1'b1}}), .col26({32{1'b1}}), .col27({32{1'b1}}), .col28({32{1'b1}}), .col29({32{1'b1}}),
    .col30({32{1'b1}}), .col31({32{1'b1}}));
  DotMatrix #(.matrixcols(32), .matrixrows(32)) dotmatrix_71 (
    .col0(pipes_49_out_5), .col1(pipes_49_out_6), .col2(pipes_49_out_7), .col3(pipes_49_out_8),
    .col4(pipes_49_out_9), .col5(pipes_49_out_10), .col6(pipes_49_out_11), .col7(pipes_49_out_12),
    .col8(pipes_49_out_13), .col9(pipes_49_out_14), .col10(pipes_49_out_15), .col11(pipes_49_out_16),
    .col12(pipes_49_out_17), .col13(pipes_49_out_18), .col14(pipes_49_out_19), .col15(pipes_49_out_20),
    .col16(pipes_49_out_21), .col17(pipes_49_out_22), .col18(pipes_49_out_23), .col19(pipes_49_out_24),
    .col20(pipes_49_out_25), .col21(pipes_49_out_26), .col22(pipes_49_out_27), .col23(pipes_49_out_28),
    .col24(pipes_49_out_29), .col25(pipes_49_out_30), .col26(pipes_49_out_31), .col27(pipes_49_out_32),
    .col28(pipes_49_out_33), .col29(pipes_49_out_34), .col30(pipes_49_out_35), .col31(pipes_49_out_36));
  pipes pipes_49 (
    .out_5(pipes_49_out_5), .out_6(pipes_49_out_6), .out_7(pipes_49_out_7), .out_8(pipes_49_out_8),
    .out_9(pipes_49_out_9), .out_10(pipes_49_out_10), .out_11(pipes_49_out_11), .out_12(pipes_49_out_12),
    .out_13(pipes_49_out_13), .out_14(pipes_49_out_14), .out_15(pipes_49_out_15), .out_16(pipes_49_out_16),
    .out_17(pipes_49_out_17), .out_18(pipes_49_out_18), .out_19(pipes_49_out_19), .out_20(pipes_49_out_20),
    .out_21(pipes_49_out_21), .out_22(pipes_49_out_22), .out_23(pipes_49_out_23), .out_24(pipes_49_out_24),
    .out_25(pipes_49_out_25), .out_26(pipes_49_out_26), .out_27(pipes_49_out_27), .out_28(pipes_49_out_28),
    .out_29(pipes_49_out_29), .out_30(pipes_49_out_30), .out_31(pipes_49_out_31), .out_32(pipes_49_out_32),
    .out_33(pipes_49_out_33), .out_34(pipes_49_out_34), .out_35(pipes_49_out_35), .out_36(pipes_49_out_36),
    .pipe(pipes_61_pipe_2), .pipe_2(pipes_49_pipe_2), .signal(pipes_61_signal_2),
    .signal_2(pipes_49_signal_2), .bird_1(pipes_61_bird_1_2), .bird_1_2(pipes_49_bird_1_2),
    .bird_2(pipes_61_bird), .bird(pipes_49_bird));
  DotMatrix #(.matrixcols(32), .matrixrows(32)) dotmatrix_72 (
    .col0(pipes_50_out_5), .col1(pipes_50_out_6), .col2(pipes_50_out_7), .col3(pipes_50_out_8),
    .col4(pipes_50_out_9), .col5(pipes_50_out_10), .col6(pipes_50_out_11), .col7(pipes_50_out_12),
    .col8(pipes_50_out_13), .col9(pipes_50_out_14), .col10(pipes_50_out_15), .col11(pipes_50_out_16),
    .col12(pipes_50_out_17), .col13(pipes_50_out_18), .col14(pipes_50_out_19), .col15(pipes_50_out_20),
    .col16(pipes_50_out_21), .col17(pipes_50_out_22), .col18(pipes_50_out_23), .col19(pipes_50_out_24),
    .col20(pipes_50_out_25), .col21(pipes_50_out_26), .col22(pipes_50_out_27), .col23(pipes_50_out_28),
    .col24(pipes_50_out_29), .col25(pipes_50_out_30), .col26(pipes_50_out_31), .col27(pipes_50_out_32),
    .col28(pipes_50_out_33), .col29(pipes_50_out_34), .col30(pipes_50_out_35), .col31(pipes_50_out_36));
  pipes pipes_50 (
    .out_5(pipes_50_out_5), .out_6(pipes_50_out_6), .out_7(pipes_50_out_7), .out_8(pipes_50_out_8),
    .out_9(pipes_50_out_9), .out_10(pipes_50_out_10), .out_11(pipes_50_out_11), .out_12(pipes_50_out_12),
    .out_13(pipes_50_out_13), .out_14(pipes_50_out_14), .out_15(pipes_50_out_15), .out_16(pipes_50_out_16),
    .out_17(pipes_50_out_17), .out_18(pipes_50_out_18), .out_19(pipes_50_out_19), .out_20(pipes_50_out_20),
    .out_21(pipes_50_out_21), .out_22(pipes_50_out_22), .out_23(pipes_50_out_23), .out_24(pipes_50_out_24),
    .out_25(pipes_50_out_25), .out_26(pipes_50_out_26), .out_27(pipes_50_out_27), .out_28(pipes_50_out_28),
    .out_29(pipes_50_out_29), .out_30(pipes_50_out_30), .out_31(pipes_50_out_31), .out_32(pipes_50_out_32),
    .out_33(pipes_50_out_33), .out_34(pipes_50_out_34), .out_35(pipes_50_out_35), .out_36(pipes_50_out_36),
    .pipe(pipes_62_pipe_2), .pipe_2(pipes_50_pipe_2), .signal(pipes_62_signal_2),
    .signal_2(pipes_50_signal_2), .bird_1(pipes_62_bird_1_2), .bird_1_2(pipes_50_bird_1_2),
    .bird_2(pipes_62_bird), .bird(pipes_50_bird));
  DotMatrix #(.matrixcols(32), .matrixrows(32)) dotmatrix_73 (
    .col0(pipes_51_out_5), .col1(pipes_51_out_6), .col2(pipes_51_out_7), .col3(pipes_51_out_8),
    .col4(pipes_51_out_9), .col5(pipes_51_out_10), .col6(pipes_51_out_11), .col7(pipes_51_out_12),
    .col8(pipes_51_out_13), .col9(pipes_51_out_14), .col10(pipes_51_out_15), .col11(pipes_51_out_16),
    .col12(pipes_51_out_17), .col13(pipes_51_out_18), .col14(pipes_51_out_19), .col15(pipes_51_out_20),
    .col16(pipes_51_out_21), .col17(pipes_51_out_22), .col18(pipes_51_out_23), .col19(pipes_51_out_24),
    .col20(pipes_51_out_25), .col21(pipes_51_out_26), .col22(pipes_51_out_27), .col23(pipes_51_out_28),
    .col24(pipes_51_out_29), .col25(pipes_51_out_30), .col26(pipes_51_out_31), .col27(pipes_51_out_32),
    .col28(pipes_51_out_33), .col29(pipes_51_out_34), .col30(pipes_51_out_35), .col31(pipes_51_out_36));
  pipes pipes_51 (
    .out_5(pipes_51_out_5), .out_6(pipes_51_out_6), .out_7(pipes_51_out_7), .out_8(pipes_51_out_8),
    .out_9(pipes_51_out_9), .out_10(pipes_51_out_10), .out_11(pipes_51_out_11), .out_12(pipes_51_out_12),
    .out_13(pipes_51_out_13), .out_14(pipes_51_out_14), .out_15(pipes_51_out_15), .out_16(pipes_51_out_16),
    .out_17(pipes_51_out_17), .out_18(pipes_51_out_18), .out_19(pipes_51_out_19), .out_20(pipes_51_out_20),
    .out_21(pipes_51_out_21), .out_22(pipes_51_out_22), .out_23(pipes_51_out_23), .out_24(pipes_51_out_24),
    .out_25(pipes_51_out_25), .out_26(pipes_51_out_26), .out_27(pipes_51_out_27), .out_28(pipes_51_out_28),
    .out_29(pipes_51_out_29), .out_30(pipes_51_out_30), .out_31(pipes_51_out_31), .out_32(pipes_51_out_32),
    .out_33(pipes_51_out_33), .out_34(pipes_51_out_34), .out_35(pipes_51_out_35), .out_36(pipes_51_out_36),
    .pipe(pipes_63_pipe_2), .pipe_2(pipes_51_pipe_2), .signal(pipes_63_signal_2),
    .signal_2(pipes_51_signal_2), .bird_1(pipes_63_bird_1_2), .bird_1_2(pipes_51_bird_1_2),
    .bird_2(pipes_63_bird), .bird(pipes_51_bird));
  pipes pipes_52 (
    .out_5(pipes_52_out_5), .out_6(pipes_52_out_6), .out_7(pipes_52_out_7), .out_8(pipes_52_out_8),
    .out_9(pipes_52_out_9), .out_10(pipes_52_out_10), .out_11(pipes_52_out_11), .out_12(pipes_52_out_12),
    .out_13(pipes_52_out_13), .out_14(pipes_52_out_14), .out_15(pipes_52_out_15), .out_16(pipes_52_out_16),
    .out_17(pipes_52_out_17), .out_18(pipes_52_out_18), .out_19(pipes_52_out_19), .out_20(pipes_52_out_20),
    .out_21(pipes_52_out_21), .out_22(pipes_52_out_22), .out_23(pipes_52_out_23), .out_24(pipes_52_out_24),
    .out_25(pipes_52_out_25), .out_26(pipes_52_out_26), .out_27(pipes_52_out_27), .out_28(pipes_52_out_28),
    .out_29(pipes_52_out_29), .out_30(pipes_52_out_30), .out_31(pipes_52_out_31), .out_32(pipes_52_out_32),
    .out_33(pipes_52_out_33), .out_34(pipes_52_out_34), .out_35(pipes_52_out_35), .out_36(pipes_52_out_36),
    .pipe(pipes_64_pipe_2), .pipe_2(pipes_52_pipe_2), .signal(pipes_64_signal_2),
    .signal_2(pipes_52_signal_2), .bird_1(pipes_64_bird_1_2), .bird_1_2(pipes_52_bird_1_2),
    .bird_2(pipes_64_bird), .bird(pipes_52_bird));
  DotMatrix #(.matrixcols(32), .matrixrows(32)) dotmatrix_74 (
    .col0(pipes_52_out_5), .col1(pipes_52_out_6), .col2(pipes_52_out_7), .col3(pipes_52_out_8),
    .col4(pipes_52_out_9), .col5(pipes_52_out_10), .col6(pipes_52_out_11), .col7(pipes_52_out_12),
    .col8(pipes_52_out_13), .col9(pipes_52_out_14), .col10(pipes_52_out_15), .col11(pipes_52_out_16),
    .col12(pipes_52_out_17), .col13(pipes_52_out_18), .col14(pipes_52_out_19), .col15(pipes_52_out_20),
    .col16(pipes_52_out_21), .col17(pipes_52_out_22), .col18(pipes_52_out_23), .col19(pipes_52_out_24),
    .col20(pipes_52_out_25), .col21(pipes_52_out_26), .col22(pipes_52_out_27), .col23(pipes_52_out_28),
    .col24(pipes_52_out_29), .col25(pipes_52_out_30), .col26(pipes_52_out_31), .col27(pipes_52_out_32),
    .col28(pipes_52_out_33), .col29(pipes_52_out_34), .col30(pipes_52_out_35), .col31(pipes_52_out_36));
  DotMatrix #(.matrixcols(32), .matrixrows(32)) dotmatrix_75 (
    .col0(pipes_53_out_5), .col1(pipes_53_out_6), .col2(pipes_53_out_7), .col3(pipes_53_out_8),
    .col4(pipes_53_out_9), .col5(pipes_53_out_10), .col6(pipes_53_out_11), .col7(pipes_53_out_12),
    .col8(pipes_53_out_13), .col9(pipes_53_out_14), .col10(pipes_53_out_15), .col11(pipes_53_out_16),
    .col12(pipes_53_out_17), .col13(pipes_53_out_18), .col14(pipes_53_out_19), .col15(pipes_53_out_20),
    .col16(pipes_53_out_21), .col17(pipes_53_out_22), .col18(pipes_53_out_23), .col19(pipes_53_out_24),
    .col20(pipes_53_out_25), .col21(pipes_53_out_26), .col22(pipes_53_out_27), .col23(pipes_53_out_28),
    .col24(pipes_53_out_29), .col25(pipes_53_out_30), .col26(pipes_53_out_31), .col27(pipes_53_out_32),
    .col28(pipes_53_out_33), .col29(pipes_53_out_34), .col30(pipes_53_out_35), .col31(pipes_53_out_36));
  pipes pipes_53 (
    .out_5(pipes_53_out_5), .out_6(pipes_53_out_6), .out_7(pipes_53_out_7), .out_8(pipes_53_out_8),
    .out_9(pipes_53_out_9), .out_10(pipes_53_out_10), .out_11(pipes_53_out_11), .out_12(pipes_53_out_12),
    .out_13(pipes_53_out_13), .out_14(pipes_53_out_14), .out_15(pipes_53_out_15), .out_16(pipes_53_out_16),
    .out_17(pipes_53_out_17), .out_18(pipes_53_out_18), .out_19(pipes_53_out_19), .out_20(pipes_53_out_20),
    .out_21(pipes_53_out_21), .out_22(pipes_53_out_22), .out_23(pipes_53_out_23), .out_24(pipes_53_out_24),
    .out_25(pipes_53_out_25), .out_26(pipes_53_out_26), .out_27(pipes_53_out_27), .out_28(pipes_53_out_28),
    .out_29(pipes_53_out_29), .out_30(pipes_53_out_30), .out_31(pipes_53_out_31), .out_32(pipes_53_out_32),
    .out_33(pipes_53_out_33), .out_34(pipes_53_out_34), .out_35(pipes_53_out_35), .out_36(pipes_53_out_36),
    .pipe(pipes_65_pipe_2), .pipe_2(pipes_53_pipe_2), .signal(pipes_65_signal_2),
    .signal_2(pipes_53_signal_2), .bird_1(pipes_65_bird_1_2), .bird_1_2(pipes_53_bird_1_2),
    .bird_2(pipes_65_bird), .bird(pipes_53_bird));
  DotMatrix #(.matrixcols(32), .matrixrows(32)) dotmatrix_76 (
    .col0(pipes_54_out_5), .col1(pipes_54_out_6), .col2(pipes_54_out_7), .col3(pipes_54_out_8),
    .col4(pipes_54_out_9), .col5(pipes_54_out_10), .col6(pipes_54_out_11), .col7(pipes_54_out_12),
    .col8(pipes_54_out_13), .col9(pipes_54_out_14), .col10(pipes_54_out_15), .col11(pipes_54_out_16),
    .col12(pipes_54_out_17), .col13(pipes_54_out_18), .col14(pipes_54_out_19), .col15(pipes_54_out_20),
    .col16(pipes_54_out_21), .col17(pipes_54_out_22), .col18(pipes_54_out_23), .col19(pipes_54_out_24),
    .col20(pipes_54_out_25), .col21(pipes_54_out_26), .col22(pipes_54_out_27), .col23(pipes_54_out_28),
    .col24(pipes_54_out_29), .col25(pipes_54_out_30), .col26(pipes_54_out_31), .col27(pipes_54_out_32),
    .col28(pipes_54_out_33), .col29(pipes_54_out_34), .col30(pipes_54_out_35), .col31(pipes_54_out_36));
  pipes pipes_54 (
    .out_5(pipes_54_out_5), .out_6(pipes_54_out_6), .out_7(pipes_54_out_7), .out_8(pipes_54_out_8),
    .out_9(pipes_54_out_9), .out_10(pipes_54_out_10), .out_11(pipes_54_out_11), .out_12(pipes_54_out_12),
    .out_13(pipes_54_out_13), .out_14(pipes_54_out_14), .out_15(pipes_54_out_15), .out_16(pipes_54_out_16),
    .out_17(pipes_54_out_17), .out_18(pipes_54_out_18), .out_19(pipes_54_out_19), .out_20(pipes_54_out_20),
    .out_21(pipes_54_out_21), .out_22(pipes_54_out_22), .out_23(pipes_54_out_23), .out_24(pipes_54_out_24),
    .out_25(pipes_54_out_25), .out_26(pipes_54_out_26), .out_27(pipes_54_out_27), .out_28(pipes_54_out_28),
    .out_29(pipes_54_out_29), .out_30(pipes_54_out_30), .out_31(pipes_54_out_31), .out_32(pipes_54_out_32),
    .out_33(pipes_54_out_33), .out_34(pipes_54_out_34), .out_35(pipes_54_out_35), .out_36(pipes_54_out_36),
    .pipe(pipes_66_pipe_2), .pipe_2(pipes_54_pipe_2), .signal(pipes_66_signal_2),
    .signal_2(pipes_54_signal_2), .bird_1(pipes_66_bird_1_2), .bird_1_2(pipes_54_bird_1_2),
    .bird_2(pipes_66_bird), .bird(pipes_54_bird));
  pipes pipes_55 (
    .out_5(pipes_55_out_5), .out_6(pipes_55_out_6), .out_7(pipes_55_out_7), .out_8(pipes_55_out_8),
    .out_9(pipes_55_out_9), .out_10(pipes_55_out_10), .out_11(pipes_55_out_11), .out_12(pipes_55_out_12),
    .out_13(pipes_55_out_13), .out_14(pipes_55_out_14), .out_15(pipes_55_out_15), .out_16(pipes_55_out_16),
    .out_17(pipes_55_out_17), .out_18(pipes_55_out_18), .out_19(pipes_55_out_19), .out_20(pipes_55_out_20),
    .out_21(pipes_55_out_21), .out_22(pipes_55_out_22), .out_23(pipes_55_out_23), .out_24(pipes_55_out_24),
    .out_25(pipes_55_out_25), .out_26(pipes_55_out_26), .out_27(pipes_55_out_27), .out_28(pipes_55_out_28),
    .out_29(pipes_55_out_29), .out_30(pipes_55_out_30), .out_31(pipes_55_out_31), .out_32(pipes_55_out_32),
    .out_33(pipes_55_out_33), .out_34(pipes_55_out_34), .out_35(pipes_55_out_35), .out_36(pipes_55_out_36),
    .pipe(pipes_67_pipe_2), .pipe_2(pipes_55_pipe_2), .signal(pipes_67_signal_2),
    .signal_2(pipes_55_signal_2), .bird_1(pipes_67_bird_1_2), .bird_1_2(pipes_55_bird_1_2),
    .bird_2(pipes_67_bird), .bird(pipes_55_bird));
  DotMatrix #(.matrixcols(32), .matrixrows(32)) dotmatrix_77 (
    .col0(pipes_55_out_5), .col1(pipes_55_out_6), .col2(pipes_55_out_7), .col3(pipes_55_out_8),
    .col4(pipes_55_out_9), .col5(pipes_55_out_10), .col6(pipes_55_out_11), .col7(pipes_55_out_12),
    .col8(pipes_55_out_13), .col9(pipes_55_out_14), .col10(pipes_55_out_15), .col11(pipes_55_out_16),
    .col12(pipes_55_out_17), .col13(pipes_55_out_18), .col14(pipes_55_out_19), .col15(pipes_55_out_20),
    .col16(pipes_55_out_21), .col17(pipes_55_out_22), .col18(pipes_55_out_23), .col19(pipes_55_out_24),
    .col20(pipes_55_out_25), .col21(pipes_55_out_26), .col22(pipes_55_out_27), .col23(pipes_55_out_28),
    .col24(pipes_55_out_29), .col25(pipes_55_out_30), .col26(pipes_55_out_31), .col27(pipes_55_out_32),
    .col28(pipes_55_out_33), .col29(pipes_55_out_34), .col30(pipes_55_out_35), .col31(pipes_55_out_36));
  pipes pipes_56 (
    .out_5(pipes_56_out_5), .out_6(pipes_56_out_6), .out_7(pipes_56_out_7), .out_8(pipes_56_out_8),
    .out_9(pipes_56_out_9), .out_10(pipes_56_out_10), .out_11(pipes_56_out_11), .out_12(pipes_56_out_12),
    .out_13(pipes_56_out_13), .out_14(pipes_56_out_14), .out_15(pipes_56_out_15), .out_16(pipes_56_out_16),
    .out_17(pipes_56_out_17), .out_18(pipes_56_out_18), .out_19(pipes_56_out_19), .out_20(pipes_56_out_20),
    .out_21(pipes_56_out_21), .out_22(pipes_56_out_22), .out_23(pipes_56_out_23), .out_24(pipes_56_out_24),
    .out_25(pipes_56_out_25), .out_26(pipes_56_out_26), .out_27(pipes_56_out_27), .out_28(pipes_56_out_28),
    .out_29(pipes_56_out_29), .out_30(pipes_56_out_30), .out_31(pipes_56_out_31), .out_32(pipes_56_out_32),
    .out_33(pipes_56_out_33), .out_34(pipes_56_out_34), .out_35(pipes_56_out_35), .out_36(pipes_56_out_36),
    .pipe(pipes_68_pipe_2), .pipe_2(pipes_56_pipe_2), .signal(pipes_68_signal_2),
    .signal_2(pipes_56_signal_2), .bird_1(pipes_68_bird_1_2), .bird_1_2(pipes_56_bird_1_2),
    .bird_2(pipes_68_bird), .bird(pipes_56_bird));
  DotMatrix #(.matrixcols(32), .matrixrows(32)) dotmatrix_78 (
    .col0(pipes_56_out_5), .col1(pipes_56_out_6), .col2(pipes_56_out_7), .col3(pipes_56_out_8),
    .col4(pipes_56_out_9), .col5(pipes_56_out_10), .col6(pipes_56_out_11), .col7(pipes_56_out_12),
    .col8(pipes_56_out_13), .col9(pipes_56_out_14), .col10(pipes_56_out_15), .col11(pipes_56_out_16),
    .col12(pipes_56_out_17), .col13(pipes_56_out_18), .col14(pipes_56_out_19), .col15(pipes_56_out_20),
    .col16(pipes_56_out_21), .col17(pipes_56_out_22), .col18(pipes_56_out_23), .col19(pipes_56_out_24),
    .col20(pipes_56_out_25), .col21(pipes_56_out_26), .col22(pipes_56_out_27), .col23(pipes_56_out_28),
    .col24(pipes_56_out_29), .col25(pipes_56_out_30), .col26(pipes_56_out_31), .col27(pipes_56_out_32),
    .col28(pipes_56_out_33), .col29(pipes_56_out_34), .col30(pipes_56_out_35), .col31(pipes_56_out_36));
  DotMatrix #(.matrixcols(32), .matrixrows(32)) dotmatrix_79 (
    .col0(pipes_57_out_5), .col1(pipes_57_out_6), .col2(pipes_57_out_7), .col3(pipes_57_out_8),
    .col4(pipes_57_out_9), .col5(pipes_57_out_10), .col6(pipes_57_out_11), .col7(pipes_57_out_12),
    .col8(pipes_57_out_13), .col9(pipes_57_out_14), .col10(pipes_57_out_15), .col11(pipes_57_out_16),
    .col12(pipes_57_out_17), .col13(pipes_57_out_18), .col14(pipes_57_out_19), .col15(pipes_57_out_20),
    .col16(pipes_57_out_21), .col17(pipes_57_out_22), .col18(pipes_57_out_23), .col19(pipes_57_out_24),
    .col20(pipes_57_out_25), .col21(pipes_57_out_26), .col22(pipes_57_out_27), .col23(pipes_57_out_28),
    .col24(pipes_57_out_29), .col25(pipes_57_out_30), .col26(pipes_57_out_31), .col27(pipes_57_out_32),
    .col28(pipes_57_out_33), .col29(pipes_57_out_34), .col30(pipes_57_out_35), .col31(pipes_57_out_36));
  pipes pipes_57 (
    .out_5(pipes_57_out_5), .out_6(pipes_57_out_6), .out_7(pipes_57_out_7), .out_8(pipes_57_out_8),
    .out_9(pipes_57_out_9), .out_10(pipes_57_out_10), .out_11(pipes_57_out_11), .out_12(pipes_57_out_12),
    .out_13(pipes_57_out_13), .out_14(pipes_57_out_14), .out_15(pipes_57_out_15), .out_16(pipes_57_out_16),
    .out_17(pipes_57_out_17), .out_18(pipes_57_out_18), .out_19(pipes_57_out_19), .out_20(pipes_57_out_20),
    .out_21(pipes_57_out_21), .out_22(pipes_57_out_22), .out_23(pipes_57_out_23), .out_24(pipes_57_out_24),
    .out_25(pipes_57_out_25), .out_26(pipes_57_out_26), .out_27(pipes_57_out_27), .out_28(pipes_57_out_28),
    .out_29(pipes_57_out_29), .out_30(pipes_57_out_30), .out_31(pipes_57_out_31), .out_32(pipes_57_out_32),
    .out_33(pipes_57_out_33), .out_34(pipes_57_out_34), .out_35(pipes_57_out_35), .out_36(pipes_57_out_36),
    .pipe(pipes_69_pipe_2), .pipe_2(pipes_57_pipe_2), .signal(pipes_69_signal_2),
    .signal_2(pipes_57_signal_2), .bird_1(pipes_69_bird_1_2), .bird_1_2(pipes_57_bird_1_2),
    .bird_2(pipes_69_bird), .bird(pipes_57_bird));
  pipes pipes_58 (
    .out_5(pipes_58_out_5), .out_6(pipes_58_out_6), .out_7(pipes_58_out_7), .out_8(pipes_58_out_8),
    .out_9(pipes_58_out_9), .out_10(pipes_58_out_10), .out_11(pipes_58_out_11), .out_12(pipes_58_out_12),
    .out_13(pipes_58_out_13), .out_14(pipes_58_out_14), .out_15(pipes_58_out_15), .out_16(pipes_58_out_16),
    .out_17(pipes_58_out_17), .out_18(pipes_58_out_18), .out_19(pipes_58_out_19), .out_20(pipes_58_out_20),
    .out_21(pipes_58_out_21), .out_22(pipes_58_out_22), .out_23(pipes_58_out_23), .out_24(pipes_58_out_24),
    .out_25(pipes_58_out_25), .out_26(pipes_58_out_26), .out_27(pipes_58_out_27), .out_28(pipes_58_out_28),
    .out_29(pipes_58_out_29), .out_30(pipes_58_out_30), .out_31(pipes_58_out_31), .out_32(pipes_58_out_32),
    .out_33(pipes_58_out_33), .out_34(pipes_58_out_34), .out_35(pipes_58_out_35), .out_36(pipes_58_out_36),
    .pipe(pipes_70_pipe_2), .pipe_2(pipes_58_pipe_2), .signal(pipes_70_signal_2),
    .signal_2(pipes_58_signal_2), .bird_1(pipes_70_bird_1_2), .bird_1_2(pipes_58_bird_1_2),
    .bird_2(pipes_70_bird), .bird(pipes_58_bird));
  DotMatrix #(.matrixcols(32), .matrixrows(32)) dotmatrix_80 (
    .col0(pipes_58_out_5), .col1(pipes_58_out_6), .col2(pipes_58_out_7), .col3(pipes_58_out_8),
    .col4(pipes_58_out_9), .col5(pipes_58_out_10), .col6(pipes_58_out_11), .col7(pipes_58_out_12),
    .col8(pipes_58_out_13), .col9(pipes_58_out_14), .col10(pipes_58_out_15), .col11(pipes_58_out_16),
    .col12(pipes_58_out_17), .col13(pipes_58_out_18), .col14(pipes_58_out_19), .col15(pipes_58_out_20),
    .col16(pipes_58_out_21), .col17(pipes_58_out_22), .col18(pipes_58_out_23), .col19(pipes_58_out_24),
    .col20(pipes_58_out_25), .col21(pipes_58_out_26), .col22(pipes_58_out_27), .col23(pipes_58_out_28),
    .col24(pipes_58_out_29), .col25(pipes_58_out_30), .col26(pipes_58_out_31), .col27(pipes_58_out_32),
    .col28(pipes_58_out_33), .col29(pipes_58_out_34), .col30(pipes_58_out_35), .col31(pipes_58_out_36));
  pipes pipes_59 (
    .out_5(pipes_59_out_5), .out_6(pipes_59_out_6), .out_7(pipes_59_out_7), .out_8(pipes_59_out_8),
    .out_9(pipes_59_out_9), .out_10(pipes_59_out_10), .out_11(pipes_59_out_11), .out_12(pipes_59_out_12),
    .out_13(pipes_59_out_13), .out_14(pipes_59_out_14), .out_15(pipes_59_out_15), .out_16(pipes_59_out_16),
    .out_17(pipes_59_out_17), .out_18(pipes_59_out_18), .out_19(pipes_59_out_19), .out_20(pipes_59_out_20),
    .out_21(pipes_59_out_21), .out_22(pipes_59_out_22), .out_23(pipes_59_out_23), .out_24(pipes_59_out_24),
    .out_25(pipes_59_out_25), .out_26(pipes_59_out_26), .out_27(pipes_59_out_27), .out_28(pipes_59_out_28),
    .out_29(pipes_59_out_29), .out_30(pipes_59_out_30), .out_31(pipes_59_out_31), .out_32(pipes_59_out_32),
    .out_33(pipes_59_out_33), .out_34(pipes_59_out_34), .out_35(pipes_59_out_35), .out_36(pipes_59_out_36),
    .pipe(pipes_71_pipe_2), .pipe_2(pipes_59_pipe_2), .signal(pipes_71_signal_2),
    .signal_2(pipes_59_signal_2), .bird_1(pipes_71_bird_1_2), .bird_1_2(pipes_59_bird_1_2),
    .bird_2(pipes_71_bird), .bird(pipes_59_bird));
  DotMatrix #(.matrixcols(32), .matrixrows(32)) dotmatrix_81 (
    .col0(pipes_59_out_5), .col1(pipes_59_out_6), .col2(pipes_59_out_7), .col3(pipes_59_out_8),
    .col4(pipes_59_out_9), .col5(pipes_59_out_10), .col6(pipes_59_out_11), .col7(pipes_59_out_12),
    .col8(pipes_59_out_13), .col9(pipes_59_out_14), .col10(pipes_59_out_15), .col11(pipes_59_out_16),
    .col12(pipes_59_out_17), .col13(pipes_59_out_18), .col14(pipes_59_out_19), .col15(pipes_59_out_20),
    .col16(pipes_59_out_21), .col17(pipes_59_out_22), .col18(pipes_59_out_23), .col19(pipes_59_out_24),
    .col20(pipes_59_out_25), .col21(pipes_59_out_26), .col22(pipes_59_out_27), .col23(pipes_59_out_28),
    .col24(pipes_59_out_29), .col25(pipes_59_out_30), .col26(pipes_59_out_31), .col27(pipes_59_out_32),
    .col28(pipes_59_out_33), .col29(pipes_59_out_34), .col30(pipes_59_out_35), .col31(pipes_59_out_36));
  pipes pipes_60 (
    .out_5(pipes_60_out_5), .out_6(pipes_60_out_6), .out_7(pipes_60_out_7), .out_8(pipes_60_out_8),
    .out_9(pipes_60_out_9), .out_10(pipes_60_out_10), .out_11(pipes_60_out_11), .out_12(pipes_60_out_12),
    .out_13(pipes_60_out_13), .out_14(pipes_60_out_14), .out_15(pipes_60_out_15), .out_16(pipes_60_out_16),
    .out_17(pipes_60_out_17), .out_18(pipes_60_out_18), .out_19(pipes_60_out_19), .out_20(pipes_60_out_20),
    .out_21(pipes_60_out_21), .out_22(pipes_60_out_22), .out_23(pipes_60_out_23), .out_24(pipes_60_out_24),
    .out_25(pipes_60_out_25), .out_26(pipes_60_out_26), .out_27(pipes_60_out_27), .out_28(pipes_60_out_28),
    .out_29(pipes_60_out_29), .out_30(pipes_60_out_30), .out_31(pipes_60_out_31), .out_32(pipes_60_out_32),
    .out_33(pipes_60_out_33), .out_34(pipes_60_out_34), .out_35(pipes_60_out_35), .out_36(pipes_60_out_36),
    .pipe(pipes_72_pipe_2), .pipe_2(pipes_60_pipe_2), .signal(pipes_72_signal_2),
    .signal_2(pipes_60_signal_2), .bird_1(pipes_72_bird_1_2), .bird_1_2(pipes_60_bird_1_2),
    .bird_2(pipes_72_bird), .bird(pipes_60_bird));
  DotMatrix #(.matrixcols(32), .matrixrows(32)) dotmatrix_82 (
    .col0(pipes_60_out_5), .col1(pipes_60_out_6), .col2(pipes_60_out_7), .col3(pipes_60_out_8),
    .col4(pipes_60_out_9), .col5(pipes_60_out_10), .col6(pipes_60_out_11), .col7(pipes_60_out_12),
    .col8(pipes_60_out_13), .col9(pipes_60_out_14), .col10(pipes_60_out_15), .col11(pipes_60_out_16),
    .col12(pipes_60_out_17), .col13(pipes_60_out_18), .col14(pipes_60_out_19), .col15(pipes_60_out_20),
    .col16(pipes_60_out_21), .col17(pipes_60_out_22), .col18(pipes_60_out_23), .col19(pipes_60_out_24),
    .col20(pipes_60_out_25), .col21(pipes_60_out_26), .col22(pipes_60_out_27), .col23(pipes_60_out_28),
    .col24(pipes_60_out_29), .col25(pipes_60_out_30), .col26(pipes_60_out_31), .col27(pipes_60_out_32),
    .col28(pipes_60_out_33), .col29(pipes_60_out_34), .col30(pipes_60_out_35), .col31(pipes_60_out_36));
  DotMatrix #(.matrixcols(32), .matrixrows(32)) dotmatrix_83 (
    .col0({32{1'b1}}), .col1({32{1'b1}}), .col2({32{1'b1}}), .col3({32{1'b1}}), .col4({32{1'b1}}),
    .col5({32{1'b1}}), .col6({32{1'b1}}), .col7({32{1'b1}}), .col8({32{1'b1}}), .col9({32{1'b1}}),
    .col10({32{1'b1}}), .col11({32{1'b1}}), .col12({32{1'b1}}), .col13({32{1'b1}}), .col14({32{1'b1}}),
    .col15({32{1'b1}}), .col16({32{1'b1}}), .col17({32{1'b1}}), .col18({32{1'b1}}), .col19({32{1'b1}}),
    .col20({32{1'b1}}), .col21({32{1'b1}}), .col22({32{1'b1}}), .col23({32{1'b1}}), .col24({32{1'b1}}),
    .col25({32{1'b1}}), .col26({32{1'b1}}), .col27({32{1'b1}}), .col28({32{1'b1}}), .col29({32{1'b1}}),
    .col30({32{1'b1}}), .col31({32{1'b1}}));
  DotMatrix #(.matrixcols(32), .matrixrows(32)) dotmatrix_84 (
    .col0({32{1'b1}}), .col1({32{1'b1}}), .col2({32{1'b1}}), .col3({32{1'b1}}), .col4({32{1'b1}}),
    .col5({32{1'b1}}), .col6({32{1'b1}}), .col7({32{1'b1}}), .col8({32{1'b1}}), .col9({32{1'b1}}),
    .col10({32{1'b1}}), .col11({32{1'b1}}), .col12({32{1'b1}}), .col13({32{1'b1}}), .col14({32{1'b1}}),
    .col15({32{1'b1}}), .col16({32{1'b1}}), .col17({32{1'b1}}), .col18({32{1'b1}}), .col19({32{1'b1}}),
    .col20({32{1'b1}}), .col21({32{1'b1}}), .col22({32{1'b1}}), .col23({32{1'b1}}), .col24({32{1'b1}}),
    .col25({32{1'b1}}), .col26({32{1'b1}}), .col27({32{1'b1}}), .col28({32{1'b1}}), .col29({32{1'b1}}),
    .col30({32{1'b1}}), .col31({32{1'b1}}));
  pipes pipes_61 (
    .out_5(pipes_61_out_5), .out_6(pipes_61_out_6), .out_7(pipes_61_out_7), .out_8(pipes_61_out_8),
    .out_9(pipes_61_out_9), .out_10(pipes_61_out_10), .out_11(pipes_61_out_11), .out_12(pipes_61_out_12),
    .out_13(pipes_61_out_13), .out_14(pipes_61_out_14), .out_15(pipes_61_out_15), .out_16(pipes_61_out_16),
    .out_17(pipes_61_out_17), .out_18(pipes_61_out_18), .out_19(pipes_61_out_19), .out_20(pipes_61_out_20),
    .out_21(pipes_61_out_21), .out_22(pipes_61_out_22), .out_23(pipes_61_out_23), .out_24(pipes_61_out_24),
    .out_25(pipes_61_out_25), .out_26(pipes_61_out_26), .out_27(pipes_61_out_27), .out_28(pipes_61_out_28),
    .out_29(pipes_61_out_29), .out_30(pipes_61_out_30), .out_31(pipes_61_out_31), .out_32(pipes_61_out_32),
    .out_33(pipes_61_out_33), .out_34(pipes_61_out_34), .out_35(pipes_61_out_35), .out_36(pipes_61_out_36),
    .pipe(pipes_73_pipe_2), .pipe_2(pipes_61_pipe_2), .signal(pipes_73_signal_2),
    .signal_2(pipes_61_signal_2), .bird_1(pipes_73_bird_1_2), .bird_1_2(pipes_61_bird_1_2),
    .bird_2(pipes_73_bird), .bird(pipes_61_bird));
  DotMatrix #(.matrixcols(32), .matrixrows(32)) dotmatrix_85 (
    .col0(pipes_61_out_5), .col1(pipes_61_out_6), .col2(pipes_61_out_7), .col3(pipes_61_out_8),
    .col4(pipes_61_out_9), .col5(pipes_61_out_10), .col6(pipes_61_out_11), .col7(pipes_61_out_12),
    .col8(pipes_61_out_13), .col9(pipes_61_out_14), .col10(pipes_61_out_15), .col11(pipes_61_out_16),
    .col12(pipes_61_out_17), .col13(pipes_61_out_18), .col14(pipes_61_out_19), .col15(pipes_61_out_20),
    .col16(pipes_61_out_21), .col17(pipes_61_out_22), .col18(pipes_61_out_23), .col19(pipes_61_out_24),
    .col20(pipes_61_out_25), .col21(pipes_61_out_26), .col22(pipes_61_out_27), .col23(pipes_61_out_28),
    .col24(pipes_61_out_29), .col25(pipes_61_out_30), .col26(pipes_61_out_31), .col27(pipes_61_out_32),
    .col28(pipes_61_out_33), .col29(pipes_61_out_34), .col30(pipes_61_out_35), .col31(pipes_61_out_36));
  DotMatrix #(.matrixcols(32), .matrixrows(32)) dotmatrix_86 (
    .col0(pipes_62_out_5), .col1(pipes_62_out_6), .col2(pipes_62_out_7), .col3(pipes_62_out_8),
    .col4(pipes_62_out_9), .col5(pipes_62_out_10), .col6(pipes_62_out_11), .col7(pipes_62_out_12),
    .col8(pipes_62_out_13), .col9(pipes_62_out_14), .col10(pipes_62_out_15), .col11(pipes_62_out_16),
    .col12(pipes_62_out_17), .col13(pipes_62_out_18), .col14(pipes_62_out_19), .col15(pipes_62_out_20),
    .col16(pipes_62_out_21), .col17(pipes_62_out_22), .col18(pipes_62_out_23), .col19(pipes_62_out_24),
    .col20(pipes_62_out_25), .col21(pipes_62_out_26), .col22(pipes_62_out_27), .col23(pipes_62_out_28),
    .col24(pipes_62_out_29), .col25(pipes_62_out_30), .col26(pipes_62_out_31), .col27(pipes_62_out_32),
    .col28(pipes_62_out_33), .col29(pipes_62_out_34), .col30(pipes_62_out_35), .col31(pipes_62_out_36));
  pipes pipes_62 (
    .out_5(pipes_62_out_5), .out_6(pipes_62_out_6), .out_7(pipes_62_out_7), .out_8(pipes_62_out_8),
    .out_9(pipes_62_out_9), .out_10(pipes_62_out_10), .out_11(pipes_62_out_11), .out_12(pipes_62_out_12),
    .out_13(pipes_62_out_13), .out_14(pipes_62_out_14), .out_15(pipes_62_out_15), .out_16(pipes_62_out_16),
    .out_17(pipes_62_out_17), .out_18(pipes_62_out_18), .out_19(pipes_62_out_19), .out_20(pipes_62_out_20),
    .out_21(pipes_62_out_21), .out_22(pipes_62_out_22), .out_23(pipes_62_out_23), .out_24(pipes_62_out_24),
    .out_25(pipes_62_out_25), .out_26(pipes_62_out_26), .out_27(pipes_62_out_27), .out_28(pipes_62_out_28),
    .out_29(pipes_62_out_29), .out_30(pipes_62_out_30), .out_31(pipes_62_out_31), .out_32(pipes_62_out_32),
    .out_33(pipes_62_out_33), .out_34(pipes_62_out_34), .out_35(pipes_62_out_35), .out_36(pipes_62_out_36),
    .pipe(pipes_74_pipe_2), .pipe_2(pipes_62_pipe_2), .signal(pipes_74_signal_2),
    .signal_2(pipes_62_signal_2), .bird_1(pipes_74_bird_1_2), .bird_1_2(pipes_62_bird_1_2),
    .bird_2(pipes_74_bird), .bird(pipes_62_bird));
  DotMatrix #(.matrixcols(32), .matrixrows(32)) dotmatrix_87 (
    .col0(pipes_63_out_5), .col1(pipes_63_out_6), .col2(pipes_63_out_7), .col3(pipes_63_out_8),
    .col4(pipes_63_out_9), .col5(pipes_63_out_10), .col6(pipes_63_out_11), .col7(pipes_63_out_12),
    .col8(pipes_63_out_13), .col9(pipes_63_out_14), .col10(pipes_63_out_15), .col11(pipes_63_out_16),
    .col12(pipes_63_out_17), .col13(pipes_63_out_18), .col14(pipes_63_out_19), .col15(pipes_63_out_20),
    .col16(pipes_63_out_21), .col17(pipes_63_out_22), .col18(pipes_63_out_23), .col19(pipes_63_out_24),
    .col20(pipes_63_out_25), .col21(pipes_63_out_26), .col22(pipes_63_out_27), .col23(pipes_63_out_28),
    .col24(pipes_63_out_29), .col25(pipes_63_out_30), .col26(pipes_63_out_31), .col27(pipes_63_out_32),
    .col28(pipes_63_out_33), .col29(pipes_63_out_34), .col30(pipes_63_out_35), .col31(pipes_63_out_36));
  pipes pipes_63 (
    .out_5(pipes_63_out_5), .out_6(pipes_63_out_6), .out_7(pipes_63_out_7), .out_8(pipes_63_out_8),
    .out_9(pipes_63_out_9), .out_10(pipes_63_out_10), .out_11(pipes_63_out_11), .out_12(pipes_63_out_12),
    .out_13(pipes_63_out_13), .out_14(pipes_63_out_14), .out_15(pipes_63_out_15), .out_16(pipes_63_out_16),
    .out_17(pipes_63_out_17), .out_18(pipes_63_out_18), .out_19(pipes_63_out_19), .out_20(pipes_63_out_20),
    .out_21(pipes_63_out_21), .out_22(pipes_63_out_22), .out_23(pipes_63_out_23), .out_24(pipes_63_out_24),
    .out_25(pipes_63_out_25), .out_26(pipes_63_out_26), .out_27(pipes_63_out_27), .out_28(pipes_63_out_28),
    .out_29(pipes_63_out_29), .out_30(pipes_63_out_30), .out_31(pipes_63_out_31), .out_32(pipes_63_out_32),
    .out_33(pipes_63_out_33), .out_34(pipes_63_out_34), .out_35(pipes_63_out_35), .out_36(pipes_63_out_36),
    .pipe(pipes_75_pipe_2), .pipe_2(pipes_63_pipe_2), .signal(pipes_75_signal_2),
    .signal_2(pipes_63_signal_2), .bird_1(pipes_75_bird_1_2), .bird_1_2(pipes_63_bird_1_2),
    .bird_2(pipes_75_bird), .bird(pipes_63_bird));
  pipes pipes_64 (
    .out_5(pipes_64_out_5), .out_6(pipes_64_out_6), .out_7(pipes_64_out_7), .out_8(pipes_64_out_8),
    .out_9(pipes_64_out_9), .out_10(pipes_64_out_10), .out_11(pipes_64_out_11), .out_12(pipes_64_out_12),
    .out_13(pipes_64_out_13), .out_14(pipes_64_out_14), .out_15(pipes_64_out_15), .out_16(pipes_64_out_16),
    .out_17(pipes_64_out_17), .out_18(pipes_64_out_18), .out_19(pipes_64_out_19), .out_20(pipes_64_out_20),
    .out_21(pipes_64_out_21), .out_22(pipes_64_out_22), .out_23(pipes_64_out_23), .out_24(pipes_64_out_24),
    .out_25(pipes_64_out_25), .out_26(pipes_64_out_26), .out_27(pipes_64_out_27), .out_28(pipes_64_out_28),
    .out_29(pipes_64_out_29), .out_30(pipes_64_out_30), .out_31(pipes_64_out_31), .out_32(pipes_64_out_32),
    .out_33(pipes_64_out_33), .out_34(pipes_64_out_34), .out_35(pipes_64_out_35), .out_36(pipes_64_out_36),
    .pipe(pipes_76_pipe_2), .pipe_2(pipes_64_pipe_2), .signal(pipes_76_signal_2),
    .signal_2(pipes_64_signal_2), .bird_1(pipes_76_bird_1_2), .bird_1_2(pipes_64_bird_1_2),
    .bird_2(pipes_76_bird), .bird(pipes_64_bird));
  DotMatrix #(.matrixcols(32), .matrixrows(32)) dotmatrix_88 (
    .col0(pipes_64_out_5), .col1(pipes_64_out_6), .col2(pipes_64_out_7), .col3(pipes_64_out_8),
    .col4(pipes_64_out_9), .col5(pipes_64_out_10), .col6(pipes_64_out_11), .col7(pipes_64_out_12),
    .col8(pipes_64_out_13), .col9(pipes_64_out_14), .col10(pipes_64_out_15), .col11(pipes_64_out_16),
    .col12(pipes_64_out_17), .col13(pipes_64_out_18), .col14(pipes_64_out_19), .col15(pipes_64_out_20),
    .col16(pipes_64_out_21), .col17(pipes_64_out_22), .col18(pipes_64_out_23), .col19(pipes_64_out_24),
    .col20(pipes_64_out_25), .col21(pipes_64_out_26), .col22(pipes_64_out_27), .col23(pipes_64_out_28),
    .col24(pipes_64_out_29), .col25(pipes_64_out_30), .col26(pipes_64_out_31), .col27(pipes_64_out_32),
    .col28(pipes_64_out_33), .col29(pipes_64_out_34), .col30(pipes_64_out_35), .col31(pipes_64_out_36));
  DotMatrix #(.matrixcols(32), .matrixrows(32)) dotmatrix_89 (
    .col0(pipes_65_out_5), .col1(pipes_65_out_6), .col2(pipes_65_out_7), .col3(pipes_65_out_8),
    .col4(pipes_65_out_9), .col5(pipes_65_out_10), .col6(pipes_65_out_11), .col7(pipes_65_out_12),
    .col8(pipes_65_out_13), .col9(pipes_65_out_14), .col10(pipes_65_out_15), .col11(pipes_65_out_16),
    .col12(pipes_65_out_17), .col13(pipes_65_out_18), .col14(pipes_65_out_19), .col15(pipes_65_out_20),
    .col16(pipes_65_out_21), .col17(pipes_65_out_22), .col18(pipes_65_out_23), .col19(pipes_65_out_24),
    .col20(pipes_65_out_25), .col21(pipes_65_out_26), .col22(pipes_65_out_27), .col23(pipes_65_out_28),
    .col24(pipes_65_out_29), .col25(pipes_65_out_30), .col26(pipes_65_out_31), .col27(pipes_65_out_32),
    .col28(pipes_65_out_33), .col29(pipes_65_out_34), .col30(pipes_65_out_35), .col31(pipes_65_out_36));
  pipes pipes_65 (
    .out_5(pipes_65_out_5), .out_6(pipes_65_out_6), .out_7(pipes_65_out_7), .out_8(pipes_65_out_8),
    .out_9(pipes_65_out_9), .out_10(pipes_65_out_10), .out_11(pipes_65_out_11), .out_12(pipes_65_out_12),
    .out_13(pipes_65_out_13), .out_14(pipes_65_out_14), .out_15(pipes_65_out_15), .out_16(pipes_65_out_16),
    .out_17(pipes_65_out_17), .out_18(pipes_65_out_18), .out_19(pipes_65_out_19), .out_20(pipes_65_out_20),
    .out_21(pipes_65_out_21), .out_22(pipes_65_out_22), .out_23(pipes_65_out_23), .out_24(pipes_65_out_24),
    .out_25(pipes_65_out_25), .out_26(pipes_65_out_26), .out_27(pipes_65_out_27), .out_28(pipes_65_out_28),
    .out_29(pipes_65_out_29), .out_30(pipes_65_out_30), .out_31(pipes_65_out_31), .out_32(pipes_65_out_32),
    .out_33(pipes_65_out_33), .out_34(pipes_65_out_34), .out_35(pipes_65_out_35), .out_36(pipes_65_out_36),
    .pipe(pipes_77_pipe_2), .pipe_2(pipes_65_pipe_2), .signal(pipes_77_signal_2),
    .signal_2(pipes_65_signal_2), .bird_1(pipes_77_bird_1_2), .bird_1_2(pipes_65_bird_1_2),
    .bird_2(pipes_77_bird), .bird(pipes_65_bird));
  pipes pipes_66 (
    .out_5(pipes_66_out_5), .out_6(pipes_66_out_6), .out_7(pipes_66_out_7), .out_8(pipes_66_out_8),
    .out_9(pipes_66_out_9), .out_10(pipes_66_out_10), .out_11(pipes_66_out_11), .out_12(pipes_66_out_12),
    .out_13(pipes_66_out_13), .out_14(pipes_66_out_14), .out_15(pipes_66_out_15), .out_16(pipes_66_out_16),
    .out_17(pipes_66_out_17), .out_18(pipes_66_out_18), .out_19(pipes_66_out_19), .out_20(pipes_66_out_20),
    .out_21(pipes_66_out_21), .out_22(pipes_66_out_22), .out_23(pipes_66_out_23), .out_24(pipes_66_out_24),
    .out_25(pipes_66_out_25), .out_26(pipes_66_out_26), .out_27(pipes_66_out_27), .out_28(pipes_66_out_28),
    .out_29(pipes_66_out_29), .out_30(pipes_66_out_30), .out_31(pipes_66_out_31), .out_32(pipes_66_out_32),
    .out_33(pipes_66_out_33), .out_34(pipes_66_out_34), .out_35(pipes_66_out_35), .out_36(pipes_66_out_36),
    .pipe(pipes_78_pipe_2), .pipe_2(pipes_66_pipe_2), .signal(pipes_78_signal_2),
    .signal_2(pipes_66_signal_2), .bird_1(pipes_78_bird_1_2), .bird_1_2(pipes_66_bird_1_2),
    .bird_2(pipes_78_bird), .bird(pipes_66_bird));
  DotMatrix #(.matrixcols(32), .matrixrows(32)) dotmatrix_90 (
    .col0(pipes_66_out_5), .col1(pipes_66_out_6), .col2(pipes_66_out_7), .col3(pipes_66_out_8),
    .col4(pipes_66_out_9), .col5(pipes_66_out_10), .col6(pipes_66_out_11), .col7(pipes_66_out_12),
    .col8(pipes_66_out_13), .col9(pipes_66_out_14), .col10(pipes_66_out_15), .col11(pipes_66_out_16),
    .col12(pipes_66_out_17), .col13(pipes_66_out_18), .col14(pipes_66_out_19), .col15(pipes_66_out_20),
    .col16(pipes_66_out_21), .col17(pipes_66_out_22), .col18(pipes_66_out_23), .col19(pipes_66_out_24),
    .col20(pipes_66_out_25), .col21(pipes_66_out_26), .col22(pipes_66_out_27), .col23(pipes_66_out_28),
    .col24(pipes_66_out_29), .col25(pipes_66_out_30), .col26(pipes_66_out_31), .col27(pipes_66_out_32),
    .col28(pipes_66_out_33), .col29(pipes_66_out_34), .col30(pipes_66_out_35), .col31(pipes_66_out_36));
  pipes pipes_67 (
    .out_5(pipes_67_out_5), .out_6(pipes_67_out_6), .out_7(pipes_67_out_7), .out_8(pipes_67_out_8),
    .out_9(pipes_67_out_9), .out_10(pipes_67_out_10), .out_11(pipes_67_out_11), .out_12(pipes_67_out_12),
    .out_13(pipes_67_out_13), .out_14(pipes_67_out_14), .out_15(pipes_67_out_15), .out_16(pipes_67_out_16),
    .out_17(pipes_67_out_17), .out_18(pipes_67_out_18), .out_19(pipes_67_out_19), .out_20(pipes_67_out_20),
    .out_21(pipes_67_out_21), .out_22(pipes_67_out_22), .out_23(pipes_67_out_23), .out_24(pipes_67_out_24),
    .out_25(pipes_67_out_25), .out_26(pipes_67_out_26), .out_27(pipes_67_out_27), .out_28(pipes_67_out_28),
    .out_29(pipes_67_out_29), .out_30(pipes_67_out_30), .out_31(pipes_67_out_31), .out_32(pipes_67_out_32),
    .out_33(pipes_67_out_33), .out_34(pipes_67_out_34), .out_35(pipes_67_out_35), .out_36(pipes_67_out_36),
    .pipe(pipes_79_pipe_2), .pipe_2(pipes_67_pipe_2), .signal(pipes_79_signal_2),
    .signal_2(pipes_67_signal_2), .bird_1(pipes_79_bird_1_2), .bird_1_2(pipes_67_bird_1_2),
    .bird_2(pipes_79_bird), .bird(pipes_67_bird));
  DotMatrix #(.matrixcols(32), .matrixrows(32)) dotmatrix_91 (
    .col0(pipes_67_out_5), .col1(pipes_67_out_6), .col2(pipes_67_out_7), .col3(pipes_67_out_8),
    .col4(pipes_67_out_9), .col5(pipes_67_out_10), .col6(pipes_67_out_11), .col7(pipes_67_out_12),
    .col8(pipes_67_out_13), .col9(pipes_67_out_14), .col10(pipes_67_out_15), .col11(pipes_67_out_16),
    .col12(pipes_67_out_17), .col13(pipes_67_out_18), .col14(pipes_67_out_19), .col15(pipes_67_out_20),
    .col16(pipes_67_out_21), .col17(pipes_67_out_22), .col18(pipes_67_out_23), .col19(pipes_67_out_24),
    .col20(pipes_67_out_25), .col21(pipes_67_out_26), .col22(pipes_67_out_27), .col23(pipes_67_out_28),
    .col24(pipes_67_out_29), .col25(pipes_67_out_30), .col26(pipes_67_out_31), .col27(pipes_67_out_32),
    .col28(pipes_67_out_33), .col29(pipes_67_out_34), .col30(pipes_67_out_35), .col31(pipes_67_out_36));
  pipes pipes_68 (
    .out_5(pipes_68_out_5), .out_6(pipes_68_out_6), .out_7(pipes_68_out_7), .out_8(pipes_68_out_8),
    .out_9(pipes_68_out_9), .out_10(pipes_68_out_10), .out_11(pipes_68_out_11), .out_12(pipes_68_out_12),
    .out_13(pipes_68_out_13), .out_14(pipes_68_out_14), .out_15(pipes_68_out_15), .out_16(pipes_68_out_16),
    .out_17(pipes_68_out_17), .out_18(pipes_68_out_18), .out_19(pipes_68_out_19), .out_20(pipes_68_out_20),
    .out_21(pipes_68_out_21), .out_22(pipes_68_out_22), .out_23(pipes_68_out_23), .out_24(pipes_68_out_24),
    .out_25(pipes_68_out_25), .out_26(pipes_68_out_26), .out_27(pipes_68_out_27), .out_28(pipes_68_out_28),
    .out_29(pipes_68_out_29), .out_30(pipes_68_out_30), .out_31(pipes_68_out_31), .out_32(pipes_68_out_32),
    .out_33(pipes_68_out_33), .out_34(pipes_68_out_34), .out_35(pipes_68_out_35), .out_36(pipes_68_out_36),
    .pipe(pipes_80_pipe_2), .pipe_2(pipes_68_pipe_2), .signal(pipes_80_signal_2),
    .signal_2(pipes_68_signal_2), .bird_1(pipes_80_bird_1_2), .bird_1_2(pipes_68_bird_1_2),
    .bird_2(pipes_80_bird), .bird(pipes_68_bird));
  DotMatrix #(.matrixcols(32), .matrixrows(32)) dotmatrix_92 (
    .col0(pipes_68_out_5), .col1(pipes_68_out_6), .col2(pipes_68_out_7), .col3(pipes_68_out_8),
    .col4(pipes_68_out_9), .col5(pipes_68_out_10), .col6(pipes_68_out_11), .col7(pipes_68_out_12),
    .col8(pipes_68_out_13), .col9(pipes_68_out_14), .col10(pipes_68_out_15), .col11(pipes_68_out_16),
    .col12(pipes_68_out_17), .col13(pipes_68_out_18), .col14(pipes_68_out_19), .col15(pipes_68_out_20),
    .col16(pipes_68_out_21), .col17(pipes_68_out_22), .col18(pipes_68_out_23), .col19(pipes_68_out_24),
    .col20(pipes_68_out_25), .col21(pipes_68_out_26), .col22(pipes_68_out_27), .col23(pipes_68_out_28),
    .col24(pipes_68_out_29), .col25(pipes_68_out_30), .col26(pipes_68_out_31), .col27(pipes_68_out_32),
    .col28(pipes_68_out_33), .col29(pipes_68_out_34), .col30(pipes_68_out_35), .col31(pipes_68_out_36));
  DotMatrix #(.matrixcols(32), .matrixrows(32)) dotmatrix_93 (
    .col0(pipes_69_out_5), .col1(pipes_69_out_6), .col2(pipes_69_out_7), .col3(pipes_69_out_8),
    .col4(pipes_69_out_9), .col5(pipes_69_out_10), .col6(pipes_69_out_11), .col7(pipes_69_out_12),
    .col8(pipes_69_out_13), .col9(pipes_69_out_14), .col10(pipes_69_out_15), .col11(pipes_69_out_16),
    .col12(pipes_69_out_17), .col13(pipes_69_out_18), .col14(pipes_69_out_19), .col15(pipes_69_out_20),
    .col16(pipes_69_out_21), .col17(pipes_69_out_22), .col18(pipes_69_out_23), .col19(pipes_69_out_24),
    .col20(pipes_69_out_25), .col21(pipes_69_out_26), .col22(pipes_69_out_27), .col23(pipes_69_out_28),
    .col24(pipes_69_out_29), .col25(pipes_69_out_30), .col26(pipes_69_out_31), .col27(pipes_69_out_32),
    .col28(pipes_69_out_33), .col29(pipes_69_out_34), .col30(pipes_69_out_35), .col31(pipes_69_out_36));
  pipes pipes_69 (
    .out_5(pipes_69_out_5), .out_6(pipes_69_out_6), .out_7(pipes_69_out_7), .out_8(pipes_69_out_8),
    .out_9(pipes_69_out_9), .out_10(pipes_69_out_10), .out_11(pipes_69_out_11), .out_12(pipes_69_out_12),
    .out_13(pipes_69_out_13), .out_14(pipes_69_out_14), .out_15(pipes_69_out_15), .out_16(pipes_69_out_16),
    .out_17(pipes_69_out_17), .out_18(pipes_69_out_18), .out_19(pipes_69_out_19), .out_20(pipes_69_out_20),
    .out_21(pipes_69_out_21), .out_22(pipes_69_out_22), .out_23(pipes_69_out_23), .out_24(pipes_69_out_24),
    .out_25(pipes_69_out_25), .out_26(pipes_69_out_26), .out_27(pipes_69_out_27), .out_28(pipes_69_out_28),
    .out_29(pipes_69_out_29), .out_30(pipes_69_out_30), .out_31(pipes_69_out_31), .out_32(pipes_69_out_32),
    .out_33(pipes_69_out_33), .out_34(pipes_69_out_34), .out_35(pipes_69_out_35), .out_36(pipes_69_out_36),
    .pipe(pipes_81_pipe_2), .pipe_2(pipes_69_pipe_2), .signal(pipes_81_signal_2),
    .signal_2(pipes_69_signal_2), .bird_1(pipes_81_bird_1_2), .bird_1_2(pipes_69_bird_1_2),
    .bird_2(pipes_81_bird), .bird(pipes_69_bird));
  DotMatrix #(.matrixcols(32), .matrixrows(32)) dotmatrix_94 (
    .col0(pipes_70_out_5), .col1(pipes_70_out_6), .col2(pipes_70_out_7), .col3(pipes_70_out_8),
    .col4(pipes_70_out_9), .col5(pipes_70_out_10), .col6(pipes_70_out_11), .col7(pipes_70_out_12),
    .col8(pipes_70_out_13), .col9(pipes_70_out_14), .col10(pipes_70_out_15), .col11(pipes_70_out_16),
    .col12(pipes_70_out_17), .col13(pipes_70_out_18), .col14(pipes_70_out_19), .col15(pipes_70_out_20),
    .col16(pipes_70_out_21), .col17(pipes_70_out_22), .col18(pipes_70_out_23), .col19(pipes_70_out_24),
    .col20(pipes_70_out_25), .col21(pipes_70_out_26), .col22(pipes_70_out_27), .col23(pipes_70_out_28),
    .col24(pipes_70_out_29), .col25(pipes_70_out_30), .col26(pipes_70_out_31), .col27(pipes_70_out_32),
    .col28(pipes_70_out_33), .col29(pipes_70_out_34), .col30(pipes_70_out_35), .col31(pipes_70_out_36));
  pipes pipes_70 (
    .out_5(pipes_70_out_5), .out_6(pipes_70_out_6), .out_7(pipes_70_out_7), .out_8(pipes_70_out_8),
    .out_9(pipes_70_out_9), .out_10(pipes_70_out_10), .out_11(pipes_70_out_11), .out_12(pipes_70_out_12),
    .out_13(pipes_70_out_13), .out_14(pipes_70_out_14), .out_15(pipes_70_out_15), .out_16(pipes_70_out_16),
    .out_17(pipes_70_out_17), .out_18(pipes_70_out_18), .out_19(pipes_70_out_19), .out_20(pipes_70_out_20),
    .out_21(pipes_70_out_21), .out_22(pipes_70_out_22), .out_23(pipes_70_out_23), .out_24(pipes_70_out_24),
    .out_25(pipes_70_out_25), .out_26(pipes_70_out_26), .out_27(pipes_70_out_27), .out_28(pipes_70_out_28),
    .out_29(pipes_70_out_29), .out_30(pipes_70_out_30), .out_31(pipes_70_out_31), .out_32(pipes_70_out_32),
    .out_33(pipes_70_out_33), .out_34(pipes_70_out_34), .out_35(pipes_70_out_35), .out_36(pipes_70_out_36),
    .pipe(pipes_82_pipe_2), .pipe_2(pipes_70_pipe_2), .signal(pipes_82_signal_2),
    .signal_2(pipes_70_signal_2), .bird_1(pipes_82_bird_1_2), .bird_1_2(pipes_70_bird_1_2),
    .bird_2(pipes_82_bird), .bird(pipes_70_bird));
  pipes pipes_71 (
    .out_5(pipes_71_out_5), .out_6(pipes_71_out_6), .out_7(pipes_71_out_7), .out_8(pipes_71_out_8),
    .out_9(pipes_71_out_9), .out_10(pipes_71_out_10), .out_11(pipes_71_out_11), .out_12(pipes_71_out_12),
    .out_13(pipes_71_out_13), .out_14(pipes_71_out_14), .out_15(pipes_71_out_15), .out_16(pipes_71_out_16),
    .out_17(pipes_71_out_17), .out_18(pipes_71_out_18), .out_19(pipes_71_out_19), .out_20(pipes_71_out_20),
    .out_21(pipes_71_out_21), .out_22(pipes_71_out_22), .out_23(pipes_71_out_23), .out_24(pipes_71_out_24),
    .out_25(pipes_71_out_25), .out_26(pipes_71_out_26), .out_27(pipes_71_out_27), .out_28(pipes_71_out_28),
    .out_29(pipes_71_out_29), .out_30(pipes_71_out_30), .out_31(pipes_71_out_31), .out_32(pipes_71_out_32),
    .out_33(pipes_71_out_33), .out_34(pipes_71_out_34), .out_35(pipes_71_out_35), .out_36(pipes_71_out_36),
    .pipe(pipes_83_pipe_2), .pipe_2(pipes_71_pipe_2), .signal(pipes_83_signal_2),
    .signal_2(pipes_71_signal_2), .bird_1(pipes_83_bird_1_2), .bird_1_2(pipes_71_bird_1_2),
    .bird_2(pipes_83_bird), .bird(pipes_71_bird));
  DotMatrix #(.matrixcols(32), .matrixrows(32)) dotmatrix_95 (
    .col0(pipes_71_out_5), .col1(pipes_71_out_6), .col2(pipes_71_out_7), .col3(pipes_71_out_8),
    .col4(pipes_71_out_9), .col5(pipes_71_out_10), .col6(pipes_71_out_11), .col7(pipes_71_out_12),
    .col8(pipes_71_out_13), .col9(pipes_71_out_14), .col10(pipes_71_out_15), .col11(pipes_71_out_16),
    .col12(pipes_71_out_17), .col13(pipes_71_out_18), .col14(pipes_71_out_19), .col15(pipes_71_out_20),
    .col16(pipes_71_out_21), .col17(pipes_71_out_22), .col18(pipes_71_out_23), .col19(pipes_71_out_24),
    .col20(pipes_71_out_25), .col21(pipes_71_out_26), .col22(pipes_71_out_27), .col23(pipes_71_out_28),
    .col24(pipes_71_out_29), .col25(pipes_71_out_30), .col26(pipes_71_out_31), .col27(pipes_71_out_32),
    .col28(pipes_71_out_33), .col29(pipes_71_out_34), .col30(pipes_71_out_35), .col31(pipes_71_out_36));
  DotMatrix #(.matrixcols(32), .matrixrows(32)) dotmatrix_96 (
    .col0(pipes_72_out_5), .col1(pipes_72_out_6), .col2(pipes_72_out_7), .col3(pipes_72_out_8),
    .col4(pipes_72_out_9), .col5(pipes_72_out_10), .col6(pipes_72_out_11), .col7(pipes_72_out_12),
    .col8(pipes_72_out_13), .col9(pipes_72_out_14), .col10(pipes_72_out_15), .col11(pipes_72_out_16),
    .col12(pipes_72_out_17), .col13(pipes_72_out_18), .col14(pipes_72_out_19), .col15(pipes_72_out_20),
    .col16(pipes_72_out_21), .col17(pipes_72_out_22), .col18(pipes_72_out_23), .col19(pipes_72_out_24),
    .col20(pipes_72_out_25), .col21(pipes_72_out_26), .col22(pipes_72_out_27), .col23(pipes_72_out_28),
    .col24(pipes_72_out_29), .col25(pipes_72_out_30), .col26(pipes_72_out_31), .col27(pipes_72_out_32),
    .col28(pipes_72_out_33), .col29(pipes_72_out_34), .col30(pipes_72_out_35), .col31(pipes_72_out_36));
  pipes pipes_72 (
    .out_5(pipes_72_out_5), .out_6(pipes_72_out_6), .out_7(pipes_72_out_7), .out_8(pipes_72_out_8),
    .out_9(pipes_72_out_9), .out_10(pipes_72_out_10), .out_11(pipes_72_out_11), .out_12(pipes_72_out_12),
    .out_13(pipes_72_out_13), .out_14(pipes_72_out_14), .out_15(pipes_72_out_15), .out_16(pipes_72_out_16),
    .out_17(pipes_72_out_17), .out_18(pipes_72_out_18), .out_19(pipes_72_out_19), .out_20(pipes_72_out_20),
    .out_21(pipes_72_out_21), .out_22(pipes_72_out_22), .out_23(pipes_72_out_23), .out_24(pipes_72_out_24),
    .out_25(pipes_72_out_25), .out_26(pipes_72_out_26), .out_27(pipes_72_out_27), .out_28(pipes_72_out_28),
    .out_29(pipes_72_out_29), .out_30(pipes_72_out_30), .out_31(pipes_72_out_31), .out_32(pipes_72_out_32),
    .out_33(pipes_72_out_33), .out_34(pipes_72_out_34), .out_35(pipes_72_out_35), .out_36(pipes_72_out_36),
    .pipe(pipes_84_pipe_2), .pipe_2(pipes_72_pipe_2), .signal(pipes_84_signal_2),
    .signal_2(pipes_72_signal_2), .bird_1(pipes_84_bird_1_2), .bird_1_2(pipes_72_bird_1_2),
    .bird_2(pipes_84_bird), .bird(pipes_72_bird));
  DotMatrix #(.matrixcols(32), .matrixrows(32)) dotmatrix_97 (
    .col0({32{1'b1}}), .col1({32{1'b1}}), .col2({32{1'b1}}), .col3({32{1'b1}}), .col4({32{1'b1}}),
    .col5({32{1'b1}}), .col6({32{1'b1}}), .col7({32{1'b1}}), .col8({32{1'b1}}), .col9({32{1'b1}}),
    .col10({32{1'b1}}), .col11({32{1'b1}}), .col12({32{1'b1}}), .col13({32{1'b1}}), .col14({32{1'b1}}),
    .col15({32{1'b1}}), .col16({32{1'b1}}), .col17({32{1'b1}}), .col18({32{1'b1}}), .col19({32{1'b1}}),
    .col20({32{1'b1}}), .col21({32{1'b1}}), .col22({32{1'b1}}), .col23({32{1'b1}}), .col24({32{1'b1}}),
    .col25({32{1'b1}}), .col26({32{1'b1}}), .col27({32{1'b1}}), .col28({32{1'b1}}), .col29({32{1'b1}}),
    .col30({32{1'b1}}), .col31({32{1'b1}}));
  DotMatrix #(.matrixcols(32), .matrixrows(32)) dotmatrix_98 (
    .col0({32{1'b1}}), .col1({32{1'b1}}), .col2({32{1'b1}}), .col3({32{1'b1}}), .col4({32{1'b1}}),
    .col5({32{1'b1}}), .col6({32{1'b1}}), .col7({32{1'b1}}), .col8({32{1'b1}}), .col9({32{1'b1}}),
    .col10({32{1'b1}}), .col11({32{1'b1}}), .col12({32{1'b1}}), .col13({32{1'b1}}), .col14({32{1'b1}}),
    .col15({32{1'b1}}), .col16({32{1'b1}}), .col17({32{1'b1}}), .col18({32{1'b1}}), .col19({32{1'b1}}),
    .col20({32{1'b1}}), .col21({32{1'b1}}), .col22({32{1'b1}}), .col23({32{1'b1}}), .col24({32{1'b1}}),
    .col25({32{1'b1}}), .col26({32{1'b1}}), .col27({32{1'b1}}), .col28({32{1'b1}}), .col29({32{1'b1}}),
    .col30({32{1'b1}}), .col31({32{1'b1}}));
  DotMatrix #(.matrixcols(32), .matrixrows(32)) dotmatrix_99 (
    .col0(pipes_73_out_5), .col1(pipes_73_out_6), .col2(pipes_73_out_7), .col3(pipes_73_out_8),
    .col4(pipes_73_out_9), .col5(pipes_73_out_10), .col6(pipes_73_out_11), .col7(pipes_73_out_12),
    .col8(pipes_73_out_13), .col9(pipes_73_out_14), .col10(pipes_73_out_15), .col11(pipes_73_out_16),
    .col12(pipes_73_out_17), .col13(pipes_73_out_18), .col14(pipes_73_out_19), .col15(pipes_73_out_20),
    .col16(pipes_73_out_21), .col17(pipes_73_out_22), .col18(pipes_73_out_23), .col19(pipes_73_out_24),
    .col20(pipes_73_out_25), .col21(pipes_73_out_26), .col22(pipes_73_out_27), .col23(pipes_73_out_28),
    .col24(pipes_73_out_29), .col25(pipes_73_out_30), .col26(pipes_73_out_31), .col27(pipes_73_out_32),
    .col28(pipes_73_out_33), .col29(pipes_73_out_34), .col30(pipes_73_out_35), .col31(pipes_73_out_36));
  pipes pipes_73 (
    .out_5(pipes_73_out_5), .out_6(pipes_73_out_6), .out_7(pipes_73_out_7), .out_8(pipes_73_out_8),
    .out_9(pipes_73_out_9), .out_10(pipes_73_out_10), .out_11(pipes_73_out_11), .out_12(pipes_73_out_12),
    .out_13(pipes_73_out_13), .out_14(pipes_73_out_14), .out_15(pipes_73_out_15), .out_16(pipes_73_out_16),
    .out_17(pipes_73_out_17), .out_18(pipes_73_out_18), .out_19(pipes_73_out_19), .out_20(pipes_73_out_20),
    .out_21(pipes_73_out_21), .out_22(pipes_73_out_22), .out_23(pipes_73_out_23), .out_24(pipes_73_out_24),
    .out_25(pipes_73_out_25), .out_26(pipes_73_out_26), .out_27(pipes_73_out_27), .out_28(pipes_73_out_28),
    .out_29(pipes_73_out_29), .out_30(pipes_73_out_30), .out_31(pipes_73_out_31), .out_32(pipes_73_out_32),
    .out_33(pipes_73_out_33), .out_34(pipes_73_out_34), .out_35(pipes_73_out_35), .out_36(pipes_73_out_36),
    .pipe(height_2_pipe), .pipe_2(pipes_73_pipe_2), .signal(height_2_signal), .signal_2(pipes_73_signal_2),
    .bird_1(height_2_bird_1), .bird_1_2(pipes_73_bird_1_2), .bird_2(height_2_bird_2), .bird(pipes_73_bird));
  pipes pipes_74 (
    .out_5(pipes_74_out_5), .out_6(pipes_74_out_6), .out_7(pipes_74_out_7), .out_8(pipes_74_out_8),
    .out_9(pipes_74_out_9), .out_10(pipes_74_out_10), .out_11(pipes_74_out_11), .out_12(pipes_74_out_12),
    .out_13(pipes_74_out_13), .out_14(pipes_74_out_14), .out_15(pipes_74_out_15), .out_16(pipes_74_out_16),
    .out_17(pipes_74_out_17), .out_18(pipes_74_out_18), .out_19(pipes_74_out_19), .out_20(pipes_74_out_20),
    .out_21(pipes_74_out_21), .out_22(pipes_74_out_22), .out_23(pipes_74_out_23), .out_24(pipes_74_out_24),
    .out_25(pipes_74_out_25), .out_26(pipes_74_out_26), .out_27(pipes_74_out_27), .out_28(pipes_74_out_28),
    .out_29(pipes_74_out_29), .out_30(pipes_74_out_30), .out_31(pipes_74_out_31), .out_32(pipes_74_out_32),
    .out_33(pipes_74_out_33), .out_34(pipes_74_out_34), .out_35(pipes_74_out_35), .out_36(pipes_74_out_36),
    .pipe(height_3_pipe), .pipe_2(pipes_74_pipe_2), .signal(height_3_signal), .signal_2(pipes_74_signal_2),
    .bird_1(height_3_bird_1), .bird_1_2(pipes_74_bird_1_2), .bird_2(height_3_bird_2), .bird(pipes_74_bird));
  DotMatrix #(.matrixcols(32), .matrixrows(32)) dotmatrix_100 (
    .col0(pipes_74_out_5), .col1(pipes_74_out_6), .col2(pipes_74_out_7), .col3(pipes_74_out_8),
    .col4(pipes_74_out_9), .col5(pipes_74_out_10), .col6(pipes_74_out_11), .col7(pipes_74_out_12),
    .col8(pipes_74_out_13), .col9(pipes_74_out_14), .col10(pipes_74_out_15), .col11(pipes_74_out_16),
    .col12(pipes_74_out_17), .col13(pipes_74_out_18), .col14(pipes_74_out_19), .col15(pipes_74_out_20),
    .col16(pipes_74_out_21), .col17(pipes_74_out_22), .col18(pipes_74_out_23), .col19(pipes_74_out_24),
    .col20(pipes_74_out_25), .col21(pipes_74_out_26), .col22(pipes_74_out_27), .col23(pipes_74_out_28),
    .col24(pipes_74_out_29), .col25(pipes_74_out_30), .col26(pipes_74_out_31), .col27(pipes_74_out_32),
    .col28(pipes_74_out_33), .col29(pipes_74_out_34), .col30(pipes_74_out_35), .col31(pipes_74_out_36));
  pipes pipes_75 (
    .out_5(pipes_75_out_5), .out_6(pipes_75_out_6), .out_7(pipes_75_out_7), .out_8(pipes_75_out_8),
    .out_9(pipes_75_out_9), .out_10(pipes_75_out_10), .out_11(pipes_75_out_11), .out_12(pipes_75_out_12),
    .out_13(pipes_75_out_13), .out_14(pipes_75_out_14), .out_15(pipes_75_out_15), .out_16(pipes_75_out_16),
    .out_17(pipes_75_out_17), .out_18(pipes_75_out_18), .out_19(pipes_75_out_19), .out_20(pipes_75_out_20),
    .out_21(pipes_75_out_21), .out_22(pipes_75_out_22), .out_23(pipes_75_out_23), .out_24(pipes_75_out_24),
    .out_25(pipes_75_out_25), .out_26(pipes_75_out_26), .out_27(pipes_75_out_27), .out_28(pipes_75_out_28),
    .out_29(pipes_75_out_29), .out_30(pipes_75_out_30), .out_31(pipes_75_out_31), .out_32(pipes_75_out_32),
    .out_33(pipes_75_out_33), .out_34(pipes_75_out_34), .out_35(pipes_75_out_35), .out_36(pipes_75_out_36),
    .pipe(height_4_pipe), .pipe_2(pipes_75_pipe_2), .signal(height_4_signal), .signal_2(pipes_75_signal_2),
    .bird_1(height_4_bird_1), .bird_1_2(pipes_75_bird_1_2), .bird_2(height_4_bird_2), .bird(pipes_75_bird));
  DotMatrix #(.matrixcols(32), .matrixrows(32)) dotmatrix_101 (
    .col0(pipes_75_out_5), .col1(pipes_75_out_6), .col2(pipes_75_out_7), .col3(pipes_75_out_8),
    .col4(pipes_75_out_9), .col5(pipes_75_out_10), .col6(pipes_75_out_11), .col7(pipes_75_out_12),
    .col8(pipes_75_out_13), .col9(pipes_75_out_14), .col10(pipes_75_out_15), .col11(pipes_75_out_16),
    .col12(pipes_75_out_17), .col13(pipes_75_out_18), .col14(pipes_75_out_19), .col15(pipes_75_out_20),
    .col16(pipes_75_out_21), .col17(pipes_75_out_22), .col18(pipes_75_out_23), .col19(pipes_75_out_24),
    .col20(pipes_75_out_25), .col21(pipes_75_out_26), .col22(pipes_75_out_27), .col23(pipes_75_out_28),
    .col24(pipes_75_out_29), .col25(pipes_75_out_30), .col26(pipes_75_out_31), .col27(pipes_75_out_32),
    .col28(pipes_75_out_33), .col29(pipes_75_out_34), .col30(pipes_75_out_35), .col31(pipes_75_out_36));
  pipes pipes_76 (
    .out_5(pipes_76_out_5), .out_6(pipes_76_out_6), .out_7(pipes_76_out_7), .out_8(pipes_76_out_8),
    .out_9(pipes_76_out_9), .out_10(pipes_76_out_10), .out_11(pipes_76_out_11), .out_12(pipes_76_out_12),
    .out_13(pipes_76_out_13), .out_14(pipes_76_out_14), .out_15(pipes_76_out_15), .out_16(pipes_76_out_16),
    .out_17(pipes_76_out_17), .out_18(pipes_76_out_18), .out_19(pipes_76_out_19), .out_20(pipes_76_out_20),
    .out_21(pipes_76_out_21), .out_22(pipes_76_out_22), .out_23(pipes_76_out_23), .out_24(pipes_76_out_24),
    .out_25(pipes_76_out_25), .out_26(pipes_76_out_26), .out_27(pipes_76_out_27), .out_28(pipes_76_out_28),
    .out_29(pipes_76_out_29), .out_30(pipes_76_out_30), .out_31(pipes_76_out_31), .out_32(pipes_76_out_32),
    .out_33(pipes_76_out_33), .out_34(pipes_76_out_34), .out_35(pipes_76_out_35), .out_36(pipes_76_out_36),
    .pipe(height_5_pipe), .pipe_2(pipes_76_pipe_2), .signal(height_5_signal), .signal_2(pipes_76_signal_2),
    .bird_1(height_5_bird_1), .bird_1_2(pipes_76_bird_1_2), .bird_2(height_5_bird_2), .bird(pipes_76_bird));
  DotMatrix #(.matrixcols(32), .matrixrows(32)) dotmatrix_102 (
    .col0(pipes_76_out_5), .col1(pipes_76_out_6), .col2(pipes_76_out_7), .col3(pipes_76_out_8),
    .col4(pipes_76_out_9), .col5(pipes_76_out_10), .col6(pipes_76_out_11), .col7(pipes_76_out_12),
    .col8(pipes_76_out_13), .col9(pipes_76_out_14), .col10(pipes_76_out_15), .col11(pipes_76_out_16),
    .col12(pipes_76_out_17), .col13(pipes_76_out_18), .col14(pipes_76_out_19), .col15(pipes_76_out_20),
    .col16(pipes_76_out_21), .col17(pipes_76_out_22), .col18(pipes_76_out_23), .col19(pipes_76_out_24),
    .col20(pipes_76_out_25), .col21(pipes_76_out_26), .col22(pipes_76_out_27), .col23(pipes_76_out_28),
    .col24(pipes_76_out_29), .col25(pipes_76_out_30), .col26(pipes_76_out_31), .col27(pipes_76_out_32),
    .col28(pipes_76_out_33), .col29(pipes_76_out_34), .col30(pipes_76_out_35), .col31(pipes_76_out_36));
  pipes pipes_77 (
    .out_5(pipes_77_out_5), .out_6(pipes_77_out_6), .out_7(pipes_77_out_7), .out_8(pipes_77_out_8),
    .out_9(pipes_77_out_9), .out_10(pipes_77_out_10), .out_11(pipes_77_out_11), .out_12(pipes_77_out_12),
    .out_13(pipes_77_out_13), .out_14(pipes_77_out_14), .out_15(pipes_77_out_15), .out_16(pipes_77_out_16),
    .out_17(pipes_77_out_17), .out_18(pipes_77_out_18), .out_19(pipes_77_out_19), .out_20(pipes_77_out_20),
    .out_21(pipes_77_out_21), .out_22(pipes_77_out_22), .out_23(pipes_77_out_23), .out_24(pipes_77_out_24),
    .out_25(pipes_77_out_25), .out_26(pipes_77_out_26), .out_27(pipes_77_out_27), .out_28(pipes_77_out_28),
    .out_29(pipes_77_out_29), .out_30(pipes_77_out_30), .out_31(pipes_77_out_31), .out_32(pipes_77_out_32),
    .out_33(pipes_77_out_33), .out_34(pipes_77_out_34), .out_35(pipes_77_out_35), .out_36(pipes_77_out_36),
    .pipe(height_6_pipe), .pipe_2(pipes_77_pipe_2), .signal(height_6_signal), .signal_2(pipes_77_signal_2),
    .bird_1(height_6_bird_1), .bird_1_2(pipes_77_bird_1_2), .bird_2(height_6_bird_2), .bird(pipes_77_bird));
  DotMatrix #(.matrixcols(32), .matrixrows(32)) dotmatrix_103 (
    .col0(pipes_77_out_5), .col1(pipes_77_out_6), .col2(pipes_77_out_7), .col3(pipes_77_out_8),
    .col4(pipes_77_out_9), .col5(pipes_77_out_10), .col6(pipes_77_out_11), .col7(pipes_77_out_12),
    .col8(pipes_77_out_13), .col9(pipes_77_out_14), .col10(pipes_77_out_15), .col11(pipes_77_out_16),
    .col12(pipes_77_out_17), .col13(pipes_77_out_18), .col14(pipes_77_out_19), .col15(pipes_77_out_20),
    .col16(pipes_77_out_21), .col17(pipes_77_out_22), .col18(pipes_77_out_23), .col19(pipes_77_out_24),
    .col20(pipes_77_out_25), .col21(pipes_77_out_26), .col22(pipes_77_out_27), .col23(pipes_77_out_28),
    .col24(pipes_77_out_29), .col25(pipes_77_out_30), .col26(pipes_77_out_31), .col27(pipes_77_out_32),
    .col28(pipes_77_out_33), .col29(pipes_77_out_34), .col30(pipes_77_out_35), .col31(pipes_77_out_36));
  pipes pipes_78 (
    .out_5(pipes_78_out_5), .out_6(pipes_78_out_6), .out_7(pipes_78_out_7), .out_8(pipes_78_out_8),
    .out_9(pipes_78_out_9), .out_10(pipes_78_out_10), .out_11(pipes_78_out_11), .out_12(pipes_78_out_12),
    .out_13(pipes_78_out_13), .out_14(pipes_78_out_14), .out_15(pipes_78_out_15), .out_16(pipes_78_out_16),
    .out_17(pipes_78_out_17), .out_18(pipes_78_out_18), .out_19(pipes_78_out_19), .out_20(pipes_78_out_20),
    .out_21(pipes_78_out_21), .out_22(pipes_78_out_22), .out_23(pipes_78_out_23), .out_24(pipes_78_out_24),
    .out_25(pipes_78_out_25), .out_26(pipes_78_out_26), .out_27(pipes_78_out_27), .out_28(pipes_78_out_28),
    .out_29(pipes_78_out_29), .out_30(pipes_78_out_30), .out_31(pipes_78_out_31), .out_32(pipes_78_out_32),
    .out_33(pipes_78_out_33), .out_34(pipes_78_out_34), .out_35(pipes_78_out_35), .out_36(pipes_78_out_36),
    .pipe(height_7_pipe), .pipe_2(pipes_78_pipe_2), .signal(height_7_signal), .signal_2(pipes_78_signal_2),
    .bird_1(height_7_bird_1), .bird_1_2(pipes_78_bird_1_2), .bird_2(height_7_bird_2), .bird(pipes_78_bird));
  DotMatrix #(.matrixcols(32), .matrixrows(32)) dotmatrix_104 (
    .col0(pipes_78_out_5), .col1(pipes_78_out_6), .col2(pipes_78_out_7), .col3(pipes_78_out_8),
    .col4(pipes_78_out_9), .col5(pipes_78_out_10), .col6(pipes_78_out_11), .col7(pipes_78_out_12),
    .col8(pipes_78_out_13), .col9(pipes_78_out_14), .col10(pipes_78_out_15), .col11(pipes_78_out_16),
    .col12(pipes_78_out_17), .col13(pipes_78_out_18), .col14(pipes_78_out_19), .col15(pipes_78_out_20),
    .col16(pipes_78_out_21), .col17(pipes_78_out_22), .col18(pipes_78_out_23), .col19(pipes_78_out_24),
    .col20(pipes_78_out_25), .col21(pipes_78_out_26), .col22(pipes_78_out_27), .col23(pipes_78_out_28),
    .col24(pipes_78_out_29), .col25(pipes_78_out_30), .col26(pipes_78_out_31), .col27(pipes_78_out_32),
    .col28(pipes_78_out_33), .col29(pipes_78_out_34), .col30(pipes_78_out_35), .col31(pipes_78_out_36));
  pipes pipes_79 (
    .out_5(pipes_79_out_5), .out_6(pipes_79_out_6), .out_7(pipes_79_out_7), .out_8(pipes_79_out_8),
    .out_9(pipes_79_out_9), .out_10(pipes_79_out_10), .out_11(pipes_79_out_11), .out_12(pipes_79_out_12),
    .out_13(pipes_79_out_13), .out_14(pipes_79_out_14), .out_15(pipes_79_out_15), .out_16(pipes_79_out_16),
    .out_17(pipes_79_out_17), .out_18(pipes_79_out_18), .out_19(pipes_79_out_19), .out_20(pipes_79_out_20),
    .out_21(pipes_79_out_21), .out_22(pipes_79_out_22), .out_23(pipes_79_out_23), .out_24(pipes_79_out_24),
    .out_25(pipes_79_out_25), .out_26(pipes_79_out_26), .out_27(pipes_79_out_27), .out_28(pipes_79_out_28),
    .out_29(pipes_79_out_29), .out_30(pipes_79_out_30), .out_31(pipes_79_out_31), .out_32(pipes_79_out_32),
    .out_33(pipes_79_out_33), .out_34(pipes_79_out_34), .out_35(pipes_79_out_35), .out_36(pipes_79_out_36),
    .pipe(height_8_pipe), .pipe_2(pipes_79_pipe_2), .signal(height_8_signal), .signal_2(pipes_79_signal_2),
    .bird_1(height_8_bird_1), .bird_1_2(pipes_79_bird_1_2), .bird_2(height_8_bird_2), .bird(pipes_79_bird));
  DotMatrix #(.matrixcols(32), .matrixrows(32)) dotmatrix_105 (
    .col0(pipes_79_out_5), .col1(pipes_79_out_6), .col2(pipes_79_out_7), .col3(pipes_79_out_8),
    .col4(pipes_79_out_9), .col5(pipes_79_out_10), .col6(pipes_79_out_11), .col7(pipes_79_out_12),
    .col8(pipes_79_out_13), .col9(pipes_79_out_14), .col10(pipes_79_out_15), .col11(pipes_79_out_16),
    .col12(pipes_79_out_17), .col13(pipes_79_out_18), .col14(pipes_79_out_19), .col15(pipes_79_out_20),
    .col16(pipes_79_out_21), .col17(pipes_79_out_22), .col18(pipes_79_out_23), .col19(pipes_79_out_24),
    .col20(pipes_79_out_25), .col21(pipes_79_out_26), .col22(pipes_79_out_27), .col23(pipes_79_out_28),
    .col24(pipes_79_out_29), .col25(pipes_79_out_30), .col26(pipes_79_out_31), .col27(pipes_79_out_32),
    .col28(pipes_79_out_33), .col29(pipes_79_out_34), .col30(pipes_79_out_35), .col31(pipes_79_out_36));
  pipes pipes_80 (
    .out_5(pipes_80_out_5), .out_6(pipes_80_out_6), .out_7(pipes_80_out_7), .out_8(pipes_80_out_8),
    .out_9(pipes_80_out_9), .out_10(pipes_80_out_10), .out_11(pipes_80_out_11), .out_12(pipes_80_out_12),
    .out_13(pipes_80_out_13), .out_14(pipes_80_out_14), .out_15(pipes_80_out_15), .out_16(pipes_80_out_16),
    .out_17(pipes_80_out_17), .out_18(pipes_80_out_18), .out_19(pipes_80_out_19), .out_20(pipes_80_out_20),
    .out_21(pipes_80_out_21), .out_22(pipes_80_out_22), .out_23(pipes_80_out_23), .out_24(pipes_80_out_24),
    .out_25(pipes_80_out_25), .out_26(pipes_80_out_26), .out_27(pipes_80_out_27), .out_28(pipes_80_out_28),
    .out_29(pipes_80_out_29), .out_30(pipes_80_out_30), .out_31(pipes_80_out_31), .out_32(pipes_80_out_32),
    .out_33(pipes_80_out_33), .out_34(pipes_80_out_34), .out_35(pipes_80_out_35), .out_36(pipes_80_out_36),
    .pipe(height_9_pipe), .pipe_2(pipes_80_pipe_2), .signal(height_9_signal), .signal_2(pipes_80_signal_2),
    .bird_1(height_9_bird_1), .bird_1_2(pipes_80_bird_1_2), .bird_2(height_9_bird_2), .bird(pipes_80_bird));
  DotMatrix #(.matrixcols(32), .matrixrows(32)) dotmatrix_106 (
    .col0(pipes_80_out_5), .col1(pipes_80_out_6), .col2(pipes_80_out_7), .col3(pipes_80_out_8),
    .col4(pipes_80_out_9), .col5(pipes_80_out_10), .col6(pipes_80_out_11), .col7(pipes_80_out_12),
    .col8(pipes_80_out_13), .col9(pipes_80_out_14), .col10(pipes_80_out_15), .col11(pipes_80_out_16),
    .col12(pipes_80_out_17), .col13(pipes_80_out_18), .col14(pipes_80_out_19), .col15(pipes_80_out_20),
    .col16(pipes_80_out_21), .col17(pipes_80_out_22), .col18(pipes_80_out_23), .col19(pipes_80_out_24),
    .col20(pipes_80_out_25), .col21(pipes_80_out_26), .col22(pipes_80_out_27), .col23(pipes_80_out_28),
    .col24(pipes_80_out_29), .col25(pipes_80_out_30), .col26(pipes_80_out_31), .col27(pipes_80_out_32),
    .col28(pipes_80_out_33), .col29(pipes_80_out_34), .col30(pipes_80_out_35), .col31(pipes_80_out_36));
  pipes pipes_81 (
    .out_5(pipes_81_out_5), .out_6(pipes_81_out_6), .out_7(pipes_81_out_7), .out_8(pipes_81_out_8),
    .out_9(pipes_81_out_9), .out_10(pipes_81_out_10), .out_11(pipes_81_out_11), .out_12(pipes_81_out_12),
    .out_13(pipes_81_out_13), .out_14(pipes_81_out_14), .out_15(pipes_81_out_15), .out_16(pipes_81_out_16),
    .out_17(pipes_81_out_17), .out_18(pipes_81_out_18), .out_19(pipes_81_out_19), .out_20(pipes_81_out_20),
    .out_21(pipes_81_out_21), .out_22(pipes_81_out_22), .out_23(pipes_81_out_23), .out_24(pipes_81_out_24),
    .out_25(pipes_81_out_25), .out_26(pipes_81_out_26), .out_27(pipes_81_out_27), .out_28(pipes_81_out_28),
    .out_29(pipes_81_out_29), .out_30(pipes_81_out_30), .out_31(pipes_81_out_31), .out_32(pipes_81_out_32),
    .out_33(pipes_81_out_33), .out_34(pipes_81_out_34), .out_35(pipes_81_out_35), .out_36(pipes_81_out_36),
    .pipe(height_10_pipe), .pipe_2(pipes_81_pipe_2), .signal(height_10_signal), .signal_2(pipes_81_signal_2),
    .bird_1(height_10_bird_1), .bird_1_2(pipes_81_bird_1_2), .bird_2(height_10_bird_2), .bird(pipes_81_bird));
  DotMatrix #(.matrixcols(32), .matrixrows(32)) dotmatrix_107 (
    .col0(pipes_81_out_5), .col1(pipes_81_out_6), .col2(pipes_81_out_7), .col3(pipes_81_out_8),
    .col4(pipes_81_out_9), .col5(pipes_81_out_10), .col6(pipes_81_out_11), .col7(pipes_81_out_12),
    .col8(pipes_81_out_13), .col9(pipes_81_out_14), .col10(pipes_81_out_15), .col11(pipes_81_out_16),
    .col12(pipes_81_out_17), .col13(pipes_81_out_18), .col14(pipes_81_out_19), .col15(pipes_81_out_20),
    .col16(pipes_81_out_21), .col17(pipes_81_out_22), .col18(pipes_81_out_23), .col19(pipes_81_out_24),
    .col20(pipes_81_out_25), .col21(pipes_81_out_26), .col22(pipes_81_out_27), .col23(pipes_81_out_28),
    .col24(pipes_81_out_29), .col25(pipes_81_out_30), .col26(pipes_81_out_31), .col27(pipes_81_out_32),
    .col28(pipes_81_out_33), .col29(pipes_81_out_34), .col30(pipes_81_out_35), .col31(pipes_81_out_36));
  DotMatrix #(.matrixcols(32), .matrixrows(32)) dotmatrix_108 (
    .col0(pipes_82_out_5), .col1(pipes_82_out_6), .col2(pipes_82_out_7), .col3(pipes_82_out_8),
    .col4(pipes_82_out_9), .col5(pipes_82_out_10), .col6(pipes_82_out_11), .col7(pipes_82_out_12),
    .col8(pipes_82_out_13), .col9(pipes_82_out_14), .col10(pipes_82_out_15), .col11(pipes_82_out_16),
    .col12(pipes_82_out_17), .col13(pipes_82_out_18), .col14(pipes_82_out_19), .col15(pipes_82_out_20),
    .col16(pipes_82_out_21), .col17(pipes_82_out_22), .col18(pipes_82_out_23), .col19(pipes_82_out_24),
    .col20(pipes_82_out_25), .col21(pipes_82_out_26), .col22(pipes_82_out_27), .col23(pipes_82_out_28),
    .col24(pipes_82_out_29), .col25(pipes_82_out_30), .col26(pipes_82_out_31), .col27(pipes_82_out_32),
    .col28(pipes_82_out_33), .col29(pipes_82_out_34), .col30(pipes_82_out_35), .col31(pipes_82_out_36));
  pipes pipes_82 (
    .out_5(pipes_82_out_5), .out_6(pipes_82_out_6), .out_7(pipes_82_out_7), .out_8(pipes_82_out_8),
    .out_9(pipes_82_out_9), .out_10(pipes_82_out_10), .out_11(pipes_82_out_11), .out_12(pipes_82_out_12),
    .out_13(pipes_82_out_13), .out_14(pipes_82_out_14), .out_15(pipes_82_out_15), .out_16(pipes_82_out_16),
    .out_17(pipes_82_out_17), .out_18(pipes_82_out_18), .out_19(pipes_82_out_19), .out_20(pipes_82_out_20),
    .out_21(pipes_82_out_21), .out_22(pipes_82_out_22), .out_23(pipes_82_out_23), .out_24(pipes_82_out_24),
    .out_25(pipes_82_out_25), .out_26(pipes_82_out_26), .out_27(pipes_82_out_27), .out_28(pipes_82_out_28),
    .out_29(pipes_82_out_29), .out_30(pipes_82_out_30), .out_31(pipes_82_out_31), .out_32(pipes_82_out_32),
    .out_33(pipes_82_out_33), .out_34(pipes_82_out_34), .out_35(pipes_82_out_35), .out_36(pipes_82_out_36),
    .pipe(height_11_pipe), .pipe_2(pipes_82_pipe_2), .signal(height_11_signal), .signal_2(pipes_82_signal_2),
    .bird_1(height_11_bird_1), .bird_1_2(pipes_82_bird_1_2), .bird_2(height_11_bird_2), .bird(pipes_82_bird));
  pipes pipes_83 (
    .out_5(pipes_83_out_5), .out_6(pipes_83_out_6), .out_7(pipes_83_out_7), .out_8(pipes_83_out_8),
    .out_9(pipes_83_out_9), .out_10(pipes_83_out_10), .out_11(pipes_83_out_11), .out_12(pipes_83_out_12),
    .out_13(pipes_83_out_13), .out_14(pipes_83_out_14), .out_15(pipes_83_out_15), .out_16(pipes_83_out_16),
    .out_17(pipes_83_out_17), .out_18(pipes_83_out_18), .out_19(pipes_83_out_19), .out_20(pipes_83_out_20),
    .out_21(pipes_83_out_21), .out_22(pipes_83_out_22), .out_23(pipes_83_out_23), .out_24(pipes_83_out_24),
    .out_25(pipes_83_out_25), .out_26(pipes_83_out_26), .out_27(pipes_83_out_27), .out_28(pipes_83_out_28),
    .out_29(pipes_83_out_29), .out_30(pipes_83_out_30), .out_31(pipes_83_out_31), .out_32(pipes_83_out_32),
    .out_33(pipes_83_out_33), .out_34(pipes_83_out_34), .out_35(pipes_83_out_35), .out_36(pipes_83_out_36),
    .pipe(height_12_pipe), .pipe_2(pipes_83_pipe_2), .signal(height_12_signal), .signal_2(pipes_83_signal_2),
    .bird_1(height_12_bird_1), .bird_1_2(pipes_83_bird_1_2), .bird_2(height_12_bird_2), .bird(pipes_83_bird));
  DotMatrix #(.matrixcols(32), .matrixrows(32)) dotmatrix_109 (
    .col0(pipes_83_out_5), .col1(pipes_83_out_6), .col2(pipes_83_out_7), .col3(pipes_83_out_8),
    .col4(pipes_83_out_9), .col5(pipes_83_out_10), .col6(pipes_83_out_11), .col7(pipes_83_out_12),
    .col8(pipes_83_out_13), .col9(pipes_83_out_14), .col10(pipes_83_out_15), .col11(pipes_83_out_16),
    .col12(pipes_83_out_17), .col13(pipes_83_out_18), .col14(pipes_83_out_19), .col15(pipes_83_out_20),
    .col16(pipes_83_out_21), .col17(pipes_83_out_22), .col18(pipes_83_out_23), .col19(pipes_83_out_24),
    .col20(pipes_83_out_25), .col21(pipes_83_out_26), .col22(pipes_83_out_27), .col23(pipes_83_out_28),
    .col24(pipes_83_out_29), .col25(pipes_83_out_30), .col26(pipes_83_out_31), .col27(pipes_83_out_32),
    .col28(pipes_83_out_33), .col29(pipes_83_out_34), .col30(pipes_83_out_35), .col31(pipes_83_out_36));
  DotMatrix #(.matrixcols(32), .matrixrows(32)) dotmatrix_110 (
    .col0(pipes_84_out_5), .col1(pipes_84_out_6), .col2(pipes_84_out_7), .col3(pipes_84_out_8),
    .col4(pipes_84_out_9), .col5(pipes_84_out_10), .col6(pipes_84_out_11), .col7(pipes_84_out_12),
    .col8(pipes_84_out_13), .col9(pipes_84_out_14), .col10(pipes_84_out_15), .col11(pipes_84_out_16),
    .col12(pipes_84_out_17), .col13(pipes_84_out_18), .col14(pipes_84_out_19), .col15(pipes_84_out_20),
    .col16(pipes_84_out_21), .col17(pipes_84_out_22), .col18(pipes_84_out_23), .col19(pipes_84_out_24),
    .col20(pipes_84_out_25), .col21(pipes_84_out_26), .col22(pipes_84_out_27), .col23(pipes_84_out_28),
    .col24(pipes_84_out_29), .col25(pipes_84_out_30), .col26(pipes_84_out_31), .col27(pipes_84_out_32),
    .col28(pipes_84_out_33), .col29(pipes_84_out_34), .col30(pipes_84_out_35), .col31(pipes_84_out_36));
  pipes pipes_84 (
    .out_5(pipes_84_out_5), .out_6(pipes_84_out_6), .out_7(pipes_84_out_7), .out_8(pipes_84_out_8),
    .out_9(pipes_84_out_9), .out_10(pipes_84_out_10), .out_11(pipes_84_out_11), .out_12(pipes_84_out_12),
    .out_13(pipes_84_out_13), .out_14(pipes_84_out_14), .out_15(pipes_84_out_15), .out_16(pipes_84_out_16),
    .out_17(pipes_84_out_17), .out_18(pipes_84_out_18), .out_19(pipes_84_out_19), .out_20(pipes_84_out_20),
    .out_21(pipes_84_out_21), .out_22(pipes_84_out_22), .out_23(pipes_84_out_23), .out_24(pipes_84_out_24),
    .out_25(pipes_84_out_25), .out_26(pipes_84_out_26), .out_27(pipes_84_out_27), .out_28(pipes_84_out_28),
    .out_29(pipes_84_out_29), .out_30(pipes_84_out_30), .out_31(pipes_84_out_31), .out_32(pipes_84_out_32),
    .out_33(pipes_84_out_33), .out_34(pipes_84_out_34), .out_35(pipes_84_out_35), .out_36(pipes_84_out_36),
    .pipe(height_13_pipe), .pipe_2(pipes_84_pipe_2), .signal(height_13_signal), .signal_2(pipes_84_signal_2),
    .bird_1(height_13_bird_1), .bird_1_2(pipes_84_bird_1_2), .bird_2(height_13_bird_2), .bird(pipes_84_bird));
  DotMatrix #(.matrixcols(32), .matrixrows(32)) dotmatrix_111 (
    .col0({32{1'b1}}), .col1({32{1'b1}}), .col2({32{1'b1}}), .col3({32{1'b1}}), .col4({32{1'b1}}),
    .col5({32{1'b1}}), .col6({32{1'b1}}), .col7({32{1'b1}}), .col8({32{1'b1}}), .col9({32{1'b1}}),
    .col10({32{1'b1}}), .col11({32{1'b1}}), .col12({32{1'b1}}), .col13({32{1'b1}}), .col14({32{1'b1}}),
    .col15({32{1'b1}}), .col16({32{1'b1}}), .col17({32{1'b1}}), .col18({32{1'b1}}), .col19({32{1'b1}}),
    .col20({32{1'b1}}), .col21({32{1'b1}}), .col22({32{1'b1}}), .col23({32{1'b1}}), .col24({32{1'b1}}),
    .col25({32{1'b1}}), .col26({32{1'b1}}), .col27({32{1'b1}}), .col28({32{1'b1}}), .col29({32{1'b1}}),
    .col30({32{1'b1}}), .col31({32{1'b1}}));
  DotMatrix #(.matrixcols(32), .matrixrows(32)) dotmatrix_112 (
    .col0({32{1'b1}}), .col1({32{1'b1}}), .col2({32{1'b1}}), .col3({32{1'b1}}), .col4({32{1'b1}}),
    .col5({32{1'b1}}), .col6({32{1'b1}}), .col7({32{1'b1}}), .col8({32{1'b1}}), .col9({32{1'b1}}),
    .col10({32{1'b1}}), .col11({32{1'b1}}), .col12({32{1'b1}}), .col13({32{1'b1}}), .col14({32{1'b1}}),
    .col15({32{1'b1}}), .col16({32{1'b1}}), .col17({32{1'b1}}), .col18({32{1'b1}}), .col19({32{1'b1}}),
    .col20({32{1'b1}}), .col21({32{1'b1}}), .col22({32{1'b1}}), .col23({32{1'b1}}), .col24({32{1'b1}}),
    .col25({32{1'b1}}), .col26({32{1'b1}}), .col27({32{1'b1}}), .col28({32{1'b1}}), .col29({32{1'b1}}),
    .col30({32{1'b1}}), .col31({32{1'b1}}));
  height height_1 (
    .signal_up_2(s_up), .signal_down(height_2_signal_up_2), .signal_down_2(height_1_signal_down_2));  // open: pipe, pipe_signal, signal, bird_1, bird_2, signal_up
  height height_2 (
    .pipe(height_2_pipe), .pipe_signal(rand_1_rand_pipe), .signal(height_2_signal), .bird_1(height_2_bird_1),
    .signal_up_2(height_2_signal_up_2), .signal_down(height_3_signal_up_2), .bird_2(height_2_bird_2),
    .signal_up(height_1_signal_down_2), .signal_down_2(height_2_signal_down_2));
  height height_3 (
    .pipe(height_3_pipe), .pipe_signal(rand_1_rand_pipe), .signal(height_3_signal), .bird_1(height_3_bird_1),
    .signal_up_2(height_3_signal_up_2), .signal_down(height_4_signal_up_2), .bird_2(height_3_bird_2),
    .signal_up(height_2_signal_down_2), .signal_down_2(height_3_signal_down_2));
  height height_4 (
    .pipe(height_4_pipe), .pipe_signal(rand_1_rand_pipe), .signal(height_4_signal), .bird_1(height_4_bird_1),
    .signal_up_2(height_4_signal_up_2), .signal_down(height_5_signal_up_2), .bird_2(height_4_bird_2),
    .signal_up(height_3_signal_down_2), .signal_down_2(height_4_signal_down_2));
  height height_5 (
    .pipe(height_5_pipe), .pipe_signal(rand_1_rand_pipe), .signal(height_5_signal), .bird_1(height_5_bird_1),
    .signal_up_2(height_5_signal_up_2), .signal_down(height_6_signal_up_2), .bird_2(height_5_bird_2),
    .signal_up(height_4_signal_down_2), .signal_down_2(height_5_signal_down_2));
  height height_6 (
    .pipe(height_6_pipe), .pipe_signal(rand_1_rand_pipe), .signal(height_6_signal), .bird_1(height_6_bird_1),
    .signal_up_2(height_6_signal_up_2), .signal_down(height_7_signal_up_2), .bird_2(height_6_bird_2),
    .signal_up(height_5_signal_down_2), .signal_down_2(height_6_signal_down_2));
  height height_7 (
    .pipe(height_7_pipe), .pipe_signal(rand_1_rand_pipe), .signal(height_7_signal), .bird_1(height_7_bird_1),
    .signal_up_2(height_7_signal_up_2), .signal_down(height_8_signal_up_2), .bird_2(height_7_bird_2),
    .signal_up(height_6_signal_down_2), .signal_down_2(height_7_signal_down_2));
  height height_8 (
    .pipe(height_8_pipe), .pipe_signal(rand_1_rand_pipe), .signal(height_8_signal), .bird_1(height_8_bird_1),
    .signal_up_2(height_8_signal_up_2), .signal_down(height_9_signal_up_2), .bird_2(height_8_bird_2),
    .signal_up(height_7_signal_down_2), .signal_down_2(height_8_signal_down_2));
  height height_9 (
    .pipe(height_9_pipe), .pipe_signal(rand_1_rand_pipe), .signal(height_9_signal), .bird_1(height_9_bird_1),
    .signal_up_2(height_9_signal_up_2), .signal_down(height_10_signal_up_2), .bird_2(height_9_bird_2),
    .signal_up(height_8_signal_down_2), .signal_down_2(height_9_signal_down_2));
  height height_10 (
    .pipe(height_10_pipe), .pipe_signal(rand_1_rand_pipe), .signal(height_10_signal),
    .bird_1(height_10_bird_1), .signal_up_2(height_10_signal_up_2), .signal_down(height_11_signal_up_2),
    .bird_2(height_10_bird_2), .signal_up(height_9_signal_down_2), .signal_down_2(height_10_signal_down_2));
  height height_11 (
    .pipe(height_11_pipe), .pipe_signal(rand_1_rand_pipe), .signal(height_11_signal),
    .bird_1(height_11_bird_1), .signal_up_2(height_11_signal_up_2), .signal_down(height_12_signal_up_2),
    .bird_2(height_11_bird_2), .signal_up(height_10_signal_down_2), .signal_down_2(height_11_signal_down_2));
  height height_12 (
    .pipe(height_12_pipe), .pipe_signal(rand_1_rand_pipe), .signal(height_12_signal),
    .bird_1(height_12_bird_1), .signal_up_2(height_12_signal_up_2), .signal_down(height_13_signal_up_2),
    .bird_2(height_12_bird_2), .signal_up(height_11_signal_down_2), .signal_down_2(height_12_signal_down_2));
  height height_13 (
    .pipe(height_13_pipe), .pipe_signal(rand_1_rand_pipe), .signal(height_13_signal),
    .bird_1(height_13_bird_1), .signal_up_2(height_13_signal_up_2), .signal_down(rand_1_signal),
    .bird_2(height_13_bird_2), .signal_up(height_12_signal_down_2));  // open: signal_down_2
  \rand  rand_1 (
    .tick(controlled_buffer_1_out), .rand_pipe(rand_1_rand_pipe), .button(button_1_out),
    .signal(rand_1_signal));  // open: clear
  assign controlled_buffer_1_out = \вкл  ? clock_1_out : 1'bz;  // Controlled_Buffer controlled_buffer_1
  Button button_1 (.out(button_1_out));
  // Probe on rand_1_rand_pipe
  Clock clock_1 (.out(clock_1_out));
  nor nor_1 (\вкл , s1[9], s2[9], s3[9], s4[9], s5[9], s6[9], s7[9], s8[9], s9[9], s10[9], s11[9], s12[9], s_up[4]);
  Pull_Resistor pull_resistor_1 (.node(s_up[4]));
  \индикаторы  \u_индикаторы_1  (
    .in_1(\вкл ), .in_2(plus_1[31]), .out_3(\индикаторы_1_out_3 ), .out_4(\индикаторы_1_out_4 ),
    .out_5(\индикаторы_1_out_5 ), .out_6(\индикаторы_1_out_6 ), .out_7(\индикаторы_1_out_7 ),
    .out_8(\индикаторы_1_out_8 ), .out_9(\индикаторы_1_out_9 ), .out_10(\индикаторы_1_out_10 ),
    .out_11(\индикаторы_1_out_11 ), .out_12(\индикаторы_1_out_12 ), .out_13(\индикаторы_1_out_13 ),
    .out_14(\индикаторы_1_out_14 ), .out_15(\индикаторы_1_out_15 ), .out_16(\индикаторы_1_out_16 ),
    .out_17(\индикаторы_1_out_17 ), .out_18(\индикаторы_1_out_18 ), .out_19(\индикаторы_1_out_19 ),
    .out_20(\индикаторы_1_out_20 ), .out_21(\индикаторы_1_out_21 ), .out_22(\индикаторы_1_out_22 ),
    .out_23(\индикаторы_1_out_23 ), .out_24(\индикаторы_1_out_24 ), .out_25(\индикаторы_1_out_25 ),
    .out_26(\индикаторы_1_out_26 ), .out_27(\индикаторы_1_out_27 ), .out_28(\индикаторы_1_out_28 ),
    .out_29(\индикаторы_1_out_29 ), .out_30(\индикаторы_1_out_30 ), .out_31(\индикаторы_1_out_31 ),
    .out_32(\индикаторы_1_out_32 ), .out_33(\индикаторы_1_out_33 ), .out_34(\индикаторы_1_out_34 ),
    .out_35(\индикаторы_1_out_35 ), .out_36(\индикаторы_1_out_36 ), .out_37(\индикаторы_1_out_37 ),
    .out_38(\индикаторы_1_out_38 ), .out_39(\индикаторы_1_out_39 ), .out_40(\индикаторы_1_out_40 ),
    .out_41(\индикаторы_1_out_41 ), .out_42(\индикаторы_1_out_42 ), .out_43(\индикаторы_1_out_43 ),
    .out_44(\индикаторы_1_out_44 ), .out_45(\индикаторы_1_out_45 ), .out_46(\индикаторы_1_out_46 ),
    .out_47(\индикаторы_1_out_47 ), .out_48(\индикаторы_1_out_48 ), .out_49(\индикаторы_1_out_49 ),
    .out_50(\индикаторы_1_out_50 ), .out_51(\индикаторы_1_out_51 ), .out_52(\индикаторы_1_out_52 ),
    .out_53(\индикаторы_1_out_53 ), .out_54(\индикаторы_1_out_54 ), .out_55(\индикаторы_1_out_55 ),
    .out_56(\индикаторы_1_out_56 ), .out_57(\индикаторы_1_out_57 ), .out_58(\индикаторы_1_out_58 ),
    .out_59(\индикаторы_1_out_59 ), .out_60(\индикаторы_1_out_60 ), .out_61(\индикаторы_1_out_61 ),
    .out_62(\индикаторы_1_out_62 ), .out_63(\индикаторы_1_out_63 ), .out_64(\индикаторы_1_out_64 ),
    .out_65(\индикаторы_1_out_65 ), .out_66(\индикаторы_1_out_66 ), .out_67(\индикаторы_1_out_67 ),
    .out_68(\индикаторы_1_out_68 ), .out_69(\индикаторы_1_out_69 ), .out_70(\индикаторы_1_out_70 ),
    .out_71(\индикаторы_1_out_71 ), .out_72(\индикаторы_1_out_72 ), .out_73(\индикаторы_1_out_73 ),
    .out_74(\индикаторы_1_out_74 ), .out_75(\индикаторы_1_out_75 ), .out_76(\индикаторы_1_out_76 ),
    .out_77(\индикаторы_1_out_77 ), .out_78(\индикаторы_1_out_78 ), .out_79(\индикаторы_1_out_79 ),
    .out_80(\индикаторы_1_out_80 ), .out_81(\индикаторы_1_out_81 ), .out_82(\индикаторы_1_out_82 ),
    .out_83(\индикаторы_1_out_83 ), .out_84(\индикаторы_1_out_84 ), .out_85(\индикаторы_1_out_85 ),
    .out_86(\индикаторы_1_out_86 ), .out_87(\индикаторы_1_out_87 ), .out_88(\индикаторы_1_out_88 ),
    .out_89(\индикаторы_1_out_89 ), .out_90(\индикаторы_1_out_90 ), .out_91(\индикаторы_1_out_91 ),
    .out_92(\индикаторы_1_out_92 ), .out_93(\индикаторы_1_out_93 ), .out_94(\индикаторы_1_out_94 ),
    .out_95(\индикаторы_1_out_95 ), .out_96(\индикаторы_1_out_96 ), .out_97(\индикаторы_1_out_97 ),
    .out_98(\индикаторы_1_out_98 ), .out_99(\индикаторы_1_out_99 ), .out_100(\индикаторы_1_out_100 ),
    .out_101(\индикаторы_1_out_101 ), .out_102(\индикаторы_1_out_102 ), .out_103(\индикаторы_1_out_103 ),
    .out_104(\индикаторы_1_out_104 ), .out_105(\индикаторы_1_out_105 ), .out_106(\индикаторы_1_out_106 ),
    .out_107(\индикаторы_1_out_107 ), .out_108(\индикаторы_1_out_108 ), .out_109(\индикаторы_1_out_109 ),
    .out_110(\индикаторы_1_out_110 ), .out_111(\индикаторы_1_out_111 ), .out_112(\индикаторы_1_out_112 ),
    .out_113(\индикаторы_1_out_113 ), .out_114(\индикаторы_1_out_114 ), .out_115(\индикаторы_1_out_115 ),
    .out_116(\индикаторы_1_out_116 ), .out_117(\индикаторы_1_out_117 ), .out_118(\индикаторы_1_out_118 ),
    .out_119(\индикаторы_1_out_119 ), .out_120(\индикаторы_1_out_120 ), .out_121(\индикаторы_1_out_121 ),
    .out_122(\индикаторы_1_out_122 ));
  DotMatrix #(.matrixcols(20), .matrixrows(32)) dotmatrix_113 (
    .col0(\индикаторы_1_out_3 ), .col1(\индикаторы_1_out_4 ), .col2(\индикаторы_1_out_5 ),
    .col3(\индикаторы_1_out_6 ), .col4(\индикаторы_1_out_7 ), .col5(\индикаторы_1_out_8 ),
    .col6(\индикаторы_1_out_9 ), .col7(\индикаторы_1_out_10 ), .col8(\индикаторы_1_out_11 ),
    .col9(\индикаторы_1_out_12 ), .col10(\индикаторы_1_out_13 ), .col11(\индикаторы_1_out_14 ),
    .col12(\индикаторы_1_out_15 ), .col13(\индикаторы_1_out_16 ), .col14(\индикаторы_1_out_17 ),
    .col15(\индикаторы_1_out_18 ), .col16(\индикаторы_1_out_19 ), .col17(\индикаторы_1_out_20 ),
    .col18(\индикаторы_1_out_21 ), .col19(\индикаторы_1_out_22 ));
  DotMatrix #(.matrixcols(20), .matrixrows(32)) dotmatrix_114 (
    .col0(\индикаторы_1_out_63 ), .col1(\индикаторы_1_out_64 ), .col2(\индикаторы_1_out_65 ),
    .col3(\индикаторы_1_out_66 ), .col4(\индикаторы_1_out_67 ), .col5(\индикаторы_1_out_68 ),
    .col6(\индикаторы_1_out_69 ), .col7(\индикаторы_1_out_70 ), .col8(\индикаторы_1_out_71 ),
    .col9(\индикаторы_1_out_72 ), .col10(\индикаторы_1_out_73 ), .col11(\индикаторы_1_out_74 ),
    .col12(\индикаторы_1_out_75 ), .col13(\индикаторы_1_out_76 ), .col14(\индикаторы_1_out_77 ),
    .col15(\индикаторы_1_out_78 ), .col16(\индикаторы_1_out_79 ), .col17(\индикаторы_1_out_80 ),
    .col18(\индикаторы_1_out_81 ), .col19(\индикаторы_1_out_82 ));
  DotMatrix #(.matrixcols(20), .matrixrows(32)) dotmatrix_115 (
    .col0(\индикаторы_1_out_23 ), .col1(\индикаторы_1_out_24 ), .col2(\индикаторы_1_out_25 ),
    .col3(\индикаторы_1_out_26 ), .col4(\индикаторы_1_out_27 ), .col5(\индикаторы_1_out_28 ),
    .col6(\индикаторы_1_out_29 ), .col7(\индикаторы_1_out_30 ), .col8(\индикаторы_1_out_31 ),
    .col9(\индикаторы_1_out_32 ), .col10(\индикаторы_1_out_33 ), .col11(\индикаторы_1_out_34 ),
    .col12(\индикаторы_1_out_35 ), .col13(\индикаторы_1_out_36 ), .col14(\индикаторы_1_out_37 ),
    .col15(\индикаторы_1_out_38 ), .col16(\индикаторы_1_out_39 ), .col17(\индикаторы_1_out_40 ),
    .col18(\индикаторы_1_out_41 ), .col19(\индикаторы_1_out_42 ));
  DotMatrix #(.matrixcols(20), .matrixrows(32)) dotmatrix_116 (
    .col0(\индикаторы_1_out_83 ), .col1(\индикаторы_1_out_84 ), .col2(\индикаторы_1_out_85 ),
    .col3(\индикаторы_1_out_86 ), .col4(\индикаторы_1_out_87 ), .col5(\индикаторы_1_out_88 ),
    .col6(\индикаторы_1_out_89 ), .col7(\индикаторы_1_out_90 ), .col8(\индикаторы_1_out_91 ),
    .col9(\индикаторы_1_out_92 ), .col10(\индикаторы_1_out_93 ), .col11(\индикаторы_1_out_94 ),
    .col12(\индикаторы_1_out_95 ), .col13(\индикаторы_1_out_96 ), .col14(\индикаторы_1_out_97 ),
    .col15(\индикаторы_1_out_98 ), .col16(\индикаторы_1_out_99 ), .col17(\индикаторы_1_out_100 ),
    .col18(\индикаторы_1_out_101 ), .col19(\индикаторы_1_out_102 ));
  DotMatrix #(.matrixcols(20), .matrixrows(32)) dotmatrix_117 (
    .col0(\индикаторы_1_out_43 ), .col1(\индикаторы_1_out_44 ), .col2(\индикаторы_1_out_45 ),
    .col3(\индикаторы_1_out_46 ), .col4(\индикаторы_1_out_47 ), .col5(\индикаторы_1_out_48 ),
    .col6(\индикаторы_1_out_49 ), .col7(\индикаторы_1_out_50 ), .col8(\индикаторы_1_out_51 ),
    .col9(\индикаторы_1_out_52 ), .col10(\индикаторы_1_out_53 ), .col11(\индикаторы_1_out_54 ),
    .col12(\индикаторы_1_out_55 ), .col13(\индикаторы_1_out_56 ), .col14(\индикаторы_1_out_57 ),
    .col15(\индикаторы_1_out_58 ), .col16(\индикаторы_1_out_59 ), .col17(\индикаторы_1_out_60 ),
    .col18(\индикаторы_1_out_61 ), .col19(\индикаторы_1_out_62 ));
  DotMatrix #(.matrixcols(20), .matrixrows(32)) dotmatrix_118 (
    .col0(\индикаторы_1_out_103 ), .col1(\индикаторы_1_out_104 ), .col2(\индикаторы_1_out_105 ),
    .col3(\индикаторы_1_out_106 ), .col4(\индикаторы_1_out_107 ), .col5(\индикаторы_1_out_108 ),
    .col6(\индикаторы_1_out_109 ), .col7(\индикаторы_1_out_110 ), .col8(\индикаторы_1_out_111 ),
    .col9(\индикаторы_1_out_112 ), .col10(\индикаторы_1_out_113 ), .col11(\индикаторы_1_out_114 ),
    .col12(\индикаторы_1_out_115 ), .col13(\индикаторы_1_out_116 ), .col14(\индикаторы_1_out_117 ),
    .col15(\индикаторы_1_out_118 ), .col16(\индикаторы_1_out_119 ), .col17(\индикаторы_1_out_120 ),
    .col18(\индикаторы_1_out_121 ), .col19(\индикаторы_1_out_122 ));
endmodule

module \rand  (
  input  tick,
  input  button,
  input  clear,
  output [17:0] rand_pipe,
  output [9:0] signal
);

  wire and_1_out, and_2_out, and_3_out, and_4_out, clear0, clock_1_out, comparator_1_eq, comparator_2_eq,
       counter_3_carry, counter_4_carry, not_1_out, not_2_out, not_3_out, not_4_out, not_5_out, not_6_out,
       not_7_out, not_8_out, not_9_out, not_10_out, not_11_out, not_12_out, not_13_out, not_14_out,
       not_15_out, not_16_out, not_17_out, not_18_out, not_19_out, not_20_out, not_21_out, not_22_out,
       not_23_out, not_24_out, not_25_out, not_26_out, not_27_out, not_28_out, not_29_out, not_30_out,
       not_31_out, not_32_out, or_1_out, shift_register_1_q0, shift_register_1_q1, shift_register_1_q2,
       shift_register_1_q3, shift_register_1_q4, shift_register_1_q5, shift_register_1_q6,
       shift_register_1_q7, shift_register_1_q8, shift_register_1_q9, shift_register_1_q10,
       shift_register_1_q11, shift_register_1_q12, shift_register_1_q13, shift_register_1_q14,
       shift_register_1_q15, shift_register_1_q16, shift_register_1_q17, shift_register_1_q18,
       shift_register_1_q19, shift_register_1_q20, shift_register_1_q21, shift_register_1_q22,
       shift_register_1_q23, shift_register_1_q24, shift_register_1_q25, shift_register_1_q26,
       shift_register_1_q27, shift_register_1_q28, shift_register_1_q29, shift_register_1_q30,
       shift_register_1_q31;
  wire [2:0] adder_1_out, counter_4_q, multiplexer_1_out, random_1_out, register_1_q;
  wire [7:0] counter_2_q;

  Counter #(.width(5), .max('h7), .trigger("falling")) counter_1 (
    .carry(signal[8]), .clk(tick), .clr(clear));  // open: load, D, count, Q
  bird bird_1 (.button(button), .tick(tick), .tick_2(signal[7]));
  Counter #(.max('h7f), .trigger("falling")) counter_2 (
    .Q(counter_2_q), .clk(signal[8]), .clr(clear));  // open: load, D, count, carry
  D_Flip_Flop d_ff_1 (.clk(clear), .D(clear), .Q(clear0), .reset(not_32_out));  // open: Qn, preset, en
  Comparator #(.mode("unsigned")) comparator_1 (.a({8{1'b0}}), .b(counter_2_q), .eq(comparator_1_eq));  // open: gt, lt
  Clock clock_1 (.out(clock_1_out));
  Counter #(.width(6), .max('h2b)) counter_3 (
    .D(6'b101010), .carry(counter_3_carry), .clk(and_2_out));  // open: load, count, Q, clr
  and and_1 (and_1_out, comparator_1_eq, ~clear0);  // AND_Gate
  and and_2 (and_2_out, clock_1_out, clear0);
  Counter #(.width(3), .max('h7)) counter_4 (
    .Q(counter_4_q), .carry(counter_4_carry), .clk(signal[9]), .clr(clear));  // open: load, D, count
  Shift_Register #(.length(32)) shift_register_1 (
    .in(and_1_out), .clk(or_1_out), .q0(shift_register_1_q0), .q1(shift_register_1_q1),
    .q2(shift_register_1_q2), .q3(shift_register_1_q3), .q4(shift_register_1_q4), .q5(shift_register_1_q5),
    .q6(shift_register_1_q6), .q7(shift_register_1_q7), .q8(shift_register_1_q8), .q9(shift_register_1_q9),
    .q10(shift_register_1_q10), .q11(shift_register_1_q11), .q12(shift_register_1_q12),
    .q13(shift_register_1_q13), .q14(shift_register_1_q14), .q15(shift_register_1_q15),
    .q16(shift_register_1_q16), .q17(shift_register_1_q17), .q18(shift_register_1_q18),
    .q19(shift_register_1_q19), .q20(shift_register_1_q20), .q21(shift_register_1_q21),
    .q22(shift_register_1_q22), .q23(shift_register_1_q23), .q24(shift_register_1_q24),
    .q25(shift_register_1_q25), .q26(shift_register_1_q26), .q27(shift_register_1_q27),
    .q28(shift_register_1_q28), .q29(shift_register_1_q29), .q30(shift_register_1_q30),
    .q31(shift_register_1_q31));  // open: shift, out, load, clr, d0, d1, d2, d3, d4, d5, d6, d7, d8, d9, d10, d11, d12, d13, d14, d15, d16, d17, d18, d19, d20, d21, d22, d23, d24, d25, d26, d27, d28, d29, d30, d31
  or or_1 (or_1_out, and_2_out, signal[8]);
  and and_3 (and_3_out, counter_3_carry, clear0);
  Random #(.width(3)) random_1 (.clk(counter_4_carry), .out(random_1_out));  // open: next, clr
  Adder #(.width(3)) adder_1 (.a(3'b001), .b(random_1_out), .out(adder_1_out));  // open: cin, cout
  Register #(.width(3), .trigger("low")) register_1 (
    .D(random_1_out), .Q(register_1_q), .clk(counter_4_carry), .clr(clear));  // open: en
  or or_2 (signal[9], shift_register_1_q0, shift_register_1_q1, shift_register_1_q2, shift_register_1_q3, shift_register_1_q4, shift_register_1_q5, shift_register_1_q6, shift_register_1_q7, shift_register_1_q8, shift_register_1_q9, shift_register_1_q10, shift_register_1_q11, shift_register_1_q12, shift_register_1_q13, shift_register_1_q14, shift_register_1_q15, shift_register_1_q17, shift_register_1_q18, shift_register_1_q19, shift_register_1_q20, shift_register_1_q21, shift_register_1_q22, shift_register_1_q23, shift_register_1_q24, shift_register_1_q25, shift_register_1_q26, shift_register_1_q27, shift_register_1_q28, shift_register_1_q29, shift_register_1_q30, shift_register_1_q31, shift_register_1_q16);
  Comparator #(.width(3)) comparator_2 (.a(register_1_q), .b(random_1_out), .eq(comparator_2_eq));  // open: gt, lt
  Multiplexer #(.width(3)) multiplexer_1 (
    .in0(random_1_out), .in1(adder_1_out), .out(multiplexer_1_out), .sel(and_4_out));  // open: en
  and and_4 (and_4_out, comparator_2_eq, counter_4_carry);
  not not_1 (not_1_out, and_3_out);
  not not_2 (not_2_out, not_3_out);
  not not_3 (not_3_out, not_1_out);
  rand_pipe rand_pipe_1 (.out_3(rand_pipe), .rand_2(multiplexer_1_out), .rand_1(counter_4_q));
  not not_4 (not_4_out, not_2_out);
  not not_5 (not_5_out, not_4_out);
  not not_6 (not_6_out, not_7_out);
  not not_7 (not_7_out, not_5_out);
  not not_8 (not_8_out, not_6_out);
  not not_9 (not_9_out, not_10_out);
  not not_10 (not_10_out, not_11_out);
  not not_11 (not_11_out, not_8_out);
  not not_12 (not_12_out, not_13_out);
  not not_13 (not_13_out, not_15_out);
  not not_14 (not_14_out, not_12_out);
  not not_15 (not_15_out, not_9_out);
  not not_16 (not_16_out, not_17_out);
  not not_17 (not_17_out, not_18_out);
  not not_18 (not_18_out, not_19_out);
  not not_19 (not_19_out, not_14_out);
  not not_20 (not_20_out, not_21_out);
  not not_21 (not_21_out, not_16_out);
  not not_22 (not_22_out, not_23_out);
  not not_23 (not_23_out, not_20_out);
  not not_24 (not_24_out, not_26_out);
  not not_25 (not_25_out, not_27_out);
  not not_26 (not_26_out, not_25_out);
  not not_27 (not_27_out, not_22_out);
  not not_28 (not_28_out, not_31_out);
  not not_29 (not_29_out, not_24_out);
  not not_30 (not_30_out, not_29_out);
  not not_31 (not_31_out, not_30_out);
  not not_32 (not_32_out, not_28_out);

  assign signal[6:0] = {button, {6{1'b0}}};

  // Other names for the same wires on the sheet: tick_1 = signal[8]; tick_2 = signal[9]
endmodule
module pipes (
  input  [31:0] pipe,
  input  [9:0] signal,
  input  [31:0] bird_1,
  input  [31:0] bird_2,
  output [31:0] out_5,
  output [31:0] out_6,
  output [31:0] out_7,
  output [31:0] out_8,
  output [31:0] out_9,
  output [31:0] out_10,
  output [31:0] out_11,
  output [31:0] out_12,
  output [31:0] out_13,
  output [31:0] out_14,
  output [31:0] out_15,
  output [31:0] out_16,
  output [31:0] out_17,
  output [31:0] out_18,
  output [31:0] out_19,
  output [31:0] out_20,
  output [31:0] out_21,
  output [31:0] out_22,
  output [31:0] out_23,
  output [31:0] out_24,
  output [31:0] out_25,
  output [31:0] out_26,
  output [31:0] out_27,
  output [31:0] out_28,
  output [31:0] out_29,
  output [31:0] out_30,
  output [31:0] out_31,
  output [31:0] out_32,
  output [31:0] out_33,
  output [31:0] out_34,
  output [31:0] out_35,
  output [31:0] out_36,
  output [31:0] pipe_2,
  output [31:0] bird_1_2,
  output [9:0] signal_2,
  output [31:0] bird
);

  wire [31:0] _1, _2, pull_resistor_1_node, pull_resistor_2_node, pull_resistor_3_node, pull_resistor_4_node,
       pull_resistor_5_node, pull_resistor_6_node, pull_resistor_7_node, pull_resistor_8_node,
       pull_resistor_9_node, pull_resistor_10_node, pull_resistor_11_node, pull_resistor_12_node,
       pull_resistor_13_node, pull_resistor_14_node, pull_resistor_15_node, pull_resistor_16_node,
       pull_resistor_17_node, pull_resistor_18_node, pull_resistor_19_node, pull_resistor_20_node,
       pull_resistor_21_node, pull_resistor_22_node, pull_resistor_23_node, pull_resistor_24_node,
       pull_resistor_25_node, pull_resistor_26_node, pull_resistor_27_node, pull_resistor_28_node,
       pull_resistor_29_node, pull_resistor_30_node, pull_resistor_31_node, pull_resistor_32_node,
       register_2_q, register_3_q, register_4_q, register_5_q, register_6_q, register_7_q, register_8_q,
       register_9_q, register_10_q, register_11_q, register_12_q, register_13_q, register_14_q,
       register_15_q, register_16_q, register_17_q, register_18_q, register_19_q, register_20_q,
       register_21_q, register_22_q, register_23_q, register_24_q, register_25_q, register_26_q,
       register_27_q, register_28_q, register_29_q, register_30_q, register_31_q, register_32_q;

  assign out_5 = pull_resistor_1_node | _2;  // OR_Gate or_1, 32 bits wide
  Pull_Resistor pull_resistor_1 (.node(pull_resistor_1_node));
  assign pull_resistor_1_node = _1[0] ? pipe_2 : 32'bz;  // Controlled_Buffer controlled_buffer_1
  Register #(.width(32), .trigger("high")) register_1 (.D(register_2_q), .Q(pipe_2), .clk(_1[0]));  // open: en, clr
  Shift_Register #(.length(32)) shift_register_1 (
    .in(signal[8]), .clk(signal[7]), .out(signal_2[8]), .q0(_1[31]), .q1(_1[30]), .q2(_1[29]), .q3(_1[28]),
    .q4(_1[27]), .q5(_1[26]), .q6(_1[25]), .q7(_1[24]), .q8(_1[23]), .q9(_1[22]), .q10(_1[21]), .q11(_1[20]),
    .q12(_1[19]), .q13(_1[18]), .q14(_1[17]), .q15(_1[16]), .q16(_1[15]), .q17(_1[14]), .q18(_1[13]),
    .q19(_1[12]), .q20(_1[11]), .q21(_1[10]), .q22(_1[9]), .q23(_1[8]), .q24(_1[7]), .q25(_1[6]),
    .q26(_1[5]), .q27(_1[4]), .q28(_1[3]), .q29(_1[2]), .q30(_1[1]), .q31(_1[0]));  // open: shift, load, clr, d0, d1, d2, d3, d4, d5, d6, d7, d8, d9, d10, d11, d12, d13, d14, d15, d16, d17, d18, d19, d20, d21, d22, d23, d24, d25, d26, d27, d28, d29, d30, d31
  assign out_6 = pull_resistor_2_node | _2;  // OR_Gate or_2, 32 bits wide
  Pull_Resistor pull_resistor_2 (.node(pull_resistor_2_node));
  assign pull_resistor_2_node = _1[1] ? register_2_q : 32'bz;  // Controlled_Buffer controlled_buffer_2
  Register #(.width(32), .trigger("high")) register_2 (
    .D(register_3_q), .Q(register_2_q), .clk(_1[1]));  // open: en, clr
  Pull_Resistor pull_resistor_3 (.node(pull_resistor_3_node));
  assign pull_resistor_3_node = _1[2] ? register_3_q : 32'bz;  // Controlled_Buffer controlled_buffer_3
  Register #(.width(32), .trigger("high")) register_3 (
    .D(register_4_q), .Q(register_3_q), .clk(_1[2]));  // open: en, clr
  assign out_7 = pull_resistor_3_node | _2;  // OR_Gate or_3, 32 bits wide
  Adder #(.width(3)) adder_1 (.a(signal[6:4]), .b(3'b001), .out(signal_2[6:4]));  // open: cin, cout
  assign out_8 = pull_resistor_4_node | _2;  // OR_Gate or_4, 32 bits wide
  Pull_Resistor pull_resistor_4 (.node(pull_resistor_4_node));
  assign pull_resistor_4_node = _1[3] ? register_4_q : 32'bz;  // Controlled_Buffer controlled_buffer_4
  Register #(.width(32), .trigger("high")) register_4 (
    .D(register_5_q), .Q(register_4_q), .clk(_1[3]));  // open: en, clr
  assign out_9 = pull_resistor_5_node | _2;  // OR_Gate or_5, 32 bits wide
  Pull_Resistor pull_resistor_5 (.node(pull_resistor_5_node));
  assign pull_resistor_5_node = _1[4] ? register_5_q : 32'bz;  // Controlled_Buffer controlled_buffer_5
  Register #(.width(32), .trigger("high")) register_5 (
    .D(register_6_q), .Q(register_5_q), .clk(_1[4]));  // open: en, clr
  assign out_10 = pull_resistor_6_node | _2;  // OR_Gate or_6, 32 bits wide
  Pull_Resistor pull_resistor_6 (.node(pull_resistor_6_node));
  assign pull_resistor_6_node = _1[5] ? register_6_q : 32'bz;  // Controlled_Buffer controlled_buffer_6
  Register #(.width(32), .trigger("high")) register_6 (
    .D(register_7_q), .Q(register_6_q), .clk(_1[5]));  // open: en, clr
  Pull_Resistor pull_resistor_7 (.node(pull_resistor_7_node));
  assign pull_resistor_7_node = _1[6] ? register_7_q : 32'bz;  // Controlled_Buffer controlled_buffer_7
  Register #(.width(32), .trigger("high")) register_7 (
    .D(register_8_q), .Q(register_7_q), .clk(_1[6]));  // open: en, clr
  assign out_11 = pull_resistor_7_node | _2;  // OR_Gate or_7, 32 bits wide
  assign out_12 = pull_resistor_8_node | _2;  // OR_Gate or_8, 32 bits wide
  Pull_Resistor pull_resistor_8 (.node(pull_resistor_8_node));
  assign pull_resistor_8_node = _1[7] ? register_8_q : 32'bz;  // Controlled_Buffer controlled_buffer_8
  Register #(.width(32), .trigger("high")) register_8 (
    .D(register_9_q), .Q(register_8_q), .clk(_1[7]));  // open: en, clr
  assign out_13 = pull_resistor_9_node | _2;  // OR_Gate or_9, 32 bits wide
  Pull_Resistor pull_resistor_9 (.node(pull_resistor_9_node));
  assign pull_resistor_9_node = _1[8] ? register_9_q : 32'bz;  // Controlled_Buffer controlled_buffer_9
  Register #(.width(32), .trigger("high")) register_9 (
    .D(register_10_q), .Q(register_9_q), .clk(_1[8]));  // open: en, clr
  assign out_14 = pull_resistor_10_node | _2;  // OR_Gate or_10, 32 bits wide
  Pull_Resistor pull_resistor_10 (.node(pull_resistor_10_node));
  assign pull_resistor_10_node = _1[9] ? register_10_q : 32'bz;  // Controlled_Buffer controlled_buffer_10
  Register #(.width(32), .trigger("high")) register_10 (
    .D(register_11_q), .Q(register_10_q), .clk(_1[9]));  // open: en, clr
  Multiplexer #(.select(4), .width(32)) multiplexer_1 (
    .in0(32'h3ff), .in1({32{1'b0}}), .in2({32{1'b0}}), .in3({32{1'b0}}), .in4({32{1'b0}}), .in5({32{1'b0}}),
    .in6({32{1'b0}}), .in7({32{1'b0}}), .in8({32{1'b0}}), .in9({32{1'b0}}), .in10({32{1'b0}}),
    .in11({32{1'b0}}), .out(_2), .sel(signal[3:0]));  // open: in12, in13, in14, in15, en
  Pull_Resistor pull_resistor_11 (.node(pull_resistor_11_node));
  assign pull_resistor_11_node = _1[10] ? register_11_q : 32'bz;  // Controlled_Buffer controlled_buffer_11
  Register #(.width(32), .trigger("high")) register_11 (
    .D(register_12_q), .Q(register_11_q), .clk(_1[10]));  // open: en, clr
  assign out_15 = pull_resistor_11_node | _2;  // OR_Gate or_11, 32 bits wide
  assign out_16 = pull_resistor_12_node | _2;  // OR_Gate or_12, 32 bits wide
  Pull_Resistor pull_resistor_12 (.node(pull_resistor_12_node));
  assign pull_resistor_12_node = _1[11] ? register_12_q : 32'bz;  // Controlled_Buffer controlled_buffer_12
  Register #(.width(32), .trigger("high")) register_12 (
    .D(register_13_q), .Q(register_12_q), .clk(_1[11]));  // open: en, clr
  assign out_17 = pull_resistor_13_node | _2;  // OR_Gate or_13, 32 bits wide
  Pull_Resistor pull_resistor_13 (.node(pull_resistor_13_node));
  assign pull_resistor_13_node = _1[12] ? register_13_q : 32'bz;  // Controlled_Buffer controlled_buffer_13
  Register #(.width(32), .trigger("high")) register_13 (
    .D(register_14_q), .Q(register_13_q), .clk(_1[12]));  // open: en, clr
  assign out_18 = pull_resistor_14_node | _2;  // OR_Gate or_14, 32 bits wide
  Pull_Resistor pull_resistor_14 (.node(pull_resistor_14_node));
  assign pull_resistor_14_node = _1[13] ? register_14_q : 32'bz;  // Controlled_Buffer controlled_buffer_14
  Register #(.width(32), .trigger("high")) register_14 (
    .D(register_15_q), .Q(register_14_q), .clk(_1[13]));  // open: en, clr
  Pull_Resistor pull_resistor_15 (.node(pull_resistor_15_node));
  assign pull_resistor_15_node = _1[14] ? register_15_q : 32'bz;  // Controlled_Buffer controlled_buffer_15
  Register #(.width(32), .trigger("high")) register_15 (
    .D(register_16_q), .Q(register_15_q), .clk(_1[14]));  // open: en, clr
  assign out_19 = pull_resistor_15_node | _2;  // OR_Gate or_15, 32 bits wide
  assign out_20 = pull_resistor_16_node | _2;  // OR_Gate or_16, 32 bits wide
  Pull_Resistor pull_resistor_16 (.node(pull_resistor_16_node));
  assign pull_resistor_16_node = _1[15] ? register_16_q : 32'bz;  // Controlled_Buffer controlled_buffer_16
  Register #(.width(32), .trigger("high")) register_16 (
    .D(register_17_q), .Q(register_16_q), .clk(_1[15]));  // open: en, clr
  assign out_21 = pull_resistor_17_node | _2;  // OR_Gate or_17, 32 bits wide
  Pull_Resistor pull_resistor_17 (.node(pull_resistor_17_node));
  assign pull_resistor_17_node = _1[16] ? register_17_q : 32'bz;  // Controlled_Buffer controlled_buffer_17
  Register #(.width(32), .trigger("high")) register_17 (
    .D(register_18_q), .Q(register_17_q), .clk(_1[16]));  // open: en, clr
  assign out_22 = pull_resistor_18_node | _2;  // OR_Gate or_18, 32 bits wide
  Pull_Resistor pull_resistor_18 (.node(pull_resistor_18_node));
  assign pull_resistor_18_node = _1[17] ? register_18_q : 32'bz;  // Controlled_Buffer controlled_buffer_18
  Register #(.width(32), .trigger("high")) register_18 (
    .D(register_19_q), .Q(register_18_q), .clk(_1[17]));  // open: en, clr
  Pull_Resistor pull_resistor_19 (.node(pull_resistor_19_node));
  assign pull_resistor_19_node = _1[18] ? register_19_q : 32'bz;  // Controlled_Buffer controlled_buffer_19
  Register #(.width(32), .trigger("high")) register_19 (
    .D(register_20_q), .Q(register_19_q), .clk(_1[18]));  // open: en, clr
  assign out_23 = pull_resistor_19_node | _2;  // OR_Gate or_19, 32 bits wide
  assign out_24 = pull_resistor_20_node | _2;  // OR_Gate or_20, 32 bits wide
  Pull_Resistor pull_resistor_20 (.node(pull_resistor_20_node));
  assign pull_resistor_20_node = _1[19] ? register_20_q : 32'bz;  // Controlled_Buffer controlled_buffer_20
  Register #(.width(32), .trigger("high")) register_20 (
    .D(register_21_q), .Q(register_20_q), .clk(_1[19]));  // open: en, clr
  assign out_25 = pull_resistor_21_node | _2;  // OR_Gate or_21, 32 bits wide
  Pull_Resistor pull_resistor_21 (.node(pull_resistor_21_node));
  assign pull_resistor_21_node = _1[20] ? register_21_q : 32'bz;  // Controlled_Buffer controlled_buffer_21
  Register #(.width(32), .trigger("high")) register_21 (
    .D(register_22_q), .Q(register_21_q), .clk(_1[20]));  // open: en, clr
  assign out_26 = pull_resistor_22_node | _2;  // OR_Gate or_22, 32 bits wide
  Pull_Resistor pull_resistor_22 (.node(pull_resistor_22_node));
  assign pull_resistor_22_node = _1[21] ? register_22_q : 32'bz;  // Controlled_Buffer controlled_buffer_22
  Register #(.width(32), .trigger("high")) register_22 (
    .D(register_23_q), .Q(register_22_q), .clk(_1[21]));  // open: en, clr
  Pull_Resistor pull_resistor_23 (.node(pull_resistor_23_node));
  assign pull_resistor_23_node = _1[22] ? register_23_q : 32'bz;  // Controlled_Buffer controlled_buffer_23
  Register #(.width(32), .trigger("high")) register_23 (
    .D(register_24_q), .Q(register_23_q), .clk(_1[22]));  // open: en, clr
  assign out_27 = pull_resistor_23_node | _2;  // OR_Gate or_23, 32 bits wide
  assign out_28 = pull_resistor_24_node | _2;  // OR_Gate or_24, 32 bits wide
  Pull_Resistor pull_resistor_24 (.node(pull_resistor_24_node));
  assign pull_resistor_24_node = _1[23] ? register_24_q : 32'bz;  // Controlled_Buffer controlled_buffer_24
  Register #(.width(32), .trigger("high")) register_24 (
    .D(register_25_q), .Q(register_24_q), .clk(_1[23]));  // open: en, clr
  assign out_29 = pull_resistor_25_node | _2;  // OR_Gate or_25, 32 bits wide
  Pull_Resistor pull_resistor_25 (.node(pull_resistor_25_node));
  assign pull_resistor_25_node = _1[24] ? register_25_q : 32'bz;  // Controlled_Buffer controlled_buffer_25
  Register #(.width(32), .trigger("high")) register_25 (
    .D(register_26_q), .Q(register_25_q), .clk(_1[24]));  // open: en, clr
  assign out_30 = pull_resistor_26_node | _2;  // OR_Gate or_26, 32 bits wide
  Pull_Resistor pull_resistor_26 (.node(pull_resistor_26_node));
  assign pull_resistor_26_node = _1[25] ? register_26_q : 32'bz;  // Controlled_Buffer controlled_buffer_26
  Register #(.width(32), .trigger("high")) register_26 (
    .D(register_27_q), .Q(register_26_q), .clk(_1[25]));  // open: en, clr
  Pull_Resistor pull_resistor_27 (.node(pull_resistor_27_node));
  assign pull_resistor_27_node = _1[26] ? register_27_q : 32'bz;  // Controlled_Buffer controlled_buffer_27
  Register #(.width(32), .trigger("high")) register_27 (
    .D(register_28_q), .Q(register_27_q), .clk(_1[26]));  // open: en, clr
  assign out_31 = pull_resistor_27_node | _2;  // OR_Gate or_27, 32 bits wide
  assign out_32 = pull_resistor_28_node | _2;  // OR_Gate or_28, 32 bits wide
  Pull_Resistor pull_resistor_28 (.node(pull_resistor_28_node));
  assign pull_resistor_28_node = _1[27] ? register_28_q : 32'bz;  // Controlled_Buffer controlled_buffer_28
  Register #(.width(32), .trigger("high")) register_28 (
    .D(register_29_q), .Q(register_28_q), .clk(_1[27]));  // open: en, clr
  assign out_33 = pull_resistor_29_node | _2;  // OR_Gate or_29, 32 bits wide
  Pull_Resistor pull_resistor_29 (.node(pull_resistor_29_node));
  assign pull_resistor_29_node = _1[28] ? register_29_q : 32'bz;  // Controlled_Buffer controlled_buffer_29
  Register #(.width(32), .trigger("high")) register_29 (
    .D(register_30_q), .Q(register_29_q), .clk(_1[28]));  // open: en, clr
  assign out_34 = pull_resistor_30_node | _2;  // OR_Gate or_30, 32 bits wide
  Pull_Resistor pull_resistor_30 (.node(pull_resistor_30_node));
  assign pull_resistor_30_node = _1[29] ? register_30_q : 32'bz;  // Controlled_Buffer controlled_buffer_30
  Register #(.width(32), .trigger("high")) register_30 (
    .D(register_31_q), .Q(register_30_q), .clk(_1[29]));  // open: en, clr
  Pull_Resistor pull_resistor_31 (.node(pull_resistor_31_node));
  assign pull_resistor_31_node = _1[30] ? register_31_q : 32'bz;  // Controlled_Buffer controlled_buffer_31
  Register #(.width(32), .trigger("high")) register_31 (
    .D(register_32_q), .Q(register_31_q), .clk(_1[30]));  // open: en, clr
  assign out_35 = pull_resistor_31_node | _2;  // OR_Gate or_31, 32 bits wide
  assign out_36 = pull_resistor_32_node | _2;  // OR_Gate or_32, 32 bits wide
  Pull_Resistor pull_resistor_32 (.node(pull_resistor_32_node));
  assign pull_resistor_32_node = _1[31] ? register_32_q : 32'bz;  // Controlled_Buffer controlled_buffer_32
  Register #(.width(32), .trigger("high")) register_32 (.D(pipe), .Q(register_32_q), .clk(_1[31]));  // open: en, clr

  assign bird = bird_2;
  assign bird_1_2 = bird_1;
  assign {signal_2[9], signal_2[7], signal_2[3:0]} = {signal[9], signal[7], signal[3:0]};
endmodule

module rand_pipe (
  input  [2:0] rand_1,
  input  [2:0] rand_2,
  output [17:0] out_3
);

  wire [17:0] multiplexer_1_out, multiplexer_2_out, multiplexer_3_out, multiplexer_4_out, multiplexer_5_out,
       multiplexer_6_out, multiplexer_7_out, multiplexer_8_out;

  Multiplexer #(.select(3), .width(18)) multiplexer_1 (
    .in0(18'h20f75), .in1(18'h20f75), .in2(18'h20f75), .in3(18'h20f75), .in4(18'h20f75), .in5(18'h20f75),
    .in6(18'h20f75), .in7(18'h20f75), .out(multiplexer_1_out), .sel(rand_1));  // open: en
  Multiplexer #(.select(3), .width(18)) multiplexer_2 (
    .in0(18'h20f75), .in1(18'h20f75), .in2(18'h20f75), .in3(18'h20f75), .in4(18'h20f75), .in5(18'h20f75),
    .in6(18'h20f75), .in7(18'h20f75), .out(multiplexer_2_out), .sel(rand_1));  // open: en
  Multiplexer #(.select(3), .width(18)) multiplexer_3 (
    .in0(18'h20f75), .in1(18'h20f75), .in2(18'h20f75), .in3(18'h20f75), .in4(18'h20f75), .in5(18'h20f75),
    .in6(18'h20f75), .in7(18'h20f75), .out(multiplexer_3_out), .sel(rand_1));  // open: en
  Multiplexer #(.select(3), .width(18)) multiplexer_4 (
    .in0(18'h20f75), .in1(18'h20f75), .in2(18'h20f75), .in3(18'h20f75), .in4(18'h20f75), .in5(18'h20f75),
    .in6(18'h20f75), .in7(18'h20f75), .out(multiplexer_4_out), .sel(rand_1));  // open: en
  Multiplexer #(.select(3), .width(18)) multiplexer_5 (
    .in0(18'h20f75), .in1(18'h20f75), .in2(18'h20f75), .in3(18'h20f75), .in4(18'h20f75), .in5(18'h20f75),
    .in6(18'h20f75), .in7(18'h20f75), .out(multiplexer_5_out), .sel(rand_1));  // open: en
  Multiplexer #(.select(3), .width(18)) multiplexer_6 (
    .in0(18'h20f75), .in1(18'h20f75), .in2(18'h20f75), .in3(18'h20f75), .in4(18'h20f75), .in5(18'h20f75),
    .in6(18'h20f75), .in7(18'h20f75), .out(multiplexer_6_out), .sel(rand_1));  // open: en
  Multiplexer #(.select(3), .width(18)) multiplexer_7 (
    .in0(18'h20f75), .in1(18'h20f75), .in2(18'h20f75), .in3(18'h20f75), .in4(18'h20f75), .in5(18'h20f75),
    .in6(18'h20f75), .in7(18'h20f75), .out(multiplexer_7_out), .sel(rand_1));  // open: en
  Multiplexer #(.select(3), .width(18)) multiplexer_8 (
    .in0(18'h20f75), .in1(18'h20f75), .in2(18'h20f75), .in3(18'h20f75), .in4(18'h20f75), .in5(18'h20f75),
    .in6(18'h20f75), .in7(18'h20f75), .out(multiplexer_8_out), .sel(rand_1));  // open: en
  Multiplexer #(.select(3), .width(18)) multiplexer_9 (
    .in0(multiplexer_1_out), .in1(multiplexer_2_out), .in2(multiplexer_3_out), .in3(multiplexer_4_out),
    .in4(multiplexer_5_out), .in5(multiplexer_6_out), .in6(multiplexer_7_out), .in7(multiplexer_8_out),
    .out(out_3), .sel(rand_2));  // open: en

  // Other names for the same wires on the sheet: _1[2:0] = rand_1
endmodule

module bird (
  input  tick,
  input  button,
  output tick_2
);

  wire counter_19_carry, d_ff_1_q, multiplexer_1_out, multiplexer_2_out, not_2_out, reset_1, tick_1,
       tick_2_t, tick_3, tick_4, tick_5, tick_6, tick_7, tick_8, tick_9, tick_10, tick_11, tick_12, tick_13,
       tick_14, tick_15, tick_16, tick_fall, tick_jump;
  wire [3:0] counter_19_q, counter_20_q;

  Counter #(.width(32), .max('h13), .trigger("falling")) counter_1 (
    .carry(tick_jump), .clk(tick));  // open: load, D, count, Q, clr
  Counter #(.width(32), .max('h31), .trigger("falling")) counter_2 (
    .carry(tick_fall), .clk(tick));  // open: load, D, count, Q, clr
  Counter #(.width(32), .max('h3), .trigger("falling")) counter_3 (
    .carry(tick_1), .clk(tick));  // open: load, D, count, Q, clr
  Counter #(.width(32), .max('h4), .trigger("falling")) counter_4 (
    .carry(tick_2_t), .clk(tick));  // open: load, D, count, Q, clr
  Counter #(.width(32), .max('h5), .trigger("falling")) counter_5 (
    .carry(tick_3), .clk(tick));  // open: load, D, count, Q, clr
  Counter #(.width(32), .max('h6), .trigger("falling")) counter_6 (
    .carry(tick_4), .clk(tick));  // open: load, D, count, Q, clr
  Counter #(.width(32), .max('h7), .trigger("falling")) counter_7 (
    .carry(tick_5), .clk(tick));  // open: load, D, count, Q, clr
  Counter #(.width(32), .max('h9), .trigger("falling")) counter_8 (
    .carry(tick_6), .clk(tick));  // open: load, D, count, Q, clr
  Counter #(.width(32), .max('hb), .trigger("falling")) counter_9 (
    .carry(tick_7), .clk(tick));  // open: load, D, count, Q, clr
  Counter #(.width(32), .max('hd), .trigger("falling")) counter_10 (
    .carry(tick_8), .clk(tick));  // open: load, D, count, Q, clr
  Counter #(.width(32), .max('h10), .trigger("falling")) counter_11 (
    .carry(tick_9), .clk(tick));  // open: load, D, count, Q, clr
  Counter #(.width(32), .max('h14), .trigger("falling")) counter_12 (
    .carry(tick_10), .clk(tick));  // open: load, D, count, Q, clr
  Counter #(.width(32), .max('h18), .trigger("falling")) counter_13 (
    .carry(tick_11), .clk(tick));  // open: load, D, count, Q, clr
  Counter #(.width(32), .max('h1d), .trigger("falling")) counter_14 (
    .carry(tick_12), .clk(tick));  // open: load, D, count, Q, clr
  Counter #(.width(32), .max('h23), .trigger("falling")) counter_15 (
    .carry(tick_13), .clk(tick));  // open: load, D, count, Q, clr
  Counter #(.width(32), .max('h2a), .trigger("falling")) counter_16 (
    .carry(tick_14), .clk(tick));  // open: load, D, count, Q, clr
  Counter #(.width(32), .max('h32), .trigger("falling")) counter_17 (
    .carry(tick_15), .clk(tick));  // open: load, D, count, Q, clr
  Counter #(.width(32), .max('h3d), .trigger("falling")) counter_18 (
    .carry(tick_16), .clk(tick));  // open: load, D, count, Q, clr
  Counter #(.width(4), .max('hf), .ongoal("stay")) counter_19 (
    .Q(counter_19_q), .carry(counter_19_carry), .clk(tick_jump), .clr(button));  // open: load, D, count
  Multiplexer #(.select(4)) multiplexer_1 (
    .in0(tick_1), .in1(tick_2_t), .in2(tick_3), .in3(tick_4), .in4(tick_5), .in5(tick_6), .in6(tick_7),
    .in7(tick_8), .in8(tick_9), .in9(tick_10), .in10(tick_11), .in11(tick_12), .in12(tick_13),
    .in13(tick_14), .in14(tick_15), .in15(tick_16), .out(multiplexer_1_out), .sel(counter_19_q));  // open: en
  // NOT_Gate not_1 has open pins: in=counter_19_carry, out=open
  Multiplexer #(.select(4)) multiplexer_2 (
    .in0(tick_16), .in1(tick_15), .in2(tick_14), .in3(tick_13), .in4(tick_12), .in5(tick_11), .in6(tick_10),
    .in7(tick_9), .in8(tick_8), .in9(tick_7), .in10(tick_6), .in11(tick_5), .in12(tick_4), .in13(tick_3),
    .in14(tick_2_t), .in15(tick_1), .out(multiplexer_2_out), .sel(counter_20_q));  // open: en
  Counter #(.width(4), .max('hf), .ongoal("stay")) counter_20 (
    .Q(counter_20_q), .clk(tick_fall), .clr(reset_1));  // open: load, D, count, carry
  Multiplexer multiplexer_3 (
    .in0(multiplexer_2_out), .in1(multiplexer_1_out), .out(tick_2), .sel(d_ff_1_q));  // open: en
  not not_2 (not_2_out, d_ff_1_q);
  D_Flip_Flop d_ff_1 (.Q(d_ff_1_q), .preset(button), .reset(reset_1));  // open: clk, D, Qn, en
  Counter #(.max('h1f), .ongoal("stay")) counter_21 (
    .carry(reset_1), .clk(tick_2), .clr(not_2_out));  // open: load, D, count, Q

  // Other names for the same wires on the sheet: reset_2 = button
endmodule

module height (
  input  [17:0] pipe_signal,
  input  [9:0] signal_down,
  input  [1:0] signal_up,
  output [31:0] bird_1,
  output [31:0] bird_2,
  output [31:0] pipe,
  output [9:0] signal_up_2,
  output [1:0] signal_down_2,
  output [9:0] signal
);

  wire _1, _2, _3, _4, _5, and_1_out, comparator_1_eq, comparator_1_lt, counter_1_carry, counter_2_carry,
       counter_5_carry, d_ff_4_q, not_1_out, not_2_out, or_1_out, or_2_out, or_3_out;
  wire [7:0] counter_4_q;
  wire [31:0] _6, _7, bird_down_1, bird_down_2, bird_up_1, bird_up_2, reset_1, reset_2;

  pipe_height pipe_height_1 (.height(signal_down[3:0]), .pipe_signal(pipe_signal), .pipe(pipe));
  Counter #(.width(2), .max('h3), .ongoal("stay")) counter_1 (
    .carry(counter_1_carry), .clk(counter_2_carry));  // open: load, D, count, Q, clr
  Counter #(.max('hc)) counter_2 (.carry(counter_2_carry), .clk(signal_down[8]));  // open: load, D, count, Q, clr
  and and_1 (and_1_out, signal_down[6], _5);
  D_Flip_Flop d_ff_1 (.Q(_3), .preset(and_1_out), .reset(_4));  // open: clk, D, Qn, en
  Multiplexer #(.width(32)) multiplexer_1 (
    .in0(_6), .in1(bird_up_1), .out(reset_1), .sel(counter_1_carry));  // open: en
  Counter #(.width(1), .max('h1), .ongoal("stay")) counter_3 (
    .carry(_4), .clk(signal_down[7]), .clr(not_1_out));  // open: load, D, count, Q
  not not_1 (not_1_out, _3);
  Adder #(.width(4)) adder_1 (.a(signal_down[3:0]), .b(4'b0001), .out(signal_up_2[3:0]));  // open: cin, cout
  Multiplexer #(.width(32)) multiplexer_2 (
    .in0(_7), .in1(bird_up_2), .out(reset_2), .sel(counter_1_carry));  // open: en
  D_Flip_Flop d_ff_2 (.Q(_1), .preset(counter_2_carry), .reset(counter_1_carry));  // open: clk, D, Qn, en
  Counter #(.ongoal("stay")) counter_4 (
    .Q(counter_4_q), .clk(signal_down[7]), .clr(or_1_out));  // open: load, D, count, carry
  or or_1 (or_1_out, _5, signal_down[6]);
  Pull_Resistor pull_resistor_1 (.node(signal_up));
  D_Flip_Flop d_ff_3 (.Q(_2), .preset(comparator_1_eq), .reset(counter_5_carry));  // open: clk, D, Qn, en
  Counter #(.width(1), .max('h1), .ongoal("stay")) counter_5 (
    .carry(counter_5_carry), .clk(signal_down[7]), .clr(not_2_out));  // open: load, D, count, Q
  not not_2 (not_2_out, _2);
  Comparator #(.mode("unsigned")) comparator_1 (
    .a(8'h1d), .b(counter_4_q), .eq(comparator_1_eq), .lt(comparator_1_lt));  // open: gt
  not not_3 (_5, d_ff_4_q);
  or or_2 (or_2_out, _1, _2);
  Shift_Register #(.length(32)) shift_register_1 (
    .in(signal_up[0]), .clk(signal_down[7]), .out(signal_down_2[0]), .load(or_2_out), .d0(reset_1[31]),
    .q0(bird_down_1[31]), .d1(reset_1[30]), .q1(bird_down_1[30]), .d2(reset_1[29]), .q2(bird_down_1[29]),
    .d3(reset_1[28]), .q3(bird_down_1[28]), .d4(reset_1[27]), .q4(bird_down_1[27]), .d5(reset_1[26]),
    .q5(bird_down_1[26]), .d6(reset_1[25]), .q6(bird_down_1[25]), .d7(reset_1[24]), .q7(bird_down_1[24]),
    .d8(reset_1[23]), .q8(bird_down_1[23]), .d9(reset_1[22]), .q9(bird_down_1[22]), .d10(reset_1[21]),
    .q10(bird_down_1[21]), .d11(reset_1[20]), .q11(bird_down_1[20]), .d12(reset_1[19]),
    .q12(bird_down_1[19]), .d13(reset_1[18]), .q13(bird_down_1[18]), .d14(reset_1[17]),
    .q14(bird_down_1[17]), .d15(reset_1[16]), .q15(bird_down_1[16]), .d16(reset_1[15]),
    .q16(bird_down_1[15]), .d17(reset_1[14]), .q17(bird_down_1[14]), .d18(reset_1[13]),
    .q18(bird_down_1[13]), .d19(reset_1[12]), .q19(bird_down_1[12]), .d20(reset_1[11]),
    .q20(bird_down_1[11]), .d21(reset_1[10]), .q21(bird_down_1[10]), .d22(reset_1[9]), .q22(bird_down_1[9]),
    .d23(reset_1[8]), .q23(bird_down_1[8]), .d24(reset_1[7]), .q24(bird_down_1[7]), .d25(reset_1[6]),
    .q25(bird_down_1[6]), .d26(reset_1[5]), .q26(bird_down_1[5]), .d27(reset_1[4]), .q27(bird_down_1[4]),
    .d28(reset_1[3]), .q28(bird_down_1[3]), .d29(reset_1[2]), .q29(bird_down_1[2]), .d30(reset_1[1]),
    .q30(bird_down_1[1]), .d31(reset_1[0]), .q31(bird_down_1[0]));  // open: shift, clr
  Shift_Register #(.length(32)) shift_register_2 (
    .in(signal_down[4]), .clk(signal_down[7]), .out(signal_up_2[4]), .load(_3), .d0(bird_down_1[0]),
    .q0(bird_up_1[0]), .d1(bird_down_1[1]), .q1(bird_up_1[1]), .d2(bird_down_1[2]), .q2(bird_up_1[2]),
    .d3(bird_down_1[3]), .q3(bird_up_1[3]), .d4(bird_down_1[4]), .q4(bird_up_1[4]), .d5(bird_down_1[5]),
    .q5(bird_up_1[5]), .d6(bird_down_1[6]), .q6(bird_up_1[6]), .d7(bird_down_1[7]), .q7(bird_up_1[7]),
    .d8(bird_down_1[8]), .q8(bird_up_1[8]), .d9(bird_down_1[9]), .q9(bird_up_1[9]), .d10(bird_down_1[10]),
    .q10(bird_up_1[10]), .d11(bird_down_1[11]), .q11(bird_up_1[11]), .d12(bird_down_1[12]),
    .q12(bird_up_1[12]), .d13(bird_down_1[13]), .q13(bird_up_1[13]), .d14(bird_down_1[14]),
    .q14(bird_up_1[14]), .d15(bird_down_1[15]), .q15(bird_up_1[15]), .d16(bird_down_1[16]),
    .q16(bird_up_1[16]), .d17(bird_down_1[17]), .q17(bird_up_1[17]), .d18(bird_down_1[18]),
    .q18(bird_up_1[18]), .d19(bird_down_1[19]), .q19(bird_up_1[19]), .d20(bird_down_1[20]),
    .q20(bird_up_1[20]), .d21(bird_down_1[21]), .q21(bird_up_1[21]), .d22(bird_down_1[22]),
    .q22(bird_up_1[22]), .d23(bird_down_1[23]), .q23(bird_up_1[23]), .d24(bird_down_1[24]),
    .q24(bird_up_1[24]), .d25(bird_down_1[25]), .q25(bird_up_1[25]), .d26(bird_down_1[26]),
    .q26(bird_up_1[26]), .d27(bird_down_1[27]), .q27(bird_up_1[27]), .d28(bird_down_1[28]),
    .q28(bird_up_1[28]), .d29(bird_down_1[29]), .q29(bird_up_1[29]), .d30(bird_down_1[30]),
    .q30(bird_up_1[30]), .d31(bird_down_1[31]), .q31(bird_up_1[31]));  // open: shift, clr
  D_Flip_Flop d_ff_4 (.Q(d_ff_4_q), .preset(_4), .reset(comparator_1_lt));  // open: clk, D, Qn, en
  Multiplexer #(.width(32)) multiplexer_3 (
    .in0(bird_down_1), .in1(bird_up_1), .out(bird_1), .sel(d_ff_4_q));  // open: en
  Multiplexer #(.width(32)) multiplexer_4 (
    .in0(bird_down_2), .in1(bird_up_2), .out(bird_2), .sel(d_ff_4_q));  // open: en
  Multiplexer #(.select(4), .width(32)) multiplexer_5 (
    .in0({32{1'b0}}), .in1({32{1'b0}}), .in2({32{1'b0}}), .in3({32{1'b0}}), .in4({32{1'b0}}),
    .in5(32'h200000), .in6({32{1'b0}}), .in7({32{1'b0}}), .in8({32{1'b0}}), .in9({32{1'b0}}),
    .in10({32{1'b0}}), .in11({32{1'b0}}), .out(_6), .sel(signal_down[3:0]));  // open: in12, in13, in14, in15, en
  or or_3 (or_3_out, _1, _2);
  Shift_Register #(.length(32)) shift_register_3 (
    .in(signal_up[1]), .clk(signal_down[7]), .out(signal_down_2[1]), .load(or_3_out), .d0(reset_2[31]),
    .q0(bird_down_2[31]), .d1(reset_2[30]), .q1(bird_down_2[30]), .d2(reset_2[29]), .q2(bird_down_2[29]),
    .d3(reset_2[28]), .q3(bird_down_2[28]), .d4(reset_2[27]), .q4(bird_down_2[27]), .d5(reset_2[26]),
    .q5(bird_down_2[26]), .d6(reset_2[25]), .q6(bird_down_2[25]), .d7(reset_2[24]), .q7(bird_down_2[24]),
    .d8(reset_2[23]), .q8(bird_down_2[23]), .d9(reset_2[22]), .q9(bird_down_2[22]), .d10(reset_2[21]),
    .q10(bird_down_2[21]), .d11(reset_2[20]), .q11(bird_down_2[20]), .d12(reset_2[19]),
    .q12(bird_down_2[19]), .d13(reset_2[18]), .q13(bird_down_2[18]), .d14(reset_2[17]),
    .q14(bird_down_2[17]), .d15(reset_2[16]), .q15(bird_down_2[16]), .d16(reset_2[15]),
    .q16(bird_down_2[15]), .d17(reset_2[14]), .q17(bird_down_2[14]), .d18(reset_2[13]),
    .q18(bird_down_2[13]), .d19(reset_2[12]), .q19(bird_down_2[12]), .d20(reset_2[11]),
    .q20(bird_down_2[11]), .d21(reset_2[10]), .q21(bird_down_2[10]), .d22(reset_2[9]), .q22(bird_down_2[9]),
    .d23(reset_2[8]), .q23(bird_down_2[8]), .d24(reset_2[7]), .q24(bird_down_2[7]), .d25(reset_2[6]),
    .q25(bird_down_2[6]), .d26(reset_2[5]), .q26(bird_down_2[5]), .d27(reset_2[4]), .q27(bird_down_2[4]),
    .d28(reset_2[3]), .q28(bird_down_2[3]), .d29(reset_2[2]), .q29(bird_down_2[2]), .d30(reset_2[1]),
    .q30(bird_down_2[1]), .d31(reset_2[0]), .q31(bird_down_2[0]));  // open: shift, clr
  Shift_Register #(.length(32)) shift_register_4 (
    .in(signal_down[5]), .clk(signal_down[7]), .out(signal_up_2[5]), .load(_3), .d0(bird_down_2[0]),
    .q0(bird_up_2[0]), .d1(bird_down_2[1]), .q1(bird_up_2[1]), .d2(bird_down_2[2]), .q2(bird_up_2[2]),
    .d3(bird_down_2[3]), .q3(bird_up_2[3]), .d4(bird_down_2[4]), .q4(bird_up_2[4]), .d5(bird_down_2[5]),
    .q5(bird_up_2[5]), .d6(bird_down_2[6]), .q6(bird_up_2[6]), .d7(bird_down_2[7]), .q7(bird_up_2[7]),
    .d8(bird_down_2[8]), .q8(bird_up_2[8]), .d9(bird_down_2[9]), .q9(bird_up_2[9]), .d10(bird_down_2[10]),
    .q10(bird_up_2[10]), .d11(bird_down_2[11]), .q11(bird_up_2[11]), .d12(bird_down_2[12]),
    .q12(bird_up_2[12]), .d13(bird_down_2[13]), .q13(bird_up_2[13]), .d14(bird_down_2[14]),
    .q14(bird_up_2[14]), .d15(bird_down_2[15]), .q15(bird_up_2[15]), .d16(bird_down_2[16]),
    .q16(bird_up_2[16]), .d17(bird_down_2[17]), .q17(bird_up_2[17]), .d18(bird_down_2[18]),
    .q18(bird_up_2[18]), .d19(bird_down_2[19]), .q19(bird_up_2[19]), .d20(bird_down_2[20]),
    .q20(bird_up_2[20]), .d21(bird_down_2[21]), .q21(bird_up_2[21]), .d22(bird_down_2[22]),
    .q22(bird_up_2[22]), .d23(bird_down_2[23]), .q23(bird_up_2[23]), .d24(bird_down_2[24]),
    .q24(bird_up_2[24]), .d25(bird_down_2[25]), .q25(bird_up_2[25]), .d26(bird_down_2[26]),
    .q26(bird_up_2[26]), .d27(bird_down_2[27]), .q27(bird_up_2[27]), .d28(bird_down_2[28]),
    .q28(bird_up_2[28]), .d29(bird_down_2[29]), .q29(bird_up_2[29]), .d30(bird_down_2[30]),
    .q30(bird_up_2[30]), .d31(bird_down_2[31]), .q31(bird_up_2[31]));  // open: shift, clr
  Multiplexer #(.select(4), .width(32)) multiplexer_6 (
    .in0({32{1'b0}}), .in1({32{1'b0}}), .in2({32{1'b0}}), .in3({32{1'b0}}), .in4({32{1'b0}}), .in5(32'h400),
    .in6({32{1'b0}}), .in7({32{1'b0}}), .in8({32{1'b0}}), .in9({32{1'b0}}), .in10({32{1'b0}}),
    .in11({32{1'b0}}), .out(_7), .sel(signal_down[3:0]));  // open: in12, in13, in14, in15, en

  assign signal = {1'b0, signal_down[9:8], 3'b000, signal_down[3:0]};
  assign signal_up_2[9:6] = signal_down[9:6];

  // Other names for the same wires on the sheet: height[3:0] = signal_down[3:0]; pipe_tick = signal_down[8];
  //   tick_down_1 = signal_down[4]; tick_down_2 = signal_down[5]; tick_down_3 = signal_down_2[0];
  //   tick_down_4 = signal_down_2[1]; tick_up_3 = signal_up[0]; tick_up_4 = signal_up[1]; tick_up_1 = signal_up_2[4];
  //   tick_up_2 = signal_up_2[5]; button = signal_down[6]; tick = signal_down[7]
endmodule

module death (
  input  [31:0] bird_1,
  input  [31:0] pipe_1,
  input  [31:0] bird_2,
  input  [31:0] pipe_2,
  input  [31:0] bird_3,
  input  [31:0] pipe_3,
  input  [31:0] bird_4,
  input  [31:0] pipe_4,
  input  [31:0] bird_5,
  input  [31:0] pipe_5,
  output death
);

  wire [31:0] and_1_out, and_2_out, and_3_out, and_4_out, and_5_out, or_1_out;

  Pull_Resistor pull_resistor_1 (.node(bird_1));
  Pull_Resistor pull_resistor_2 (.node(pipe_1));
  Pull_Resistor pull_resistor_3 (.node(bird_2));
  Pull_Resistor pull_resistor_4 (.node(pipe_2));
  Pull_Resistor pull_resistor_5 (.node(bird_3));
  Pull_Resistor pull_resistor_6 (.node(pipe_3));
  Pull_Resistor pull_resistor_7 (.node(bird_4));
  Pull_Resistor pull_resistor_8 (.node(pipe_4));
  Pull_Resistor pull_resistor_9 (.node(bird_5));
  Pull_Resistor pull_resistor_10 (.node(pipe_5));
  assign and_1_out = bird_1 & pipe_1;  // AND_Gate and_1, 32 bits wide
  assign and_2_out = bird_2 & pipe_2;  // AND_Gate and_2, 32 bits wide
  assign and_3_out = bird_3 & pipe_3;  // AND_Gate and_3, 32 bits wide
  assign and_4_out = bird_4 & pipe_4;  // AND_Gate and_4, 32 bits wide
  assign and_5_out = bird_5 & pipe_5;  // AND_Gate and_5, 32 bits wide
  assign or_1_out = and_1_out | and_2_out | and_3_out | and_4_out | and_5_out;  // OR_Gate or_1, 32 bits wide
  or or_2 (death, or_1_out[0], or_1_out[1], or_1_out[2], or_1_out[3], or_1_out[4], or_1_out[5], or_1_out[6], or_1_out[7], or_1_out[8], or_1_out[9], or_1_out[10], or_1_out[11], or_1_out[12], or_1_out[13], or_1_out[14], or_1_out[15], or_1_out[17], or_1_out[18], or_1_out[19], or_1_out[20], or_1_out[21], or_1_out[22], or_1_out[23], or_1_out[24], or_1_out[25], or_1_out[26], or_1_out[27], or_1_out[28], or_1_out[29], or_1_out[30], or_1_out[31], or_1_out[16]);
endmodule

module pipe_height (
  input  [3:0] height,
  input  [17:0] pipe_signal,
  output [31:0] pipe
);

  wire _2, comparator_1_gt, comparator_2_lt;
  wire [1:0] _1;
  wire [4:0] subtractor_1_out;
  wire [31:0] multiplexer_1_out, or_2_out, shifter_1_out, shifter_2_out;

  Comparator #(.width(4), .mode("unsigned")) comparator_1 (
    .a(height), .b(pipe_signal[7:4]), .gt(comparator_1_gt), .eq(_1[1]));  // open: lt
  Comparator #(.width(4), .mode("unsigned")) comparator_2 (
    .a(height), .b(pipe_signal[3:0]), .eq(_1[0]), .lt(comparator_2_lt));  // open: gt
  or or_1 (_2, comparator_1_gt, comparator_2_lt);
  Subtractor #(.width(5)) subtractor_1 (
    .a({5{1'b1}}), .b(pipe_signal[12:8]), .out(subtractor_1_out));  // open: bin, bout
  Multiplexer #(.width(32)) multiplexer_1 (
    .in0({32{1'b0}}), .in1({32{1'b1}}), .out(multiplexer_1_out), .sel(_2));  // open: en
  Shifter #(.width(32), .shift("lr")) shifter_1 (.in({32{1'b1}}), .\dist (subtractor_1_out), .out(shifter_1_out));
  Shifter #(.width(32)) shifter_2 (.in({32{1'b1}}), .\dist (pipe_signal[17:13]), .out(shifter_2_out));
  assign or_2_out = shifter_1_out | shifter_2_out;  // OR_Gate or_2, 32 bits wide
  Multiplexer #(.select(2), .width(32)) multiplexer_2 (
    .in0(multiplexer_1_out), .in1(shifter_1_out), .in2(shifter_2_out), .in3(or_2_out), .out(pipe), .sel(_1));  // open: en

  // Other names for the same wires on the sheet: pipe_down[4:0] = pipe_signal[12:8];
  //   pipe_up[4:0] = pipe_signal[17:13]
endmodule

module pipes___bird (
  input  [31:0] pipe,
  input  [9:0] signal,
  input  [31:0] bird_1,
  input  [31:0] bird_2,
  output [31:0] out_5,
  output [31:0] out_6,
  output [31:0] out_7,
  output [31:0] out_8,
  output [31:0] out_9,
  output [31:0] out_10,
  output [31:0] out_11,
  output [31:0] out_12,
  output [31:0] out_13,
  output [31:0] out_14,
  output [31:0] out_15,
  output [31:0] out_16,
  output [31:0] out_17,
  output [31:0] out_18,
  output [31:0] out_19,
  output [31:0] out_20,
  output [31:0] out_21,
  output [31:0] out_22,
  output [31:0] out_23,
  output [31:0] out_24,
  output [31:0] out_25,
  output [31:0] out_26,
  output [31:0] out_27,
  output [31:0] out_28,
  output [31:0] out_29,
  output [31:0] out_30,
  output [31:0] out_31,
  output [31:0] out_32,
  output [31:0] out_33,
  output [31:0] out_34,
  output [31:0] out_35,
  output [31:0] out_36,
  output [31:0] pipe_2,
  output [9:0] signal_2,
  output [31:0] bird_1_2,
  output [31:0] bird_2_2
);

  wire [31:0] _1, _2, B1, b1_2, b1_3, b1_4, b1_5, b1_6, b1_7, b1_8, b1_9, b1_10, b1_11, b1_12, B2, b2_2,
       b2_3, b2_4, b2_5, b2_6, b2_7, b2_8, b2_9, b2_10, b2_11, b2_12, B3, B4, B5, B6, B7, B8, B10, B11, B12,
       B13, B14, B15, B16, B17, B18, or_3_out, or_4_out, or_5_out, or_7_out, or_8_out, p1, p2, p3, p4, p5,
       pull_resistor_1_node, pull_resistor_2_node, pull_resistor_3_node, pull_resistor_4_node,
       pull_resistor_5_node, pull_resistor_6_node, pull_resistor_7_node, pull_resistor_9_node,
       pull_resistor_10_node, pull_resistor_11_node, pull_resistor_13_node, pull_resistor_14_node,
       pull_resistor_15_node, pull_resistor_17_node, pull_resistor_18_node, pull_resistor_19_node,
       pull_resistor_21_node, pull_resistor_22_node, pull_resistor_23_node, pull_resistor_25_node,
       pull_resistor_26_node, pull_resistor_27_node, pull_resistor_28_node, pull_resistor_29_node,
       pull_resistor_30_node, pull_resistor_31_node, pull_resistor_32_node, register_2_q, register_3_q,
       register_4_q, register_5_q, register_6_q, register_7_q, register_8_q, register_9_q, register_10_q,
       register_11_q, register_12_q, register_13_q, register_14_q, register_15_q, register_16_q,
       register_17_q, register_18_q, register_19_q, register_20_q, register_21_q, register_22_q,
       register_23_q, register_24_q, register_25_q, register_26_q, register_27_q, register_28_q,
       register_29_q, register_30_q, register_31_q, register_32_q, \с1_1 , \с1_2 , \с1_3 , \с1_4 , \с1_5 ,
       \с1_6 , \с1_7 , \с1_8 , \с1_9 , \с1_10 , \с1_11 , \с1_12 , \с1_13 , \с1_14 , \с1_15 , \с1_16 , \с2_1 ,
       \с2_2 , \с2_3 , \с2_4 , \с2_5 , \с2_6 , \с2_7 , \с2_8 , \с2_9 , \с2_10 , \с2_11 , \с2_12 , \с2_13 ,
       \с2_14 , \с2_15 , \с2_16 ;

  assign out_5 = pull_resistor_1_node | _2;  // OR_Gate or_1, 32 bits wide
  Pull_Resistor pull_resistor_1 (.node(pull_resistor_1_node));
  assign pull_resistor_1_node = _1[0] ? pipe_2 : 32'bz;  // Controlled_Buffer controlled_buffer_1
  Register #(.width(32), .trigger("high")) register_1 (.D(register_2_q), .Q(pipe_2), .clk(_1[0]));  // open: en, clr
  Shift_Register #(.length(32)) shift_register_1 (
    .in(signal[8]), .clk(signal[7]), .out(signal_2[8]), .q0(_1[31]), .q1(_1[30]), .q2(_1[29]), .q3(_1[28]),
    .q4(_1[27]), .q5(_1[26]), .q6(_1[25]), .q7(_1[24]), .q8(_1[23]), .q9(_1[22]), .q10(_1[21]), .q11(_1[20]),
    .q12(_1[19]), .q13(_1[18]), .q14(_1[17]), .q15(_1[16]), .q16(_1[15]), .q17(_1[14]), .q18(_1[13]),
    .q19(_1[12]), .q20(_1[11]), .q21(_1[10]), .q22(_1[9]), .q23(_1[8]), .q24(_1[7]), .q25(_1[6]),
    .q26(_1[5]), .q27(_1[4]), .q28(_1[3]), .q29(_1[2]), .q30(_1[1]), .q31(_1[0]));  // open: shift, load, clr, d0, d1, d2, d3, d4, d5, d6, d7, d8, d9, d10, d11, d12, d13, d14, d15, d16, d17, d18, d19, d20, d21, d22, d23, d24, d25, d26, d27, d28, d29, d30, d31
  assign out_6 = pull_resistor_2_node | _2;  // OR_Gate or_2, 32 bits wide
  Pull_Resistor pull_resistor_2 (.node(pull_resistor_2_node));
  assign pull_resistor_2_node = _1[1] ? register_2_q : 32'bz;  // Controlled_Buffer controlled_buffer_2
  Register #(.width(32), .trigger("high")) register_2 (
    .D(register_3_q), .Q(register_2_q), .clk(_1[1]));  // open: en, clr
  assign or_3_out = _2 | p1;  // OR_Gate or_3, 32 bits wide
  Pull_Resistor pull_resistor_3 (.node(pull_resistor_3_node));
  assign pull_resistor_3_node = _1[2] ? register_3_q : 32'bz;  // Controlled_Buffer controlled_buffer_3
  Register #(.width(32), .trigger("high")) register_3 (
    .D(register_4_q), .Q(register_3_q), .clk(_1[2]));  // open: en, clr
  assign or_4_out = _2 | p2;  // OR_Gate or_4, 32 bits wide
  assign or_5_out = _2 | p3;  // OR_Gate or_5, 32 bits wide
  assign out_7 = pull_resistor_3_node | _2;  // OR_Gate or_6, 32 bits wide
  Adder #(.width(3)) adder_1 (.a(signal[6:4]), .b(3'b001), .out(signal_2[6:4]));  // open: cin, cout
  assign or_7_out = _2 | p4;  // OR_Gate or_7, 32 bits wide
  assign or_8_out = _2 | p5;  // OR_Gate or_8, 32 bits wide
  assign out_8 = pull_resistor_4_node | _2;  // OR_Gate or_9, 32 bits wide
  Pull_Resistor pull_resistor_4 (.node(pull_resistor_4_node));
  assign pull_resistor_4_node = _1[3] ? register_4_q : 32'bz;  // Controlled_Buffer controlled_buffer_4
  Register #(.width(32), .trigger("high")) register_4 (
    .D(register_5_q), .Q(register_4_q), .clk(_1[3]));  // open: en, clr
  death death_1 (
    .death(signal_2[9]), .bird_1(B1), .bird_2(B5), .bird_3(B8), .bird_4(B13), .bird_5(B17),
    .pipe_1(or_3_out), .pipe_2(or_4_out), .pipe_3(or_5_out), .pipe_4(or_7_out), .pipe_5(or_8_out));
  assign out_9 = pull_resistor_5_node | _2;  // OR_Gate or_10, 32 bits wide
  Pull_Resistor pull_resistor_5 (.node(pull_resistor_5_node));
  assign pull_resistor_5_node = _1[4] ? register_5_q : 32'bz;  // Controlled_Buffer controlled_buffer_5
  Register #(.width(32), .trigger("high")) register_5 (
    .D(register_6_q), .Q(register_5_q), .clk(_1[4]));  // open: en, clr
  assign out_10 = pull_resistor_6_node | _2;  // OR_Gate or_11, 32 bits wide
  Pull_Resistor pull_resistor_6 (.node(pull_resistor_6_node));
  assign pull_resistor_6_node = _1[5] ? register_6_q : 32'bz;  // Controlled_Buffer controlled_buffer_6
  Register #(.width(32), .trigger("high")) register_6 (
    .D(register_7_q), .Q(register_6_q), .clk(_1[5]));  // open: en, clr
  Pull_Resistor pull_resistor_7 (.node(pull_resistor_7_node));
  assign pull_resistor_7_node = _1[6] ? register_7_q : 32'bz;  // Controlled_Buffer controlled_buffer_7
  Register #(.width(32), .trigger("high")) register_7 (
    .D(register_8_q), .Q(register_7_q), .clk(_1[6]));  // open: en, clr
  assign out_11 = pull_resistor_7_node | _2;  // OR_Gate or_12, 32 bits wide
  assign out_12 = p1 | _2 | B1;  // OR_Gate or_13, 32 bits wide
  Pull_Resistor pull_resistor_8 (.node(p1));
  assign p1 = _1[7] ? register_8_q : 32'bz;  // Controlled_Buffer controlled_buffer_8
  Register #(.width(32), .trigger("high")) register_8 (
    .D(register_9_q), .Q(register_8_q), .clk(_1[7]));  // open: en, clr
  Shifter #(.width(32), .shift("lr")) shifter_1 (.in(bird_1), .\dist (5'b00001), .out(b1_2));
  Shifter #(.width(32), .shift("lr")) shifter_2 (.in(bird_1), .\dist (5'b00010), .out(b1_3));
  Shifter #(.width(32), .shift("lr")) shifter_3 (.in(bird_1), .\dist (5'b00011), .out(b1_4));
  Shifter #(.width(32), .shift("lr")) shifter_4 (.in(bird_1), .\dist (5'b00100), .out(b1_5));
  Shifter #(.width(32), .shift("lr")) shifter_5 (.in(bird_1), .\dist (5'b00101), .out(b1_6));
  Shifter #(.width(32), .shift("lr")) shifter_6 (.in(bird_1), .\dist (5'b00110), .out(b1_7));
  Shifter #(.width(32), .shift("lr")) shifter_7 (.in(bird_1), .\dist (5'b00111), .out(b1_8));
  Shifter #(.width(32), .shift("lr")) shifter_8 (.in(bird_1), .\dist (5'b01000), .out(b1_9));
  Shifter #(.width(32), .shift("lr")) shifter_9 (.in(bird_1), .\dist (5'b01001), .out(b1_10));
  Shifter #(.width(32), .shift("lr")) shifter_10 (.in(bird_1), .\dist (5'b01010), .out(b1_11));
  Shifter #(.width(32), .shift("lr")) shifter_11 (.in(bird_1), .\dist (5'b01011), .out(b1_12));
  assign out_13 = pull_resistor_9_node | _2 | B2;  // OR_Gate or_14, 32 bits wide
  Pull_Resistor pull_resistor_9 (.node(pull_resistor_9_node));
  assign pull_resistor_9_node = _1[8] ? register_9_q : 32'bz;  // Controlled_Buffer controlled_buffer_9
  Register #(.width(32), .trigger("high")) register_9 (
    .D(register_10_q), .Q(register_9_q), .clk(_1[8]));  // open: en, clr
  assign out_14 = pull_resistor_10_node | _2 | B3;  // OR_Gate or_15, 32 bits wide
  Pull_Resistor pull_resistor_10 (.node(pull_resistor_10_node));
  assign pull_resistor_10_node = _1[9] ? register_10_q : 32'bz;  // Controlled_Buffer controlled_buffer_10
  Register #(.width(32), .trigger("high")) register_10 (
    .D(register_11_q), .Q(register_10_q), .clk(_1[9]));  // open: en, clr
  Pull_Resistor pull_resistor_11 (.node(pull_resistor_11_node));
  assign pull_resistor_11_node = _1[10] ? register_11_q : 32'bz;  // Controlled_Buffer controlled_buffer_11
  Register #(.width(32), .trigger("high")) register_11 (
    .D(register_12_q), .Q(register_11_q), .clk(_1[10]));  // open: en, clr
  Multiplexer #(.select(4), .width(32)) multiplexer_1 (
    .in0(32'h3ff), .in1({32{1'b0}}), .in2({32{1'b0}}), .in3({32{1'b0}}), .in4({32{1'b0}}), .in5({32{1'b0}}),
    .in6({32{1'b0}}), .in7({32{1'b0}}), .in8({32{1'b0}}), .in9({32{1'b0}}), .in10({32{1'b0}}),
    .in11({32{1'b0}}), .out(_2), .sel(signal[3:0]));  // open: in12, in13, in14, in15, en
  assign \с1_1  = b1_5 | b1_6 | b1_7;  // OR_Gate or_16, 32 bits wide
  assign \с1_2  = b1_4 | b1_8 | b1_9;  // OR_Gate or_17, 32 bits wide
  assign \с1_3  = b1_4 | b1_8 | b1_10;  // OR_Gate or_18, 32 bits wide
  assign \с1_4  = b1_3 | b1_4 | b1_9 | b1_11;  // OR_Gate or_19, 32 bits wide
  assign \с1_5  = b1_2 | b1_5 | b1_9 | b1_11;  // OR_Gate or_20, 32 bits wide
  assign \с1_6  = b1_2 | b1_5 | b1_8 | b1_12;  // OR_Gate or_21, 32 bits wide
  assign \с1_7  = bird_1 | b1_6 | b1_7 | b1_12;  // OR_Gate or_22, 32 bits wide
  assign \с1_8  = bird_1 | b1_12;  // OR_Gate or_23, 32 bits wide
  assign \с1_9  = bird_1 | b1_5 | b1_6 | b1_12;  // OR_Gate or_24, 32 bits wide
  assign \с1_10  = bird_1 | b1_4 | b1_7 | b1_12;  // OR_Gate or_25, 32 bits wide
  assign \с1_11  = bird_1 | b1_4 | b1_6 | b1_7 | b1_10 | b1_12;  // OR_Gate or_26, 32 bits wide
  assign \с1_12  = b1_2 | b1_5 | b1_6 | b1_9 | b1_11;  // OR_Gate or_27, 32 bits wide
  assign \с1_13  = b1_3 | b1_8 | b1_11;  // OR_Gate or_28, 32 bits wide
  assign \с1_14  = b1_4 | b1_5 | b1_6 | b1_7 | b1_11;  // OR_Gate or_29, 32 bits wide
  assign \с1_15  = b1_8 | b1_11;  // OR_Gate or_30, 32 bits wide
  assign \с1_16  = b1_9 | b1_11;  // OR_Gate or_31, 32 bits wide
  assign out_15 = pull_resistor_11_node | _2 | B4;  // OR_Gate or_32, 32 bits wide
  assign out_16 = p2 | _2 | B5;  // OR_Gate or_33, 32 bits wide
  Pull_Resistor pull_resistor_12 (.node(p2));
  assign p2 = _1[11] ? register_12_q : 32'bz;  // Controlled_Buffer controlled_buffer_12
  Register #(.width(32), .trigger("high")) register_12 (
    .D(register_13_q), .Q(register_12_q), .clk(_1[11]));  // open: en, clr
  assign out_17 = pull_resistor_13_node | _2 | B6;  // OR_Gate or_34, 32 bits wide
  Pull_Resistor pull_resistor_13 (.node(pull_resistor_13_node));
  assign pull_resistor_13_node = _1[12] ? register_13_q : 32'bz;  // Controlled_Buffer controlled_buffer_13
  Register #(.width(32), .trigger("high")) register_13 (
    .D(register_14_q), .Q(register_13_q), .clk(_1[12]));  // open: en, clr
  Shifter #(.width(32)) shifter_12 (.in(bird_2), .\dist (5'b00001), .out(b2_2));
  Shifter #(.width(32)) shifter_13 (.in(bird_2), .\dist (5'b00010), .out(b2_3));
  Shifter #(.width(32)) shifter_14 (.in(bird_2), .\dist (5'b00011), .out(b2_4));
  Shifter #(.width(32)) shifter_15 (.in(bird_2), .\dist (5'b00100), .out(b2_5));
  Shifter #(.width(32)) shifter_16 (.in(bird_2), .\dist (5'b00101), .out(b2_6));
  Shifter #(.width(32)) shifter_17 (.in(bird_2), .\dist (5'b00110), .out(b2_7));
  Shifter #(.width(32)) shifter_18 (.in(bird_2), .\dist (5'b00111), .out(b2_8));
  Shifter #(.width(32)) shifter_19 (.in(bird_2), .\dist (5'b01000), .out(b2_9));
  Shifter #(.width(32)) shifter_20 (.in(bird_2), .\dist (5'b01001), .out(b2_10));
  Shifter #(.width(32)) shifter_21 (.in(bird_2), .\dist (5'b01010), .out(b2_11));
  Shifter #(.width(32)) shifter_22 (.in(bird_2), .\dist (5'b01011), .out(b2_12));
  assign out_18 = pull_resistor_14_node | _2 | B7;  // OR_Gate or_35, 32 bits wide
  Pull_Resistor pull_resistor_14 (.node(pull_resistor_14_node));
  assign pull_resistor_14_node = _1[13] ? register_14_q : 32'bz;  // Controlled_Buffer controlled_buffer_14
  Register #(.width(32), .trigger("high")) register_14 (
    .D(register_15_q), .Q(register_14_q), .clk(_1[13]));  // open: en, clr
  Pull_Resistor pull_resistor_15 (.node(pull_resistor_15_node));
  assign pull_resistor_15_node = _1[14] ? register_15_q : 32'bz;  // Controlled_Buffer controlled_buffer_15
  Register #(.width(32), .trigger("high")) register_15 (
    .D(register_16_q), .Q(register_15_q), .clk(_1[14]));  // open: en, clr
  assign out_19 = pull_resistor_15_node | _2 | B8;  // OR_Gate or_36, 32 bits wide
  assign out_20 = p3 | _2 | B8;  // OR_Gate or_37, 32 bits wide
  Pull_Resistor pull_resistor_16 (.node(p3));
  assign p3 = _1[15] ? register_16_q : 32'bz;  // Controlled_Buffer controlled_buffer_16
  Register #(.width(32), .trigger("high")) register_16 (
    .D(register_17_q), .Q(register_16_q), .clk(_1[15]));  // open: en, clr
  assign \с2_1  = b2_6 | b2_7 | b2_8;  // OR_Gate or_38, 32 bits wide
  assign \с2_2  = b2_4 | b2_5 | b2_9;  // OR_Gate or_39, 32 bits wide
  assign \с2_3  = b2_3 | b2_5 | b2_9;  // OR_Gate or_40, 32 bits wide
  assign \с2_4  = b2_2 | b2_4 | b2_9 | b2_10;  // OR_Gate or_41, 32 bits wide
  assign \с2_5  = b2_2 | b2_4 | b2_8 | b2_11;  // OR_Gate or_42, 32 bits wide
  assign \с2_6  = bird_2 | b2_5 | b2_8 | b2_11;  // OR_Gate or_43, 32 bits wide
  assign \с2_7  = bird_2 | b2_6 | b2_7 | b2_12;  // OR_Gate or_44, 32 bits wide
  assign \с2_8  = bird_2 | b2_12;  // OR_Gate or_45, 32 bits wide
  assign \с2_9  = bird_2 | b2_7 | b2_8 | b2_12;  // OR_Gate or_46, 32 bits wide
  assign \с2_10  = bird_2 | b2_6 | b2_9 | b2_12;  // OR_Gate or_47, 32 bits wide
  assign \с2_11  = bird_2 | b2_3 | b2_6 | b2_7 | b2_9 | b2_12;  // OR_Gate or_48, 32 bits wide
  assign \с2_12  = b2_2 | b2_4 | b2_7 | b2_8 | b2_11;  // OR_Gate or_49, 32 bits wide
  assign \с2_13  = b2_2 | b2_5 | b2_10;  // OR_Gate or_50, 32 bits wide
  assign \с2_14  = b2_2 | b2_6 | b2_7 | b2_8 | b2_9;  // OR_Gate or_51, 32 bits wide
  assign \с2_15  = b2_2 | b2_5;  // OR_Gate or_52, 32 bits wide
  assign \с2_16  = b2_2 | b2_4;  // OR_Gate or_53, 32 bits wide
  assign out_21 = pull_resistor_17_node | _2 | B10;  // OR_Gate or_54, 32 bits wide
  Pull_Resistor pull_resistor_17 (.node(pull_resistor_17_node));
  assign pull_resistor_17_node = _1[16] ? register_17_q : 32'bz;  // Controlled_Buffer controlled_buffer_17
  Register #(.width(32), .trigger("high")) register_17 (
    .D(register_18_q), .Q(register_17_q), .clk(_1[16]));  // open: en, clr
  assign out_22 = pull_resistor_18_node | _2 | B11;  // OR_Gate or_55, 32 bits wide
  Pull_Resistor pull_resistor_18 (.node(pull_resistor_18_node));
  assign pull_resistor_18_node = _1[17] ? register_18_q : 32'bz;  // Controlled_Buffer controlled_buffer_18
  Register #(.width(32), .trigger("high")) register_18 (
    .D(register_19_q), .Q(register_18_q), .clk(_1[17]));  // open: en, clr
  Pull_Resistor pull_resistor_19 (.node(pull_resistor_19_node));
  assign pull_resistor_19_node = _1[18] ? register_19_q : 32'bz;  // Controlled_Buffer controlled_buffer_19
  Register #(.width(32), .trigger("high")) register_19 (
    .D(register_20_q), .Q(register_19_q), .clk(_1[18]));  // open: en, clr
  assign B1 = \с1_1  | \с2_1 ;  // OR_Gate or_56, 32 bits wide
  assign B2 = \с1_2  | \с2_2 ;  // OR_Gate or_57, 32 bits wide
  assign B3 = \с1_3  | \с2_3 ;  // OR_Gate or_58, 32 bits wide
  assign B4 = \с1_4  | \с2_4 ;  // OR_Gate or_59, 32 bits wide
  assign B5 = \с1_5  | \с2_5 ;  // OR_Gate or_60, 32 bits wide
  assign B6 = \с1_6  | \с2_6 ;  // OR_Gate or_61, 32 bits wide
  assign B7 = \с1_7  | \с2_7 ;  // OR_Gate or_62, 32 bits wide
  assign B8 = \с1_8  | \с2_8 ;  // OR_Gate or_63, 32 bits wide
  assign B10 = \с1_9  | \с2_9 ;  // OR_Gate or_64, 32 bits wide
  assign B11 = \с1_10  | \с2_10 ;  // OR_Gate or_65, 32 bits wide
  assign B12 = \с1_11  | \с2_11 ;  // OR_Gate or_66, 32 bits wide
  assign B13 = \с1_12  | \с2_12 ;  // OR_Gate or_67, 32 bits wide
  assign B14 = \с1_13  | \с2_13 ;  // OR_Gate or_68, 32 bits wide
  assign B15 = \с1_14  | \с2_14 ;  // OR_Gate or_69, 32 bits wide
  assign B16 = \с1_15  | \с2_15 ;  // OR_Gate or_70, 32 bits wide
  assign B17 = \с1_16  | \с2_16 ;  // OR_Gate or_71, 32 bits wide
  assign B18 = b1_10 | b2_3;  // OR_Gate or_72, 32 bits wide
  assign out_23 = pull_resistor_19_node | _2 | B12;  // OR_Gate or_73, 32 bits wide
  assign out_24 = p4 | _2 | B13;  // OR_Gate or_74, 32 bits wide
  Pull_Resistor pull_resistor_20 (.node(p4));
  assign p4 = _1[19] ? register_20_q : 32'bz;  // Controlled_Buffer controlled_buffer_20
  Register #(.width(32), .trigger("high")) register_20 (
    .D(register_21_q), .Q(register_20_q), .clk(_1[19]));  // open: en, clr
  assign out_25 = pull_resistor_21_node | _2 | B14;  // OR_Gate or_75, 32 bits wide
  Pull_Resistor pull_resistor_21 (.node(pull_resistor_21_node));
  assign pull_resistor_21_node = _1[20] ? register_21_q : 32'bz;  // Controlled_Buffer controlled_buffer_21
  Register #(.width(32), .trigger("high")) register_21 (
    .D(register_22_q), .Q(register_21_q), .clk(_1[20]));  // open: en, clr
  assign out_26 = pull_resistor_22_node | _2 | B15;  // OR_Gate or_76, 32 bits wide
  Pull_Resistor pull_resistor_22 (.node(pull_resistor_22_node));
  assign pull_resistor_22_node = _1[21] ? register_22_q : 32'bz;  // Controlled_Buffer controlled_buffer_22
  Register #(.width(32), .trigger("high")) register_22 (
    .D(register_23_q), .Q(register_22_q), .clk(_1[21]));  // open: en, clr
  Pull_Resistor pull_resistor_23 (.node(pull_resistor_23_node));
  assign pull_resistor_23_node = _1[22] ? register_23_q : 32'bz;  // Controlled_Buffer controlled_buffer_23
  Register #(.width(32), .trigger("high")) register_23 (
    .D(register_24_q), .Q(register_23_q), .clk(_1[22]));  // open: en, clr
  assign out_27 = pull_resistor_23_node | _2 | B16;  // OR_Gate or_77, 32 bits wide
  assign out_28 = p5 | _2 | B17;  // OR_Gate or_78, 32 bits wide
  Pull_Resistor pull_resistor_24 (.node(p5));
  assign p5 = _1[23] ? register_24_q : 32'bz;  // Controlled_Buffer controlled_buffer_24
  Register #(.width(32), .trigger("high")) register_24 (
    .D(register_25_q), .Q(register_24_q), .clk(_1[23]));  // open: en, clr
  assign out_29 = pull_resistor_25_node | _2 | B18;  // OR_Gate or_79, 32 bits wide
  Pull_Resistor pull_resistor_25 (.node(pull_resistor_25_node));
  assign pull_resistor_25_node = _1[24] ? register_25_q : 32'bz;  // Controlled_Buffer controlled_buffer_25
  Register #(.width(32), .trigger("high")) register_25 (
    .D(register_26_q), .Q(register_25_q), .clk(_1[24]));  // open: en, clr
  assign out_30 = pull_resistor_26_node | _2;  // OR_Gate or_80, 32 bits wide
  Pull_Resistor pull_resistor_26 (.node(pull_resistor_26_node));
  assign pull_resistor_26_node = _1[25] ? register_26_q : 32'bz;  // Controlled_Buffer controlled_buffer_26
  Register #(.width(32), .trigger("high")) register_26 (
    .D(register_27_q), .Q(register_26_q), .clk(_1[25]));  // open: en, clr
  Pull_Resistor pull_resistor_27 (.node(pull_resistor_27_node));
  assign pull_resistor_27_node = _1[26] ? register_27_q : 32'bz;  // Controlled_Buffer controlled_buffer_27
  Register #(.width(32), .trigger("high")) register_27 (
    .D(register_28_q), .Q(register_27_q), .clk(_1[26]));  // open: en, clr
  assign out_31 = pull_resistor_27_node | _2;  // OR_Gate or_81, 32 bits wide
  assign out_32 = pull_resistor_28_node | _2;  // OR_Gate or_82, 32 bits wide
  Pull_Resistor pull_resistor_28 (.node(pull_resistor_28_node));
  assign pull_resistor_28_node = _1[27] ? register_28_q : 32'bz;  // Controlled_Buffer controlled_buffer_28
  Register #(.width(32), .trigger("high")) register_28 (
    .D(register_29_q), .Q(register_28_q), .clk(_1[27]));  // open: en, clr
  assign out_33 = pull_resistor_29_node | _2;  // OR_Gate or_83, 32 bits wide
  Pull_Resistor pull_resistor_29 (.node(pull_resistor_29_node));
  assign pull_resistor_29_node = _1[28] ? register_29_q : 32'bz;  // Controlled_Buffer controlled_buffer_29
  Register #(.width(32), .trigger("high")) register_29 (
    .D(register_30_q), .Q(register_29_q), .clk(_1[28]));  // open: en, clr
  assign out_34 = pull_resistor_30_node | _2;  // OR_Gate or_84, 32 bits wide
  Pull_Resistor pull_resistor_30 (.node(pull_resistor_30_node));
  assign pull_resistor_30_node = _1[29] ? register_30_q : 32'bz;  // Controlled_Buffer controlled_buffer_30
  Register #(.width(32), .trigger("high")) register_30 (
    .D(register_31_q), .Q(register_30_q), .clk(_1[29]));  // open: en, clr
  Pull_Resistor pull_resistor_31 (.node(pull_resistor_31_node));
  assign pull_resistor_31_node = _1[30] ? register_31_q : 32'bz;  // Controlled_Buffer controlled_buffer_31
  Register #(.width(32), .trigger("high")) register_31 (
    .D(register_32_q), .Q(register_31_q), .clk(_1[30]));  // open: en, clr
  assign out_35 = pull_resistor_31_node | _2;  // OR_Gate or_85, 32 bits wide
  assign out_36 = pull_resistor_32_node | _2;  // OR_Gate or_86, 32 bits wide
  Pull_Resistor pull_resistor_32 (.node(pull_resistor_32_node));
  assign pull_resistor_32_node = _1[31] ? register_32_q : 32'bz;  // Controlled_Buffer controlled_buffer_32
  Register #(.width(32), .trigger("high")) register_32 (.D(pipe), .Q(register_32_q), .clk(_1[31]));  // open: en, clr

  assign bird_1_2 = bird_1;
  assign bird_2_2 = bird_2;
  assign {signal_2[7], signal_2[3:0]} = {signal[7], signal[3:0]};

  // Other names for the same wires on the sheet: b1_1[31:0] = bird_1; b2_1[31:0] = bird_2; B9[31:0] = B8
endmodule

module \индикаторы  (
  input  in_1,
  input  in_2,
  output [31:0] out_3,
  output [31:0] out_4,
  output [31:0] out_5,
  output [31:0] out_6,
  output [31:0] out_7,
  output [31:0] out_8,
  output [31:0] out_9,
  output [31:0] out_10,
  output [31:0] out_11,
  output [31:0] out_12,
  output [31:0] out_13,
  output [31:0] out_14,
  output [31:0] out_15,
  output [31:0] out_16,
  output [31:0] out_17,
  output [31:0] out_18,
  output [31:0] out_19,
  output [31:0] out_20,
  output [31:0] out_21,
  output [31:0] out_22,
  output [31:0] out_23,
  output [31:0] out_24,
  output [31:0] out_25,
  output [31:0] out_26,
  output [31:0] out_27,
  output [31:0] out_28,
  output [31:0] out_29,
  output [31:0] out_30,
  output [31:0] out_31,
  output [31:0] out_32,
  output [31:0] out_33,
  output [31:0] out_34,
  output [31:0] out_35,
  output [31:0] out_36,
  output [31:0] out_37,
  output [31:0] out_38,
  output [31:0] out_39,
  output [31:0] out_40,
  output [31:0] out_41,
  output [31:0] out_42,
  output [31:0] out_43,
  output [31:0] out_44,
  output [31:0] out_45,
  output [31:0] out_46,
  output [31:0] out_47,
  output [31:0] out_48,
  output [31:0] out_49,
  output [31:0] out_50,
  output [31:0] out_51,
  output [31:0] out_52,
  output [31:0] out_53,
  output [31:0] out_54,
  output [31:0] out_55,
  output [31:0] out_56,
  output [31:0] out_57,
  output [31:0] out_58,
  output [31:0] out_59,
  output [31:0] out_60,
  output [31:0] out_61,
  output [31:0] out_62,
  output [31:0] out_63,
  output [31:0] out_64,
  output [31:0] out_65,
  output [31:0] out_66,
  output [31:0] out_67,
  output [31:0] out_68,
  output [31:0] out_69,
  output [31:0] out_70,
  output [31:0] out_71,
  output [31:0] out_72,
  output [31:0] out_73,
  output [31:0] out_74,
  output [31:0] out_75,
  output [31:0] out_76,
  output [31:0] out_77,
  output [31:0] out_78,
  output [31:0] out_79,
  output [31:0] out_80,
  output [31:0] out_81,
  output [31:0] out_82,
  output [31:0] out_83,
  output [31:0] out_84,
  output [31:0] out_85,
  output [31:0] out_86,
  output [31:0] out_87,
  output [31:0] out_88,
  output [31:0] out_89,
  output [31:0] out_90,
  output [31:0] out_91,
  output [31:0] out_92,
  output [31:0] out_93,
  output [31:0] out_94,
  output [31:0] out_95,
  output [31:0] out_96,
  output [31:0] out_97,
  output [31:0] out_98,
  output [31:0] out_99,
  output [31:0] out_100,
  output [31:0] out_101,
  output [31:0] out_102,
  output [31:0] out_103,
  output [31:0] out_104,
  output [31:0] out_105,
  output [31:0] out_106,
  output [31:0] out_107,
  output [31:0] out_108,
  output [31:0] out_109,
  output [31:0] out_110,
  output [31:0] out_111,
  output [31:0] out_112,
  output [31:0] out_113,
  output [31:0] out_114,
  output [31:0] out_115,
  output [31:0] out_116,
  output [31:0] out_117,
  output [31:0] out_118,
  output [31:0] out_119,
  output [31:0] out_120,
  output [31:0] out_121,
  output [31:0] out_122
);

  wire [3:0] bcd_1_out_2, bcd_1_out_3, bcd_1_out_4, bcd_2_out_2, bcd_2_out_3, bcd_2_out_4;
  wire [7:0] \cdm_1_рекорд , \cdm_1_счет ;

  cdm cdm_1 (.\вкл (in_1), .plus_1(in_2), .\счет (\cdm_1_счет ), .\рекорд (\cdm_1_рекорд ));
  // Probe on bcd_1_out_2
  // Probe on \cdm_1_счет 
  // Probe on \cdm_1_рекорд 
  bcd bcd_1 (.in_1(\cdm_1_счет ), .out_2(bcd_1_out_2), .out_3(bcd_1_out_3), .out_4(bcd_1_out_4));
  bcd bcd_2 (.in_1(\cdm_1_рекорд ), .out_2(bcd_2_out_2), .out_3(bcd_2_out_3), .out_4(bcd_2_out_4));
  \циферьки  \u_циферьки_1  (
    .in_1(bcd_1_out_2), .out_2(out_3), .out_3(out_4), .out_4(out_5), .out_5(out_6), .out_6(out_7),
    .out_7(out_8), .out_8(out_9), .out_9(out_10), .out_10(out_11), .out_11(out_12), .out_12(out_13),
    .out_13(out_14), .out_14(out_15), .out_15(out_16), .out_16(out_17), .out_17(out_18), .out_18(out_19),
    .out_19(out_20), .out_20(out_21), .out_21(out_22));
  \циферьки  \u_циферьки_2  (
    .in_1(bcd_2_out_2), .out_2(out_63), .out_3(out_64), .out_4(out_65), .out_5(out_66), .out_6(out_67),
    .out_7(out_68), .out_8(out_69), .out_9(out_70), .out_10(out_71), .out_11(out_72), .out_12(out_73),
    .out_13(out_74), .out_14(out_75), .out_15(out_76), .out_16(out_77), .out_17(out_78), .out_18(out_79),
    .out_19(out_80), .out_20(out_81), .out_21(out_82));
  // Probe on bcd_1_out_3
  \циферьки  \u_циферьки_3  (
    .in_1(bcd_2_out_3), .out_2(out_83), .out_3(out_84), .out_4(out_85), .out_5(out_86), .out_6(out_87),
    .out_7(out_88), .out_8(out_89), .out_9(out_90), .out_10(out_91), .out_11(out_92), .out_12(out_93),
    .out_13(out_94), .out_14(out_95), .out_15(out_96), .out_16(out_97), .out_17(out_98), .out_18(out_99),
    .out_19(out_100), .out_20(out_101), .out_21(out_102));
  \циферьки  \u_циферьки_4  (
    .in_1(bcd_1_out_3), .out_2(out_23), .out_3(out_24), .out_4(out_25), .out_5(out_26), .out_6(out_27),
    .out_7(out_28), .out_8(out_29), .out_9(out_30), .out_10(out_31), .out_11(out_32), .out_12(out_33),
    .out_13(out_34), .out_14(out_35), .out_15(out_36), .out_16(out_37), .out_17(out_38), .out_18(out_39),
    .out_19(out_40), .out_20(out_41), .out_21(out_42));
  // Probe on bcd_1_out_4
  \циферьки  \u_циферьки_5  (
    .in_1(bcd_2_out_4), .out_2(out_103), .out_3(out_104), .out_4(out_105), .out_5(out_106), .out_6(out_107),
    .out_7(out_108), .out_8(out_109), .out_9(out_110), .out_10(out_111), .out_11(out_112), .out_12(out_113),
    .out_13(out_114), .out_14(out_115), .out_15(out_116), .out_16(out_117), .out_17(out_118),
    .out_18(out_119), .out_19(out_120), .out_20(out_121), .out_21(out_122));
  \циферьки  \u_циферьки_6  (
    .in_1(bcd_1_out_4), .out_2(out_43), .out_3(out_44), .out_4(out_45), .out_5(out_46), .out_6(out_47),
    .out_7(out_48), .out_8(out_49), .out_9(out_50), .out_10(out_51), .out_11(out_52), .out_12(out_53),
    .out_13(out_54), .out_14(out_55), .out_15(out_56), .out_16(out_57), .out_17(out_58), .out_18(out_59),
    .out_19(out_60), .out_20(out_61), .out_21(out_62));
endmodule

module \циферьки  (
  input  [3:0] in_1,
  output [31:0] out_2,
  output [31:0] out_3,
  output [31:0] out_4,
  output [31:0] out_5,
  output [31:0] out_6,
  output [31:0] out_7,
  output [31:0] out_8,
  output [31:0] out_9,
  output [31:0] out_10,
  output [31:0] out_11,
  output [31:0] out_12,
  output [31:0] out_13,
  output [31:0] out_14,
  output [31:0] out_15,
  output [31:0] out_16,
  output [31:0] out_17,
  output [31:0] out_18,
  output [31:0] out_19,
  output [31:0] out_20,
  output [31:0] out_21
);

  DotMatrix #(.matrixcols(20), .matrixrows(32)) dotmatrix_1 (
    .col0(32'hffffff0), .col1(32'hffffff0), .col2(32'h3000000c), .col3(32'h3000000c), .col4(32'hc0000003),
    .col5(32'hc0000003), .col6(32'hc0ffff03), .col7(32'hc0ffff03), .col8(32'hc30000c3), .col9(32'hc30000c3),
    .col10(32'hc30000c3), .col11(32'hc30000c3), .col12(32'hc0ffff03), .col13(32'hc0ffff03),
    .col14(32'hc0000003), .col15(32'hc0000003), .col16(32'h3000000c), .col17(32'h3000000c),
    .col18(32'hffffff0), .col19(32'hffffff0));
  DotMatrix #(.matrixcols(20), .matrixrows(32)) dotmatrix_2 (
    .col0({32{1'b0}}), .col1({32{1'b0}}), .col2(32'h3f), .col3(32'h3f), .col4(32'hfc000c3),
    .col5(32'hfc000c3), .col6(32'h30ffff03), .col7(32'h30ffff03), .col8(32'hc0000003), .col9(32'hc0000003),
    .col10(32'hc0000003), .col11(32'hc0000003), .col12(32'hffffff03), .col13(32'hffffff03), .col14(32'hc3),
    .col15(32'hc3), .col16(32'h3f), .col17(32'h3f), .col18({32{1'b0}}), .col19({32{1'b0}}));
  DotMatrix #(.matrixcols(20), .matrixrows(32)) dotmatrix_3 (
    .col0(32'hfc000ff), .col1(32'hfc000ff), .col2(32'h30c00303), .col3(32'h30c00303), .col4(32'hc0c00c03),
    .col5(32'hc0c00c03), .col6(32'hc3c03003), .col7(32'hc3c03003), .col8(32'hc300c0c3), .col9(32'hc300c0c3),
    .col10(32'hc30303c3), .col11(32'hc30303c3), .col12(32'hc3fc0cc3), .col13(32'hc3fc0cc3),
    .col14(32'hc00030c3), .col15(32'hc00030c3), .col16(32'h3000c0c3), .col17(32'h3000c0c3),
    .col18(32'hfff00ff), .col19(32'hfff00ff));
  DotMatrix #(.matrixcols(20), .matrixrows(32)) dotmatrix_4 (
    .col0(32'hfc003f0), .col1(32'hfc003f0), .col2(32'h30c0030c), .col3(32'h30c0030c), .col4(32'hc0c00303),
    .col5(32'hc0c00303), .col6(32'hc3c003c3), .col7(32'hc3c003c3), .col8(32'hc303c0c3), .col9(32'hc303c0c3),
    .col10(32'hc30c30c3), .col11(32'hc30c30c3), .col12(32'hc3f00fc3), .col13(32'hc3f00fc3),
    .col14(32'hc0000003), .col15(32'hc0000003), .col16(32'h3003c00c), .col17(32'h3003c00c),
    .col18(32'hffc3ff0), .col19(32'hffc3ff0));
  DotMatrix #(.matrixcols(20), .matrixrows(32)) dotmatrix_5 (
    .col0(32'h3ff000), .col1(32'h3ff000), .col2(32'hc03000), .col3(32'hc03000), .col4(32'h3003000),
    .col5(32'h3003000), .col6(32'hc0c3000), .col7(32'hc0c3000), .col8(32'h303c3000), .col9(32'h303c3000),
    .col10(32'hc0fc3fff), .col11(32'hc0fc3fff), .col12(32'hc0000003), .col13(32'hc0000003),
    .col14(32'hc0000003), .col15(32'hc0000003), .col16(32'hfffc3fff), .col17(32'hfffc3fff),
    .col18(32'hff000), .col19(32'hff000));
  DotMatrix #(.matrixcols(20), .matrixrows(32)) dotmatrix_6 (
    .col0(32'hffffc3f0), .col1(32'hffffc3f0), .col2(32'hc000c30c), .col3(32'hc000c30c), .col4(32'hc000c303),
    .col5(32'hc000c303), .col6(32'hc3f0c3c3), .col7(32'hc3f0c3c3), .col8(32'hc330c0c3), .col9(32'hc330c0c3),
    .col10(32'hc330c0c3), .col11(32'hc330c0c3), .col12(32'hc330ffc3), .col13(32'hc330ffc3),
    .col14(32'hc3300003), .col15(32'hc3300003), .col16(32'hc30c000c), .col17(32'hc30c000c),
    .col18(32'hff03fff0), .col19(32'hff03fff0));
  DotMatrix #(.matrixcols(20), .matrixrows(32)) dotmatrix_7 (
    .col0(32'hffffff0), .col1(32'hffffff0), .col2(32'h3000000c), .col3(32'h3000000c), .col4(32'hc0000003),
    .col5(32'hc0000003), .col6(32'hc3fc3fc3), .col7(32'hc3fc3fc3), .col8(32'hc30c30c3), .col9(32'hc30c30c3),
    .col10(32'hc30c30c3), .col11(32'hc30c30c3), .col12(32'hc3cc3fc3), .col13(32'hc3cc3fc3),
    .col14(32'hc0cc0003), .col15(32'hc0cc0003), .col16(32'h30c3000c), .col17(32'h30c3000c),
    .col18(32'hf00fff0), .col19(32'hf00fff0));
  DotMatrix #(.matrixcols(20), .matrixrows(32)) dotmatrix_8 (
    .col0(32'hff00000f), .col1(32'hff00000f), .col2(32'hc30000f3), .col3(32'hc30000f3), .col4(32'hc3000f03),
    .col5(32'hc3000f03), .col6(32'hc300f00f), .col7(32'hc300f00f), .col8(32'hc30f00f0), .col9(32'hc30f00f0),
    .col10(32'hc3f00f00), .col11(32'hc3f00f00), .col12(32'hc000f000), .col13(32'hc000f000),
    .col14(32'hc00f0000), .col15(32'hc00f0000), .col16(32'hc0f00000), .col17(32'hc0f00000),
    .col18(32'hff000000), .col19(32'hff000000));
  DotMatrix #(.matrixcols(20), .matrixrows(32)) dotmatrix_9 (
    .col0(32'hffc3ff0), .col1(32'hffc3ff0), .col2(32'h3003c00c), .col3(32'h3003c00c), .col4(32'hc0000003),
    .col5(32'hc0000003), .col6(32'hc3f00fc3), .col7(32'hc3f00fc3), .col8(32'hc30c30c3), .col9(32'hc30c30c3),
    .col10(32'hc30c30c3), .col11(32'hc30c30c3), .col12(32'hc3f00fc3), .col13(32'hc3f00fc3),
    .col14(32'hc0000003), .col15(32'hc0000003), .col16(32'h3003c00c), .col17(32'h3003c00c),
    .col18(32'hffc3ff0), .col19(32'hffc3ff0));
  DotMatrix #(.matrixcols(20), .matrixrows(32)) dotmatrix_10 (
    .col0(32'hfff03f0), .col1(32'hfff03f0), .col2(32'h3000c30c), .col3(32'h3000c30c), .col4(32'hc0003303),
    .col5(32'hc0003303), .col6(32'hc3fc30c3), .col7(32'hc3fc30c3), .col8(32'hc30c30c3), .col9(32'hc30c30c3),
    .col10(32'hc30c30c3), .col11(32'hc30c30c3), .col12(32'hc3fc3fc3), .col13(32'hc3fc3fc3),
    .col14(32'hc0000003), .col15(32'hc0000003), .col16(32'h3000000c), .col17(32'h3000000c),
    .col18(32'hffffff0), .col19(32'hffffff0));
  Multiplexer #(.select(4), .width(32)) multiplexer_1 (
    .in0(32'hffffff0), .in1({32{1'b0}}), .in2(32'hfc000ff), .in3(32'hfc003f0), .in4(32'h3ff000),
    .in5(32'hffffc3f0), .in6(32'hffffff0), .in7(32'hff00000f), .in8(32'hffc3ff0), .in9(32'hfff03f0),
    .in10({32{1'b0}}), .in11({32{1'b0}}), .in12({32{1'b0}}), .in13({32{1'b0}}), .in14({32{1'b0}}),
    .in15({32{1'b0}}), .out(out_2), .sel(in_1));  // open: en
  Multiplexer #(.select(4), .width(32)) multiplexer_2 (
    .in0(32'h3000000c), .in1(32'h3f), .in2(32'h30c00303), .in3(32'h30c0030c), .in4(32'hc03000),
    .in5(32'hc000c30c), .in6(32'h3000000c), .in7(32'hc30000f3), .in8(32'h3003c00c), .in9(32'h3000c30c),
    .in11({32{1'b0}}), .in12({32{1'b0}}), .in13({32{1'b0}}), .in14({32{1'b0}}), .in15({32{1'b0}}),
    .out(out_4), .sel(in_1));  // open: in10, en
  Multiplexer #(.select(4), .width(32)) multiplexer_3 (
    .in0(32'hc0000003), .in1(32'hfc000c3), .in2(32'hc0c00c03), .in3(32'hc0c00303), .in4(32'h3003000),
    .in5(32'hc000c303), .in6(32'hc0000003), .in7(32'hc3000f03), .in8(32'hc0000003), .in9(32'hc0003303),
    .in11({32{1'b0}}), .in12({32{1'b0}}), .in13({32{1'b0}}), .in14({32{1'b0}}), .in15({32{1'b0}}),
    .out(out_6), .sel(in_1));  // open: in10, en
  Multiplexer #(.select(4), .width(32)) multiplexer_4 (
    .in0(32'hc0ffff03), .in1(32'h30ffff03), .in2(32'hc3c03003), .in3(32'hc3c003c3), .in4(32'hc0c3000),
    .in5(32'hc3f0c3c3), .in6(32'hc3fc3fc3), .in7(32'hc300f00f), .in8(32'hc3f00fc3), .in9(32'hc3fc30c3),
    .in11({32{1'b0}}), .in12({32{1'b0}}), .in13({32{1'b0}}), .in14({32{1'b0}}), .in15({32{1'b0}}),
    .out(out_8), .sel(in_1));  // open: in10, en
  Multiplexer #(.select(4), .width(32)) multiplexer_5 (
    .in0(32'hc30000c3), .in1(32'hc0000003), .in2(32'hc300c0c3), .in3(32'hc303c0c3), .in4(32'h303c3000),
    .in5(32'hc330c0c3), .in6(32'hc30c30c3), .in7(32'hc30f00f0), .in8(32'hc30c30c3), .in9(32'hc30c30c3),
    .in11({32{1'b0}}), .in12({32{1'b0}}), .in13({32{1'b0}}), .in14({32{1'b0}}), .in15({32{1'b0}}),
    .out(out_10), .sel(in_1));  // open: in10, en
  Multiplexer #(.select(4), .width(32)) multiplexer_6 (
    .in0(32'hc30000c3), .in1(32'hc0000003), .in2(32'hc30303c3), .in3(32'hc30c30c3), .in4(32'hc0fc3fff),
    .in5(32'hc330c0c3), .in6(32'hc30c30c3), .in7(32'hc3f00f00), .in8(32'hc30c30c3), .in9(32'hc30c30c3),
    .in11({32{1'b0}}), .in12({32{1'b0}}), .in13({32{1'b0}}), .in14({32{1'b0}}), .in15({32{1'b0}}),
    .out(out_12), .sel(in_1));  // open: in10, en
  Multiplexer #(.select(4), .width(32)) multiplexer_7 (
    .in0(32'hc0ffff03), .in1(32'hffffff03), .in2(32'hc3fc0cc3), .in3(32'hc3f00fc3), .in4(32'hc0000003),
    .in5(32'hc330ffc3), .in6(32'hc3cc3fc3), .in7(32'hc000f000), .in8(32'hc3f00fc3), .in9(32'hc3fc3fc3),
    .in11({32{1'b0}}), .in12({32{1'b0}}), .in13({32{1'b0}}), .in14({32{1'b0}}), .in15({32{1'b0}}),
    .out(out_14), .sel(in_1));  // open: in10, en
  Multiplexer #(.select(4), .width(32)) multiplexer_8 (
    .in0(32'hc0000003), .in1(32'hc3), .in2(32'hc00030c3), .in3(32'hc0000003), .in4(32'hc0000003),
    .in5(32'hc3300003), .in6(32'hc0cc0003), .in7(32'hc00f0000), .in8(32'hc0000003), .in9(32'hc0000003),
    .in11({32{1'b0}}), .in12({32{1'b0}}), .in13({32{1'b0}}), .in14({32{1'b0}}), .in15({32{1'b0}}),
    .out(out_16), .sel(in_1));  // open: in10, en
  Multiplexer #(.select(4), .width(32)) multiplexer_9 (
    .in0(32'h3000000c), .in1(32'h3f), .in2(32'h3000c0c3), .in3(32'h3003c00c), .in4(32'hfffc3fff),
    .in5(32'hc30c000c), .in6(32'h30c3000c), .in7(32'hc0f00000), .in8(32'h3003c00c), .in9(32'h3000000c),
    .in11({32{1'b0}}), .in12({32{1'b0}}), .in13({32{1'b0}}), .in14({32{1'b0}}), .in15({32{1'b0}}),
    .out(out_18), .sel(in_1));  // open: in10, en
  Multiplexer #(.select(4), .width(32)) multiplexer_10 (
    .in0(32'hffffff0), .in1({32{1'b0}}), .in2(32'hfff00ff), .in3(32'hffc3ff0), .in4(32'hff000),
    .in5(32'hff03fff0), .in6(32'hf00fff0), .in7(32'hff000000), .in8(32'hffc3ff0), .in9(32'hffffff0),
    .in11({32{1'b0}}), .in12({32{1'b0}}), .in13({32{1'b0}}), .in14({32{1'b0}}), .in15({32{1'b0}}),
    .out(out_20), .sel(in_1));  // open: in10, en

  assign out_3 = out_2;
  assign out_5 = out_4;
  assign out_7 = out_6;
  assign out_9 = out_8;
  assign out_11 = out_10;
  assign out_13 = out_12;
  assign out_15 = out_14;
  assign out_17 = out_16;
  assign out_19 = out_18;
  assign out_21 = out_20;
endmodule

module bcd (
  input  [7:0] in_1,
  output [3:0] out_2,
  output [3:0] out_3,
  output [3:0] out_4
);

  wire bcd0_1_u, bcd0_1_v, bcd0_1_w, bcd0_1_x, bcd0_1_y, bcd0_1_z, bcd0_2_y;

  // Probe on in_1
  bcd0 bcd0_1 (
    .a(in_1[7]), .b(in_1[6]), .c(in_1[5]), .d(in_1[4]), .e(in_1[3]), .x(bcd0_1_x), .y(bcd0_1_y),
    .z(bcd0_1_z), .u(bcd0_1_u), .v(bcd0_1_v), .w(bcd0_1_w));
  // Probe on in_1
  bcd0 bcd0_2 (
    .a(bcd0_1_u), .b(bcd0_1_v), .c(bcd0_1_w), .d(in_1[2]), .e(in_1[1]), .y(bcd0_2_y), .z(out_3[0]),
    .u(out_4[3]), .v(out_4[2]), .w(out_4[1]));  // open: x
  bcd0 bcd0_3 (
    .a(1'b0), .b(bcd0_1_x), .c(bcd0_1_y), .d(bcd0_1_z), .e(bcd0_2_y), .y(out_2[1]), .z(out_2[0]),
    .u(out_3[3]), .v(out_3[2]), .w(out_3[1]));  // open: x
  DotMatrix #(.inputtype("row"), .matrixcols(1), .matrixrows(10)) dotmatrix_1 (
    .row0(in_1[0]), .row1(out_4[1]), .row2(out_4[2]), .row3(out_4[3]), .row4(out_3[0]), .row5(out_3[1]),
    .row6(out_3[2]), .row7(out_3[3]), .row8(out_2[0]), .row9(out_2[1]));
  // Probe on {out_4[3:1], in_1[0]}

  assign out_2[3:2] = 2'b00;
  assign out_4[0] = in_1[0];

  // Notes on the sheet:
  //   HEX(16)
  //   DEC(10)
endmodule

module cdm (
  input  \вкл ,
  input  plus_1,
  output [7:0] \счет ,
  output [7:0] \рекорд 
);

  wire and_1_out, and_2_out, and_3_out, and_4_out, and_5_out, and_6_out, and_7_out, cdm_8_mark5_1_data_inst,
       cdm_8_mark5_1_mem_cycle, cl, code, comparator_1_eq, counter_1_carry, data, demultiplexer_2_out1,
       demultiplexer_2_out2, not_1_out, not_2_out, not_3_out, not_4_out, not_5_out, not_6_out, not_7_out,
       not_8_out, or_1_out, or_2_out, or_3_out, or_4_out, or_5_out, or_6_out, rd_wr_prime, res, t_ff_1_q,
       xor_1_out;
  wire [1:0] counter_1_q;
  wire [7:0] adr_rez, cdm_8_mark5_1_addr, cdm_8_mark5_1_data_out, cdm_8_mark5_1_pc, cdm_8_mark5_1_ps,
       cdm_8_mark5_1_r0, cdm_8_mark5_1_r1, cdm_8_mark5_1_r2, cdm_8_mark5_1_r3, cdm_8_mark5_1_sp,
       controlled_buffer_1_out, controlled_buffer_2_out, controlled_buffer_3_out, data_rez,
       demultiplexer_3_out1, demultiplexer_4_out1, rom_1_data;

  Comparator comparator_1 (.a(cdm_8_mark5_1_pc), .b(8'h17), .eq(comparator_1_eq));  // open: gt, lt
  not not_1 (not_1_out, \вкл );
  xor xor_1 (xor_1_out, comparator_1_eq, plus_1);
  // Probe on cdm_8_mark5_1_r0
  or or_1 (or_1_out, comparator_1_eq, not_1_out);
  and and_1 (and_1_out, cl, and_2_out);
  Clock clock_1 (.out(cl));
  and and_2 (and_2_out, \вкл , t_ff_1_q);
  T_Flip_Flop t_ff_1 (.clk(xor_1_out), .T(xor_1_out), .Q(t_ff_1_q));  // open: Qn, preset, reset, en
  // Probe on cdm_8_mark5_1_r2
  // Probe on cdm_8_mark5_1_r3
  // Probe on cdm_8_mark5_1_r1
  // Probe on cdm_8_mark5_1_pc
  or or_2 (or_2_out, comparator_1_eq, counter_1_carry);
  Demultiplexer demultiplexer_1 (.out0(code), .out1(data), .in(1'b1), .sel(or_3_out), .en(1'b1));
  // Probe on cdm_8_mark5_1_sp
  // Probe on cdm_8_mark5_1_ps
  CdM_8_mark5 cdm_8_mark5_1 (
    .clock(and_1_out), .addr(cdm_8_mark5_1_addr), .mem_read(rd_wr_prime),
    .mem_cycle(cdm_8_mark5_1_mem_cycle), .data_inst(cdm_8_mark5_1_data_inst),
    .data_out(cdm_8_mark5_1_data_out), .data_in(controlled_buffer_1_out), .r0(cdm_8_mark5_1_r0),
    .r1(cdm_8_mark5_1_r1), .r2(cdm_8_mark5_1_r2), .r3(cdm_8_mark5_1_r3), .PC(cdm_8_mark5_1_pc),
    .SP(cdm_8_mark5_1_sp), .PS(cdm_8_mark5_1_ps), .Clear(or_1_out));  // open: IAck, IRQ, vec
  T_Flip_Flop t_ff_2 (.clk(or_2_out), .T(or_2_out), .Q(res));  // open: Qn, preset, reset, en
  or or_3 (or_3_out, cdm_8_mark5_1_data_inst, not_2_out);
  not not_2 (not_2_out, cdm_8_mark5_1_mem_cycle);
  not not_3 (not_3_out, rd_wr_prime);
  assign controlled_buffer_1_out = rd_wr_prime ? controlled_buffer_2_out : 8'bz;  // Controlled_Buffer controlled_buffer_1
  or or_4 (or_4_out, res, counter_1_carry);
  and and_3 (and_3_out, or_4_out, cl);
  and and_4 (and_4_out, not_4_out, \вкл );
  assign controlled_buffer_2_out = not_3_out ? cdm_8_mark5_1_data_out : 8'bz;  // Controlled_Buffer controlled_buffer_2
  not not_4 (not_4_out, res);
  Counter #(.width(2), .max('h3), .trigger("falling")) counter_1 (
    .Q(counter_1_q), .carry(counter_1_carry), .clk(and_3_out));  // open: load, D, count, clr
  assign controlled_buffer_3_out = and_4_out ? cdm_8_mark5_1_addr : 8'bz;  // Controlled_Buffer controlled_buffer_3
  assign controlled_buffer_3_out = not_5_out ? 8'h3 : 8'bz;  // Controlled_Buffer controlled_buffer_4
  not not_5 (not_5_out, \вкл );
  assign controlled_buffer_3_out = res ? adr_rez : 8'bz;  // Controlled_Buffer controlled_buffer_5
  Demultiplexer #(.select(2)) demultiplexer_2 (
    .out1(demultiplexer_2_out1), .out2(demultiplexer_2_out2), .in(1'b1), .sel(counter_1_q));  // open: out0, out3, en
  and and_5 (and_5_out, \вкл , code);
  or or_5 (or_5_out, data, and_6_out, res);
  and and_6 (and_6_out, ~data, not_6_out, ~res);  // AND_Gate
  not not_6 (not_6_out, \вкл );
  ROM rom_1 (.addr(controlled_buffer_3_out), .data(rom_1_data), .sel(and_5_out));
  RAM ram_1 (
    .addr(controlled_buffer_3_out), .data(controlled_buffer_2_out), .sel(or_5_out), .clk(cl), .ld(or_6_out));  // open: clr
  or or_6 (or_6_out, and_7_out, res);
  and and_7 (and_7_out, rd_wr_prime, \вкл );
  not not_7 (not_7_out, res);
  Multiplexer #(.width(8)) multiplexer_1 (.in1(8'h3), .out(adr_rez), .sel(demultiplexer_2_out1));  // open: in0, en
  Multiplexer #(.width(8)) multiplexer_2 (.in1(8'h2), .out(adr_rez), .sel(demultiplexer_2_out2));  // open: in0, en
  assign controlled_buffer_2_out = not_7_out ? rom_1_data : 8'bz;  // Controlled_Buffer controlled_buffer_6
  assign data_rez = res ? controlled_buffer_2_out : 8'bz;  // Controlled_Buffer controlled_buffer_7
  assign controlled_buffer_2_out = not_8_out ? {8{1'b0}} : 8'bz;  // Controlled_Buffer controlled_buffer_8
  not not_8 (not_8_out, \вкл );
  Demultiplexer #(.width(8)) demultiplexer_3 (
    .out1(demultiplexer_3_out1), .in(data_rez), .sel(demultiplexer_2_out1));  // open: out0, en
  Demultiplexer #(.width(8)) demultiplexer_4 (
    .out1(demultiplexer_4_out1), .in(data_rez), .sel(demultiplexer_2_out2));  // open: out0, en
  Register #(.trigger("high")) register_1 (
    .D(demultiplexer_3_out1), .Q(\счет ), .clk(demultiplexer_2_out1));  // open: en, clr
  Register #(.trigger("high")) register_2 (
    .D(demultiplexer_4_out1), .Q(\рекорд ), .clk(demultiplexer_2_out2));  // open: en, clr

  // Other names for the same wires on the sheet: _0 = \вкл 

  // Notes on the sheet:
  //   contents of rom_1 (hex, n*v repeats v):
  //   d0 3 b1 d2 4 d3 1 ab 1d d0 0 b1 d0 3 a1 d2 2 bb 7d ea 16 a9 d4
endmodule

module bcd0 (
  input  a,
  input  b,
  input  c,
  input  d,
  input  e,
  output x,
  output y,
  output z,
  output u,
  output v,
  output w
);

  wire and_1_out, and_2_out, and_3_out, and_4_out, and_5_out, and_6_out, and_7_out, and_8_out, and_9_out,
       and_10_out, and_11_out, and_12_out, and_13_out, and_14_out, and_15_out, and_16_out, and_17_out,
       and_18_out, and_19_out, and_20_out, and_21_out, and_22_out, and_23_out, and_24_out, and_25_out,
       and_26_out, and_27_out, and_28_out, and_29_out, and_30_out, and_31_out, and_32_out, and_33_out,
       and_34_out, and_35_out, and_36_out, and_37_out, and_38_out, not_1_out, not_2_out, not_3_out,
       not_4_out, not_5_out, not_6_out, not_7_out, not_8_out, not_9_out, not_10_out, not_11_out, not_12_out,
       not_13_out, not_14_out, not_15_out, not_16_out, not_17_out, not_18_out, not_19_out, not_20_out,
       not_21_out, not_22_out, not_23_out, not_24_out, not_25_out, not_26_out, not_27_out, not_28_out,
       not_29_out, not_30_out, not_31_out, not_32_out, not_33_out, not_34_out, not_35_out, not_36_out,
       not_37_out, not_38_out, not_39_out, not_40_out, not_41_out, not_42_out, not_43_out, not_44_out,
       not_45_out, not_46_out, not_47_out, not_48_out, not_49_out, not_50_out, not_51_out, not_52_out,
       not_53_out, not_54_out, not_55_out, not_56_out, not_57_out, not_58_out, not_59_out, not_60_out,
       not_61_out, not_62_out, not_63_out, not_64_out, not_65_out, not_66_out, not_67_out, not_68_out,
       not_69_out, not_70_out, not_71_out;

  and and_1 (and_1_out, a, c);
  and and_2 (and_2_out, a, b);
  not not_1 (not_1_out, a);
  not not_2 (not_2_out, a);
  not not_3 (not_3_out, b);
  not not_4 (not_4_out, c);
  not not_5 (not_5_out, a);
  not not_6 (not_6_out, b);
  not not_7 (not_7_out, a);
  not not_8 (not_8_out, b);
  not not_9 (not_9_out, a);
  not not_10 (not_10_out, a);
  not not_11 (not_11_out, c);
  not not_12 (not_12_out, d);
  not not_13 (not_13_out, b);
  not not_14 (not_14_out, c);
  not not_15 (not_15_out, c);
  not not_16 (not_16_out, c);
  not not_17 (not_17_out, d);
  not not_18 (not_18_out, a);
  not not_19 (not_19_out, b);
  not not_20 (not_20_out, d);
  not not_21 (not_21_out, e);
  not not_22 (not_22_out, a);
  not not_23 (not_23_out, c);
  not not_24 (not_24_out, d);
  not not_25 (not_25_out, a);
  not not_26 (not_26_out, e);
  not not_27 (not_27_out, b);
  not not_28 (not_28_out, c);
  not not_29 (not_29_out, c);
  not not_30 (not_30_out, d);
  not not_31 (not_31_out, e);
  not not_32 (not_32_out, d);
  not not_33 (not_33_out, b);
  not not_34 (not_34_out, c);
  not not_35 (not_35_out, e);
  not not_36 (not_36_out, a);
  not not_37 (not_37_out, b);
  not not_38 (not_38_out, a);
  not not_39 (not_39_out, d);
  not not_40 (not_40_out, e);
  not not_41 (not_41_out, a);
  not not_42 (not_42_out, d);
  not not_43 (not_43_out, d);
  not not_44 (not_44_out, e);
  not not_45 (not_45_out, b);
  not not_46 (not_46_out, c);
  not not_47 (not_47_out, d);
  not not_48 (not_48_out, b);
  not not_49 (not_49_out, c);
  not not_50 (not_50_out, a);
  not not_51 (not_51_out, b);
  not not_52 (not_52_out, c);
  not not_53 (not_53_out, a);
  not not_54 (not_54_out, c);
  not not_55 (not_55_out, a);
  not not_56 (not_56_out, b);
  not not_57 (not_57_out, e);
  not not_58 (not_58_out, a);
  not not_59 (not_59_out, c);
  not not_60 (not_60_out, d);
  not not_61 (not_61_out, e);
  not not_62 (not_62_out, a);
  not not_63 (not_63_out, d);
  not not_64 (not_64_out, b);
  not not_65 (not_65_out, c);
  not not_66 (not_66_out, e);
  not not_67 (not_67_out, c);
  not not_68 (not_68_out, e);
  not not_69 (not_69_out, b);
  not not_70 (not_70_out, d);
  not not_71 (not_71_out, e);
  or or_1 (x, and_1_out, and_2_out);
  and and_3 (and_3_out, not_1_out, b, d);
  and and_4 (and_4_out, not_2_out, b, c);
  and and_5 (and_5_out, b, c, d);
  and and_6 (and_6_out, a, not_3_out, not_4_out);
  and and_7 (and_7_out, not_5_out, not_6_out, c, e);
  and and_8 (and_8_out, not_7_out, not_8_out, c, d);
  and and_9 (and_9_out, not_9_out, c, d, e);
  and and_10 (and_10_out, not_10_out, b, not_11_out, not_12_out);
  and and_11 (and_11_out, a, not_13_out, not_14_out);
  and and_12 (and_12_out, a, not_15_out, e);
  and and_13 (and_13_out, a, not_16_out, d);
  and and_14 (and_14_out, a, b, c, not_17_out);
  and and_15 (and_15_out, not_18_out, not_19_out, c, not_20_out, not_21_out);
  and and_16 (and_16_out, not_22_out, b, not_23_out, not_24_out, e);
  and and_17 (and_17_out, not_25_out, b, c, d, not_26_out);
  and and_18 (and_18_out, a, not_27_out, not_28_out, d, e);
  and and_19 (and_19_out, a, b, not_29_out, not_30_out, not_31_out);
  and and_20 (and_20_out, a, b, c, not_32_out, e);
  and and_21 (and_21_out, not_33_out, not_34_out, d, not_35_out);
  and and_22 (and_22_out, not_36_out, not_37_out, d, e);
  and and_23 (and_23_out, not_38_out, b, not_39_out, not_40_out);
  and and_24 (and_24_out, not_41_out, b, c, not_42_out);
  and and_25 (and_25_out, b, c, not_43_out, not_44_out);
  and and_26 (and_26_out, a, not_45_out, not_46_out, not_47_out, e);
  and and_27 (and_27_out, a, not_48_out, c, d);
  and and_28 (and_28_out, a, b, not_49_out, d, e);
  and and_29 (and_29_out, not_50_out, not_51_out, not_52_out, e);
  and and_30 (and_30_out, not_53_out, not_54_out, d, e);
  and and_31 (and_31_out, not_55_out, not_56_out, c, d, not_57_out);
  and and_32 (and_32_out, not_58_out, b, not_59_out, not_60_out, not_61_out);
  and and_33 (and_33_out, not_62_out, b, c, not_63_out, e);
  and and_34 (and_34_out, a, not_64_out, not_65_out, not_66_out);
  and and_35 (and_35_out, a, not_67_out, d, not_68_out);
  and and_36 (and_36_out, a, not_69_out, c, e);
  and and_37 (and_37_out, a, c, d, e);
  and and_38 (and_38_out, a, b, c, not_70_out, not_71_out);
  or or_2 (y, and_3_out, and_4_out, and_5_out, and_6_out);
  or or_3 (z, and_7_out, and_8_out, and_9_out, and_10_out, and_11_out, and_12_out, and_13_out, and_14_out);
  or or_4 (u, and_15_out, and_16_out, and_17_out, and_18_out, and_19_out, and_20_out);
  or or_5 (v, and_21_out, and_22_out, and_23_out, and_24_out, and_25_out, and_26_out, and_27_out, and_28_out);
  or or_6 (w, and_29_out, and_30_out, and_31_out, and_32_out, and_33_out, and_34_out, and_35_out, and_36_out, and_37_out, and_38_out);
endmodule

module \проверка  (
  input  in_1,
  input  in_2
);

  wire [31:0] \индикаторы_1_out_3 , \индикаторы_1_out_4 , \индикаторы_1_out_5 , \индикаторы_1_out_6 ,
       \индикаторы_1_out_7 , \индикаторы_1_out_8 , \индикаторы_1_out_9 , \индикаторы_1_out_10 ,
       \индикаторы_1_out_11 , \индикаторы_1_out_12 , \индикаторы_1_out_13 , \индикаторы_1_out_14 ,
       \индикаторы_1_out_15 , \индикаторы_1_out_16 , \индикаторы_1_out_17 , \индикаторы_1_out_18 ,
       \индикаторы_1_out_19 , \индикаторы_1_out_20 , \индикаторы_1_out_21 , \индикаторы_1_out_22 ,
       \индикаторы_1_out_23 , \индикаторы_1_out_24 , \индикаторы_1_out_25 , \индикаторы_1_out_26 ,
       \индикаторы_1_out_27 , \индикаторы_1_out_28 , \индикаторы_1_out_29 , \индикаторы_1_out_30 ,
       \индикаторы_1_out_31 , \индикаторы_1_out_32 , \индикаторы_1_out_33 , \индикаторы_1_out_34 ,
       \индикаторы_1_out_35 , \индикаторы_1_out_36 , \индикаторы_1_out_37 , \индикаторы_1_out_38 ,
       \индикаторы_1_out_39 , \индикаторы_1_out_40 , \индикаторы_1_out_41 , \индикаторы_1_out_42 ,
       \индикаторы_1_out_43 , \индикаторы_1_out_44 , \индикаторы_1_out_45 , \индикаторы_1_out_46 ,
       \индикаторы_1_out_47 , \индикаторы_1_out_48 , \индикаторы_1_out_49 , \индикаторы_1_out_50 ,
       \индикаторы_1_out_51 , \индикаторы_1_out_52 , \индикаторы_1_out_53 , \индикаторы_1_out_54 ,
       \индикаторы_1_out_55 , \индикаторы_1_out_56 , \индикаторы_1_out_57 , \индикаторы_1_out_58 ,
       \индикаторы_1_out_59 , \индикаторы_1_out_60 , \индикаторы_1_out_61 , \индикаторы_1_out_62 ,
       \индикаторы_1_out_63 , \индикаторы_1_out_64 , \индикаторы_1_out_65 , \индикаторы_1_out_66 ,
       \индикаторы_1_out_67 , \индикаторы_1_out_68 , \индикаторы_1_out_69 , \индикаторы_1_out_70 ,
       \индикаторы_1_out_71 , \индикаторы_1_out_72 , \индикаторы_1_out_73 , \индикаторы_1_out_74 ,
       \индикаторы_1_out_75 , \индикаторы_1_out_76 , \индикаторы_1_out_77 , \индикаторы_1_out_78 ,
       \индикаторы_1_out_79 , \индикаторы_1_out_80 , \индикаторы_1_out_81 , \индикаторы_1_out_82 ,
       \индикаторы_1_out_83 , \индикаторы_1_out_84 , \индикаторы_1_out_85 , \индикаторы_1_out_86 ,
       \индикаторы_1_out_87 , \индикаторы_1_out_88 , \индикаторы_1_out_89 , \индикаторы_1_out_90 ,
       \индикаторы_1_out_91 , \индикаторы_1_out_92 , \индикаторы_1_out_93 , \индикаторы_1_out_94 ,
       \индикаторы_1_out_95 , \индикаторы_1_out_96 , \индикаторы_1_out_97 , \индикаторы_1_out_98 ,
       \индикаторы_1_out_99 , \индикаторы_1_out_100 , \индикаторы_1_out_101 , \индикаторы_1_out_102 ,
       \индикаторы_1_out_103 , \индикаторы_1_out_104 , \индикаторы_1_out_105 , \индикаторы_1_out_106 ,
       \индикаторы_1_out_107 , \индикаторы_1_out_108 , \индикаторы_1_out_109 , \индикаторы_1_out_110 ,
       \индикаторы_1_out_111 , \индикаторы_1_out_112 , \индикаторы_1_out_113 , \индикаторы_1_out_114 ,
       \индикаторы_1_out_115 , \индикаторы_1_out_116 , \индикаторы_1_out_117 , \индикаторы_1_out_118 ,
       \индикаторы_1_out_119 , \индикаторы_1_out_120 , \индикаторы_1_out_121 , \индикаторы_1_out_122 ;

  \индикаторы  \u_индикаторы_1  (
    .in_1(in_1), .in_2(in_2), .out_3(\индикаторы_1_out_3 ), .out_4(\индикаторы_1_out_4 ),
    .out_5(\индикаторы_1_out_5 ), .out_6(\индикаторы_1_out_6 ), .out_7(\индикаторы_1_out_7 ),
    .out_8(\индикаторы_1_out_8 ), .out_9(\индикаторы_1_out_9 ), .out_10(\индикаторы_1_out_10 ),
    .out_11(\индикаторы_1_out_11 ), .out_12(\индикаторы_1_out_12 ), .out_13(\индикаторы_1_out_13 ),
    .out_14(\индикаторы_1_out_14 ), .out_15(\индикаторы_1_out_15 ), .out_16(\индикаторы_1_out_16 ),
    .out_17(\индикаторы_1_out_17 ), .out_18(\индикаторы_1_out_18 ), .out_19(\индикаторы_1_out_19 ),
    .out_20(\индикаторы_1_out_20 ), .out_21(\индикаторы_1_out_21 ), .out_22(\индикаторы_1_out_22 ),
    .out_23(\индикаторы_1_out_23 ), .out_24(\индикаторы_1_out_24 ), .out_25(\индикаторы_1_out_25 ),
    .out_26(\индикаторы_1_out_26 ), .out_27(\индикаторы_1_out_27 ), .out_28(\индикаторы_1_out_28 ),
    .out_29(\индикаторы_1_out_29 ), .out_30(\индикаторы_1_out_30 ), .out_31(\индикаторы_1_out_31 ),
    .out_32(\индикаторы_1_out_32 ), .out_33(\индикаторы_1_out_33 ), .out_34(\индикаторы_1_out_34 ),
    .out_35(\индикаторы_1_out_35 ), .out_36(\индикаторы_1_out_36 ), .out_37(\индикаторы_1_out_37 ),
    .out_38(\индикаторы_1_out_38 ), .out_39(\индикаторы_1_out_39 ), .out_40(\индикаторы_1_out_40 ),
    .out_41(\индикаторы_1_out_41 ), .out_42(\индикаторы_1_out_42 ), .out_43(\индикаторы_1_out_43 ),
    .out_44(\индикаторы_1_out_44 ), .out_45(\индикаторы_1_out_45 ), .out_46(\индикаторы_1_out_46 ),
    .out_47(\индикаторы_1_out_47 ), .out_48(\индикаторы_1_out_48 ), .out_49(\индикаторы_1_out_49 ),
    .out_50(\индикаторы_1_out_50 ), .out_51(\индикаторы_1_out_51 ), .out_52(\индикаторы_1_out_52 ),
    .out_53(\индикаторы_1_out_53 ), .out_54(\индикаторы_1_out_54 ), .out_55(\индикаторы_1_out_55 ),
    .out_56(\индикаторы_1_out_56 ), .out_57(\индикаторы_1_out_57 ), .out_58(\индикаторы_1_out_58 ),
    .out_59(\индикаторы_1_out_59 ), .out_60(\индикаторы_1_out_60 ), .out_61(\индикаторы_1_out_61 ),
    .out_62(\индикаторы_1_out_62 ), .out_63(\индикаторы_1_out_63 ), .out_64(\индикаторы_1_out_64 ),
    .out_65(\индикаторы_1_out_65 ), .out_66(\индикаторы_1_out_66 ), .out_67(\индикаторы_1_out_67 ),
    .out_68(\индикаторы_1_out_68 ), .out_69(\индикаторы_1_out_69 ), .out_70(\индикаторы_1_out_70 ),
    .out_71(\индикаторы_1_out_71 ), .out_72(\индикаторы_1_out_72 ), .out_73(\индикаторы_1_out_73 ),
    .out_74(\индикаторы_1_out_74 ), .out_75(\индикаторы_1_out_75 ), .out_76(\индикаторы_1_out_76 ),
    .out_77(\индикаторы_1_out_77 ), .out_78(\индикаторы_1_out_78 ), .out_79(\индикаторы_1_out_79 ),
    .out_80(\индикаторы_1_out_80 ), .out_81(\индикаторы_1_out_81 ), .out_82(\индикаторы_1_out_82 ),
    .out_83(\индикаторы_1_out_83 ), .out_84(\индикаторы_1_out_84 ), .out_85(\индикаторы_1_out_85 ),
    .out_86(\индикаторы_1_out_86 ), .out_87(\индикаторы_1_out_87 ), .out_88(\индикаторы_1_out_88 ),
    .out_89(\индикаторы_1_out_89 ), .out_90(\индикаторы_1_out_90 ), .out_91(\индикаторы_1_out_91 ),
    .out_92(\индикаторы_1_out_92 ), .out_93(\индикаторы_1_out_93 ), .out_94(\индикаторы_1_out_94 ),
    .out_95(\индикаторы_1_out_95 ), .out_96(\индикаторы_1_out_96 ), .out_97(\индикаторы_1_out_97 ),
    .out_98(\индикаторы_1_out_98 ), .out_99(\индикаторы_1_out_99 ), .out_100(\индикаторы_1_out_100 ),
    .out_101(\индикаторы_1_out_101 ), .out_102(\индикаторы_1_out_102 ), .out_103(\индикаторы_1_out_103 ),
    .out_104(\индикаторы_1_out_104 ), .out_105(\индикаторы_1_out_105 ), .out_106(\индикаторы_1_out_106 ),
    .out_107(\индикаторы_1_out_107 ), .out_108(\индикаторы_1_out_108 ), .out_109(\индикаторы_1_out_109 ),
    .out_110(\индикаторы_1_out_110 ), .out_111(\индикаторы_1_out_111 ), .out_112(\индикаторы_1_out_112 ),
    .out_113(\индикаторы_1_out_113 ), .out_114(\индикаторы_1_out_114 ), .out_115(\индикаторы_1_out_115 ),
    .out_116(\индикаторы_1_out_116 ), .out_117(\индикаторы_1_out_117 ), .out_118(\индикаторы_1_out_118 ),
    .out_119(\индикаторы_1_out_119 ), .out_120(\индикаторы_1_out_120 ), .out_121(\индикаторы_1_out_121 ),
    .out_122(\индикаторы_1_out_122 ));
  DotMatrix #(.matrixcols(20), .matrixrows(32)) dotmatrix_1 (
    .col0(\индикаторы_1_out_3 ), .col1(\индикаторы_1_out_4 ), .col2(\индикаторы_1_out_5 ),
    .col3(\индикаторы_1_out_6 ), .col4(\индикаторы_1_out_7 ), .col5(\индикаторы_1_out_8 ),
    .col6(\индикаторы_1_out_9 ), .col7(\индикаторы_1_out_10 ), .col8(\индикаторы_1_out_11 ),
    .col9(\индикаторы_1_out_12 ), .col10(\индикаторы_1_out_13 ), .col11(\индикаторы_1_out_14 ),
    .col12(\индикаторы_1_out_15 ), .col13(\индикаторы_1_out_16 ), .col14(\индикаторы_1_out_17 ),
    .col15(\индикаторы_1_out_18 ), .col16(\индикаторы_1_out_19 ), .col17(\индикаторы_1_out_20 ),
    .col18(\индикаторы_1_out_21 ), .col19(\индикаторы_1_out_22 ));
  DotMatrix #(.matrixcols(20), .matrixrows(32)) dotmatrix_2 (
    .col0(\индикаторы_1_out_63 ), .col1(\индикаторы_1_out_64 ), .col2(\индикаторы_1_out_65 ),
    .col3(\индикаторы_1_out_66 ), .col4(\индикаторы_1_out_67 ), .col5(\индикаторы_1_out_68 ),
    .col6(\индикаторы_1_out_69 ), .col7(\индикаторы_1_out_70 ), .col8(\индикаторы_1_out_71 ),
    .col9(\индикаторы_1_out_72 ), .col10(\индикаторы_1_out_73 ), .col11(\индикаторы_1_out_74 ),
    .col12(\индикаторы_1_out_75 ), .col13(\индикаторы_1_out_76 ), .col14(\индикаторы_1_out_77 ),
    .col15(\индикаторы_1_out_78 ), .col16(\индикаторы_1_out_79 ), .col17(\индикаторы_1_out_80 ),
    .col18(\индикаторы_1_out_81 ), .col19(\индикаторы_1_out_82 ));
  DotMatrix #(.matrixcols(20), .matrixrows(32)) dotmatrix_3 (
    .col0(\индикаторы_1_out_23 ), .col1(\индикаторы_1_out_24 ), .col2(\индикаторы_1_out_25 ),
    .col3(\индикаторы_1_out_26 ), .col4(\индикаторы_1_out_27 ), .col5(\индикаторы_1_out_28 ),
    .col6(\индикаторы_1_out_29 ), .col7(\индикаторы_1_out_30 ), .col8(\индикаторы_1_out_31 ),
    .col9(\индикаторы_1_out_32 ), .col10(\индикаторы_1_out_33 ), .col11(\индикаторы_1_out_34 ),
    .col12(\индикаторы_1_out_35 ), .col13(\индикаторы_1_out_36 ), .col14(\индикаторы_1_out_37 ),
    .col15(\индикаторы_1_out_38 ), .col16(\индикаторы_1_out_39 ), .col17(\индикаторы_1_out_40 ),
    .col18(\индикаторы_1_out_41 ), .col19(\индикаторы_1_out_42 ));
  DotMatrix #(.matrixcols(20), .matrixrows(32)) dotmatrix_4 (
    .col0(\индикаторы_1_out_83 ), .col1(\индикаторы_1_out_84 ), .col2(\индикаторы_1_out_85 ),
    .col3(\индикаторы_1_out_86 ), .col4(\индикаторы_1_out_87 ), .col5(\индикаторы_1_out_88 ),
    .col6(\индикаторы_1_out_89 ), .col7(\индикаторы_1_out_90 ), .col8(\индикаторы_1_out_91 ),
    .col9(\индикаторы_1_out_92 ), .col10(\индикаторы_1_out_93 ), .col11(\индикаторы_1_out_94 ),
    .col12(\индикаторы_1_out_95 ), .col13(\индикаторы_1_out_96 ), .col14(\индикаторы_1_out_97 ),
    .col15(\индикаторы_1_out_98 ), .col16(\индикаторы_1_out_99 ), .col17(\индикаторы_1_out_100 ),
    .col18(\индикаторы_1_out_101 ), .col19(\индикаторы_1_out_102 ));
  DotMatrix #(.matrixcols(20), .matrixrows(32)) dotmatrix_5 (
    .col0(\индикаторы_1_out_43 ), .col1(\индикаторы_1_out_44 ), .col2(\индикаторы_1_out_45 ),
    .col3(\индикаторы_1_out_46 ), .col4(\индикаторы_1_out_47 ), .col5(\индикаторы_1_out_48 ),
    .col6(\индикаторы_1_out_49 ), .col7(\индикаторы_1_out_50 ), .col8(\индикаторы_1_out_51 ),
    .col9(\индикаторы_1_out_52 ), .col10(\индикаторы_1_out_53 ), .col11(\индикаторы_1_out_54 ),
    .col12(\индикаторы_1_out_55 ), .col13(\индикаторы_1_out_56 ), .col14(\индикаторы_1_out_57 ),
    .col15(\индикаторы_1_out_58 ), .col16(\индикаторы_1_out_59 ), .col17(\индикаторы_1_out_60 ),
    .col18(\индикаторы_1_out_61 ), .col19(\индикаторы_1_out_62 ));
  DotMatrix #(.matrixcols(20), .matrixrows(32)) dotmatrix_6 (
    .col0(\индикаторы_1_out_103 ), .col1(\индикаторы_1_out_104 ), .col2(\индикаторы_1_out_105 ),
    .col3(\индикаторы_1_out_106 ), .col4(\индикаторы_1_out_107 ), .col5(\индикаторы_1_out_108 ),
    .col6(\индикаторы_1_out_109 ), .col7(\индикаторы_1_out_110 ), .col8(\индикаторы_1_out_111 ),
    .col9(\индикаторы_1_out_112 ), .col10(\индикаторы_1_out_113 ), .col11(\индикаторы_1_out_114 ),
    .col12(\индикаторы_1_out_115 ), .col13(\индикаторы_1_out_116 ), .col14(\индикаторы_1_out_117 ),
    .col15(\индикаторы_1_out_118 ), .col16(\индикаторы_1_out_119 ), .col17(\индикаторы_1_out_120 ),
    .col18(\индикаторы_1_out_121 ), .col19(\индикаторы_1_out_122 ));
endmodule
