// Logisim project chernovoy_variant2.circ as structural Verilog: 6 circuits, main circuit main
module main (
);

  wire button_1_out, vcyo_1_bus_0;
  wire [31:0] pipes_1_out_2, pipes_1_out_3, pipes_1_out_4, pipes_1_out_5, pipes_1_out_6, pipes_1_out_7,
       pipes_1_out_8, pipes_1_out_9, pipes_1_out_10, pipes_1_out_11, pipes_1_out_12, pipes_1_out_13,
       pipes_1_out_14, pipes_1_out_15, pipes_1_out_16, pipes_1_out_17, pipes_1_out_18, pipes_1_out_19,
       pipes_1_out_20, pipes_1_out_21, pipes_1_out_22, pipes_1_out_23, pipes_1_out_24, pipes_1_out_25,
       pipes_1_out_26, pipes_1_out_27, pipes_1_out_28, pipes_1_out_29, pipes_1_out_30, pipes_1_out_31,
       pipes_1_out_32, pipes_1_out_33, vcyo_1_out_2, vcyo_1_out_3, vcyo_1_out_4, vcyo_1_out_5, vcyo_1_out_6,
       vcyo_1_out_7, vcyo_1_out_8, vcyo_1_out_9, vcyo_1_out_10, vcyo_1_out_11, vcyo_1_out_12, vcyo_1_out_13,
       vcyo_1_out_14, vcyo_1_out_15, vcyo_1_out_16, vcyo_1_out_17, vcyo_1_out_18, vcyo_1_out_19,
       vcyo_1_out_20, vcyo_1_out_21, vcyo_1_out_22, vcyo_1_out_23, vcyo_1_out_24, vcyo_1_out_25,
       vcyo_1_out_26, vcyo_1_out_27, vcyo_1_out_28, vcyo_1_out_29, vcyo_1_out_30, vcyo_1_out_31,
       vcyo_1_out_32, vcyo_1_out_33, vcyo_1_out_34;

  Button button_1 (.out(button_1_out));
  DotMatrix #(.matrixcols(32), .matrixrows(32)) dotmatrix_1 (
    .col0(vcyo_1_out_2), .col1(vcyo_1_out_17), .col2(vcyo_1_out_5), .col3(vcyo_1_out_15),
    .col4(vcyo_1_out_3), .col5(vcyo_1_out_14), .col6(vcyo_1_out_12), .col7(vcyo_1_out_10),
    .col8(vcyo_1_out_9), .col9(vcyo_1_out_8), .col10(vcyo_1_out_6), .col11(vcyo_1_out_7),
    .col12(vcyo_1_out_16), .col13(vcyo_1_out_24), .col14(vcyo_1_out_4), .col15(vcyo_1_out_19),
    .col16(vcyo_1_out_22), .col17(vcyo_1_out_26), .col18(vcyo_1_out_27), .col19(vcyo_1_out_28),
    .col20(vcyo_1_out_20), .col21(vcyo_1_out_29), .col22(vcyo_1_out_21), .col23(vcyo_1_out_31),
    .col24(vcyo_1_out_25), .col25(vcyo_1_out_32), .col26(vcyo_1_out_11), .col27(vcyo_1_out_23),
    .col28(vcyo_1_out_30), .col29(vcyo_1_out_13), .col30(vcyo_1_out_18), .col31(vcyo_1_out_33));
  vcyo vcyo_1 (
    .\Кнопка (button_1_out), .out_34(vcyo_1_out_34), .out_2(vcyo_1_out_2), .out_17(vcyo_1_out_17),
    .out_5(vcyo_1_out_5), .out_15(vcyo_1_out_15), .out_3(vcyo_1_out_3), .out_14(vcyo_1_out_14),
    .out_12(vcyo_1_out_12), .out_10(vcyo_1_out_10), .out_9(vcyo_1_out_9), .out_8(vcyo_1_out_8),
    .out_6(vcyo_1_out_6), .out_7(vcyo_1_out_7), .out_16(vcyo_1_out_16), .out_24(vcyo_1_out_24),
    .out_4(vcyo_1_out_4), .out_19(vcyo_1_out_19), .out_22(vcyo_1_out_22), .out_26(vcyo_1_out_26),
    .out_27(vcyo_1_out_27), .out_28(vcyo_1_out_28), .out_20(vcyo_1_out_20), .out_29(vcyo_1_out_29),
    .out_21(vcyo_1_out_21), .out_31(vcyo_1_out_31), .out_25(vcyo_1_out_25), .out_32(vcyo_1_out_32),
    .out_11(vcyo_1_out_11), .out_23(vcyo_1_out_23), .out_30(vcyo_1_out_30), .out_13(vcyo_1_out_13),
    .out_18(vcyo_1_out_18), .out_33(vcyo_1_out_33), .bus_0(vcyo_1_bus_0));
  // DotMatrix #(.inputtype("select"), .matrixcols(32), .matrixrows(32)) dotmatrix_2: pin names not known; wires that end beside it: 32'h40, vcyo_1_out_34
  DotMatrix #(.matrixcols(32), .matrixrows(32)) dotmatrix_3 (
    .col0(pipes_1_out_2), .col1(pipes_1_out_3), .col2(pipes_1_out_4), .col3(pipes_1_out_5),
    .col4(pipes_1_out_6), .col5(pipes_1_out_7), .col6(pipes_1_out_8), .col7(pipes_1_out_9),
    .col8(pipes_1_out_10), .col9(pipes_1_out_11), .col10(pipes_1_out_12), .col11(pipes_1_out_13),
    .col12(pipes_1_out_14), .col13(pipes_1_out_15), .col14(pipes_1_out_16), .col15(pipes_1_out_17),
    .col16(pipes_1_out_18), .col17(pipes_1_out_19), .col18(pipes_1_out_20), .col19(pipes_1_out_21),
    .col20(pipes_1_out_22), .col21(pipes_1_out_23), .col22(pipes_1_out_24), .col23(pipes_1_out_25),
    .col24(pipes_1_out_26), .col25(pipes_1_out_27), .col26(pipes_1_out_28), .col27(pipes_1_out_29),
    .col28(pipes_1_out_30), .col29(pipes_1_out_31), .col30(pipes_1_out_32), .col31(pipes_1_out_33));
  pipes pipes_1 (
    .out_2(pipes_1_out_2), .out_3(pipes_1_out_3), .out_4(pipes_1_out_4), .out_5(pipes_1_out_5),
    .out_6(pipes_1_out_6), .out_7(pipes_1_out_7), .out_8(pipes_1_out_8), .out_9(pipes_1_out_9),
    .out_10(pipes_1_out_10), .out_11(pipes_1_out_11), .out_12(pipes_1_out_12), .out_13(pipes_1_out_13),
    .out_14(pipes_1_out_14), .out_15(pipes_1_out_15), .out_16(pipes_1_out_16), .out_17(pipes_1_out_17),
    .out_18(pipes_1_out_18), .out_19(pipes_1_out_19), .out_20(pipes_1_out_20), .out_21(pipes_1_out_21),
    .out_22(pipes_1_out_22), .out_23(pipes_1_out_23), .out_24(pipes_1_out_24), .out_25(pipes_1_out_25),
    .out_26(pipes_1_out_26), .out_27(pipes_1_out_27), .out_28(pipes_1_out_28), .out_29(pipes_1_out_29),
    .out_30(pipes_1_out_30), .out_31(pipes_1_out_31), .out_32(pipes_1_out_32), .out_33(pipes_1_out_33),
    .bus_0(vcyo_1_bus_0));
endmodule

module pipes (
  input  bus_0,
  output [31:0] out_2,
  output [31:0] out_3,
  output [31:0] out_4,
  output [31:0] out_5,
  output [31:0] out_6,
  output [31:0] out_7,
  output [31:0] out_8,
  output [31:0] out_9,
  output [31:0] out_10,
  output [31:0] out_11,
  output [31:0] out_12,
  output [31:0] out_13,
  output [31:0] out_14,
  output [31:0] out_15,
  output [31:0] out_16,
  output [31:0] out_17,
  output [31:0] out_18,
  output [31:0] out_19,
  output [31:0] out_20,
  output [31:0] out_21,
  output [31:0] out_22,
  output [31:0] out_23,
  output [31:0] out_24,
  output [31:0] out_25,
  output [31:0] out_26,
  output [31:0] out_27,
  output [31:0] out_28,
  output [31:0] out_29,
  output [31:0] out_30,
  output [31:0] out_31,
  output [31:0] out_32,
  output [31:0] out_33
);

  wire _0, _3, comparator_1_eq, d_ff_1_qn, decoder_1_out0, decoder_1_out1;
  wire [3:0] counter_2_q;
  wire [31:0] _1, _2, counter_1_q, pull_resistor_1_node, pull_resistor_2_node, pull_resistor_3_node,
       pull_resistor_4_node, pull_resistor_5_node, pull_resistor_6_node, pull_resistor_7_node,
       pull_resistor_8_node, pull_resistor_9_node, pull_resistor_10_node, pull_resistor_11_node,
       pull_resistor_12_node, pull_resistor_13_node, pull_resistor_14_node, pull_resistor_15_node,
       pull_resistor_16_node, pull_resistor_17_node, pull_resistor_18_node, pull_resistor_19_node,
       pull_resistor_20_node, pull_resistor_21_node, pull_resistor_22_node, pull_resistor_23_node,
       pull_resistor_24_node, pull_resistor_25_node, pull_resistor_26_node, pull_resistor_27_node,
       pull_resistor_28_node, pull_resistor_29_node, pull_resistor_30_node, pull_resistor_31_node,
       pull_resistor_32_node, register_1_q, register_2_q, register_3_q, register_4_q, register_5_q,
       register_6_q, register_7_q, register_8_q, register_9_q, register_10_q, register_11_q, register_12_q,
       register_13_q, register_14_q, register_15_q, register_16_q, register_17_q, register_18_q,
       register_19_q, register_20_q, register_21_q, register_22_q, register_23_q, register_24_q,
       register_25_q, register_26_q, register_27_q, register_28_q, register_29_q, register_30_q,
       register_31_q, register_32_q;

  assign out_2 = pull_resistor_1_node | 32'h3;  // OR_Gate or_1, 32 bits wide
  Pull_Resistor pull_resistor_1 (.node(pull_resistor_1_node));
  assign pull_resistor_1_node = _1[0] ? register_1_q : 32'bz;  // Controlled_Buffer controlled_buffer_1
  Register #(.width(32), .trigger("high")) register_1 (
    .D(register_2_q), .Q(register_1_q), .clk(_1[0]));  // open: en, clr
  assign out_3 = pull_resistor_2_node | 32'h3;  // OR_Gate or_2, 32 bits wide
  Pull_Resistor pull_resistor_2 (.node(pull_resistor_2_node));
  assign pull_resistor_2_node = _1[1] ? register_2_q : 32'bz;  // Controlled_Buffer controlled_buffer_2
  Register #(.width(32), .trigger("high")) register_2 (
    .D(register_3_q), .Q(register_2_q), .clk(_1[1]));  // open: en, clr
  Pull_Resistor pull_resistor_3 (.node(pull_resistor_3_node));
  assign pull_resistor_3_node = _1[2] ? register_3_q : 32'bz;  // Controlled_Buffer controlled_buffer_3
  Register #(.width(32), .trigger("high")) register_3 (
    .D(register_4_q), .Q(register_3_q), .clk(_1[2]));  // open: en, clr
  assign out_4 = pull_resistor_3_node | 32'h3;  // OR_Gate or_3, 32 bits wide
  assign out_5 = pull_resistor_4_node | 32'h3;  // OR_Gate or_4, 32 bits wide
  Pull_Resistor pull_resistor_4 (.node(pull_resistor_4_node));
  assign pull_resistor_4_node = _1[3] ? register_4_q : 32'bz;  // Controlled_Buffer controlled_buffer_4
  Register #(.width(32), .trigger("high")) register_4 (
    .D(register_5_q), .Q(register_4_q), .clk(_1[3]));  // open: en, clr
  Counter #(.width(32), .max('hffffffff), .trigger("falling")) counter_1 (
    .Q(counter_1_q), .clk(bus_0), .clr(comparator_1_eq));  // open: load, D, count, carry
  assign out_6 = pull_resistor_5_node | 32'h3;  // OR_Gate or_5, 32 bits wide
  Pull_Resistor pull_resistor_5 (.node(pull_resistor_5_node));
  assign pull_resistor_5_node = _1[4] ? register_5_q : 32'bz;  // Controlled_Buffer controlled_buffer_5
  Register #(.width(32), .trigger("high")) register_5 (
    .D(register_6_q), .Q(register_5_q), .clk(_1[4]));  // open: en, clr
  Comparator #(.width(32), .mode("unsigned")) comparator_1 (
    .a(counter_1_q), .b(32'h5a), .eq(comparator_1_eq));  // open: gt, lt
  assign out_7 = pull_resistor_6_node | 32'h3;  // OR_Gate or_6, 32 bits wide
  Pull_Resistor pull_resistor_6 (.node(pull_resistor_6_node));
  assign pull_resistor_6_node = _1[5] ? register_6_q : 32'bz;  // Controlled_Buffer controlled_buffer_6
  Register #(.width(32), .trigger("high")) register_6 (
    .D(register_7_q), .Q(register_6_q), .clk(_1[5]));  // open: en, clr
  D_Flip_Flop d_ff_1 (.clk(comparator_1_eq), .D(d_ff_1_qn), .Q(_0), .Qn(d_ff_1_qn));  // open: preset, en, reset
  Pull_Resistor pull_resistor_7 (.node(pull_resistor_7_node));
  assign pull_resistor_7_node = _1[6] ? register_7_q : 32'bz;  // Controlled_Buffer controlled_buffer_7
  Register #(.width(32), .trigger("high")) register_7 (
    .D(register_8_q), .Q(register_7_q), .clk(_1[6]));  // open: en, clr
  assign out_8 = pull_resistor_7_node | 32'h3;  // OR_Gate or_7, 32 bits wide
  or or_8 (_3, decoder_1_out0, decoder_1_out1);
  Counter #(.width(4), .max('hd), .trigger("falling")) counter_2 (
    .Q(counter_2_q), .clk(_0));  // open: load, D, count, carry, clr
  Decoder #(.select(4)) decoder_1 (
    .out0(decoder_1_out0), .out1(decoder_1_out1), .sel(counter_2_q));  // open: out2, out3, out4, out5, out6, out7, out8, out9, out10, out11, out12, out13, out14, out15, en
  assign out_9 = pull_resistor_8_node | 32'h3;  // OR_Gate or_9, 32 bits wide
  Pull_Resistor pull_resistor_8 (.node(pull_resistor_8_node));
  assign pull_resistor_8_node = _1[7] ? register_8_q : 32'bz;  // Controlled_Buffer controlled_buffer_8
  Register #(.width(32), .trigger("high")) register_8 (
    .D(register_9_q), .Q(register_8_q), .clk(_1[7]));  // open: en, clr
  assign out_10 = pull_resistor_9_node | 32'h3;  // OR_Gate or_10, 32 bits wide
  Pull_Resistor pull_resistor_9 (.node(pull_resistor_9_node));
  assign pull_resistor_9_node = _1[8] ? register_9_q : 32'bz;  // Controlled_Buffer controlled_buffer_9
  Register #(.width(32), .trigger("high")) register_9 (
    .D(register_10_q), .Q(register_9_q), .clk(_1[8]));  // open: en, clr
  rand_pipe rand_pipe_1 (.tick(_3), .out_2(_2));
  assign out_11 = pull_resistor_10_node | 32'h3;  // OR_Gate or_11, 32 bits wide
  Pull_Resistor pull_resistor_10 (.node(pull_resistor_10_node));
  assign pull_resistor_10_node = _1[9] ? register_10_q : 32'bz;  // Controlled_Buffer controlled_buffer_10
  Register #(.width(32), .trigger("high")) register_10 (
    .D(register_11_q), .Q(register_10_q), .clk(_1[9]));  // open: en, clr
  Pull_Resistor pull_resistor_11 (.node(pull_resistor_11_node));
  assign pull_resistor_11_node = _1[10] ? register_11_q : 32'bz;  // Controlled_Buffer controlled_buffer_11
  Register #(.width(32), .trigger("high")) register_11 (
    .D(register_12_q), .Q(register_11_q), .clk(_1[10]));  // open: en, clr
  Shift_Register #(.length(32)) shift_register_1 (
    .in(_3), .clk(_0), .q0(_1[31]), .q1(_1[30]), .q2(_1[29]), .q3(_1[28]), .q4(_1[27]), .q5(_1[26]),
    .q6(_1[25]), .q7(_1[24]), .q8(_1[23]), .q9(_1[22]), .q10(_1[21]), .q11(_1[20]), .q12(_1[19]),
    .q13(_1[18]), .q14(_1[17]), .q15(_1[16]), .q16(_1[15]), .q17(_1[14]), .q18(_1[13]), .q19(_1[12]),
    .q20(_1[11]), .q21(_1[10]), .q22(_1[9]), .q23(_1[8]), .q24(_1[7]), .q25(_1[6]), .q26(_1[5]), .q27(_1[4]),
    .q28(_1[3]), .q29(_1[2]), .q30(_1[1]), .q31(_1[0]));  // open: shift, out, load, clr, d0, d1, d2, d3, d4, d5, d6, d7, d8, d9, d10, d11, d12, d13, d14, d15, d16, d17, d18, d19, d20, d21, d22, d23, d24, d25, d26, d27, d28, d29, d30, d31
  assign out_12 = pull_resistor_11_node | 32'h3;  // OR_Gate or_12, 32 bits wide
  assign out_13 = pull_resistor_12_node | 32'h3;  // OR_Gate or_13, 32 bits wide
  Pull_Resistor pull_resistor_12 (.node(pull_resistor_12_node));
  assign pull_resistor_12_node = _1[11] ? register_12_q : 32'bz;  // Controlled_Buffer controlled_buffer_12
  Register #(.width(32), .trigger("high")) register_12 (
    .D(register_13_q), .Q(register_12_q), .clk(_1[11]));  // open: en, clr
  assign out_14 = pull_resistor_13_node | 32'h3;  // OR_Gate or_14, 32 bits wide
  Pull_Resistor pull_resistor_13 (.node(pull_resistor_13_node));
  assign pull_resistor_13_node = _1[12] ? register_13_q : 32'bz;  // Controlled_Buffer controlled_buffer_13
  Register #(.width(32), .trigger("high")) register_13 (
    .D(register_14_q), .Q(register_13_q), .clk(_1[12]));  // open: en, clr
  assign out_15 = pull_resistor_14_node | 32'h3;  // OR_Gate or_15, 32 bits wide
  Pull_Resistor pull_resistor_14 (.node(pull_resistor_14_node));
  assign pull_resistor_14_node = _1[13] ? register_14_q : 32'bz;  // Controlled_Buffer controlled_buffer_14
  Register #(.width(32), .trigger("high")) register_14 (
    .D(register_15_q), .Q(register_14_q), .clk(_1[13]));  // open: en, clr
  Pull_Resistor pull_resistor_15 (.node(pull_resistor_15_node));
  assign pull_resistor_15_node = _1[14] ? register_15_q : 32'bz;  // Controlled_Buffer controlled_buffer_15
  Register #(.width(32), .trigger("high")) register_15 (
    .D(register_16_q), .Q(register_15_q), .clk(_1[14]));  // open: en, clr
  assign out_16 = pull_resistor_15_node | 32'h3;  // OR_Gate or_16, 32 bits wide
  assign out_17 = pull_resistor_16_node | 32'h3;  // OR_Gate or_17, 32 bits wide
  Pull_Resistor pull_resistor_16 (.node(pull_resistor_16_node));
  assign pull_resistor_16_node = _1[15] ? register_16_q : 32'bz;  // Controlled_Buffer controlled_buffer_16
  Register #(.width(32), .trigger("high")) register_16 (
    .D(register_17_q), .Q(register_16_q), .clk(_1[15]));  // open: en, clr
  assign out_18 = pull_resistor_17_node | 32'h3;  // OR_Gate or_18, 32 bits wide
  Pull_Resistor pull_resistor_17 (.node(pull_resistor_17_node));
  assign pull_resistor_17_node = _1[16] ? register_17_q : 32'bz;  // Controlled_Buffer controlled_buffer_17
  Register #(.width(32), .trigger("high")) register_17 (
    .D(register_18_q), .Q(register_17_q), .clk(_1[16]));  // open: en, clr
  assign out_19 = pull_resistor_18_node | 32'h3;  // OR_Gate or_19, 32 bits wide
  Pull_Resistor pull_resistor_18 (.node(pull_resistor_18_node));
  assign pull_resistor_18_node = _1[17] ? register_18_q : 32'bz;  // Controlled_Buffer controlled_buffer_18
  Register #(.width(32), .trigger("high")) register_18 (
    .D(register_19_q), .Q(register_18_q), .clk(_1[17]));  // open: en, clr
  Pull_Resistor pull_resistor_19 (.node(pull_resistor_19_node));
  assign pull_resistor_19_node = _1[18] ? register_19_q : 32'bz;  // Controlled_Buffer controlled_buffer_19
  Register #(.width(32), .trigger("high")) register_19 (
    .D(register_20_q), .Q(register_19_q), .clk(_1[18]));  // open: en, clr
  assign out_20 = pull_resistor_19_node | 32'h3;  // OR_Gate or_20, 32 bits wide
  assign out_21 = pull_resistor_20_node | 32'h3;  // OR_Gate or_21, 32 bits wide
  Pull_Resistor pull_resistor_20 (.node(pull_resistor_20_node));
  assign pull_resistor_20_node = _1[19] ? register_20_q : 32'bz;  // Controlled_Buffer controlled_buffer_20
  Register #(.width(32), .trigger("high")) register_20 (
    .D(register_21_q), .Q(register_20_q), .clk(_1[19]));  // open: en, clr
  assign out_22 = pull_resistor_21_node | 32'h3;  // OR_Gate or_22, 32 bits wide
  Pull_Resistor pull_resistor_21 (.node(pull_resistor_21_node));
  assign pull_resistor_21_node = _1[20] ? register_21_q : 32'bz;  // Controlled_Buffer controlled_buffer_21
  Register #(.width(32), .trigger("high")) register_21 (
    .D(register_22_q), .Q(register_21_q), .clk(_1[20]));  // open: en, clr
  assign out_23 = pull_resistor_22_node | 32'h3;  // OR_Gate or_23, 32 bits wide
  Pull_Resistor pull_resistor_22 (.node(pull_resistor_22_node));
  assign pull_resistor_22_node = _1[21] ? register_22_q : 32'bz;  // Controlled_Buffer controlled_buffer_22
  Register #(.width(32), .trigger("high")) register_22 (
    .D(register_23_q), .Q(register_22_q), .clk(_1[21]));  // open: en, clr
  Pull_Resistor pull_resistor_23 (.node(pull_resistor_23_node));
  assign pull_resistor_23_node = _1[22] ? register_23_q : 32'bz;  // Controlled_Buffer controlled_buffer_23
  Register #(.width(32), .trigger("high")) register_23 (
    .D(register_24_q), .Q(register_23_q), .clk(_1[22]));  // open: en, clr
  assign out_24 = pull_resistor_23_node | 32'h3;  // OR_Gate or_24, 32 bits wide
  assign out_25 = pull_resistor_24_node | 32'h3;  // OR_Gate or_25, 32 bits wide
  Pull_Resistor pull_resistor_24 (.node(pull_resistor_24_node));
  assign pull_resistor_24_node = _1[23] ? register_24_q : 32'bz;  // Controlled_Buffer controlled_buffer_24
  Register #(.width(32), .trigger("high")) register_24 (
    .D(register_25_q), .Q(register_24_q), .clk(_1[23]));  // open: en, clr
  assign out_26 = pull_resistor_25_node | 32'h3;  // OR_Gate or_26, 32 bits wide
  Pull_Resistor pull_resistor_25 (.node(pull_resistor_25_node));
  assign pull_resistor_25_node = _1[24] ? register_25_q : 32'bz;  // Controlled_Buffer controlled_buffer_25
  Register #(.width(32), .trigger("high")) register_25 (
    .D(register_26_q), .Q(register_25_q), .clk(_1[24]));  // open: en, clr
  assign out_27 = pull_resistor_26_node | 32'h3;  // OR_Gate or_27, 32 bits wide
  Pull_Resistor pull_resistor_26 (.node(pull_resistor_26_node));
  assign pull_resistor_26_node = _1[25] ? register_26_q : 32'bz;  // Controlled_Buffer controlled_buffer_26
  Register #(.width(32), .trigger("high")) register_26 (
    .D(register_27_q), .Q(register_26_q), .clk(_1[25]));  // open: en, clr
  Pull_Resistor pull_resistor_27 (.node(pull_resistor_27_node));
  assign pull_resistor_27_node = _1[26] ? register_27_q : 32'bz;  // Controlled_Buffer controlled_buffer_27
  Register #(.width(32), .trigger("high")) register_27 (
    .D(register_28_q), .Q(register_27_q), .clk(_1[26]));  // open: en, clr
  assign out_28 = pull_resistor_27_node | 32'h3;  // OR_Gate or_28, 32 bits wide
  assign out_29 = pull_resistor_28_node | 32'h3;  // OR_Gate or_29, 32 bits wide
  Pull_Resistor pull_resistor_28 (.node(pull_resistor_28_node));
  assign pull_resistor_28_node = _1[27] ? register_28_q : 32'bz;  // Controlled_Buffer controlled_buffer_28
  Register #(.width(32), .trigger("high")) register_28 (
    .D(register_29_q), .Q(register_28_q), .clk(_1[27]));  // open: en, clr
  assign out_30 = pull_resistor_29_node | 32'h3;  // OR_Gate or_30, 32 bits wide
  Pull_Resistor pull_resistor_29 (.node(pull_resistor_29_node));
  assign pull_resistor_29_node = _1[28] ? register_29_q : 32'bz;  // Controlled_Buffer controlled_buffer_29
  Register #(.width(32), .trigger("high")) register_29 (
    .D(register_30_q), .Q(register_29_q), .clk(_1[28]));  // open: en, clr
  assign out_31 = pull_resistor_30_node | 32'h3;  // OR_Gate or_31, 32 bits wide
  Pull_Resistor pull_resistor_30 (.node(pull_resistor_30_node));
  assign pull_resistor_30_node = _1[29] ? register_30_q : 32'bz;  // Controlled_Buffer controlled_buffer_30
  Register #(.width(32), .trigger("high")) register_30 (
    .D(register_31_q), .Q(register_30_q), .clk(_1[29]));  // open: en, clr
  Pull_Resistor pull_resistor_31 (.node(pull_resistor_31_node));
  assign pull_resistor_31_node = _1[30] ? register_31_q : 32'bz;  // Controlled_Buffer controlled_buffer_31
  Register #(.width(32), .trigger("high")) register_31 (
    .D(register_32_q), .Q(register_31_q), .clk(_1[30]));  // open: en, clr
  assign out_32 = pull_resistor_31_node | 32'h3;  // OR_Gate or_32, 32 bits wide
  assign out_33 = pull_resistor_32_node | 32'h3;  // OR_Gate or_33, 32 bits wide
  Pull_Resistor pull_resistor_32 (.node(pull_resistor_32_node));
  assign pull_resistor_32_node = _1[31] ? register_32_q : 32'bz;  // Controlled_Buffer controlled_buffer_32
  Register #(.width(32), .trigger("high")) register_32 (.D(_2), .Q(register_32_q), .clk(_1[31]));  // open: en, clr
endmodule

module rand_pipe (
  input  tick,
  output [31:0] out_2
);

  wire and_1_out, comparator_1_eq, counter_1_carry;
  wire [2:0] _1, _2, adder_1_out, random_1_out, register_1_q;
  wire [31:0] multiplexer_2_out, multiplexer_3_out, multiplexer_4_out, multiplexer_5_out, multiplexer_6_out,
       multiplexer_7_out, multiplexer_8_out, multiplexer_9_out;

  Counter #(.width(3), .max('h7)) counter_1 (.Q(_1), .carry(counter_1_carry), .clk(tick));  // open: load, D, count, clr
  Random #(.width(3)) random_1 (.clk(counter_1_carry), .out(random_1_out));  // open: next, clr
  Adder #(.width(3)) adder_1 (.a(3'b001), .b(random_1_out), .out(adder_1_out));  // open: cin, cout
  Register #(.width(3), .trigger("low")) register_1 (
    .D(random_1_out), .Q(register_1_q), .clk(counter_1_carry));  // open: en, clr
  Comparator #(.width(3)) comparator_1 (.a(register_1_q), .b(random_1_out), .eq(comparator_1_eq));  // open: gt, lt
  and and_1 (and_1_out, comparator_1_eq, counter_1_carry);
  Multiplexer #(.width(3)) multiplexer_1 (
    .in0(random_1_out), .in1(adder_1_out), .out(_2), .sel(and_1_out));  // open: en
  Multiplexer #(.select(3), .width(32)) multiplexer_2 (
    .in0(32'hff807fff), .in1(32'hfe01ffff), .in2(32'hfc03ffff), .in3(32'hf00fffff), .in4(32'hff00ffff),
    .in5(32'hf807ffff), .in6(32'hff00ffff), .in7(32'hfff807ff), .out(multiplexer_2_out), .sel(_1));  // open: en
  Multiplexer #(.select(3), .width(32)) multiplexer_3 (
    .in0(32'hffc03fff), .in1(32'hfff807ff), .in2(32'hffff807f), .in3(32'hffc03fff), .in4(32'hffff00ff),
    .in5(32'hffe01fff), .in6(32'hffffc03f), .in7(32'hfffe01ff), .out(multiplexer_3_out), .sel(_1));  // open: en
  Multiplexer #(.select(3), .width(32)) multiplexer_4 (
    .in0(32'hffc03fff), .in1(32'hfffe01ff), .in2(32'hffe01fff), .in3(32'hffffe01f), .in4(32'hfff807ff),
    .in5(32'hfffff00f), .in6(32'hff807fff), .in7(32'hfffe01ff), .out(multiplexer_4_out), .sel(_1));  // open: en
  Multiplexer #(.select(3), .width(32)) multiplexer_5 (
    .in0(32'hffe01fff), .in1(32'hfff807ff), .in2(32'hfff00fff), .in3(32'hfffc03ff), .in4(32'hffff807f),
    .in5(32'hfff807ff), .in6(32'hffc03fff), .in7(32'hfff00fff), .out(multiplexer_5_out), .sel(_1));  // open: en
  Multiplexer #(.select(3), .width(32)) multiplexer_6 (
    .in0(32'hfff807ff), .in1(32'hfffe01ff), .in2(32'hfffff00f), .in3(32'hffffc03f), .in4(32'hffc03fff),
    .in5(32'hfc03ffff), .in6(32'hff00ffff), .in7(32'hfffe01ff), .out(multiplexer_6_out), .sel(_1));  // open: en
  Multiplexer #(.select(3), .width(32)) multiplexer_7 (
    .in0(32'hfffc03ff), .in1(32'hffc03fff), .in2(32'hffe01fff), .in3(32'hff807fff), .in4(32'hfc03ffff),
    .in5(32'hff807fff), .in6(32'hf807ffff), .in7(32'hfff00fff), .out(multiplexer_7_out), .sel(_1));  // open: en
  Multiplexer #(.select(3), .width(32)) multiplexer_8 (
    .in0(32'hff807fff), .in1(32'hfff00fff), .in2(32'hfe01ffff), .in3(32'hf00fffff), .in4(32'hfe01ffff),
    .in5(32'hffff00ff), .in6(32'hfffc03ff), .in7(32'hffe01fff), .out(multiplexer_8_out), .sel(_1));  // open: en
  Multiplexer #(.select(3), .width(32)) multiplexer_9 (
    .in0(32'hfff00fff), .in1(32'hffff00ff), .in2(32'hfffc03ff), .in3(32'hffe01fff), .in4(32'hffff807f),
    .in5(32'hffffe01f), .in6(32'hffffc03f), .in7(32'hfffc03ff), .out(multiplexer_9_out), .sel(_1));  // open: en
  Multiplexer #(.select(3), .width(32)) multiplexer_10 (
    .in0(multiplexer_2_out), .in1(multiplexer_3_out), .in2(multiplexer_4_out), .in3(multiplexer_5_out),
    .in4(multiplexer_6_out), .in5(multiplexer_7_out), .in6(multiplexer_8_out), .in7(multiplexer_9_out),
    .out(out_2), .sel(_2));  // open: en
endmodule

module prigalka (
  input  \Кнопка ,
  output [31:0] bus_0,
  output \робит_ли_генератор 
);

  wire _551, _69699, and_1_out, clock_1_out, comparator_1_eq, counter_3_carry, counter_4_carry,
       counter_8_carry, d_ff_1_q, d_ff_1_qn, d_ff_2_q, d_ff_2_qn, d_ff_3_q, d_ff_3_qn, d_ff_4_q, d_ff_4_qn,
       d_ff_5_q, d_ff_5_qn, d_ff_6_qn, multiplexer_1_out, not_1_out, not_2_out, not_3_out, not_4_out,
       not_5_out, not_6_out, not_7_out, not_8_out, not_9_out, or_1_out, or_2_out, transistor_2_out,
       transistor_4_out, \умер , \упал_умер , \упал_умер2 ;
  wire [2:0] counter_6_q;
  wire [4:0] counter_7_q;
  wire [31:0] counter_5_q;

  Clock clock_1 (.out(clock_1_out));
  Transistor transistor_1 (.in(clock_1_out), .out(\робит_ли_генератор ), .gate(\умер ));
  Counter #(.width(2), .max('h3), .ongoal("stay")) counter_1 (
    .clk(d_ff_3_q), .clr(and_1_out));  // open: load, D, count, Q, carry
  Counter #(.width(1), .max('h0), .ongoal("stay")) counter_2 (.clk(d_ff_3_q));  // open: load, D, count, Q, carry, clr
  Counter #(.width(2), .max('h2), .ongoal("stay")) counter_3 (
    .carry(counter_3_carry), .clk(d_ff_3_q), .clr(and_1_out));  // open: load, D, count, Q
  Counter #(.width(1), .max('h1), .ongoal("stay")) counter_4 (
    .carry(counter_4_carry), .clk(d_ff_3_q), .clr(and_1_out));  // open: load, D, count, Q
  Counter #(.width(32), .max('hffffffff), .trigger("falling")) counter_5 (
    .Q(counter_5_q), .clk(\робит_ли_генератор ), .clr(comparator_1_eq));  // open: load, D, count, carry
  Comparator #(.width(32), .mode("unsigned")) comparator_1 (
    .a(counter_5_q), .b(32'h20), .eq(comparator_1_eq));  // open: gt, lt
  D_Flip_Flop d_ff_1 (.clk(comparator_1_eq), .D(d_ff_1_qn), .Q(d_ff_1_q), .Qn(d_ff_1_qn));  // open: preset, en, reset
  Comparator #(.width(5), .mode("unsigned")) comparator_2 (
    .a(counter_7_q), .b(5'b11110), .eq(\упал_умер2 ));  // open: gt, lt
  D_Flip_Flop d_ff_2 (.clk(d_ff_1_q), .D(d_ff_2_qn), .Q(d_ff_2_q), .Qn(d_ff_2_qn));  // open: preset, en, reset
  Decoder #(.select(5)) decoder_1 (
    .out0(bus_0[31]), .out1(bus_0[30]), .out2(bus_0[29]), .out3(bus_0[28]), .out4(bus_0[27]),
    .out5(bus_0[26]), .out6(bus_0[25]), .out7(bus_0[24]), .out8(bus_0[23]), .out9(bus_0[22]),
    .out10(bus_0[21]), .out11(bus_0[20]), .out12(bus_0[19]), .out13(bus_0[18]), .out14(bus_0[17]),
    .out15(bus_0[16]), .out16(bus_0[15]), .out17(bus_0[14]), .out18(bus_0[13]), .out19(bus_0[12]),
    .out20(bus_0[11]), .out21(bus_0[10]), .out22(bus_0[9]), .out23(bus_0[8]), .out24(bus_0[7]),
    .out25(bus_0[6]), .out26(bus_0[5]), .out27(bus_0[4]), .out28(bus_0[3]), .out29(bus_0[2]),
    .out30(bus_0[1]), .out31(bus_0[0]), .sel(counter_7_q));  // open: en
  D_Flip_Flop d_ff_3 (.clk(d_ff_2_q), .D(d_ff_3_qn), .Q(d_ff_3_q), .Qn(d_ff_3_qn));  // open: preset, en, reset
  Comparator #(.width(5), .mode("unsigned")) comparator_3 (
    .a(counter_7_q), .b({5{1'b1}}), .eq(\упал_умер ));  // open: gt, lt
  D_Flip_Flop d_ff_4 (.clk(d_ff_3_q), .D(d_ff_4_qn), .Q(d_ff_4_q), .Qn(d_ff_4_qn));  // open: preset, en, reset
  nand nand_1 (_551, counter_3_carry, counter_4_carry);
  D_Flip_Flop d_ff_5 (.clk(d_ff_4_q), .D(d_ff_5_qn), .Q(d_ff_5_q), .Qn(d_ff_5_qn));  // open: preset, en, reset
  Comparator #(.width(5), .mode("unsigned")) comparator_4 (.a(counter_7_q), .b(5'b11110), .gt(_69699));  // open: eq, lt
  D_Flip_Flop d_ff_6 (.clk(d_ff_5_q), .D(d_ff_6_qn), .Qn(d_ff_6_qn));  // open: Q, preset, en, reset
  Counter #(.width(3), .max('h7)) counter_6 (
    .Q(counter_6_q), .clk(d_ff_4_q), .clr(or_1_out));  // open: load, D, count, carry
  or or_1 (or_1_out, _69699, _551);
  not not_1 (not_1_out, \Кнопка );
  Multiplexer #(.select(3)) multiplexer_1 (
    .in0(d_ff_5_q), .in1(d_ff_4_q), .in2(d_ff_3_q), .in3(d_ff_3_q), .in4(d_ff_2_q), .in5(d_ff_1_q),
    .in6(d_ff_1_q), .in7(comparator_1_eq), .out(multiplexer_1_out), .sel(counter_6_q));  // open: en
  and and_1 (and_1_out, not_1_out, \Кнопка );
  Transistor #(.\type ("n")) transistor_2 (.in(d_ff_2_q), .out(transistor_2_out), .gate(_551));
  Transistor transistor_3 (.in(multiplexer_1_out), .out(transistor_2_out), .gate(_551));
  // DotMatrix #(.inputtype("select"), .matrixcols(32), .matrixrows(32)) dotmatrix_1: pin names not known; wires that end beside it: 32'h40, bus_0
  Counter #(.width(5), .max('h1f)) counter_7 (
    .load(_551), .Q(counter_7_q), .clk(transistor_2_out), .clr(transistor_4_out));  // open: D, count, carry
  not not_2 (not_2_out, not_3_out);
  not not_3 (not_3_out, not_4_out);
  not not_4 (not_4_out, not_5_out);
  not not_5 (not_5_out, not_6_out);
  not not_6 (not_6_out, not_7_out);
  not not_7 (not_7_out, not_8_out);
  not not_8 (not_8_out, not_9_out);
  not not_9 (not_9_out, or_2_out);
  or or_2 (or_2_out, \упал_умер , \упал_умер2 );
  Transistor transistor_4 (.in(not_2_out), .out(transistor_4_out), .gate(counter_8_carry));
  Counter #(.width(4), .max('h4), .ongoal("stay")) counter_8 (
    .carry(counter_8_carry), .clk(or_2_out));  // open: load, D, count, Q, clr
  Counter #(.width(4), .max('h1), .ongoal("stay")) counter_9 (
    .carry(\умер ), .clk(counter_8_carry));  // open: load, D, count, Q, clr
endmodule

module d (
);

  wire [31:0] pipes_1_out_2, pipes_1_out_3, pipes_1_out_4, pipes_1_out_5, pipes_1_out_6, pipes_1_out_7,
       pipes_1_out_8, pipes_1_out_9, pipes_1_out_10, pipes_1_out_11, pipes_1_out_12, pipes_1_out_13,
       pipes_1_out_14, pipes_1_out_15, pipes_1_out_16, pipes_1_out_17, pipes_1_out_18, pipes_1_out_19,
       pipes_1_out_20, pipes_1_out_21, pipes_1_out_22, pipes_1_out_23, pipes_1_out_24, pipes_1_out_25,
       pipes_1_out_26, pipes_1_out_27, pipes_1_out_28, pipes_1_out_29, pipes_1_out_30, pipes_1_out_31,
       pipes_1_out_32, pipes_1_out_33;

  pipes pipes_1 (
    .out_2(pipes_1_out_2), .out_3(pipes_1_out_3), .out_4(pipes_1_out_4), .out_5(pipes_1_out_5),
    .out_6(pipes_1_out_6), .out_7(pipes_1_out_7), .out_8(pipes_1_out_8), .out_9(pipes_1_out_9),
    .out_10(pipes_1_out_10), .out_11(pipes_1_out_11), .out_12(pipes_1_out_12), .out_13(pipes_1_out_13),
    .out_14(pipes_1_out_14), .out_15(pipes_1_out_15), .out_16(pipes_1_out_16), .out_17(pipes_1_out_17),
    .out_18(pipes_1_out_18), .out_19(pipes_1_out_19), .out_20(pipes_1_out_20), .out_21(pipes_1_out_21),
    .out_22(pipes_1_out_22), .out_23(pipes_1_out_23), .out_24(pipes_1_out_24), .out_25(pipes_1_out_25),
    .out_26(pipes_1_out_26), .out_27(pipes_1_out_27), .out_28(pipes_1_out_28), .out_29(pipes_1_out_29),
    .out_30(pipes_1_out_30), .out_31(pipes_1_out_31), .out_32(pipes_1_out_32), .out_33(pipes_1_out_33));  // open: bus_0
endmodule

module vcyo (
  input  \Кнопка ,
  output [31:0] out_2,
  output [31:0] out_3,
  output [31:0] out_4,
  output [31:0] out_5,
  output [31:0] out_6,
  output [31:0] out_7,
  output [31:0] out_8,
  output [31:0] out_9,
  output [31:0] out_10,
  output [31:0] out_11,
  output [31:0] out_12,
  output [31:0] out_13,
  output [31:0] out_14,
  output [31:0] out_15,
  output [31:0] out_16,
  output [31:0] out_17,
  output [31:0] out_18,
  output [31:0] out_19,
  output [31:0] out_20,
  output [31:0] out_21,
  output [31:0] out_22,
  output [31:0] out_23,
  output [31:0] out_24,
  output [31:0] out_25,
  output [31:0] out_26,
  output [31:0] out_27,
  output [31:0] out_28,
  output [31:0] out_29,
  output [31:0] out_30,
  output [31:0] out_31,
  output [31:0] out_32,
  output [31:0] out_33,
  output [31:0] out_34,
  output bus_0
);

  wire _1_1, _1_2, _1_3, _1_4, _1_5, _1_6, _1_7, _1_8, _1_9, _1_10, _1_11, _1_12, _1_13, _1_14, _1_15, _1_16,
       _1_17, _1_18, _1_19, _1_20, _1_21, _1_22, _1_23, _1_24, _1_25, _1_26, _1_27, _1_28, _1_29, _1_30,
       _1_31, _1_32, _2_1, _2_2, _2_3, _2_4, _2_5, _2_6, _2_7, _2_8, _2_9, _2_10, _2_11, _2_12, _2_13, _2_14,
       _2_15, _2_16, _2_17, _2_18, _2_19, _2_20, _2_21, _2_22, _2_23, _2_24, _2_25, _2_26, _2_27, _2_28,
       _2_29, _2_30, _2_31, _2_32, _551, _69699, and_1_out, and_2_out, and_3_out, and_4_out, and_5_out,
       and_6_out, and_7_out, and_8_out, and_9_out, and_10_out, and_11_out, and_12_out, and_13_out,
       and_14_out, and_15_out, and_16_out, and_17_out, and_18_out, and_19_out, and_20_out, and_21_out,
       and_22_out, and_23_out, and_24_out, and_25_out, and_26_out, and_27_out, and_28_out, and_29_out,
       and_30_out, and_31_out, and_32_out, and_33_out, button_1_out, clock_1_out, comparator_1_eq,
       counter_3_carry, counter_4_carry, counter_8_carry, d_ff_1_q, d_ff_1_qn, d_ff_2_q, d_ff_2_qn, d_ff_3_q,
       d_ff_3_qn, d_ff_4_q, d_ff_4_qn, d_ff_5_q, d_ff_5_qn, d_ff_6_qn, multiplexer_1_out, not_1_out,
       not_2_out, not_3_out, not_4_out, not_5_out, not_6_out, not_7_out, not_8_out, not_9_out, or_1_out,
       or_2_out, or_3_out, or_4_out, or_5_out, or_6_out, or_7_out, or_8_out, or_9_out, or_11_out, or_12_out,
       or_13_out, or_14_out, or_15_out, or_16_out, or_17_out, or_18_out, or_19_out, or_20_out, or_21_out,
       or_22_out, or_23_out, or_24_out, or_25_out, or_26_out, or_27_out, or_28_out, or_29_out, or_30_out,
       or_31_out, or_32_out, or_33_out, or_34_out, or_35_out, or_36_out, transistor_2_out, transistor_3_out,
       transistor_5_out, \врезался_умер , \умер , \упал_умер , \упал_умер2 ;
  wire [2:0] counter_6_q;
  wire [4:0] counter_7_q;
  wire [31:0] counter_5_q, pipes_2_out_2, pipes_2_out_3, pipes_2_out_4, pipes_2_out_5, pipes_2_out_6,
       pipes_2_out_7, pipes_2_out_8, pipes_2_out_9, pipes_2_out_10, pipes_2_out_11, pipes_2_out_12,
       pipes_2_out_13, pipes_2_out_14, pipes_2_out_15, pipes_2_out_16, pipes_2_out_17, pipes_2_out_18,
       pipes_2_out_19, pipes_2_out_20, pipes_2_out_21, pipes_2_out_22, pipes_2_out_23, pipes_2_out_24,
       pipes_2_out_25, pipes_2_out_26, pipes_2_out_27, pipes_2_out_28, pipes_2_out_29, pipes_2_out_30,
       pipes_2_out_31, pipes_2_out_32, pipes_2_out_33, pipes_3_out_2, pipes_3_out_3, pipes_3_out_4,
       pipes_3_out_5, pipes_3_out_6, pipes_3_out_7, pipes_3_out_8, pipes_3_out_9, pipes_3_out_10,
       pipes_3_out_11, pipes_3_out_12, pipes_3_out_13, pipes_3_out_14, pipes_3_out_15, pipes_3_out_16,
       pipes_3_out_17, pipes_3_out_18, pipes_3_out_19, pipes_3_out_20, pipes_3_out_21, pipes_3_out_22,
       pipes_3_out_23, pipes_3_out_24, pipes_3_out_25, pipes_3_out_26, pipes_3_out_27, pipes_3_out_28,
       pipes_3_out_29, pipes_3_out_30, pipes_3_out_31, pipes_3_out_32, pipes_3_out_33, pipes_4_out_7;

  or or_1 (or_1_out, _1_1, _2_1);
  and and_1 (and_1_out, out_34[31], or_1_out);
  or or_2 (or_2_out, _1_2, _2_2);
  and and_2 (and_2_out, out_34[30], or_2_out);
  or or_3 (or_3_out, _1_3, _2_3);
  and and_3 (and_3_out, out_34[29], or_3_out);
  or or_4 (or_4_out, _1_4, _2_4);
  and and_4 (and_4_out, out_34[28], or_4_out);
  and and_5 (and_5_out, out_34[27], or_5_out);
  or or_5 (or_5_out, _1_5, _2_5);
  or or_6 (or_6_out, _1_6, _2_6);
  and and_6 (and_6_out, out_34[26], or_6_out);
  or or_7 (or_7_out, _1_7, _2_7);
  and and_7 (and_7_out, out_34[25], or_7_out);
  or or_8 (or_8_out, _1_8, _2_8);
  and and_8 (and_8_out, out_34[24], or_8_out);
  or or_9 (or_9_out, _1_9, _2_9);
  and and_9 (and_9_out, out_34[23], or_9_out);
  or or_10 (\врезался_умер , and_1_out, and_2_out, and_3_out, and_4_out, and_5_out, and_6_out, and_7_out, and_8_out, and_9_out, and_10_out, and_11_out, and_12_out, and_13_out, and_14_out, and_15_out, and_16_out, and_17_out, and_19_out, and_18_out, and_20_out, and_21_out, and_22_out, and_23_out, and_24_out, and_25_out, and_26_out, and_27_out, and_28_out, and_29_out, and_30_out, and_32_out, and_33_out);
  or or_11 (or_11_out, _1_10, _2_10);
  and and_10 (and_10_out, out_34[22], or_11_out);
  or or_12 (or_12_out, _1_11, _2_11);
  and and_11 (and_11_out, out_34[21], or_12_out);
  Clock clock_1 (.out(clock_1_out));
  or or_13 (or_13_out, _1_13, _2_13);
  or or_14 (or_14_out, _1_12, _2_12);
  and and_12 (and_12_out, out_34[20], or_14_out);
  and and_13 (and_13_out, out_34[19], or_13_out);
  Transistor transistor_1 (.in(clock_1_out), .out(bus_0), .gate(or_16_out));
  or or_15 (or_15_out, _1_14, _2_14);
  and and_14 (and_14_out, out_34[18], or_15_out);
  pipes pipes_1 (
    .out_8({_2_1, _2_2, _2_3, _2_4, _2_5, _2_6, _2_7, _2_8, _2_9, _2_10, _2_11, _2_12, _2_13, _2_14, _2_15, _2_16, _2_17, _2_18, _2_19, _2_20, _2_21, _2_22, _2_23, _2_24, _2_25, _2_26, _2_27, _2_28, _2_29, _2_30, _2_31, _2_32}),
    .out_9({_1_1, _1_2, _1_3, _1_4, _1_5, _1_6, _1_7, _1_8, _1_9, _1_10, _1_11, _1_12, _1_13, _1_14, _1_15, _1_16, _1_17, _1_18, _1_19, _1_20, _1_21, _1_22, _1_23, _1_24, _1_25, _1_26, _1_27, _1_28, _1_29, _1_30, _1_31, _1_32}),
    .bus_0(bus_0));  // open: out_2, out_3, out_4, out_5, out_6, out_7, out_10, out_11, out_12, out_13, out_14, out_15, out_16, out_17, out_18, out_19, out_20, out_21, out_22, out_23, out_24, out_25, out_26, out_27, out_28, out_29, out_30, out_31, out_32, out_33
  or or_16 (or_16_out, \умер , \врезался_умер );
  or or_17 (or_17_out, _1_15, _2_15);
  and and_15 (and_15_out, out_34[17], or_17_out);
  or or_18 (or_18_out, _1_16, _2_16);
  and and_16 (and_16_out, out_34[16], or_18_out);
  Counter #(.width(1), .max('h0), .ongoal("stay")) counter_1 (.clk(d_ff_3_q));  // open: load, D, count, Q, carry, clr
  Counter #(.width(2), .max('h3), .ongoal("stay")) counter_2 (
    .clk(d_ff_3_q), .clr(transistor_2_out));  // open: load, D, count, Q, carry
  or or_19 (or_19_out, _1_17, _2_17);
  and and_17 (and_17_out, out_34[15], or_19_out);
  Counter #(.width(2), .max('h2), .ongoal("stay")) counter_3 (
    .carry(counter_3_carry), .clk(d_ff_3_q), .clr(transistor_2_out));  // open: load, D, count, Q
  Counter #(.width(1), .max('h1), .ongoal("stay")) counter_4 (
    .carry(counter_4_carry), .clk(d_ff_3_q), .clr(transistor_2_out));  // open: load, D, count, Q
  Counter #(.width(32), .max('hffffffff), .trigger("falling")) counter_5 (
    .Q(counter_5_q), .clk(bus_0), .clr(comparator_1_eq));  // open: load, D, count, carry
  or or_20 (or_20_out, _1_18, _2_18);
  and and_18 (and_18_out, out_34[13], or_22_out);
  and and_19 (and_19_out, out_34[14], or_20_out);
  Comparator #(.width(32), .mode("unsigned")) comparator_1 (
    .a(counter_5_q), .b(32'h20), .eq(comparator_1_eq));  // open: gt, lt
  or or_21 (or_21_out, _1_20, _2_20);
  or or_22 (or_22_out, _1_19, _2_19);
  and and_20 (and_20_out, out_34[12], or_21_out);
  Transistor transistor_2 (.in(and_31_out), .out(transistor_2_out), .gate(or_16_out));
  D_Flip_Flop d_ff_1 (.clk(comparator_1_eq), .D(d_ff_1_qn), .Q(d_ff_1_q), .Qn(d_ff_1_qn));  // open: preset, en, reset
  or or_23 (or_23_out, _1_21, _2_21);
  and and_21 (and_21_out, out_34[11], or_23_out);
  Comparator #(.width(5), .mode("unsigned")) comparator_2 (
    .a(counter_7_q), .b(5'b11110), .eq(\упал_умер2 ));  // open: gt, lt
  D_Flip_Flop d_ff_2 (.clk(d_ff_1_q), .D(d_ff_2_qn), .Q(d_ff_2_q), .Qn(d_ff_2_qn));  // open: preset, en, reset
  or or_24 (or_24_out, _1_22, _2_22);
  and and_22 (and_22_out, out_34[10], or_24_out);
  Decoder #(.select(5)) decoder_1 (
    .out0(out_34[31]), .out1(out_34[30]), .out2(out_34[29]), .out3(out_34[28]), .out4(out_34[27]),
    .out5(out_34[26]), .out6(out_34[25]), .out7(out_34[24]), .out8(out_34[23]), .out9(out_34[22]),
    .out10(out_34[21]), .out11(out_34[20]), .out12(out_34[19]), .out13(out_34[18]), .out14(out_34[17]),
    .out15(out_34[16]), .out16(out_34[15]), .out17(out_34[14]), .out18(out_34[13]), .out19(out_34[12]),
    .out20(out_34[11]), .out21(out_34[10]), .out22(out_34[9]), .out23(out_34[8]), .out24(out_34[7]),
    .out25(out_34[6]), .out26(out_34[5]), .out27(out_34[4]), .out28(out_34[3]), .out29(out_34[2]),
    .out30(out_34[1]), .out31(out_34[0]), .sel(counter_7_q));  // open: en
  D_Flip_Flop d_ff_3 (.clk(d_ff_2_q), .D(d_ff_3_qn), .Q(d_ff_3_q), .Qn(d_ff_3_qn));  // open: preset, en, reset
  or or_25 (or_25_out, _1_23, _2_23);
  and and_23 (and_23_out, out_34[9], or_25_out);
  D_Flip_Flop d_ff_4 (.clk(d_ff_3_q), .D(d_ff_4_qn), .Q(d_ff_4_q), .Qn(d_ff_4_qn));  // open: preset, en, reset
  or or_26 (or_26_out, _1_24, _2_24);
  and and_24 (and_24_out, out_34[8], or_26_out);
  Comparator #(.width(5), .mode("unsigned")) comparator_3 (
    .a(counter_7_q), .b({5{1'b1}}), .eq(\упал_умер ));  // open: gt, lt
  D_Flip_Flop d_ff_5 (.clk(d_ff_4_q), .D(d_ff_5_qn), .Q(d_ff_5_q), .Qn(d_ff_5_qn));  // open: preset, en, reset
  or or_27 (or_27_out, _1_25, _2_25);
  and and_25 (and_25_out, out_34[7], or_27_out);
  and and_26 (and_26_out, out_34[6], or_29_out);
  Comparator #(.width(5), .mode("unsigned")) comparator_4 (.a(counter_7_q), .b(5'b11110), .gt(_69699));  // open: eq, lt
  nand nand_1 (_551, counter_3_carry, counter_4_carry);
  D_Flip_Flop d_ff_6 (.clk(d_ff_5_q), .D(d_ff_6_qn), .Qn(d_ff_6_qn));  // open: Q, preset, en, reset
  or or_28 (or_28_out, _1_27, _2_27);
  or or_29 (or_29_out, _1_26, _2_26);
  and and_27 (and_27_out, out_34[5], or_28_out);
  or or_30 (or_30_out, _1_28, _2_28);
  and and_28 (and_28_out, out_34[4], or_30_out);
  Button button_1 (.out(button_1_out));
  Multiplexer #(.select(3)) multiplexer_1 (
    .in0(d_ff_5_q), .in1(d_ff_4_q), .in2(d_ff_3_q), .in3(d_ff_3_q), .in4(d_ff_2_q), .in5(d_ff_1_q),
    .in6(d_ff_1_q), .in7(comparator_1_eq), .out(multiplexer_1_out), .sel(counter_6_q));  // open: en
  Counter #(.width(3), .max('h7)) counter_6 (
    .Q(counter_6_q), .clk(d_ff_4_q), .clr(or_31_out));  // open: load, D, count, carry
  or or_31 (or_31_out, _69699, _551);
  or or_32 (or_32_out, _1_29, _2_29);
  and and_29 (and_29_out, out_34[3], or_32_out);
  not not_1 (not_1_out, \Кнопка );
  or or_33 (or_33_out, _1_30, _2_30);
  and and_30 (and_30_out, out_34[2], or_33_out);
  and and_31 (and_31_out, not_1_out, \Кнопка );
  Transistor transistor_3 (.in(multiplexer_1_out), .out(transistor_3_out), .gate(_551));
  or or_34 (or_34_out, _1_31, _2_31);
  and and_32 (and_32_out, out_34[1], or_34_out);
  Transistor #(.\type ("n")) transistor_4 (.in(d_ff_2_q), .out(transistor_3_out), .gate(_551));
  or or_35 (or_35_out, _1_32, _2_32);
  and and_33 (and_33_out, out_34[0], or_35_out);
  Counter #(.width(5), .max('h1f)) counter_7 (
    .load(_551), .Q(counter_7_q), .clk(transistor_3_out), .clr(transistor_5_out));  // open: D, count, carry
  Transistor transistor_5 (.in(not_2_out), .out(transistor_5_out), .gate(counter_8_carry));
  not not_2 (not_2_out, not_3_out);
  not not_3 (not_3_out, not_4_out);
  not not_4 (not_4_out, not_5_out);
  not not_5 (not_5_out, not_6_out);
  not not_6 (not_6_out, not_7_out);
  not not_7 (not_7_out, not_8_out);
  not not_8 (not_8_out, not_9_out);
  not not_9 (not_9_out, or_36_out);
  Counter #(.width(4), .max('h4), .ongoal("stay")) counter_8 (
    .carry(counter_8_carry), .clk(or_36_out));  // open: load, D, count, Q, clr
  or or_36 (or_36_out, \упал_умер , \упал_умер2 );
  Counter #(.width(4), .max('h1), .ongoal("stay")) counter_9 (
    .carry(\умер ), .clk(counter_8_carry));  // open: load, D, count, Q, clr
  // DotMatrix #(.inputtype("select"), .matrixcols(32), .matrixrows(32)) dotmatrix_1: pin names not known; wires that end beside it: 32'h40, out_34
  DotMatrix #(.matrixcols(32), .matrixrows(32)) dotmatrix_2 (
    .col0(pipes_2_out_2), .col1(pipes_2_out_3), .col2(pipes_2_out_4), .col3(pipes_2_out_5),
    .col4(pipes_2_out_6), .col5(pipes_2_out_7), .col6(pipes_2_out_8), .col7(pipes_2_out_9),
    .col8(pipes_2_out_10), .col9(pipes_2_out_11), .col10(pipes_2_out_12), .col11(pipes_2_out_13),
    .col12(pipes_2_out_14), .col13(pipes_2_out_15), .col14(pipes_2_out_16), .col15(pipes_2_out_17),
    .col16(pipes_2_out_18), .col17(pipes_2_out_19), .col18(pipes_2_out_20), .col19(pipes_2_out_21),
    .col20(pipes_2_out_22), .col21(pipes_2_out_23), .col22(pipes_2_out_24), .col23(pipes_2_out_25),
    .col24(pipes_2_out_26), .col25(pipes_2_out_27), .col26(pipes_2_out_28), .col27(pipes_2_out_29),
    .col28(pipes_2_out_30), .col29(pipes_2_out_31), .col30(pipes_2_out_32), .col31(pipes_2_out_33));
  pipes pipes_2 (
    .out_2(pipes_2_out_2), .out_3(pipes_2_out_3), .out_4(pipes_2_out_4), .out_5(pipes_2_out_5),
    .out_6(pipes_2_out_6), .out_7(pipes_2_out_7), .out_8(pipes_2_out_8), .out_9(pipes_2_out_9),
    .out_10(pipes_2_out_10), .out_11(pipes_2_out_11), .out_12(pipes_2_out_12), .out_13(pipes_2_out_13),
    .out_14(pipes_2_out_14), .out_15(pipes_2_out_15), .out_16(pipes_2_out_16), .out_17(pipes_2_out_17),
    .out_18(pipes_2_out_18), .out_19(pipes_2_out_19), .out_20(pipes_2_out_20), .out_21(pipes_2_out_21),
    .out_22(pipes_2_out_22), .out_23(pipes_2_out_23), .out_24(pipes_2_out_24), .out_25(pipes_2_out_25),
    .out_26(pipes_2_out_26), .out_27(pipes_2_out_27), .out_28(pipes_2_out_28), .out_29(pipes_2_out_29),
    .out_30(pipes_2_out_30), .out_31(pipes_2_out_31), .out_32(pipes_2_out_32), .out_33(pipes_2_out_33),
    .bus_0(bus_0));
  assign out_3 = out_34 | pipes_4_out_7;  // OR_Gate or_37, 32 bits wide
  DotMatrix #(.matrixcols(32), .matrixrows(32)) dotmatrix_3 (
    .col0(pipes_3_out_2), .col1(pipes_3_out_3), .col2(pipes_3_out_4), .col3(pipes_3_out_5),
    .col4(pipes_3_out_6), .col5(out_3), .col6(pipes_3_out_8), .col7(pipes_3_out_9), .col8(pipes_3_out_10),
    .col9(pipes_3_out_11), .col10(pipes_3_out_12), .col11(pipes_3_out_13), .col12(pipes_3_out_14),
    .col13(pipes_3_out_15), .col14(pipes_3_out_16), .col15(pipes_3_out_17), .col16(pipes_3_out_18),
    .col17(pipes_3_out_19), .col18(pipes_3_out_20), .col19(pipes_3_out_21), .col20(pipes_3_out_22),
    .col21(pipes_3_out_23), .col22(pipes_3_out_24), .col23(pipes_3_out_25), .col24(pipes_3_out_26),
    .col25(pipes_3_out_27), .col26(pipes_3_out_28), .col27(pipes_3_out_29), .col28(pipes_3_out_30),
    .col29(pipes_3_out_31), .col30(pipes_3_out_32), .col31(pipes_3_out_33));
  pipes pipes_3 (
    .out_2(pipes_3_out_2), .out_3(pipes_3_out_3), .out_4(pipes_3_out_4), .out_5(pipes_3_out_5),
    .out_6(pipes_3_out_6), .out_7(pipes_3_out_7), .out_8(pipes_3_out_8), .out_9(pipes_3_out_9),
    .out_10(pipes_3_out_10), .out_11(pipes_3_out_11), .out_12(pipes_3_out_12), .out_13(pipes_3_out_13),
    .out_14(pipes_3_out_14), .out_15(pipes_3_out_15), .out_16(pipes_3_out_16), .out_17(pipes_3_out_17),
    .out_18(pipes_3_out_18), .out_19(pipes_3_out_19), .out_20(pipes_3_out_20), .out_21(pipes_3_out_21),
    .out_22(pipes_3_out_22), .out_23(pipes_3_out_23), .out_24(pipes_3_out_24), .out_25(pipes_3_out_25),
    .out_26(pipes_3_out_26), .out_27(pipes_3_out_27), .out_28(pipes_3_out_28), .out_29(pipes_3_out_29),
    .out_30(pipes_3_out_30), .out_31(pipes_3_out_31), .out_32(pipes_3_out_32), .out_33(pipes_3_out_33),
    .bus_0(bus_0));
  pipes pipes_4 (
    .out_2(out_2), .out_3(out_17), .out_4(out_5), .out_5(out_15), .out_6(out_14), .out_7(pipes_4_out_7),
    .out_8(out_12), .out_9(out_10), .out_10(out_9), .out_11(out_8), .out_12(out_6), .out_13(out_7),
    .out_14(out_4), .out_15(out_16), .out_16(out_24), .out_17(out_19), .out_18(out_22), .out_19(out_20),
    .out_20(out_21), .out_21(out_26), .out_22(out_27), .out_23(out_28), .out_24(out_29), .out_25(out_11),
    .out_26(out_13), .out_27(out_25), .out_28(out_31), .out_29(out_18), .out_30(out_32), .out_31(out_23),
    .out_32(out_30), .out_33(out_33), .bus_0(bus_0));

  // Other names for the same wires on the sheet: _3_32 = out_34[0]; _3_31 = out_34[1]; _3_30 = out_34[2];
  //   _3_29 = out_34[3]; _3_28 = out_34[4]; _3_27 = out_34[5]; _3_26 = out_34[6]; _3_25 = out_34[7];
  //   _3_24 = out_34[8]; _3_23 = out_34[9]; _3_22 = out_34[10]; _3_21 = out_34[11]; _3_20 = out_34[12];
  //   _3_19 = out_34[13]; _3_18 = out_34[14]; _3_17 = out_34[15]; _3_16 = out_34[16]; _3_15 = out_34[17];
  //   _3_14 = out_34[18]; _3_13 = out_34[19]; _3_12 = out_34[20]; _3_11 = out_34[21]; _3_10 = out_34[22];
  //   _3_9 = out_34[23]; _3_8 = out_34[24]; _3_7 = out_34[25]; _3_6 = out_34[26]; _3_5 = out_34[27];
  //   _3_4 = out_34[28]; _3_3 = out_34[29]; _3_2 = out_34[30]; _3_1 = out_34[31]
endmodule
