// Logisim project dvoichny_kod_-_dvoichno-desyatichny_na_PR7.circ as structural Verilog: 2 circuits, main circuit main
module main (
  input  [7:0] in_1
);

  wire \пр7_1_u , \пр7_1_v , \пр7_1_w , \пр7_1_x , \пр7_1_y , \пр7_1_z , \пр7_2_y ;
  wire [9:1] \пр7_2_w ;

  // Probe on in_1
  \ПР7  \u_пр7_1  (
    .a(in_1[7]), .b(in_1[6]), .c(in_1[5]), .d(in_1[4]), .e(in_1[3]), .x(\пр7_1_x ), .y(\пр7_1_y ),
    .z(\пр7_1_z ), .u(\пр7_1_u ), .v(\пр7_1_v ), .w(\пр7_1_w ));
  // Probe on in_1
  \ПР7  \u_пр7_2  (
    .a(\пр7_1_u ), .b(\пр7_1_v ), .c(\пр7_1_w ), .d(in_1[2]), .e(in_1[1]), .y(\пр7_2_y ), .z(\пр7_2_w [4]),
    .u(\пр7_2_w [3]), .v(\пр7_2_w [2]), .w(\пр7_2_w [1]));  // open: x
  \ПР7  \u_пр7_3  (
    .a(1'b0), .b(\пр7_1_x ), .c(\пр7_1_y ), .d(\пр7_1_z ), .e(\пр7_2_y ), .y(\пр7_2_w [9]), .z(\пр7_2_w [8]),
    .u(\пр7_2_w [7]), .v(\пр7_2_w [6]), .w(\пр7_2_w [5]));  // open: x
  DotMatrix #(.inputtype("row"), .matrixcols(1), .matrixrows(10)) dotmatrix_1 (
    .row0(in_1[0]), .row1(\пр7_2_w [1]), .row2(\пр7_2_w [2]), .row3(\пр7_2_w [3]), .row4(\пр7_2_w [4]),
    .row5(\пр7_2_w [5]), .row6(\пр7_2_w [6]), .row7(\пр7_2_w [7]), .row8(\пр7_2_w [8]), .row9(\пр7_2_w [9]));
  Hex_Digit_Display hex_digit_display_1 (.value(\пр7_2_w [7:4]));  // open: dp
  Hex_Digit_Display hex_digit_display_2 (.value({2'b00, \пр7_2_w [9:8]}));  // open: dp
  Hex_Digit_Display hex_digit_display_3 (.value({\пр7_2_w [3:1], in_1[0]}));  // open: dp

  // Notes on the sheet:
  //   HEX(16)
  //   DEC(10)
endmodule

module \ПР7  (
  input  a,
  input  b,
  input  c,
  input  d,
  input  e,
  output x,
  output y,
  output z,
  output u,
  output v,
  output w
);

  wire and_1_out, and_2_out, and_3_out, and_4_out, and_5_out, and_6_out, and_7_out, and_8_out, and_9_out,
       and_10_out, and_11_out, and_12_out, and_13_out, and_14_out, and_15_out, and_16_out, and_17_out,
       and_18_out, and_19_out, and_20_out, and_21_out, and_22_out, and_23_out, and_24_out, and_25_out,
       and_26_out, and_27_out, and_28_out, and_29_out, and_30_out, and_31_out, and_32_out, and_33_out,
       and_34_out, and_35_out, and_36_out, and_37_out, and_38_out, not_1_out, not_2_out, not_3_out,
       not_4_out, not_5_out, not_6_out, not_7_out, not_8_out, not_9_out, not_10_out, not_11_out, not_12_out,
       not_13_out, not_14_out, not_15_out, not_16_out, not_17_out, not_18_out, not_19_out, not_20_out,
       not_21_out, not_22_out, not_23_out, not_24_out, not_25_out, not_26_out, not_27_out, not_28_out,
       not_29_out, not_30_out, not_31_out, not_32_out, not_33_out, not_34_out, not_35_out, not_36_out,
       not_37_out, not_38_out, not_39_out, not_40_out, not_41_out, not_42_out, not_43_out, not_44_out,
       not_45_out, not_46_out, not_47_out, not_48_out, not_49_out, not_50_out, not_51_out, not_52_out,
       not_53_out, not_54_out, not_55_out, not_56_out, not_57_out, not_58_out, not_59_out, not_60_out,
       not_61_out, not_62_out, not_63_out, not_64_out, not_65_out, not_66_out, not_67_out, not_68_out,
       not_69_out, not_70_out, not_71_out;

  and and_1 (and_1_out, a, c);
  and and_2 (and_2_out, a, b);
  not not_1 (not_1_out, a);
  not not_2 (not_2_out, a);
  not not_3 (not_3_out, b);
  not not_4 (not_4_out, c);
  not not_5 (not_5_out, a);
  not not_6 (not_6_out, b);
  not not_7 (not_7_out, a);
  not not_8 (not_8_out, b);
  not not_9 (not_9_out, a);
  not not_10 (not_10_out, a);
  not not_11 (not_11_out, c);
  not not_12 (not_12_out, d);
  not not_13 (not_13_out, b);
  not not_14 (not_14_out, c);
  not not_15 (not_15_out, c);
  not not_16 (not_16_out, c);
  not not_17 (not_17_out, d);
  not not_18 (not_18_out, a);
  not not_19 (not_19_out, b);
  not not_20 (not_20_out, d);
  not not_21 (not_21_out, e);
  not not_22 (not_22_out, a);
  not not_23 (not_23_out, c);
  not not_24 (not_24_out, d);
  not not_25 (not_25_out, a);
  not not_26 (not_26_out, e);
  not not_27 (not_27_out, b);
  not not_28 (not_28_out, c);
  not not_29 (not_29_out, c);
  not not_30 (not_30_out, d);
  not not_31 (not_31_out, e);
  not not_32 (not_32_out, d);
  not not_33 (not_33_out, b);
  not not_34 (not_34_out, c);
  not not_35 (not_35_out, e);
  not not_36 (not_36_out, a);
  not not_37 (not_37_out, b);
  not not_38 (not_38_out, a);
  not not_39 (not_39_out, d);
  not not_40 (not_40_out, e);
  not not_41 (not_41_out, a);
  not not_42 (not_42_out, d);
  not not_43 (not_43_out, d);
  not not_44 (not_44_out, e);
  not not_45 (not_45_out, b);
  not not_46 (not_46_out, c);
  not not_47 (not_47_out, d);
  not not_48 (not_48_out, b);
  not not_49 (not_49_out, c);
  not not_50 (not_50_out, a);
  not not_51 (not_51_out, b);
  not not_52 (not_52_out, c);
  not not_53 (not_53_out, a);
  not not_54 (not_54_out, c);
  not not_55 (not_55_out, a);
  not not_56 (not_56_out, b);
  not not_57 (not_57_out, e);
  not not_58 (not_58_out, a);
  not not_59 (not_59_out, c);
  not not_60 (not_60_out, d);
  not not_61 (not_61_out, e);
  not not_62 (not_62_out, a);
  not not_63 (not_63_out, d);
  not not_64 (not_64_out, b);
  not not_65 (not_65_out, c);
  not not_66 (not_66_out, e);
  not not_67 (not_67_out, c);
  not not_68 (not_68_out, e);
  not not_69 (not_69_out, b);
  not not_70 (not_70_out, d);
  not not_71 (not_71_out, e);
  or or_1 (x, and_1_out, and_2_out);
  and and_3 (and_3_out, not_1_out, b, d);
  and and_4 (and_4_out, not_2_out, b, c);
  and and_5 (and_5_out, b, c, d);
  and and_6 (and_6_out, a, not_3_out, not_4_out);
  and and_7 (and_7_out, not_5_out, not_6_out, c, e);
  and and_8 (and_8_out, not_7_out, not_8_out, c, d);
  and and_9 (and_9_out, not_9_out, c, d, e);
  and and_10 (and_10_out, not_10_out, b, not_11_out, not_12_out);
  and and_11 (and_11_out, a, not_13_out, not_14_out);
  and and_12 (and_12_out, a, not_15_out, e);
  and and_13 (and_13_out, a, not_16_out, d);
  and and_14 (and_14_out, a, b, c, not_17_out);
  and and_15 (and_15_out, not_18_out, not_19_out, c, not_20_out, not_21_out);
  and and_16 (and_16_out, not_22_out, b, not_23_out, not_24_out, e);
  and and_17 (and_17_out, not_25_out, b, c, d, not_26_out);
  and and_18 (and_18_out, a, not_27_out, not_28_out, d, e);
  and and_19 (and_19_out, a, b, not_29_out, not_30_out, not_31_out);
  and and_20 (and_20_out, a, b, c, not_32_out, e);
  and and_21 (and_21_out, not_33_out, not_34_out, d, not_35_out);
  and and_22 (and_22_out, not_36_out, not_37_out, d, e);
  and and_23 (and_23_out, not_38_out, b, not_39_out, not_40_out);
  and and_24 (and_24_out, not_41_out, b, c, not_42_out);
  and and_25 (and_25_out, b, c, not_43_out, not_44_out);
  and and_26 (and_26_out, a, not_45_out, not_46_out, not_47_out, e);
  and and_27 (and_27_out, a, not_48_out, c, d);
  and and_28 (and_28_out, a, b, not_49_out, d, e);
  and and_29 (and_29_out, not_50_out, not_51_out, not_52_out, e);
  and and_30 (and_30_out, not_53_out, not_54_out, d, e);
  and and_31 (and_31_out, not_55_out, not_56_out, c, d, not_57_out);
  and and_32 (and_32_out, not_58_out, b, not_59_out, not_60_out, not_61_out);
  and and_33 (and_33_out, not_62_out, b, c, not_63_out, e);
  and and_34 (and_34_out, a, not_64_out, not_65_out, not_66_out);
  and and_35 (and_35_out, a, not_67_out, d, not_68_out);
  and and_36 (and_36_out, a, not_69_out, c, e);
  and and_37 (and_37_out, a, c, d, e);
  and and_38 (and_38_out, a, b, c, not_70_out, not_71_out);
  or or_2 (y, and_3_out, and_4_out, and_5_out, and_6_out);
  or or_3 (z, and_7_out, and_8_out, and_9_out, and_10_out, and_11_out, and_12_out, and_13_out, and_14_out);
  or or_4 (u, and_15_out, and_16_out, and_17_out, and_18_out, and_19_out, and_20_out);
  or or_5 (v, and_21_out, and_22_out, and_23_out, and_24_out, and_25_out, and_26_out, and_27_out, and_28_out);
  or or_6 (w, and_29_out, and_30_out, and_31_out, and_32_out, and_33_out, and_34_out, and_35_out, and_36_out, and_37_out, and_38_out);
endmodule
