// Logisim project pipes_1.circ as structural Verilog: 3 circuits, main circuit main
module main (
);

  wire clock_1_out;
  wire [31:0] pipes_1_out_2, pipes_1_out_3, pipes_1_out_4, pipes_1_out_5, pipes_1_out_6, pipes_1_out_7,
       pipes_1_out_8, pipes_1_out_9, pipes_1_out_10, pipes_1_out_11, pipes_1_out_12, pipes_1_out_13,
       pipes_1_out_14, pipes_1_out_15, pipes_1_out_16, pipes_1_out_17, pipes_1_out_18, pipes_1_out_19,
       pipes_1_out_20, pipes_1_out_21, pipes_1_out_22, pipes_1_out_23, pipes_1_out_24, pipes_1_out_25,
       pipes_1_out_26, pipes_1_out_27, pipes_1_out_28, pipes_1_out_29, pipes_1_out_30, pipes_1_out_31,
       pipes_1_out_32, pipes_1_out_33;

  Clock clock_1 (.out(clock_1_out));
  pipes pipes_1 (
    .tick(clock_1_out), .out_2(pipes_1_out_2), .out_3(pipes_1_out_3), .out_4(pipes_1_out_4),
    .out_5(pipes_1_out_5), .out_6(pipes_1_out_6), .out_7(pipes_1_out_7), .out_8(pipes_1_out_8),
    .out_9(pipes_1_out_9), .out_10(pipes_1_out_10), .out_11(pipes_1_out_11), .out_12(pipes_1_out_12),
    .out_13(pipes_1_out_13), .out_14(pipes_1_out_14), .out_15(pipes_1_out_15), .out_16(pipes_1_out_16),
    .out_17(pipes_1_out_17), .out_18(pipes_1_out_18), .out_19(pipes_1_out_19), .out_20(pipes_1_out_20),
    .out_21(pipes_1_out_21), .out_22(pipes_1_out_22), .out_23(pipes_1_out_23), .out_24(pipes_1_out_24),
    .out_25(pipes_1_out_25), .out_26(pipes_1_out_26), .out_27(pipes_1_out_27), .out_28(pipes_1_out_28),
    .out_29(pipes_1_out_29), .out_30(pipes_1_out_30), .out_31(pipes_1_out_31), .out_32(pipes_1_out_32),
    .out_33(pipes_1_out_33));
  DotMatrix #(.matrixcols(32), .matrixrows(32)) dotmatrix_1 (
    .col0(pipes_1_out_2), .col1(pipes_1_out_3), .col2(pipes_1_out_4), .col3(pipes_1_out_5),
    .col4(pipes_1_out_6), .col5(pipes_1_out_7), .col6(pipes_1_out_8), .col7(pipes_1_out_9),
    .col8(pipes_1_out_10), .col9(pipes_1_out_11), .col10(pipes_1_out_12), .col11(pipes_1_out_13),
    .col12(pipes_1_out_14), .col13(pipes_1_out_15), .col14(pipes_1_out_16), .col15(pipes_1_out_17),
    .col16(pipes_1_out_18), .col17(pipes_1_out_19), .col18(pipes_1_out_20), .col19(pipes_1_out_21),
    .col20(pipes_1_out_22), .col21(pipes_1_out_23), .col22(pipes_1_out_24), .col23(pipes_1_out_25),
    .col24(pipes_1_out_26), .col25(pipes_1_out_27), .col26(pipes_1_out_28), .col27(pipes_1_out_29),
    .col28(pipes_1_out_30), .col29(pipes_1_out_31), .col30(pipes_1_out_32), .col31(pipes_1_out_33));
endmodule

module pipes (
  input  tick,
  output [31:0] out_2,
  output [31:0] out_3,
  output [31:0] out_4,
  output [31:0] out_5,
  output [31:0] out_6,
  output [31:0] out_7,
  output [31:0] out_8,
  output [31:0] out_9,
  output [31:0] out_10,
  output [31:0] out_11,
  output [31:0] out_12,
  output [31:0] out_13,
  output [31:0] out_14,
  output [31:0] out_15,
  output [31:0] out_16,
  output [31:0] out_17,
  output [31:0] out_18,
  output [31:0] out_19,
  output [31:0] out_20,
  output [31:0] out_21,
  output [31:0] out_22,
  output [31:0] out_23,
  output [31:0] out_24,
  output [31:0] out_25,
  output [31:0] out_26,
  output [31:0] out_27,
  output [31:0] out_28,
  output [31:0] out_29,
  output [31:0] out_30,
  output [31:0] out_31,
  output [31:0] out_32,
  output [31:0] out_33
);

  wire _3, decoder_1_out0, decoder_1_out1;
  wire [3:0] counter_1_q;
  wire [31:0] _1, _2, register_1_q, register_2_q, register_3_q, register_4_q, register_5_q, register_6_q,
       register_7_q, register_8_q, register_9_q, register_10_q, register_11_q, register_12_q, register_13_q,
       register_14_q, register_15_q, register_16_q, register_17_q, register_18_q, register_19_q,
       register_20_q, register_21_q, register_22_q, register_23_q, register_24_q, register_25_q,
       register_26_q, register_27_q, register_28_q, register_29_q, register_30_q, register_31_q,
       register_32_q;

  Counter #(.width(4), .max('hd), .trigger("falling")) counter_1 (
    .Q(counter_1_q), .clk(tick));  // open: load, D, count, carry, clr
  Pull_Resistor pull_resistor_1 (.node(out_2));
  assign out_2 = _1[0] ? register_1_q : 32'bz;  // Controlled_Buffer controlled_buffer_1
  Register #(.width(32), .trigger("high")) register_1 (
    .D(register_2_q), .Q(register_1_q), .clk(_1[0]));  // open: en, clr
  or or_1 (_3, decoder_1_out0, decoder_1_out1);
  Decoder #(.select(4)) decoder_1 (
    .out0(decoder_1_out0), .out1(decoder_1_out1), .sel(counter_1_q));  // open: out2, out3, out4, out5, out6, out7, out8, out9, out10, out11, out12, out13, out14, out15, en
  Pull_Resistor pull_resistor_2 (.node(out_3));
  assign out_3 = _1[1] ? register_2_q : 32'bz;  // Controlled_Buffer controlled_buffer_2
  Register #(.width(32), .trigger("high")) register_2 (
    .D(register_3_q), .Q(register_2_q), .clk(_1[1]));  // open: en, clr
  rand_pipe rand_pipe_1 (.tick(_3), .out_2(_2));
  Register #(.width(32), .trigger("high")) register_3 (
    .D(register_4_q), .Q(register_3_q), .clk(_1[2]));  // open: en, clr
  Pull_Resistor pull_resistor_3 (.node(out_4));
  assign out_4 = _1[2] ? register_3_q : 32'bz;  // Controlled_Buffer controlled_buffer_3
  Shift_Register #(.length(32)) shift_register_1 (
    .in(_3), .clk(tick), .q0(_1[31]), .q1(_1[30]), .q2(_1[29]), .q3(_1[28]), .q4(_1[27]), .q5(_1[26]),
    .q6(_1[25]), .q7(_1[24]), .q8(_1[23]), .q9(_1[22]), .q10(_1[21]), .q11(_1[20]), .q12(_1[19]),
    .q13(_1[18]), .q14(_1[17]), .q15(_1[16]), .q16(_1[15]), .q17(_1[14]), .q18(_1[13]), .q19(_1[12]),
    .q20(_1[11]), .q21(_1[10]), .q22(_1[9]), .q23(_1[8]), .q24(_1[7]), .q25(_1[6]), .q26(_1[5]), .q27(_1[4]),
    .q28(_1[3]), .q29(_1[2]), .q30(_1[1]), .q31(_1[0]));  // open: shift, out, load, clr, d0, d1, d2, d3, d4, d5, d6, d7, d8, d9, d10, d11, d12, d13, d14, d15, d16, d17, d18, d19, d20, d21, d22, d23, d24, d25, d26, d27, d28, d29, d30, d31
  Pull_Resistor pull_resistor_4 (.node(out_5));
  assign out_5 = _1[3] ? register_4_q : 32'bz;  // Controlled_Buffer controlled_buffer_4
  Register #(.width(32), .trigger("high")) register_4 (
    .D(register_5_q), .Q(register_4_q), .clk(_1[3]));  // open: en, clr
  Pull_Resistor pull_resistor_5 (.node(out_6));
  assign out_6 = _1[4] ? register_5_q : 32'bz;  // Controlled_Buffer controlled_buffer_5
  Register #(.width(32), .trigger("high")) register_5 (
    .D(register_6_q), .Q(register_5_q), .clk(_1[4]));  // open: en, clr
  Pull_Resistor pull_resistor_6 (.node(out_7));
  assign out_7 = _1[5] ? register_6_q : 32'bz;  // Controlled_Buffer controlled_buffer_6
  Register #(.width(32), .trigger("high")) register_6 (
    .D(register_7_q), .Q(register_6_q), .clk(_1[5]));  // open: en, clr
  Register #(.width(32), .trigger("high")) register_7 (
    .D(register_8_q), .Q(register_7_q), .clk(_1[6]));  // open: en, clr
  Pull_Resistor pull_resistor_7 (.node(out_8));
  assign out_8 = _1[6] ? register_7_q : 32'bz;  // Controlled_Buffer controlled_buffer_7
  Pull_Resistor pull_resistor_8 (.node(out_9));
  assign out_9 = _1[7] ? register_8_q : 32'bz;  // Controlled_Buffer controlled_buffer_8
  Register #(.width(32), .trigger("high")) register_8 (
    .D(register_9_q), .Q(register_8_q), .clk(_1[7]));  // open: en, clr
  Pull_Resistor pull_resistor_9 (.node(out_10));
  assign out_10 = _1[8] ? register_9_q : 32'bz;  // Controlled_Buffer controlled_buffer_9
  Register #(.width(32), .trigger("high")) register_9 (
    .D(register_10_q), .Q(register_9_q), .clk(_1[8]));  // open: en, clr
  Pull_Resistor pull_resistor_10 (.node(out_11));
  assign out_11 = _1[9] ? register_10_q : 32'bz;  // Controlled_Buffer controlled_buffer_10
  Register #(.width(32), .trigger("high")) register_10 (
    .D(register_11_q), .Q(register_10_q), .clk(_1[9]));  // open: en, clr
  Register #(.width(32), .trigger("high")) register_11 (
    .D(register_12_q), .Q(register_11_q), .clk(_1[10]));  // open: en, clr
  Pull_Resistor pull_resistor_11 (.node(out_12));
  assign out_12 = _1[10] ? register_11_q : 32'bz;  // Controlled_Buffer controlled_buffer_11
  Pull_Resistor pull_resistor_12 (.node(out_13));
  assign out_13 = _1[11] ? register_12_q : 32'bz;  // Controlled_Buffer controlled_buffer_12
  Register #(.width(32), .trigger("high")) register_12 (
    .D(register_13_q), .Q(register_12_q), .clk(_1[11]));  // open: en, clr
  Pull_Resistor pull_resistor_13 (.node(out_14));
  assign out_14 = _1[12] ? register_13_q : 32'bz;  // Controlled_Buffer controlled_buffer_13
  Register #(.width(32), .trigger("high")) register_13 (
    .D(register_14_q), .Q(register_13_q), .clk(_1[12]));  // open: en, clr
  Pull_Resistor pull_resistor_14 (.node(out_15));
  assign out_15 = _1[13] ? register_14_q : 32'bz;  // Controlled_Buffer controlled_buffer_14
  Register #(.width(32), .trigger("high")) register_14 (
    .D(register_15_q), .Q(register_14_q), .clk(_1[13]));  // open: en, clr
  Register #(.width(32), .trigger("high")) register_15 (
    .D(register_16_q), .Q(register_15_q), .clk(_1[14]));  // open: en, clr
  Pull_Resistor pull_resistor_15 (.node(out_16));
  assign out_16 = _1[14] ? register_15_q : 32'bz;  // Controlled_Buffer controlled_buffer_15
  Pull_Resistor pull_resistor_16 (.node(out_17));
  assign out_17 = _1[15] ? register_16_q : 32'bz;  // Controlled_Buffer controlled_buffer_16
  Register #(.width(32), .trigger("high")) register_16 (
    .D(register_17_q), .Q(register_16_q), .clk(_1[15]));  // open: en, clr
  Pull_Resistor pull_resistor_17 (.node(out_18));
  assign out_18 = _1[16] ? register_17_q : 32'bz;  // Controlled_Buffer controlled_buffer_17
  Register #(.width(32), .trigger("high")) register_17 (
    .D(register_18_q), .Q(register_17_q), .clk(_1[16]));  // open: en, clr
  Pull_Resistor pull_resistor_18 (.node(out_19));
  assign out_19 = _1[17] ? register_18_q : 32'bz;  // Controlled_Buffer controlled_buffer_18
  Register #(.width(32), .trigger("high")) register_18 (
    .D(register_19_q), .Q(register_18_q), .clk(_1[17]));  // open: en, clr
  Register #(.width(32), .trigger("high")) register_19 (
    .D(register_20_q), .Q(register_19_q), .clk(_1[18]));  // open: en, clr
  Pull_Resistor pull_resistor_19 (.node(out_20));
  assign out_20 = _1[18] ? register_19_q : 32'bz;  // Controlled_Buffer controlled_buffer_19
  Pull_Resistor pull_resistor_20 (.node(out_21));
  assign out_21 = _1[19] ? register_20_q : 32'bz;  // Controlled_Buffer controlled_buffer_20
  Register #(.width(32), .trigger("high")) register_20 (
    .D(register_21_q), .Q(register_20_q), .clk(_1[19]));  // open: en, clr
  Pull_Resistor pull_resistor_21 (.node(out_22));
  assign out_22 = _1[20] ? register_21_q : 32'bz;  // Controlled_Buffer controlled_buffer_21
  Register #(.width(32), .trigger("high")) register_21 (
    .D(register_22_q), .Q(register_21_q), .clk(_1[20]));  // open: en, clr
  Pull_Resistor pull_resistor_22 (.node(out_23));
  assign out_23 = _1[21] ? register_22_q : 32'bz;  // Controlled_Buffer controlled_buffer_22
  Register #(.width(32), .trigger("high")) register_22 (
    .D(register_23_q), .Q(register_22_q), .clk(_1[21]));  // open: en, clr
  Register #(.width(32), .trigger("high")) register_23 (
    .D(register_24_q), .Q(register_23_q), .clk(_1[22]));  // open: en, clr
  Pull_Resistor pull_resistor_23 (.node(out_24));
  assign out_24 = _1[22] ? register_23_q : 32'bz;  // Controlled_Buffer controlled_buffer_23
  Pull_Resistor pull_resistor_24 (.node(out_25));
  assign out_25 = _1[23] ? register_24_q : 32'bz;  // Controlled_Buffer controlled_buffer_24
  Register #(.width(32), .trigger("high")) register_24 (
    .D(register_25_q), .Q(register_24_q), .clk(_1[23]));  // open: en, clr
  Pull_Resistor pull_resistor_25 (.node(out_26));
  assign out_26 = _1[24] ? register_25_q : 32'bz;  // Controlled_Buffer controlled_buffer_25
  Register #(.width(32), .trigger("high")) register_25 (
    .D(register_26_q), .Q(register_25_q), .clk(_1[24]));  // open: en, clr
  Pull_Resistor pull_resistor_26 (.node(out_27));
  assign out_27 = _1[25] ? register_26_q : 32'bz;  // Controlled_Buffer controlled_buffer_26
  Register #(.width(32), .trigger("high")) register_26 (
    .D(register_27_q), .Q(register_26_q), .clk(_1[25]));  // open: en, clr
  Register #(.width(32), .trigger("high")) register_27 (
    .D(register_28_q), .Q(register_27_q), .clk(_1[26]));  // open: en, clr
  Pull_Resistor pull_resistor_27 (.node(out_28));
  assign out_28 = _1[26] ? register_27_q : 32'bz;  // Controlled_Buffer controlled_buffer_27
  Pull_Resistor pull_resistor_28 (.node(out_29));
  assign out_29 = _1[27] ? register_28_q : 32'bz;  // Controlled_Buffer controlled_buffer_28
  Register #(.width(32), .trigger("high")) register_28 (
    .D(register_29_q), .Q(register_28_q), .clk(_1[27]));  // open: en, clr
  Pull_Resistor pull_resistor_29 (.node(out_30));
  assign out_30 = _1[28] ? register_29_q : 32'bz;  // Controlled_Buffer controlled_buffer_29
  Register #(.width(32), .trigger("high")) register_29 (
    .D(register_30_q), .Q(register_29_q), .clk(_1[28]));  // open: en, clr
  Pull_Resistor pull_resistor_30 (.node(out_31));
  assign out_31 = _1[29] ? register_30_q : 32'bz;  // Controlled_Buffer controlled_buffer_30
  Register #(.width(32), .trigger("high")) register_30 (
    .D(register_31_q), .Q(register_30_q), .clk(_1[29]));  // open: en, clr
  Register #(.width(32), .trigger("high")) register_31 (
    .D(register_32_q), .Q(register_31_q), .clk(_1[30]));  // open: en, clr
  Pull_Resistor pull_resistor_31 (.node(out_32));
  assign out_32 = _1[30] ? register_31_q : 32'bz;  // Controlled_Buffer controlled_buffer_31
  Pull_Resistor pull_resistor_32 (.node(out_33));
  assign out_33 = _1[31] ? register_32_q : 32'bz;  // Controlled_Buffer controlled_buffer_32
  Register #(.width(32), .trigger("high")) register_32 (.D(_2), .Q(register_32_q), .clk(_1[31]));  // open: en, clr

  // Other names for the same wires on the sheet: _0 = tick
endmodule

module rand_pipe (
  input  tick,
  output [31:0] out_2
);

  wire and_1_out, comparator_1_eq, counter_1_carry;
  wire [2:0] _1, _2, adder_1_out, random_1_out, register_1_q;
  wire [31:0] multiplexer_2_out, multiplexer_3_out, multiplexer_4_out, multiplexer_5_out, multiplexer_6_out,
       multiplexer_7_out, multiplexer_8_out, multiplexer_9_out;

  Counter #(.width(3), .max('h7)) counter_1 (.Q(_1), .carry(counter_1_carry), .clk(tick));  // open: load, D, count, clr
  Random #(.width(3)) random_1 (.clk(counter_1_carry), .out(random_1_out));  // open: next, clr
  Adder #(.width(3)) adder_1 (.a(3'b001), .b(random_1_out), .out(adder_1_out));  // open: cin, cout
  Register #(.width(3), .trigger("low")) register_1 (
    .D(random_1_out), .Q(register_1_q), .clk(counter_1_carry));  // open: en, clr
  Comparator #(.width(3)) comparator_1 (.a(register_1_q), .b(random_1_out), .eq(comparator_1_eq));  // open: gt, lt
  and and_1 (and_1_out, comparator_1_eq, counter_1_carry);
  Multiplexer #(.width(3)) multiplexer_1 (
    .in0(random_1_out), .in1(adder_1_out), .out(_2), .sel(and_1_out));  // open: en
  Multiplexer #(.select(3), .width(32)) multiplexer_2 (
    .in0(32'hff807fff), .in1(32'hfe01ffff), .in2(32'hfc03ffff), .in3(32'hf00fffff), .in4(32'hff00ffff),
    .in5(32'hf807ffff), .in6(32'hff00ffff), .in7(32'hfff807ff), .out(multiplexer_2_out), .sel(_1));  // open: en
  Multiplexer #(.select(3), .width(32)) multiplexer_3 (
    .in0(32'hffc03fff), .in1(32'hfff807ff), .in2(32'hffff807f), .in3(32'hffc03fff), .in4(32'hffff00ff),
    .in5(32'hffe01fff), .in6(32'hffffc03f), .in7(32'hfffe01ff), .out(multiplexer_3_out), .sel(_1));  // open: en
  Multiplexer #(.select(3), .width(32)) multiplexer_4 (
    .in0(32'hffc03fff), .in1(32'hfffe01ff), .in2(32'hffe01fff), .in3(32'hffffe01f), .in4(32'hfff807ff),
    .in5(32'hfffff00f), .in6(32'hff807fff), .in7(32'hfffe01ff), .out(multiplexer_4_out), .sel(_1));  // open: en
  Multiplexer #(.select(3), .width(32)) multiplexer_5 (
    .in0(32'hffe01fff), .in1(32'hfff807ff), .in2(32'hfff00fff), .in3(32'hfffc03ff), .in4(32'hffff807f),
    .in5(32'hfff807ff), .in6(32'hffc03fff), .in7(32'hfff00fff), .out(multiplexer_5_out), .sel(_1));  // open: en
  Multiplexer #(.select(3), .width(32)) multiplexer_6 (
    .in0(32'hfff807ff), .in1(32'hfffe01ff), .in2(32'hfffff00f), .in3(32'hffffc03f), .in4(32'hffc03fff),
    .in5(32'hfc03ffff), .in6(32'hff00ffff), .in7(32'hfffe01ff), .out(multiplexer_6_out), .sel(_1));  // open: en
  Multiplexer #(.select(3), .width(32)) multiplexer_7 (
    .in0(32'hfffc03ff), .in1(32'hffc03fff), .in2(32'hffe01fff), .in3(32'hff807fff), .in4(32'hfc03ffff),
    .in5(32'hff807fff), .in6(32'hf807ffff), .in7(32'hfff00fff), .out(multiplexer_7_out), .sel(_1));  // open: en
  Multiplexer #(.select(3), .width(32)) multiplexer_8 (
    .in0(32'hff807fff), .in1(32'hfff00fff), .in2(32'hfe01ffff), .in3(32'hf00fffff), .in4(32'hfe01ffff),
    .in5(32'hffff00ff), .in6(32'hfffc03ff), .in7(32'hffe01fff), .out(multiplexer_8_out), .sel(_1));  // open: en
  Multiplexer #(.select(3), .width(32)) multiplexer_9 (
    .in0(32'hfff00fff), .in1(32'hffff00ff), .in2(32'hfffc03ff), .in3(32'hffe01fff), .in4(32'hffff807f),
    .in5(32'hffffe01f), .in6(32'hffffc03f), .in7(32'hfffc03ff), .out(multiplexer_9_out), .sel(_1));  // open: en
  Multiplexer #(.select(3), .width(32)) multiplexer_10 (
    .in0(multiplexer_2_out), .in1(multiplexer_3_out), .in2(multiplexer_4_out), .in3(multiplexer_5_out),
    .in4(multiplexer_6_out), .in5(multiplexer_7_out), .in6(multiplexer_8_out), .in7(multiplexer_9_out),
    .out(out_2), .sel(_2));  // open: en
endmodule
