// Logisim project screenMessage .circ as structural Verilog: 6 circuits, main circuit S/L
module S_L (
  input  [1:0] in_1,
  output [31:0] out_2,
  output [31:0] out_3,
  output [31:0] out_4,
  output [31:0] out_5,
  output [31:0] out_6,
  output [31:0] out_7,
  output [31:0] out_8,
  output [31:0] out_9,
  output [31:0] out_10,
  output [31:0] out_11,
  output [31:0] out_12,
  output [31:0] out_13,
  output [31:0] out_14,
  output [31:0] out_15,
  output [31:0] out_16,
  output [31:0] out_17,
  output [31:0] out_18,
  output [31:0] out_19,
  output [31:0] out_20,
  output [31:0] out_21
);

  Multiplexer #(.select(2), .width(32)) multiplexer_1 (
    .in0({32{1'b0}}), .in1({32{1'b0}}), .in2({32{1'b0}}), .in3({32{1'b0}}), .out(out_2), .sel(in_1));  // open: en
  DotMatrix #(.matrixcols(20), .matrixrows(32)) dotmatrix_1 (
    .col0({32{1'b0}}), .col1({32{1'b0}}), .col2({32{1'b0}}), .col3(32'h3ffffffc), .col4(32'h3ffffffc),
    .col5(32'h3ffffffc), .col6(32'h3ffffffc), .col7(32'h3ffffffc), .col8(32'h3ffffffc), .col9(32'h3ffffffc),
    .col10(32'hfc), .col11(32'hfc), .col12(32'hfc), .col13(32'hfc), .col14(32'hfc), .col15(32'hfc),
    .col16(32'hfc), .col17(32'hfc), .col18({32{1'b0}}), .col19({32{1'b0}}));
  Multiplexer #(.select(2), .width(32)) multiplexer_2 (
    .in0({32{1'b0}}), .in1({32{1'b0}}), .in2({32{1'b0}}), .in3({32{1'b0}}), .out(out_3), .sel(in_1));  // open: en
  Multiplexer #(.select(2), .width(32)) multiplexer_3 (
    .in0({32{1'b0}}), .in1({32{1'b0}}), .in2(32'h3fffe0fe), .in3({32{1'b0}}), .out(out_4), .sel(in_1));  // open: en
  Multiplexer #(.select(2), .width(32)) multiplexer_4 (
    .in0({32{1'b0}}), .in1(32'h3ffffffc), .in2(32'h3fffe0fe), .in3({32{1'b0}}), .out(out_5), .sel(in_1));  // open: en
  Multiplexer #(.select(2), .width(32)) multiplexer_5 (
    .in0({32{1'b0}}), .in1(32'h3ffffffc), .in2(32'h3fffe0fe), .in3({32{1'b0}}), .out(out_6), .sel(in_1));  // open: en
  DotMatrix #(.matrixcols(20), .matrixrows(32)) dotmatrix_2 (
    .col0({32{1'b0}}), .col1({32{1'b0}}), .col2(32'h3fffe0fe), .col3(32'h3fffe0fe), .col4(32'h3fffe0fe),
    .col5(32'h3fffe0fe), .col6(32'h3f83e0fe), .col7(32'h3f83e0fe), .col8(32'h3f83e0fe), .col9(32'h3f83e0fe),
    .col10(32'h3f83e0fe), .col11(32'h3f83e0fe), .col12(32'h3f83e0fe), .col13(32'h3f83fffe),
    .col14(32'h3f83fffe), .col15(32'h3f83fffe), .col16(32'h3f83fffe), .col17(32'h3f83fffe),
    .col18({32{1'b0}}), .col19({32{1'b0}}));
  Multiplexer #(.select(2), .width(32)) multiplexer_6 (
    .in0({32{1'b0}}), .in1(32'h3ffffffc), .in2(32'h3fffe0fe), .in3({32{1'b0}}), .out(out_7), .sel(in_1));  // open: en
  Multiplexer #(.select(2), .width(32)) multiplexer_7 (
    .in0({32{1'b0}}), .in1(32'h3ffffffc), .in2(32'h3f83e0fe), .in3({32{1'b0}}), .out(out_8), .sel(in_1));  // open: en
  Multiplexer #(.select(2), .width(32)) multiplexer_8 (
    .in0({32{1'b0}}), .in1(32'h3ffffffc), .in2(32'h3f83e0fe), .in3({32{1'b0}}), .out(out_9), .sel(in_1));  // open: en
  Multiplexer #(.select(2), .width(32)) multiplexer_9 (
    .in0({32{1'b0}}), .in1(32'h3ffffffc), .in2(32'h3f83e0fe), .in3({32{1'b0}}), .out(out_10), .sel(in_1));  // open: en
  Multiplexer #(.select(2), .width(32)) multiplexer_10 (
    .in0({32{1'b0}}), .in1(32'h3ffffffc), .in2(32'h3f83e0fe), .in3({32{1'b0}}), .out(out_11), .sel(in_1));  // open: en
  Multiplexer #(.select(2), .width(32)) multiplexer_11 (
    .in0({32{1'b0}}), .in1(32'hfc), .in2(32'h3f83e0fe), .in3({32{1'b0}}), .out(out_12), .sel(in_1));  // open: en
  Multiplexer #(.select(2), .width(32)) multiplexer_12 (
    .in0({32{1'b0}}), .in1(32'hfc), .in2(32'h3f83e0fe), .in3({32{1'b0}}), .out(out_13), .sel(in_1));  // open: en
  Multiplexer #(.select(2), .width(32)) multiplexer_13 (
    .in0({32{1'b0}}), .in1(32'hfc), .in2(32'h3f83e0fe), .in3({32{1'b0}}), .out(out_14), .sel(in_1));  // open: en
  Multiplexer #(.select(2), .width(32)) multiplexer_14 (
    .in0({32{1'b0}}), .in1(32'hfc), .in2(32'h3f83fffe), .in3({32{1'b0}}), .out(out_15), .sel(in_1));  // open: en
  Multiplexer #(.select(2), .width(32)) multiplexer_15 (
    .in0({32{1'b0}}), .in1(32'hfc), .in2(32'h3f83fffe), .in3({32{1'b0}}), .out(out_16), .sel(in_1));  // open: en
  Multiplexer #(.select(2), .width(32)) multiplexer_16 (
    .in0({32{1'b0}}), .in1(32'hfc), .in2(32'h3f83fffe), .in3({32{1'b0}}), .out(out_17), .sel(in_1));  // open: en
  Multiplexer #(.select(2), .width(32)) multiplexer_17 (
    .in0({32{1'b0}}), .in1(32'hfc), .in2(32'h3f83fffe), .in3({32{1'b0}}), .out(out_18), .sel(in_1));  // open: en
  Multiplexer #(.select(2), .width(32)) multiplexer_18 (
    .in0({32{1'b0}}), .in1(32'hfc), .in2(32'h3f83fffe), .in3({32{1'b0}}), .out(out_19), .sel(in_1));  // open: en
  Multiplexer #(.select(2), .width(32)) multiplexer_19 (
    .in0({32{1'b0}}), .in1({32{1'b0}}), .in2({32{1'b0}}), .in3({32{1'b0}}), .out(out_20), .sel(in_1));  // open: en
  Multiplexer #(.select(2), .width(32)) multiplexer_20 (
    .in0({32{1'b0}}), .in1({32{1'b0}}), .in2({32{1'b0}}), .in3({32{1'b0}}), .out(out_21), .sel(in_1));  // open: en
endmodule

module t_o (
  input  [1:0] in_1,
  output [31:0] out_2,
  output [31:0] out_3,
  output [31:0] out_4,
  output [31:0] out_5,
  output [31:0] out_6,
  output [31:0] out_7,
  output [31:0] out_8,
  output [31:0] out_9,
  output [31:0] out_10,
  output [31:0] out_11,
  output [31:0] out_12,
  output [31:0] out_13,
  output [31:0] out_14,
  output [31:0] out_15,
  output [31:0] out_16,
  output [31:0] out_17,
  output [31:0] out_18,
  output [31:0] out_19,
  output [31:0] out_20,
  output [31:0] out_21
);

  Multiplexer #(.select(2), .width(32)) multiplexer_1 (
    .in0({32{1'b0}}), .in1({32{1'b0}}), .in2({32{1'b0}}), .in3({32{1'b0}}), .out(out_2), .sel(in_1));  // open: en
  DotMatrix #(.matrixcols(20), .matrixrows(32)) dotmatrix_1 (
    .col0({32{1'b0}}), .col1({32{1'b0}}), .col2(32'h3ffffffc), .col3(32'h3ffffffc), .col4(32'h3ffffffc),
    .col5(32'h3ffffffc), .col6(32'h3c00003c), .col7(32'h3c00003c), .col8(32'h3c00003c), .col9(32'h3c00003c),
    .col10(32'h3c00003c), .col11(32'h3c00003c), .col12(32'h3c00003c), .col13(32'h3c00003c),
    .col14(32'h3ffffffc), .col15(32'h3ffffffc), .col16(32'h3ffffffc), .col17(32'h3ffffffc),
    .col18({32{1'b0}}), .col19({32{1'b0}}));
  Multiplexer #(.select(2), .width(32)) multiplexer_2 (
    .in0({32{1'b0}}), .in1({32{1'b0}}), .in2(32'h3e000000), .in3({32{1'b0}}), .out(out_3), .sel(in_1));  // open: en
  Multiplexer #(.select(2), .width(32)) multiplexer_3 (
    .in0({32{1'b0}}), .in1(32'h3ffffffc), .in2(32'h3e000000), .in3({32{1'b0}}), .out(out_4), .sel(in_1));  // open: en
  Multiplexer #(.select(2), .width(32)) multiplexer_4 (
    .in0({32{1'b0}}), .in1(32'h3ffffffc), .in2(32'h3e000000), .in3({32{1'b0}}), .out(out_5), .sel(in_1));  // open: en
  Multiplexer #(.select(2), .width(32)) multiplexer_5 (
    .in0({32{1'b0}}), .in1(32'h3ffffffc), .in2(32'h3e000000), .in3({32{1'b0}}), .out(out_6), .sel(in_1));  // open: en
  DotMatrix #(.matrixcols(20), .matrixrows(32)) dotmatrix_2 (
    .col0({32{1'b0}}), .col1(32'h3e000000), .col2(32'h3e000000), .col3(32'h3e000000), .col4(32'h3e000000),
    .col5(32'h3e000000), .col6(32'h3e000000), .col7(32'h3ffffffc), .col8(32'h3ffffffc), .col9(32'h3ffffffc),
    .col10(32'h3ffffffc), .col11(32'h3ffffffc), .col12(32'h3ffffffc), .col13(32'h3e000000),
    .col14(32'h3e000000), .col15(32'h3e000000), .col16(32'h3e000000), .col17(32'h3e000000),
    .col18(32'h3e000000), .col19({32{1'b0}}));
  Multiplexer #(.select(2), .width(32)) multiplexer_6 (
    .in0({32{1'b0}}), .in1(32'h3ffffffc), .in2(32'h3e000000), .in3({32{1'b0}}), .out(out_7), .sel(in_1));  // open: en
  Multiplexer #(.select(2), .width(32)) multiplexer_7 (
    .in0({32{1'b0}}), .in1(32'h3c00003c), .in2(32'h3e000000), .in3({32{1'b0}}), .out(out_8), .sel(in_1));  // open: en
  Multiplexer #(.select(2), .width(32)) multiplexer_8 (
    .in0({32{1'b0}}), .in1(32'h3c00003c), .in2(32'h3ffffffc), .in3({32{1'b0}}), .out(out_9), .sel(in_1));  // open: en
  Multiplexer #(.select(2), .width(32)) multiplexer_9 (
    .in0({32{1'b0}}), .in1(32'h3c00003c), .in2(32'h3ffffffc), .in3({32{1'b0}}), .out(out_10), .sel(in_1));  // open: en
  Multiplexer #(.select(2), .width(32)) multiplexer_10 (
    .in0({32{1'b0}}), .in1(32'h3c00003c), .in2(32'h3ffffffc), .in3({32{1'b0}}), .out(out_11), .sel(in_1));  // open: en
  Multiplexer #(.select(2), .width(32)) multiplexer_11 (
    .in0({32{1'b0}}), .in1(32'h3c00003c), .in2(32'h3ffffffc), .in3({32{1'b0}}), .out(out_12), .sel(in_1));  // open: en
  Multiplexer #(.select(2), .width(32)) multiplexer_12 (
    .in0({32{1'b0}}), .in1(32'h3c00003c), .in2(32'h3ffffffc), .in3({32{1'b0}}), .out(out_13), .sel(in_1));  // open: en
  Multiplexer #(.select(2), .width(32)) multiplexer_13 (
    .in0({32{1'b0}}), .in1(32'h3c00003c), .in2(32'h3ffffffc), .in3({32{1'b0}}), .out(out_14), .sel(in_1));  // open: en
  Multiplexer #(.select(2), .width(32)) multiplexer_14 (
    .in0({32{1'b0}}), .in1(32'h3c00003c), .in2(32'h3e000000), .in3({32{1'b0}}), .out(out_15), .sel(in_1));  // open: en
  Multiplexer #(.select(2), .width(32)) multiplexer_15 (
    .in0({32{1'b0}}), .in1(32'h3ffffffc), .in2(32'h3e000000), .in3({32{1'b0}}), .out(out_16), .sel(in_1));  // open: en
  Multiplexer #(.select(2), .width(32)) multiplexer_16 (
    .in0({32{1'b0}}), .in1(32'h3ffffffc), .in2(32'h3e000000), .in3({32{1'b0}}), .out(out_17), .sel(in_1));  // open: en
  Multiplexer #(.select(2), .width(32)) multiplexer_17 (
    .in0({32{1'b0}}), .in1(32'h3ffffffc), .in2(32'h3e000000), .in3({32{1'b0}}), .out(out_18), .sel(in_1));  // open: en
  Multiplexer #(.select(2), .width(32)) multiplexer_18 (
    .in0({32{1'b0}}), .in1(32'h3ffffffc), .in2(32'h3e000000), .in3({32{1'b0}}), .out(out_19), .sel(in_1));  // open: en
  Multiplexer #(.select(2), .width(32)) multiplexer_19 (
    .in0({32{1'b0}}), .in1({32{1'b0}}), .in2(32'h3e000000), .in3({32{1'b0}}), .out(out_20), .sel(in_1));  // open: en
  Multiplexer #(.select(2), .width(32)) multiplexer_20 (
    .in0({32{1'b0}}), .in1({32{1'b0}}), .in2({32{1'b0}}), .in3({32{1'b0}}), .out(out_21), .sel(in_1));  // open: en
endmodule

module a_s (
  input  [1:0] in_1,
  output [31:0] out_2,
  output [31:0] out_3,
  output [31:0] out_4,
  output [31:0] out_5,
  output [31:0] out_6,
  output [31:0] out_7,
  output [31:0] out_8,
  output [31:0] out_9,
  output [31:0] out_10,
  output [31:0] out_11,
  output [31:0] out_12,
  output [31:0] out_13,
  output [31:0] out_14,
  output [31:0] out_15,
  output [31:0] out_16,
  output [31:0] out_17,
  output [31:0] out_18,
  output [31:0] out_19,
  output [31:0] out_20,
  output [31:0] out_21
);

  Multiplexer #(.select(2), .width(32)) multiplexer_1 (
    .in0({32{1'b0}}), .in1({32{1'b0}}), .in2({32{1'b0}}), .in3({32{1'b0}}), .out(out_2), .sel(in_1));  // open: en
  DotMatrix #(.matrixcols(20), .matrixrows(32)) dotmatrix_1 (
    .col0({32{1'b0}}), .col1({32{1'b0}}), .col2(32'h3fffe0fe), .col3(32'h3fffe0fe), .col4(32'h3fffe0fe),
    .col5(32'h3fffe0fe), .col6(32'h3f83e0fe), .col7(32'h3f83e0fe), .col8(32'h3f83e0fe), .col9(32'h3f83e0fe),
    .col10(32'h3f83e0fe), .col11(32'h3f83e0fe), .col12(32'h3f83e0fe), .col13(32'h3f83fffe),
    .col14(32'h3f83fffe), .col15(32'h3f83fffe), .col16(32'h3f83fffe), .col17(32'h3f83fffe),
    .col18({32{1'b0}}), .col19({32{1'b0}}));
  Multiplexer #(.select(2), .width(32)) multiplexer_2 (
    .in0({32{1'b0}}), .in1({32{1'b0}}), .in2({32{1'b0}}), .in3({32{1'b0}}), .out(out_3), .sel(in_1));  // open: en
  Multiplexer #(.select(2), .width(32)) multiplexer_3 (
    .in0({32{1'b0}}), .in1(32'h3fffe0fe), .in2({32{1'b0}}), .in3({32{1'b0}}), .out(out_4), .sel(in_1));  // open: en
  Multiplexer #(.select(2), .width(32)) multiplexer_4 (
    .in0({32{1'b0}}), .in1(32'h3fffe0fe), .in2(32'h3fffffc), .in3({32{1'b0}}), .out(out_5), .sel(in_1));  // open: en
  Multiplexer #(.select(2), .width(32)) multiplexer_5 (
    .in0({32{1'b0}}), .in1(32'h3fffe0fe), .in2(32'hffffffc), .in3({32{1'b0}}), .out(out_6), .sel(in_1));  // open: en
  DotMatrix #(.matrixcols(20), .matrixrows(32)) dotmatrix_2 (
    .col0({32{1'b0}}), .col1({32{1'b0}}), .col2({32{1'b0}}), .col3(32'h3fffffc), .col4(32'hffffffc),
    .col5(32'h1ffffffc), .col6(32'h1ffffffc), .col7(32'h3f007c00), .col8(32'h3e007c00), .col9(32'h3c007c00),
    .col10(32'h3c007c00), .col11(32'h3e007c00), .col12(32'h3f007c00), .col13(32'h1ffffffc),
    .col14(32'h1ffffffc), .col15(32'hffffffc), .col16(32'h3fffffc), .col17({32{1'b0}}), .col18({32{1'b0}}),
    .col19({32{1'b0}}));
  Multiplexer #(.select(2), .width(32)) multiplexer_6 (
    .in0({32{1'b0}}), .in1(32'h3fffe0fe), .in2(32'h1ffffffc), .in3({32{1'b0}}), .out(out_7), .sel(in_1));  // open: en
  Multiplexer #(.select(2), .width(32)) multiplexer_7 (
    .in0({32{1'b0}}), .in1(32'h3f83e0fe), .in2(32'h1ffffffc), .in3({32{1'b0}}), .out(out_8), .sel(in_1));  // open: en
  Multiplexer #(.select(2), .width(32)) multiplexer_8 (
    .in0({32{1'b0}}), .in1(32'h3f83e0fe), .in2(32'h3f007c00), .in3({32{1'b0}}), .out(out_9), .sel(in_1));  // open: en
  Multiplexer #(.select(2), .width(32)) multiplexer_9 (
    .in0({32{1'b0}}), .in1(32'h3f83e0fe), .in2(32'h3e007c00), .in3({32{1'b0}}), .out(out_10), .sel(in_1));  // open: en
  Multiplexer #(.select(2), .width(32)) multiplexer_10 (
    .in0({32{1'b0}}), .in1(32'h3f83e0fe), .in2(32'h3c007c00), .in3({32{1'b0}}), .out(out_11), .sel(in_1));  // open: en
  Multiplexer #(.select(2), .width(32)) multiplexer_11 (
    .in0({32{1'b0}}), .in1(32'h3f83e0fe), .in2(32'h3c007c00), .in3({32{1'b0}}), .out(out_12), .sel(in_1));  // open: en
  Multiplexer #(.select(2), .width(32)) multiplexer_12 (
    .in0({32{1'b0}}), .in1(32'h3f83e0fe), .in2(32'h3e007c00), .in3({32{1'b0}}), .out(out_13), .sel(in_1));  // open: en
  Multiplexer #(.select(2), .width(32)) multiplexer_13 (
    .in0({32{1'b0}}), .in1(32'h3f83e0fe), .in2(32'h3f007c00), .in3({32{1'b0}}), .out(out_14), .sel(in_1));  // open: en
  Multiplexer #(.select(2), .width(32)) multiplexer_14 (
    .in0({32{1'b0}}), .in1(32'h3f83fffe), .in2(32'h1ffffffc), .in3({32{1'b0}}), .out(out_15), .sel(in_1));  // open: en
  Multiplexer #(.select(2), .width(32)) multiplexer_15 (
    .in0({32{1'b0}}), .in1(32'h3f83fffe), .in2(32'h1ffffffc), .in3({32{1'b0}}), .out(out_16), .sel(in_1));  // open: en
  Multiplexer #(.select(2), .width(32)) multiplexer_16 (
    .in0({32{1'b0}}), .in1(32'h3f83fffe), .in2(32'hffffffc), .in3({32{1'b0}}), .out(out_17), .sel(in_1));  // open: en
  Multiplexer #(.select(2), .width(32)) multiplexer_17 (
    .in0({32{1'b0}}), .in1(32'h3f83fffe), .in2(32'h3fffffc), .in3({32{1'b0}}), .out(out_18), .sel(in_1));  // open: en
  Multiplexer #(.select(2), .width(32)) multiplexer_18 (
    .in0({32{1'b0}}), .in1(32'h3f83fffe), .in2({32{1'b0}}), .in3({32{1'b0}}), .out(out_19), .sel(in_1));  // open: en
  Multiplexer #(.select(2), .width(32)) multiplexer_19 (
    .in0({32{1'b0}}), .in1({32{1'b0}}), .in2({32{1'b0}}), .in3({32{1'b0}}), .out(out_20), .sel(in_1));  // open: en
  Multiplexer #(.select(2), .width(32)) multiplexer_20 (
    .in0({32{1'b0}}), .in1({32{1'b0}}), .in2({32{1'b0}}), .in3({32{1'b0}}), .out(out_21), .sel(in_1));  // open: en
endmodule

module r_s (
  input  [1:0] in_1,
  output [31:0] out_2,
  output [31:0] out_3,
  output [31:0] out_4,
  output [31:0] out_5,
  output [31:0] out_6,
  output [31:0] out_7,
  output [31:0] out_8,
  output [31:0] out_9,
  output [31:0] out_10,
  output [31:0] out_11,
  output [31:0] out_12,
  output [31:0] out_13,
  output [31:0] out_14,
  output [31:0] out_15,
  output [31:0] out_16,
  output [31:0] out_17,
  output [31:0] out_18,
  output [31:0] out_19,
  output [31:0] out_20,
  output [31:0] out_21
);

  Multiplexer #(.select(2), .width(32)) multiplexer_1 (
    .in0({32{1'b0}}), .in1({32{1'b0}}), .in2({32{1'b0}}), .in3({32{1'b0}}), .out(out_2), .sel(in_1));  // open: en
  DotMatrix #(.matrixcols(20), .matrixrows(32)) dotmatrix_1 (
    .col0({32{1'b0}}), .col1({32{1'b0}}), .col2(32'h3fffe0fe), .col3(32'h3fffe0fe), .col4(32'h3fffe0fe),
    .col5(32'h3fffe0fe), .col6(32'h3f83e0fe), .col7(32'h3f83e0fe), .col8(32'h3f83e0fe), .col9(32'h3f83e0fe),
    .col10(32'h3f83e0fe), .col11(32'h3f83e0fe), .col12(32'h3f83e0fe), .col13(32'h3f83fffe),
    .col14(32'h3f83fffe), .col15(32'h3f83fffe), .col16(32'h3f83fffe), .col17(32'h3f83fffe),
    .col18({32{1'b0}}), .col19({32{1'b0}}));
  Multiplexer #(.select(2), .width(32)) multiplexer_2 (
    .in0({32{1'b0}}), .in1({32{1'b0}}), .in2({32{1'b0}}), .in3({32{1'b0}}), .out(out_3), .sel(in_1));  // open: en
  Multiplexer #(.select(2), .width(32)) multiplexer_3 (
    .in0({32{1'b0}}), .in1(32'h3fffe0fe), .in2(32'hffffffe), .in3({32{1'b0}}), .out(out_4), .sel(in_1));  // open: en
  Multiplexer #(.select(2), .width(32)) multiplexer_4 (
    .in0({32{1'b0}}), .in1(32'h3fffe0fe), .in2(32'h1ffffffe), .in3({32{1'b0}}), .out(out_5), .sel(in_1));  // open: en
  Multiplexer #(.select(2), .width(32)) multiplexer_5 (
    .in0({32{1'b0}}), .in1(32'h3fffe0fe), .in2(32'h3ffffffe), .in3({32{1'b0}}), .out(out_6), .sel(in_1));  // open: en
  DotMatrix #(.matrixcols(20), .matrixrows(32)) dotmatrix_2 (
    .col0({32{1'b0}}), .col1({32{1'b0}}), .col2(32'hffffffe), .col3(32'h1ffffffe), .col4(32'h3ffffffe),
    .col5(32'h3ffffffe), .col6(32'h3c1ffffe), .col7(32'h3c1dc000), .col8(32'h3c1dc000), .col9(32'h3c1de000),
    .col10(32'h3c1df800), .col11(32'h3c1dfe00), .col12(32'h3c1c7f80), .col13(32'h3c1c3fc0),
    .col14(32'h3c1c0ff0), .col15(32'h1ff801fe), .col16(32'h1ff8007e), .col17(32'hff0001e),
    .col18({32{1'b0}}), .col19({32{1'b0}}));
  Multiplexer #(.select(2), .width(32)) multiplexer_6 (
    .in0({32{1'b0}}), .in1(32'h3fffe0fe), .in2(32'h3ffffffe), .in3({32{1'b0}}), .out(out_7), .sel(in_1));  // open: en
  Multiplexer #(.select(2), .width(32)) multiplexer_7 (
    .in0({32{1'b0}}), .in1(32'h3f83e0fe), .in2(32'h3c1ffffe), .in3({32{1'b0}}), .out(out_8), .sel(in_1));  // open: en
  Multiplexer #(.select(2), .width(32)) multiplexer_8 (
    .in0({32{1'b0}}), .in1(32'h3f83e0fe), .in2(32'h3c1dc000), .in3({32{1'b0}}), .out(out_9), .sel(in_1));  // open: en
  Multiplexer #(.select(2), .width(32)) multiplexer_9 (
    .in0({32{1'b0}}), .in1(32'h3f83e0fe), .in2(32'h3c1dc000), .in3({32{1'b0}}), .out(out_10), .sel(in_1));  // open: en
  Multiplexer #(.select(2), .width(32)) multiplexer_10 (
    .in0({32{1'b0}}), .in1(32'h3f83e0fe), .in2(32'h3c1de000), .in3({32{1'b0}}), .out(out_11), .sel(in_1));  // open: en
  Multiplexer #(.select(2), .width(32)) multiplexer_11 (
    .in0({32{1'b0}}), .in1(32'h3f83e0fe), .in2(32'h3c1df800), .in3({32{1'b0}}), .out(out_12), .sel(in_1));  // open: en
  Multiplexer #(.select(2), .width(32)) multiplexer_12 (
    .in0({32{1'b0}}), .in1(32'h3f83e0fe), .in2(32'h3c1dfe00), .in3({32{1'b0}}), .out(out_13), .sel(in_1));  // open: en
  Multiplexer #(.select(2), .width(32)) multiplexer_13 (
    .in0({32{1'b0}}), .in1(32'h3f83e0fe), .in2(32'h3c1c7f80), .in3({32{1'b0}}), .out(out_14), .sel(in_1));  // open: en
  Multiplexer #(.select(2), .width(32)) multiplexer_14 (
    .in0({32{1'b0}}), .in1(32'h3f83fffe), .in2(32'h3c1c3fc0), .in3({32{1'b0}}), .out(out_15), .sel(in_1));  // open: en
  Multiplexer #(.select(2), .width(32)) multiplexer_15 (
    .in0({32{1'b0}}), .in1(32'h3f83fffe), .in2(32'h3c1c0ff0), .in3({32{1'b0}}), .out(out_16), .sel(in_1));  // open: en
  Multiplexer #(.select(2), .width(32)) multiplexer_16 (
    .in0({32{1'b0}}), .in1(32'h3f83fffe), .in2(32'h1ff801fe), .in3({32{1'b0}}), .out(out_17), .sel(in_1));  // open: en
  Multiplexer #(.select(2), .width(32)) multiplexer_17 (
    .in0({32{1'b0}}), .in1(32'h3f83fffe), .in2(32'h1ff8007e), .in3({32{1'b0}}), .out(out_18), .sel(in_1));  // open: en
  Multiplexer #(.select(2), .width(32)) multiplexer_18 (
    .in0({32{1'b0}}), .in1(32'h3f83fffe), .in2(32'hff0001e), .in3({32{1'b0}}), .out(out_19), .sel(in_1));  // open: en
  Multiplexer #(.select(2), .width(32)) multiplexer_19 (
    .in0({32{1'b0}}), .in1({32{1'b0}}), .in2({32{1'b0}}), .in3({32{1'b0}}), .out(out_20), .sel(in_1));  // open: en
  Multiplexer #(.select(2), .width(32)) multiplexer_20 (
    .in0({32{1'b0}}), .in1({32{1'b0}}), .in2({32{1'b0}}), .in3({32{1'b0}}), .out(out_21), .sel(in_1));  // open: en
endmodule

module t (
  input  [1:0] in_1,
  output [31:0] out_2,
  output [31:0] out_3,
  output [31:0] out_4,
  output [31:0] out_5,
  output [31:0] out_6,
  output [31:0] out_7,
  output [31:0] out_8,
  output [31:0] out_9,
  output [31:0] out_10,
  output [31:0] out_11,
  output [31:0] out_12,
  output [31:0] out_13,
  output [31:0] out_14,
  output [31:0] out_15,
  output [31:0] out_16,
  output [31:0] out_17,
  output [31:0] out_18,
  output [31:0] out_19,
  output [31:0] out_20,
  output [31:0] out_21
);

  Multiplexer #(.select(2), .width(32)) multiplexer_1 (
    .in0({32{1'b0}}), .in1({32{1'b0}}), .in2({32{1'b0}}), .in3({32{1'b0}}), .out(out_2), .sel(in_1));  // open: en
  DotMatrix #(.matrixcols(20), .matrixrows(32)) dotmatrix_1 (
    .col0({32{1'b0}}), .col1({32{1'b0}}), .col2({32{1'b0}}), .col3({32{1'b0}}), .col4({32{1'b0}}),
    .col5({32{1'b0}}), .col6({32{1'b0}}), .col7(32'h3ffffe7c), .col8(32'h3ffffe7c), .col9(32'h3ffffe7c),
    .col10(32'h3ffffe7c), .col11(32'h3ffffe7c), .col12(32'h3ffffe7c), .col13(32'h3ffffe7c),
    .col14({32{1'b0}}), .col15({32{1'b0}}), .col16({32{1'b0}}), .col17({32{1'b0}}), .col18({32{1'b0}}),
    .col19({32{1'b0}}));
  Multiplexer #(.select(2), .width(32)) multiplexer_2 (
    .in0({32{1'b0}}), .in1({32{1'b0}}), .in2(32'h3e000000), .in3({32{1'b0}}), .out(out_3), .sel(in_1));  // open: en
  Multiplexer #(.select(2), .width(32)) multiplexer_3 (
    .in0({32{1'b0}}), .in1({32{1'b0}}), .in2(32'h3e000000), .in3({32{1'b0}}), .out(out_4), .sel(in_1));  // open: en
  Multiplexer #(.select(2), .width(32)) multiplexer_4 (
    .in0({32{1'b0}}), .in1({32{1'b0}}), .in2(32'h3e000000), .in3({32{1'b0}}), .out(out_5), .sel(in_1));  // open: en
  Multiplexer #(.select(2), .width(32)) multiplexer_5 (
    .in0({32{1'b0}}), .in1({32{1'b0}}), .in2(32'h3e000000), .in3({32{1'b0}}), .out(out_6), .sel(in_1));  // open: en
  DotMatrix #(.matrixcols(20), .matrixrows(32)) dotmatrix_2 (
    .col0({32{1'b0}}), .col1(32'h3e000000), .col2(32'h3e000000), .col3(32'h3e000000), .col4(32'h3e000000),
    .col5(32'h3e000000), .col6(32'h3e000000), .col7(32'h3ffffffc), .col8(32'h3ffffffc), .col9(32'h3ffffffc),
    .col10(32'h3ffffffc), .col11(32'h3ffffffc), .col12(32'h3ffffffc), .col13(32'h3e000000),
    .col14(32'h3e000000), .col15(32'h3e000000), .col16(32'h3e000000), .col17(32'h3e000000),
    .col18(32'h3e000000), .col19({32{1'b0}}));
  Multiplexer #(.select(2), .width(32)) multiplexer_6 (
    .in0({32{1'b0}}), .in1({32{1'b0}}), .in2(32'h3e000000), .in3({32{1'b0}}), .out(out_7), .sel(in_1));  // open: en
  Multiplexer #(.select(2), .width(32)) multiplexer_7 (
    .in0({32{1'b0}}), .in1({32{1'b0}}), .in2(32'h3e000000), .in3({32{1'b0}}), .out(out_8), .sel(in_1));  // open: en
  Multiplexer #(.select(2), .width(32)) multiplexer_8 (
    .in0({32{1'b0}}), .in1(32'h3ffffe7c), .in2(32'h3ffffffc), .in3({32{1'b0}}), .out(out_9), .sel(in_1));  // open: en
  Multiplexer #(.select(2), .width(32)) multiplexer_9 (
    .in0({32{1'b0}}), .in1(32'h3ffffe7c), .in2(32'h3ffffffc), .in3({32{1'b0}}), .out(out_10), .sel(in_1));  // open: en
  Multiplexer #(.select(2), .width(32)) multiplexer_10 (
    .in0({32{1'b0}}), .in1(32'h3ffffe7c), .in2(32'h3ffffffc), .in3({32{1'b0}}), .out(out_11), .sel(in_1));  // open: en
  Multiplexer #(.select(2), .width(32)) multiplexer_11 (
    .in0({32{1'b0}}), .in1(32'h3ffffe7c), .in2(32'h3ffffffc), .in3({32{1'b0}}), .out(out_12), .sel(in_1));  // open: en
  Multiplexer #(.select(2), .width(32)) multiplexer_12 (
    .in0({32{1'b0}}), .in1(32'h3ffffe7c), .in2(32'h3ffffffc), .in3({32{1'b0}}), .out(out_13), .sel(in_1));  // open: en
  Multiplexer #(.select(2), .width(32)) multiplexer_13 (
    .in0({32{1'b0}}), .in1(32'h3ffffe7c), .in2(32'h3ffffffc), .in3({32{1'b0}}), .out(out_14), .sel(in_1));  // open: en
  Multiplexer #(.select(2), .width(32)) multiplexer_14 (
    .in0({32{1'b0}}), .in1(32'h3ffffe7c), .in2(32'h3e000000), .in3({32{1'b0}}), .out(out_15), .sel(in_1));  // open: en
  Multiplexer #(.select(2), .width(32)) multiplexer_15 (
    .in0({32{1'b0}}), .in1({32{1'b0}}), .in2(32'h3e000000), .in3({32{1'b0}}), .out(out_16), .sel(in_1));  // open: en
  Multiplexer #(.select(2), .width(32)) multiplexer_16 (
    .in0({32{1'b0}}), .in1({32{1'b0}}), .in2(32'h3e000000), .in3({32{1'b0}}), .out(out_17), .sel(in_1));  // open: en
  Multiplexer #(.select(2), .width(32)) multiplexer_17 (
    .in0({32{1'b0}}), .in1({32{1'b0}}), .in2(32'h3e000000), .in3({32{1'b0}}), .out(out_18), .sel(in_1));  // open: en
  Multiplexer #(.select(2), .width(32)) multiplexer_18 (
    .in0({32{1'b0}}), .in1({32{1'b0}}), .in2(32'h3e000000), .in3({32{1'b0}}), .out(out_19), .sel(in_1));  // open: en
  Multiplexer #(.select(2), .width(32)) multiplexer_19 (
    .in0({32{1'b0}}), .in1({32{1'b0}}), .in2(32'h3e000000), .in3({32{1'b0}}), .out(out_20), .sel(in_1));  // open: en
  Multiplexer #(.select(2), .width(32)) multiplexer_20 (
    .in0({32{1'b0}}), .in1({32{1'b0}}), .in2({32{1'b0}}), .in3({32{1'b0}}), .out(out_21), .sel(in_1));  // open: en
endmodule

module totalScreen (
  input  [1:0] in_1,
  output [31:0] out_2,
  output [31:0] out_3,
  output [31:0] out_4,
  output [31:0] out_5,
  output [31:0] out_6,
  output [31:0] out_7,
  output [31:0] out_8,
  output [31:0] out_9,
  output [31:0] out_10,
  output [31:0] out_11,
  output [31:0] out_12,
  output [31:0] out_13,
  output [31:0] out_14,
  output [31:0] out_15,
  output [31:0] out_16,
  output [31:0] out_17,
  output [31:0] out_18,
  output [31:0] out_19,
  output [31:0] out_20,
  output [31:0] out_21,
  output [31:0] out_22,
  output [31:0] out_23,
  output [31:0] out_24,
  output [31:0] out_25,
  output [31:0] out_26,
  output [31:0] out_27,
  output [31:0] out_28,
  output [31:0] out_29,
  output [31:0] out_30,
  output [31:0] out_31,
  output [31:0] out_32,
  output [31:0] out_33,
  output [31:0] out_34,
  output [31:0] out_35,
  output [31:0] out_36,
  output [31:0] out_37,
  output [31:0] out_38,
  output [31:0] out_39,
  output [31:0] out_40,
  output [31:0] out_41,
  output [31:0] out_42,
  output [31:0] out_43,
  output [31:0] out_44,
  output [31:0] out_45,
  output [31:0] out_46,
  output [31:0] out_47,
  output [31:0] out_48,
  output [31:0] out_49,
  output [31:0] out_50,
  output [31:0] out_51,
  output [31:0] out_52,
  output [31:0] out_53,
  output [31:0] out_54,
  output [31:0] out_55,
  output [31:0] out_56,
  output [31:0] out_57,
  output [31:0] out_58,
  output [31:0] out_59,
  output [31:0] out_60,
  output [31:0] out_61,
  output [31:0] out_62,
  output [31:0] out_63,
  output [31:0] out_64,
  output [31:0] out_65,
  output [31:0] out_66,
  output [31:0] out_67,
  output [31:0] out_68,
  output [31:0] out_69,
  output [31:0] out_70,
  output [31:0] out_71,
  output [31:0] out_72,
  output [31:0] out_73,
  output [31:0] out_74,
  output [31:0] out_75,
  output [31:0] out_76,
  output [31:0] out_77,
  output [31:0] out_78,
  output [31:0] out_79,
  output [31:0] out_80,
  output [31:0] out_81,
  output [31:0] out_82,
  output [31:0] out_83,
  output [31:0] out_84,
  output [31:0] out_85,
  output [31:0] out_86,
  output [31:0] out_87,
  output [31:0] out_88,
  output [31:0] out_89,
  output [31:0] out_90,
  output [31:0] out_91,
  output [31:0] out_92,
  output [31:0] out_93,
  output [31:0] out_94,
  output [31:0] out_95,
  output [31:0] out_96,
  output [31:0] out_97,
  output [31:0] out_98,
  output [31:0] out_99,
  output [31:0] out_100,
  output [31:0] out_101
);

  S_L s_l_1 (
    .in_1(in_1), .out_2(out_2), .out_3(out_3), .out_4(out_4), .out_5(out_5), .out_6(out_6), .out_7(out_7),
    .out_8(out_8), .out_9(out_9), .out_10(out_10), .out_11(out_11), .out_12(out_12), .out_13(out_13),
    .out_14(out_14), .out_15(out_15), .out_16(out_16), .out_17(out_17), .out_18(out_18), .out_19(out_19),
    .out_20(out_20), .out_21(out_21));
  t_o t_o_1 (
    .in_1(in_1), .out_2(out_22), .out_3(out_23), .out_4(out_24), .out_5(out_25), .out_6(out_26),
    .out_7(out_27), .out_8(out_28), .out_9(out_29), .out_10(out_30), .out_11(out_31), .out_12(out_32),
    .out_13(out_33), .out_14(out_34), .out_15(out_35), .out_16(out_36), .out_17(out_37), .out_18(out_38),
    .out_19(out_39), .out_20(out_40), .out_21(out_41));
  a_s a_s_1 (
    .in_1(in_1), .out_2(out_42), .out_3(out_43), .out_4(out_44), .out_5(out_45), .out_6(out_46),
    .out_7(out_47), .out_8(out_48), .out_9(out_49), .out_10(out_50), .out_11(out_51), .out_12(out_52),
    .out_13(out_53), .out_14(out_54), .out_15(out_55), .out_16(out_56), .out_17(out_57), .out_18(out_58),
    .out_19(out_59), .out_20(out_60), .out_21(out_61));
  r_s r_s_1 (
    .in_1(in_1), .out_2(out_62), .out_3(out_63), .out_4(out_64), .out_5(out_65), .out_6(out_66),
    .out_7(out_67), .out_8(out_68), .out_9(out_69), .out_10(out_70), .out_11(out_71), .out_12(out_72),
    .out_13(out_73), .out_14(out_74), .out_15(out_75), .out_16(out_76), .out_17(out_77), .out_18(out_78),
    .out_19(out_79), .out_20(out_80), .out_21(out_81));
  t t_1 (
    .in_1(in_1), .out_2(out_82), .out_3(out_83), .out_4(out_84), .out_5(out_85), .out_6(out_86),
    .out_7(out_87), .out_8(out_88), .out_9(out_89), .out_10(out_90), .out_11(out_91), .out_12(out_92),
    .out_13(out_93), .out_14(out_94), .out_15(out_95), .out_16(out_96), .out_17(out_97), .out_18(out_98),
    .out_19(out_99), .out_20(out_100), .out_21(out_101));
endmodule
