// Logisim project screenMessage.circ as structural Verilog: 6 circuits, main circuit S/L
module S_L (
  input  [1:0] in_1,
  output [31:0] out_2,
  output [31:0] out_3,
  output [31:0] out_4,
  output [31:0] out_5,
  output [31:0] out_6,
  output [31:0] out_7,
  output [31:0] out_8,
  output [31:0] out_9,
  output [31:0] out_10,
  output [31:0] out_11,
  output [31:0] out_12,
  output [31:0] out_13,
  output [31:0] out_14,
  output [31:0] out_15,
  output [31:0] out_16,
  output [31:0] out_17,
  output [31:0] out_18,
  output [31:0] out_19,
  output [31:0] out_20,
  output [31:0] out_21
);

  Multiplexer #(.select(2), .width(32)) multiplexer_1 (
    .in0({32{1'b0}}), .in1({32{1'b0}}), .in2({32{1'b0}}), .in3({32{1'b0}}), .out(out_2), .sel(in_1));  // open: en
  DotMatrix #(.matrixcols(20), .matrixrows(32)) dotmatrix_1 (
    .col0({32{1'b0}}), .col1({32{1'b0}}), .col2({32{1'b0}}), .col3(32'h3ffffffc), .col4(32'h3ffffffc),
    .col5(32'h3ffffffc), .col6(32'h3ffffffc), .col7(32'h3ffffffc), .col8(32'h3ffffffc), .col9(32'h3ffffffc),
    .col10(32'hfc), .col11(32'hfc), .col12(32'hfc), .col13(32'hfc), .col14(32'hfc), .col15(32'hfc),
    .col16(32'hfc), .col17(32'hfc), .col18({32{1'b0}}), .col19({32{1'b0}}));
  Multiplexer #(.select(2), .width(32)) multiplexer_2 (
    .in0({32{1'b0}}), .in1({32{1'b0}}), .in2({32{1'b0}}), .in3({32{1'b0}}), .out(out_3), .sel(in_1));  // open: en
  Multiplexer #(.select(2), .width(32)) multiplexer_3 (
    .in0({32{1'b0}}), .in1(32'h3fffe0fe), .in2({32{1'b0}}), .in3({32{1'b0}}), .out(out_4), .sel(in_1));  // open: en
  Multiplexer #(.select(2), .width(32)) multiplexer_4 (
    .in0(32'h3ffffffc), .in1(32'h3fffe0fe), .in2({32{1'b0}}), .in3({32{1'b0}}), .out(out_5), .sel(in_1));  // open: en
  Multiplexer #(.select(2), .width(32)) multiplexer_5 (
    .in0(32'h3ffffffc), .in1(32'h3fffe0fe), .in2({32{1'b0}}), .in3({32{1'b0}}), .out(out_6), .sel(in_1));  // open: en
  DotMatrix #(.matrixcols(20), .matrixrows(32)) dotmatrix_2 (
    .col0({32{1'b0}}), .col1({32{1'b0}}), .col2(32'h3fffe0fe), .col3(32'h3fffe0fe), .col4(32'h3fffe0fe),
    .col5(32'h3fffe0fe), .col6(32'h3f83e0fe), .col7(32'h3f83e0fe), .col8(32'h3f83e0fe), .col9(32'h3f83e0fe),
    .col10(32'h3f83e0fe), .col11(32'h3f83e0fe), .col12(32'h3f83e0fe), .col13(32'h3f83fffe),
    .col14(32'h3f83fffe), .col15(32'h3f83fffe), .col16(32'h3f83fffe), .col17(32'h3f83fffe),
    .col18({32{1'b0}}), .col19({32{1'b0}}));
  Multiplexer #(.select(2), .width(32)) multiplexer_6 (
    .in0(32'h3ffffffc), .in1(32'h3fffe0fe), .in2({32{1'b0}}), .in3({32{1'b0}}), .out(out_7), .sel(in_1));  // open: en
  Multiplexer #(.select(2), .width(32)) multiplexer_7 (
    .in0(32'h3ffffffc), .in1(32'h3f83e0fe), .in2({32{1'b0}}), .in3({32{1'b0}}), .out(out_8), .sel(in_1));  // open: en
  Multiplexer #(.select(2), .width(32)) multiplexer_8 (
    .in0(32'h3ffffffc), .in1(32'h3f83e0fe), .in2({32{1'b0}}), .in3({32{1'b0}}), .out(out_9), .sel(in_1));  // open: en
  Multiplexer #(.select(2), .width(32)) multiplexer_9 (
    .in0(32'h3ffffffc), .in1(32'h3f83e0fe), .in2({32{1'b0}}), .in3({32{1'b0}}), .out(out_10), .sel(in_1));  // open: en
  Multiplexer #(.select(2), .width(32)) multiplexer_10 (
    .in0(32'h3ffffffc), .in1(32'h3f83e0fe), .in2({32{1'b0}}), .in3({32{1'b0}}), .out(out_11), .sel(in_1));  // open: en
  Multiplexer #(.select(2), .width(32)) multiplexer_11 (
    .in0(32'hfc), .in1(32'h3f83e0fe), .in2({32{1'b0}}), .in3({32{1'b0}}), .out(out_12), .sel(in_1));  // open: en
  Multiplexer #(.select(2), .width(32)) multiplexer_12 (
    .in0(32'hfc), .in1(32'h3f83e0fe), .in2({32{1'b0}}), .in3({32{1'b0}}), .out(out_13), .sel(in_1));  // open: en
  Multiplexer #(.select(2), .width(32)) multiplexer_13 (
    .in0(32'hfc), .in1(32'h3f83e0fe), .in2({32{1'b0}}), .in3({32{1'b0}}), .out(out_14), .sel(in_1));  // open: en
  Multiplexer #(.select(2), .width(32)) multiplexer_14 (
    .in0(32'hfc), .in1(32'h3f83fffe), .in2({32{1'b0}}), .in3({32{1'b0}}), .out(out_15), .sel(in_1));  // open: en
  Multiplexer #(.select(2), .width(32)) multiplexer_15 (
    .in0(32'hfc), .in1(32'h3f83fffe), .in2({32{1'b0}}), .in3({32{1'b0}}), .out(out_16), .sel(in_1));  // open: en
  Multiplexer #(.select(2), .width(32)) multiplexer_16 (
    .in0(32'hfc), .in1(32'h3f83fffe), .in2({32{1'b0}}), .in3({32{1'b0}}), .out(out_17), .sel(in_1));  // open: en
  Multiplexer #(.select(2), .width(32)) multiplexer_17 (
    .in0(32'hfc), .in1(32'h3f83fffe), .in2({32{1'b0}}), .in3({32{1'b0}}), .out(out_18), .sel(in_1));  // open: en
  Multiplexer #(.select(2), .width(32)) multiplexer_18 (
    .in0(32'hfc), .in1(32'h3f83fffe), .in2({32{1'b0}}), .in3({32{1'b0}}), .out(out_19), .sel(in_1));  // open: en
  Multiplexer #(.select(2), .width(32)) multiplexer_19 (
    .in0({32{1'b0}}), .in1({32{1'b0}}), .in2({32{1'b0}}), .in3({32{1'b0}}), .out(out_20), .sel(in_1));  // open: en
  Multiplexer #(.select(2), .width(32)) multiplexer_20 (
    .in0({32{1'b0}}), .in1({32{1'b0}}), .in2({32{1'b0}}), .in3({32{1'b0}}), .out(out_21), .sel(in_1));  // open: en
endmodule

module t_o (
  input  [1:0] in_1,
  output [31:0] out_2,
  output [31:0] out_3,
  output [31:0] out_4,
  output [31:0] out_5,
  output [31:0] out_6,
  output [31:0] out_7,
  output [31:0] out_8,
  output [31:0] out_9,
  output [31:0] out_10,
  output [31:0] out_11,
  output [31:0] out_12,
  output [31:0] out_13,
  output [31:0] out_14,
  output [31:0] out_15,
  output [31:0] out_16,
  output [31:0] out_17,
  output [31:0] out_18,
  output [31:0] out_19,
  output [31:0] out_20,
  output [31:0] out_21
);

  Multiplexer #(.select(2), .width(32)) multiplexer_1 (
    .in0({32{1'b0}}), .in1({32{1'b0}}), .in2({32{1'b0}}), .in3({32{1'b0}}), .out(out_2), .sel(in_1));  // open: en
  DotMatrix #(.matrixcols(20), .matrixrows(32)) dotmatrix_1 (
    .col0({32{1'b0}}), .col1({32{1'b0}}), .col2(32'h3ffffffc), .col3(32'h3ffffffc), .col4(32'h3ffffffc),
    .col5(32'h3ffffffc), .col6(32'h3c00003c), .col7(32'h3c00003c), .col8(32'h3c00003c), .col9(32'h3c00003c),
    .col10(32'h3c00003c), .col11(32'h3c00003c), .col12(32'h3c00003c), .col13(32'h3c00003c),
    .col14(32'h3ffffffc), .col15(32'h3ffffffc), .col16(32'h3ffffffc), .col17(32'h3ffffffc),
    .col18({32{1'b0}}), .col19({32{1'b0}}));
  Multiplexer #(.select(2), .width(32)) multiplexer_2 (
    .in0({32{1'b0}}), .in1(32'h3e000000), .in2({32{1'b0}}), .in3({32{1'b0}}), .out(out_3), .sel(in_1));  // open: en
  Multiplexer #(.select(2), .width(32)) multiplexer_3 (
    .in0(32'h3ffffffc), .in1(32'h3e000000), .in2({32{1'b0}}), .in3({32{1'b0}}), .out(out_4), .sel(in_1));  // open: en
  Multiplexer #(.select(2), .width(32)) multiplexer_4 (
    .in0(32'h3ffffffc), .in1(32'h3e000000), .in2({32{1'b0}}), .in3({32{1'b0}}), .out(out_5), .sel(in_1));  // open: en
  Multiplexer #(.select(2), .width(32)) multiplexer_5 (
    .in0(32'h3ffffffc), .in1(32'h3e000000), .in2({32{1'b0}}), .in3({32{1'b0}}), .out(out_6), .sel(in_1));  // open: en
  DotMatrix #(.matrixcols(20), .matrixrows(32)) dotmatrix_2 (
    .col0({32{1'b0}}), .col1(32'h3e000000), .col2(32'h3e000000), .col3(32'h3e000000), .col4(32'h3e000000),
    .col5(32'h3e000000), .col6(32'h3e000000), .col7(32'h3ffffffc), .col8(32'h3ffffffc), .col9(32'h3ffffffc),
    .col10(32'h3ffffffc), .col11(32'h3ffffffc), .col12(32'h3ffffffc), .col13(32'h3e000000),
    .col14(32'h3e000000), .col15(32'h3e000000), .col16(32'h3e000000), .col17(32'h3e000000),
    .col18(32'h3e000000), .col19({32{1'b0}}));
  Multiplexer #(.select(2), .width(32)) multiplexer_6 (
    .in0(32'h3ffffffc), .in1(32'h3e000000), .in2({32{1'b0}}), .in3({32{1'b0}}), .out(out_7), .sel(in_1));  // open: en
  Multiplexer #(.select(2), .width(32)) multiplexer_7 (
    .in0(32'h3c00003c), .in1(32'h3e000000), .in2({32{1'b0}}), .in3({32{1'b0}}), .out(out_8), .sel(in_1));  // open: en
  Multiplexer #(.select(2), .width(32)) multiplexer_8 (
    .in0(32'h3c00003c), .in1(32'h3ffffffc), .in2({32{1'b0}}), .in3({32{1'b0}}), .out(out_9), .sel(in_1));  // open: en
  Multiplexer #(.select(2), .width(32)) multiplexer_9 (
    .in0(32'h3c00003c), .in1(32'h3ffffffc), .in2({32{1'b0}}), .in3({32{1'b0}}), .out(out_10), .sel(in_1));  // open: en
  Multiplexer #(.select(2), .width(32)) multiplexer_10 (
    .in0(32'h3c00003c), .in1(32'h3ffffffc), .in2({32{1'b0}}), .in3({32{1'b0}}), .out(out_11), .sel(in_1));  // open: en
  Multiplexer #(.select(2), .width(32)) multiplexer_11 (
    .in0(32'h3c00003c), .in1(32'h3ffffffc), .in2({32{1'b0}}), .in3({32{1'b0}}), .out(out_12), .sel(in_1));  // open: en
  Multiplexer #(.select(2), .width(32)) multiplexer_12 (
    .in0(32'h3c00003c), .in1(32'h3ffffffc), .in2({32{1'b0}}), .in3({32{1'b0}}), .out(out_13), .sel(in_1));  // open: en
  Multiplexer #(.select(2), .width(32)) multiplexer_13 (
    .in0(32'h3c00003c), .in1(32'h3ffffffc), .in2({32{1'b0}}), .in3({32{1'b0}}), .out(out_14), .sel(in_1));  // open: en
  Multiplexer #(.select(2), .width(32)) multiplexer_14 (
    .in0(32'h3c00003c), .in1(32'h3e000000), .in2({32{1'b0}}), .in3({32{1'b0}}), .out(out_15), .sel(in_1));  // open: en
  Multiplexer #(.select(2), .width(32)) multiplexer_15 (
    .in0(32'h3ffffffc), .in1(32'h3e000000), .in2({32{1'b0}}), .in3({32{1'b0}}), .out(out_16), .sel(in_1));  // open: en
  Multiplexer #(.select(2), .width(32)) multiplexer_16 (
    .in0(32'h3ffffffc), .in1(32'h3e000000), .in2({32{1'b0}}), .in3({32{1'b0}}), .out(out_17), .sel(in_1));  // open: en
  Multiplexer #(.select(2), .width(32)) multiplexer_17 (
    .in0(32'h3ffffffc), .in1(32'h3e000000), .in2({32{1'b0}}), .in3({32{1'b0}}), .out(out_18), .sel(in_1));  // open: en
  Multiplexer #(.select(2), .width(32)) multiplexer_18 (
    .in0(32'h3ffffffc), .in1(32'h3e000000), .in2({32{1'b0}}), .in3({32{1'b0}}), .out(out_19), .sel(in_1));  // open: en
  Multiplexer #(.select(2), .width(32)) multiplexer_19 (
    .in0({32{1'b0}}), .in1(32'h3e000000), .in2({32{1'b0}}), .in3({32{1'b0}}), .out(out_20), .sel(in_1));  // open: en
  Multiplexer #(.select(2), .width(32)) multiplexer_20 (
    .in0({32{1'b0}}), .in1({32{1'b0}}), .in2({32{1'b0}}), .in3({32{1'b0}}), .out(out_21), .sel(in_1));  // open: en
endmodule

module a_s (
  input  [1:0] in_1,
  output [31:0] out_2,
  output [31:0] out_3,
  output [31:0] out_4,
  output [31:0] out_5,
  output [31:0] out_6,
  output [31:0] out_7,
  output [31:0] out_8,
  output [31:0] out_9,
  output [31:0] out_10,
  output [31:0] out_11,
  output [31:0] out_12,
  output [31:0] out_13,
  output [31:0] out_14,
  output [31:0] out_15,
  output [31:0] out_16,
  output [31:0] out_17,
  output [31:0] out_18,
  output [31:0] out_19,
  output [31:0] out_20,
  output [31:0] out_21
);

  Multiplexer #(.select(2), .width(32)) multiplexer_1 (
    .in0({32{1'b0}}), .in1({32{1'b0}}), .in2({32{1'b0}}), .in3({32{1'b0}}), .out(out_2), .sel(in_1));  // open: en
  DotMatrix #(.matrixcols(20), .matrixrows(32)) dotmatrix_1 (
    .col0({32{1'b0}}), .col1({32{1'b0}}), .col2(32'h3fffe0fe), .col3(32'h3fffe0fe), .col4(32'h3fffe0fe),
    .col5(32'h3fffe0fe), .col6(32'h3f83e0fe), .col7(32'h3f83e0fe), .col8(32'h3f83e0fe), .col9(32'h3f83e0fe),
    .col10(32'h3f83e0fe), .col11(32'h3f83e0fe), .col12(32'h3f83e0fe), .col13(32'h3f83fffe),
    .col14(32'h3f83fffe), .col15(32'h3f83fffe), .col16(32'h3f83fffe), .col17(32'h3f83fffe),
    .col18({32{1'b0}}), .col19({32{1'b0}}));
  Multiplexer #(.select(2), .width(32)) multiplexer_2 (
    .in0({32{1'b0}}), .in1({32{1'b0}}), .in2({32{1'b0}}), .in3({32{1'b0}}), .out(out_3), .sel(in_1));  // open: en
  Multiplexer #(.select(2), .width(32)) multiplexer_3 (
    .in0(32'h3fffe0fe), .in1({32{1'b0}}), .in2({32{1'b0}}), .in3({32{1'b0}}), .out(out_4), .sel(in_1));  // open: en
  Multiplexer #(.select(2), .width(32)) multiplexer_4 (
    .in0(32'h3fffe0fe), .in1(32'h3fffffc), .in2({32{1'b0}}), .in3({32{1'b0}}), .out(out_5), .sel(in_1));  // open: en
  Multiplexer #(.select(2), .width(32)) multiplexer_5 (
    .in0(32'h3fffe0fe), .in1(32'hffffffc), .in2({32{1'b0}}), .in3({32{1'b0}}), .out(out_6), .sel(in_1));  // open: en
  DotMatrix #(.matrixcols(20), .matrixrows(32)) dotmatrix_2 (
    .col0({32{1'b0}}), .col1({32{1'b0}}), .col2({32{1'b0}}), .col3(32'h3fffffc), .col4(32'hffffffc),
    .col5(32'h1ffffffc), .col6(32'h1ffffffc), .col7(32'h3f007c00), .col8(32'h3e007c00), .col9(32'h3c007c00),
    .col10(32'h3c007c00), .col11(32'h3e007c00), .col12(32'h3f007c00), .col13(32'h1ffffffc),
    .col14(32'h1ffffffc), .col15(32'hffffffc), .col16(32'h3fffffc), .col17({32{1'b0}}), .col18({32{1'b0}}),
    .col19({32{1'b0}}));
  Multiplexer #(.select(2), .width(32)) multiplexer_6 (
    .in0(32'h3fffe0fe), .in1(32'h1ffffffc), .in2({32{1'b0}}), .in3({32{1'b0}}), .out(out_7), .sel(in_1));  // open: en
  Multiplexer #(.select(2), .width(32)) multiplexer_7 (
    .in0(32'h3f83e0fe), .in1(32'h1ffffffc), .in2({32{1'b0}}), .in3({32{1'b0}}), .out(out_8), .sel(in_1));  // open: en
  Multiplexer #(.select(2), .width(32)) multiplexer_8 (
    .in0(32'h3f83e0fe), .in1(32'h3f007c00), .in2({32{1'b0}}), .in3({32{1'b0}}), .out(out_9), .sel(in_1));  // open: en
  Multiplexer #(.select(2), .width(32)) multiplexer_9 (
    .in0(32'h3f83e0fe), .in1(32'h3e007c00), .in2({32{1'b0}}), .in3({32{1'b0}}), .out(out_10), .sel(in_1));  // open: en
  Multiplexer #(.select(2), .width(32)) multiplexer_10 (
    .in0(32'h3f83e0fe), .in1(32'h3c007c00), .in2({32{1'b0}}), .in3({32{1'b0}}), .out(out_11), .sel(in_1));  // open: en
  Multiplexer #(.select(2), .width(32)) multiplexer_11 (
    .in0(32'h3f83e0fe), .in1(32'h3c007c00), .in2({32{1'b0}}), .in3({32{1'b0}}), .out(out_12), .sel(in_1));  // open: en
  Multiplexer #(.select(2), .width(32)) multiplexer_12 (
    .in0(32'h3f83e0fe), .in1(32'h3e007c00), .in2({32{1'b0}}), .in3({32{1'b0}}), .out(out_13), .sel(in_1));  // open: en
  Multiplexer #(.select(2), .width(32)) multiplexer_13 (
    .in0(32'h3f83e0fe), .in1(32'h3f007c00), .in2({32{1'b0}}), .in3({32{1'b0}}), .out(out_14), .sel(in_1));  // open: en
  Multiplexer #(.select(2), .width(32)) multiplexer_14 (
    .in0(32'h3f83fffe), .in1(32'h1ffffffc), .in2({32{1'b0}}), .in3({32{1'b0}}), .out(out_15), .sel(in_1));  // open: en
  Multiplexer #(.select(2), .width(32)) multiplexer_15 (
    .in0(32'h3f83fffe), .in1(32'h1ffffffc), .in2({32{1'b0}}), .in3({32{1'b0}}), .out(out_16), .sel(in_1));  // open: en
  Multiplexer #(.select(2), .width(32)) multiplexer_16 (
    .in0(32'h3f83fffe), .in1(32'hffffffc), .in2({32{1'b0}}), .in3({32{1'b0}}), .out(out_17), .sel(in_1));  // open: en
  Multiplexer #(.select(2), .width(32)) multiplexer_17 (
    .in0(32'h3f83fffe), .in1(32'h3fffffc), .in2({32{1'b0}}), .in3({32{1'b0}}), .out(out_18), .sel(in_1));  // open: en
  Multiplexer #(.select(2), .width(32)) multiplexer_18 (
    .in0(32'h3f83fffe), .in1({32{1'b0}}), .in2({32{1'b0}}), .in3({32{1'b0}}), .out(out_19), .sel(in_1));  // open: en
  Multiplexer #(.select(2), .width(32)) multiplexer_19 (
    .in0({32{1'b0}}), .in1({32{1'b0}}), .in2({32{1'b0}}), .in3({32{1'b0}}), .out(out_20), .sel(in_1));  // open: en
  Multiplexer #(.select(2), .width(32)) multiplexer_20 (
    .in0({32{1'b0}}), .in1({32{1'b0}}), .in2({32{1'b0}}), .in3({32{1'b0}}), .out(out_21), .sel(in_1));  // open: en
endmodule

module r_s (
  input  [1:0] in_1,
  output [31:0] out_2,
  output [31:0] out_3,
  output [31:0] out_4,
  output [31:0] out_5,
  output [31:0] out_6,
  output [31:0] out_7,
  output [31:0] out_8,
  output [31:0] out_9,
  output [31:0] out_10,
  output [31:0] out_11,
  output [31:0] out_12,
  output [31:0] out_13,
  output [31:0] out_14,
  output [31:0] out_15,
  output [31:0] out_16,
  output [31:0] out_17,
  output [31:0] out_18,
  output [31:0] out_19,
  output [31:0] out_20,
  output [31:0] out_21
);

  Multiplexer #(.select(2), .width(32)) multiplexer_1 (
    .in0({32{1'b0}}), .in1({32{1'b0}}), .in2({32{1'b0}}), .in3({32{1'b0}}), .out(out_2), .sel(in_1));  // open: en
  DotMatrix #(.matrixcols(20), .matrixrows(32)) dotmatrix_1 (
    .col0({32{1'b0}}), .col1({32{1'b0}}), .col2(32'h3fffe0fe), .col3(32'h3fffe0fe), .col4(32'h3fffe0fe),
    .col5(32'h3fffe0fe), .col6(32'h3f83e0fe), .col7(32'h3f83e0fe), .col8(32'h3f83e0fe), .col9(32'h3f83e0fe),
    .col10(32'h3f83e0fe), .col11(32'h3f83e0fe), .col12(32'h3f83e0fe), .col13(32'h3f83fffe),
    .col14(32'h3f83fffe), .col15(32'h3f83fffe), .col16(32'h3f83fffe), .col17(32'h3f83fffe),
    .col18({32{1'b0}}), .col19({32{1'b0}}));
  Multiplexer #(.select(2), .width(32)) multiplexer_2 (
    .in0({32{1'b0}}), .in1({32{1'b0}}), .in2({32{1'b0}}), .in3({32{1'b0}}), .out(out_3), .sel(in_1));  // open: en
  Multiplexer #(.select(2), .width(32)) multiplexer_3 (
    .in0(32'h3fffe0fe), .in1(32'hffffffe), .in2({32{1'b0}}), .in3({32{1'b0}}), .out(out_4), .sel(in_1));  // open: en
  Multiplexer #(.select(2), .width(32)) multiplexer_4 (
    .in0(32'h3fffe0fe), .in1(32'h1ffffffe), .in2({32{1'b0}}), .in3({32{1'b0}}), .out(out_5), .sel(in_1));  // open: en
  Multiplexer #(.select(2), .width(32)) multiplexer_5 (
    .in0(32'h3fffe0fe), .in1(32'h3ffffffe), .in2({32{1'b0}}), .in3({32{1'b0}}), .out(out_6), .sel(in_1));  // open: en
  DotMatrix #(.matrixcols(20), .matrixrows(32)) dotmatrix_2 (
    .col0({32{1'b0}}), .col1({32{1'b0}}), .col2(32'hffffffe), .col3(32'h1ffffffe), .col4(32'h3ffffffe),
    .col5(32'h3ffffffe), .col6(32'h3c1ffffe), .col7(32'h3c1dc000), .col8(32'h3c1dc000), .col9(32'h3c1de000),
    .col10(32'h3c1df800), .col11(32'h3c1dfe00), .col12(32'h3c1c7f80), .col13(32'h3c1c7f80),
    .col14(32'h3c1c0ff0), .col15(32'h1ff801fe), .col16(32'h1ff8007e), .col17(32'hff0001e),
    .col18({32{1'b0}}), .col19({32{1'b0}}));
  Multiplexer #(.select(2), .width(32)) multiplexer_6 (
    .in0(32'h3fffe0fe), .in1(32'h3ffffffe), .in2({32{1'b0}}), .in3({32{1'b0}}), .out(out_7), .sel(in_1));  // open: en
  Multiplexer #(.select(2), .width(32)) multiplexer_7 (
    .in0(32'h3f83e0fe), .in1(32'h3c1ffffe), .in2({32{1'b0}}), .in3({32{1'b0}}), .out(out_8), .sel(in_1));  // open: en
  Multiplexer #(.select(2), .width(32)) multiplexer_8 (
    .in0(32'h3f83e0fe), .in1(32'h3c1dc000), .in2({32{1'b0}}), .in3({32{1'b0}}), .out(out_9), .sel(in_1));  // open: en
  Multiplexer #(.select(2), .width(32)) multiplexer_9 (
    .in0(32'h3f83e0fe), .in1(32'h3c1dc000), .in2({32{1'b0}}), .in3({32{1'b0}}), .out(out_10), .sel(in_1));  // open: en
  Multiplexer #(.select(2), .width(32)) multiplexer_10 (
    .in0(32'h3f83e0fe), .in1(32'h3c1de000), .in2({32{1'b0}}), .in3({32{1'b0}}), .out(out_11), .sel(in_1));  // open: en
  Multiplexer #(.select(2), .width(32)) multiplexer_11 (
    .in0(32'h3f83e0fe), .in1(32'h3c1df800), .in2({32{1'b0}}), .in3({32{1'b0}}), .out(out_12), .sel(in_1));  // open: en
  Multiplexer #(.select(2), .width(32)) multiplexer_12 (
    .in0(32'h3f83e0fe), .in1(32'h3c1dfe00), .in2({32{1'b0}}), .in3({32{1'b0}}), .out(out_13), .sel(in_1));  // open: en
  Multiplexer #(.select(2), .width(32)) multiplexer_13 (
    .in0(32'h3f83e0fe), .in1(32'h3c1c7f80), .in2({32{1'b0}}), .in3({32{1'b0}}), .out(out_14), .sel(in_1));  // open: en
  Multiplexer #(.select(2), .width(32)) multiplexer_14 (
    .in0(32'h3f83fffe), .in1(32'h3c1c7f80), .in2({32{1'b0}}), .in3({32{1'b0}}), .out(out_15), .sel(in_1));  // open: en
  Multiplexer #(.select(2), .width(32)) multiplexer_15 (
    .in0(32'h3f83fffe), .in1(32'h3c1c0ff0), .in2({32{1'b0}}), .in3({32{1'b0}}), .out(out_16), .sel(in_1));  // open: en
  Multiplexer #(.select(2), .width(32)) multiplexer_16 (
    .in0(32'h3f83fffe), .in1(32'h1ff801fe), .in2({32{1'b0}}), .in3({32{1'b0}}), .out(out_17), .sel(in_1));  // open: en
  Multiplexer #(.select(2), .width(32)) multiplexer_17 (
    .in0(32'h3f83fffe), .in1(32'h1ff8007e), .in2({32{1'b0}}), .in3({32{1'b0}}), .out(out_18), .sel(in_1));  // open: en
  Multiplexer #(.select(2), .width(32)) multiplexer_18 (
    .in0(32'h3f83fffe), .in1(32'hff0001e), .in2({32{1'b0}}), .in3({32{1'b0}}), .out(out_19), .sel(in_1));  // open: en
  Multiplexer #(.select(2), .width(32)) multiplexer_19 (
    .in0({32{1'b0}}), .in1({32{1'b0}}), .in2({32{1'b0}}), .in3({32{1'b0}}), .out(out_20), .sel(in_1));  // open: en
  Multiplexer #(.select(2), .width(32)) multiplexer_20 (
    .in0({32{1'b0}}), .in1({32{1'b0}}), .in2({32{1'b0}}), .in3({32{1'b0}}), .out(out_21), .sel(in_1));  // open: en
endmodule

module t (
  input  [1:0] in_1,
  output [31:0] out_2,
  output [31:0] out_3,
  output [31:0] out_4,
  output [31:0] out_5,
  output [31:0] out_6,
  output [31:0] out_7,
  output [31:0] out_8,
  output [31:0] out_9,
  output [31:0] out_10,
  output [31:0] out_11,
  output [31:0] out_12,
  output [31:0] out_13,
  output [31:0] out_14,
  output [31:0] out_15,
  output [31:0] out_16,
  output [31:0] out_17,
  output [31:0] out_18,
  output [31:0] out_19,
  output [31:0] out_20,
  output [31:0] out_21
);

  Multiplexer #(.select(2), .width(32)) multiplexer_1 (
    .in0({32{1'b0}}), .in1({32{1'b0}}), .in2({32{1'b0}}), .in3({32{1'b0}}), .out(out_2), .sel(in_1));  // open: en
  DotMatrix #(.matrixcols(20), .matrixrows(32)) dotmatrix_1 (
    .col0({32{1'b0}}), .col1({32{1'b0}}), .col2({32{1'b0}}), .col3({32{1'b0}}), .col4({32{1'b0}}),
    .col5({32{1'b0}}), .col6({32{1'b0}}), .col7(32'h3ffffe7c), .col8(32'h3ffffe7c), .col9(32'h3ffffe7c),
    .col10(32'h3ffffe7c), .col11(32'h3ffffe7c), .col12(32'h3ffffe7c), .col13(32'h3ffffe7c),
    .col14({32{1'b0}}), .col15({32{1'b0}}), .col16({32{1'b0}}), .col17({32{1'b0}}), .col18({32{1'b0}}),
    .col19({32{1'b0}}));
  Multiplexer #(.select(2), .width(32)) multiplexer_2 (
    .in0({32{1'b0}}), .in1(32'h3e000000), .in2({32{1'b0}}), .in3({32{1'b0}}), .out(out_3), .sel(in_1));  // open: en
  Multiplexer #(.select(2), .width(32)) multiplexer_3 (
    .in0({32{1'b0}}), .in1(32'h3e000000), .in2({32{1'b0}}), .in3({32{1'b0}}), .out(out_4), .sel(in_1));  // open: en
  Multiplexer #(.select(2), .width(32)) multiplexer_4 (
    .in0({32{1'b0}}), .in1(32'h3e000000), .in2({32{1'b0}}), .in3({32{1'b0}}), .out(out_5), .sel(in_1));  // open: en
  Multiplexer #(.select(2), .width(32)) multiplexer_5 (
    .in0({32{1'b0}}), .in1(32'h3e000000), .in2({32{1'b0}}), .in3({32{1'b0}}), .out(out_6), .sel(in_1));  // open: en
  DotMatrix #(.matrixcols(20), .matrixrows(32)) dotmatrix_2 (
    .col0({32{1'b0}}), .col1(32'h3e000000), .col2(32'h3e000000), .col3(32'h3e000000), .col4(32'h3e000000),
    .col5(32'h3e000000), .col6(32'h3e000000), .col7(32'h3ffffffc), .col8(32'h3ffffffc), .col9(32'h3ffffffc),
    .col10(32'h3ffffffc), .col11(32'h3ffffffc), .col12(32'h3ffffffc), .col13(32'h3e000000),
    .col14(32'h3e000000), .col15(32'h3e000000), .col16(32'h3e000000), .col17(32'h3e000000),
    .col18(32'h3e000000), .col19({32{1'b0}}));
  Multiplexer #(.select(2), .width(32)) multiplexer_6 (
    .in0({32{1'b0}}), .in1(32'h3e000000), .in2({32{1'b0}}), .in3({32{1'b0}}), .out(out_7), .sel(in_1));  // open: en
  Multiplexer #(.select(2), .width(32)) multiplexer_7 (
    .in0({32{1'b0}}), .in1(32'h3e000000), .in2({32{1'b0}}), .in3({32{1'b0}}), .out(out_8), .sel(in_1));  // open: en
  Multiplexer #(.select(2), .width(32)) multiplexer_8 (
    .in0(32'h3ffffe7c), .in1(32'h3ffffffc), .in2({32{1'b0}}), .in3({32{1'b0}}), .out(out_9), .sel(in_1));  // open: en
  Multiplexer #(.select(2), .width(32)) multiplexer_9 (
    .in0(32'h3ffffe7c), .in1(32'h3ffffffc), .in2({32{1'b0}}), .in3({32{1'b0}}), .out(out_10), .sel(in_1));  // open: en
  Multiplexer #(.select(2), .width(32)) multiplexer_10 (
    .in0(32'h3ffffe7c), .in1(32'h3ffffffc), .in2({32{1'b0}}), .in3({32{1'b0}}), .out(out_11), .sel(in_1));  // open: en
  Multiplexer #(.select(2), .width(32)) multiplexer_11 (
    .in0(32'h3ffffe7c), .in1(32'h3ffffffc), .in2({32{1'b0}}), .in3({32{1'b0}}), .out(out_12), .sel(in_1));  // open: en
  Multiplexer #(.select(2), .width(32)) multiplexer_12 (
    .in0(32'h3ffffe7c), .in1(32'h3ffffffc), .in2({32{1'b0}}), .in3({32{1'b0}}), .out(out_13), .sel(in_1));  // open: en
  Multiplexer #(.select(2), .width(32)) multiplexer_13 (
    .in0(32'h3ffffe7c), .in1(32'h3ffffffc), .in2({32{1'b0}}), .in3({32{1'b0}}), .out(out_14), .sel(in_1));  // open: en
  Multiplexer #(.select(2), .width(32)) multiplexer_14 (
    .in0(32'h3ffffe7c), .in1(32'h3e000000), .in2({32{1'b0}}), .in3({32{1'b0}}), .out(out_15), .sel(in_1));  // open: en
  Multiplexer #(.select(2), .width(32)) multiplexer_15 (
    .in0({32{1'b0}}), .in1(32'h3e000000), .in2({32{1'b0}}), .in3({32{1'b0}}), .out(out_16), .sel(in_1));  // open: en
  Multiplexer #(.select(2), .width(32)) multiplexer_16 (
    .in0({32{1'b0}}), .in1(32'h3e000000), .in2({32{1'b0}}), .in3({32{1'b0}}), .out(out_17), .sel(in_1));  // open: en
  Multiplexer #(.select(2), .width(32)) multiplexer_17 (
    .in0({32{1'b0}}), .in1(32'h3e000000), .in2({32{1'b0}}), .in3({32{1'b0}}), .out(out_18), .sel(in_1));  // open: en
  Multiplexer #(.select(2), .width(32)) multiplexer_18 (
    .in0({32{1'b0}}), .in1(32'h3e000000), .in2({32{1'b0}}), .in3({32{1'b0}}), .out(out_19), .sel(in_1));  // open: en
  Multiplexer #(.select(2), .width(32)) multiplexer_19 (
    .in0({32{1'b0}}), .in1(32'h3e000000), .in2({32{1'b0}}), .in3({32{1'b0}}), .out(out_20), .sel(in_1));  // open: en
  Multiplexer #(.select(2), .width(32)) multiplexer_20 (
    .in0({32{1'b0}}), .in1({32{1'b0}}), .in2({32{1'b0}}), .in3({32{1'b0}}), .out(out_21), .sel(in_1));  // open: en
endmodule

module totalScreen (
  input  [1:0] in_1
);

  wire [31:0] a_s_1_out_2, a_s_1_out_3, a_s_1_out_4, a_s_1_out_5, a_s_1_out_6, a_s_1_out_7, a_s_1_out_8,
       a_s_1_out_9, a_s_1_out_10, a_s_1_out_11, a_s_1_out_12, a_s_1_out_13, a_s_1_out_14, a_s_1_out_15,
       a_s_1_out_16, a_s_1_out_17, a_s_1_out_18, a_s_1_out_19, a_s_1_out_20, a_s_1_out_21, r_s_1_out_2,
       r_s_1_out_3, r_s_1_out_4, r_s_1_out_5, r_s_1_out_6, r_s_1_out_7, r_s_1_out_8, r_s_1_out_9,
       r_s_1_out_10, r_s_1_out_11, r_s_1_out_12, r_s_1_out_13, r_s_1_out_14, r_s_1_out_15, r_s_1_out_16,
       r_s_1_out_17, r_s_1_out_18, r_s_1_out_19, r_s_1_out_20, r_s_1_out_21, s_l_1_out_2, s_l_1_out_3,
       s_l_1_out_4, s_l_1_out_5, s_l_1_out_6, s_l_1_out_7, s_l_1_out_8, s_l_1_out_9, s_l_1_out_10,
       s_l_1_out_11, s_l_1_out_12, s_l_1_out_13, s_l_1_out_14, s_l_1_out_15, s_l_1_out_16, s_l_1_out_17,
       s_l_1_out_18, s_l_1_out_19, s_l_1_out_20, s_l_1_out_21, t_1_out_2, t_1_out_3, t_1_out_4, t_1_out_5,
       t_1_out_6, t_1_out_7, t_1_out_8, t_1_out_9, t_1_out_10, t_1_out_11, t_1_out_12, t_1_out_13,
       t_1_out_14, t_1_out_15, t_1_out_16, t_1_out_17, t_1_out_18, t_1_out_19, t_1_out_20, t_1_out_21,
       t_o_1_out_2, t_o_1_out_3, t_o_1_out_4, t_o_1_out_5, t_o_1_out_6, t_o_1_out_7, t_o_1_out_8,
       t_o_1_out_9, t_o_1_out_10, t_o_1_out_11, t_o_1_out_12, t_o_1_out_13, t_o_1_out_14, t_o_1_out_15,
       t_o_1_out_16, t_o_1_out_17, t_o_1_out_18, t_o_1_out_19, t_o_1_out_20, t_o_1_out_21;

  DotMatrix #(.matrixcols(20), .matrixrows(32)) dotmatrix_1 (
    .col0(s_l_1_out_2), .col1(s_l_1_out_3), .col2(s_l_1_out_4), .col3(s_l_1_out_5), .col4(s_l_1_out_6),
    .col5(s_l_1_out_7), .col6(s_l_1_out_8), .col7(s_l_1_out_9), .col8(s_l_1_out_10), .col9(s_l_1_out_11),
    .col10(s_l_1_out_12), .col11(s_l_1_out_13), .col12(s_l_1_out_14), .col13(s_l_1_out_15),
    .col14(s_l_1_out_16), .col15(s_l_1_out_17), .col16(s_l_1_out_18), .col17(s_l_1_out_19),
    .col18(s_l_1_out_20), .col19(s_l_1_out_21));
  S_L s_l_1 (
    .in_1(in_1), .out_2(s_l_1_out_2), .out_3(s_l_1_out_3), .out_4(s_l_1_out_4), .out_5(s_l_1_out_5),
    .out_6(s_l_1_out_6), .out_7(s_l_1_out_7), .out_8(s_l_1_out_8), .out_9(s_l_1_out_9),
    .out_10(s_l_1_out_10), .out_11(s_l_1_out_11), .out_12(s_l_1_out_12), .out_13(s_l_1_out_13),
    .out_14(s_l_1_out_14), .out_15(s_l_1_out_15), .out_16(s_l_1_out_16), .out_17(s_l_1_out_17),
    .out_18(s_l_1_out_18), .out_19(s_l_1_out_19), .out_20(s_l_1_out_20), .out_21(s_l_1_out_21));
  t_o t_o_1 (
    .in_1(in_1), .out_2(t_o_1_out_2), .out_3(t_o_1_out_3), .out_4(t_o_1_out_4), .out_5(t_o_1_out_5),
    .out_6(t_o_1_out_6), .out_7(t_o_1_out_7), .out_8(t_o_1_out_8), .out_9(t_o_1_out_9),
    .out_10(t_o_1_out_10), .out_11(t_o_1_out_11), .out_12(t_o_1_out_12), .out_13(t_o_1_out_13),
    .out_14(t_o_1_out_14), .out_15(t_o_1_out_15), .out_16(t_o_1_out_16), .out_17(t_o_1_out_17),
    .out_18(t_o_1_out_18), .out_19(t_o_1_out_19), .out_20(t_o_1_out_20), .out_21(t_o_1_out_21));
  DotMatrix #(.matrixcols(20), .matrixrows(32)) dotmatrix_2 (
    .col0(t_o_1_out_2), .col1(t_o_1_out_3), .col2(t_o_1_out_4), .col3(t_o_1_out_5), .col4(t_o_1_out_6),
    .col5(t_o_1_out_7), .col6(t_o_1_out_8), .col7(t_o_1_out_9), .col8(t_o_1_out_10), .col9(t_o_1_out_11),
    .col10(t_o_1_out_12), .col11(t_o_1_out_13), .col12(t_o_1_out_14), .col13(t_o_1_out_15),
    .col14(t_o_1_out_16), .col15(t_o_1_out_17), .col16(t_o_1_out_18), .col17(t_o_1_out_19),
    .col18(t_o_1_out_20), .col19(t_o_1_out_21));
  DotMatrix #(.matrixcols(20), .matrixrows(32)) dotmatrix_3 (
    .col0(a_s_1_out_2), .col1(a_s_1_out_3), .col2(a_s_1_out_4), .col3(a_s_1_out_5), .col4(a_s_1_out_6),
    .col5(a_s_1_out_7), .col6(a_s_1_out_8), .col7(a_s_1_out_9), .col8(a_s_1_out_10), .col9(a_s_1_out_11),
    .col10(a_s_1_out_12), .col11(a_s_1_out_13), .col12(a_s_1_out_14), .col13(a_s_1_out_15),
    .col14(a_s_1_out_16), .col15(a_s_1_out_17), .col16(a_s_1_out_18), .col17(a_s_1_out_19),
    .col18(a_s_1_out_20), .col19(a_s_1_out_21));
  a_s a_s_1 (
    .in_1(in_1), .out_2(a_s_1_out_2), .out_3(a_s_1_out_3), .out_4(a_s_1_out_4), .out_5(a_s_1_out_5),
    .out_6(a_s_1_out_6), .out_7(a_s_1_out_7), .out_8(a_s_1_out_8), .out_9(a_s_1_out_9),
    .out_10(a_s_1_out_10), .out_11(a_s_1_out_11), .out_12(a_s_1_out_12), .out_13(a_s_1_out_13),
    .out_14(a_s_1_out_14), .out_15(a_s_1_out_15), .out_16(a_s_1_out_16), .out_17(a_s_1_out_17),
    .out_18(a_s_1_out_18), .out_19(a_s_1_out_19), .out_20(a_s_1_out_20), .out_21(a_s_1_out_21));
  DotMatrix #(.matrixcols(20), .matrixrows(32)) dotmatrix_4 (
    .col0(r_s_1_out_2), .col1(r_s_1_out_3), .col2(r_s_1_out_4), .col3(r_s_1_out_5), .col4(r_s_1_out_6),
    .col5(r_s_1_out_7), .col6(r_s_1_out_8), .col7(r_s_1_out_9), .col8(r_s_1_out_10), .col9(r_s_1_out_11),
    .col10(r_s_1_out_12), .col11(r_s_1_out_13), .col12(r_s_1_out_14), .col13(r_s_1_out_15),
    .col14(r_s_1_out_16), .col15(r_s_1_out_17), .col16(r_s_1_out_18), .col17(r_s_1_out_19),
    .col18(r_s_1_out_20), .col19(r_s_1_out_21));
  r_s r_s_1 (
    .in_1(in_1), .out_2(r_s_1_out_2), .out_3(r_s_1_out_3), .out_4(r_s_1_out_4), .out_5(r_s_1_out_5),
    .out_6(r_s_1_out_6), .out_7(r_s_1_out_7), .out_8(r_s_1_out_8), .out_9(r_s_1_out_9),
    .out_10(r_s_1_out_10), .out_11(r_s_1_out_11), .out_12(r_s_1_out_12), .out_13(r_s_1_out_13),
    .out_14(r_s_1_out_14), .out_15(r_s_1_out_15), .out_16(r_s_1_out_16), .out_17(r_s_1_out_17),
    .out_18(r_s_1_out_18), .out_19(r_s_1_out_19), .out_20(r_s_1_out_20), .out_21(r_s_1_out_21));
  DotMatrix #(.matrixcols(20), .matrixrows(32)) dotmatrix_5 (
    .col0(t_1_out_2), .col1(t_1_out_3), .col2(t_1_out_4), .col3(t_1_out_5), .col4(t_1_out_6),
    .col5(t_1_out_7), .col6(t_1_out_8), .col7(t_1_out_9), .col8(t_1_out_10), .col9(t_1_out_11),
    .col10(t_1_out_12), .col11(t_1_out_13), .col12(t_1_out_14), .col13(t_1_out_15), .col14(t_1_out_16),
    .col15(t_1_out_17), .col16(t_1_out_18), .col17(t_1_out_19), .col18(t_1_out_20), .col19(t_1_out_21));
  t t_1 (
    .in_1(in_1), .out_2(t_1_out_2), .out_3(t_1_out_3), .out_4(t_1_out_4), .out_5(t_1_out_5),
    .out_6(t_1_out_6), .out_7(t_1_out_7), .out_8(t_1_out_8), .out_9(t_1_out_9), .out_10(t_1_out_10),
    .out_11(t_1_out_11), .out_12(t_1_out_12), .out_13(t_1_out_13), .out_14(t_1_out_14), .out_15(t_1_out_15),
    .out_16(t_1_out_16), .out_17(t_1_out_17), .out_18(t_1_out_18), .out_19(t_1_out_19), .out_20(t_1_out_20),
    .out_21(t_1_out_21));
endmodule
