// Logisim project дисплеи10.circ as structural Verilog: 11 circuits, main circuit main
module main (
  input  in_1
);

  wire comparator_1_eq, not_1_out, not_2_out, rand_1_tick_1, rand_1_tick_2, taktdel_11_1_1_out_1,
       \vcyo_1_робит_ли_генератор , \vcyo_1_флаг_смерти ;
  wire [2:0] rand_1_rand_1, rand_1_rand_2;
  wire [3:0] vec_adr1, vec_adr2, vec_adr3, \из_16ричной_в_10_1_out_2 , \из_16ричной_в_10_1_out_3 ,
       \из_16ричной_в_10_1_out_4 ;
  wire [6:0] keyboard_1_data;
  wire [7:0] \cdm8_1_рекорд , \cdm8_1_счет ;
  wire [31:0] pipes_1_out_6, pipes_1_out_7, pipes_1_out_8, pipes_1_out_9, pipes_1_out_10, pipes_1_out_11,
       pipes_1_out_12, pipes_1_out_13, pipes_1_out_14, pipes_1_out_15, pipes_1_out_16, pipes_1_out_17,
       pipes_1_out_18, pipes_1_out_19, pipes_1_out_20, pipes_1_out_21, pipes_1_out_22, pipes_1_out_23,
       pipes_1_out_24, pipes_1_out_25, pipes_1_out_26, pipes_1_out_27, pipes_1_out_28, pipes_1_out_29,
       pipes_1_out_30, pipes_1_out_31, pipes_1_out_32, pipes_1_out_33, pipes_1_out_34, pipes_1_out_35,
       pipes_1_out_36, pipes_1_out_37, pipes_2_out_6, pipes_2_out_7, pipes_2_out_8, pipes_2_out_9,
       pipes_2_out_10, pipes_2_out_11, pipes_2_out_12, pipes_2_out_13, pipes_2_out_14, pipes_2_out_15,
       pipes_2_out_16, pipes_2_out_17, pipes_2_out_18, pipes_2_out_19, pipes_2_out_20, pipes_2_out_21,
       pipes_2_out_22, pipes_2_out_23, pipes_2_out_24, pipes_2_out_25, pipes_2_out_26, pipes_2_out_27,
       pipes_2_out_28, pipes_2_out_29, pipes_2_out_30, pipes_2_out_31, pipes_2_out_32, pipes_2_out_33,
       pipes_2_out_34, pipes_2_out_35, pipes_2_out_36, pipes_2_out_37, vcyo_1_bus_0;

  taktDel_11_1 taktdel_11_1_1 (.out_1(taktdel_11_1_1_out_1));
  Keyboard #(.buflen(10)) keyboard_1 (
    .clk(taktdel_11_1_1_out_1), .re(1'b1), .clr(1'b0), .data(keyboard_1_data));  // open: avail
  \rand  rand_1 (
    .tick(\vcyo_1_робит_ли_генератор ), .rand_2(rand_1_rand_2), .tick_1(rand_1_tick_1),
    .tick_2(rand_1_tick_2), .rand_1(rand_1_rand_1));  // open: in_2
  Comparator #(.width(7)) comparator_1 (.a(keyboard_1_data), .b(7'b0100000), .eq(comparator_1_eq));  // open: gt, lt
  vcyo vcyo_1 (
    .rand_2(rand_1_rand_2), .rand_1(rand_1_rand_1), .tick_2(rand_1_tick_2), .tick_1(rand_1_tick_1),
    .\Кнопка (comparator_1_eq), .bus_0(vcyo_1_bus_0), .\робит_ли_генератор (\vcyo_1_робит_ли_генератор ),
    .\флаг_смерти (\vcyo_1_флаг_смерти ), .in_6(in_1));
  Hex_Digit_Display hex_digit_display_1 (.value(vec_adr1));  // open: dp
  Hex_Digit_Display hex_digit_display_2 (.value(vec_adr2));  // open: dp
  not not_1 (not_1_out, \vcyo_1_флаг_смерти );
  cdm8 cdm8_1 (.\вкл (not_1_out), .plus_1(rand_1_tick_2), .\счет (\cdm8_1_счет ), .\рекорд (\cdm8_1_рекорд ));
  not not_2 (not_2_out, in_1);
  Hex_Digit_Display hex_digit_display_3 (.value(vec_adr3));  // open: dp
  \из_16ричной_в_10  \u_из_16ричной_в_10_1  (
    .in_1(\cdm8_1_счет ), .out_2(\из_16ричной_в_10_1_out_2 ), .out_3(\из_16ричной_в_10_1_out_3 ),
    .out_4(\из_16ричной_в_10_1_out_4 ));
  \из_16ричной_в_10  \u_из_16ричной_в_10_2  (
    .in_1(\cdm8_1_рекорд ), .out_2(vec_adr1), .out_3(vec_adr2), .out_4(vec_adr3));
  Hex_Digit_Display hex_digit_display_4 (.value(\из_16ричной_в_10_1_out_3 ));  // open: dp
  Hex_Digit_Display hex_digit_display_5 (.value(\из_16ричной_в_10_1_out_2 ));  // open: dp
  Hex_Digit_Display hex_digit_display_6 (.value(\из_16ричной_в_10_1_out_4 ));  // open: dp
  // DotMatrix #(.inputtype("select"), .matrixcols(32), .matrixrows(32)) dotmatrix_1: pin names not known; wires that end beside it: 32'h40, vcyo_1_bus_0
  DotMatrix #(.matrixcols(32), .matrixrows(32)) dotmatrix_2 (
    .col0(pipes_1_out_6), .col1(pipes_1_out_7), .col2(pipes_1_out_8), .col3(pipes_1_out_9),
    .col4(pipes_1_out_10), .col5(pipes_1_out_11), .col6(pipes_1_out_12), .col7(pipes_1_out_13),
    .col8(pipes_1_out_14), .col9(pipes_1_out_15), .col10(pipes_1_out_16), .col11(pipes_1_out_17),
    .col12(pipes_1_out_18), .col13(pipes_1_out_19), .col14(pipes_1_out_20), .col15(pipes_1_out_21),
    .col16(pipes_1_out_22), .col17(pipes_1_out_23), .col18(pipes_1_out_24), .col19(pipes_1_out_25),
    .col20(pipes_1_out_26), .col21(pipes_1_out_27), .col22(pipes_1_out_28), .col23(pipes_1_out_29),
    .col24(pipes_1_out_30), .col25(pipes_1_out_31), .col26(pipes_1_out_32), .col27(pipes_1_out_33),
    .col28(pipes_1_out_34), .col29(pipes_1_out_35), .col30(pipes_1_out_36), .col31(pipes_1_out_37));
  pipes pipes_1 (
    .out_6(pipes_1_out_6), .out_7(pipes_1_out_7), .out_8(pipes_1_out_8), .out_9(pipes_1_out_9),
    .out_10(pipes_1_out_10), .out_11(pipes_1_out_11), .out_12(pipes_1_out_12), .out_13(pipes_1_out_13),
    .out_14(pipes_1_out_14), .out_15(pipes_1_out_15), .out_16(pipes_1_out_16), .out_17(pipes_1_out_17),
    .out_18(pipes_1_out_18), .out_19(pipes_1_out_19), .out_20(pipes_1_out_20), .out_21(pipes_1_out_21),
    .out_22(pipes_1_out_22), .out_23(pipes_1_out_23), .out_24(pipes_1_out_24), .out_25(pipes_1_out_25),
    .out_26(pipes_1_out_26), .out_27(pipes_1_out_27), .out_28(pipes_1_out_28), .out_29(pipes_1_out_29),
    .out_30(pipes_1_out_30), .out_31(pipes_1_out_31), .out_32(pipes_1_out_32), .out_33(pipes_1_out_33),
    .out_34(pipes_1_out_34), .out_35(pipes_1_out_35), .out_36(pipes_1_out_36), .out_37(pipes_1_out_37),
    .rand_2(rand_1_rand_2), .rand_1(rand_1_rand_1), .tick_2(rand_1_tick_2), .tick_1(rand_1_tick_1),
    .in_5(not_2_out));
  DotMatrix #(.matrixcols(32), .matrixrows(32)) dotmatrix_3 (
    .col0(pipes_2_out_6), .col1(pipes_2_out_7), .col2(pipes_2_out_8), .col3(pipes_2_out_9),
    .col4(pipes_2_out_10), .col5(pipes_2_out_11), .col6(pipes_2_out_12), .col7(pipes_2_out_13),
    .col8(pipes_2_out_14), .col9(pipes_2_out_15), .col10(pipes_2_out_16), .col11(pipes_2_out_17),
    .col12(pipes_2_out_18), .col13(pipes_2_out_19), .col14(pipes_2_out_20), .col15(pipes_2_out_21),
    .col16(pipes_2_out_22), .col17(pipes_2_out_23), .col18(pipes_2_out_24), .col19(pipes_2_out_25),
    .col20(pipes_2_out_26), .col21(pipes_2_out_27), .col22(pipes_2_out_28), .col23(pipes_2_out_29),
    .col24(pipes_2_out_30), .col25(pipes_2_out_31), .col26(pipes_2_out_32), .col27(pipes_2_out_33),
    .col28(pipes_2_out_34), .col29(pipes_2_out_35), .col30(pipes_2_out_36), .col31(pipes_2_out_37));
  pipes pipes_2 (
    .out_6(pipes_2_out_6), .out_7(pipes_2_out_7), .out_8(pipes_2_out_8), .out_9(pipes_2_out_9),
    .out_10(pipes_2_out_10), .out_11(pipes_2_out_11), .out_12(pipes_2_out_12), .out_13(pipes_2_out_13),
    .out_14(pipes_2_out_14), .out_15(pipes_2_out_15), .out_16(pipes_2_out_16), .out_17(pipes_2_out_17),
    .out_18(pipes_2_out_18), .out_19(pipes_2_out_19), .out_20(pipes_2_out_20), .out_21(pipes_2_out_21),
    .out_22(pipes_2_out_22), .out_23(pipes_2_out_23), .out_24(pipes_2_out_24), .out_25(pipes_2_out_25),
    .out_26(pipes_2_out_26), .out_27(pipes_2_out_27), .out_28(pipes_2_out_28), .out_29(pipes_2_out_29),
    .out_30(pipes_2_out_30), .out_31(pipes_2_out_31), .out_32(pipes_2_out_32), .out_33(pipes_2_out_33),
    .out_34(pipes_2_out_34), .out_35(pipes_2_out_35), .out_36(pipes_2_out_36), .out_37(pipes_2_out_37),
    .rand_2(rand_1_rand_2), .rand_1(rand_1_rand_1), .tick_2(rand_1_tick_2), .tick_1(rand_1_tick_1),
    .in_5(not_2_out));

  // Notes on the sheet:
  //   кнопка вкл без сброса (1-вкл)
endmodule

module \rand  (
  input  tick,
  input  in_2,
  output [2:0] rand_2,
  output [2:0] rand_1,
  output tick_2,
  output tick_1
);

  wire and_1_out, comparator_1_eq, comparator_2_eq, counter_3_carry, d_ff_1_qn, decoder_1_out0,
       decoder_1_out1, or_1_out;
  wire [2:0] adder_1_out, random_1_out, register_1_q;
  wire [3:0] counter_2_q;
  wire [31:0] counter_1_q;

  Counter #(.width(32), .max('hffffffff), .trigger("falling")) counter_1 (
    .Q(counter_1_q), .clk(tick), .clr(or_1_out));  // open: load, D, count, carry
  or or_1 (or_1_out, in_2, comparator_1_eq);
  Comparator #(.width(32), .mode("unsigned")) comparator_1 (
    .a(counter_1_q), .b(32'h5a), .eq(comparator_1_eq));  // open: gt, lt
  D_Flip_Flop d_ff_1 (.clk(comparator_1_eq), .D(d_ff_1_qn), .Q(tick_1), .Qn(d_ff_1_qn));  // open: preset, en, reset
  or or_2 (tick_2, decoder_1_out0, decoder_1_out1);
  Counter #(.width(4), .max('hd), .trigger("falling")) counter_2 (
    .Q(counter_2_q), .clk(tick_1), .clr(in_2));  // open: load, D, count, carry
  Decoder #(.select(4)) decoder_1 (
    .out0(decoder_1_out0), .out1(decoder_1_out1), .sel(counter_2_q));  // open: out2, out3, out4, out5, out6, out7, out8, out9, out10, out11, out12, out13, out14, out15, en
  Counter #(.width(3), .max('h7)) counter_3 (
    .Q(rand_1), .carry(counter_3_carry), .clk(tick_2), .clr(in_2));  // open: load, D, count
  Register #(.width(3), .trigger("low")) register_1 (
    .D(random_1_out), .Q(register_1_q), .clk(counter_3_carry), .clr(in_2));  // open: en
  Random #(.width(3)) random_1 (.clk(counter_3_carry), .out(random_1_out));  // open: next, clr
  Adder #(.width(3)) adder_1 (.a(3'b001), .b(random_1_out), .out(adder_1_out));  // open: cin, cout
  Comparator #(.width(3)) comparator_2 (.a(register_1_q), .b(random_1_out), .eq(comparator_2_eq));  // open: gt, lt
  Multiplexer #(.width(3)) multiplexer_1 (
    .in0(random_1_out), .in1(adder_1_out), .out(rand_2), .sel(and_1_out));  // open: en
  and and_1 (and_1_out, comparator_2_eq, counter_3_carry);
endmodule

module pipes (
  input  [2:0] rand_2,
  input  [2:0] rand_1,
  input  tick_2,
  input  tick_1,
  input  in_5,
  output [31:0] out_6,
  output [31:0] out_7,
  output [31:0] out_8,
  output [31:0] out_9,
  output [31:0] out_10,
  output [31:0] out_11,
  output [31:0] out_12,
  output [31:0] out_13,
  output [31:0] out_14,
  output [31:0] out_15,
  output [31:0] out_16,
  output [31:0] out_17,
  output [31:0] out_18,
  output [31:0] out_19,
  output [31:0] out_20,
  output [31:0] out_21,
  output [31:0] out_22,
  output [31:0] out_23,
  output [31:0] out_24,
  output [31:0] out_25,
  output [31:0] out_26,
  output [31:0] out_27,
  output [31:0] out_28,
  output [31:0] out_29,
  output [31:0] out_30,
  output [31:0] out_31,
  output [31:0] out_32,
  output [31:0] out_33,
  output [31:0] out_34,
  output [31:0] out_35,
  output [31:0] out_36,
  output [31:0] out_37
);

  wire [31:0] _1, _2, pull_resistor_1_node, pull_resistor_2_node, pull_resistor_3_node, pull_resistor_4_node,
       pull_resistor_5_node, pull_resistor_6_node, pull_resistor_7_node, pull_resistor_8_node,
       pull_resistor_9_node, pull_resistor_10_node, pull_resistor_11_node, pull_resistor_12_node,
       pull_resistor_13_node, pull_resistor_14_node, pull_resistor_15_node, pull_resistor_16_node,
       pull_resistor_17_node, pull_resistor_18_node, pull_resistor_19_node, pull_resistor_20_node,
       pull_resistor_21_node, pull_resistor_22_node, pull_resistor_23_node, pull_resistor_24_node,
       pull_resistor_25_node, pull_resistor_26_node, pull_resistor_27_node, pull_resistor_28_node,
       pull_resistor_29_node, pull_resistor_30_node, pull_resistor_31_node, pull_resistor_32_node,
       register_1_q, register_2_q, register_3_q, register_4_q, register_5_q, register_6_q, register_7_q,
       register_8_q, register_9_q, register_10_q, register_11_q, register_12_q, register_13_q, register_14_q,
       register_15_q, register_16_q, register_17_q, register_18_q, register_19_q, register_20_q,
       register_21_q, register_22_q, register_23_q, register_24_q, register_25_q, register_26_q,
       register_27_q, register_28_q, register_29_q, register_30_q, register_31_q, register_32_q;

  Shift_Register #(.length(32)) shift_register_1 (
    .in(tick_2), .clk(tick_1), .q0(_1[31]), .q1(_1[30]), .q2(_1[29]), .q3(_1[28]), .q4(_1[27]), .q5(_1[26]),
    .q6(_1[25]), .q7(_1[24]), .q8(_1[23]), .q9(_1[22]), .q10(_1[21]), .q11(_1[20]), .q12(_1[19]),
    .q13(_1[18]), .q14(_1[17]), .q15(_1[16]), .q16(_1[15]), .q17(_1[14]), .q18(_1[13]), .q19(_1[12]),
    .q20(_1[11]), .q21(_1[10]), .q22(_1[9]), .q23(_1[8]), .q24(_1[7]), .q25(_1[6]), .q26(_1[5]), .q27(_1[4]),
    .q28(_1[3]), .q29(_1[2]), .q30(_1[1]), .q31(_1[0]));  // open: shift, out, load, clr, d0, d1, d2, d3, d4, d5, d6, d7, d8, d9, d10, d11, d12, d13, d14, d15, d16, d17, d18, d19, d20, d21, d22, d23, d24, d25, d26, d27, d28, d29, d30, d31
  rand_pipe rand_pipe_1 (.out_3(_2), .rand_2(rand_2), .rand_1(rand_1));
  assign out_6 = pull_resistor_1_node | 32'h3;  // OR_Gate or_1, 32 bits wide
  Pull_Resistor pull_resistor_1 (.node(pull_resistor_1_node));
  assign pull_resistor_1_node = _1[0] ? register_1_q : 32'bz;  // Controlled_Buffer controlled_buffer_1
  Register #(.width(32), .trigger("high")) register_1 (
    .D(register_2_q), .Q(register_1_q), .clk(_1[0]), .clr(in_5));  // open: en
  assign out_7 = pull_resistor_2_node | 32'h3;  // OR_Gate or_2, 32 bits wide
  Pull_Resistor pull_resistor_2 (.node(pull_resistor_2_node));
  assign pull_resistor_2_node = _1[1] ? register_2_q : 32'bz;  // Controlled_Buffer controlled_buffer_2
  Register #(.width(32), .trigger("high")) register_2 (
    .D(register_3_q), .Q(register_2_q), .clk(_1[1]), .clr(in_5));  // open: en
  Pull_Resistor pull_resistor_3 (.node(pull_resistor_3_node));
  assign pull_resistor_3_node = _1[2] ? register_3_q : 32'bz;  // Controlled_Buffer controlled_buffer_3
  Register #(.width(32), .trigger("high")) register_3 (
    .D(register_4_q), .Q(register_3_q), .clk(_1[2]), .clr(in_5));  // open: en
  assign out_8 = pull_resistor_3_node | 32'h3;  // OR_Gate or_3, 32 bits wide
  assign out_9 = pull_resistor_4_node | 32'h3;  // OR_Gate or_4, 32 bits wide
  Pull_Resistor pull_resistor_4 (.node(pull_resistor_4_node));
  assign pull_resistor_4_node = _1[3] ? register_4_q : 32'bz;  // Controlled_Buffer controlled_buffer_4
  Register #(.width(32), .trigger("high")) register_4 (
    .D(register_5_q), .Q(register_4_q), .clk(_1[3]), .clr(in_5));  // open: en
  assign out_10 = pull_resistor_5_node | 32'h3;  // OR_Gate or_5, 32 bits wide
  Pull_Resistor pull_resistor_5 (.node(pull_resistor_5_node));
  assign pull_resistor_5_node = _1[4] ? register_5_q : 32'bz;  // Controlled_Buffer controlled_buffer_5
  Register #(.width(32), .trigger("high")) register_5 (
    .D(register_6_q), .Q(register_5_q), .clk(_1[4]), .clr(in_5));  // open: en
  assign out_11 = pull_resistor_6_node | 32'h3;  // OR_Gate or_6, 32 bits wide
  Pull_Resistor pull_resistor_6 (.node(pull_resistor_6_node));
  assign pull_resistor_6_node = _1[5] ? register_6_q : 32'bz;  // Controlled_Buffer controlled_buffer_6
  Register #(.width(32), .trigger("high")) register_6 (
    .D(register_7_q), .Q(register_6_q), .clk(_1[5]), .clr(in_5));  // open: en
  Pull_Resistor pull_resistor_7 (.node(pull_resistor_7_node));
  assign pull_resistor_7_node = _1[6] ? register_7_q : 32'bz;  // Controlled_Buffer controlled_buffer_7
  Register #(.width(32), .trigger("high")) register_7 (
    .D(register_8_q), .Q(register_7_q), .clk(_1[6]), .clr(in_5));  // open: en
  assign out_12 = pull_resistor_7_node | 32'h3;  // OR_Gate or_7, 32 bits wide
  assign out_13 = pull_resistor_8_node | 32'h3;  // OR_Gate or_8, 32 bits wide
  Pull_Resistor pull_resistor_8 (.node(pull_resistor_8_node));
  assign pull_resistor_8_node = _1[7] ? register_8_q : 32'bz;  // Controlled_Buffer controlled_buffer_8
  Register #(.width(32), .trigger("high")) register_8 (
    .D(register_9_q), .Q(register_8_q), .clk(_1[7]), .clr(in_5));  // open: en
  assign out_14 = pull_resistor_9_node | 32'h3;  // OR_Gate or_9, 32 bits wide
  Pull_Resistor pull_resistor_9 (.node(pull_resistor_9_node));
  assign pull_resistor_9_node = _1[8] ? register_9_q : 32'bz;  // Controlled_Buffer controlled_buffer_9
  Register #(.width(32), .trigger("high")) register_9 (
    .D(register_10_q), .Q(register_9_q), .clk(_1[8]), .clr(in_5));  // open: en
  assign out_15 = pull_resistor_10_node | 32'h3;  // OR_Gate or_10, 32 bits wide
  Pull_Resistor pull_resistor_10 (.node(pull_resistor_10_node));
  assign pull_resistor_10_node = _1[9] ? register_10_q : 32'bz;  // Controlled_Buffer controlled_buffer_10
  Register #(.width(32), .trigger("high")) register_10 (
    .D(register_11_q), .Q(register_10_q), .clk(_1[9]), .clr(in_5));  // open: en
  Pull_Resistor pull_resistor_11 (.node(pull_resistor_11_node));
  assign pull_resistor_11_node = _1[10] ? register_11_q : 32'bz;  // Controlled_Buffer controlled_buffer_11
  Register #(.width(32), .trigger("high")) register_11 (
    .D(register_12_q), .Q(register_11_q), .clk(_1[10]), .clr(in_5));  // open: en
  assign out_16 = pull_resistor_11_node | 32'h3;  // OR_Gate or_11, 32 bits wide
  assign out_17 = pull_resistor_12_node | 32'h3;  // OR_Gate or_12, 32 bits wide
  Pull_Resistor pull_resistor_12 (.node(pull_resistor_12_node));
  assign pull_resistor_12_node = _1[11] ? register_12_q : 32'bz;  // Controlled_Buffer controlled_buffer_12
  Register #(.width(32), .trigger("high")) register_12 (
    .D(register_13_q), .Q(register_12_q), .clk(_1[11]), .clr(in_5));  // open: en
  assign out_18 = pull_resistor_13_node | 32'h3;  // OR_Gate or_13, 32 bits wide
  Pull_Resistor pull_resistor_13 (.node(pull_resistor_13_node));
  assign pull_resistor_13_node = _1[12] ? register_13_q : 32'bz;  // Controlled_Buffer controlled_buffer_13
  Register #(.width(32), .trigger("high")) register_13 (
    .D(register_14_q), .Q(register_13_q), .clk(_1[12]), .clr(in_5));  // open: en
  assign out_19 = pull_resistor_14_node | 32'h3;  // OR_Gate or_14, 32 bits wide
  Pull_Resistor pull_resistor_14 (.node(pull_resistor_14_node));
  assign pull_resistor_14_node = _1[13] ? register_14_q : 32'bz;  // Controlled_Buffer controlled_buffer_14
  Register #(.width(32), .trigger("high")) register_14 (
    .D(register_15_q), .Q(register_14_q), .clk(_1[13]), .clr(in_5));  // open: en
  Pull_Resistor pull_resistor_15 (.node(pull_resistor_15_node));
  assign pull_resistor_15_node = _1[14] ? register_15_q : 32'bz;  // Controlled_Buffer controlled_buffer_15
  Register #(.width(32), .trigger("high")) register_15 (
    .D(register_16_q), .Q(register_15_q), .clk(_1[14]), .clr(in_5));  // open: en
  assign out_20 = pull_resistor_15_node | 32'h3;  // OR_Gate or_15, 32 bits wide
  assign out_21 = pull_resistor_16_node | 32'h3;  // OR_Gate or_16, 32 bits wide
  Pull_Resistor pull_resistor_16 (.node(pull_resistor_16_node));
  assign pull_resistor_16_node = _1[15] ? register_16_q : 32'bz;  // Controlled_Buffer controlled_buffer_16
  Register #(.width(32), .trigger("high")) register_16 (
    .D(register_17_q), .Q(register_16_q), .clk(_1[15]), .clr(in_5));  // open: en
  assign out_22 = pull_resistor_17_node | 32'h3;  // OR_Gate or_17, 32 bits wide
  Pull_Resistor pull_resistor_17 (.node(pull_resistor_17_node));
  assign pull_resistor_17_node = _1[16] ? register_17_q : 32'bz;  // Controlled_Buffer controlled_buffer_17
  Register #(.width(32), .trigger("high")) register_17 (
    .D(register_18_q), .Q(register_17_q), .clk(_1[16]), .clr(in_5));  // open: en
  assign out_23 = pull_resistor_18_node | 32'h3;  // OR_Gate or_18, 32 bits wide
  Pull_Resistor pull_resistor_18 (.node(pull_resistor_18_node));
  assign pull_resistor_18_node = _1[17] ? register_18_q : 32'bz;  // Controlled_Buffer controlled_buffer_18
  Register #(.width(32), .trigger("high")) register_18 (
    .D(register_19_q), .Q(register_18_q), .clk(_1[17]), .clr(in_5));  // open: en
  Pull_Resistor pull_resistor_19 (.node(pull_resistor_19_node));
  assign pull_resistor_19_node = _1[18] ? register_19_q : 32'bz;  // Controlled_Buffer controlled_buffer_19
  Register #(.width(32), .trigger("high")) register_19 (
    .D(register_20_q), .Q(register_19_q), .clk(_1[18]), .clr(in_5));  // open: en
  assign out_24 = pull_resistor_19_node | 32'h3;  // OR_Gate or_19, 32 bits wide
  assign out_25 = pull_resistor_20_node | 32'h3;  // OR_Gate or_20, 32 bits wide
  Pull_Resistor pull_resistor_20 (.node(pull_resistor_20_node));
  assign pull_resistor_20_node = _1[19] ? register_20_q : 32'bz;  // Controlled_Buffer controlled_buffer_20
  Register #(.width(32), .trigger("high")) register_20 (
    .D(register_21_q), .Q(register_20_q), .clk(_1[19]), .clr(in_5));  // open: en
  assign out_26 = pull_resistor_21_node | 32'h3;  // OR_Gate or_21, 32 bits wide
  Pull_Resistor pull_resistor_21 (.node(pull_resistor_21_node));
  assign pull_resistor_21_node = _1[20] ? register_21_q : 32'bz;  // Controlled_Buffer controlled_buffer_21
  Register #(.width(32), .trigger("high")) register_21 (
    .D(register_22_q), .Q(register_21_q), .clk(_1[20]), .clr(in_5));  // open: en
  assign out_27 = pull_resistor_22_node | 32'h3;  // OR_Gate or_22, 32 bits wide
  Pull_Resistor pull_resistor_22 (.node(pull_resistor_22_node));
  assign pull_resistor_22_node = _1[21] ? register_22_q : 32'bz;  // Controlled_Buffer controlled_buffer_22
  Register #(.width(32), .trigger("high")) register_22 (
    .D(register_23_q), .Q(register_22_q), .clk(_1[21]), .clr(in_5));  // open: en
  Pull_Resistor pull_resistor_23 (.node(pull_resistor_23_node));
  assign pull_resistor_23_node = _1[22] ? register_23_q : 32'bz;  // Controlled_Buffer controlled_buffer_23
  Register #(.width(32), .trigger("high")) register_23 (
    .D(register_24_q), .Q(register_23_q), .clk(_1[22]), .clr(in_5));  // open: en
  assign out_28 = pull_resistor_23_node | 32'h3;  // OR_Gate or_23, 32 bits wide
  assign out_29 = pull_resistor_24_node | 32'h3;  // OR_Gate or_24, 32 bits wide
  Pull_Resistor pull_resistor_24 (.node(pull_resistor_24_node));
  assign pull_resistor_24_node = _1[23] ? register_24_q : 32'bz;  // Controlled_Buffer controlled_buffer_24
  Register #(.width(32), .trigger("high")) register_24 (
    .D(register_25_q), .Q(register_24_q), .clk(_1[23]), .clr(in_5));  // open: en
  assign out_30 = pull_resistor_25_node | 32'h3;  // OR_Gate or_25, 32 bits wide
  Pull_Resistor pull_resistor_25 (.node(pull_resistor_25_node));
  assign pull_resistor_25_node = _1[24] ? register_25_q : 32'bz;  // Controlled_Buffer controlled_buffer_25
  Register #(.width(32), .trigger("high")) register_25 (
    .D(register_26_q), .Q(register_25_q), .clk(_1[24]), .clr(in_5));  // open: en
  assign out_31 = pull_resistor_26_node | 32'h3;  // OR_Gate or_26, 32 bits wide
  Pull_Resistor pull_resistor_26 (.node(pull_resistor_26_node));
  assign pull_resistor_26_node = _1[25] ? register_26_q : 32'bz;  // Controlled_Buffer controlled_buffer_26
  Register #(.width(32), .trigger("high")) register_26 (
    .D(register_27_q), .Q(register_26_q), .clk(_1[25]), .clr(in_5));  // open: en
  Pull_Resistor pull_resistor_27 (.node(pull_resistor_27_node));
  assign pull_resistor_27_node = _1[26] ? register_27_q : 32'bz;  // Controlled_Buffer controlled_buffer_27
  Register #(.width(32), .trigger("high")) register_27 (
    .D(register_28_q), .Q(register_27_q), .clk(_1[26]), .clr(in_5));  // open: en
  assign out_32 = pull_resistor_27_node | 32'h3;  // OR_Gate or_27, 32 bits wide
  assign out_33 = pull_resistor_28_node | 32'h3;  // OR_Gate or_28, 32 bits wide
  Pull_Resistor pull_resistor_28 (.node(pull_resistor_28_node));
  assign pull_resistor_28_node = _1[27] ? register_28_q : 32'bz;  // Controlled_Buffer controlled_buffer_28
  Register #(.width(32), .trigger("high")) register_28 (
    .D(register_29_q), .Q(register_28_q), .clk(_1[27]), .clr(in_5));  // open: en
  assign out_34 = pull_resistor_29_node | 32'h3;  // OR_Gate or_29, 32 bits wide
  Pull_Resistor pull_resistor_29 (.node(pull_resistor_29_node));
  assign pull_resistor_29_node = _1[28] ? register_29_q : 32'bz;  // Controlled_Buffer controlled_buffer_29
  Register #(.width(32), .trigger("high")) register_29 (
    .D(register_30_q), .Q(register_29_q), .clk(_1[28]), .clr(in_5));  // open: en
  assign out_35 = pull_resistor_30_node | 32'h3;  // OR_Gate or_30, 32 bits wide
  Pull_Resistor pull_resistor_30 (.node(pull_resistor_30_node));
  assign pull_resistor_30_node = _1[29] ? register_30_q : 32'bz;  // Controlled_Buffer controlled_buffer_30
  Register #(.width(32), .trigger("high")) register_30 (
    .D(register_31_q), .Q(register_30_q), .clk(_1[29]), .clr(in_5));  // open: en
  Pull_Resistor pull_resistor_31 (.node(pull_resistor_31_node));
  assign pull_resistor_31_node = _1[30] ? register_31_q : 32'bz;  // Controlled_Buffer controlled_buffer_31
  Register #(.width(32), .trigger("high")) register_31 (
    .D(register_32_q), .Q(register_31_q), .clk(_1[30]), .clr(in_5));  // open: en
  assign out_36 = pull_resistor_31_node | 32'h3;  // OR_Gate or_31, 32 bits wide
  assign out_37 = pull_resistor_32_node | 32'h3;  // OR_Gate or_32, 32 bits wide
  Pull_Resistor pull_resistor_32 (.node(pull_resistor_32_node));
  assign pull_resistor_32_node = _1[31] ? register_32_q : 32'bz;  // Controlled_Buffer controlled_buffer_32
  Register #(.width(32), .trigger("high")) register_32 (
    .D(_2), .Q(register_32_q), .clk(_1[31]), .clr(in_5));  // open: en

  // Other names for the same wires on the sheet: _0 = in_5
endmodule

module rand_pipe (
  input  [2:0] rand_1,
  input  [2:0] rand_2,
  output [31:0] out_3
);

  wire [31:0] multiplexer_1_out, multiplexer_2_out, multiplexer_3_out, multiplexer_4_out, multiplexer_5_out,
       multiplexer_6_out, multiplexer_7_out, multiplexer_8_out;

  Multiplexer #(.select(3), .width(32)) multiplexer_1 (
    .in0(32'hff807fff), .in1(32'hfe01ffff), .in2(32'hfc03ffff), .in3(32'hf00fffff), .in4(32'hff00ffff),
    .in5(32'hf807ffff), .in6(32'hff00ffff), .in7(32'hfff807ff), .out(multiplexer_1_out), .sel(rand_1));  // open: en
  Multiplexer #(.select(3), .width(32)) multiplexer_2 (
    .in0(32'hffc03fff), .in1(32'hfff807ff), .in2(32'hffff807f), .in3(32'hffc03fff), .in4(32'hffff00ff),
    .in5(32'hffe01fff), .in6(32'hffffc03f), .in7(32'hfffe01ff), .out(multiplexer_2_out), .sel(rand_1));  // open: en
  Multiplexer #(.select(3), .width(32)) multiplexer_3 (
    .in0(32'hffc03fff), .in1(32'hfffe01ff), .in2(32'hffe01fff), .in3(32'hffffe01f), .in4(32'hfff807ff),
    .in5(32'hfffff00f), .in6(32'hff807fff), .in7(32'hfffe01ff), .out(multiplexer_3_out), .sel(rand_1));  // open: en
  Multiplexer #(.select(3), .width(32)) multiplexer_4 (
    .in0(32'hffe01fff), .in1(32'hfff807ff), .in2(32'hfff00fff), .in3(32'hfffc03ff), .in4(32'hffff807f),
    .in5(32'hfff807ff), .in6(32'hffc03fff), .in7(32'hfff00fff), .out(multiplexer_4_out), .sel(rand_1));  // open: en
  Multiplexer #(.select(3), .width(32)) multiplexer_5 (
    .in0(32'hfff807ff), .in1(32'hfffe01ff), .in2(32'hfffff00f), .in3(32'hffffc03f), .in4(32'hffc03fff),
    .in5(32'hfc03ffff), .in6(32'hff00ffff), .in7(32'hfffe01ff), .out(multiplexer_5_out), .sel(rand_1));  // open: en
  Multiplexer #(.select(3), .width(32)) multiplexer_6 (
    .in0(32'hfffc03ff), .in1(32'hffc03fff), .in2(32'hffe01fff), .in3(32'hff807fff), .in4(32'hfc03ffff),
    .in5(32'hff807fff), .in6(32'hf807ffff), .in7(32'hfff00fff), .out(multiplexer_6_out), .sel(rand_1));  // open: en
  Multiplexer #(.select(3), .width(32)) multiplexer_7 (
    .in0(32'hff807fff), .in1(32'hfff00fff), .in2(32'hfe01ffff), .in3(32'hf00fffff), .in4(32'hfe01ffff),
    .in5(32'hffff00ff), .in6(32'hfffc03ff), .in7(32'hffe01fff), .out(multiplexer_7_out), .sel(rand_1));  // open: en
  Multiplexer #(.select(3), .width(32)) multiplexer_8 (
    .in0(32'hfff00fff), .in1(32'hffff00ff), .in2(32'hfffc03ff), .in3(32'hffe01fff), .in4(32'hffff807f),
    .in5(32'hffffe01f), .in6(32'hffffc03f), .in7(32'hfffc03ff), .out(multiplexer_8_out), .sel(rand_1));  // open: en
  Multiplexer #(.select(3), .width(32)) multiplexer_9 (
    .in0(multiplexer_1_out), .in1(multiplexer_2_out), .in2(multiplexer_3_out), .in3(multiplexer_4_out),
    .in4(multiplexer_5_out), .in5(multiplexer_6_out), .in6(multiplexer_7_out), .in7(multiplexer_8_out),
    .out(out_3), .sel(rand_2));  // open: en

  // Other names for the same wires on the sheet: _1[2:0] = rand_1
endmodule

module prigalka (
  input  \Кнопка ,
  output [31:0] bus_0,
  output \робит_ли_генератор 
);

  wire _551, _69699, and_1_out, clock_1_out, comparator_1_eq, counter_3_carry, counter_4_carry,
       counter_8_carry, d_ff_1_q, d_ff_1_qn, d_ff_2_q, d_ff_2_qn, d_ff_3_q, d_ff_3_qn, d_ff_4_q, d_ff_4_qn,
       d_ff_5_q, d_ff_5_qn, d_ff_6_qn, multiplexer_1_out, not_1_out, not_2_out, not_3_out, not_4_out,
       not_5_out, not_6_out, not_7_out, not_8_out, not_9_out, or_1_out, or_2_out, transistor_2_out,
       transistor_4_out, \умер , \упал_умер , \упал_умер2 ;
  wire [2:0] counter_6_q;
  wire [4:0] counter_7_q;
  wire [31:0] counter_5_q;

  Clock clock_1 (.out(clock_1_out));
  Transistor transistor_1 (.in(clock_1_out), .out(\робит_ли_генератор ), .gate(\умер ));
  Counter #(.width(2), .max('h3), .ongoal("stay")) counter_1 (
    .clk(d_ff_3_q), .clr(and_1_out));  // open: load, D, count, Q, carry
  Counter #(.width(1), .max('h0), .ongoal("stay")) counter_2 (.clk(d_ff_3_q));  // open: load, D, count, Q, carry, clr
  Counter #(.width(2), .max('h2), .ongoal("stay")) counter_3 (
    .carry(counter_3_carry), .clk(d_ff_3_q), .clr(and_1_out));  // open: load, D, count, Q
  Counter #(.width(1), .max('h1), .ongoal("stay")) counter_4 (
    .carry(counter_4_carry), .clk(d_ff_3_q), .clr(and_1_out));  // open: load, D, count, Q
  Counter #(.width(32), .max('hffffffff), .trigger("falling")) counter_5 (
    .Q(counter_5_q), .clk(\робит_ли_генератор ), .clr(comparator_1_eq));  // open: load, D, count, carry
  Comparator #(.width(32), .mode("unsigned")) comparator_1 (
    .a(counter_5_q), .b(32'h20), .eq(comparator_1_eq));  // open: gt, lt
  D_Flip_Flop d_ff_1 (.clk(comparator_1_eq), .D(d_ff_1_qn), .Q(d_ff_1_q), .Qn(d_ff_1_qn));  // open: preset, en, reset
  Comparator #(.width(5), .mode("unsigned")) comparator_2 (
    .a(counter_7_q), .b(5'b11110), .eq(\упал_умер2 ));  // open: gt, lt
  D_Flip_Flop d_ff_2 (.clk(d_ff_1_q), .D(d_ff_2_qn), .Q(d_ff_2_q), .Qn(d_ff_2_qn));  // open: preset, en, reset
  Decoder #(.select(5)) decoder_1 (
    .out0(bus_0[31]), .out1(bus_0[30]), .out2(bus_0[29]), .out3(bus_0[28]), .out4(bus_0[27]),
    .out5(bus_0[26]), .out6(bus_0[25]), .out7(bus_0[24]), .out8(bus_0[23]), .out9(bus_0[22]),
    .out10(bus_0[21]), .out11(bus_0[20]), .out12(bus_0[19]), .out13(bus_0[18]), .out14(bus_0[17]),
    .out15(bus_0[16]), .out16(bus_0[15]), .out17(bus_0[14]), .out18(bus_0[13]), .out19(bus_0[12]),
    .out20(bus_0[11]), .out21(bus_0[10]), .out22(bus_0[9]), .out23(bus_0[8]), .out24(bus_0[7]),
    .out25(bus_0[6]), .out26(bus_0[5]), .out27(bus_0[4]), .out28(bus_0[3]), .out29(bus_0[2]),
    .out30(bus_0[1]), .out31(bus_0[0]), .sel(counter_7_q));  // open: en
  D_Flip_Flop d_ff_3 (.clk(d_ff_2_q), .D(d_ff_3_qn), .Q(d_ff_3_q), .Qn(d_ff_3_qn));  // open: preset, en, reset
  Comparator #(.width(5), .mode("unsigned")) comparator_3 (
    .a(counter_7_q), .b({5{1'b1}}), .eq(\упал_умер ));  // open: gt, lt
  D_Flip_Flop d_ff_4 (.clk(d_ff_3_q), .D(d_ff_4_qn), .Q(d_ff_4_q), .Qn(d_ff_4_qn));  // open: preset, en, reset
  nand nand_1 (_551, counter_3_carry, counter_4_carry);
  D_Flip_Flop d_ff_5 (.clk(d_ff_4_q), .D(d_ff_5_qn), .Q(d_ff_5_q), .Qn(d_ff_5_qn));  // open: preset, en, reset
  Comparator #(.width(5), .mode("unsigned")) comparator_4 (.a(counter_7_q), .b(5'b11110), .gt(_69699));  // open: eq, lt
  D_Flip_Flop d_ff_6 (.clk(d_ff_5_q), .D(d_ff_6_qn), .Qn(d_ff_6_qn));  // open: Q, preset, en, reset
  Counter #(.width(3), .max('h7)) counter_6 (
    .Q(counter_6_q), .clk(d_ff_4_q), .clr(or_1_out));  // open: load, D, count, carry
  or or_1 (or_1_out, _69699, _551);
  not not_1 (not_1_out, \Кнопка );
  Multiplexer #(.select(3)) multiplexer_1 (
    .in0(d_ff_5_q), .in1(d_ff_4_q), .in2(d_ff_3_q), .in3(d_ff_3_q), .in4(d_ff_2_q), .in5(d_ff_1_q),
    .in6(d_ff_1_q), .in7(comparator_1_eq), .out(multiplexer_1_out), .sel(counter_6_q));  // open: en
  and and_1 (and_1_out, not_1_out, \Кнопка );
  Transistor #(.\type ("n")) transistor_2 (.in(d_ff_2_q), .out(transistor_2_out), .gate(_551));
  Transistor transistor_3 (.in(multiplexer_1_out), .out(transistor_2_out), .gate(_551));
  // DotMatrix #(.inputtype("select"), .matrixcols(32), .matrixrows(32)) dotmatrix_1: pin names not known; wires that end beside it: 32'h40, bus_0
  Counter #(.width(5), .max('h1f)) counter_7 (
    .load(_551), .Q(counter_7_q), .clk(transistor_2_out), .clr(transistor_4_out));  // open: D, count, carry
  not not_2 (not_2_out, not_3_out);
  not not_3 (not_3_out, not_4_out);
  not not_4 (not_4_out, not_5_out);
  not not_5 (not_5_out, not_6_out);
  not not_6 (not_6_out, not_7_out);
  not not_7 (not_7_out, not_8_out);
  not not_8 (not_8_out, not_9_out);
  not not_9 (not_9_out, or_2_out);
  or or_2 (or_2_out, \упал_умер , \упал_умер2 );
  Transistor transistor_4 (.in(not_2_out), .out(transistor_4_out), .gate(counter_8_carry));
  Counter #(.width(4), .max('h4), .ongoal("stay")) counter_8 (
    .carry(counter_8_carry), .clk(or_2_out));  // open: load, D, count, Q, clr
  Counter #(.width(4), .max('h1), .ongoal("stay")) counter_9 (
    .carry(\умер ), .clk(counter_8_carry));  // open: load, D, count, Q, clr
endmodule

module d (
  input  [31:0] \Вход ,
  output \Выход 
);

  or or_1 (\Выход , \Вход [0], \Вход [1], \Вход [2], \Вход [3], \Вход [4], \Вход [5], \Вход [6], \Вход [7], \Вход [8], \Вход [9], \Вход [10], \Вход [11], \Вход [12], \Вход [13], \Вход [14], \Вход [15], \Вход [17], \Вход [18], \Вход [19], \Вход [20], \Вход [21], \Вход [22], \Вход [23], \Вход [24], \Вход [25], \Вход [26], \Вход [27], \Вход [28], \Вход [29], \Вход [30], \Вход [31], \Вход [16]);
endmodule

module vcyo (
  input  [2:0] rand_2,
  input  [2:0] rand_1,
  input  tick_2,
  input  tick_1,
  input  \Кнопка ,
  input  in_6,
  output [31:0] bus_0,
  output \флаг_смерти ,
  output \робит_ли_генератор 
);

  wire _1_1, _1_2, _1_3, _1_4, _1_5, _1_6, _1_7, _1_8, _1_9, _1_10, _1_11, _1_12, _1_13, _1_14, _1_15, _1_16,
       _1_17, _1_18, _1_19, _1_20, _1_21, _1_22, _1_23, _1_24, _1_25, _1_26, _1_27, _1_28, _1_29, _1_30,
       _1_31, _1_32, _2_1, _2_2, _2_3, _2_4, _2_5, _2_6, _2_7, _2_8, _2_9, _2_10, _2_11, _2_12, _2_13, _2_14,
       _2_15, _2_16, _2_17, _2_18, _2_19, _2_20, _2_21, _2_22, _2_23, _2_24, _2_25, _2_26, _2_27, _2_28,
       _2_29, _2_30, _2_31, _2_32, _551, _69699, and_1_out, and_2_out, and_3_out, and_4_out, and_5_out,
       and_6_out, and_7_out, and_8_out, and_9_out, and_10_out, and_11_out, and_12_out, and_13_out,
       and_14_out, and_15_out, and_16_out, and_17_out, and_18_out, and_19_out, and_20_out, and_21_out,
       and_22_out, and_23_out, and_24_out, and_25_out, and_26_out, and_27_out, and_28_out, and_29_out,
       and_30_out, and_31_out, and_32_out, and_33_out, and_34_out, clock_1_out, comparator_1_eq,
       counter_3_carry, counter_4_carry, counter_8_carry, d_ff_1_q, d_ff_1_qn, d_ff_2_q, d_ff_2_qn, d_ff_3_q,
       d_ff_3_qn, d_ff_4_q, d_ff_4_qn, d_ff_5_q, d_ff_5_qn, d_ff_6_qn, multiplexer_1_out, not_2_out,
       not_3_out, not_4_out, not_5_out, not_6_out, not_7_out, not_8_out, not_9_out, not_10_out, or_1_out,
       or_2_out, or_3_out, or_4_out, or_5_out, or_6_out, or_7_out, or_8_out, or_9_out, or_11_out, or_12_out,
       or_13_out, or_14_out, or_15_out, or_17_out, or_18_out, or_19_out, or_20_out, or_21_out, or_22_out,
       or_23_out, or_24_out, or_25_out, or_26_out, or_27_out, or_28_out, or_29_out, or_30_out, or_31_out,
       or_32_out, or_33_out, or_34_out, or_35_out, or_36_out, or_37_out, or_38_out, transistor_2_out,
       transistor_4_out, vec_adr, \врезался_умер , \умер , \упал_умер , \упал_умер2 ;
  wire [2:0] counter_6_q;
  wire [4:0] counter_7_q;
  wire [31:0] counter_5_q, pipes_2_out_6, pipes_2_out_7, pipes_2_out_8, pipes_2_out_9, pipes_2_out_10,
       pipes_2_out_11, pipes_2_out_12, pipes_2_out_13, pipes_2_out_14, pipes_2_out_15, pipes_2_out_16,
       pipes_2_out_17, pipes_2_out_18, pipes_2_out_19, pipes_2_out_20, pipes_2_out_21, pipes_2_out_22,
       pipes_2_out_23, pipes_2_out_24, pipes_2_out_25, pipes_2_out_26, pipes_2_out_27, pipes_2_out_28,
       pipes_2_out_29, pipes_2_out_30, pipes_2_out_31, pipes_2_out_32, pipes_2_out_33, pipes_2_out_34,
       pipes_2_out_35, pipes_2_out_36, pipes_2_out_37;

  or or_1 (or_1_out, _1_1, _2_1);
  and and_1 (and_1_out, bus_0[31], or_1_out);
  or or_2 (or_2_out, _1_2, _2_2);
  and and_2 (and_2_out, bus_0[30], or_2_out);
  or or_3 (or_3_out, _1_3, _2_3);
  and and_3 (and_3_out, bus_0[29], or_3_out);
  or or_4 (or_4_out, _1_4, _2_4);
  and and_4 (and_4_out, bus_0[28], or_4_out);
  and and_5 (and_5_out, bus_0[27], or_5_out);
  or or_5 (or_5_out, _1_5, _2_5);
  or or_6 (or_6_out, _1_6, _2_6);
  and and_6 (and_6_out, bus_0[26], or_6_out);
  or or_7 (or_7_out, _1_7, _2_7);
  and and_7 (and_7_out, bus_0[25], or_7_out);
  or or_8 (or_8_out, _1_8, _2_8);
  and and_8 (and_8_out, bus_0[24], or_8_out);
  or or_9 (or_9_out, _1_9, _2_9);
  and and_9 (and_9_out, bus_0[23], or_9_out);
  or or_10 (\врезался_умер , and_1_out, and_2_out, and_3_out, and_4_out, and_5_out, and_6_out, and_7_out, and_8_out, and_9_out, and_10_out, and_11_out, and_14_out, and_13_out, and_15_out, and_16_out, and_17_out, and_18_out, and_19_out, and_20_out, and_21_out, and_22_out, and_23_out, and_24_out, and_25_out, and_27_out, and_26_out, and_28_out, and_29_out, and_30_out, and_31_out, and_33_out, and_34_out);
  or or_11 (or_11_out, _1_10, _2_10);
  and and_10 (and_10_out, bus_0[22], or_11_out);
  Clock clock_1 (.out(clock_1_out));
  or or_12 (or_12_out, _1_11, _2_11);
  and and_11 (and_11_out, bus_0[21], or_12_out);
  and and_12 (and_12_out, clock_1_out, in_6);
  or or_13 (or_13_out, _1_13, _2_13);
  or or_14 (or_14_out, _1_12, _2_12);
  and and_13 (and_13_out, bus_0[19], or_13_out);
  and and_14 (and_14_out, bus_0[20], or_14_out);
  Transistor transistor_1 (.in(and_12_out), .out(\робит_ли_генератор ), .gate(\флаг_смерти ));
  not not_1 (vec_adr, in_6);
  or or_15 (or_15_out, _1_14, _2_14);
  and and_15 (and_15_out, bus_0[18], or_15_out);
  pipes pipes_1 (
    .out_12({_2_1, _2_2, _2_3, _2_4, _2_5, _2_6, _2_7, _2_8, _2_9, _2_10, _2_11, _2_12, _2_13, _2_14, _2_15, _2_16, _2_17, _2_18, _2_19, _2_20, _2_21, _2_22, _2_23, _2_24, _2_25, _2_26, _2_27, _2_28, _2_29, _2_30, _2_31, _2_32}),
    .out_13({_1_1, _1_2, _1_3, _1_4, _1_5, _1_6, _1_7, _1_8, _1_9, _1_10, _1_11, _1_12, _1_13, _1_14, _1_15, _1_16, _1_17, _1_18, _1_19, _1_20, _1_21, _1_22, _1_23, _1_24, _1_25, _1_26, _1_27, _1_28, _1_29, _1_30, _1_31, _1_32}),
    .rand_2(rand_2), .rand_1(rand_1), .tick_2(tick_2), .tick_1(tick_1), .in_5(vec_adr));  // open: out_6, out_7, out_8, out_9, out_10, out_11, out_14, out_15, out_16, out_17, out_18, out_19, out_20, out_21, out_22, out_23, out_24, out_25, out_26, out_27, out_28, out_29, out_30, out_31, out_32, out_33, out_34, out_35, out_36, out_37
  or or_16 (\флаг_смерти , \умер , \врезался_умер );
  or or_17 (or_17_out, _1_15, _2_15);
  and and_16 (and_16_out, bus_0[17], or_17_out);
  or or_18 (or_18_out, _1_16, _2_16);
  and and_17 (and_17_out, bus_0[16], or_18_out);
  Counter #(.width(1), .max('h0), .ongoal("stay")) counter_1 (.clk(d_ff_3_q));  // open: load, D, count, Q, carry, clr
  Counter #(.width(2), .max('h3), .ongoal("stay")) counter_2 (
    .clk(d_ff_3_q), .clr(or_34_out));  // open: load, D, count, Q, carry
  or or_19 (or_19_out, _1_17, _2_17);
  and and_18 (and_18_out, bus_0[15], or_19_out);
  Counter #(.width(2), .max('h2), .ongoal("stay")) counter_3 (
    .carry(counter_3_carry), .clk(d_ff_3_q), .clr(or_34_out));  // open: load, D, count, Q
  Counter #(.width(1), .max('h1), .ongoal("stay")) counter_4 (
    .carry(counter_4_carry), .clk(d_ff_3_q), .clr(or_34_out));  // open: load, D, count, Q
  Counter #(.width(32), .max('hffffffff), .trigger("falling")) counter_5 (
    .Q(counter_5_q), .clk(\робит_ли_генератор ), .clr(comparator_1_eq));  // open: load, D, count, carry
  or or_20 (or_20_out, _1_18, _2_18);
  and and_19 (and_19_out, bus_0[14], or_20_out);
  and and_20 (and_20_out, bus_0[13], or_21_out);
  Comparator #(.width(32), .mode("unsigned")) comparator_1 (
    .a(counter_5_q), .b(32'h20), .eq(comparator_1_eq));  // open: gt, lt
  or or_21 (or_21_out, _1_19, _2_19);
  or or_22 (or_22_out, _1_20, _2_20);
  and and_21 (and_21_out, bus_0[12], or_22_out);
  D_Flip_Flop d_ff_1 (
    .clk(comparator_1_eq), .D(d_ff_1_qn), .Q(d_ff_1_q), .Qn(d_ff_1_qn), .reset(vec_adr));  // open: preset, en
  or or_23 (or_23_out, _1_21, _2_21);
  and and_22 (and_22_out, bus_0[11], or_23_out);
  Comparator #(.width(5), .mode("unsigned")) comparator_2 (
    .a(counter_7_q), .b(5'b11110), .eq(\упал_умер2 ));  // open: gt, lt
  D_Flip_Flop d_ff_2 (
    .clk(d_ff_1_q), .D(d_ff_2_qn), .Q(d_ff_2_q), .Qn(d_ff_2_qn), .reset(vec_adr));  // open: preset, en
  or or_24 (or_24_out, _1_22, _2_22);
  and and_23 (and_23_out, bus_0[10], or_24_out);
  Decoder #(.select(5)) decoder_1 (
    .out0(bus_0[31]), .out1(bus_0[30]), .out2(bus_0[29]), .out3(bus_0[28]), .out4(bus_0[27]),
    .out5(bus_0[26]), .out6(bus_0[25]), .out7(bus_0[24]), .out8(bus_0[23]), .out9(bus_0[22]),
    .out10(bus_0[21]), .out11(bus_0[20]), .out12(bus_0[19]), .out13(bus_0[18]), .out14(bus_0[17]),
    .out15(bus_0[16]), .out16(bus_0[15]), .out17(bus_0[14]), .out18(bus_0[13]), .out19(bus_0[12]),
    .out20(bus_0[11]), .out21(bus_0[10]), .out22(bus_0[9]), .out23(bus_0[8]), .out24(bus_0[7]),
    .out25(bus_0[6]), .out26(bus_0[5]), .out27(bus_0[4]), .out28(bus_0[3]), .out29(bus_0[2]),
    .out30(bus_0[1]), .out31(bus_0[0]), .sel(counter_7_q));  // open: en
  D_Flip_Flop d_ff_3 (
    .clk(d_ff_2_q), .D(d_ff_3_qn), .Q(d_ff_3_q), .Qn(d_ff_3_qn), .reset(vec_adr));  // open: preset, en
  or or_25 (or_25_out, _1_23, _2_23);
  and and_24 (and_24_out, bus_0[9], or_25_out);
  D_Flip_Flop d_ff_4 (
    .clk(d_ff_3_q), .D(d_ff_4_qn), .Q(d_ff_4_q), .Qn(d_ff_4_qn), .reset(vec_adr));  // open: preset, en
  or or_26 (or_26_out, _1_24, _2_24);
  and and_25 (and_25_out, bus_0[8], or_26_out);
  Comparator #(.width(5), .mode("unsigned")) comparator_3 (
    .a(counter_7_q), .b({5{1'b1}}), .eq(\упал_умер ));  // open: gt, lt
  D_Flip_Flop d_ff_5 (
    .clk(d_ff_4_q), .D(d_ff_5_qn), .Q(d_ff_5_q), .Qn(d_ff_5_qn), .reset(vec_adr));  // open: preset, en
  or or_27 (or_27_out, _1_25, _2_25);
  and and_26 (and_26_out, bus_0[6], or_28_out);
  and and_27 (and_27_out, bus_0[7], or_27_out);
  Comparator #(.width(5), .mode("unsigned")) comparator_4 (.a(counter_7_q), .b(5'b11110), .gt(_69699));  // open: eq, lt
  nand nand_1 (_551, counter_3_carry, counter_4_carry);
  D_Flip_Flop d_ff_6 (.clk(d_ff_5_q), .D(d_ff_6_qn), .Qn(d_ff_6_qn), .reset(vec_adr));  // open: Q, preset, en
  or or_28 (or_28_out, _1_26, _2_26);
  or or_29 (or_29_out, _1_27, _2_27);
  and and_28 (and_28_out, bus_0[5], or_29_out);
  or or_30 (or_30_out, _1_28, _2_28);
  and and_29 (and_29_out, bus_0[4], or_30_out);
  Multiplexer #(.select(3)) multiplexer_1 (
    .in0(d_ff_5_q), .in1(d_ff_4_q), .in2(d_ff_3_q), .in3(d_ff_3_q), .in4(d_ff_2_q), .in5(d_ff_1_q),
    .in6(d_ff_1_q), .in7(comparator_1_eq), .out(multiplexer_1_out), .sel(counter_6_q));  // open: en
  Counter #(.width(3), .max('h7)) counter_6 (
    .Q(counter_6_q), .clk(d_ff_4_q), .clr(or_31_out));  // open: load, D, count, carry
  or or_31 (or_31_out, _69699, vec_adr, _551);
  or or_32 (or_32_out, _1_29, _2_29);
  and and_30 (and_30_out, bus_0[3], or_32_out);
  not not_2 (not_2_out, \Кнопка );
  or or_33 (or_33_out, _1_30, _2_30);
  and and_31 (and_31_out, bus_0[2], or_33_out);
  and and_32 (and_32_out, not_2_out, \Кнопка );
  or or_34 (or_34_out, and_32_out, vec_adr);
  Transistor transistor_2 (.in(multiplexer_1_out), .out(transistor_2_out), .gate(_551));
  or or_35 (or_35_out, _1_31, _2_31);
  and and_33 (and_33_out, bus_0[1], or_35_out);
  Transistor #(.\type ("n")) transistor_3 (.in(d_ff_2_q), .out(transistor_2_out), .gate(_551));
  or or_36 (or_36_out, _1_32, _2_32);
  and and_34 (and_34_out, bus_0[0], or_36_out);
  Counter #(.width(5), .max('h1f)) counter_7 (
    .load(_551), .Q(counter_7_q), .clk(transistor_2_out), .clr(or_37_out));  // open: D, count, carry
  or or_37 (or_37_out, transistor_4_out, vec_adr);
  Transistor transistor_4 (.in(not_3_out), .out(transistor_4_out), .gate(counter_8_carry));
  not not_3 (not_3_out, not_4_out);
  not not_4 (not_4_out, not_5_out);
  not not_5 (not_5_out, not_6_out);
  not not_6 (not_6_out, not_7_out);
  not not_7 (not_7_out, not_8_out);
  not not_8 (not_8_out, not_9_out);
  not not_9 (not_9_out, not_10_out);
  not not_10 (not_10_out, or_38_out);
  Counter #(.width(4), .max('h4), .ongoal("stay")) counter_8 (
    .carry(counter_8_carry), .clk(or_38_out), .clr(vec_adr));  // open: load, D, count, Q
  or or_38 (or_38_out, \упал_умер , \упал_умер2 );
  Counter #(.width(4), .max('h1), .ongoal("stay")) counter_9 (
    .carry(\умер ), .clk(counter_8_carry), .clr(vec_adr));  // open: load, D, count, Q
  // DotMatrix #(.inputtype("select"), .matrixcols(32), .matrixrows(32)) dotmatrix_1: pin names not known; wires that end beside it: 32'h40, bus_0
  DotMatrix #(.matrixcols(32), .matrixrows(32)) dotmatrix_2 (
    .col0(pipes_2_out_6), .col1(pipes_2_out_7), .col2(pipes_2_out_8), .col3(pipes_2_out_9),
    .col4(pipes_2_out_10), .col5(pipes_2_out_11), .col6(pipes_2_out_12), .col7(pipes_2_out_13),
    .col8(pipes_2_out_14), .col9(pipes_2_out_15), .col10(pipes_2_out_16), .col11(pipes_2_out_17),
    .col12(pipes_2_out_18), .col13(pipes_2_out_19), .col14(pipes_2_out_20), .col15(pipes_2_out_21),
    .col16(pipes_2_out_22), .col17(pipes_2_out_23), .col18(pipes_2_out_24), .col19(pipes_2_out_25),
    .col20(pipes_2_out_26), .col21(pipes_2_out_27), .col22(pipes_2_out_28), .col23(pipes_2_out_29),
    .col24(pipes_2_out_30), .col25(pipes_2_out_31), .col26(pipes_2_out_32), .col27(pipes_2_out_33),
    .col28(pipes_2_out_34), .col29(pipes_2_out_35), .col30(pipes_2_out_36), .col31(pipes_2_out_37));
  pipes pipes_2 (
    .out_6(pipes_2_out_6), .out_7(pipes_2_out_7), .out_8(pipes_2_out_8), .out_9(pipes_2_out_9),
    .out_10(pipes_2_out_10), .out_11(pipes_2_out_11), .out_12(pipes_2_out_12), .out_13(pipes_2_out_13),
    .out_14(pipes_2_out_14), .out_15(pipes_2_out_15), .out_16(pipes_2_out_16), .out_17(pipes_2_out_17),
    .out_18(pipes_2_out_18), .out_19(pipes_2_out_19), .out_20(pipes_2_out_20), .out_21(pipes_2_out_21),
    .out_22(pipes_2_out_22), .out_23(pipes_2_out_23), .out_24(pipes_2_out_24), .out_25(pipes_2_out_25),
    .out_26(pipes_2_out_26), .out_27(pipes_2_out_27), .out_28(pipes_2_out_28), .out_29(pipes_2_out_29),
    .out_30(pipes_2_out_30), .out_31(pipes_2_out_31), .out_32(pipes_2_out_32), .out_33(pipes_2_out_33),
    .out_34(pipes_2_out_34), .out_35(pipes_2_out_35), .out_36(pipes_2_out_36), .out_37(pipes_2_out_37),
    .in_5(vec_adr));  // open: rand_2, rand_1, tick_2, tick_1

  // Other names for the same wires on the sheet: _3_32 = bus_0[0]; _3_31 = bus_0[1]; _3_30 = bus_0[2];
  //   _3_29 = bus_0[3]; _3_28 = bus_0[4]; _3_27 = bus_0[5]; _3_26 = bus_0[6]; _3_25 = bus_0[7]; _3_24 = bus_0[8];
  //   _3_23 = bus_0[9]; _3_22 = bus_0[10]; _3_21 = bus_0[11]; _3_20 = bus_0[12]; _3_19 = bus_0[13]; _3_18 = bus_0[14];
  //   _3_17 = bus_0[15]; _3_16 = bus_0[16]; _3_15 = bus_0[17]; _3_14 = bus_0[18]; _3_13 = bus_0[19];
  //   _3_12 = bus_0[20]; _3_11 = bus_0[21]; _3_10 = bus_0[22]; _3_9 = bus_0[23]; _3_8 = bus_0[24]; _3_7 = bus_0[25];
  //   _3_6 = bus_0[26]; _3_5 = bus_0[27]; _3_4 = bus_0[28]; _3_3 = bus_0[29]; _3_2 = bus_0[30]; _3_1 = bus_0[31]
endmodule

module cdm8 (
  input  \вкл ,
  input  plus_1,
  output [7:0] \счет ,
  output [7:0] \рекорд 
);

  wire and_1_out, and_2_out, and_3_out, and_4_out, and_5_out, and_6_out, and_7_out, cdm_8_mark5_1_data_inst,
       cdm_8_mark5_1_mem_cycle, cl, code, comparator_1_eq, counter_1_carry, data, demultiplexer_2_out1,
       demultiplexer_2_out2, not_1_out, not_2_out, not_3_out, not_4_out, not_5_out, not_6_out, not_7_out,
       not_8_out, or_1_out, or_2_out, or_3_out, or_4_out, or_5_out, or_6_out, rd_wr_prime, res, t_ff_1_q,
       xor_1_out;
  wire [1:0] counter_1_q;
  wire [7:0] adr_rez, cdm_8_mark5_1_addr, cdm_8_mark5_1_data_out, cdm_8_mark5_1_pc, cdm_8_mark5_1_ps,
       cdm_8_mark5_1_r0, cdm_8_mark5_1_r1, cdm_8_mark5_1_r2, cdm_8_mark5_1_r3, cdm_8_mark5_1_sp,
       controlled_buffer_1_out, controlled_buffer_2_out, controlled_buffer_3_out, data_rez,
       demultiplexer_3_out1, demultiplexer_4_out1, rom_1_data;

  Comparator comparator_1 (.a(cdm_8_mark5_1_pc), .b(8'h17), .eq(comparator_1_eq));  // open: gt, lt
  not not_1 (not_1_out, \вкл );
  xor xor_1 (xor_1_out, comparator_1_eq, plus_1);
  // Probe on cdm_8_mark5_1_r0
  or or_1 (or_1_out, comparator_1_eq, not_1_out);
  and and_1 (and_1_out, cl, and_2_out);
  Clock clock_1 (.out(cl));
  and and_2 (and_2_out, \вкл , t_ff_1_q);
  T_Flip_Flop t_ff_1 (.clk(xor_1_out), .T(xor_1_out), .Q(t_ff_1_q));  // open: Qn, preset, reset, en
  // Probe on cdm_8_mark5_1_r2
  // Probe on cdm_8_mark5_1_r1
  // Probe on cdm_8_mark5_1_r3
  // Probe on cdm_8_mark5_1_pc
  or or_2 (or_2_out, comparator_1_eq, counter_1_carry);
  Demultiplexer demultiplexer_1 (.out0(code), .out1(data), .in(1'b1), .sel(or_3_out), .en(1'b1));
  // Probe on cdm_8_mark5_1_ps
  // Probe on cdm_8_mark5_1_sp
  CdM_8_mark5 cdm_8_mark5_1 (
    .clock(and_1_out), .addr(cdm_8_mark5_1_addr), .mem_read(rd_wr_prime),
    .mem_cycle(cdm_8_mark5_1_mem_cycle), .data_inst(cdm_8_mark5_1_data_inst),
    .data_out(cdm_8_mark5_1_data_out), .data_in(controlled_buffer_1_out), .r0(cdm_8_mark5_1_r0),
    .r1(cdm_8_mark5_1_r1), .r2(cdm_8_mark5_1_r2), .r3(cdm_8_mark5_1_r3), .PC(cdm_8_mark5_1_pc),
    .SP(cdm_8_mark5_1_sp), .PS(cdm_8_mark5_1_ps), .Clear(or_1_out));  // open: IAck, IRQ, vec
  T_Flip_Flop t_ff_2 (.clk(or_2_out), .T(or_2_out), .Q(res));  // open: Qn, preset, reset, en
  or or_3 (or_3_out, cdm_8_mark5_1_data_inst, not_2_out);
  not not_2 (not_2_out, cdm_8_mark5_1_mem_cycle);
  not not_3 (not_3_out, rd_wr_prime);
  assign controlled_buffer_1_out = rd_wr_prime ? controlled_buffer_2_out : 8'bz;  // Controlled_Buffer controlled_buffer_1
  or or_4 (or_4_out, res, counter_1_carry);
  and and_3 (and_3_out, or_4_out, cl);
  and and_4 (and_4_out, not_4_out, \вкл );
  assign controlled_buffer_2_out = not_3_out ? cdm_8_mark5_1_data_out : 8'bz;  // Controlled_Buffer controlled_buffer_2
  not not_4 (not_4_out, res);
  Counter #(.width(2), .max('h3), .trigger("falling")) counter_1 (
    .Q(counter_1_q), .carry(counter_1_carry), .clk(and_3_out));  // open: load, D, count, clr
  assign controlled_buffer_3_out = and_4_out ? cdm_8_mark5_1_addr : 8'bz;  // Controlled_Buffer controlled_buffer_3
  assign controlled_buffer_3_out = not_5_out ? 8'h3 : 8'bz;  // Controlled_Buffer controlled_buffer_4
  not not_5 (not_5_out, \вкл );
  assign controlled_buffer_3_out = res ? adr_rez : 8'bz;  // Controlled_Buffer controlled_buffer_5
  Demultiplexer #(.select(2)) demultiplexer_2 (
    .out1(demultiplexer_2_out1), .out2(demultiplexer_2_out2), .in(1'b1), .sel(counter_1_q));  // open: out0, out3, en
  and and_5 (and_5_out, \вкл , code);
  or or_5 (or_5_out, data, and_6_out, res);
  and and_6 (and_6_out, ~data, not_6_out, ~res);  // AND_Gate
  not not_6 (not_6_out, \вкл );
  ROM rom_1 (.addr(controlled_buffer_3_out), .data(rom_1_data), .sel(and_5_out));
  RAM ram_1 (
    .addr(controlled_buffer_3_out), .data(controlled_buffer_2_out), .sel(or_5_out), .clk(cl), .ld(or_6_out));  // open: clr
  or or_6 (or_6_out, and_7_out, res);
  and and_7 (and_7_out, rd_wr_prime, \вкл );
  not not_7 (not_7_out, res);
  Multiplexer #(.width(8)) multiplexer_1 (.in1(8'h3), .out(adr_rez), .sel(demultiplexer_2_out1));  // open: in0, en
  Multiplexer #(.width(8)) multiplexer_2 (.in1(8'h2), .out(adr_rez), .sel(demultiplexer_2_out2));  // open: in0, en
  assign controlled_buffer_2_out = not_7_out ? rom_1_data : 8'bz;  // Controlled_Buffer controlled_buffer_6
  assign data_rez = res ? controlled_buffer_2_out : 8'bz;  // Controlled_Buffer controlled_buffer_7
  assign controlled_buffer_2_out = not_8_out ? {8{1'b0}} : 8'bz;  // Controlled_Buffer controlled_buffer_8
  not not_8 (not_8_out, \вкл );
  Demultiplexer #(.width(8)) demultiplexer_3 (
    .out1(demultiplexer_3_out1), .in(data_rez), .sel(demultiplexer_2_out1));  // open: out0, en
  Demultiplexer #(.width(8)) demultiplexer_4 (
    .out1(demultiplexer_4_out1), .in(data_rez), .sel(demultiplexer_2_out2));  // open: out0, en
  Register #(.trigger("high")) register_1 (
    .D(demultiplexer_3_out1), .Q(\счет ), .clk(demultiplexer_2_out1));  // open: en, clr
  Register #(.trigger("high")) register_2 (
    .D(demultiplexer_4_out1), .Q(\рекорд ), .clk(demultiplexer_2_out2));  // open: en, clr

  // Other names for the same wires on the sheet: _0 = \вкл 

  // Notes on the sheet:
  //   contents of rom_1 (hex, n*v repeats v):
  //   d0 3 b1 d2 4 d3 1 ab 1d d0 0 b1 d0 3 a1 d2 2 bb 7d ea 16 a9 d4
  //   попробавать и зправить и убрать все до регистров жи есс
endmodule

module taktDel_11_1 (
  output out_1
);

  wire clock_1_out, d_ff_1_q, d_ff_2_q, d_ff_3_q, d_ff_4_q, d_ff_5_q, d_ff_6_q, d_ff_7_q, d_ff_8_q, d_ff_9_q,
       d_ff_10_q, d_ff_11_qn;

  Clock clock_1 (.out(clock_1_out));
  D_Flip_Flop d_ff_1 (.clk(clock_1_out), .D(d_ff_11_qn), .Q(d_ff_1_q));  // open: Qn, preset, en, reset
  D_Flip_Flop d_ff_2 (.clk(clock_1_out), .D(d_ff_1_q), .Q(d_ff_2_q));  // open: Qn, preset, en, reset
  D_Flip_Flop d_ff_3 (.clk(clock_1_out), .D(d_ff_2_q), .Q(d_ff_3_q));  // open: Qn, preset, en, reset
  D_Flip_Flop d_ff_4 (.clk(clock_1_out), .D(d_ff_3_q), .Q(d_ff_4_q));  // open: Qn, preset, en, reset
  D_Flip_Flop d_ff_5 (.clk(clock_1_out), .D(d_ff_4_q), .Q(d_ff_5_q));  // open: Qn, preset, en, reset
  D_Flip_Flop d_ff_6 (.clk(clock_1_out), .D(d_ff_5_q), .Q(d_ff_6_q));  // open: Qn, preset, en, reset
  D_Flip_Flop d_ff_7 (.clk(clock_1_out), .D(d_ff_6_q), .Q(d_ff_7_q));  // open: Qn, preset, en, reset
  D_Flip_Flop d_ff_8 (.clk(clock_1_out), .D(d_ff_7_q), .Q(d_ff_8_q));  // open: Qn, preset, en, reset
  D_Flip_Flop d_ff_9 (.clk(clock_1_out), .D(d_ff_8_q), .Q(d_ff_9_q));  // open: Qn, preset, en, reset
  D_Flip_Flop d_ff_10 (.clk(clock_1_out), .D(d_ff_9_q), .Q(d_ff_10_q));  // open: Qn, preset, en, reset
  D_Flip_Flop d_ff_11 (.clk(clock_1_out), .D(d_ff_10_q), .Q(out_1), .Qn(d_ff_11_qn));  // open: preset, en, reset
endmodule

module \из_16ричной_в_10  (
  input  [7:0] in_1,
  output [3:0] out_2,
  output [3:0] out_3,
  output [3:0] out_4
);

  wire \пр7_1_u , \пр7_1_v , \пр7_1_w , \пр7_1_x , \пр7_1_y , \пр7_1_z , \пр7_2_y ;

  // Probe on in_1
  \ПР7  \u_пр7_1  (
    .a(in_1[7]), .b(in_1[6]), .c(in_1[5]), .d(in_1[4]), .e(in_1[3]), .x(\пр7_1_x ), .y(\пр7_1_y ),
    .z(\пр7_1_z ), .u(\пр7_1_u ), .v(\пр7_1_v ), .w(\пр7_1_w ));
  // Probe on in_1
  \ПР7  \u_пр7_2  (
    .a(\пр7_1_u ), .b(\пр7_1_v ), .c(\пр7_1_w ), .d(in_1[2]), .e(in_1[1]), .y(\пр7_2_y ), .z(out_3[0]),
    .u(out_4[3]), .v(out_4[2]), .w(out_4[1]));  // open: x
  \ПР7  \u_пр7_3  (
    .a(1'b0), .b(\пр7_1_x ), .c(\пр7_1_y ), .d(\пр7_1_z ), .e(\пр7_2_y ), .y(out_2[1]), .z(out_2[0]),
    .u(out_3[3]), .v(out_3[2]), .w(out_3[1]));  // open: x
  DotMatrix #(.inputtype("row"), .matrixcols(1), .matrixrows(10)) dotmatrix_1 (
    .row0(in_1[0]), .row1(out_4[1]), .row2(out_4[2]), .row3(out_4[3]), .row4(out_3[0]), .row5(out_3[1]),
    .row6(out_3[2]), .row7(out_3[3]), .row8(out_2[0]), .row9(out_2[1]));

  assign out_2[3:2] = 2'b00;
  assign out_4[0] = in_1[0];

  // Notes on the sheet:
  //   HEX(16)
  //   DEC(10)
endmodule

module \вспомогательная_схема  (
  input  a,
  input  b,
  input  c,
  input  d,
  input  e,
  output x,
  output y,
  output z,
  output u,
  output v,
  output w
);

  wire and_1_out, and_2_out, and_3_out, and_4_out, and_5_out, and_6_out, and_7_out, and_8_out, and_9_out,
       and_10_out, and_11_out, and_12_out, and_13_out, and_14_out, and_15_out, and_16_out, and_17_out,
       and_18_out, and_19_out, and_20_out, and_21_out, and_22_out, and_23_out, and_24_out, and_25_out,
       and_26_out, and_27_out, and_28_out, and_29_out, and_30_out, and_31_out, and_32_out, and_33_out,
       and_34_out, and_35_out, and_36_out, and_37_out, and_38_out, not_1_out, not_2_out, not_3_out,
       not_4_out, not_5_out, not_6_out, not_7_out, not_8_out, not_9_out, not_10_out, not_11_out, not_12_out,
       not_13_out, not_14_out, not_15_out, not_16_out, not_17_out, not_18_out, not_19_out, not_20_out,
       not_21_out, not_22_out, not_23_out, not_24_out, not_25_out, not_26_out, not_27_out, not_28_out,
       not_29_out, not_30_out, not_31_out, not_32_out, not_33_out, not_34_out, not_35_out, not_36_out,
       not_37_out, not_38_out, not_39_out, not_40_out, not_41_out, not_42_out, not_43_out, not_44_out,
       not_45_out, not_46_out, not_47_out, not_48_out, not_49_out, not_50_out, not_51_out, not_52_out,
       not_53_out, not_54_out, not_55_out, not_56_out, not_57_out, not_58_out, not_59_out, not_60_out,
       not_61_out, not_62_out, not_63_out, not_64_out, not_65_out, not_66_out, not_67_out, not_68_out,
       not_69_out, not_70_out, not_71_out;

  and and_1 (and_1_out, a, c);
  and and_2 (and_2_out, a, b);
  not not_1 (not_1_out, a);
  not not_2 (not_2_out, a);
  not not_3 (not_3_out, b);
  not not_4 (not_4_out, c);
  not not_5 (not_5_out, a);
  not not_6 (not_6_out, b);
  not not_7 (not_7_out, a);
  not not_8 (not_8_out, b);
  not not_9 (not_9_out, a);
  not not_10 (not_10_out, a);
  not not_11 (not_11_out, c);
  not not_12 (not_12_out, d);
  not not_13 (not_13_out, b);
  not not_14 (not_14_out, c);
  not not_15 (not_15_out, c);
  not not_16 (not_16_out, c);
  not not_17 (not_17_out, d);
  not not_18 (not_18_out, a);
  not not_19 (not_19_out, b);
  not not_20 (not_20_out, d);
  not not_21 (not_21_out, e);
  not not_22 (not_22_out, a);
  not not_23 (not_23_out, c);
  not not_24 (not_24_out, d);
  not not_25 (not_25_out, a);
  not not_26 (not_26_out, e);
  not not_27 (not_27_out, b);
  not not_28 (not_28_out, c);
  not not_29 (not_29_out, c);
  not not_30 (not_30_out, d);
  not not_31 (not_31_out, e);
  not not_32 (not_32_out, d);
  not not_33 (not_33_out, b);
  not not_34 (not_34_out, c);
  not not_35 (not_35_out, e);
  not not_36 (not_36_out, a);
  not not_37 (not_37_out, b);
  not not_38 (not_38_out, a);
  not not_39 (not_39_out, d);
  not not_40 (not_40_out, e);
  not not_41 (not_41_out, a);
  not not_42 (not_42_out, d);
  not not_43 (not_43_out, d);
  not not_44 (not_44_out, e);
  not not_45 (not_45_out, b);
  not not_46 (not_46_out, c);
  not not_47 (not_47_out, d);
  not not_48 (not_48_out, b);
  not not_49 (not_49_out, c);
  not not_50 (not_50_out, a);
  not not_51 (not_51_out, b);
  not not_52 (not_52_out, c);
  not not_53 (not_53_out, a);
  not not_54 (not_54_out, c);
  not not_55 (not_55_out, a);
  not not_56 (not_56_out, b);
  not not_57 (not_57_out, e);
  not not_58 (not_58_out, a);
  not not_59 (not_59_out, c);
  not not_60 (not_60_out, d);
  not not_61 (not_61_out, e);
  not not_62 (not_62_out, a);
  not not_63 (not_63_out, d);
  not not_64 (not_64_out, b);
  not not_65 (not_65_out, c);
  not not_66 (not_66_out, e);
  not not_67 (not_67_out, c);
  not not_68 (not_68_out, e);
  not not_69 (not_69_out, b);
  not not_70 (not_70_out, d);
  not not_71 (not_71_out, e);
  or or_1 (x, and_1_out, and_2_out);
  and and_3 (and_3_out, not_1_out, b, d);
  and and_4 (and_4_out, not_2_out, b, c);
  and and_5 (and_5_out, b, c, d);
  and and_6 (and_6_out, a, not_3_out, not_4_out);
  and and_7 (and_7_out, not_5_out, not_6_out, c, e);
  and and_8 (and_8_out, not_7_out, not_8_out, c, d);
  and and_9 (and_9_out, not_9_out, c, d, e);
  and and_10 (and_10_out, not_10_out, b, not_11_out, not_12_out);
  and and_11 (and_11_out, a, not_13_out, not_14_out);
  and and_12 (and_12_out, a, not_15_out, e);
  and and_13 (and_13_out, a, not_16_out, d);
  and and_14 (and_14_out, a, b, c, not_17_out);
  and and_15 (and_15_out, not_18_out, not_19_out, c, not_20_out, not_21_out);
  and and_16 (and_16_out, not_22_out, b, not_23_out, not_24_out, e);
  and and_17 (and_17_out, not_25_out, b, c, d, not_26_out);
  and and_18 (and_18_out, a, not_27_out, not_28_out, d, e);
  and and_19 (and_19_out, a, b, not_29_out, not_30_out, not_31_out);
  and and_20 (and_20_out, a, b, c, not_32_out, e);
  and and_21 (and_21_out, not_33_out, not_34_out, d, not_35_out);
  and and_22 (and_22_out, not_36_out, not_37_out, d, e);
  and and_23 (and_23_out, not_38_out, b, not_39_out, not_40_out);
  and and_24 (and_24_out, not_41_out, b, c, not_42_out);
  and and_25 (and_25_out, b, c, not_43_out, not_44_out);
  and and_26 (and_26_out, a, not_45_out, not_46_out, not_47_out, e);
  and and_27 (and_27_out, a, not_48_out, c, d);
  and and_28 (and_28_out, a, b, not_49_out, d, e);
  and and_29 (and_29_out, not_50_out, not_51_out, not_52_out, e);
  and and_30 (and_30_out, not_53_out, not_54_out, d, e);
  and and_31 (and_31_out, not_55_out, not_56_out, c, d, not_57_out);
  and and_32 (and_32_out, not_58_out, b, not_59_out, not_60_out, not_61_out);
  and and_33 (and_33_out, not_62_out, b, c, not_63_out, e);
  and and_34 (and_34_out, a, not_64_out, not_65_out, not_66_out);
  and and_35 (and_35_out, a, not_67_out, d, not_68_out);
  and and_36 (and_36_out, a, not_69_out, c, e);
  and and_37 (and_37_out, a, c, d, e);
  and and_38 (and_38_out, a, b, c, not_70_out, not_71_out);
  or or_2 (y, and_3_out, and_4_out, and_5_out, and_6_out);
  or or_3 (z, and_7_out, and_8_out, and_9_out, and_10_out, and_11_out, and_12_out, and_13_out, and_14_out);
  or or_4 (u, and_15_out, and_16_out, and_17_out, and_18_out, and_19_out, and_20_out);
  or or_5 (v, and_21_out, and_22_out, and_23_out, and_24_out, and_25_out, and_26_out, and_27_out, and_28_out);
  or or_6 (w, and_29_out, and_30_out, and_31_out, and_32_out, and_33_out, and_34_out, and_35_out, and_36_out, and_37_out, and_38_out);
endmodule
